// Digital circuit adder.dig as structural Verilog
module adder (
  input  A,
  input  B,
  input  C_i_1,
  output C_i,
  output S
);

  wire and_1_out, and_2_out, xor_1_out;

  and and_1 (and_1_out, A, B);
  xor xor_1 (xor_1_out, A, B);
  and and_2 (and_2_out, xor_1_out, C_i_1);
  xor xor_2 (S, xor_1_out, C_i_1);
  or or_1 (C_i, and_1_out, and_2_out);

  // Notes on the sheet:
  //   A: first bit to add
  //   {{de Erstes zu addierendes Bit.}}
  //   B: second bit to add
  //   {{de Zweites zu addierendes Bit.}}
  //   C_i_1: carry in
  //   {{de Übertragsbit der Vorgängerschaltung.}}
  //   C_i: carry bit
  //   {{de Übertragsbit}}
  //   S: sum {{de Summe}}
endmodule
