// Digital circuit sample1.dig as structural Verilog
module sample1 (
  input  [1:0] A1,
  input  [1:0] A2,
  input  [1:0] A3,
  input  [1:0] A4,
  input  [1:0] A5,
  output [1:0] Y1,
  output [1:0] Y2
);

  assign Y1 = A1 & ~A3 & A2;  // And and_1, 2 bits wide
  // Probe on A3
  assign Y2 = A4 & ~2'b00 & A5;  // And and_2, 2 bits wide
  // Probe on 2'b00

  // Other names for the same wires on the sheet: a1_t[1:0] = A4
endmodule
