// Digital circuit sample11.dig as structural Verilog
module sample11 (
  input  [1:0] A3,
  input  [3:0] A12,
  input  [3:0] A34,
  output [3:0] Y
);

  sample1 sample1_1 (.A1(A12[1:0]), .A2(A34[1:0]), .A3(A3), .A4(A12[3:2]), .A5(A34[3:2]), .Y1(Y[1:0]), .Y2(Y[3:2]));
endmodule
