// Digital circuit Hamming.dig as structural Verilog
module Hamming (
  input  [5:0] A,
  input  [9:0] Y,
  output [9:0] Y_2,
  output [3:0] Error
);

  wire xor_3_out, xor_6_out, xor_7_out, xor_8_out, xor_10_out, xor_12_out, xor_13_out, xor_14_out,
       xor_16_out, xor_18_out, xor_19_out, xor_20_out, xor_21_out, xor_22_out;

  xor xor_1 (Y_2[7], A[4], A[5]);
  xor xor_2 (Error[3], xor_6_out, Y[9]);
  xor xor_3 (xor_3_out, A[1], A[2]);
  xor xor_4 (Y_2[3], xor_3_out, A[3]);
  xor xor_5 (Error[1], xor_10_out, Y[9]);
  xor xor_6 (xor_6_out, Y[8], Y[7]);
  xor xor_7 (xor_7_out, A[3], A[5]);
  xor xor_8 (xor_8_out, A[0], A[2]);
  xor xor_9 (Y_2[1], xor_8_out, xor_7_out);
  xor xor_10 (xor_10_out, xor_13_out, xor_12_out);
  xor xor_11 (Error[0], xor_14_out, Y[8]);
  xor xor_12 (xor_12_out, Y[5], Y[6]);
  xor xor_13 (xor_13_out, Y[1], Y[2]);
  xor xor_14 (xor_14_out, xor_19_out, xor_18_out);
  xor xor_15 (Error[2], xor_22_out, xor_21_out);
  xor xor_16 (xor_16_out, A[3], A[4]);
  xor xor_17 (Y_2[0], xor_20_out, xor_16_out);
  xor xor_18 (xor_18_out, Y[4], Y[6]);
  xor xor_19 (xor_19_out, Y[0], Y[2]);
  xor xor_20 (xor_20_out, A[0], A[1]);
  xor xor_21 (xor_21_out, Y[6], Y[5]);
  xor xor_22 (xor_22_out, Y[4], Y[3]);

  assign {Y_2[9:8], Y_2[6:4], Y_2[2]} = A;

  // Other names for the same wires on the sheet: B3 = A[0]; B5 = A[1]; B6 = A[2]; B7 = A[3]; B9 = A[4]; B10 = A[5];
  //   B1 = Y_2[0]; P1 = Y_2[0]; B2 = Y_2[1]; P2 = Y_2[1]; B4 = Y_2[3]; P4 = Y_2[3]; B8 = Y_2[7]; P8 = Y_2[7];
  //   B_1 = Y[0]; B_2 = Y[1]; B_3 = Y[2]; B_4 = Y[3]; B_5 = Y[4]; B_6 = Y[5]; B_7 = Y[6]; B_8 = Y[7]; B_9 = Y[8];
  //   B_10 = Y[9]

  // Notes on the sheet:
  //   A: default 45
endmodule

/* Test case:
Y'     Error
0x2E4   0
0x2E5   0x01
0x2E6   0x02
0x2E0   0x03
0x2EC   0x04
0x2F4   0x05
0x2C4   0x06
0x2A4   0x07
0x264   0x08
0x3E4   0x09
0x0E4    0x0A
*/
