// Digital circuit XOR.dig as structural Verilog
module XOR (
  input  A,
  input  B,
  output Y1,
  output Y2,
  output Y3,
  output Y0,
  output Y4
);

  wire and_1_out, and_2_out, nand_1_out, nand_2_out, nand_3_out, nand_4_out, not_1_out, not_2_out, or_1_out;

  or or_1 (or_1_out, A, B);
  nand nand_1 (nand_1_out, A, B);
  and and_1 (and_1_out, not_1_out, B);
  not not_1 (not_1_out, A);
  and and_2 (and_2_out, A, not_2_out);
  not not_2 (not_2_out, B);
  nand nand_2 (nand_2_out, A, B);
  xor xor_1 (Y0, A, B);
  nand nand_3 (nand_3_out, A, nand_2_out);
  nand nand_4 (nand_4_out, nand_2_out, B);
  and and_3 (Y1, or_1_out, nand_1_out);
  or or_2 (Y2, and_1_out, and_2_out);
  nand nand_5 (Y3, nand_3_out, nand_4_out);
  LookUpTable lookuptable_1 (.in0(A), .in1(B), .out(Y4));

  // Notes on the sheet:
  //   contents of lookuptable_1 (hex, n*v repeats v):
  //   0,1,1
endmodule

/* Test case:
A B Y0 Y1 Y2 Y3
0 0 0  0  0  0
0 1 1  1  1  1
1 0 1  1  1  1
1 1 0  0  0  01
*/
