// Digital circuit and & nand sample.dig as structural Verilog
module and___nand_sample (
  input  in_1,
  input  in_3,
  input  in_4,
  input  in_5,
  input  in_7,
  input  in_9,
  input  in_10,
  input  in_11,
  input  A,
  input  B,
  input  A_2,
  input  B_2,
  output out_2,
  output out_6,
  output out_8,
  output out_12,
  output Y,
  output Y_2
);

  wire nfet_1_s, nfet_4_s, pullup_1_out, T1_d, T3_s, T7_s;

  and and_1 (Y, A, B);
  PFET T1 (.G(in_1), .S(1'b1), .D(T1_d));
  NFET T3 (.G(in_1), .D(T1_d), .S(T3_s));
  NFET T4 (.G(in_3), .D(T3_s), .S(1'b0));
  PullUp pullup_1 (.out(pullup_1_out));
  NFET nfet_1 (.G(in_5), .D(pullup_1_out), .S(nfet_1_s));
  NFET nfet_2 (.G(in_4), .D(nfet_1_s), .S(1'b0));
  PFET T2 (.G(in_3), .S(1'b1), .D(T1_d));
  PullUp pullup_2 (.out(out_6));
  NFET nfet_3 (.G(pullup_1_out), .D(out_6), .S(1'b0));
  PFET T5 (.G(T1_d), .S(1'b1), .D(out_2));
  NFET T6 (.G(T1_d), .D(out_2), .S(1'b0));
  nand nand_1 (Y_2, A_2, B_2);
  NFET nfet_4 (.G(in_11), .D(out_12), .S(nfet_4_s));
  NFET nfet_5 (.G(in_10), .D(nfet_4_s), .S(1'b0));
  PFET T6_2 (.G(in_7), .S(1'b1), .D(out_8));
  NFET T7 (.G(in_7), .D(out_8), .S(T7_s));
  NFET T8 (.G(in_9), .D(T7_s), .S(1'b0));
  PullUp pullup_3 (.out(out_12));
  PFET T7_2 (.G(in_9), .S(1'b1), .D(out_8));
endmodule
