// Digital circuit bus arbiter.dig as structural Verilog
module bus_arbiter (
  input  [3:0] A,
  input  [3:0] B,
  input  [3:0] C,
  output Y_3,
  output Y_0,
  output Y_2,
  output Y_1
);

  wire and_1_out, and_2_out, and_3_out, and_4_out, and_5_out, and_6_out, and_7_out, and_8_out, and_9_out,
       and_10_out, and_11_out, and_12_out, and_13_out, and_14_out, and_15_out, and_16_out, and_17_out,
       and_18_out, and_19_out, and_20_out, and_21_out, or_1_out, or_2_out, or_3_out, or_4_out, or_5_out,
       or_6_out, or_7_out, or_8_out, or_9_out, T1_d, T2_d, T3_4_d, T3_d;

  and and_1 (and_1_out, 1'b1, C[3]);
  not not_1 (Y_3, T1_d);
  and and_2 (and_2_out, 1'b1, A[3]);
  and and_3 (and_3_out, 1'b1, B[3]);
  NFET T1 (.G(and_1_out), .D(T1_d), .S(1'b0));
  or or_1 (or_1_out, T1_d, C[3]);
  and and_4 (and_4_out, or_1_out, 1'b1);
  PullUp pullup_1 (.out(T1_d));
  NFET T1_2 (.G(and_2_out), .D(T1_d), .S(1'b0));
  or or_2 (or_2_out, T1_d, A[3]);
  and and_5 (and_5_out, or_2_out, 1'b1);
  NFET T1_3 (.G(and_3_out), .D(T1_d), .S(1'b0));
  or or_3 (or_3_out, T1_d, B[3]);
  and and_6 (and_6_out, or_3_out, 1'b1);
  and and_7 (and_7_out, and_4_out, C[2]);
  not not_2 (Y_2, T2_d);
  and and_8 (and_8_out, and_5_out, A[2]);
  and and_9 (and_9_out, and_6_out, B[2]);
  NFET T2 (.G(and_7_out), .D(T2_d), .S(1'b0));
  or or_4 (or_4_out, T2_d, C[2]);
  and and_10 (and_10_out, or_4_out, and_4_out);
  PullUp pullup_2 (.out(T2_d));
  NFET T2_2 (.G(and_8_out), .D(T2_d), .S(1'b0));
  or or_5 (or_5_out, T2_d, A[2]);
  and and_11 (and_11_out, or_5_out, and_5_out);
  NFET T2_3 (.G(and_9_out), .D(T2_d), .S(1'b0));
  or or_6 (or_6_out, T2_d, B[2]);
  and and_12 (and_12_out, or_6_out, and_6_out);
  and and_13 (and_13_out, and_10_out, C[1]);
  not not_3 (Y_1, T3_d);
  and and_14 (and_14_out, and_11_out, A[1]);
  and and_15 (and_15_out, and_12_out, B[1]);
  NFET T3 (.G(and_13_out), .D(T3_d), .S(1'b0));
  or or_7 (or_7_out, T3_d, C[1]);
  and and_16 (and_16_out, or_7_out, and_10_out);
  PullUp pullup_3 (.out(T3_d));
  PullUp pullup_4 (.out(T3_d));
  NFET T3_2 (.G(and_14_out), .D(T3_d), .S(1'b0));
  or or_8 (or_8_out, T3_d, A[1]);
  and and_17 (and_17_out, or_8_out, and_11_out);
  NFET T3_3 (.G(and_15_out), .D(T3_d), .S(1'b0));
  or or_9 (or_9_out, T3_d, B[1]);
  and and_18 (and_18_out, or_9_out, and_12_out);
  and and_19 (and_19_out, and_16_out, C[0]);
  not not_4 (Y_0, T3_4_d);
  and and_20 (and_20_out, and_17_out, A[0]);
  and and_21 (and_21_out, and_18_out, B[0]);
  NFET T3_4 (.G(and_19_out), .D(T3_4_d), .S(1'b0));
  PullUp pullup_5 (.out(T3_4_d));
  NFET T3_5 (.G(and_20_out), .D(T3_4_d), .S(1'b0));
  NFET T3_6 (.G(and_21_out), .D(T3_4_d), .S(1'b0));
endmodule
