// Digital circuit logic gate.dig as structural Verilog
module logic_gate (
  input  [7:0] A1,
  input  [7:0] B1,
  input  A2,
  input  B2,
  input  A3,
  input  B3,
  input  C2,
  input  A4,
  input  B4,
  input  A5,
  input  A6,
  input  B6,
  input  A7,
  input  B7,
  input  A8,
  input  B8,
  output [7:0] Y1,
  output Y2,
  output Y3,
  output Y4,
  output Y5,
  output Y6,
  output Y7,
  output Y8
);

  assign Y1 = A1 & B1;  // And and_1, 8 bits wide
  or or_1 (Y3, A3, B3);
  not not_1 (Y5, A5);
  assign Y7 = A7 ? B7 : 1'bz;  // Driver driver_1
  nand nand_1 (Y2, A2, B2, C2);
  nor nor_1 (Y4, A4, B4);
  xor xor_1 (Y6, A6, B6);
  assign Y8 = ~A8 ? B8 : 1'bz;  // DriverInvSel driverinvsel_1
endmodule
