// Digital circuit mos.dig as structural Verilog
module mos (
  input  in_1,
  input  in_4,
  output out_2,
  output out_3,
  output out_5,
  output out_6
);

  PullUp pullup_1 (.out(out_2));
  PFET pfet_1 (.G(in_1), .S(out_2), .D(1'b0));
  PullUp pullup_2 (.out(out_3));
  NFET nfet_1 (.G(in_1), .D(out_3), .S(1'b0));
  PullUp pullup_3 (.out(out_5));
  FGPFET #(.Blown("true")) fgpfet_1 (.G(in_4), .S(out_5), .D(1'b0));
  PullUp pullup_4 (.out(out_6));
  FGNFET fgnfet_1 (.G(in_4), .D(out_6), .S(1'b0));
endmodule
