// Digital circuit not & driver sample.dig as structural Verilog
module not___driver_sample (
  input  in_1,
  input  A,
  input  A_2,
  input  EN,
  input  in_9,
  input  A_3,
  input  EN_2,
  output out_2,
  output Y,
  output out_5,
  output Y_2,
  output Y_3
);

  wire T1_2_d, T3_d, T5_d;

  not not_1 (out_5, in_9);
  PFET T1 (.G(A), .S(1'b1), .D(Y));
  NFET T2 (.G(A), .D(Y), .S(1'b0));
  PullUp pullup_1 (.out(out_2));
  NFET nfet_1 (.G(in_1), .D(out_2), .S(1'b0));
  PFET T1_2 (.G(EN), .S(1'b1), .D(T1_2_d));
  NFET T2_2 (.G(EN), .D(T1_2_d), .S(1'b0));
  assign Y_3 = EN_2 ? A_3 : 1'bz;  // Driver driver_1
  PFET T3 (.G(T1_2_d), .S(1'b1), .D(T3_d));
  NFET T6 (.G(A_2), .D(T3_d), .S(Y_2));
  PFET T5 (.G(A_2), .S(Y_2), .D(T5_d));
  NFET T4 (.G(EN), .D(T5_d), .S(1'b0));
endmodule
