// Digital circuit open drain bus.dig as structural Verilog
module open_drain_bus (
  input  C,
  input  B,
  input  A,
  input  C_2,
  input  B_2,
  input  A_2,
  output Y,
  output Y_2
);

  NFET T1 (.G(A), .D(Y), .S(1'b0));
  PFET pfet_1 (.G(A_2), .S(Y_2), .D(1'b0));
  PullUp pullup_1 (.out(Y));
  NFET T2 (.G(B), .D(Y), .S(1'b0));
  PullUp pullup_2 (.out(Y_2));
  PFET pfet_2 (.G(B_2), .S(Y_2), .D(1'b0));
  NFET T3 (.G(C), .D(Y), .S(1'b0));
  PFET pfet_3 (.G(C_2), .S(Y_2), .D(1'b0));

  // Notes on the sheet:
  //   $R$ {{de $R$}}
endmodule
