// Digital circuit or & xor sample.dig as structural Verilog
module or___xor_sample (
  input  in_1,
  input  in_2,
  input  A,
  input  B,
  input  in_8,
  input  in_9,
  input  A_2,
  input  B_2,
  input  in_15,
  input  in_16,
  input  in_17,
  input  in_18,
  output out_3,
  output Y,
  output out_7,
  output out_10,
  output Y_2,
  output out_14
);

  wire nfet_5_d, pfet_1_d, pullup_1_out, T1_d, T2_d;

  PullUp pullup_1 (.out(pullup_1_out));
  NFET nfet_1 (.G(in_2), .D(pullup_1_out), .S(1'b0));
  NFET nfet_2 (.G(in_1), .D(pullup_1_out), .S(1'b0));
  or or_1 (out_7, in_16, in_15);
  PFET T1 (.G(A), .S(1'b1), .D(T1_d));
  PFET T2 (.G(B), .S(T1_d), .D(T2_d));
  NFET T3 (.G(A), .D(T2_d), .S(1'b0));
  NFET T4 (.G(B), .D(T2_d), .S(1'b0));
  PullUp pullup_2 (.out(out_3));
  NFET nfet_3 (.G(pullup_1_out), .D(out_3), .S(1'b0));
  PFET T5 (.G(T2_d), .S(1'b1), .D(Y));
  NFET T6 (.G(T2_d), .D(Y), .S(1'b0));
  xor xor_1 (out_14, in_18, in_17);
  PFET pfet_1 (.G(A_2), .S(1'b1), .D(pfet_1_d));
  NFET nfet_4 (.G(A_2), .D(pfet_1_d), .S(1'b0));
  NFET #(.unidirectional("true")) nfet_5 (.G(in_8), .D(nfet_5_d), .S(in_9));
  NFET #(.unidirectional("true")) nfet_6 (.G(in_9), .D(nfet_5_d), .S(in_8));
  PullUp pullup_3 (.out(nfet_5_d));
  PullUp pullup_4 (.out(out_10));
  NFET nfet_7 (.G(nfet_5_d), .D(out_10), .S(1'b0));
  PFET #(.unidirectional("true")) pfet_2 (.G(B_2), .S(A_2), .D(Y_2));
  NFET #(.unidirectional("true")) nfet_8 (.G(B_2), .D(Y_2), .S(pfet_1_d));
endmodule
