// Digital circuit wire and.dig as structural Verilog
module wire_and (
  input  [3:0] A,
  input  [3:0] B,
  input  [3:0] C,
  output Y_3,
  output Y_0,
  output Y_2,
  output Y_1
);

  wire pullup_1_out, pullup_2_out, pullup_3_out, T3_4_d;

  not not_1 (Y_3, pullup_1_out);
  PullUp pullup_1 (.out(pullup_1_out));
  NFET T1 (.G(A[3]), .D(pullup_1_out), .S(1'b0));
  NFET T1_2 (.G(B[3]), .D(pullup_1_out), .S(1'b0));
  NFET T1_3 (.G(C[3]), .D(pullup_1_out), .S(1'b0));
  not not_2 (Y_2, pullup_2_out);
  PullUp pullup_2 (.out(pullup_2_out));
  NFET T2 (.G(A[2]), .D(pullup_2_out), .S(1'b0));
  NFET T2_2 (.G(B[2]), .D(pullup_2_out), .S(1'b0));
  NFET T2_3 (.G(C[2]), .D(pullup_2_out), .S(1'b0));
  not not_3 (Y_1, pullup_3_out);
  PullUp pullup_3 (.out(pullup_3_out));
  PullUp pullup_4 (.out(pullup_3_out));
  NFET T3 (.G(A[1]), .D(pullup_3_out), .S(1'b0));
  NFET T3_2 (.G(B[1]), .D(pullup_3_out), .S(1'b0));
  NFET T3_3 (.G(C[1]), .D(pullup_3_out), .S(1'b0));
  not not_4 (Y_0, T3_4_d);
  NFET T3_4 (.G(A[0]), .D(T3_4_d), .S(1'b0));
  NFET T3_5 (.G(B[0]), .D(T3_4_d), .S(1'b0));
  NFET T3_6 (.G(C[0]), .D(T3_4_d), .S(1'b0));
  PullUp pullup_5 (.out(T3_4_d));
endmodule
