// Digital circuit Comp.dig as structural Verilog
// Simple comparator, which compares two bits.
// {{de Einfacher Vergleicher, welcher zwei Bits 
// miteinander vergleicht.}}
module Comp (
  input  A,
  input  B,
  input  EN,
  input  P,
  input  Q,
  output A_lt_B,
  output A_eq_B,
  output A_gt_B,
  output P_lt_Q,
  output P_eq_Q,
  output P_gt_Q,
  output a_gt_b_2,
  output a_eq_b_2,
  output a_lt_b_2
);

  wire and_1_out, and_2_out, comparator_2_eq, not_1_out, not_2_out;

  and and_1 (and_1_out, P, EN);
  and and_2 (and_2_out, EN, Q);
  not not_1 (not_1_out, A);
  not not_2 (not_2_out, B);
  Comparator comparator_1 (.a(A), .b(B), .gt(a_gt_b_2), .eq(a_eq_b_2), .lt(a_lt_b_2));
  Comparator comparator_2 (.a(and_1_out), .b(and_2_out), .gt(P_gt_Q), .eq(comparator_2_eq), .lt(P_lt_Q));
  and and_3 (A_lt_B, not_1_out, B);
  and and_4 (A_gt_B, A, not_2_out);
  nor nor_1 (A_eq_B, A_lt_B, A_gt_B);
  and and_5 (P_eq_Q, comparator_2_eq, EN);

  // Notes on the sheet:
  //   A: First bit to compare.
  //   {{de Erstes zu vergleichendes Bit.}}
  //   B: Second bit to compare.
  //   {{de Zweites zu vergleichendes Bit.}}
  //   A_lt_B: This output is one if A<B is true.
  //   {{de Das Bit ist Eins, wenn A<B gilt.}}
  //   A_eq_B: This output is one if A=B is true.
  //   {{de Das Bit ist Eins, wenn A=B gilt.}}
  //   A_gt_B: This output is one if A>B is true.
  //   {{de Das Bit ist Eins, wenn A>B gilt.}}
  //   P_lt_Q: Is set to one if P<Q is valid.
  //   {{de Das Bit ist Eins, wenn P<Q gilt.}}
  //   P_eq_Q: Is set to one if P=Q is valid.
  //   {{de Das Bit ist Eins, wenn P=Q gilt.}}
  //   P_gt_Q: Is set to one if P>Q is valid.
  //   {{de Das Bit ist Eins, wenn P>Q gilt.}}
  //   EN: Enable input. If this input goes to zero, all three output 
  //   bits are also zero. If this input is one, the comparator 
  //   has its normal function.
  //   {{de Enable Eingang. Geht dieser Eingang auf Null, sind 
  //   alle drei Ausgangsbit auch Null. Ist dieser Eingang 
  //   auf Eins, hat der Komparator seine normale 
  //   Funktion.}}
  //   P: First bit to compare.
  //   {{de Erstes zu vergleichendes Bit.}}
  //   Q: Second bit to compare.
  //   {{de Zweites zu vergleichendes Bit.}}
endmodule

/* Test case:
EN P Q P<Q P=Q P>Q
1  0 0  0   1   0
1  0 1  1   0   0
1  1 0  0   0   1
1  1 1  0   1   0
0  0 0  0   0   0
0  0 1  0   0   0
0  1 0  0   0   0
0  1 1  0   0   0
*/
