// Digital circuit CompCascade.dig as structural Verilog
// 4-bit comparator built according to the ripple-carry principle. 
// However, here the Enable bit is passed down from the 
// higher-order bit to the lower-order bit, ie in the reverse 
// direction as the carry bit of the ripple-carry adder.
// {{de 4-Bit Vergleicher der nach dem ripple-carry Prinzip
// aufgebaut ist. Jedoch wird hier das Enable-Bit
// vom höher wertigem Bit an das niederwertige Bit
// herabgereicht wird, also in der umgekehrten 
// Richtung wie das Carry-Bit des ripple-carry 
// Addierers.}}
module CompCascade (
  input  [3:0] P_15_12,
  input  [3:0] P_11_8,
  input  [3:0] P_7_4,
  input  [3:0] P_3_0,
  input  [3:0] Q_15_12,
  input  [3:0] Q_11_8,
  input  [3:0] Q_7_4,
  input  [3:0] Q_3_0,
  output P_lt_Q,
  output P_eq_Q,
  output P_gt_Q
);

  wire [3:0] comparator_1_gt, comparator_3_lt;

  Comparator #(.Bits(4)) comparator_1 (
    .a(P_15_12), .b(Q_15_12), .gt(comparator_1_gt[3]), .lt(comparator_3_lt[3]));  // open: eq
  Comparator #(.Bits(4)) comparator_2 (
    .a(P_11_8), .b(Q_11_8), .gt(comparator_1_gt[2]), .lt(comparator_3_lt[2]));  // open: eq
  Comparator #(.Bits(4)) comparator_3 (
    .a(P_7_4), .b(Q_7_4), .gt(comparator_1_gt[1]), .lt(comparator_3_lt[1]));  // open: eq
  Comparator #(.Bits(4)) comparator_4 (
    .a(P_3_0), .b(Q_3_0), .gt(comparator_1_gt[0]), .lt(comparator_3_lt[0]));  // open: eq
  Comparator #(.Bits(4)) comparator_5 (.a(comparator_1_gt), .b(comparator_3_lt), .gt(P_gt_Q), .eq(P_eq_Q), .lt(P_lt_Q));

  // Notes on the sheet:
  //   P_lt_Q: This output is high, if P<Q is valid.
  //   {{de Das Bit ist Eins, wenn P<Q gilt.}}
  //   P_eq_Q: This output is high, if P=Q is valid.
  //   {{de Das Bit ist Eins, wenn P=Q gilt.}}
  //   P_gt_Q: This output is high, if P>Q is valid.
  //   {{de Das Bit ist Eins, wenn P>Q gilt.}}
endmodule
