// Digital circuit CompRC.dig as structural Verilog
// 4-bit comparator built according to the ripple-carry principle. 
// However, here the Enable bit is passed down from the 
// higher-order bit to the lower-order bit, ie in the reverse 
// direction as the carry bit of the ripple-carry adder.
// {{de 4-Bit Vergleicher der nach dem ripple-carry Prinzip
// aufgebaut ist. Jedoch wird hier das Enable-Bit
// vom höher wertigem Bit an das niederwertige Bit
// herabgereicht wird, also in der umgekehrten 
// Richtung wie das Carry-Bit des ripple-carry 
// Addierers.}}
module CompRC (
  input  P_3,
  input  P_2,
  input  P_1,
  input  P_0,
  input  Q_3,
  input  Q_2,
  input  Q_1,
  input  Q_0,
  output P_lt_Q,
  output P_eq_Q,
  output P_gt_Q
);

  wire and_1_out, and_2_out, and_3_out, and_4_out, and_5_out, and_6_out, and_7_out, and_8_out,
       comparator_1_eq, comparator_1_gt, comparator_1_lt, comparator_2_eq, comparator_2_gt, comparator_2_lt,
       comparator_3_eq, comparator_3_gt, comparator_3_lt, comparator_4_eq, comparator_4_gt, comparator_4_lt;

  and and_1 (and_1_out, P_2, comparator_1_eq);
  and and_2 (and_2_out, comparator_1_eq, Q_2);
  and and_3 (and_3_out, P_1, and_7_out);
  and and_4 (and_4_out, and_7_out, Q_1);
  and and_5 (and_5_out, P_0, and_8_out);
  and and_6 (and_6_out, and_8_out, Q_0);
  Comparator comparator_1 (.a(P_3), .b(Q_3), .gt(comparator_1_gt), .eq(comparator_1_eq), .lt(comparator_1_lt));
  Comparator comparator_2 (
    .a(and_1_out), .b(and_2_out), .gt(comparator_2_gt), .eq(comparator_2_eq), .lt(comparator_2_lt));
  Comparator comparator_3 (
    .a(and_3_out), .b(and_4_out), .gt(comparator_3_gt), .eq(comparator_3_eq), .lt(comparator_3_lt));
  Comparator comparator_4 (
    .a(and_5_out), .b(and_6_out), .gt(comparator_4_gt), .eq(comparator_4_eq), .lt(comparator_4_lt));
  and and_7 (and_7_out, comparator_2_eq, comparator_1_eq);
  and and_8 (and_8_out, comparator_3_eq, and_7_out);
  and and_9 (P_eq_Q, comparator_4_eq, and_8_out);
  or or_1 (P_gt_Q, comparator_1_gt, comparator_2_gt, comparator_3_gt, comparator_4_gt);
  or or_2 (P_lt_Q, comparator_1_lt, comparator_2_lt, comparator_3_lt, comparator_4_lt);

  // Notes on the sheet:
  //   P_lt_Q: This output is high, if P<Q is valid.
  //   {{de Das Bit ist Eins, wenn P<Q gilt.}}
  //   P_eq_Q: This output is high, if P=Q is valid.
  //   {{de Das Bit ist Eins, wenn P=Q gilt.}}
  //   P_gt_Q: This output is high, if P>Q is valid.
  //   {{de Das Bit ist Eins, wenn P>Q gilt.}}
endmodule

/* Test case:
P_3 P_2 P_1 P_0   Q_3 Q_2 Q_1 Q_0  P<Q P=Q P>Q
repeat(256) bits(4,n>>4) bits(4,n) ((n>>4)<(n&15)) ((n>>4)=(n&15)) ((n>>4)>(n&15))
*/
