// Digital circuit Encoder.dig as structural Verilog
module Encoder (
  input  D_0,
  input  D_1,
  input  D_2,
  input  D_3,
  output A,
  output [1:0] Y,
  output a_2,
  output [1:0] y_2
);

  wire and_1_out, not_1_out;

  PriorityEncoder #(.Selector_Bits(2)) priorityencoder_1 (
    .in0(D_0), .in1(D_1), .in2(D_2), .in3(D_3), .num(y_2), .any(a_2));
  not not_1 (not_1_out, D_2);
  or or_1 (A, D_0, D_1, D_2, D_3);
  and and_1 (and_1_out, D_1, not_1_out);
  or or_2 (Y[0], and_1_out, D_3);
  or or_3 (Y[1], D_2, D_3);

  // Other names for the same wires on the sheet: D0 = D_0; D1 = D_1; D2 = D_2; D3 = D_3

  // Notes on the sheet:
  //   D_0: data bit 0.
  //   {{de Das 0. Datenbit.}}
  //   D_1: data bit 1.
  //   {{de Das 1. Datenbit.}}
  //   D_2: data bit 2.
  //   {{de Das 2. Datenbit.}}
  //   D_3: data bit 3.
  //   {{de Das 3. Datenbit.}}
  //   A: Output bit. One of the data bits is always output 
  //   here. Which one is set by the inputs A_0 and A_1.
  //   {{de Ausgangsbit. Es wird immer eines der Datenbits 
  //   hier ausgegeben. Welches das ist, legen die 
  //   Eingänge A_0 und A_1 fest.}}
endmodule

/* Test case:
D_3 D_2 D_1 D_0  A  Y 
0   0   0   0    0  0
1   X   X   X    1  3
0   1   X   X    1  2
0   0   1   X    1  1
0   0   0   1    1  0
*/
