// Digital circuit Plexers.dig as structural Verilog
module Plexers (
  input  [1:0] A3,
  input  Sel,
  input  A4,
  input  B4,
  input  A2,
  input  A1,
  input  B1,
  input  C4,
  input  D4,
  output [1:0] out_2,
  output out_3,
  output out_4,
  output out_5,
  output out_6,
  output out_7,
  output out_8,
  output out_9
);

  PriorityEncoder #(.Selector_Bits(2)) priorityencoder_1 (
    .in0(A4), .in1(B4), .in2(C4), .in3(D4), .num(out_2), .any(out_9));
  Multiplexer multiplexer_1 (.sel(Sel), .in_0(A1), .in_1(B1), .out(out_3));
  Demultiplexer demultiplexer_1 (.sel(Sel), .in(A2), .out_0(out_4), .out_1(out_5));
  BitSelector bitselector_1 (.in(A3), .sel(Sel), .out(out_8));
  Decoder decoder_1 (.sel(Sel), .out_0(out_6), .out_1(out_7));
endmodule
