// Digital circuit Selector.dig as structural Verilog
// 4-bit multiplexer.
// One of the data bits D_0 to D_3 is output at the output Y. Which 
// output is determined by the two inputs A_0 and A_1.
// {{de Diskret aufgebauter 4-Bit Multiplexer.
// Es wird immer eines der Datenbits D_0 bis D_3 am
// Ausgang Y ausgegeben. Welches ausgegeben wird,
// legen die beiden Eingänge A_0 und A_1 fest.}}
module Selector (
  input  [3:0] D,
  input  [1:0] Sel,
  input  A_0,
  input  A_1,
  input  D_0,
  input  D_1,
  input  D_2,
  input  D_3,
  output X,
  output Y
);

  wire and_1_out, and_2_out, and_3_out, and_4_out, and_5_out, and_6_out, not_1_out, not_2_out, not_3_out,
       or_1_out, or_2_out;

  and and_1 (and_1_out, D_3, A_0);
  and and_2 (and_2_out, not_1_out, D_2);
  not not_1 (not_1_out, A_0);
  and and_3 (and_3_out, D_1, A_0);
  and and_4 (and_4_out, not_2_out, D_0);
  not not_2 (not_2_out, A_0);
  or or_1 (or_1_out, and_1_out, and_2_out);
  or or_2 (or_2_out, and_3_out, and_4_out);
  not not_3 (not_3_out, A_1);
  BitSelector #(.Selector_Bits(2)) bitselector_1 (.in(D), .sel(Sel), .out(X));
  and and_5 (and_5_out, or_1_out, A_1);
  and and_6 (and_6_out, not_3_out, or_2_out);
  or or_3 (Y, and_5_out, and_6_out);

  // Other names for the same wires on the sheet: A0 = Sel[0]; A1 = Sel[1]

  // Notes on the sheet:
  //   X: Output bit. One of the data bits is always output 
  //   here. Which one is set by the inputs A_0 and A_1.
  //   {{de Ausgangsbit. Es wird immer eines der Datenbits 
  //   hier ausgegeben. Welches das ist, legen die 
  //   Eingänge A_0 und A_1 fest.}}
endmodule

/* Test case:
A_1 A_0 D_3 D_2 D_1 D_0 Y
 0   0   X   X   X   0  0
 0   0   X   X   X   1  1
 0   1   X   X   0   X  0
 0   1   X   X   1   X  1
 1   0   X   0   X   X  0
 1   0   X   1   X   X  1
 1   1   0   X   X   X  0
 1   1   1   X   X   X  1
*/
