// Digital circuit decoder.dig as structural Verilog
module decoder (
  input  A_0,
  input  A_1,
  output Y_0,
  output Y_1,
  output Y_2,
  output Y_3,
  output X_0,
  output X_1,
  output X_2,
  output X_3
);

  wire not_1_out, not_2_out;

  not not_1 (not_1_out, A_1);
  not not_2 (not_2_out, A_0);
  and and_1 (Y_0, not_2_out, not_1_out);
  and and_2 (Y_1, not_1_out, A_0);
  and and_3 (Y_2, not_2_out, A_1);
  and and_4 (Y_3, A_0, A_1);
  Decoder #(.Selector_Bits(2)) decoder_1 (.sel({A_1, A_0}), .out_0(X_0), .out_1(X_1), .out_2(X_2), .out_3(X_3));

  // Other names for the same wires on the sheet: A0 = A_0; A1 = A_1

  // Notes on the sheet:
  //   A_0: Bit 0 of the input selection.
  //   {{de Bit 0 der Signalauswahl.}}
  //   A_1: Bit 1 of the input selection.
  //   {{de Bit 1 der Signalauswahl.}}
  //   Y_0: Output bit. One of the data bits is always output 
  //   here. Which one is set by the inputs A_0 and A_1.
  //   {{de Ausgangsbit. Es wird immer eines der Datenbits 
  //   hier ausgegeben. Welches das ist, legen die 
  //   Eingänge A_0 und A_1 fest.}}
  //   Y_1: Output bit. One of the data bits is always output 
  //   here. Which one is set by the inputs A_0 and A_1.
  //   {{de Ausgangsbit. Es wird immer eines der Datenbits 
  //   hier ausgegeben. Welches das ist, legen die 
  //   Eingänge A_0 und A_1 fest.}}
  //   Y_2: Output bit. One of the data bits is always output 
  //   here. Which one is set by the inputs A_0 and A_1.
  //   {{de Ausgangsbit. Es wird immer eines der Datenbits 
  //   hier ausgegeben. Welches das ist, legen die 
  //   Eingänge A_0 und A_1 fest.}}
  //   Y_3: Output bit. One of the data bits is always output 
  //   here. Which one is set by the inputs A_0 and A_1.
  //   {{de Ausgangsbit. Es wird immer eines der Datenbits 
  //   hier ausgegeben. Welches das ist, legen die 
  //   Eingänge A_0 und A_1 fest.}}
  //   X_0: Output bit. One of the data bits is always output 
  //   here. Which one is set by the inputs A_0 and A_1.
  //   {{de Ausgangsbit. Es wird immer eines der Datenbits 
  //   hier ausgegeben. Welches das ist, legen die 
  //   Eingänge A_0 und A_1 fest.}}
  //   X_1: Output bit. One of the data bits is always output 
  //   here. Which one is set by the inputs A_0 and A_1.
  //   {{de Ausgangsbit. Es wird immer eines der Datenbits 
  //   hier ausgegeben. Welches das ist, legen die 
  //   Eingänge A_0 und A_1 fest.}}
  //   X_2: Output bit. One of the data bits is always output 
  //   here. Which one is set by the inputs A_0 and A_1.
  //   {{de Ausgangsbit. Es wird immer eines der Datenbits 
  //   hier ausgegeben. Welches das ist, legen die 
  //   Eingänge A_0 und A_1 fest.}}
  //   X_3: Output bit. One of the data bits is always output 
  //   here. Which one is set by the inputs A_0 and A_1.
  //   {{de Ausgangsbit. Es wird immer eines der Datenbits 
  //   hier ausgegeben. Welches das ist, legen die 
  //   Eingänge A_0 und A_1 fest.}}
endmodule

/* Test case:
A_1 A_0 Y_3 Y_2 Y_1 Y_0
 0   0   X   X   X   1  
 0   1   X   X   1   X  
 1   0   X   1   X   X  
 1   1   1   X   X   X  
*/
