// Digital circuit demux.dig as structural Verilog
// A 4-bit demultiplexer. The two input bits A_0 and A_1 specify 
// on which of the 4 output lines Y_0 to Y_3 the input D is output.
// {{de Ein 4-Bit Demultiplexer. Die zwei Eingangsbits A_0 
// und A_1 legen fest, auf welche der 4 
// Ausgangsleitungen Y_0 bis Y_3  der Eingang D 
// ausgegeben wird.}}
module demux (
  input  A_0,
  input  A_1,
  input  D,
  output Y_0,
  output Y_1,
  output Y_2,
  output Y_3,
  output out_8,
  output out_9,
  output out_10,
  output out_11,
  output out_12,
  output out_13,
  output out_14,
  output out_15
);

  wire not_1_out, not_2_out;

  not not_1 (not_1_out, A_1);
  Demultiplexer #(.Selector_Bits(2)) demultiplexer_1 (
    .sel({A_1, A_0}), .in(D), .out_0(out_8), .out_1(out_9), .out_2(out_10), .out_3(out_11));
  not not_2 (not_2_out, A_0);
  and and_1 (Y_0, not_2_out, not_1_out, D);
  and and_2 (Y_1, A_0, not_1_out, D);
  and and_3 (Y_2, not_2_out, A_1, D);
  and and_4 (Y_3, A_0, A_1, D);
  LookUpTable #(.Bits(4)) lookuptable_1 (.in0(D), .in1(A_0), .in2(A_1), .out({out_15, out_14, out_13, out_12}));

  // Other names for the same wires on the sheet: A0 = A_0; A1 = A_1

  // Notes on the sheet:
  //   A_0: selection bit 0
  //   {{de Das 0. Auswahlbit.}}
  //   A_1: election bit 1
  //   {{de Das 1. Auswahlbit.}}
  //   D: The data bit which is output to one of the four 
  //   outputs.
  //   {{de Das Datenbit welches auf einen der vier 
  //   Ausgänge ausgegeben wird.}}
  //   Y_0: output bit 0
  //   {{de Das 0. Ausgangsbit.}}
  //   Y_1: output bit 1
  //   {{de Das 1. Ausgangsbit.}}
  //   Y_2: output bit 2
  //   {{de Das 2. Ausgangsbit.}}
  //   Y_3: output bit 3
  //   {{de Das 3. Ausgangsbit.}}
  //   contents of lookuptable_1 (hex, n*v repeats v):
  //   0,1,0,2,0,4,0,8
endmodule

/* Test case:
A_1 A_0 D Y_3 Y_2 Y_1 Y_0
 0   0  0  0   0   0   0
 0   0  1  0   0   0   1
 0   1  0  0   0   0   0
 0   1  1  0   0   1   0
 1   0  0  0   0   0   0
 1   0  1  0   1   0   0
 1   1  0  0   0   0   0
 1   1  1  1   0   0   0
*/
