// Digital circuit mux.dig as structural Verilog
// 4-bit multiplexer.
// One of the data bits D_0 to D_3 is output at the output Y. Which 
// output is determined by the two inputs A_0 and A_1.
// {{de Diskret aufgebauter 4-Bit Multiplexer.
// Es wird immer eines der Datenbits D_0 bis D_3 am
// Ausgang Y ausgegeben. Welches ausgegeben wird,
// legen die beiden Eingänge A_0 und A_1 fest.}}
module mux (
  input  A_0,
  input  A_1,
  input  D_0,
  input  D_1,
  input  D_2,
  input  D_3,
  output Y,
  output X
);

  wire and_1_out, and_2_out, and_3_out, and_4_out, not_1_out, not_2_out;

  not not_1 (not_1_out, A_1);
  Multiplexer #(.Selector_Bits(2)) multiplexer_1 (
    .sel({A_1, A_0}), .in_0(D_0), .in_1(D_1), .in_2(D_2), .in_3(D_3), .out(X));
  not not_2 (not_2_out, A_0);
  and and_1 (and_1_out, not_2_out, not_1_out, D_0);
  and and_2 (and_2_out, A_0, not_1_out, D_1);
  and and_3 (and_3_out, not_2_out, A_1, D_2);
  and and_4 (and_4_out, A_0, A_1, D_3);
  or or_1 (Y, and_1_out, and_2_out, and_3_out, and_4_out);

  // Other names for the same wires on the sheet: A0 = A_0; A1 = A_1; D0 = D_0; D1 = D_1; D2 = D_2; D3 = D_3

  // Notes on the sheet:
  //   A_0: Bit 0 of the input selection.
  //   {{de Bit 0 der Signalauswahl.}}
  //   A_1: Bit 1 of the input selection.
  //   {{de Bit 1 der Signalauswahl.}}
  //   D_0: data bit 0.
  //   {{de Das 0. Datenbit.}}
  //   D_1: data bit 1.
  //   {{de Das 1. Datenbit.}}
  //   D_2: data bit 2.
  //   {{de Das 2. Datenbit.}}
  //   D_3: data bit 3.
  //   {{de Das 3. Datenbit.}}
  //   Y: Output bit. One of the data bits is always output 
  //   here. Which one is set by the inputs A_0 and A_1.
  //   {{de Ausgangsbit. Es wird immer eines der Datenbits 
  //   hier ausgegeben. Welches das ist, legen die 
  //   Eingänge A_0 und A_1 fest.}}
endmodule

/* Test case:
A_1 A_0 D_3 D_2 D_1 D_0 Y
 0   0   X   X   X   0  0
 0   0   X   X   X   1  1
 0   1   X   X   0   X  0
 0   1   X   X   1   X  1
 1   0   X   0   X   X  0
 1   0   X   1   X   X  1
 1   1   0   X   X   X  0
 1   1   1   X   X   X  1
*/
