// Digital circuit shifter.dig as structural Verilog
module shifter (
  input  [7:0] D_S,
  input  [3:0] shift_LL,
  input  [3:0] shift_LR,
  input  [3:0] shift_RL,
  input  [7:0] D,
  input  [3:0] shift,
  output [7:0] Q_LL,
  output [7:0] Q_LR,
  output [7:0] Q_RA,
  output [7:0] Q
);

  wire [7:0] multiplexer_1_out, multiplexer_2_out, multiplexer_3_out;

  BarrelShifter #(.Bits(8)) barrelshifter_1 (.in(D_S), .shift(shift_LL), .out(Q_LL));
  Multiplexer #(.Bits(8)) multiplexer_1 (.sel(shift[3]), .in_0(D), .in_1({8{1'b0}}), .out(multiplexer_1_out));
  Multiplexer #(.Bits(8)) multiplexer_2 (
    .sel(shift[2]), .in_0(multiplexer_1_out), .in_1({4'b0000, multiplexer_1_out[7:4]}),
    .out(multiplexer_2_out));
  Multiplexer #(.Bits(8)) multiplexer_3 (
    .sel(shift[1]), .in_0(multiplexer_2_out), .in_1({2'b00, multiplexer_2_out[7:2]}), .out(multiplexer_3_out));
  BarrelShifter #(.Bits(8), .direction("right")) barrelshifter_2 (.in(D_S), .shift(shift_RL), .out(Q_RA));
  Multiplexer #(.Bits(8)) multiplexer_4 (
    .sel(shift[0]), .in_0(multiplexer_3_out), .in_1({1'b0, multiplexer_3_out[7:1]}), .out(Q));
  BarrelShifter #(.Bits(8), .barrelShifterMode("rotate")) barrelshifter_3 (.in(D_S), .shift(shift_LR), .out(Q_LR));

  // Notes on the sheet:
  //   right shifter
endmodule
