// Digital circuit Analysis.dig as structural Verilog
module Analysis (
  input  A,
  input  B,
  input  C,
  output Y
);

  wire nand_1_out, nor_1_out, nor_2_out, not_1_out, not_2_out, or_1_out, xor_1_out, xor_2_out;

  not not_1 (not_1_out, A);
  not not_2 (not_2_out, B);
  xor xor_1 (xor_1_out, A, B);
  xor xor_2 (xor_2_out, B, C);
  nor nor_1 (nor_1_out, not_1_out, not_2_out);
  nor nor_2 (nor_2_out, A, C);
  nand nand_1 (nand_1_out, xor_1_out, xor_2_out);
  or or_1 (or_1_out, nor_1_out, nor_2_out);
  nand nand_2 (Y, nand_1_out, or_1_out);
endmodule
