// Digital circuit Hazard.dig as structural Verilog
module Hazard (
  input  In,
  input  A,
  output Out,
  output B
);

  wire delay_1_out, driver_1_out, xor_1_out, xor_2_out;

  Delay delay_1 (.in(In), .out(delay_1_out));
  xor xor_1 (xor_1_out, delay_1_out, In);
  assign driver_1_out = 1'b1 ? A : 1'bz;  // Driver driver_1
  xor xor_2 (xor_2_out, driver_1_out, A);
  xor xor_3 (Out, xor_1_out, In);
  xor xor_4 (B, xor_2_out, A);
endmodule
