// Digital circuit Hazard_1.dig as structural Verilog
module Hazard_1 (
  input  IN_0,
  output IN_1,
  output OUT_0,
  output OUT_1
);

  not not_1 (IN_1, IN_0);
  nand nand_1 (OUT_0, IN_1, IN_0);
  nand nand_2 (OUT_1, OUT_0, IN_0);
endmodule
