// Digital circuit Hazard_2.dig as structural Verilog
module Hazard_2 (
  input  x_2,
  input  x_0,
  input  x_1,
  output y
);

  wire and_1_out, and_2_out, not_1_out;

  not not_1 (not_1_out, x_0);
  and and_1 (and_1_out, x_2, not_1_out);
  and and_2 (and_2_out, x_0, x_1);
  or or_1 (y, and_1_out, and_2_out);

  // Notes on the sheet:
  //   x_2: default 1
  //   x_1: default 1
endmodule
