// Digital circuit Hazard_clear.dig as structural Verilog
module Hazard_clear (
  input  x_2,
  input  x_0,
  input  x_1,
  output y
);

  wire and_1_out, and_2_out, and_3_out, not_1_out, or_1_out;

  not not_1 (not_1_out, x_0);
  and and_1 (and_1_out, x_2, not_1_out);
  and and_2 (and_2_out, x_0, x_1);
  and and_3 (and_3_out, x_1, x_2);
  or or_1 (or_1_out, and_1_out, and_2_out);
  or or_2 (y, or_1_out, and_3_out);

  // Notes on the sheet:
  //   x_2: default 1
  //   x_1: default 1
endmodule
