// Digital circuit Oscillation.dig as structural Verilog
module Oscillation (
  input  in_1,
  input  in_3,
  output out_2,
  output out_4
);

  wire and_1_out, not_1_out, not_3_out, xor_1_out;

  not not_1 (not_1_out, out_4);
  and and_1 (and_1_out, in_3, not_1_out);
  xor xor_1 (xor_1_out, in_1, out_2);
  not not_2 (out_4, and_1_out);
  not not_3 (not_3_out, xor_1_out);
  not not_4 (out_2, not_3_out);
endmodule
