// Digital circuit Synthesise.dig as structural Verilog
module Synthesise (
  input  A_2,
  input  B_2,
  input  C_2,
  input  D_2,
  output dp,
  output a,
  output b,
  output c,
  output d,
  output e,
  output f,
  output g
);

  wire nand_1_out, nand_2_out, nand_3_out, nand_4_out, nand_5_out, nand_6_out, nand_7_out, nand_8_out,
       nand_9_out, nand_10_out, nand_11_out, nand_12_out, nand_13_out, nand_14_out, nand_15_out, nand_16_out,
       nand_17_out, nand_18_out, nand_19_out, nand_20_out, nand_21_out, nand_22_out, nand_23_out,
       nand_24_out, nand_25_out, nand_26_out, nand_27_out, nand_28_out, nand_29_out, nand_30_out,
       nand_31_out, nand_32_out, nand_33_out, not_1_out, not_2_out, not_3_out, not_4_out;

  not not_1 (not_1_out, A_2);
  not not_2 (not_2_out, B_2);
  not not_3 (not_3_out, C_2);
  not not_4 (not_4_out, D_2);
  nand nand_1 (nand_1_out, not_1_out, C_2);
  nand nand_2 (nand_2_out, not_1_out, B_2);
  nand nand_3 (nand_3_out, A_2, not_2_out, not_3_out);
  nand nand_4 (nand_4_out, B_2, C_2);
  nand nand_5 (nand_5_out, not_1_out, not_3_out, not_4_out);
  nand nand_6 (nand_6_out, not_1_out, C_2, D_2);
  nand nand_7 (nand_7_out, A_2, not_3_out, D_2);
  nand nand_8 (nand_8_out, not_2_out, not_4_out);
  nand nand_9 (nand_9_out, not_2_out, not_3_out);
  nand nand_10 (nand_10_out, not_1_out, B_2);
  nand nand_11 (nand_11_out, A_2, not_2_out);
  nand nand_12 (nand_12_out, not_2_out, D_2);
  nand nand_13 (nand_13_out, not_2_out, not_3_out);
  nand nand_14 (nand_14_out, not_3_out, D_2);
  nand nand_15 (nand_15_out, not_1_out, not_2_out, not_4_out);
  nand nand_16 (nand_16_out, A_2, not_3_out);
  nand nand_17 (nand_17_out, B_2, not_3_out, D_2);
  nand nand_18 (nand_18_out, not_2_out, C_2, D_2);
  nand nand_19 (nand_19_out, B_2, C_2, not_4_out);
  nand nand_20 (nand_20_out, A_2, C_2);
  nand nand_21 (nand_21_out, A_2, B_2);
  nand nand_22 (nand_22_out, not_2_out, not_4_out);
  nand nand_23 (nand_23_out, C_2, not_4_out);
  nand nand_24 (nand_24_out, not_1_out, B_2, not_3_out);
  nand nand_25 (nand_25_out, A_2, not_2_out);
  nand nand_26 (nand_26_out, A_2, C_2);
  nand nand_27 (nand_27_out, B_2, not_4_out);
  nand nand_28 (nand_28_out, not_3_out, not_4_out);
  nand nand_29 (nand_29_out, A_2, not_2_out);
  nand nand_30 (nand_30_out, not_1_out, B_2, not_3_out);
  nand nand_31 (nand_31_out, A_2, D_2);
  nand nand_32 (nand_32_out, not_2_out, C_2);
  nand nand_33 (nand_33_out, C_2, not_4_out);
  nand nand_34 (a, nand_1_out, nand_2_out, nand_3_out, nand_4_out, D_2);
  nand nand_35 (b, nand_5_out, nand_6_out, nand_7_out, nand_8_out, nand_9_out);
  nand nand_36 (c, nand_10_out, nand_11_out, nand_12_out, nand_13_out, nand_14_out);
  nand nand_37 (d, nand_15_out, nand_16_out, nand_17_out, nand_18_out, nand_19_out);
  nand nand_38 (e, nand_20_out, nand_21_out, nand_22_out, nand_23_out);
  nand nand_39 (f, nand_24_out, nand_25_out, nand_26_out, nand_27_out, nand_28_out);
  nand nand_40 (g, nand_29_out, nand_30_out, nand_31_out, nand_32_out, nand_33_out);

  assign dp = 1'b0;
endmodule
