// Digital circuit segment.dig as structural Verilog
module segment (
  input  D_3,
  input  D_2,
  input  D_1,
  input  D_0
);

  wire segment_1_p5, segment_1_p6, segment_1_p7, segment_1_p8, segment_1_p9, segment_1_p10, segment_1_p11,
       segment_1_p12;

  // segment segment_1: pin names not known; wires that end beside it: D_3, D_2, D_1, D_0, segment_1_p5, segment_1_p6, segment_1_p7, segment_1_p8, segment_1_p9, segment_1_p10, segment_1_p11, segment_1_p12
  Seven_Seg seven_seg_1 (
    .a(segment_1_p6), .b(segment_1_p7), .c(segment_1_p8), .d(segment_1_p9), .e(segment_1_p10),
    .f(segment_1_p11), .g(segment_1_p12), .dp(segment_1_p5));
endmodule
