// Digital circuit CRC.dig as structural Verilog
module CRC (
  input  [9:0] _10b_A,
  input  [4:0] _5b_B,
  input  Init,
  input  [9:0] A,
  input  Init_2,
  output [3:0] R,
  output [3:0] _4b_R,
  output D
);

  wire clock, clock_out, xor_2_out, xor_3_out;
  wire [0:0] d_ff_1_q;
  wire [3:0] multiplexer_3_out;
  wire [4:0] barrelshifter_1_out, d_ff_2_q, multiplexer_1_out, multiplexer_2_out, xor_1_out;
  wire [4:4] xor_1_out_2;
  wire [8:0] d_ff_4_q;
  wire [9:0] barrelshifter_2_out, multiplexer_4_out;

  Multiplexer #(.Bits(5)) multiplexer_1 (
    .sel(multiplexer_2_out[4]), .in_0({5{1'b0}}), .in_1(_5b_B), .out(multiplexer_1_out));
  Multiplexer #(.Bits(5)) multiplexer_2 (
    .sel(Init), .in_0({_4b_R, d_ff_1_q[0]}), .in_1(_10b_A[9:5]), .out(multiplexer_2_out));
  Multiplexer #(.Bits(5)) multiplexer_3 (
    .sel(Init), .in_0(d_ff_2_q), .in_1(_10b_A[4:0]), .out({xor_1_out[0], multiplexer_3_out}));
  Button u_clock (.out(clock_out));
  assign {xor_1_out_2[4], xor_1_out[4:1]} = multiplexer_1_out ^ multiplexer_2_out;  // XOr xor_1, 5 bits wide
  BarrelShifter #(.Bits(5)) barrelshifter_1 (
    .in({xor_1_out[0], multiplexer_3_out}), .shift(3'b001), .out(barrelshifter_1_out));
  // Probe on {xor_1_out_2[4], xor_1_out[4:1]}
  // Probe on barrelshifter_1_out
  D_FF #(.Bits(5)) d_ff_1 (.D(xor_1_out), .C(clock_out), .Q({_4b_R, d_ff_1_q[0]}));  // open: nQ
  D_FF #(.Bits(5)) d_ff_2 (.D(barrelshifter_1_out), .C(clock_out), .Q(d_ff_2_q));  // open: nQ
  // Probe on {_4b_R, d_ff_1_q[0]}
  // Probe on d_ff_2_q
  BarrelShifter #(.Bits(10)) barrelshifter_2 (.in({D, d_ff_4_q}), .shift(4'b0001), .out(barrelshifter_2_out));
  xor xor_2 (xor_2_out, R[3], D);
  D_FF d_ff_3 (.D(xor_2_out), .C(clock), .Q(R[0]));  // open: nQ
  Multiplexer #(.Bits(10)) multiplexer_4 (.sel(Init_2), .in_0(barrelshifter_2_out), .in_1(A), .out(multiplexer_4_out));
  // Probe on barrelshifter_2_out
  D_FF #(.Bits(10)) d_ff_4 (.D(multiplexer_4_out), .C(clock), .Q({D, d_ff_4_q}));  // open: nQ
  Button C (.out(clock));
  xor xor_3 (xor_3_out, R[3], R[0]);
  D_FF d_ff_5 (.D(xor_3_out), .C(clock), .Q(R[1]));  // open: nQ
  // Probe on {D, d_ff_4_q}
  D_FF d_ff_6 (.D(R[1]), .C(clock), .Q(R[2]));  // open: nQ
  D_FF d_ff_7 (.D(R[2]), .C(clock), .Q(R[3]));  // open: nQ

  // Other names for the same wires on the sheet: D_S = D
endmodule
