// Digital circuit D.dig as structural Verilog
module D (
  input  D,
  input  C,
  output Q_0,
  output nQ_0,
  output Q,
  output nQ,
  output Q_1,
  output nQ_1,
  output Q_2,
  output nQ_2,
  output out_10,
  output out_11
);

  wire and_1_out, and_2_out, and_3_out, and_4_out, and_5_out, and_6_out, nand_1_out, nand_2_out, nand_5_out,
       nand_6_out, nand_7_out, nand_8_out, nor_3_out, nor_4_out, not_1_out, not_2_out, not_3_out;

  and and_1 (and_1_out, not_1_out, C);
  not not_1 (not_1_out, D);
  and and_2 (and_2_out, C, D);
  nand nand_1 (nand_1_out, D, C);
  nand nand_2 (nand_2_out, nand_1_out, C);
  nor nor_1 (Q_0, and_1_out, nQ_0);
  nor nor_2 (nQ_0, Q_0, and_2_out);
  nand nand_3 (Q, nand_1_out, nQ);
  nand nand_4 (nQ, Q, nand_2_out);
  D_FF d_ff_1 (.D(D), .C(C), .Q(out_10), .nQ(out_11));
  and and_3 (and_3_out, D, C);
  not not_2 (not_2_out, D);
  and and_4 (and_4_out, C, not_2_out);
  not not_3 (not_3_out, C);
  nor nor_3 (nor_3_out, and_3_out, nor_4_out);
  nor nor_4 (nor_4_out, nor_3_out, and_4_out);
  nand nand_5 (nand_5_out, nand_8_out, nand_6_out);
  nand nand_6 (nand_6_out, nand_5_out, C);
  nand nand_7 (nand_7_out, nand_6_out, C, nand_8_out);
  nand nand_8 (nand_8_out, nand_7_out, D);
  and and_5 (and_5_out, nor_3_out, not_3_out);
  and and_6 (and_6_out, not_3_out, nor_4_out);
  nor nor_5 (Q_1, and_5_out, nQ_1);
  nor nor_6 (nQ_1, Q_1, and_6_out);
  nand nand_9 (Q_2, nand_6_out, nQ_2);
  nand nand_10 (nQ_2, Q_2, nand_7_out);
endmodule

/* Test case:
C D Q ~Q
C 1 1  0
0 1 1  0
0 0 1  0
C 0 0  1
0 0 0  1
0 1 0  1
*/
