// Digital circuit F_F.dig as structural Verilog
module F_F (
  input  S,
  input  R,
  input  J,
  input  K,
  input  D,
  input  T,
  input  set_D,
  input  clr_D,
  input  set_JK,
  input  clr_JK,
  output Q_0,
  output nQ_0,
  output Q_1,
  output nQ_1,
  output Q_3,
  output nQ_3,
  output Q_5,
  output nQ_5,
  output Q_4,
  output nQ_4,
  output Q_2,
  output nQ_2
);

  wire button_1_out;

  Button button_1 (.out(button_1_out));
  T_FF t_ff_1 (.T(T), .C(button_1_out), .Q(Q_5), .nQ(nQ_5));
  JK_FF jk_ff_1 (.J(J), .C(button_1_out), .K(K), .Q(Q_1), .nQ(nQ_1));
  D_FF d_ff_1 (.D(D), .C(button_1_out), .Q(Q_3), .nQ(nQ_3));
  RS_FF_AS rs_ff_as_1 (.S(S), .R(R), .Q(Q_0), .nQ(nQ_0));
  JK_FF_AS jk_ff_as_1 (.Set(set_JK), .J(J), .C(button_1_out), .K(K), .Clr(clr_JK), .Q(Q_2), .nQ(nQ_2));
  D_FF_AS d_ff_as_1 (.Set(set_D), .D(D), .C(button_1_out), .Clr(clr_D), .Q(Q_4), .nQ(nQ_4));
endmodule
