// Digital circuit Gray code.dig as structural Verilog
module Gray_code (
  input  clk_B,
  input  clk_A,
  input  C,
  output Q1,
  output Q0,
  output OV
);

  wire d_ff_1_q, d_ff_2_q, d_ff_3_q, d_ff_4_q, not_1_out, not_2_out, Q_0_n, Q_1_n;

  not not_1 (not_1_out, Q_1_n);
  not not_2 (not_2_out, Q_0_n);
  D_FF u_Q_1_n (.D(Q_0_n), .C(C), .Q(Q_1_n));  // open: nQ
  D_FF u_Q_0_n (.D(not_1_out), .C(C), .Q(Q_0_n));  // open: nQ
  and and_1 (OV, not_2_out, Q_1_n);
  D_FF d_ff_1 (.D(Q_1_n), .C(clk_A), .Q(d_ff_1_q));  // open: nQ
  D_FF d_ff_2 (.D(Q_0_n), .C(clk_A), .Q(d_ff_2_q));  // open: nQ
  D_FF d_ff_3 (.D(d_ff_1_q), .C(clk_B), .Q(d_ff_3_q));  // open: nQ
  D_FF d_ff_4 (.D(d_ff_2_q), .C(clk_B), .Q(d_ff_4_q));  // open: nQ
  D_FF d_ff_5 (.D(d_ff_3_q), .C(clk_B), .Q(Q1));  // open: nQ
  D_FF d_ff_6 (.D(d_ff_4_q), .C(clk_B), .Q(Q0));  // open: nQ

  // Notes on the sheet:
  //   transmission
  //   Gray
  //   received side
endmodule
