// Digital circuit RESET_1.dig as structural Verilog
module RESET_1 (
  input  IN_2,
  input  RST_2,
  input  CLK,
  input  IN_1,
  input  RST_1,
  output OUT_2,
  output OUT_1
);

  wire and_1_out;

  and and_1 (and_1_out, ~RST_1, IN_1);  // And
  D_FF_AS d_ff_as_1 (.Set(1'b0), .D(and_1_out), .C(CLK), .Clr(1'b0), .Q(OUT_1));  // open: nQ
  D_FF_AS d_ff_as_2 (.Set(1'b0), .D(IN_2), .C(CLK), .Clr(RST_2), .Q(OUT_2));  // open: nQ

  // Notes on the sheet:
  //   SyncReset
  //   AsyncReset
endmodule
