// Digital circuit RESET_2.dig as structural Verilog
module RESET_2 (
  input  reset,
  input  IN,
  input  clk,
  output OUT,
  output RST
);

  wire d_ff_as_1_q, d_ff_as_3_q;

  D_FF_AS d_ff_as_1 (.Set(1'b0), .D(1'b1), .C(clk), .Clr(reset), .Q(d_ff_as_1_q));  // open: nQ
  D_FF_AS d_ff_as_2 (.Set(1'b0), .D(d_ff_as_1_q), .C(clk), .Clr(reset), .nQ(RST));  // open: Q
  D_FF_AS d_ff_as_3 (.Set(1'b0), .D(IN), .C(clk), .Clr(RST), .Q(d_ff_as_3_q));  // open: nQ
  D_FF_AS d_ff_as_4 (.Set(1'b0), .D(d_ff_as_3_q), .C(clk), .Clr(RST), .Q(OUT));  // open: nQ

  // Notes on the sheet:
  //   clk: Hz: 2
endmodule
