// Digital circuit RS.dig as structural Verilog
module RS (
  input  R,
  input  S,
  input  C,
  output Q,
  output nQ,
  output Q_C,
  output nQ_C,
  output out_8,
  output out_9
);

  wire and_1_out, and_2_out;

  nor nor_1 (Q, R, nQ);
  nor nor_2 (nQ, Q, S);
  and and_1 (and_1_out, R, C);
  and and_2 (and_2_out, C, S);
  nor nor_3 (Q_C, and_1_out, nQ_C);
  nor nor_4 (nQ_C, Q_C, and_2_out);
  RS_FF_AS rs_ff_as_1 (.S(S), .R(R), .Q(out_8), .nQ(out_9));

  // Notes on the sheet:
  //   C: gate input
  //   {{de Freigabeeingang}}
  //   Q_C: The stored bit.
  //   {{de Das gespeicherte Bit}}
  //   nQ_C: The inverted stored bit.
  //   {{de Das inverse des gespeicherten Bits}}
endmodule

/* Test case RS:
R S Q ~Q
1 0 0  1
0 0 0  1
0 1 1  0
0 0 1  0
*/

/* Test case RS_C:
R C S Q_C ~Q_C
1 C 0  0   1
X 0 X  0   1
0 C 1  1   0
X 0 X  1   0
*/
