// Digital circuit T.dig as structural Verilog
module T (
  input  C,
  input  T,
  output Q,
  output nQ,
  output out_4,
  output out_5
);

  wire and_1_out, and_2_out, and_3_out, and_4_out, nand_1_out, nor_1_out, nor_2_out, nor_3_out, nor_4_out,
       not_1_out;

  T_FF t_ff_1 (.T(T), .C(C), .Q(out_4), .nQ(out_5));
  nand nand_1 (nand_1_out, T, C);
  and and_1 (and_1_out, nor_4_out, nand_1_out);
  not not_1 (not_1_out, nand_1_out);
  and and_2 (and_2_out, nand_1_out, nor_3_out);
  nor nor_1 (nor_1_out, and_1_out, nor_2_out);
  nor nor_2 (nor_2_out, nor_1_out, and_2_out);
  and and_3 (and_3_out, nor_1_out, not_1_out);
  and and_4 (and_4_out, not_1_out, nor_2_out);
  nor nor_3 (nor_3_out, and_3_out, nor_4_out);
  nor nor_4 (nor_4_out, nor_3_out, and_4_out);
  not not_2 (Q, nor_3_out);
  not not_3 (nQ, nor_4_out);
endmodule

/* Test case:
C T  Q ~Q
C 0  0 1
C 0  0 1
0 1  0 1
C 1  1 0
*/
