// Digital circuit clock gate.dig as structural Verilog
module clock_gate (
  input  D,
  input  in_3,
  input  x_2,
  input  x_0,
  input  x_1,
  input  CLK,
  output Q,
  output out_4,
  output y,
  output y_2
);

  wire and_1_out, and_2_out, not_1_out, not_2_out, not_4_out, not_5_out, xor_1_out, xor_2_out;

  xor xor_1 (xor_1_out, in_3, out_4);
  xor xor_2 (xor_2_out, D, Q);
  not not_1 (not_1_out, xor_1_out);
  not not_2 (not_2_out, xor_2_out);
  not not_3 (out_4, not_1_out);
  not not_4 (not_4_out, not_2_out);
  D_FF d_ff_1 (.D(not_4_out), .C(CLK), .Q(Q));  // open: nQ
  and and_1 (and_1_out, x_2, not_5_out);
  not not_5 (not_5_out, x_0);
  and and_2 (and_2_out, x_0, x_1);
  or or_1 (y_2, and_1_out, and_2_out);
  D_FF d_ff_2 (.D(y_2), .C(CLK), .Q(y));  // open: nQ

  // Notes on the sheet:
  //   x_2: default 1
  //   x_1: default 1
endmodule
