// Digital circuit edge_det.dig as structural Verilog
module edge_det (
  input  clk_B,
  input  A,
  input  clk_A,
  output B2,
  output B1
);

  wire d_ff_1_q, d_ff_2_q, d_ff_4_q, not_1_out;

  D_FF d_ff_1 (.D(A), .C(clk_A), .Q(d_ff_1_q));  // open: nQ
  D_FF d_ff_2 (.D(d_ff_1_q), .C(clk_B), .Q(d_ff_2_q));  // open: nQ
  D_FF d_ff_3 (.D(d_ff_2_q), .C(clk_B), .Q(B1));  // open: nQ
  D_FF d_ff_4 (.D(B1), .C(clk_B), .Q(d_ff_4_q));  // open: nQ
  not not_1 (not_1_out, d_ff_4_q);
  and and_1 (B2, B1, not_1_out);

  // Notes on the sheet:
  //   clk_B: Hz: 2
  //   clk_A: Hz: 2
  //   transmission
  //   received side
endmodule
