// Digital circuit edge_det2.dig as structural Verilog
module edge_det2 (
  input  clk_B,
  input  A,
  input  clk_A,
  output C_2,
  output B1,
  output B0
);

  wire d_ff_1_q, d_ff_2_q, d_ff_4_q;

  D_FF d_ff_1 (.D(A), .C(clk_A), .Q(d_ff_1_q));  // open: nQ
  D_FF d_ff_2 (.D(d_ff_1_q), .C(C_2), .Q(d_ff_2_q));  // open: nQ
  D_FF d_ff_3 (.D(d_ff_2_q), .C(C_2), .Q(B0));  // open: nQ
  D_FF d_ff_4 (.D(C_2), .C(clk_B), .Q(d_ff_4_q));  // open: nQ
  D_FF d_ff_5 (.D(B0), .C(clk_B), .Q(B1));  // open: nQ
  not not_1 (C_2, d_ff_4_q);

  // Notes on the sheet:
  //   clk_B: Hz: 10
  //   clk_A: Hz: 2
  //   transmission
  //   received side
endmodule
