// Digital circuit pulse_det1.dig as structural Verilog
module pulse_det1 (
  input  clk_1Hz,
  input  clk_2Hz,
  input  EN_A,
  input  A,
  output B,
  output EN_B
);

  wire d_ff_1_q, d_ff_2_q, multiplexer_1_out, multiplexer_2_out;

  Multiplexer multiplexer_1 (.sel(EN_A), .in_0(d_ff_1_q), .in_1(A), .out(multiplexer_1_out));
  D_FF d_ff_1 (.D(multiplexer_1_out), .C(clk_2Hz), .Q(d_ff_1_q));  // open: nQ
  D_FF d_ff_2 (.D(EN_A), .C(clk_1Hz), .Q(d_ff_2_q));  // open: nQ
  D_FF d_ff_3 (.D(d_ff_2_q), .C(clk_1Hz), .Q(EN_B));  // open: nQ
  Multiplexer multiplexer_2 (.sel(EN_B), .in_0(B), .in_1(d_ff_1_q), .out(multiplexer_2_out));
  D_FF d_ff_4 (.D(multiplexer_2_out), .C(clk_1Hz), .Q(B));  // open: nQ

  // Notes on the sheet:
  //   clk_2Hz: Hz: 2
endmodule
