// Digital circuit pulse_det2.dig as structural Verilog
module pulse_det2 (
  input  clk_1Hz,
  input  A,
  input  clk_2Hz,
  output B2,
  output B1
);

  wire d_ff_1_nq, d_ff_1_q, d_ff_2_q, d_ff_4_q, multiplexer_1_out;

  Multiplexer multiplexer_1 (.sel(A), .in_0(d_ff_1_q), .in_1(d_ff_1_nq), .out(multiplexer_1_out));
  D_FF d_ff_1 (.D(multiplexer_1_out), .C(clk_2Hz), .Q(d_ff_1_q), .nQ(d_ff_1_nq));
  D_FF d_ff_2 (.D(d_ff_1_q), .C(clk_1Hz), .Q(d_ff_2_q));  // open: nQ
  D_FF d_ff_3 (.D(d_ff_2_q), .C(clk_1Hz), .Q(B1));  // open: nQ
  D_FF d_ff_4 (.D(B1), .C(clk_1Hz), .Q(d_ff_4_q));  // open: nQ
  xor xor_1 (B2, B1, d_ff_4_q);

  // Notes on the sheet:
  //   clk_2Hz: Hz: 2
endmodule
