// Digital circuit register.dig as structural Verilog
module register (
  input  C,
  input  [3:0] D,
  input  E,
  output [3:0] out_4,
  output out_5,
  output out_6,
  output out_7,
  output out_8,
  output [3:0] Q
);

  Register #(.Bits(4)) register_1 (.D(D), .C(C), .en(E), .Q(out_4));
  D_FF D0 (.D(D[0]), .C(C), .Q(Q[0]), .nQ(out_5));
  D_FF D1 (.D(D[1]), .C(C), .Q(Q[1]), .nQ(out_6));
  D_FF D2 (.D(D[2]), .C(C), .Q(Q[2]), .nQ(out_7));
  D_FF D3 (.D(D[3]), .C(C), .Q(Q[3]), .nQ(out_8));
endmodule
