// Digital circuit shift register.dig as structural Verilog
module shift_register (
  input  R,
  input  C,
  input  Load,
  input  [3:0] D,
  output Q_0,
  output Q_1,
  output Q_2,
  output Q_3,
  output [3:0] Q,
  output [3:0] out_10,
  output [3:0] out_11,
  output OUT,
  output out_13
);

  wire multiplexer_1_out, multiplexer_2_out, multiplexer_3_out, multiplexer_4_out;
  wire [2:0] barrelshifter_1_out;
  wire [3:0] barrelshifter_2_out, multiplexer_5_out;
  wire [3:3] barrelshifter_1_out_2;

  BarrelShifter #(.Bits(4), .direction("right")) barrelshifter_1 (
    .in(out_10), .shift(3'b001), .out({barrelshifter_1_out_2[3], barrelshifter_1_out}));
  D_FF d_ff_1 (.D(R), .C(C), .Q(Q_3));  // open: nQ
  D_FF d_ff_2 (.D(Q_3), .C(C), .Q(Q_2));  // open: nQ
  D_FF d_ff_3 (.D(Q_2), .C(C), .Q(Q_1));  // open: nQ
  D_FF d_ff_4 (.D(Q_1), .C(C), .Q(Q_0));  // open: nQ
  // Probe on barrelshifter_1_out
  // Probe on {R, barrelshifter_1_out}
  D_FF #(.Bits(4)) d_ff_5 (.D({R, barrelshifter_1_out}), .C(C), .Q(out_10));  // open: nQ
  BarrelShifter #(.Bits(4), .direction("right")) barrelshifter_2 (
    .in(out_11), .shift(3'b001), .out(barrelshifter_2_out));
  Multiplexer multiplexer_1 (.sel(Load), .in_0(1'b0), .in_1(D[3]), .out(multiplexer_1_out));
  Multiplexer multiplexer_2 (.sel(Load), .in_0(Q[3]), .in_1(D[2]), .out(multiplexer_2_out));
  Multiplexer multiplexer_3 (.sel(Load), .in_0(Q[2]), .in_1(D[1]), .out(multiplexer_3_out));
  Multiplexer multiplexer_4 (.sel(Load), .in_0(Q[1]), .in_1(D[0]), .out(multiplexer_4_out));
  // Probe on barrelshifter_2_out
  Multiplexer #(.Bits(4)) multiplexer_5 (.sel(Load), .in_0(barrelshifter_2_out), .in_1(D), .out(multiplexer_5_out));
  D_FF d_ff_6 (.D(multiplexer_1_out), .C(C), .Q(Q[3]));  // open: nQ
  D_FF d_ff_7 (.D(multiplexer_2_out), .C(C), .Q(Q[2]));  // open: nQ
  D_FF d_ff_8 (.D(multiplexer_3_out), .C(C), .Q(Q[1]));  // open: nQ
  D_FF d_ff_9 (.D(multiplexer_4_out), .C(C), .Q(Q[0]));  // open: nQ
  // Probe on multiplexer_5_out
  D_FF #(.Bits(4)) d_ff_10 (.D(multiplexer_5_out), .C(C), .Q(out_11));  // open: nQ
  D_FF d_ff_11 (.D(Q[0]), .C(C), .Q(OUT));  // open: nQ
  D_FF d_ff_12 (.D(out_11[0]), .C(C), .Q(out_13));  // open: nQ

  // Other names for the same wires on the sheet: clock = C; D_L[3:0] = D; Ld = Load; right = R
endmodule
