// Digital circuit Counter-D.dig as structural Verilog
module Counter_D (
  input  C,
  input  A,
  input  B,
  output Q_3,
  output Q_2,
  output Q_1,
  output Q_0,
  output Y
);

  wire and_1_out, and_2_out, and_3_out, and_4_out, and_5_out, and_6_out, and_7_out, and_8_out, and_9_out,
       and_10_out, and_11_out, and_12_out, and_13_out, not_1_out, not_2_out, not_3_out, not_4_out, not_5_out,
       not_6_out, or_1_out, or_2_out, or_3_out;

  not not_1 (not_1_out, Q_3);
  not not_2 (not_2_out, Q_2);
  not not_3 (not_3_out, Q_1);
  not not_4 (not_4_out, Q_0);
  and and_1 (and_1_out, Q_0, Q_1, Q_2, not_1_out);
  and and_2 (and_2_out, not_4_out, Q_3);
  and and_3 (and_3_out, not_3_out, Q_3);
  and and_4 (and_4_out, not_2_out, Q_3);
  and and_5 (and_5_out, Q_0, Q_1, not_2_out);
  and and_6 (and_6_out, not_4_out, Q_2);
  and and_7 (and_7_out, not_3_out, Q_2);
  and and_8 (and_8_out, Q_0, not_3_out);
  and and_9 (and_9_out, not_4_out, Q_1);
  or or_1 (or_1_out, and_1_out, and_2_out, and_3_out, and_4_out);
  or or_2 (or_2_out, and_5_out, and_6_out, and_7_out);
  or or_3 (or_3_out, and_8_out, and_9_out);
  D_FF Q_3n (.D(or_1_out), .C(C), .Q(Q_3));  // open: nQ
  D_FF Q_2n (.D(or_2_out), .C(C), .Q(Q_2));  // open: nQ
  D_FF Q_1n (.D(or_3_out), .C(C), .Q(Q_1));  // open: nQ
  D_FF Q_0n (.D(not_4_out), .C(C), .Q(Q_0));  // open: nQ
  not not_5 (not_5_out, A);
  not not_6 (not_6_out, B);
  and and_10 (and_10_out, Q_0, not_5_out, not_6_out);
  and and_11 (and_11_out, Q_1, A, not_6_out);
  and and_12 (and_12_out, Q_2, not_5_out, B);
  and and_13 (and_13_out, Q_3, A, B);
  or or_4 (Y, and_13_out, and_12_out, and_11_out, and_10_out);

  // Other names for the same wires on the sheet: Q_0n = Q_0; Q_1n = Q_1; Q_2n = Q_2; Q_3n = Q_3

  // Notes on the sheet:
  //   C: Hz: 2
  //   A: First bit of frequency selection
  //   {{de Erstes Bit der Frequenzwahl}}
  //   B: Second bit of frequency selection
  //   {{de zweites Bit der Frequenzwahl}}
  //   Y: Prescaler output
  //   {{de Prescaler Ausgabe}}
endmodule

/* Test case counter:
           C Q_3 Q_2 Q_1 Q_0
repeat(16) C bits(4,n+1)
*/

/* Test case Prescaler:
           C A B Y
repeat(16) C     0 0 ((n+1)&1)
repeat(16) C     1 0 ((n+1)>>1&1)
repeat(16) C     0 1 ((n+1)>>2&1)
repeat(16) C     1 1 ((n+1)>>3&1)
*/
