// Digital circuit Freq_detect.dig as structural Verilog
module Freq_detect (
  input  P,
  input  clock,
  input  [7:0] Ref,
  output gt,
  output UP,
  output DOWN,
  output eq,
  output lt
);

  wire d_ff_1_q, d_ff_2_q, d_ff_3_q, d_ff_4_q, d_ff_as_1_q, not_1_out;
  wire [7:0] counter_1_out;

  D_FF d_ff_1 (.D(P), .C(clock), .Q(d_ff_1_q));  // open: nQ
  D_FF d_ff_2 (.D(P), .C(clock), .Q(d_ff_2_q));  // open: nQ
  Counter #(.Bits(8)) counter_1 (.en(d_ff_as_1_q), .C(clock), .clr(UP), .out(counter_1_out));  // open: ovf
  D_FF d_ff_3 (.D(d_ff_1_q), .C(clock), .Q(d_ff_3_q));  // open: nQ
  D_FF d_ff_4 (.D(d_ff_2_q), .C(clock), .Q(d_ff_4_q));  // open: nQ
  // Probe on counter_1_out
  Comparator #(.Bits(8)) comparator_1 (.a(counter_1_out), .b(Ref), .gt(gt), .eq(eq), .lt(lt));
  and and_1 (DOWN, d_ff_3_q, ~d_ff_1_q);  // And
  and and_2 (UP, d_ff_2_q, ~d_ff_4_q);  // And
  not not_1 (not_1_out, DOWN);
  D_FF_AS d_ff_as_1 (.Set(UP), .D(1'b0), .C(not_1_out), .Clr(1'b0), .Q(d_ff_as_1_q));  // open: nQ
endmodule
