// Digital circuit Phase_detect.dig as structural Verilog
module Phase_detect (
  input  CLK,
  input  in_8,
  input  in_9,
  output [2:0] out_1,
  output P,
  output [2:0] out_3,
  output Q,
  output [2:0] out_6,
  output [2:0] differ,
  output S,
  output early_late,
  output Sync
);

  wire counter_1_ovf, counter_2_ovf, not_1_out;

  Counter #(.Bits(3)) counter_1 (.en(in_8), .C(CLK), .clr(1'b0), .out(out_1), .ovf(counter_1_ovf));
  JK_FF_AS jk_ff_as_1 (.Set(1'b0), .J(counter_1_ovf), .C(CLK), .K(counter_1_ovf), .Clr(1'b0), .Q(P));  // open: nQ
  Counter #(.Bits(3)) counter_2 (.en(in_9), .C(CLK), .clr(1'b0), .out(out_3), .ovf(counter_2_ovf));
  D_FF d_ff_1 (.D(P), .C(Q), .Q(early_late));  // open: nQ
  xor xor_1 (S, P, Q);
  JK_FF_AS jk_ff_as_2 (.Set(1'b0), .J(counter_2_ovf), .C(CLK), .K(counter_2_ovf), .Clr(1'b0), .Q(Q));  // open: nQ
  not not_1 (not_1_out, S);
  D_FF d_ff_2 (.D(S), .C(Q), .nQ(Sync));  // open: Q
  Counter #(.Bits(3)) counter_3 (.en(S), .C(CLK), .clr(not_1_out), .out(out_6));  // open: ovf
  D_FF #(.Bits(3)) d_ff_3 (.D(out_6), .C(not_1_out), .Q(differ));  // open: nQ

  // Notes on the sheet:
  //   CLK: Hz: 2
endmodule
