// Digital circuit Prescaler .dig as structural Verilog
module Prescaler (
  output [3:0] out_1,
  output [3:0] out_2,
  output Q,
  output P
);

  wire clock_out, counterpreset_1_ovf, counterpreset_2_ovf, d_ff_1_q, multiplexer_1_out;

  CounterPreset #(.maxValue(1), .Bits(4)) counterpreset_1 (
    .en(1'b1), .C(clock_out), .dir(1'b0), .in(4'b0000), .ld(1'b0), .clr(1'b0), .out(out_1),
    .ovf(counterpreset_1_ovf));
  Button clock (.out(clock_out));
  JK_FF_AS jk_ff_as_1 (
    .Set(1'b0), .J(counterpreset_1_ovf), .C(clock_out), .K(counterpreset_1_ovf), .Clr(1'b0), .Q(P));  // open: nQ
  CounterPreset #(.maxValue(1), .Bits(4)) counterpreset_2 (
    .en(1'b1), .C(clock_out), .dir(1'b0), .in(4'b0000), .ld(1'b0), .clr(multiplexer_1_out), .out(out_2),
    .ovf(counterpreset_2_ovf));
  D_FF d_ff_1 (.D(counterpreset_2_ovf), .C(clock_out), .Q(d_ff_1_q));  // open: nQ
  Multiplexer multiplexer_1 (.sel(Q), .in_0(counterpreset_2_ovf), .in_1(d_ff_1_q), .out(multiplexer_1_out));
  JK_FF_AS jk_ff_as_2 (
    .Set(1'b0), .J(counterpreset_2_ovf), .C(clock_out), .K(counterpreset_2_ovf), .Clr(1'b0), .Q(Q));  // open: nQ
endmodule
