// Digital circuit Prescaler 1_x div.dig as structural Verilog
module Prescaler_1_x_div (
  input  [3:0] in_4,
  input  [3:0] in_5,
  output Q,
  output P,
  output S
);

  wire CLK_out, comparator_1_eq, jk_ff_as_1_q;
  wire [3:0] counterpreset_1_out, multiplexer_1_out;

  Button CLK (.out(CLK_out));
  CounterPreset #(.maxValue(16), .Bits(4)) counterpreset_1 (
    .en(1'b1), .C(CLK_out), .dir(1'b0), .in(4'b0000), .ld(1'b0), .clr(comparator_1_eq),
    .out(counterpreset_1_out));  // open: ovf
  // Probe on counterpreset_1_out
  Comparator #(.Bits(4)) comparator_1 (
    .a(counterpreset_1_out), .b(multiplexer_1_out), .eq(comparator_1_eq));  // open: gt, lt
  Multiplexer #(.Bits(4)) multiplexer_1 (.sel(jk_ff_as_1_q), .in_0(in_4), .in_1(in_5), .out(multiplexer_1_out));
  JK_FF_AS jk_ff_as_1 (
    .Set(1'b0), .J(comparator_1_eq), .C(CLK_out), .K(comparator_1_eq), .Clr(1'b0), .Q(jk_ff_as_1_q));  // open: nQ
  JK_FF_AS jk_ff_as_2 (.Set(1'b0), .J(1'b1), .C(CLK_out), .K(1'b1), .Clr(jk_ff_as_1_q), .Q(P));  // open: nQ
  nand nand_1 (Q, jk_ff_as_1_q, CLK_out);
  Multiplexer multiplexer_2 (.sel(jk_ff_as_1_q), .in_0(P), .in_1(Q), .out(S));
endmodule
