// Digital circuit Prescaler 2&3 div.dig as structural Verilog
module Prescaler_2_3_div (
  output Q,
  output P
);

  wire clock_out, d_ff_1_nq;

  Button clock (.out(clock_out));
  JK_FF_AS jk_ff_as_1 (.Set(1'b0), .J(1'b1), .C(clock_out), .K(1'b1), .Clr(1'b0), .Q(P));  // open: nQ
  JK_FF_AS jk_ff_as_2 (.Set(1'b0), .J(d_ff_1_nq), .C(clock_out), .K(d_ff_1_nq), .Clr(1'b0), .Q(Q));  // open: nQ
  D_FF d_ff_1 (.D(Q), .C(clock_out), .nQ(d_ff_1_nq));  // open: Q
endmodule
