// Digital circuit Prescaler 3_x div.dig as structural Verilog
module Prescaler_3_x_div (
  input  [3:0] in_1,
  input  [3:0] in_2,
  output P,
  output S,
  output Q
);

  wire clock_out, comparator_1_eq, counterpreset_2_ovf, d_ff_1_nq, jk_ff_as_1_q, not_1_out;
  wire [3:0] counterpreset_1_out, multiplexer_1_out;

  Button clock (.out(clock_out));
  CounterPreset #(.maxValue(16), .Bits(4)) counterpreset_1 (
    .en(1'b1), .C(clock_out), .dir(1'b0), .in(4'b0000), .ld(1'b0), .clr(comparator_1_eq),
    .out(counterpreset_1_out));  // open: ovf
  // Probe on counterpreset_1_out
  Comparator #(.Bits(4)) comparator_1 (
    .a(counterpreset_1_out), .b(multiplexer_1_out), .eq(comparator_1_eq));  // open: gt, lt
  Multiplexer #(.Bits(4)) multiplexer_1 (.sel(jk_ff_as_1_q), .in_0(in_1), .in_1(in_2), .out(multiplexer_1_out));
  JK_FF_AS jk_ff_as_1 (
    .Set(1'b0), .J(comparator_1_eq), .C(clock_out), .K(comparator_1_eq), .Clr(1'b0), .Q(jk_ff_as_1_q));  // open: nQ
  not not_1 (not_1_out, jk_ff_as_1_q);
  JK_FF_AS jk_ff_as_2 (.Set(1'b0), .J(d_ff_1_nq), .C(clock_out), .K(d_ff_1_nq), .Clr(jk_ff_as_1_q), .Q(P));  // open: nQ
  CounterPreset #(.maxValue(1), .Bits(4)) counterpreset_2 (
    .en(1'b1), .C(clock_out), .dir(1'b0), .in(4'b0000), .ld(1'b0), .clr(not_1_out), .ovf(counterpreset_2_ovf));  // open: out
  D_FF d_ff_1 (.D(P), .C(clock_out), .nQ(d_ff_1_nq));  // open: Q
  JK_FF_AS jk_ff_as_3 (
    .Set(1'b0), .J(counterpreset_2_ovf), .C(clock_out), .K(counterpreset_2_ovf), .Clr(1'b0), .Q(Q));  // open: nQ
  Multiplexer multiplexer_2 (.sel(jk_ff_as_1_q), .in_0(P), .in_1(Q), .out(S));
endmodule
