// Digital circuit Prescaler 4_x div.dig as structural Verilog
module Prescaler_4_x_div (
  input  [3:0] in_1,
  input  [3:0] in_2,
  output P
);

  wire and_1_out, clock_out, comparator_1_eq, counterpreset_2_ovf, d_ff_1_q, jk_ff_as_1_q, multiplexer_2_out;
  wire [3:0] counterpreset_1_out, counterpreset_2_out, multiplexer_1_out;

  Button clock (.out(clock_out));
  CounterPreset #(.maxValue(16), .Bits(4)) counterpreset_1 (
    .en(1'b1), .C(clock_out), .dir(1'b0), .in(4'b0000), .ld(1'b0), .clr(comparator_1_eq),
    .out(counterpreset_1_out));  // open: ovf
  // Probe on counterpreset_1_out
  Comparator #(.Bits(4)) comparator_1 (
    .a(counterpreset_1_out), .b(multiplexer_1_out), .eq(comparator_1_eq));  // open: gt, lt
  Multiplexer #(.Bits(4)) multiplexer_1 (.sel(jk_ff_as_1_q), .in_0(in_1), .in_1(in_2), .out(multiplexer_1_out));
  JK_FF_AS jk_ff_as_1 (
    .Set(1'b0), .J(comparator_1_eq), .C(clock_out), .K(comparator_1_eq), .Clr(1'b0), .Q(jk_ff_as_1_q));  // open: nQ
  and and_1 (and_1_out, jk_ff_as_1_q, multiplexer_2_out);
  CounterPreset #(.maxValue(1), .Bits(4)) counterpreset_2 (
    .en(1'b1), .C(clock_out), .dir(1'b0), .in(4'b0000), .ld(1'b0), .clr(and_1_out),
    .out(counterpreset_2_out), .ovf(counterpreset_2_ovf));
  // Probe on counterpreset_2_out
  D_FF d_ff_1 (.D(counterpreset_2_ovf), .C(clock_out), .Q(d_ff_1_q));  // open: nQ
  Multiplexer multiplexer_2 (.sel(P), .in_0(counterpreset_2_ovf), .in_1(d_ff_1_q), .out(multiplexer_2_out));
  JK_FF_AS jk_ff_as_2 (
    .Set(1'b0), .J(counterpreset_2_ovf), .C(clock_out), .K(counterpreset_2_ovf), .Clr(1'b0), .Q(P));  // open: nQ
endmodule
