// Digital circuit counter-JK Async.dig as structural Verilog
module counter_JK_Async (
  input  C,
  input  CLR,
  output P_0,
  output P_1,
  output P_2,
  output P_3
);

  wire jk_ff_as_1_q, jk_ff_as_2_q, jk_ff_as_3_q;

  JK_FF_AS jk_ff_as_1 (.Set(1'b0), .J(1'b1), .C(C), .K(1'b1), .Clr(CLR), .Q(jk_ff_as_1_q), .nQ(P_0));
  JK_FF_AS jk_ff_as_2 (.Set(1'b0), .J(1'b1), .C(jk_ff_as_1_q), .K(1'b1), .Clr(CLR), .Q(jk_ff_as_2_q), .nQ(P_1));
  JK_FF_AS jk_ff_as_3 (.Set(1'b0), .J(1'b1), .C(jk_ff_as_2_q), .K(1'b1), .Clr(CLR), .Q(jk_ff_as_3_q), .nQ(P_2));
  JK_FF_AS jk_ff_as_4 (.Set(1'b0), .J(1'b1), .C(jk_ff_as_3_q), .K(1'b1), .Clr(CLR), .nQ(P_3));  // open: Q

  // Notes on the sheet:
  //   Asynchronous counter
endmodule
