// Digital circuit counter-JK Sync.dig as structural Verilog
module counter_JK_Sync (
  input  C,
  input  CLR,
  output [3:0] Q,
  output [3:0] nQ,
  output Q_0,
  output Q_1,
  output Q_2,
  output Q_3
);

  wire and_1_out, and_2_out;

  JK_FF_AS jk_ff_as_1 (.Set(1'b0), .J(1'b1), .C(C), .K(1'b1), .Clr(CLR), .Q(Q[0]), .nQ(nQ[0]));
  JK_FF_AS jk_ff_as_2 (.Set(1'b0), .J(Q[0]), .C(C), .K(Q[0]), .Clr(CLR), .Q(Q[1]), .nQ(nQ[1]));
  and and_1 (and_1_out, Q[0], Q[1]);
  JK_FF_AS jk_ff_as_3 (.Set(1'b0), .J(and_1_out), .C(C), .K(and_1_out), .Clr(CLR), .Q(Q[2]), .nQ(nQ[2]));
  and and_2 (and_2_out, and_1_out, Q[2]);
  JK_FF_AS jk_ff_as_4 (.Set(1'b0), .J(and_2_out), .C(C), .K(and_2_out), .Clr(CLR), .Q(Q[3]), .nQ(nQ[3]));

  assign Q_0 = Q[0];
  assign Q_1 = Q[1];
  assign Q_2 = Q[2];
  assign Q_3 = Q[3];

  // Notes on the sheet:
  //   Synchronous counter
endmodule
