// Digital circuit counters.dig as structural Verilog
module counters (
  input  E,
  input  CLR,
  input  DIR,
  input  E_in,
  input  [3:0] D_in,
  output [3:0] out_6,
  output out_7,
  output [3:0] out_8,
  output out_9,
  output [3:0] out_10,
  output out_11
);

  wire and_1_out, clock_out, not_1_out, not_2_out;

  Button clock (.out(clock_out));
  CounterPreset #(.maxValue(9), .Bits(4)) counterpreset_1 (
    .en(E), .C(clock_out), .dir(DIR), .in(D_in), .ld(E_in), .clr(CLR), .out(out_6), .ovf(out_7));
  Counter #(.Bits(4)) counter_1 (.en(E), .C(clock_out), .clr(and_1_out), .out(out_10), .ovf(out_11));
  and and_1 (and_1_out, out_10[0], not_1_out, not_2_out, out_10[3]);
  Counter #(.Bits(4)) counter_2 (.en(E), .C(clock_out), .clr(CLR), .out(out_8), .ovf(out_9));
  not not_1 (not_1_out, out_10[1]);
  not not_2 (not_2_out, out_10[2]);

  // Notes on the sheet:
  //   m-counter
endmodule
