// Digital circuit e-clock segment.dig as structural Verilog
module e_clock_segment (
  input  LOAD,
  input  CLR,
  input  E,
  input  [3:0] D5,
  input  [3:0] D4,
  input  [3:0] D3,
  input  [3:0] D2,
  input  [3:0] D1,
  input  [3:0] D0,
  input  CLK,
  output ca,
  output cb,
  output cc,
  output cd,
  output ce,
  output cf,
  output cg,
  output an0,
  output an1,
  output an2,
  output an3,
  output an4,
  output an5,
  output an6,
  output an7
);

  wire _4us_ovf, and_1_out, clk_t, counterpreset_2_ovf, counterpreset_3_ovf, counterpreset_4_ovf,
       counterpreset_5_ovf, counterpreset_6_ovf, decoder_1_out_0, decoder_1_out_1, decoder_1_out_2,
       decoder_1_out_3, decoder_1_out_4, decoder_1_out_5, decoder_1_out_6, decoder_1_out_7;
  wire [2:0] sel;
  wire [3:0] counterpreset_1_out, counterpreset_2_out, counterpreset_3_out, counterpreset_4_out,
       counterpreset_5_out, counterpreset_6_out, multiplexer_1_out;

  CounterPreset #(.maxValue(399), .Bits(16)) _4us (
    .en(1'b1), .C(CLK), .dir(1'b0), .in({16{1'b0}}), .ld(1'b0), .clr(1'b0), .ovf(_4us_ovf));  // open: out
  Decoder #(.Selector_Bits(3)) decoder_1 (
    .sel(sel), .out_0(decoder_1_out_0), .out_1(decoder_1_out_1), .out_2(decoder_1_out_2),
    .out_3(decoder_1_out_3), .out_4(decoder_1_out_4), .out_5(decoder_1_out_5), .out_6(decoder_1_out_6),
    .out_7(decoder_1_out_7));
  not not_1 (an0, decoder_1_out_0);
  not not_2 (an1, decoder_1_out_1);
  not not_3 (an2, decoder_1_out_2);
  not not_4 (an3, decoder_1_out_3);
  not not_5 (an4, decoder_1_out_4);
  not not_6 (an5, decoder_1_out_5);
  not not_7 (an6, decoder_1_out_6);
  not not_8 (an7, decoder_1_out_7);
  CounterPreset #(.maxValue(5), .Bits(3)) _6times (
    .en(1'b1), .C(_4us_ovf), .dir(1'b0), .in(3'b000), .ld(1'b0), .clr(1'b0), .out(sel));  // open: ovf
  CounterPreset #(.maxValue(249999), .Bits(32)) _1s (
    .en(1'b1), .C(_4us_ovf), .dir(1'b0), .in({32{1'b0}}), .ld(1'b0), .clr(1'b0), .ovf(clk_t));  // open: out
  CounterPreset #(.maxValue(2), .Bits(4)) counterpreset_1 (
    .en(counterpreset_2_ovf), .C(clk_t), .dir(1'b0), .in(D5), .ld(LOAD), .clr(CLR), .out(counterpreset_1_out));  // open: ovf
  Multiplexer #(.Selector_Bits(3), .Bits(4)) multiplexer_1 (
    .sel(sel), .in_0(counterpreset_1_out), .in_1(counterpreset_2_out), .in_2(counterpreset_3_out),
    .in_3(counterpreset_4_out), .in_4(counterpreset_5_out), .in_5(counterpreset_6_out), .in_6(4'b0000),
    .in_7(4'b0000), .out(multiplexer_1_out));
  CounterPreset #(.maxValue(3), .Bits(4)) counterpreset_2 (
    .en(counterpreset_3_ovf), .C(clk_t), .dir(1'b0), .in(D4), .ld(LOAD), .clr(CLR),
    .out(counterpreset_2_out), .ovf(counterpreset_2_ovf));
  CounterPreset #(.maxValue(5), .Bits(4)) counterpreset_3 (
    .en(counterpreset_4_ovf), .C(clk_t), .dir(1'b0), .in(D3), .ld(LOAD), .clr(CLR),
    .out(counterpreset_3_out), .ovf(counterpreset_3_ovf));
  segdecode segdecode_1 (
    .A(multiplexer_1_out[0]), .B(multiplexer_1_out[1]), .C(multiplexer_1_out[2]), .D(multiplexer_1_out[3]),
    .ca(ca), .cb(cb), .cc(cc), .cd(cd), .ce(ce), .cf(cf), .cg(cg));
  CounterPreset #(.maxValue(9), .Bits(4)) counterpreset_4 (
    .en(counterpreset_5_ovf), .C(clk_t), .dir(1'b0), .in(D2), .ld(LOAD), .clr(CLR),
    .out(counterpreset_4_out), .ovf(counterpreset_4_ovf));
  CounterPreset #(.maxValue(5), .Bits(4)) counterpreset_5 (
    .en(counterpreset_6_ovf), .C(clk_t), .dir(1'b0), .in(D1), .ld(LOAD), .clr(CLR),
    .out(counterpreset_5_out), .ovf(counterpreset_5_ovf));
  CounterPreset #(.maxValue(9), .Bits(4)) counterpreset_6 (
    .en(and_1_out), .C(clk_t), .dir(1'b0), .in(D0), .ld(LOAD), .clr(CLR), .out(counterpreset_6_out),
    .ovf(counterpreset_6_ovf));
  and and_1 (and_1_out, ~LOAD, E);  // And

  // Notes on the sheet:
  //   D5: default 2
  //   D4: default 3
  //   D3: default 5
  //   D2: default 9
  //   D1: default 5
endmodule
