// Digital circuit e-clock.dig as structural Verilog
module e_clock (
  input  LOAD,
  input  CLR,
  input  clock,
  input  E,
  input  [3:0] D5,
  input  [3:0] D4,
  input  [3:0] D3,
  input  [3:0] D2,
  input  [3:0] D0,
  input  [3:0] D1
);

  wire and_1_out, counterpreset_2_ovf, counterpreset_3_ovf, counterpreset_4_ovf, counterpreset_5_ovf,
       counterpreset_6_ovf;
  wire [3:0] counterpreset_1_out, counterpreset_2_out, counterpreset_3_out, counterpreset_4_out,
       counterpreset_5_out, counterpreset_6_out;

  CounterPreset #(.maxValue(2), .Bits(4)) counterpreset_1 (
    .en(counterpreset_2_ovf), .C(clock), .dir(1'b0), .in(D5), .ld(LOAD), .clr(CLR), .out(counterpreset_1_out));  // open: ovf
  Seven_Seg_Hex seven_seg_hex_1 (.d(counterpreset_1_out), .dp(1'b0));
  CounterPreset #(.maxValue(3), .Bits(4)) counterpreset_2 (
    .en(counterpreset_3_ovf), .C(clock), .dir(1'b0), .in(D4), .ld(LOAD), .clr(CLR),
    .out(counterpreset_2_out), .ovf(counterpreset_2_ovf));
  Seven_Seg_Hex seven_seg_hex_2 (.d(counterpreset_2_out), .dp(1'b0));
  CounterPreset #(.maxValue(5), .Bits(4)) counterpreset_3 (
    .en(counterpreset_4_ovf), .C(clock), .dir(1'b0), .in(D3), .ld(LOAD), .clr(CLR),
    .out(counterpreset_3_out), .ovf(counterpreset_3_ovf));
  Seven_Seg_Hex seven_seg_hex_3 (.d(counterpreset_3_out), .dp(1'b0));
  CounterPreset #(.maxValue(9), .Bits(4)) counterpreset_4 (
    .en(counterpreset_5_ovf), .C(clock), .dir(1'b0), .in(D2), .ld(LOAD), .clr(CLR),
    .out(counterpreset_4_out), .ovf(counterpreset_4_ovf));
  Seven_Seg_Hex seven_seg_hex_4 (.d(counterpreset_4_out), .dp(1'b0));
  CounterPreset #(.maxValue(5), .Bits(4)) counterpreset_5 (
    .en(counterpreset_6_ovf), .C(clock), .dir(1'b0), .in(D1), .ld(LOAD), .clr(CLR),
    .out(counterpreset_5_out), .ovf(counterpreset_5_ovf));
  Seven_Seg_Hex seven_seg_hex_5 (.d(counterpreset_5_out), .dp(1'b0));
  Seven_Seg_Hex seven_seg_hex_6 (.d(counterpreset_6_out), .dp(1'b0));
  CounterPreset #(.maxValue(9), .Bits(4)) counterpreset_6 (
    .en(and_1_out), .C(clock), .dir(1'b0), .in(D0), .ld(LOAD), .clr(CLR), .out(counterpreset_6_out),
    .ovf(counterpreset_6_ovf));
  and and_1 (and_1_out, ~LOAD, E);  // And

  // Notes on the sheet:
  //   clock: Hz: 2
endmodule
