// Digital circuit key_detect.dig as structural Verilog
module key_detect (
  input  key,
  input  clock,
  output Det,
  output Pulse
);

  wire and_2_out, and_3_out, comparator_1_eq, d_ff_1_q, d_ff_2_q, d_ff_3_q, d_ff_4_q, d_ff_as_1_q, or_1_out;
  wire [3:0] counter_1_out;

  D_FF d_ff_1 (.D(key), .C(clock), .Q(d_ff_1_q));  // open: nQ
  Counter #(.Bits(4)) counter_1 (.en(d_ff_as_1_q), .C(clock), .clr(and_3_out), .out(counter_1_out));  // open: ovf
  or or_1 (or_1_out, and_2_out, d_ff_as_1_q);
  D_FF d_ff_2 (.D(d_ff_1_q), .C(clock), .Q(d_ff_2_q));  // open: nQ
  Comparator #(.Bits(4)) comparator_1 (.a(4'b0100), .b(counter_1_out), .eq(comparator_1_eq));  // open: gt, lt
  // Probe on counter_1_out
  D_FF d_ff_3 (.D(or_1_out), .C(clock), .Q(d_ff_3_q));  // open: nQ
  and and_1 (Pulse, d_ff_1_q, ~d_ff_2_q);  // And
  and and_2 (and_2_out, comparator_1_eq, key);
  D_FF d_ff_4 (.D(d_ff_3_q), .C(clock), .Q(d_ff_4_q));  // open: nQ
  D_FF_AS d_ff_as_1 (.Set(Pulse), .D(1'b0), .C(comparator_1_eq), .Clr(1'b0), .Q(d_ff_as_1_q));  // open: nQ
  D_FF d_ff_5 (.D(and_2_out), .C(clock), .Q(Det));  // open: nQ
  and and_3 (and_3_out, d_ff_4_q, ~d_ff_3_q);  // And
endmodule
