// Digital circuit second-clock.dig as structural Verilog
module second_clock (
  input  E,
  input  CLR,
  input  clock
);

  wire counterpreset_2_ovf, counterpreset_3_ovf, counterpreset_4_ovf;
  wire [3:0] counterpreset_1_out, counterpreset_2_out, counterpreset_3_out, counterpreset_4_out;

  CounterPreset #(.maxValue(5), .Bits(4)) counterpreset_1 (
    .en(counterpreset_2_ovf), .C(clock), .dir(1'b0), .in(4'b0000), .ld(1'b0), .clr(CLR),
    .out(counterpreset_1_out));  // open: ovf
  Seven_Seg_Hex seven_seg_hex_1 (.d(counterpreset_1_out), .dp(1'b0));
  CounterPreset #(.maxValue(9), .Bits(4)) counterpreset_2 (
    .en(counterpreset_3_ovf), .C(clock), .dir(1'b0), .in(4'b0000), .ld(1'b0), .clr(CLR),
    .out(counterpreset_2_out), .ovf(counterpreset_2_ovf));
  Seven_Seg_Hex seven_seg_hex_2 (.d(counterpreset_2_out), .dp(1'b0));
  CounterPreset #(.maxValue(5), .Bits(4)) counterpreset_3 (
    .en(counterpreset_4_ovf), .C(clock), .dir(1'b0), .in(4'b0000), .ld(1'b0), .clr(CLR),
    .out(counterpreset_3_out), .ovf(counterpreset_3_ovf));
  Seven_Seg_Hex seven_seg_hex_3 (.d(counterpreset_3_out), .dp(1'b0));
  Seven_Seg_Hex seven_seg_hex_4 (.d(counterpreset_4_out), .dp(1'b0));
  CounterPreset #(.maxValue(9), .Bits(4)) counterpreset_4 (
    .en(E), .C(clock), .dir(1'b0), .in(4'b0000), .ld(1'b0), .clr(CLR), .out(counterpreset_4_out),
    .ovf(counterpreset_4_ovf));

  // Notes on the sheet:
  //   clock: Hz: 2
endmodule
