// Digital circuit segdecode.dig as structural Verilog
module segdecode (
  input  A,
  input  B,
  input  C,
  input  D,
  output ca,
  output cb,
  output cc,
  output cd,
  output ce,
  output cf,
  output cg
);

  wire and_1_out, and_2_out, and_3_out, and_4_out, and_5_out, and_6_out, and_7_out, and_8_out, and_9_out,
       and_10_out, and_11_out, and_12_out, and_13_out, and_14_out, and_15_out, and_16_out, and_17_out,
       nand_1_out, nand_2_out, nand_3_out, nand_4_out, nand_5_out, nand_6_out, nand_7_out, not_1_out;

  nand nand_1 (nand_1_out, A, 1'b1);
  nand nand_2 (nand_2_out, B, 1'b1);
  nand nand_3 (nand_3_out, C, 1'b1);
  not not_1 (not_1_out, D);
  nand nand_4 (nand_4_out, nand_1_out, 1'b1);
  nand nand_5 (nand_5_out, nand_2_out, 1'b1);
  nand nand_6 (nand_6_out, nand_3_out, 1'b1);
  nand nand_7 (nand_7_out, not_1_out, 1'b1);
  and and_1 (and_1_out, nand_5_out, nand_7_out);
  and and_2 (and_2_out, nand_1_out, nand_6_out);
  and and_3 (and_3_out, nand_4_out, nand_2_out, nand_3_out, not_1_out);
  and and_4 (and_4_out, nand_5_out, nand_7_out);
  and and_5 (and_5_out, nand_4_out, nand_2_out, nand_6_out);
  and and_6 (and_6_out, nand_1_out, nand_5_out, nand_6_out);
  and and_7 (and_7_out, nand_6_out, nand_7_out);
  and and_8 (and_8_out, nand_1_out, nand_5_out, nand_3_out);
  and and_9 (and_9_out, nand_4_out, nand_2_out, nand_3_out);
  and and_10 (and_10_out, nand_1_out, nand_2_out, nand_6_out);
  and and_11 (and_11_out, nand_4_out, nand_5_out, nand_6_out);
  and and_12 (and_12_out, nand_2_out, nand_6_out);
  and and_13 (and_13_out, nand_4_out, nand_5_out);
  and and_14 (and_14_out, nand_5_out, nand_3_out);
  and and_15 (and_15_out, nand_4_out, nand_3_out, not_1_out);
  and and_16 (and_16_out, nand_4_out, nand_5_out, nand_6_out);
  and and_17 (and_17_out, nand_2_out, nand_3_out, not_1_out, 1'b1);
  or or_1 (ca, and_1_out, and_2_out, and_3_out);
  or or_2 (cb, and_4_out, and_5_out, and_6_out);
  or or_3 (cc, and_7_out, and_8_out);
  or or_4 (cd, and_9_out, and_10_out, and_11_out);
  or or_5 (ce, nand_4_out, and_12_out);
  or or_6 (cf, and_13_out, and_14_out, and_15_out);
  or or_7 (cg, and_16_out, and_17_out);

  // Notes on the sheet:
  //   A: Bit 0, pin 7
  //   B: Bit 1, pin 1
  //   C: Bit 2, pin 2
  //   D: Bit 3, pin 6
endmodule
