// Digital circuit FSM1.dig as structural Verilog
module FSM1 (
  input  C,
  output [1:0] T,
  output G,
  output R
);

  wire and_1_out, and_2_out, and_3_out, and_4_out, not_1_out, not_2_out, or_1_out, or_2_out;

  not not_1 (not_1_out, R);
  not not_2 (not_2_out, T[0]);
  and and_1 (and_1_out, T[0], not_1_out);
  and and_2 (and_2_out, not_2_out, R);
  or or_1 (or_1_out, not_2_out, R);
  and and_3 (and_3_out, T[0], not_1_out);
  and and_4 (and_4_out, not_2_out, R);
  or or_2 (or_2_out, and_1_out, and_2_out);
  or or_3 (G, and_3_out, and_4_out);
  D_FF Q1_n (.D(or_2_out), .C(C), .Q(R));  // open: nQ
  D_FF Q0_n (.D(or_1_out), .C(C), .Q(T[0]));  // open: nQ
  // Probe traffic1.fsm on {R, T[0]}

  assign T[1] = R;

  // Other names for the same wires on the sheet: Q0_n = T[0]; Q1_n = R; T1 = R

  // Notes on the sheet:
  //   C: Hz: 2
endmodule
