// Digital circuit FSM3.dig as structural Verilog
module FSM3 (
  input  clr,
  input  en,
  input  C,
  input  [3:0] IN,
  input  Load,
  output [6:0] S,
  output ov
);

  wire and_1_out, and_2_out, and_3_out, and_4_out, and_5_out, and_6_out, and_7_out, and_8_out, and_9_out,
       and_10_out, and_11_out, and_12_out, and_13_out, and_14_out, and_15_out, and_16_out, and_17_out,
       and_18_out, and_19_out, and_20_out, and_21_out, and_22_out, and_23_out, and_24_out, and_25_out,
       and_26_out, and_27_out, and_28_out, and_29_out, not_1_out, not_2_out, not_3_out, not_4_out, not_5_out,
       not_6_out, Q0_n, Q1_n, Q2_n, Q3_n;
  wire [3:0] multiplexer_1_out, or_2_out;

  not not_1 (not_1_out, clr);
  not not_2 (not_2_out, en);
  not not_3 (not_3_out, Q3_n);
  not not_4 (not_4_out, Q2_n);
  not not_5 (not_5_out, Q1_n);
  not not_6 (not_6_out, Q0_n);
  and and_1 (and_1_out, not_6_out, not_5_out, not_4_out, not_3_out, not_1_out, en);
  and and_2 (and_2_out, Q0_n, Q3_n, not_1_out);
  and and_3 (and_3_out, Q3_n, not_1_out, not_2_out);
  and and_4 (and_4_out, not_6_out, Q3_n, not_1_out, en);
  and and_5 (and_5_out, Q0_n, Q2_n, not_1_out);
  and and_6 (and_6_out, Q1_n, Q2_n, not_1_out);
  and and_7 (and_7_out, Q2_n, not_1_out, not_2_out);
  and and_8 (and_8_out, not_6_out, not_5_out, Q2_n, not_1_out, en);
  and and_9 (and_9_out, not_6_out, Q3_n, not_1_out, en);
  and and_10 (and_10_out, Q0_n, Q1_n, not_1_out);
  and and_11 (and_11_out, Q1_n, not_1_out, not_2_out);
  and and_12 (and_12_out, not_6_out, not_1_out, en);
  and and_13 (and_13_out, Q0_n, not_1_out, not_2_out);
  and and_14 (and_14_out, not_6_out, not_4_out);
  and and_15 (and_15_out, Q0_n, Q2_n);
  and and_16 (and_16_out, not_6_out, not_5_out);
  and and_17 (and_17_out, Q0_n, Q1_n);
  or or_1 (S[2], Q0_n, not_5_out, Q2_n);
  and and_18 (and_18_out, not_6_out, not_4_out);
  and and_19 (and_19_out, Q0_n, not_5_out, Q2_n);
  and and_20 (and_20_out, not_6_out, Q1_n);
  and and_21 (and_21_out, Q1_n, not_4_out);
  and and_22 (and_22_out, not_6_out, not_4_out);
  and and_23 (and_23_out, not_6_out, Q1_n);
  and and_24 (and_24_out, not_6_out, not_5_out);
  and and_25 (and_25_out, not_6_out, Q2_n);
  and and_26 (and_26_out, not_5_out, Q2_n);
  and and_27 (and_27_out, not_6_out, Q1_n);
  and and_28 (and_28_out, Q1_n, not_4_out);
  and and_29 (and_29_out, not_5_out, Q2_n);
  and and_30 (ov, not_6_out, not_5_out, not_4_out, not_3_out, not_1_out, en);
  or or_2 (or_2_out[3], and_1_out, and_2_out, and_3_out);
  or or_3 (or_2_out[2], and_4_out, and_5_out, and_6_out, and_7_out);
  or or_4 (or_2_out[1], and_8_out, and_9_out, and_10_out, and_11_out);
  or or_5 (or_2_out[0], and_12_out, and_13_out);
  or or_6 (S[0], and_14_out, and_15_out, Q1_n, Q3_n);
  or or_7 (S[1], and_16_out, and_17_out, not_4_out);
  or or_8 (S[3], and_18_out, and_19_out, and_20_out, and_21_out, Q3_n);
  or or_9 (S[4], and_22_out, and_23_out);
  or or_10 (S[5], and_24_out, and_25_out, and_26_out, Q3_n);
  or or_11 (S[6], and_27_out, and_28_out, and_29_out, Q3_n);
  Multiplexer #(.Bits(4)) multiplexer_1 (.sel(Load), .in_0(or_2_out), .in_1(IN), .out(multiplexer_1_out));
  // Probe Counter.fsm on {Q3_n, Q2_n, Q1_n, Q0_n}
  D_FF u_Q3_n (.D(multiplexer_1_out[3]), .C(C), .Q(Q3_n));  // open: nQ
  D_FF u_Q2_n (.D(multiplexer_1_out[2]), .C(C), .Q(Q2_n));  // open: nQ
  D_FF u_Q1_n (.D(multiplexer_1_out[1]), .C(C), .Q(Q1_n));  // open: nQ
  D_FF u_Q0_n (.D(multiplexer_1_out[0]), .C(C), .Q(Q0_n));  // open: nQ

  // Notes on the sheet:
  //   C: Hz: 2
endmodule
