// Digital circuit FSM_s_mealy.dig as structural Verilog
module FSM_s_mealy (
  input  IN,
  input  C,
  output Det
);

  wire and_1_out, and_2_out, and_3_out, and_4_out, not_1_out, not_2_out, not_3_out, or_1_out, or_2_out,
       Z_0_n, Z_1_n;

  not not_1 (not_1_out, IN);
  not not_2 (not_2_out, Z_1_n);
  not not_3 (not_3_out, Z_0_n);
  and and_1 (and_1_out, IN, Z_0_n, not_2_out);
  and and_2 (and_2_out, not_3_out, Z_1_n);
  and and_3 (and_3_out, IN, not_3_out, not_2_out);
  and and_4 (and_4_out, not_1_out, not_3_out, Z_1_n);
  and and_5 (Det, IN, Z_0_n, Z_1_n);
  or or_1 (or_1_out, and_1_out, and_2_out);
  or or_2 (or_2_out, and_3_out, and_4_out);
  // Probe sequence_mealy.fsm on {Z_1_n, Z_0_n}
  D_FF u_Z_1_n (.D(or_1_out), .C(C), .Q(Z_1_n));  // open: nQ
  D_FF u_Z_0_n (.D(or_2_out), .C(C), .Q(Z_0_n));  // open: nQ

  // Notes on the sheet:
  //   C: Hz: 2
endmodule
