// Digital circuit counter_fsm2.dig as structural Verilog
module counter_fsm2 (
  input  in_2,
  input  in_3,
  input  in_4,
  output out_1
);

  wire [6:0] fsm2_1_s;

  FSM2 fsm2_1 (.clr(in_2), .en(in_3), .C(in_4), .S(fsm2_1_s), .ov(out_1));
  Seven_Seg seven_seg_1 (
    .a(fsm2_1_s[0]), .b(fsm2_1_s[1]), .c(fsm2_1_s[2]), .d(fsm2_1_s[3]), .e(fsm2_1_s[4]), .f(fsm2_1_s[5]),
    .g(fsm2_1_s[6]), .dp(1'b0));
endmodule
