// Digital circuit counter_fsm3.dig as structural Verilog
module counter_fsm3 (
  input  in_2,
  input  in_3,
  input  in_4,
  input  [3:0] in_5,
  input  in_6,
  output out_1
);

  wire [6:0] fsm3_1_s;

  FSM3 fsm3_1 (.clr(in_2), .en(in_3), .C(in_4), .IN(in_5), .Load(in_6), .S(fsm3_1_s), .ov(out_1));
  Seven_Seg seven_seg_1 (
    .a(fsm3_1_s[0]), .b(fsm3_1_s[1]), .c(fsm3_1_s[2]), .d(fsm3_1_s[3]), .e(fsm3_1_s[4]), .f(fsm3_1_s[5]),
    .g(fsm3_1_s[6]), .dp(1'b0));
endmodule
