// Digital circuit ring counter.dig as structural Verilog
module ring_counter (
  input  C0,
  output S0,
  output S1,
  output S2,
  output S3,
  output D0,
  output D1,
  output D2,
  output D3,
  output S0_2,
  output S1_2,
  output S2_2,
  output S3_2
);

  wire and_1_out, CLK_out, d_ff_3_nq, d_ff_4_nq, dipswitch_1_out, or_1_out;
  wire [1:0] d_ff_3_q, d_ff_4_q;

  Button CLK (.out(CLK_out));
  DipSwitch dipswitch_1 (.out(dipswitch_1_out));
  D_FF_AS d_ff_as_1 (.Set(dipswitch_1_out), .D(D3), .C(CLK_out), .Clr(1'b0), .Q(D0));  // open: nQ
  D_FF d_ff_1 (.D(and_1_out), .C(CLK_out), .Q(d_ff_3_q[0]));  // open: nQ
  D_FF d_ff_2 (.D(d_ff_4_nq), .C(CLK_out), .Q(d_ff_4_q[0]));  // open: nQ
  D_FF d_ff_3 (.D(d_ff_3_q[0]), .C(CLK_out), .Q(d_ff_3_q[1]), .nQ(d_ff_3_nq));
  D_FF d_ff_4 (.D(d_ff_4_q[0]), .C(CLK_out), .Q(d_ff_4_q[1]), .nQ(d_ff_4_nq));
  D_FF_AS d_ff_as_2 (.Set(1'b0), .D(D0), .C(CLK_out), .Clr(1'b0), .Q(D1));  // open: nQ
  and and_1 (and_1_out, or_1_out, d_ff_3_nq);
  or or_1 (or_1_out, C0, d_ff_3_q[0]);
  Decoder #(.Selector_Bits(2)) decoder_1 (.sel(d_ff_4_q), .out_0(S0), .out_1(S1), .out_2(S3), .out_3(S2));
  D_FF_AS d_ff_as_3 (.Set(1'b0), .D(D1), .C(CLK_out), .Clr(1'b0), .Q(D2));  // open: nQ
  Decoder #(.Selector_Bits(2)) decoder_2 (.sel(d_ff_3_q), .out_0(S0_2), .out_1(S1_2), .out_2(S3_2), .out_3(S2_2));
  D_FF_AS d_ff_as_4 (.Set(1'b0), .D(D2), .C(CLK_out), .Clr(1'b0), .Q(D3));  // open: nQ

  // Notes on the sheet:
  //   ring counter
  //   Johnson counter
  //   Johnson counter with condition
endmodule
