// Digital circuit sequence_det.dig as structural Verilog
module sequence_det (
  input  [7:0] \sequence ,
  output out_2,
  output out_3
);

  wire bitselector_1_out, button_1_out;
  wire [2:0] counter_1_out, not_1_out;

  Counter #(.Bits(3)) counter_1 (.en(1'b1), .C(button_1_out), .clr(1'b0), .out(counter_1_out));  // open: ovf
  Button button_1 (.out(button_1_out));
  assign not_1_out = ~counter_1_out;  // Not not_1, 3 bits wide
  BitSelector #(.Selector_Bits(3)) bitselector_1 (.in(\sequence ), .sel(not_1_out), .out(bitselector_1_out));
  // Probe on not_1_out
  FSM_s_moore fsm_s_moore_1 (.IN(bitselector_1_out), .C(button_1_out), .Det(out_2));
  FSM_s_mealy fsm_s_mealy_1 (.IN(bitselector_1_out), .C(button_1_out), .Det(out_3));
endmodule
