// Digital circuit traffic light.dig as structural Verilog
module traffic_light (
  input  clk,
  input  E,
  input  CLR,
  output S_0,
  output S_1
);

  wire counterpreset_1_ovf, counterpreset_2_ovf, d_ff_1_q, d_ff_2_q, d_ff_3_nq, d_ff_4_nq, load, not_1_out,
       or_1_out;
  wire [3:0] counterpreset_1_out, counterpreset_2_out, lookuptable_1_out, lookuptable_1_out_2;

  not not_1 (not_1_out, load);
  LookUpTable #(.Bits(8)) lookuptable_1 (.in0(S_0), .in1(S_1), .out({lookuptable_1_out_2, lookuptable_1_out}));
  D_FF d_ff_1 (.D(S_1), .C(not_1_out), .Q(d_ff_1_q));  // open: nQ
  D_FF d_ff_2 (.D(S_0), .C(not_1_out), .Q(d_ff_2_q));  // open: nQ
  // RGBLED rgbled_1: pin names not known; wires that end beside it: d_ff_1_q, d_ff_2_q, 1'b0
  CounterPreset #(.maxValue(9), .Bits(4)) counterpreset_1 (
    .en(counterpreset_2_ovf), .C(clk), .dir(1'b1), .in(lookuptable_1_out_2), .ld(load), .clr(CLR),
    .out(counterpreset_1_out), .ovf(counterpreset_1_ovf));
  D_FF d_ff_3 (.D(or_1_out), .C(load), .Q(S_0), .nQ(d_ff_3_nq));
  or or_1 (or_1_out, d_ff_4_nq, d_ff_3_nq);
  Seven_Seg_Hex seven_seg_hex_1 (.d(counterpreset_1_out), .dp(1'b0));
  D_FF d_ff_4 (.D(S_0), .C(load), .Q(S_1), .nQ(d_ff_4_nq));
  CounterPreset #(.maxValue(9), .Bits(4)) counterpreset_2 (
    .en(E), .C(clk), .dir(1'b1), .in(lookuptable_1_out), .ld(load), .clr(CLR), .out(counterpreset_2_out),
    .ovf(counterpreset_2_ovf));
  Seven_Seg_Hex seven_seg_hex_2 (.d(counterpreset_2_out), .dp(1'b0));
  and and_1 (load, counterpreset_1_ovf, counterpreset_2_ovf);

  // Other names for the same wires on the sheet: S0 = S_0; S1 = S_1

  // Notes on the sheet:
  //   contents of lookuptable_1 (hex, n*v repeats v):
  //   0,10,8,4
endmodule
