// Digital circuit traffic_light_fsm1.dig as structural Verilog
module traffic_light_fsm1 (
  input  clk,
  input  E,
  input  CLR
);

  wire counterpreset_1_ovf, counterpreset_2_ovf, load;
  wire [1:0] d_ff_1_q, fsm1_1_r, fsm1_1_t;
  wire [3:0] counterpreset_1_out, counterpreset_2_out, lookuptable_1_out, lookuptable_1_out_2;

  LookUpTable #(.Bits(8)) lookuptable_1 (
    .in0(fsm1_1_t[0]), .in1(fsm1_1_t[1]), .out({lookuptable_1_out_2, lookuptable_1_out}));
  FSM1 fsm1_1 (.C(load), .T(fsm1_1_t), .G(fsm1_1_r[0]), .R(fsm1_1_r[1]));
  D_FF #(.Bits(2)) d_ff_1 (.D(fsm1_1_r), .C(clk), .Q(d_ff_1_q));  // open: nQ
  // RGBLED rgbled_1: pin names not known; wires that end beside it: d_ff_1_q[1], d_ff_1_q[0], 1'b0
  CounterPreset #(.maxValue(9), .Bits(4)) counterpreset_1 (
    .en(counterpreset_2_ovf), .C(clk), .dir(1'b1), .in(lookuptable_1_out_2), .ld(load), .clr(CLR),
    .out(counterpreset_1_out), .ovf(counterpreset_1_ovf));
  Seven_Seg_Hex seven_seg_hex_1 (.d(counterpreset_1_out), .dp(1'b0));
  CounterPreset #(.maxValue(9), .Bits(4)) counterpreset_2 (
    .en(E), .C(clk), .dir(1'b1), .in(lookuptable_1_out), .ld(load), .clr(CLR), .out(counterpreset_2_out),
    .ovf(counterpreset_2_ovf));
  Seven_Seg_Hex seven_seg_hex_2 (.d(counterpreset_2_out), .dp(1'b0));
  and and_1 (load, counterpreset_1_ovf, counterpreset_2_ovf);

  // Notes on the sheet:
  //   contents of lookuptable_1 (hex, n*v repeats v):
  //   0,10,3,7
endmodule
