// Digital circuit traffic_light_fsm3.dig as structural Verilog
module traffic_light_fsm3 (
  input  clk,
  input  E,
  input  CLR
);

  wire fsm3_1_ov, fsm3_2_ov, load;
  wire [1:0] d_ff_1_q, fsm1_1_r, fsm1_1_t;
  wire [3:0] lookuptable_1_out, lookuptable_1_out_2;
  wire [6:0] fsm3_1_s, fsm3_2_s;

  FSM1 fsm1_1 (.C(load), .T(fsm1_1_t), .G(fsm1_1_r[0]), .R(fsm1_1_r[1]));
  LookUpTable #(.Bits(8)) lookuptable_1 (
    .in0(fsm1_1_t[0]), .in1(fsm1_1_t[1]), .out({lookuptable_1_out_2, lookuptable_1_out}));
  D_FF #(.Bits(2)) d_ff_1 (.D(fsm1_1_r), .C(clk), .Q(d_ff_1_q));  // open: nQ
  FSM3 fsm3_1 (.clr(CLR), .en(fsm3_2_ov), .C(clk), .IN(lookuptable_1_out_2), .Load(load), .S(fsm3_1_s), .ov(fsm3_1_ov));
  // RGBLED rgbled_1: pin names not known; wires that end beside it: d_ff_1_q[1], d_ff_1_q[0], 1'b0
  and and_1 (load, fsm3_2_ov, fsm3_1_ov);
  Seven_Seg seven_seg_1 (
    .a(fsm3_1_s[0]), .b(fsm3_1_s[1]), .c(fsm3_1_s[2]), .d(fsm3_1_s[3]), .e(fsm3_1_s[4]), .f(fsm3_1_s[5]),
    .g(fsm3_1_s[6]), .dp(1'b0));
  FSM3 fsm3_2 (.clr(CLR), .en(E), .C(clk), .IN(lookuptable_1_out), .Load(load), .S(fsm3_2_s), .ov(fsm3_2_ov));
  Seven_Seg seven_seg_2 (
    .a(fsm3_2_s[0]), .b(fsm3_2_s[1]), .c(fsm3_2_s[2]), .d(fsm3_2_s[3]), .e(fsm3_2_s[4]), .f(fsm3_2_s[5]),
    .g(fsm3_2_s[6]), .dp(1'b0));

  // Notes on the sheet:
  //   contents of lookuptable_1 (hex, n*v repeats v):
  //   0,10,3,7
endmodule
