// Digital circuit ASCII.dig as structural Verilog
module ASCII (
  input  sel,
  input  clr,
  output out_3
);

  wire clk_out, demultiplexer_1_out_0, demultiplexer_1_out_1;
  wire [3:0] counter_1_out;
  wire [15:0] keyboard_1_d, multiplexer_1_out, rom_1_d;

  Demultiplexer demultiplexer_1 (.sel(sel), .in(clk_out), .out_0(demultiplexer_1_out_0), .out_1(demultiplexer_1_out_1));
  Button clk (.out(clk_out));
  Counter #(.Bits(4)) counter_1 (.en(1'b1), .C(demultiplexer_1_out_0), .clr(clr), .out(counter_1_out));  // open: ovf
  Keyboard keyboard_1 (.C(demultiplexer_1_out_1), .en(1'b1), .D(keyboard_1_d), .av(out_3));
  // Probe on counter_1_out
  ROM #(.AddrBits(4), .Bits(16)) rom_1 (.A(counter_1_out), .sel(1'b1), .D(rom_1_d));
  // Probe on keyboard_1_d
  // Probe on rom_1_d
  Multiplexer #(.Bits(16)) multiplexer_1 (.sel(sel), .in_0(rom_1_d), .in_1(keyboard_1_d), .out(multiplexer_1_out));
  Terminal terminal_1 (.D(multiplexer_1_out), .C(clk_out), .en(1'b1));

  // Notes on the sheet:
  //   contents of rom_1 (hex, n*v repeats v):
  //   48,65,6c,6c,6f,20,0,77,6f,72,6c,64
endmodule
