// Digital circuit EPROM.dig as structural Verilog
module EPROM (
  input  A_0,
  input  A_1,
  input  A_2,
  input  A_3,
  input  CS,
  output Q
);

  wire decoder_1_out_0, decoder_1_out_1, decoder_1_out_2, decoder_1_out_3, decoder_2_out_0, decoder_2_out_1,
       decoder_2_out_2, decoder_2_out_3, fgnfet_1_d, fgnfet_5_d, nfet_1_s, pullup_3_out, pullup_4_out;

  Decoder #(.Selector_Bits(2)) decoder_1 (
    .sel({A_1, A_0}), .out_0(decoder_1_out_0), .out_1(decoder_1_out_1), .out_2(decoder_1_out_2),
    .out_3(decoder_1_out_3));
  Decoder #(.Selector_Bits(2)) decoder_2 (
    .sel({A_3, A_2}), .out_0(decoder_2_out_0), .out_1(decoder_2_out_1), .out_2(decoder_2_out_2),
    .out_3(decoder_2_out_3));
  FGNFET fgnfet_1 (.G(decoder_1_out_0), .D(fgnfet_1_d), .S(1'b0));
  FGNFET fgnfet_2 (.G(decoder_1_out_1), .D(fgnfet_1_d), .S(1'b0));
  FGNFET fgnfet_3 (.G(decoder_1_out_2), .D(fgnfet_1_d), .S(1'b0));
  FGNFET fgnfet_4 (.G(decoder_1_out_3), .D(fgnfet_1_d), .S(1'b0));
  NFET nfet_1 (.G(decoder_2_out_0), .D(fgnfet_1_d), .S(nfet_1_s));
  PullUp pullup_1 (.out(fgnfet_1_d));
  FGNFET fgnfet_5 (.G(decoder_1_out_0), .D(fgnfet_5_d), .S(1'b0));
  FGNFET fgnfet_6 (.G(decoder_1_out_1), .D(fgnfet_5_d), .S(1'b0));
  FGNFET #(.Blown("true")) fgnfet_7 (.G(decoder_1_out_2), .D(fgnfet_5_d), .S(1'b0));
  FGNFET fgnfet_8 (.G(decoder_1_out_3), .D(fgnfet_5_d), .S(1'b0));
  PullUp pullup_2 (.out(fgnfet_5_d));
  NFET nfet_2 (.G(decoder_2_out_1), .D(fgnfet_5_d), .S(nfet_1_s));
  PullUp pullup_3 (.out(pullup_3_out));
  FGNFET fgnfet_9 (.G(decoder_1_out_0), .D(pullup_3_out), .S(1'b0));
  FGNFET fgnfet_10 (.G(decoder_1_out_1), .D(pullup_3_out), .S(1'b0));
  FGNFET fgnfet_11 (.G(decoder_1_out_2), .D(pullup_3_out), .S(1'b0));
  FGNFET fgnfet_12 (.G(decoder_1_out_3), .D(pullup_3_out), .S(1'b0));
  NFET nfet_3 (.G(decoder_2_out_2), .D(pullup_3_out), .S(nfet_1_s));
  PullUp pullup_4 (.out(pullup_4_out));
  FGNFET fgnfet_13 (.G(decoder_1_out_0), .D(pullup_4_out), .S(1'b0));
  FGNFET fgnfet_14 (.G(decoder_1_out_1), .D(pullup_4_out), .S(1'b0));
  FGNFET fgnfet_15 (.G(decoder_1_out_2), .D(pullup_4_out), .S(1'b0));
  FGNFET fgnfet_16 (.G(decoder_1_out_3), .D(pullup_4_out), .S(1'b0));
  NFET nfet_4 (.G(decoder_2_out_3), .D(pullup_4_out), .S(nfet_1_s));
  assign Q = CS ? nfet_1_s : 1'bz;  // Driver driver_1

  // Notes on the sheet:
  //   CS: default 1
endmodule

/* Test case:
A_0 A_1 A_2 A_3 Q
 0   0   0   0  0
 0   0   0   1  0
 0   0   1   0  0
 0   0   1   1  0
 0   1   0   0  0
 0   1   0   1  0
 0   1   1   0  1
 0   1   1   1  0
 1   0   0   0  0
 1   0   0   1  1
 1   0   1   0  0
 1   0   1   1  0
 1   1   0   0  0
 1   1   0   1  0
 1   1   1   0  0
 1   1   1   1  0
*/
