// Digital circuit LED matrix.dig as structural Verilog
module LED_matrix (
  input  C
);

  wire [3:0] counter_1_out;
  wire [15:0] rom_1_d;

  Counter #(.Bits(4)) counter_1 (.en(1'b1), .C(C), .clr(1'b0), .out(counter_1_out));  // open: ovf
  // Probe on counter_1_out
  ROM #(.AddrBits(4), .Bits(16)) rom_1 (.A(counter_1_out), .sel(1'b1), .D(rom_1_d));
  // Probe on rom_1_d
  LedMatrix #(.ledPersistence("true"), .colAddrBits(4), .rowDataBits(16)) ledmatrix_1 (
    .rows(rom_1_d), .column(counter_1_out));

  // Notes on the sheet:
  //   contents of rom_1 (hex, n*v repeats v):
  //   0,0,ff0,810,810,810,810,ffff,810,810,810,810,ff0
endmodule
