// Digital circuit PROM.dig as structural Verilog
module PROM (
  input  A_0,
  input  A_1,
  input  A_2,
  input  A_3,
  input  CS,
  output Q
);

  wire decoder_1_out_0, decoder_1_out_1, decoder_1_out_2, decoder_1_out_3, decoder_2_out_0, decoder_2_out_1,
       decoder_2_out_2, decoder_2_out_3, fuse_9_b, fuse_13_b, nfet_1_d, nfet_2_d, nfet_3_d, nfet_4_d,
       nfet_5_s, nfet_6_d, nfet_7_d, nfet_8_d, nfet_9_d, nfet_11_d, nfet_12_d, nfet_13_d, nfet_14_d,
       nfet_16_d, nfet_17_d, nfet_18_d, nfet_19_d, pullup_1_out, pullup_2_out;

  Decoder #(.Selector_Bits(2)) decoder_1 (
    .sel({A_1, A_0}), .out_0(decoder_1_out_0), .out_1(decoder_1_out_1), .out_2(decoder_1_out_2),
    .out_3(decoder_1_out_3));
  Decoder #(.Selector_Bits(2)) decoder_2 (
    .sel({A_3, A_2}), .out_0(decoder_2_out_0), .out_1(decoder_2_out_1), .out_2(decoder_2_out_2),
    .out_3(decoder_2_out_3));
  NFET nfet_1 (.G(decoder_1_out_0), .D(nfet_1_d), .S(1'b0));
  NFET nfet_2 (.G(decoder_1_out_1), .D(nfet_2_d), .S(1'b0));
  NFET nfet_3 (.G(decoder_1_out_2), .D(nfet_3_d), .S(1'b0));
  NFET nfet_4 (.G(decoder_1_out_3), .D(nfet_4_d), .S(1'b0));
  PullUp pullup_1 (.out(pullup_1_out));
  Fuse fuse_1 (.A(nfet_1_d), .B(pullup_1_out));
  Fuse fuse_2 (.A(nfet_2_d), .B(pullup_1_out));
  Fuse fuse_3 (.A(nfet_3_d), .B(pullup_1_out));
  Fuse fuse_4 (.A(nfet_4_d), .B(pullup_1_out));
  NFET nfet_5 (.G(decoder_2_out_0), .D(pullup_1_out), .S(nfet_5_s));
  NFET nfet_6 (.G(decoder_1_out_0), .D(nfet_6_d), .S(1'b0));
  NFET nfet_7 (.G(decoder_1_out_1), .D(nfet_7_d), .S(1'b0));
  NFET nfet_8 (.G(decoder_1_out_2), .D(nfet_8_d), .S(1'b0));
  NFET nfet_9 (.G(decoder_1_out_3), .D(nfet_9_d), .S(1'b0));
  PullUp pullup_2 (.out(pullup_2_out));
  Fuse fuse_5 (.A(nfet_6_d), .B(pullup_2_out));
  Fuse fuse_6 (.A(nfet_7_d), .B(pullup_2_out));
  Fuse #(.Blown("true")) fuse_7 (.A(nfet_8_d), .B(pullup_2_out));
  Fuse fuse_8 (.A(nfet_9_d), .B(pullup_2_out));
  NFET nfet_10 (.G(decoder_2_out_1), .D(pullup_2_out), .S(nfet_5_s));
  NFET nfet_11 (.G(decoder_1_out_0), .D(nfet_11_d), .S(1'b0));
  Fuse fuse_9 (.A(nfet_11_d), .B(fuse_9_b));
  NFET nfet_12 (.G(decoder_1_out_1), .D(nfet_12_d), .S(1'b0));
  Fuse #(.Blown("true")) fuse_10 (.A(nfet_12_d), .B(fuse_9_b));
  NFET nfet_13 (.G(decoder_1_out_2), .D(nfet_13_d), .S(1'b0));
  Fuse fuse_11 (.A(nfet_13_d), .B(fuse_9_b));
  NFET nfet_14 (.G(decoder_1_out_3), .D(nfet_14_d), .S(1'b0));
  Fuse fuse_12 (.A(nfet_14_d), .B(fuse_9_b));
  PullUp pullup_3 (.out(fuse_9_b));
  NFET nfet_15 (.G(decoder_2_out_2), .D(fuse_9_b), .S(nfet_5_s));
  NFET nfet_16 (.G(decoder_1_out_0), .D(nfet_16_d), .S(1'b0));
  Fuse fuse_13 (.A(nfet_16_d), .B(fuse_13_b));
  NFET nfet_17 (.G(decoder_1_out_1), .D(nfet_17_d), .S(1'b0));
  Fuse fuse_14 (.A(nfet_17_d), .B(fuse_13_b));
  NFET nfet_18 (.G(decoder_1_out_2), .D(nfet_18_d), .S(1'b0));
  Fuse fuse_15 (.A(nfet_18_d), .B(fuse_13_b));
  NFET nfet_19 (.G(decoder_1_out_3), .D(nfet_19_d), .S(1'b0));
  Fuse fuse_16 (.A(nfet_19_d), .B(fuse_13_b));
  NFET nfet_20 (.G(decoder_2_out_3), .D(fuse_13_b), .S(nfet_5_s));
  PullUp pullup_4 (.out(fuse_13_b));
  assign Q = CS ? nfet_5_s : 1'bz;  // Driver driver_1

  // Notes on the sheet:
  //   CS: default 1
endmodule

/* Test case:
A_0 A_1 A_2 A_3 Q
 0   0   0   0  0
 0   0   0   1  0
 0   0   1   0  0
 0   0   1   1  0
 0   1   0   0  0
 0   1   0   1  0
 0   1   1   0  1
 0   1   1   1  0
 1   0   0   0  0
 1   0   0   1  1
 1   0   1   0  0
 1   0   1   1  0
 1   1   0   0  0
 1   1   0   1  0
 1   1   1   0  0
 1   1   1   1  0




# transitions
0 0 0 0 0
0 0 0 1 0
0 0 0 0 0
0 0 1 0 0
0 0 0 0 0
0 0 1 1 0
0 0 0 0 0
0 1 0 0 0
0 0 0 0 0
0 1 0 1 0
0 0 0 0 0
0 1 1 0 1
0 0 0 0 0
0 1 1 1 0
0 0 0 0 0
1 0 0 0 0
0 0 0 0 0
1 0 0 1 1
0 0 0 0 0
1 0 1 0 0
0 0 0 0 0
1 0 1 1 0
0 0 0 0 0
1 1 0 0 0
0 0 0 0 0
1 1 0 1 0
0 0 0 0 0
1 1 1 0 0
0 0 0 0 0
1 1 1 1 0
0 0 0 0 0
0 0 0 1 0
0 0 1 0 0
0 0 0 1 0
0 0 1 1 0
0 0 0 1 0
0 1 0 0 0
0 0 0 1 0
0 1 0 1 0
0 0 0 1 0
0 1 1 0 1
0 0 0 1 0
0 1 1 1 0
0 0 0 1 0
1 0 0 0 0
0 0 0 1 0
1 0 0 1 1
0 0 0 1 0
1 0 1 0 0
0 0 0 1 0
1 0 1 1 0
0 0 0 1 0
1 1 0 0 0
0 0 0 1 0
1 1 0 1 0
0 0 0 1 0
1 1 1 0 0
0 0 0 1 0
1 1 1 1 0
0 0 0 1 0
0 0 1 0 0
0 0 1 1 0
0 0 1 0 0
0 1 0 0 0
0 0 1 0 0
0 1 0 1 0
0 0 1 0 0
0 1 1 0 1
0 0 1 0 0
0 1 1 1 0
0 0 1 0 0
1 0 0 0 0
0 0 1 0 0
1 0 0 1 1
0 0 1 0 0
1 0 1 0 0
0 0 1 0 0
1 0 1 1 0
0 0 1 0 0
1 1 0 0 0
0 0 1 0 0
1 1 0 1 0
0 0 1 0 0
1 1 1 0 0
0 0 1 0 0
1 1 1 1 0
0 0 1 0 0
0 0 1 1 0
0 1 0 0 0
0 0 1 1 0
0 1 0 1 0
0 0 1 1 0
0 1 1 0 1
0 0 1 1 0
0 1 1 1 0
0 0 1 1 0
1 0 0 0 0
0 0 1 1 0
1 0 0 1 1
0 0 1 1 0
1 0 1 0 0
0 0 1 1 0
1 0 1 1 0
0 0 1 1 0
1 1 0 0 0
0 0 1 1 0
1 1 0 1 0
0 0 1 1 0
1 1 1 0 0
0 0 1 1 0
1 1 1 1 0
0 0 1 1 0
0 1 0 0 0
0 1 0 1 0
0 1 0 0 0
0 1 1 0 1
0 1 0 0 0
0 1 1 1 0
0 1 0 0 0
1 0 0 0 0
0 1 0 0 0
1 0 0 1 1
0 1 0 0 0
1 0 1 0 0
0 1 0 0 0
1 0 1 1 0
0 1 0 0 0
1 1 0 0 0
0 1 0 0 0
1 1 0 1 0
0 1 0 0 0
1 1 1 0 0
0 1 0 0 0
1 1 1 1 0
0 1 0 0 0
0 1 0 1 0
0 1 1 0 1
0 1 0 1 0
0 1 1 1 0
0 1 0 1 0
1 0 0 0 0
0 1 0 1 0
1 0 0 1 1
0 1 0 1 0
1 0 1 0 0
0 1 0 1 0
1 0 1 1 0
0 1 0 1 0
1 1 0 0 0
0 1 0 1 0
1 1 0 1 0
0 1 0 1 0
1 1 1 0 0
0 1 0 1 0
1 1 1 1 0
0 1 0 1 0
0 1 1 0 1
0 1 1 1 0
0 1 1 0 1
1 0 0 0 0
0 1 1 0 1
1 0 0 1 1
0 1 1 0 1
1 0 1 0 0
0 1 1 0 1
1 0 1 1 0
0 1 1 0 1
1 1 0 0 0
0 1 1 0 1
1 1 0 1 0
0 1 1 0 1
1 1 1 0 0
0 1 1 0 1
1 1 1 1 0
0 1 1 0 1
0 1 1 1 0
1 0 0 0 0
0 1 1 1 0
1 0 0 1 1
0 1 1 1 0
1 0 1 0 0
0 1 1 1 0
1 0 1 1 0
0 1 1 1 0
1 1 0 0 0
0 1 1 1 0
1 1 0 1 0
0 1 1 1 0
1 1 1 0 0
0 1 1 1 0
1 1 1 1 0
0 1 1 1 0
1 0 0 0 0
1 0 0 1 1
1 0 0 0 0
1 0 1 0 0
1 0 0 0 0
1 0 1 1 0
1 0 0 0 0
1 1 0 0 0
1 0 0 0 0
1 1 0 1 0
1 0 0 0 0
1 1 1 0 0
1 0 0 0 0
1 1 1 1 0
1 0 0 0 0
1 0 0 1 1
1 0 1 0 0
1 0 0 1 1
1 0 1 1 0
1 0 0 1 1
1 1 0 0 0
1 0 0 1 1
1 1 0 1 0
1 0 0 1 1
1 1 1 0 0
1 0 0 1 1
1 1 1 1 0
1 0 0 1 1
1 0 1 0 0
1 0 1 1 0
1 0 1 0 0
1 1 0 0 0
1 0 1 0 0
1 1 0 1 0
1 0 1 0 0
1 1 1 0 0
1 0 1 0 0
1 1 1 1 0
1 0 1 0 0
1 0 1 1 0
1 1 0 0 0
1 0 1 1 0
1 1 0 1 0
1 0 1 1 0
1 1 1 0 0
1 0 1 1 0
1 1 1 1 0
1 0 1 1 0
1 1 0 0 0
1 1 0 1 0
1 1 0 0 0
1 1 1 0 0
1 1 0 0 0
1 1 1 1 0
1 1 0 0 0
1 1 0 1 0
1 1 1 0 0
1 1 0 1 0
1 1 1 1 0
1 1 0 1 0
1 1 1 0 0
1 1 1 1 0
1 1 1 0 0
*/
