// Digital circuit RAM 2P.dig as structural Verilog
module RAM_2P (
  input  [3:0] A,
  input  sel,
  input  CS,
  input  WE,
  output [7:0] Do
);

  RAMSinglePort #(.AddrBits(4), .Bits(8)) ramsingleport_1 (.A(A), .str(CS), .C(WE), .ld(sel), .D(Do));
endmodule
