// Digital circuit ROM&RAM.dig as structural Verilog
module ROM_RAM (
  input  [9:0] Addr,
  input  [7:0] Din,
  input  WE,
  input  Clk,
  output [7:0] Dout
);

  wire and_1_out, and_2_out, not_1_out;
  wire [7:0] ramdualport_1_d, rom_d;

  and and_1 (and_1_out, WE, not_1_out);
  and and_2 (and_2_out, Addr[7], Addr[8], Addr[9]);
  not not_1 (not_1_out, Addr[9]);
  ROM #(.AddrBits(7), .Bits(8)) rom (.A(Addr[6:0]), .sel(and_2_out), .D(rom_d));
  RAMDualPort #(.AddrBits(9), .Bits(8)) ramdualport_1 (
    .A(Addr[8:0]), .Din(Din), .str(and_1_out), .C(Clk), .ld(not_1_out), .D(ramdualport_1_d));
  Multiplexer #(.Bits(8)) multiplexer_1 (.sel(and_2_out), .in_0(ramdualport_1_d), .in_1(rom_d), .out(Dout));

  // Notes on the sheet:
  //   Addr: A
  //   contents of rom (hex, n*v repeats v):
  //   f,0,0,0,0,0,f,0,0,0,0,0,0,0,0,0,0,0,0,0,0,0,0,0,0,0,0,0,0,0,0,1
endmodule
