// Digital circuit ROMs.dig as structural Verilog
module ROMs (
  input  [1:0] A,
  input  CS,
  input  [4:0] Addr,
  output [7:0] D,
  output [7:0] Data
);

  wire [7:0] ROM0_d, ROM1_d, ROM2_d, ROM3_d;

  ROM #(.Bits(4)) ROM_L (.A(A), .sel(CS), .D(D[3:0]));
  ROM #(.Bits(4)) ROM_H (.A(A), .sel(CS), .D(D[7:4]));
  // Probe on D[3:0]
  // Probe on D[7:4]
  ROM #(.AddrBits(3), .Bits(8), .Addr_Bits(3)) ROM0 (.A(Addr[2:0]), .sel(1'b1), .D(ROM0_d));
  ROM #(.AddrBits(3), .Bits(8), .Addr_Bits(3)) ROM1 (.A(Addr[2:0]), .sel(1'b1), .D(ROM1_d));
  ROM #(.AddrBits(3), .Bits(8), .Addr_Bits(3)) ROM2 (.A(Addr[2:0]), .sel(1'b1), .D(ROM2_d));
  ROM #(.AddrBits(3), .Bits(8), .Addr_Bits(3)) ROM3 (.A(Addr[2:0]), .sel(1'b1), .D(ROM3_d));
  Multiplexer #(.Selector_Bits(2), .Bits(8)) multiplexer_1 (
    .sel(Addr[4:3]), .in_0(ROM0_d), .in_1(ROM1_d), .in_2(ROM2_d), .in_3(ROM3_d), .out(Data));

  // Notes on the sheet:
  //   contents of ROM_L (hex, n*v repeats v):
  //   1,0,0,0,0,0,f,0,0,0,0,0,0,0,0,0,0,0,0,0,0,0,0,0,0,0,0,0,0,0,0,1
  //   contents of ROM_H (hex, n*v repeats v):
  //   f,0,0,0,0,0,f,0,0,0,0,0,0,0,0,0,0,0,0,0,0,0,0,0,0,0,0,0,0,0,0,1
  //   contents of ROM0 (hex, n*v repeats v):
  //   44,69,65,73,20,69,73,74
  //   contents of ROM1 (hex, n*v repeats v):
  //   20,65,69,6e,20,6c,61,6e
  //   contents of ROM2 (hex, n*v repeats v):
  //   67,65,72,20,54,65,73,74
  //   contents of ROM3 (hex, n*v repeats v):
  //   74,65,78,74,2e,20,20,20
endmodule

/* Test case BitEx:
CS  A   D
1   0   0xF1  
1   1   0    
1   2   0   
1   3   0  
0   0    Z    
0   1    Z    
0   2    Z    
0   3    Z    

 
*/

/* Test case AddrEx:
Addr   Data
  0    0x44
  1    0x69
  2    0x65
  3    0x73
  4    0x20
  5    0x69
  6    0x73
  7    0x74

  8    0x20
  9    0x65
 10    0x69
 11    0x6E
 12    0x20
 13    0x6C
 14    0x61
 15    0x6E

 16    0x67
 17    0x65
 18    0x72
 19    0x20
 20    0x54
 21    0x65
 22    0x73
 23    0x74

 24    0x74
 25    0x65
 26    0x78
 27    0x74
 28    0x2E
 29    0x20
 30    0x20
 31    0x20
*/
