// Digital circuit memory.dig as structural Verilog
module memory (
  input  we,
  input  [1:0] Rw,
  input  clock,
  input  [1:0] Ra,
  input  [7:0] Data,
  input  [1:0] Rb,
  input  [7:0] A,
  input  CS,
  input  [7:0] Addr,
  input  [7:0] Din,
  input  str,
  input  C,
  input  Id,
  input  clk,
  input  OE,
  input  [1:0] Addr1,
  input  [7:0] D,
  input  W,
  input  [1:0] Addr2,
  output [7:0] Da,
  output [7:0] Db,
  output [7:0] Do,
  output [7:0] Dout,
  output [7:0] D1,
  output [7:0] D2
);

  ROM #(.AddrBits(8), .Bits(8)) rom (.A(A), .sel(CS), .D(Do));
  RegisterFile #(.Bits(8)) registerfile_1 (.Din(Data), .we(we), .Rw(Rw), .C(clock), .Ra(Ra), .Rb(Rb), .Da(Da), .Db(Db));
  RAMDualPort #(.AddrBits(8), .Bits(8)) ramdualport_1 (.A(Addr), .Din(Din), .str(str), .C(C), .ld(Id), .D(Dout));
  RAMDualAccess #(.isProgramMemory("true"), .Bits(8)) ramdualaccess_1 (
    .str(W), .C(clk), .ld(OE), .A1(Addr1), .Din1(D), .A2(Addr2), .D1(D1), .D2(D2));

  // Notes on the sheet:
  //   Addr: A
  //   contents of rom (hex, n*v repeats v):
  //   ff,0,0,0,0,0,f,0,0,0,0,0,0,0,0,0,0,0,0,0,0,0,0,0,0,0,0,0,0,0,0,1
endmodule
