// Digital circuit FIFO.dig as structural Verilog
module FIFO (
  input  W_EN,
  input  [7:0] Data,
  input  CLK_W,
  input  CLK_R,
  input  R_EN,
  output [7:0] Out,
  output full,
  output empty,
  output [7:0] D_out
);

  wire comparator_1_eq, d_ff_2_q, d_ff_3_q, decoder_1_out_0, decoder_1_out_1, decoder_1_out_2,
       decoder_1_out_3, I_R, I_W, not_1_out, r0, r1, r2, r3, Read_P_ovf, Write_P_ovf, xor_1_out;
  wire [1:0] d_ff_1_q, d_ff_4_q, rp, wp;
  wire [7:0] multiplexer_1_out, Q_0_q, Q_1_q, Q_2_q, Q_3_q, registerfile_1_da;

  xor xor_1 (xor_1_out, I_R, I_W);
  Counter #(.Bits(2)) Read_P (.en(R_EN), .C(CLK_R), .clr(1'b0), .out(rp), .ovf(Read_P_ovf));
  JK_FF_AS jk_ff_as_1 (.Set(1'b0), .J(Read_P_ovf), .C(CLK_R), .K(Read_P_ovf), .Clr(1'b0), .Q(I_R));  // open: nQ
  Comparator #(.Bits(2)) comparator_1 (.a(wp), .b(rp), .eq(comparator_1_eq));  // open: gt, lt
  and and_1 (full, comparator_1_eq, xor_1_out);
  and and_2 (empty, comparator_1_eq, not_1_out);
  not not_1 (not_1_out, xor_1_out);
  Counter #(.Bits(2)) Write_P (.en(W_EN), .C(CLK_W), .clr(1'b0), .out(wp), .ovf(Write_P_ovf));
  JK_FF_AS jk_ff_as_2 (.Set(1'b0), .J(Write_P_ovf), .C(CLK_W), .K(Write_P_ovf), .Clr(1'b0), .Q(I_W));  // open: nQ
  Decoder #(.Selector_Bits(2)) decoder_1 (
    .sel(wp), .out_0(decoder_1_out_0), .out_1(decoder_1_out_1), .out_2(decoder_1_out_2),
    .out_3(decoder_1_out_3));
  RegisterFile #(.Bits(8)) registerfile_1 (
    .Din(Data), .we(W_EN), .Rw(wp), .C(CLK_W), .Ra(d_ff_1_q), .Rb(2'b00), .Da(registerfile_1_da));  // open: Db
  D_FF #(.Bits(2)) d_ff_1 (.D(rp), .C(CLK_R), .Q(d_ff_1_q));  // open: nQ
  // Probe on wp
  and and_3 (r0, W_EN, decoder_1_out_0);
  and and_4 (r1, W_EN, decoder_1_out_1);
  and and_5 (r2, W_EN, decoder_1_out_2);
  and and_6 (r3, W_EN, decoder_1_out_3);
  assign D_out = d_ff_2_q ? registerfile_1_da : 8'bz;  // Driver driver_1
  D_FF d_ff_2 (.D(R_EN), .C(CLK_R), .Q(d_ff_2_q));  // open: nQ
  Register #(.Bits(8)) Q_0 (.D(Data), .C(CLK_W), .en(r0), .Q(Q_0_q));
  Register #(.Bits(8)) Q_1 (.D(Data), .C(CLK_W), .en(r1), .Q(Q_1_q));
  Register #(.Bits(8)) Q_2 (.D(Data), .C(CLK_W), .en(r2), .Q(Q_2_q));
  Register #(.Bits(8)) Q_3 (.D(Data), .C(CLK_W), .en(r3), .Q(Q_3_q));
  // Probe on Q_0_q
  // Probe on Q_1_q
  // Probe on Q_2_q
  // Probe on Q_3_q
  D_FF d_ff_3 (.D(R_EN), .C(CLK_R), .Q(d_ff_3_q));  // open: nQ
  Multiplexer #(.Selector_Bits(2), .Bits(8)) multiplexer_1 (
    .sel(d_ff_4_q), .in_0(Q_0_q), .in_1(Q_1_q), .in_2(Q_2_q), .in_3(Q_3_q), .out(multiplexer_1_out));
  // Probe on rp
  D_FF #(.Bits(2)) d_ff_4 (.D(rp), .C(CLK_R), .Q(d_ff_4_q));  // open: nQ
  assign Out = d_ff_3_q ? multiplexer_1_out : 8'bz;  // Driver driver_2

  // Other names for the same wires on the sheet: Re = R_EN; We = W_EN
endmodule
