// Digital circuit associative map.dig as structural Verilog
module associative_map (
  input  [7:0] Addr,
  input  EN,
  input  Ready,
  input  CLK,
  output [7:0] Data,
  output [31:0] Bulkdata
);

  wire and_2_out, and_3_out, and_4_out, and_5_out, and_6_out, and_7_out, and_8_out, and_9_out, and_10_out,
       comparator_1_eq, comparator_2_eq, comparator_3_eq, comparator_4_eq, comparator_5_eq, comparator_6_eq,
       comparator_7_eq, comparator_8_eq, comparator_9_lt, comparator_10_lt, comparator_11_lt,
       comparator_12_lt, comparator_13_lt, comparator_14_lt, comparator_15_lt, h0, h1, h2, h3, h4, h5, h6,
       h7, hit, miss, not_1_out, not_2_out, not_3_out, not_4_out, not_5_out, not_6_out, not_7_out, not_8_out,
       nRd, OF, priorityencoder_1_any, V0, V1, V2, V3, V4, V5, V6, V7, W0, W1, W2, W3, W4, W5, W6, W7, We;
  wire [1:0] counter_1_out, multiplexer_3_out;
  wire [2:0] C_hit, L_hit, multiplexer_1_out, multiplexer_7_out, multiplexer_9_out, multiplexer_11_out,
       multiplexer_14_out, multiplexer_16_out, multiplexer_18_out, priorityencoder_1_num, W_hit;
  wire [4:2] multiplexer_4_out;
  wire [5:0] D0, D1, D2, D3, D4, D5, D6, D7, L0, L1, L2, L3, L4, L5, L6, L7;
  wire [7:0] addr_t, C0, C1, C2, C3, C4, C5, C6, C7, cache_d, data_t, multiplexer_2_out, multiplexer_5_out,
       multiplexer_8_out, multiplexer_10_out, multiplexer_12_out, multiplexer_15_out, multiplexer_17_out,
       multiplexer_19_out;
  wire [31:0] driver_1_out, rom_1_d;

  not not_1 (not_1_out, V0);
  not not_2 (not_2_out, V1);
  not not_3 (not_3_out, V2);
  not not_4 (not_4_out, V3);
  not not_5 (not_5_out, V4);
  not not_6 (not_6_out, V5);
  not not_7 (not_7_out, V6);
  not not_8 (not_8_out, V7);
  Register #(.Bits(8)) A (.D(Addr), .C(CLK), .en(1'b1), .Q(addr_t));
  D_FF #(.Bits(3)) d_ff_1 (.D(multiplexer_1_out), .C(Ready), .Q(W_hit));  // open: nQ
  PriorityEncoder #(.Selector_Bits(3)) priorityencoder_1 (
    .in0(not_1_out), .in1(not_2_out), .in2(not_3_out), .in3(not_4_out), .in4(not_5_out), .in5(not_6_out),
    .in6(not_7_out), .in7(not_8_out), .num(priorityencoder_1_num), .any(priorityencoder_1_any));
  // Probe on addr_t
  assign driver_1_out = Ready ? Bulkdata : 32'bz;  // Driver driver_1
  Multiplexer #(.Bits(3)) multiplexer_1 (
    .sel(priorityencoder_1_any), .in_0(C_hit), .in_1(priorityencoder_1_num), .out(multiplexer_1_out));
  // Probe on priorityencoder_1_num
  ROM #(.AddrBits(6), .Bits(32)) rom_1 (.A(addr_t[7:2]), .sel(EN), .D(rom_1_d));
  assign Data = ~miss ? data_t : 8'bz;  // DriverInvSel driverinvsel_1
  and and_1 (nRd, EN, ~Ready);  // And
  Counter #(.Bits(2)) counter_1 (.en(We), .C(CLK), .clr(1'b0), .out(counter_1_out), .ovf(OF));
  assign Bulkdata = Ready ? rom_1_d : 32'bz;  // Driver driver_2
  LED u_MISS (.in(miss));
  Multiplexer #(.Selector_Bits(2), .Bits(8)) multiplexer_2 (
    .sel(counter_1_out), .in_0(driver_1_out[7:0]), .in_1(driver_1_out[15:8]), .in_2(driver_1_out[23:16]),
    .in_3(driver_1_out[31:24]), .out(multiplexer_2_out));
  // Probe on counter_1_out
  Demultiplexer #(.Selector_Bits(3)) demultiplexer_1 (
    .sel(L_hit), .in(hit), .out_0(h0), .out_1(h1), .out_2(h2), .out_3(h3), .out_4(h4), .out_5(h5),
    .out_6(h6), .out_7(h7));
  // Probe on multiplexer_2_out
  Multiplexer #(.Bits(2)) multiplexer_3 (.sel(We), .in_0(addr_t[1:0]), .in_1(counter_1_out), .out(multiplexer_3_out));
  Multiplexer #(.Bits(3)) multiplexer_4 (.sel(We), .in_0(L_hit), .in_1(W_hit), .out(multiplexer_4_out));
  // Probe on {multiplexer_4_out, multiplexer_3_out}
  Demultiplexer #(.Selector_Bits(3)) demultiplexer_2 (
    .sel(W_hit), .in(We), .out_0(W0), .out_1(W1), .out_2(W2), .out_3(W3), .out_4(W4), .out_5(W5), .out_6(W6),
    .out_7(W7));
  Multiplexer #(.Selector_Bits(2), .Bits(8)) multiplexer_5 (
    .sel(addr_t[1:0]), .in_0(driver_1_out[7:0]), .in_1(driver_1_out[15:8]), .in_2(driver_1_out[23:16]),
    .in_3(driver_1_out[31:24]), .out(multiplexer_5_out));
  RAMDualPort #(.AddrBits(5), .Bits(8)) cache (
    .A({multiplexer_4_out, multiplexer_3_out}), .Din(multiplexer_2_out), .str(We), .C(CLK), .ld(and_2_out),
    .D(cache_d));
  and and_2 (and_2_out, hit, EN);
  Counter #(.Bits(8)) u_C0 (.en(nRd), .C(CLK), .clr(h0), .out(C0));  // open: ovf
  Register #(.Bits(6)) u_L0 (.D(D0), .C(CLK), .en(W0), .Q(L0));
  Register u_v0 (.D(1'b1), .C(CLK), .en(W0), .Q(V0));
  Multiplexer #(.Bits(8)) multiplexer_6 (.sel(We), .in_0(cache_d), .in_1(multiplexer_5_out), .out(data_t));
  // Probe on addr_t[7:2]
  Demultiplexer #(.Selector_Bits(3), .Bits(6)) demultiplexer_3 (
    .sel(W_hit), .in(addr_t[7:2]), .out_0(D0), .out_1(D1), .out_2(D2), .out_3(D3), .out_4(D4), .out_5(D5),
    .out_6(D6), .out_7(D7));
  // Probe on C0
  // Probe on L0
  // Probe on W_hit
  Counter #(.Bits(8)) u_C1 (.en(nRd), .C(CLK), .clr(h1), .out(C1));  // open: ovf
  Register #(.Bits(6)) u_L1 (.D(D1), .C(CLK), .en(W1), .Q(L1));
  Register u_v1 (.D(1'b1), .C(CLK), .en(W1), .Q(V1));
  // Probe on addr_t[1:0]
  // Probe on C1
  // Probe on L1
  Comparator #(.Bits(6)) comparator_1 (.a(addr_t[7:2]), .b(L0), .eq(comparator_1_eq));  // open: gt, lt
  Comparator #(.Bits(6)) comparator_2 (.a(addr_t[7:2]), .b(L1), .eq(comparator_2_eq));  // open: gt, lt
  Comparator #(.Bits(6)) comparator_3 (.a(addr_t[7:2]), .b(L2), .eq(comparator_3_eq));  // open: gt, lt
  Comparator #(.Bits(6)) comparator_4 (.a(addr_t[7:2]), .b(L3), .eq(comparator_4_eq));  // open: gt, lt
  Comparator #(.Bits(6)) comparator_5 (.a(addr_t[7:2]), .b(L4), .eq(comparator_5_eq));  // open: gt, lt
  Comparator #(.Bits(6)) comparator_6 (.a(addr_t[7:2]), .b(L5), .eq(comparator_6_eq));  // open: gt, lt
  Comparator #(.Bits(6)) comparator_7 (.a(addr_t[7:2]), .b(L6), .eq(comparator_7_eq));  // open: gt, lt
  Comparator #(.Bits(6)) comparator_8 (.a(addr_t[7:2]), .b(L7), .eq(comparator_8_eq));  // open: gt, lt
  and and_3 (and_3_out, comparator_1_eq, V0);
  and and_4 (and_4_out, comparator_2_eq, V1);
  and and_5 (and_5_out, comparator_3_eq, V2);
  and and_6 (and_6_out, comparator_4_eq, V3);
  and and_7 (and_7_out, comparator_5_eq, V4);
  and and_8 (and_8_out, comparator_6_eq, V5);
  and and_9 (and_9_out, comparator_7_eq, V6);
  and and_10 (and_10_out, comparator_8_eq, V7);
  Counter #(.Bits(8)) u_C2 (.en(nRd), .C(CLK), .clr(h2), .out(C2));  // open: ovf
  Register #(.Bits(6)) u_L2 (.D(D2), .C(CLK), .en(W2), .Q(L2));
  Register u_v2 (.D(1'b1), .C(CLK), .en(W2), .Q(V2));
  // Probe on C2
  // Probe on L2
  PriorityEncoder #(.Selector_Bits(3)) priorityencoder_2 (
    .in0(and_3_out), .in1(and_4_out), .in2(and_5_out), .in3(and_6_out), .in4(and_7_out), .in5(and_8_out),
    .in6(and_9_out), .in7(and_10_out), .num(L_hit), .any(hit));
  Counter #(.Bits(8)) u_C3 (.en(nRd), .C(CLK), .clr(h3), .out(C3));  // open: ovf
  Register #(.Bits(6)) u_L3 (.D(D3), .C(CLK), .en(W3), .Q(L3));
  Register u_v3 (.D(1'b1), .C(CLK), .en(W3), .Q(V3));
  // Probe on L_hit
  // Probe on C3
  // Probe on L3
  and and_11 (miss, ~hit, EN);  // And
  and and_12 (We, EN, Ready);
  Counter #(.Bits(8)) u_C4 (.en(nRd), .C(CLK), .clr(h4), .out(C4));  // open: ovf
  Register #(.Bits(6)) u_L4 (.D(D4), .C(CLK), .en(W4), .Q(L4));
  Register u_v4 (.D(1'b1), .C(CLK), .en(W4), .Q(V4));
  // Probe on C4
  // Probe on L4
  Multiplexer #(.Bits(3)) multiplexer_7 (.sel(comparator_9_lt), .in_0(3'b000), .in_1(3'b001), .out(multiplexer_7_out));
  Comparator #(.Bits(8)) comparator_9 (.a(C0), .b(C1), .lt(comparator_9_lt));  // open: gt, eq
  Multiplexer #(.Bits(8)) multiplexer_8 (.sel(comparator_9_lt), .in_0(C0), .in_1(C1), .out(multiplexer_8_out));
  Comparator #(.Bits(8)) comparator_10 (.a(C2), .b(C3), .lt(comparator_10_lt));  // open: gt, eq
  Counter #(.Bits(8)) u_C5 (.en(nRd), .C(CLK), .clr(h5), .out(C5));  // open: ovf
  Register #(.Bits(6)) u_L5 (.D(D5), .C(CLK), .en(W5), .Q(L5));
  Register u_v5 (.D(1'b1), .C(CLK), .en(W5), .Q(V5));
  Multiplexer #(.Bits(3)) multiplexer_9 (.sel(comparator_10_lt), .in_0(3'b010), .in_1(3'b011), .out(multiplexer_9_out));
  Multiplexer #(.Bits(8)) multiplexer_10 (.sel(comparator_10_lt), .in_0(C2), .in_1(C3), .out(multiplexer_10_out));
  // Probe on C5
  // Probe on L5
  Multiplexer #(.Bits(3)) multiplexer_11 (
    .sel(comparator_11_lt), .in_0(multiplexer_7_out), .in_1(multiplexer_9_out), .out(multiplexer_11_out));
  Comparator #(.Bits(8)) comparator_11 (
    .a(multiplexer_8_out), .b(multiplexer_10_out), .lt(comparator_11_lt));  // open: gt, eq
  Multiplexer #(.Bits(8)) multiplexer_12 (
    .sel(comparator_11_lt), .in_0(multiplexer_8_out), .in_1(multiplexer_10_out), .out(multiplexer_12_out));
  Counter #(.Bits(8)) u_C6 (.en(nRd), .C(CLK), .clr(h6), .out(C6));  // open: ovf
  Register #(.Bits(6)) u_L6 (.D(D6), .C(CLK), .en(W6), .Q(L6));
  Register u_v6 (.D(1'b1), .C(CLK), .en(W6), .Q(V6));
  Multiplexer #(.Bits(3)) multiplexer_13 (
    .sel(comparator_12_lt), .in_0(multiplexer_11_out), .in_1(multiplexer_18_out), .out(C_hit));
  Comparator #(.Bits(8)) comparator_12 (
    .a(multiplexer_12_out), .b(multiplexer_19_out), .lt(comparator_12_lt));  // open: gt, eq
  // Probe on C6
  // Probe on L6
  Multiplexer #(.Bits(3)) multiplexer_14 (
    .sel(comparator_13_lt), .in_0(3'b100), .in_1(3'b101), .out(multiplexer_14_out));
  Comparator #(.Bits(8)) comparator_13 (.a(C4), .b(C5), .lt(comparator_13_lt));  // open: gt, eq
  Multiplexer #(.Bits(8)) multiplexer_15 (.sel(comparator_13_lt), .in_0(C4), .in_1(C5), .out(multiplexer_15_out));
  Multiplexer #(.Bits(3)) multiplexer_16 (
    .sel(comparator_14_lt), .in_0(3'b110), .in_1(3'b111), .out(multiplexer_16_out));
  Comparator #(.Bits(8)) comparator_14 (.a(C6), .b(C7), .lt(comparator_14_lt));  // open: gt, eq
  Multiplexer #(.Bits(8)) multiplexer_17 (.sel(comparator_14_lt), .in_0(C6), .in_1(C7), .out(multiplexer_17_out));
  Counter #(.Bits(8)) u_C7 (.en(nRd), .C(CLK), .clr(h7), .out(C7));  // open: ovf
  Register #(.Bits(6)) u_L7 (.D(D7), .C(CLK), .en(W7), .Q(L7));
  Register u_v7 (.D(1'b1), .C(CLK), .en(W7), .Q(V7));
  Multiplexer #(.Bits(3)) multiplexer_18 (
    .sel(comparator_15_lt), .in_0(multiplexer_14_out), .in_1(multiplexer_16_out), .out(multiplexer_18_out));
  Comparator #(.Bits(8)) comparator_15 (
    .a(multiplexer_15_out), .b(multiplexer_17_out), .lt(comparator_15_lt));  // open: gt, eq
  Multiplexer #(.Bits(8)) multiplexer_19 (
    .sel(comparator_15_lt), .in_0(multiplexer_15_out), .in_1(multiplexer_17_out), .out(multiplexer_19_out));
  // Probe on C7
  // Probe on L7

  // Other names for the same wires on the sheet: Rd = Ready

  // Notes on the sheet:
  //   存储器电路
  //   contents of rom_1 (hex, n*v repeats v):
  //   10f9f3e7,fffff0b7,400093,40016f,158513,feb50fe3,fff20193,318233,308023,309023,30a023,
  //   40a223,402383,800403,801403,804403,805403,802403,ff3a413,ffe3b413,fff44413,247493,
  //   249513,1f4d593,25d593,40125613,40460633,c616b3,c42733,c43733,864733,e6d7b3,40f75733,
  //   d77733,c76833,200713,11d873,11d873,810f3,710f3,a973,25973,1039f3
  //   Associate Map
endmodule
