// Digital circuit bit stack.dig as structural Verilog
module bit_stack (
  input  push__pop,
  input  D,
  output S
);

  wire clock_out, d_ff_1_q;
  wire [3:0] multiplexer_2_out;
  wire [4:0] barrelshifter_1_out, d_ff_2_q;
  wire [4:4] multiplexer_1_out;

  Button clock (.out(clock_out));
  Multiplexer multiplexer_1 (.sel(push__pop), .in_0(barrelshifter_1_out[4]), .in_1(D), .out(multiplexer_1_out[4]));
  D_FF d_ff_1 (.D(push__pop), .C(clock_out), .Q(d_ff_1_q));  // open: nQ
  // Probe on {multiplexer_1_out[4], barrelshifter_1_out[3:0]}
  D_FF #(.Bits(5)) d_ff_2 (
    .D({multiplexer_1_out[4], barrelshifter_1_out[3:0]}), .C(clock_out), .Q(d_ff_2_q));  // open: nQ
  // Probe on d_ff_2_q
  Multiplexer #(.Bits(4)) multiplexer_2 (.sel(d_ff_1_q), .in_0(4'b1111), .in_1(4'b0001), .out(multiplexer_2_out));
  BarrelShifter #(.Bits(5), .barrelSigned("true"), .direction("right")) barrelshifter_1 (
    .in(d_ff_2_q), .shift(multiplexer_2_out), .out(barrelshifter_1_out));
  assign S = ~d_ff_1_q ? barrelshifter_1_out[4] : 1'bz;  // DriverInvSel driverinvsel_1
  // Probe on barrelshifter_1_out
  // Probe stack on barrelshifter_1_out[3:0]

  // Notes on the sheet:
  //   5 bit
endmodule
