// Digital circuit direct map.dig as structural Verilog
module direct_map (
  input  [7:0] Addr,
  input  EN,
  input  Ready,
  input  CLK,
  output [7:0] Data,
  output [31:0] Bulkdata
);

  wire and_1_out, comparator_1_eq, hit, miss, multiplexer_6_out, V0, V1, V2, V3, V4, V5, V6, V7, W0, W1, W2,
       W3, W4, W5, W6, W7, We;
  wire [1:0] counter_1_out, multiplexer_2_out;
  wire [2:0] D0, D1, D2, D3, D4, D5, D6, D7, L0, L1, L2, L3, L4, L5, L6, L7, multiplexer_5_out;
  wire [7:0] addr_t, cache_d, data_t, multiplexer_1_out, multiplexer_3_out;
  wire [31:0] rom_1_d;

  Register #(.Bits(8)) A (.D(Addr), .C(CLK), .en(~Ready), .Q(addr_t));
  Counter #(.Bits(2)) counter_1 (.en(We), .C(CLK), .clr(1'b0), .out(counter_1_out));  // open: ovf
  // Probe on addr_t
  Multiplexer #(.Selector_Bits(2), .Bits(8)) multiplexer_1 (
    .sel(counter_1_out), .in_0(Bulkdata[7:0]), .in_1(Bulkdata[15:8]), .in_2(Bulkdata[23:16]),
    .in_3(Bulkdata[31:24]), .out(multiplexer_1_out));
  // Probe on counter_1_out
  ROM #(.AddrBits(6), .Bits(32)) rom_1 (.A(addr_t[7:2]), .sel(EN), .D(rom_1_d));
  // Probe on multiplexer_1_out
  Multiplexer #(.Bits(2)) multiplexer_2 (.sel(We), .in_0(addr_t[1:0]), .in_1(counter_1_out), .out(multiplexer_2_out));
  assign Bulkdata = Ready ? rom_1_d : 32'bz;  // Driver driver_1
  LED u_MISS (.in(miss));
  assign Data = ~miss ? data_t : 8'bz;  // DriverInvSel driverinvsel_1
  // Probe on addr_t[1:0]
  // Probe on {addr_t[4:2], multiplexer_2_out}
  // Probe on addr_t[4:2]
  Multiplexer #(.Selector_Bits(2), .Bits(8)) multiplexer_3 (
    .sel(addr_t[1:0]), .in_0(Bulkdata[7:0]), .in_1(Bulkdata[15:8]), .in_2(Bulkdata[23:16]),
    .in_3(Bulkdata[31:24]), .out(multiplexer_3_out));
  RAMDualPort #(.AddrBits(5), .Bits(8)) cache (
    .A({addr_t[4:2], multiplexer_2_out}), .Din(multiplexer_1_out), .str(We), .C(CLK), .ld(and_1_out),
    .D(cache_d));
  and and_1 (and_1_out, hit, EN);
  Multiplexer #(.Bits(8)) multiplexer_4 (.sel(We), .in_0(cache_d), .in_1(multiplexer_3_out), .out(data_t));
  and and_2 (We, EN, Ready);
  Register u_v0 (.D(1'b1), .C(CLK), .en(W0), .Q(V0));
  Register u_v4 (.D(1'b1), .C(CLK), .en(W4), .Q(V4));
  Register #(.Bits(3)) u_L0 (.D(D0), .C(CLK), .en(W0), .Q(L0));
  Register #(.Bits(3)) u_L4 (.D(D4), .C(CLK), .en(W4), .Q(L4));
  // Probe on L0
  // Probe on L4
  Register #(.Bits(3)) u_L1 (.D(D1), .C(CLK), .en(W1), .Q(L1));
  Register #(.Bits(3)) u_L5 (.D(D5), .C(CLK), .en(W5), .Q(L5));
  Demultiplexer #(.Selector_Bits(3), .Bits(3)) demultiplexer_1 (
    .sel(addr_t[4:2]), .in(addr_t[7:5]), .out_0(D0), .out_1(D1), .out_2(D2), .out_3(D3), .out_4(D4),
    .out_5(D5), .out_6(D6), .out_7(D7));
  Demultiplexer #(.Selector_Bits(3)) demultiplexer_2 (
    .sel(addr_t[4:2]), .in(We), .out_0(W0), .out_1(W1), .out_2(W2), .out_3(W3), .out_4(W4), .out_5(W5),
    .out_6(W6), .out_7(W7));
  Register u_v1 (.D(1'b1), .C(CLK), .en(W1), .Q(V1));
  Register u_v5 (.D(1'b1), .C(CLK), .en(W5), .Q(V5));
  // Probe on L1
  // Probe on L5
  Register u_v2 (.D(1'b1), .C(CLK), .en(W2), .Q(V2));
  Register u_v6 (.D(1'b1), .C(CLK), .en(W6), .Q(V6));
  Register #(.Bits(3)) u_L2 (.D(D2), .C(CLK), .en(W2), .Q(L2));
  Register #(.Bits(3)) u_L6 (.D(D6), .C(CLK), .en(W6), .Q(L6));
  Multiplexer #(.Selector_Bits(3), .Bits(3)) multiplexer_5 (
    .sel(addr_t[4:2]), .in_0(L0), .in_1(L1), .in_2(L2), .in_3(L3), .in_4(L4), .in_5(L5), .in_6(L6),
    .in_7(L7), .out(multiplexer_5_out));
  // Probe on multiplexer_5_out
  // Probe on addr_t[4:2]
  Multiplexer #(.Selector_Bits(3)) multiplexer_6 (
    .sel(addr_t[4:2]), .in_0(V0), .in_1(V1), .in_2(V2), .in_3(V3), .in_4(V4), .in_5(V5), .in_6(V6),
    .in_7(V7), .out(multiplexer_6_out));
  // Probe on L2
  // Probe on L6
  Comparator #(.Bits(3)) comparator_1 (.a(multiplexer_5_out), .b(addr_t[7:5]), .eq(comparator_1_eq));  // open: gt, lt
  // Probe on addr_t[7:5]
  and and_3 (hit, comparator_1_eq, multiplexer_6_out);
  Register u_v3 (.D(1'b1), .C(CLK), .en(W3), .Q(V3));
  Register u_v7 (.D(1'b1), .C(CLK), .en(W7), .Q(V7));
  Register #(.Bits(3)) u_L3 (.D(D3), .C(CLK), .en(W3), .Q(L3));
  Register #(.Bits(3)) u_L7 (.D(D7), .C(CLK), .en(W7), .Q(L7));
  and and_4 (miss, ~hit, EN);  // And
  // Probe on L3
  // Probe on L7

  // Other names for the same wires on the sheet: Rd = Ready

  // Notes on the sheet:
  //   存储器电路
  //   contents of rom_1 (hex, n*v repeats v):
  //   10f9f3e7,fffff0b7,400093,40016f,158513,feb50fe3,fff20193,318233,308023,309023,30a023,
  //   40a223,402383,800403,801403,804403,805403,802403,ff3a413,ffe3b413,fff44413,247493,
  //   249513,1f4d593,25d593,40125613,40460633,c616b3,c42733,c43733,864733,e6d7b3,40f75733,
  //   d77733,c76833,200713,11d873,11d873,810f3,710f3,a973,25973,1039f3
  //   Direct Map
endmodule
