// Digital circuit queue.dig as structural Verilog
module queue (
  input  Enq__Deq,
  input  En,
  input  [7:0] Data,
  input  CLK,
  output [7:0] D_out,
  output [7:0] Out
);

  wire a0, a1, a2, a3, d_ff_2_q, d_ff_3_q, driver_1_out, driver_2_out, driver_3_out, not_1_out, not_2_out,
       not_3_out, r0, r1, r2, r3;
  wire [1:0] d_ff_1_q, d_ff_4_q, hp, tp;
  wire [7:0] multiplexer_1_out, Q_0_q, Q_1_q, Q_2_q, Q_3_q, registerfile_1_da;

  not not_1 (not_1_out, Enq__Deq);
  assign driver_1_out = En ? not_1_out : 1'bz;  // Driver driver_1
  assign driver_2_out = En ? Enq__Deq : 1'bz;  // Driver driver_2
  Counter #(.Bits(2)) Head_P (.en(driver_1_out), .C(CLK), .clr(1'b0), .out(hp));  // open: ovf
  Counter #(.Bits(2)) Tail_P (.en(driver_2_out), .C(CLK), .clr(1'b0), .out(tp));  // open: ovf
  and and_1 (r0, driver_2_out, a0);
  and and_2 (r1, driver_2_out, a1);
  and and_3 (r2, driver_2_out, a2);
  and and_4 (r3, driver_2_out, a3);
  // Probe on hp
  // Probe on tp
  Decoder #(.Selector_Bits(2)) decoder_1 (.sel(tp), .out_0(a0), .out_1(a1), .out_2(a2), .out_3(a3));
  Register #(.Bits(8)) Q_0 (.D(Data), .C(CLK), .en(r0), .Q(Q_0_q));
  Register #(.Bits(8)) Q_1 (.D(Data), .C(CLK), .en(r1), .Q(Q_1_q));
  Register #(.Bits(8)) Q_2 (.D(Data), .C(CLK), .en(r2), .Q(Q_2_q));
  Register #(.Bits(8)) Q_3 (.D(Data), .C(CLK), .en(r3), .Q(Q_3_q));
  D_FF #(.Bits(2)) d_ff_1 (.D(hp), .C(CLK), .Q(d_ff_1_q));  // open: nQ
  // Probe on Q_0_q
  // Probe on Q_1_q
  assign driver_3_out = En ? Enq__Deq : 1'bz;  // Driver driver_3
  not not_2 (not_2_out, Enq__Deq);
  // Probe on Q_2_q
  // Probe on Q_3_q
  D_FF d_ff_2 (.D(not_3_out), .C(CLK), .Q(d_ff_2_q));  // open: nQ
  not not_3 (not_3_out, Enq__Deq);
  RegisterFile #(.Bits(8)) registerfile_1 (
    .Din(Data), .we(driver_3_out), .Rw(tp), .C(CLK), .Ra(d_ff_1_q), .Rb(2'b00), .Da(registerfile_1_da));  // open: Db
  D_FF d_ff_3 (.D(not_2_out), .C(CLK), .Q(d_ff_3_q));  // open: nQ
  Multiplexer #(.Selector_Bits(2), .Bits(8)) multiplexer_1 (
    .sel(d_ff_4_q), .in_0(Q_0_q), .in_1(Q_1_q), .in_2(Q_2_q), .in_3(Q_3_q), .out(multiplexer_1_out));
  D_FF #(.Bits(2)) d_ff_4 (.D(hp), .C(CLK), .Q(d_ff_4_q));  // open: nQ
  assign D_out = d_ff_2_q ? registerfile_1_da : 8'bz;  // Driver driver_4
  assign Out = d_ff_3_q ? multiplexer_1_out : 8'bz;  // Driver driver_5

  // Other names for the same wires on the sheet: w__r = Enq__Deq
endmodule
