// Digital circuit set associative map.dig as structural Verilog
module set_associative_map (
  input  [7:0] Addr,
  input  EN,
  input  Ready,
  input  CLK,
  output [7:0] Data,
  output [31:0] Bulkdata
);

  wire and_2_out, and_3_out, and_4_out, C_hit, comparator_1_eq, comparator_2_eq, comparator_3_lt,
       comparator_4_lt, comparator_5_lt, comparator_6_lt, h0, h1, h2, h3, h4, h5, h6, h7, hit, L_hit, miss,
       multiplexer_8_out, multiplexer_10_out, multiplexer_11_out, multiplexer_12_out, multiplexer_13_out,
       multiplexer_14_out, nRd, OF, V0, V1, V2, V3, V4, V5, V6, V7, W0, W1, W2, W3, W4, W5, W6, W7, We;
  wire [0:0] multiplexer_1_out;
  wire [1:0] counter_1_out;
  wire [2:0] D0, D1, D2, D3, D4, D5, D6, D7, L0, L1, L2, L3, L4, L5, L6, L7, multiplexer_7_out,
       multiplexer_9_out, W_hit;
  wire [4:0] multiplexer_4_out;
  wire [7:0] addr_t, C0, C1, C2, C3, C4, C5, C6, C7, cache_d, data_t, driver_1_out, driver_1_out_2,
       driver_1_out_3, driver_1_out_4, multiplexer_2_out, multiplexer_5_out;
  wire [31:0] rom_1_d;

  Counter #(.Bits(2)) counter_1 (.en(We), .C(CLK), .clr(1'b0), .out(counter_1_out), .ovf(OF));
  Register #(.Bits(8)) A (.D(Addr), .C(CLK), .en(1'b1), .Q(addr_t));
  // Probe on counter_1_out
  D_FF #(.Bits(3)) d_ff_1 (.D({addr_t[4:3], multiplexer_1_out[0]}), .C(Ready), .Q(W_hit));  // open: nQ
  Multiplexer multiplexer_1 (.sel(hit), .in_0(C_hit), .in_1(L_hit), .out(multiplexer_1_out[0]));
  // Probe on addr_t
  // Probe on {driver_1_out_4, driver_1_out_3, driver_1_out_2, driver_1_out}
  assign {driver_1_out_4, driver_1_out_3, driver_1_out_2, driver_1_out} = Ready ? Bulkdata : 32'bz;  // Driver driver_1
  Multiplexer #(.Selector_Bits(2), .Bits(8)) multiplexer_2 (
    .sel(counter_1_out), .in_0(driver_1_out), .in_1(driver_1_out_2), .in_2(driver_1_out_3),
    .in_3(driver_1_out_4), .out(multiplexer_2_out));
  // Probe on {addr_t[4:3], multiplexer_1_out[0]}
  ROM #(.AddrBits(6), .Bits(32)) rom_1 (.A(addr_t[7:2]), .sel(EN), .D(rom_1_d));
  LED u_MISS (.in(miss));
  assign Data = ~miss ? data_t : 8'bz;  // DriverInvSel driverinvsel_1
  and and_1 (nRd, EN, ~Ready);  // And
  // Probe on multiplexer_4_out
  // Probe on multiplexer_2_out
  Multiplexer #(.Bits(2)) multiplexer_3 (
    .sel(We), .in_0(addr_t[1:0]), .in_1(counter_1_out), .out(multiplexer_4_out[1:0]));
  Multiplexer #(.Bits(3)) multiplexer_4 (
    .sel(We), .in_0({addr_t[4:3], L_hit}), .in_1(W_hit), .out(multiplexer_4_out[4:2]));
  assign Bulkdata = Ready ? rom_1_d : 32'bz;  // Driver driver_2
  Multiplexer #(.Selector_Bits(2), .Bits(8)) multiplexer_5 (
    .sel(addr_t[1:0]), .in_0(driver_1_out), .in_1(driver_1_out_2), .in_2(driver_1_out_3),
    .in_3(driver_1_out_4), .out(multiplexer_5_out));
  RAMDualPort #(.AddrBits(5), .Bits(8)) cache (
    .A(multiplexer_4_out), .Din(multiplexer_2_out), .str(We), .C(CLK), .ld(and_2_out), .D(cache_d));
  Demultiplexer #(.Selector_Bits(3)) demultiplexer_1 (
    .sel({addr_t[4:3], L_hit}), .in(hit), .out_0(h0), .out_1(h1), .out_2(h2), .out_3(h3), .out_4(h4),
    .out_5(h5), .out_6(h6), .out_7(h7));
  and and_2 (and_2_out, hit, EN);
  Multiplexer #(.Bits(8)) multiplexer_6 (.sel(We), .in_0(cache_d), .in_1(multiplexer_5_out), .out(data_t));
  Demultiplexer #(.Selector_Bits(3)) demultiplexer_2 (
    .sel(W_hit), .in(We), .out_0(W0), .out_1(W1), .out_2(W2), .out_3(W3), .out_4(W4), .out_5(W5), .out_6(W6),
    .out_7(W7));
  // Probe on addr_t
  // Probe on addr_t[1:0]
  // Probe on addr_t[4:3]
  Demultiplexer #(.Selector_Bits(3), .Bits(3)) demultiplexer_3 (
    .sel(W_hit), .in(addr_t[7:5]), .out_0(D0), .out_1(D1), .out_2(D2), .out_3(D3), .out_4(D4), .out_5(D5),
    .out_6(D6), .out_7(D7));
  // Probe on addr_t[7:5]
  Counter #(.Bits(8)) u_C0 (.en(nRd), .C(CLK), .clr(h0), .out(C0));  // open: ovf
  Counter #(.Bits(8)) u_C1 (.en(nRd), .C(CLK), .clr(h1), .out(C1));  // open: ovf
  Register #(.Bits(3)) u_L0 (.D(D0), .C(CLK), .en(W0), .Q(L0));
  Register #(.Bits(3)) u_L1 (.D(D1), .C(CLK), .en(W1), .Q(L1));
  Multiplexer #(.Selector_Bits(2), .Bits(3)) multiplexer_7 (
    .sel(addr_t[4:3]), .in_0(L0), .in_1(L2), .in_2(L4), .in_3(L6), .out(multiplexer_7_out));
  Multiplexer #(.Selector_Bits(2)) multiplexer_8 (
    .sel(addr_t[4:3]), .in_0(V0), .in_1(V2), .in_2(V4), .in_3(V6), .out(multiplexer_8_out));
  Multiplexer #(.Selector_Bits(2), .Bits(3)) multiplexer_9 (
    .sel(addr_t[4:3]), .in_0(L1), .in_1(L3), .in_2(L5), .in_3(L7), .out(multiplexer_9_out));
  // Probe on W_hit
  // Probe on C0
  // Probe on C1
  // Probe on L0
  // Probe on L1
  Comparator #(.Bits(3)) comparator_1 (.a(multiplexer_7_out), .b(addr_t[7:5]), .eq(comparator_1_eq));  // open: gt, lt
  Comparator #(.Bits(3)) comparator_2 (.a(multiplexer_9_out), .b(addr_t[7:5]), .eq(comparator_2_eq));  // open: gt, lt
  Multiplexer #(.Selector_Bits(2)) multiplexer_10 (
    .sel(addr_t[4:3]), .in_0(V1), .in_1(V3), .in_2(V5), .in_3(V7), .out(multiplexer_10_out));
  Counter #(.Bits(8)) u_C2 (.en(nRd), .C(CLK), .clr(h2), .out(C2));  // open: ovf
  Counter #(.Bits(8)) u_C3 (.en(nRd), .C(CLK), .clr(h3), .out(C3));  // open: ovf
  Register #(.Bits(3)) u_L2 (.D(D2), .C(CLK), .en(W2), .Q(L2));
  Register #(.Bits(3)) u_L3 (.D(D3), .C(CLK), .en(W3), .Q(L3));
  and and_3 (and_3_out, comparator_1_eq, multiplexer_8_out);
  and and_4 (and_4_out, comparator_2_eq, multiplexer_10_out);
  // Probe on C2
  // Probe on C3
  // Probe on L2
  // Probe on L3
  and and_5 (miss, ~hit, EN);  // And
  and and_6 (We, EN, Ready);
  and and_7 (L_hit, ~and_3_out, and_4_out);  // And
  or or_1 (hit, and_3_out, and_4_out);
  Counter #(.Bits(8)) u_C4 (.en(nRd), .C(CLK), .clr(h4), .out(C4));  // open: ovf
  Counter #(.Bits(8)) u_C5 (.en(nRd), .C(CLK), .clr(h5), .out(C5));  // open: ovf
  Register #(.Bits(3)) u_L4 (.D(D4), .C(CLK), .en(W4), .Q(L4));
  Register #(.Bits(3)) u_L5 (.D(D5), .C(CLK), .en(W5), .Q(L5));
  // Probe on C4
  // Probe on C5
  // Probe on L4
  // Probe on L5
  Comparator #(.Bits(8)) comparator_3 (.a(C0), .b(C1), .lt(comparator_3_lt));  // open: gt, eq
  Comparator #(.Bits(8)) comparator_4 (.a(C2), .b(C3), .lt(comparator_4_lt));  // open: gt, eq
  Comparator #(.Bits(8)) comparator_5 (.a(C4), .b(C5), .lt(comparator_5_lt));  // open: gt, eq
  Comparator #(.Bits(8)) comparator_6 (.a(C6), .b(C7), .lt(comparator_6_lt));  // open: gt, eq
  Multiplexer multiplexer_11 (.sel(comparator_3_lt), .in_0(1'b0), .in_1(1'b1), .out(multiplexer_11_out));
  Multiplexer multiplexer_12 (.sel(comparator_4_lt), .in_0(1'b0), .in_1(1'b1), .out(multiplexer_12_out));
  Multiplexer multiplexer_13 (.sel(comparator_5_lt), .in_0(1'b0), .in_1(1'b1), .out(multiplexer_13_out));
  Multiplexer multiplexer_14 (.sel(comparator_6_lt), .in_0(1'b0), .in_1(1'b1), .out(multiplexer_14_out));
  Counter #(.Bits(8)) u_C6 (.en(nRd), .C(CLK), .clr(h6), .out(C6));  // open: ovf
  Counter #(.Bits(8)) u_C7 (.en(nRd), .C(CLK), .clr(h7), .out(C7));  // open: ovf
  Register #(.Bits(3)) u_L6 (.D(D6), .C(CLK), .en(W6), .Q(L6));
  Register #(.Bits(3)) u_L7 (.D(D7), .C(CLK), .en(W7), .Q(L7));
  Multiplexer #(.Selector_Bits(2)) multiplexer_15 (
    .sel(addr_t[4:3]), .in_0(multiplexer_11_out), .in_1(multiplexer_12_out), .in_2(multiplexer_13_out),
    .in_3(multiplexer_14_out), .out(C_hit));
  // Probe on C6
  // Probe on C7
  // Probe on L6
  // Probe on L7
  Register u_v0 (.D(1'b1), .C(CLK), .en(W0), .Q(V0));
  Register u_v1 (.D(1'b1), .C(CLK), .en(W1), .Q(V1));
  Register u_v2 (.D(1'b1), .C(CLK), .en(W2), .Q(V2));
  Register u_v3 (.D(1'b1), .C(CLK), .en(W3), .Q(V3));
  Register u_v4 (.D(1'b1), .C(CLK), .en(W4), .Q(V4));
  Register u_v5 (.D(1'b1), .C(CLK), .en(W5), .Q(V5));
  Register u_v6 (.D(1'b1), .C(CLK), .en(W6), .Q(V6));
  Register u_v7 (.D(1'b1), .C(CLK), .en(W7), .Q(V7));

  // Other names for the same wires on the sheet: set[1:0] = addr_t[4:3]; Rd = Ready

  // Notes on the sheet:
  //   存储器电路
  //   contents of rom_1 (hex, n*v repeats v):
  //   10f9f3e7,fffff0b7,400093,40016f,158513,feb50fe3,fff20193,318233,308023,309023,30a023,
  //   40a223,402383,800403,801403,804403,805403,802403,ff3a413,ffe3b413,fff44413,247493,
  //   249513,1f4d593,25d593,40125613,40460633,c616b3,c42733,c43733,864733,e6d7b3,40f75733,
  //   d77733,c76833,200713,11d873,11d873,810f3,710f3,a973,25973,1039f3
  //   Set Associate Map
endmodule
