// Digital circuit stack.dig as structural Verilog
module stack (
  input  Push__Pop,
  input  En,
  input  [7:0] Data,
  input  CLK,
  output [7:0] Out,
  output [7:0] D_out
);

  wire d0, d1, d2, d3, d_ff_1_q, d_ff_2_q, r0, r1, r2, r3;
  wire [1:0] driver_1_out, sp;
  wire [7:0] multiplexer_1_out, registerfile_1_da, stack_0_q, stack_1_q, stack_2_q, stack_3_q;

  assign driver_1_out = Push__Pop ? sp : 2'bz;  // Driver driver_1
  CounterPreset #(.Bits(2)) counterpreset_1 (
    .en(En), .C(CLK), .dir(~Push__Pop), .in(2'b00), .ld(1'b0), .clr(1'b0), .out(sp));  // open: ovf
  D_FF d_ff_1 (.D(Push__Pop), .C(CLK), .Q(d_ff_1_q));  // open: nQ
  RegisterFile #(.Bits(8)) registerfile_1 (
    .Din(Data), .we(Push__Pop), .Rw(driver_1_out), .C(CLK), .Ra(sp), .Rb(2'b00), .Da(registerfile_1_da));  // open: Db
  // Probe on sp
  assign D_out = ~d_ff_1_q ? registerfile_1_da : 8'bz;  // DriverInvSel driverinvsel_1
  Decoder #(.Selector_Bits(2)) decoder_1 (.sel(sp), .out_0(d0), .out_1(d1), .out_2(d2), .out_3(d3));
  and and_1 (r0, En, Push__Pop, d0);
  and and_2 (r1, En, Push__Pop, d1);
  and and_3 (r2, En, Push__Pop, d2);
  and and_4 (r3, En, Push__Pop, d3);
  Register #(.Bits(8)) stack_0 (.D(Data), .C(CLK), .en(r0), .Q(stack_0_q));
  Register #(.Bits(8)) stack_1 (.D(Data), .C(CLK), .en(r1), .Q(stack_1_q));
  Register #(.Bits(8)) stack_2 (.D(Data), .C(CLK), .en(r2), .Q(stack_2_q));
  Register #(.Bits(8)) stack_3 (.D(Data), .C(CLK), .en(r3), .Q(stack_3_q));
  // Probe on stack_0_q
  // Probe on stack_1_q
  Multiplexer #(.Selector_Bits(2), .Bits(8)) multiplexer_1 (
    .sel(sp), .in_0(stack_0_q), .in_1(stack_1_q), .in_2(stack_2_q), .in_3(stack_3_q), .out(multiplexer_1_out));
  // Probe on stack_2_q
  // Probe on stack_3_q
  D_FF d_ff_2 (.D(Push__Pop), .C(CLK), .Q(d_ff_2_q));  // open: nQ
  assign Out = ~d_ff_2_q ? multiplexer_1_out : 8'bz;  // DriverInvSel driverinvsel_2

  // Other names for the same wires on the sheet: pushpop = Push__Pop
endmodule
