// Digital circuit 16bit CSA adder.dig as structural Verilog
// Simple 4-bit multiplier built from three 4-bit adders. 
// The actual 1-bit multiplications are implemented by the AND gates.
// {{de Einfacher 4-Bit Multiplikator aufgebaut aus drei 4-Bit
// Addierern. Die eigentlichen 1-Bit Multiplikationen 
// werden durch die Und-Gatter implementiert.}}
module _16bit_CSA_adder (
  input  A0,
  input  A1,
  input  A2,
  input  A3,
  input  C0,
  input  A4,
  input  A5,
  input  A6,
  input  A7,
  input  A8,
  input  A9,
  input  A10,
  input  A11,
  input  A12,
  input  A13,
  input  A14,
  input  A15,
  input  B0,
  input  B1,
  input  B2,
  input  B3,
  input  B4,
  input  B5,
  input  B6,
  input  B7,
  input  B8,
  input  B9,
  input  B10,
  input  B11,
  input  B12,
  input  B13,
  input  B14,
  input  B15,
  output C16,
  output S0,
  output S1,
  output S2,
  output S3,
  output S4,
  output S5,
  output S6,
  output S7,
  output S8,
  output S9,
  output S10,
  output S11,
  output S12,
  output S13,
  output S14,
  output S15
);

  wire multiplexer_2_out, multiplexer_3_out, multiplexer_4_out, undriven, undriven_2, undriven_3, undriven_4,
       undriven_5, undriven_6, undriven_7, undriven_8;

  _4bit_CSA_sub_adder _4bit_csa_sub_adder_1 (
    .A3(A15), .A2(A14), .A1(A13), .A0(A12), .B3(B15), .B2(B14), .B1(B13), .B0(B12), .C0(multiplexer_2_out));  // open: S3, S2, S1, S0, P, G
  _4bit_CSA_sub_adder _4bit_csa_sub_adder_2 (
    .A3(A11), .A2(A10), .A1(A9), .A0(A8), .B3(B11), .B2(B10), .B1(B9), .B0(B8), .C0(multiplexer_3_out));  // open: S3, S2, S1, S0, P, G
  _4bit_CSA_sub_adder _4bit_csa_sub_adder_3 (
    .A3(A7), .A2(A6), .A1(A5), .A0(A4), .B3(B7), .B2(B6), .B1(B5), .B0(B4), .C0(multiplexer_4_out));  // open: S3, S2, S1, S0, P, G
  _4bit_CSA_sub_adder _4bit_csa_sub_adder_4 (
    .A3(A3), .A2(A2), .A1(A1), .A0(A0), .B3(B3), .B2(B2), .B1(B1), .B0(B0), .C0(C0));  // open: S3, S2, S1, S0, P, G
  Multiplexer multiplexer_1 (.sel(undriven_8), .in_0(undriven_7), .in_1(multiplexer_2_out), .out(C16));
  Multiplexer multiplexer_2 (.sel(undriven), .in_0(undriven_2), .in_1(multiplexer_3_out), .out(multiplexer_2_out));
  Multiplexer multiplexer_3 (.sel(undriven_3), .in_0(undriven_4), .in_1(multiplexer_4_out), .out(multiplexer_3_out));
  Multiplexer multiplexer_4 (.sel(undriven_5), .in_0(undriven_6), .in_1(C0), .out(multiplexer_4_out));
endmodule
