// Digital circuit 4bit CSA sub_adder.dig as structural Verilog
// Simple 4-bit multiplier built from three 4-bit adders. 
// The actual 1-bit multiplications are implemented by the AND gates.
// {{de Einfacher 4-Bit Multiplikator aufgebaut aus drei 4-Bit
// Addierern. Die eigentlichen 1-Bit Multiplikationen 
// werden durch die Und-Gatter implementiert.}}
module _4bit_CSA_sub_adder (
  input  A3,
  input  A2,
  input  A1,
  input  A0,
  input  B3,
  input  B2,
  input  B1,
  input  B0,
  input  C0,
  output S3,
  output S2,
  output S1,
  output S0,
  output P,
  output G
);

  wire and_5_out, and_6_out, and_7_out, and_9_out, and_10_out, and_11_out, and_12_out, and_13_out,
       and_14_out, G0, G1, G2, G3, or_2_out, or_3_out, or_4_out, P0, P1, P2, P3;

  xor xor_1 (P3, A3, B3);
  and and_1 (G3, A3, B3);
  xor xor_2 (P2, A2, B2);
  and and_2 (G2, A2, B2);
  xor xor_3 (P1, A1, B1);
  and and_3 (G1, A1, B1);
  xor xor_4 (P0, A0, B0);
  and and_4 (G0, A0, B0);
  and and_5 (and_5_out, G2, P3);
  and and_6 (and_6_out, G1, P3, P2);
  and and_7 (and_7_out, G0, P3, P2, P1);
  and and_8 (P, P3, P2, P1, P0);
  and and_9 (and_9_out, G1, P2);
  and and_10 (and_10_out, G0, P2, P1);
  and and_11 (and_11_out, P2, P1, P0, C0);
  and and_12 (and_12_out, G0, P1);
  and and_13 (and_13_out, P1, P0, C0);
  and and_14 (and_14_out, P0, C0);
  or or_1 (G, G3, and_5_out, and_6_out, and_7_out);
  or or_2 (or_2_out, G2, and_9_out, and_10_out, and_11_out);
  or or_3 (or_3_out, G1, and_12_out, and_13_out);
  or or_4 (or_4_out, G0, and_14_out);
  xor xor_5 (S0, P0, C0);
  xor xor_6 (S3, P3, or_2_out);
  // Probe C3 on or_2_out
  xor xor_7 (S2, P2, or_3_out);
  // Probe C2 on or_3_out
  xor xor_8 (S1, P1, or_4_out);
  // Probe C1 on or_4_out

  // Notes on the sheet:
  //   A3: default 1
  //   A0: default 1
  //   B2: default 1
  //   B1: default 1
endmodule
