// Digital circuit ACC&MAX.dig as structural Verilog
module ACC_MAX (
  input  clr,
  input  CLR_2,
  output [3:0] out_2,
  output [7:0] out_4
);

  wire clk_out, clock_out, comparator_1_gt;
  wire [0:0] add_1_c_o;
  wire [3:0] add_1_s, add_2_s, counter_1_out, counter_2_out, multiplexer_1_out, rom_1_d, rom_2_d;

  Button clk (.out(clk_out));
  Button clock (.out(clock_out));
  Counter #(.Bits(4)) counter_1 (.en(1'b1), .C(clk_out), .clr(clr), .out(counter_1_out));  // open: ovf
  Counter #(.Bits(4)) counter_2 (.en(1'b1), .C(clock_out), .clr(CLR_2), .out(counter_2_out));  // open: ovf
  // Probe on counter_1_out
  ROM #(.AddrBits(4), .Bits(4)) rom_1 (.A(counter_1_out), .sel(1'b1), .D(rom_1_d));
  // Probe on counter_2_out
  ROM #(.AddrBits(4), .Bits(4)) rom_2 (.A(counter_2_out), .sel(1'b1), .D(rom_2_d));
  Multiplexer #(.Bits(4)) multiplexer_1 (.sel(comparator_1_gt), .in_0(out_2), .in_1(rom_1_d), .out(multiplexer_1_out));
  Comparator #(.Bits(4)) comparator_1 (.a(rom_1_d), .b(out_2), .gt(comparator_1_gt));  // open: eq, lt
  // Probe on rom_1_d
  // Probe on rom_2_d
  Add #(.Bits(4)) add_1 (.a(out_4[3:0]), .b(rom_2_d), .c_i(1'b0), .s(add_1_s), .c_o(add_1_c_o[0]));
  Add #(.Bits(4)) add_2 (.a(out_4[7:4]), .b({3'b000, add_1_c_o[0]}), .c_i(1'b0), .s(add_2_s));  // open: c_o
  D_FF_AS #(.Bits(4)) d_ff_as_1 (.Set(1'b0), .D(multiplexer_1_out), .C(clk_out), .Clr(clr), .Q(out_2));  // open: nQ
  D_FF_AS #(.Bits(4)) d_ff_as_2 (.Set(1'b0), .D(add_1_s), .C(clock_out), .Clr(CLR_2), .Q(out_4[3:0]));  // open: nQ
  D_FF_AS #(.Bits(4)) d_ff_as_3 (.Set(1'b0), .D(add_2_s), .C(clock_out), .Clr(CLR_2), .Q(out_4[7:4]));  // open: nQ

  // Notes on the sheet:
  //   contents of rom_1 (hex, n*v repeats v):
  //   0,1,2,3,4,5,6,7,8,9
  //   contents of rom_2 (hex, n*v repeats v):
  //   0,1,2,3,4,5,6,7,8,9
endmodule
