// Digital circuit Adder_Sub.dig as structural Verilog
module Adder_Sub (
  input  A,
  input  B,
  input  a_2,
  input  b_2,
  input  A_i,
  input  B_i,
  input  C_i_1,
  input  BO_j_1,
  input  A_j,
  input  B_j,
  output S,
  output C,
  output s_2,
  output bo,
  output C_i,
  output S_i,
  output S_j,
  output BO_j
);

  wire and_3_out, and_4_out, and_5_out, and_6_out, not_1_out, not_2_out, not_3_out, xor_3_out, xor_4_out;

  xor xor_1 (S, A, B);
  and and_1 (C, A, B);
  not not_1 (not_1_out, a_2);
  xor xor_2 (s_2, a_2, b_2);
  and and_2 (bo, not_1_out, b_2);
  and and_3 (and_3_out, A_i, B_i);
  xor xor_3 (xor_3_out, A_i, B_i);
  not not_2 (not_2_out, A_j);
  xor xor_4 (xor_4_out, A_j, B_j);
  and and_4 (and_4_out, not_2_out, B_j);
  and and_5 (and_5_out, xor_3_out, C_i_1);
  xor xor_5 (S_i, xor_3_out, C_i_1);
  not not_3 (not_3_out, xor_4_out);
  or or_1 (C_i, and_3_out, and_5_out);
  xor xor_6 (S_j, xor_4_out, BO_j_1);
  and and_6 (and_6_out, not_3_out, BO_j_1);
  or or_2 (BO_j, and_6_out, and_4_out);

  // Notes on the sheet:
  //   A_i: first bit to add
  //   {{de Erstes zu addierendes Bit.}}
  //   B_i: second bit to add
  //   {{de Zweites zu addierendes Bit.}}
  //   C_i_1: carry in
  //   {{de Übertragsbit der Vorgängerschaltung.}}
  //   C_i: carry bit
  //   {{de Übertragsbit}}
  //   S_i: sum {{de Summe}}
  //   Half Adder
  //   Half Sub
  //   Full Adder
  //   Full Sub
endmodule

/* Test case Full Adder:
  A_i B_i C_{i-1} C_i S_i

loop (A,2)
  loop (B,2)
    loop (Ci,2)
 (A) (B) (Ci)   bits(2, A+B+Ci)
    end loop
  end loop
end loop
*/

/* Test case Full Sub:
A_j B_j BO_{j-1}  BO_j S_j
 0   0   0        0   0
 0   0   1        1   1
 0   1   0        1   1
 0   1   1        1   0
 1   0   0        0   1
 1   0   1        0   0
 1   1   0        0   0
 1   1   1        1   1
*/
