// Digital circuit Brent-Kung adder.dig as structural Verilog
// Simple 4-bit multiplier built from three 4-bit adders. 
// The actual 1-bit multiplications are implemented by the AND gates.
// {{de Einfacher 4-Bit Multiplikator aufgebaut aus drei 4-Bit
// Addierern. Die eigentlichen 1-Bit Multiplikationen 
// werden durch die Und-Gatter implementiert.}}
module Brent_Kung_adder (
  input  A3,
  input  A2,
  input  A1,
  input  A4,
  input  B3,
  input  B2,
  input  B1,
  input  B4,
  input  C0,
  output S1,
  output S2,
  output S3,
  output S4,
  output C4
);

  wire and_5_out, and_6_out, and_7_out, and_8_out, and_9_out, and_10_out, and_11_out, and_12_out, and_13_out,
       and_14_out, and_15_out, and_16_out, g1, g2, g3, g4, or_1_out, or_2_out, or_3_out, or_4_out, or_5_out,
       or_6_out, or_8_out, p1, p2, p3, p4;

  xor xor_1 (p4, A4, B4);
  and and_1 (g4, A4, B4);
  xor xor_2 (p3, A3, B3);
  and and_2 (g3, A3, B3);
  xor xor_3 (p2, A2, B2);
  and and_3 (g2, A2, B2);
  xor xor_4 (p1, A1, B1);
  and and_4 (g1, A1, B1);
  and and_5 (and_5_out, p4, g3);
  and and_6 (and_6_out, p4, p3);
  and and_7 (and_7_out, p2, g1);
  and and_8 (and_8_out, p2, p1);
  and and_9 (and_9_out, p1, C0);
  or or_1 (or_1_out, g4, and_5_out);
  or or_2 (or_2_out, g2, and_7_out);
  or or_3 (or_3_out, g1, and_9_out);
  // Probe P2 on and_8_out
  xor xor_5 (S1, or_3_out, p1);
  // Probe G2 on or_2_out
  and and_10 (and_10_out, and_6_out, or_2_out);
  and and_11 (and_11_out, and_6_out, and_8_out);
  and and_12 (and_12_out, p3, or_2_out);
  and and_13 (and_13_out, p3, and_8_out);
  and and_14 (and_14_out, and_8_out, C0);
  or or_4 (or_4_out, or_1_out, and_10_out);
  // Probe P4 on and_11_out
  or or_5 (or_5_out, g3, and_12_out);
  // Probe P3 on and_13_out
  or or_6 (or_6_out, or_2_out, and_14_out);
  // Probe G4 on or_4_out
  // Probe G3 on or_5_out
  xor xor_6 (S2, or_6_out, p2);
  and and_15 (and_15_out, and_11_out, C0);
  and and_16 (and_16_out, and_13_out, C0);
  or or_7 (C4, or_4_out, and_15_out);
  or or_8 (or_8_out, or_5_out, and_16_out);
  xor xor_7 (S4, C4, p4);
  xor xor_8 (S3, or_8_out, p3);

  // Notes on the sheet:
  //   A3: default 1
  //   A4: default 1
  //   B2: default 1
  //   B1: default 1
  //   node
endmodule
