// Digital circuit CompParall_sign.dig as structural Verilog
// 4-bit comparator built according to the ripple-carry principle. 
// However, here the Enable bit is passed down from the 
// higher-order bit to the lower-order bit, ie in the reverse 
// direction as the carry bit of the ripple-carry adder.
// {{de 4-Bit Vergleicher der nach dem ripple-carry Prinzip
// aufgebaut ist. Jedoch wird hier das Enable-Bit
// vom höher wertigem Bit an das niederwertige Bit
// herabgereicht wird, also in der umgekehrten 
// Richtung wie das Carry-Bit des ripple-carry 
// Addierers.}}
module CompParall_sign (
  input  P_3,
  input  P_2,
  input  P_1,
  input  P_0,
  input  Q_3,
  input  Q_2,
  input  Q_1,
  input  Q_0,
  output P_gt_Q
);

  wire comparator_1_eq, comparator_2_eq, comparator_3_eq, comparator_4_gt, multiplexer_1_out,
       multiplexer_2_out, multiplexer_3_out, not_1_out;

  not not_1 (not_1_out, P_3);
  Comparator comparator_1 (.a(P_3), .b(Q_3), .eq(comparator_1_eq));  // open: gt, lt
  Comparator comparator_2 (.a(P_2), .b(Q_2), .eq(comparator_2_eq));  // open: gt, lt
  Comparator comparator_3 (.a(P_1), .b(Q_1), .eq(comparator_3_eq));  // open: gt, lt
  Comparator comparator_4 (.a(P_0), .b(Q_0), .gt(comparator_4_gt));  // open: eq, lt
  Multiplexer multiplexer_1 (.sel(comparator_4_gt), .in_0(1'b0), .in_1(1'b1), .out(multiplexer_1_out));
  Multiplexer multiplexer_2 (.sel(comparator_3_eq), .in_0(P_1), .in_1(multiplexer_1_out), .out(multiplexer_2_out));
  Multiplexer multiplexer_3 (.sel(comparator_2_eq), .in_0(P_2), .in_1(multiplexer_2_out), .out(multiplexer_3_out));
  Multiplexer multiplexer_4 (.sel(comparator_1_eq), .in_0(not_1_out), .in_1(multiplexer_3_out), .out(P_gt_Q));

  // Notes on the sheet:
  //   P_gt_Q: This output is high, if P>Q is valid.
  //   {{de Das Bit ist Eins, wenn P>Q gilt.}}
endmodule

/* Test case:
P_3 P_2 P_1 P_0   Q_3 Q_2 Q_1 Q_0  P>Q
repeat(64) 0 bits(3,n>>3) 0 bits(3,n) ((n>>3)>(n&7))
repeat(64) 1 bits(3,n>>3) 1 bits(3,n) ((n>>3)>(n&7))
*/
