// Digital circuit Comp_Sign.dig as structural Verilog
module Comp_Sign (
  input  [1:0] A,
  input  [1:0] B,
  output A_lt_B,
  output A_eq_B,
  output A_gt_B,
  output a_gt_b_2,
  output a_eq_b_2,
  output a_lt_b_2,
  output a_gt_b_3,
  output a_eq_b_3,
  output a_lt_b_3
);

  wire and_1_out, and_2_out, and_3_out, and_5_out, decoder_1_out_1, decoder_1_out_2, nor_1_out, nor_2_out,
       not_1_out, not_2_out;

  Comparator #(.Bits(2), .Signed("true")) comparator_1 (.a(A), .b(B), .gt(a_gt_b_2), .eq(a_eq_b_2), .lt(a_lt_b_2));
  not not_1 (not_1_out, A[0]);
  not not_2 (not_2_out, B[0]);
  Decoder #(.Selector_Bits(2)) decoder_1 (
    .sel({B[1], A[1]}), .out_1(decoder_1_out_1), .out_2(decoder_1_out_2));  // open: out_0, out_3
  and and_1 (and_1_out, not_1_out, B[0]);
  and and_2 (and_2_out, A[0], not_2_out);
  nor nor_1 (nor_1_out, decoder_1_out_1, decoder_1_out_2);
  nor nor_2 (nor_2_out, and_1_out, and_2_out);
  and and_3 (and_3_out, nor_1_out, and_1_out);
  and and_4 (A_eq_B, nor_1_out, nor_2_out);
  and and_5 (and_5_out, nor_1_out, and_2_out);
  Comparator #(.Bits(2)) comparator_2 (.a(A), .b(B), .gt(a_gt_b_3), .eq(a_eq_b_3), .lt(a_lt_b_3));
  or or_1 (A_lt_B, decoder_1_out_1, and_3_out);
  or or_2 (A_gt_B, and_5_out, decoder_1_out_2);

  // Notes on the sheet:
  //   A: First bit to compare.
  //   {{de Erstes zu vergleichendes Bit.}}
  //   B: Second bit to compare.
  //   {{de Zweites zu vergleichendes Bit.}}
  //   A_lt_B: This output is one if A<B is true.
  //   {{de Das Bit ist Eins, wenn A<B gilt.}}
  //   A_eq_B: This output is one if A=B is true.
  //   {{de Das Bit ist Eins, wenn A=B gilt.}}
  //   A_gt_B: This output is one if A>B is true.
  //   {{de Das Bit ist Eins, wenn A>B gilt.}}
  //   Sign
  //   Unsign
endmodule
