// Digital circuit Full Adder_Sub Naive.dig as structural Verilog
// Naive implementation of a full adder.
// {{de Naive Umsetzung eines Volladdierers.}}
module Full_Adder_Sub_Naive (
  input  C_i_1,
  input  A_i,
  input  B_i,
  input  A_j,
  input  B_j,
  input  BO_j_1,
  output S_i,
  output C_i,
  output S_j,
  output BO_j,
  output S_add,
  output C_o,
  output S_sub,
  output BO_o
);

  wire and_1_out, and_2_out, and_3_out, and_4_out, and_5_out, and_6_out, and_7_out, and_8_out, and_9_out,
       and_10_out, and_11_out, and_12_out, and_13_out, and_14_out, not_1_out, not_2_out, not_3_out,
       not_4_out, not_5_out, not_6_out;

  Add add_1 (.a(A_i), .b(B_i), .c_i(C_i_1), .s(S_add), .c_o(C_o));
  not not_1 (not_1_out, A_i);
  not not_2 (not_2_out, B_i);
  not not_3 (not_3_out, C_i_1);
  and and_1 (and_1_out, not_1_out, not_2_out, C_i_1);
  and and_2 (and_2_out, not_1_out, B_i, not_3_out);
  and and_3 (and_3_out, A_i, not_2_out, not_3_out);
  and and_4 (and_4_out, A_i, B_i, C_i_1);
  and and_5 (and_5_out, B_i, C_i_1);
  and and_6 (and_6_out, A_i, C_i_1);
  and and_7 (and_7_out, A_i, B_i);
  or or_1 (S_i, and_1_out, and_2_out, and_3_out, and_4_out);
  or or_2 (C_i, and_5_out, and_6_out, and_7_out);
  not not_4 (not_4_out, A_j);
  Sub sub_1 (.a(A_j), .b(B_j), .c_i(BO_j_1), .s(S_sub), .c_o(BO_o));
  not not_5 (not_5_out, B_j);
  not not_6 (not_6_out, BO_j_1);
  and and_8 (and_8_out, not_4_out, not_5_out, BO_j_1);
  and and_9 (and_9_out, not_4_out, B_j, not_6_out);
  and and_10 (and_10_out, A_j, not_5_out, not_6_out);
  and and_11 (and_11_out, A_j, B_j, BO_j_1);
  and and_12 (and_12_out, not_4_out, BO_j_1);
  and and_13 (and_13_out, not_4_out, B_j);
  and and_14 (and_14_out, B_j, BO_j_1);
  or or_3 (S_j, and_8_out, and_9_out, and_10_out, and_11_out);
  or or_4 (BO_j, and_12_out, and_13_out, and_14_out);
endmodule

/* Test case:
A_i B_i C_i-1 C_i S_i
 0   0   0     0   0
 0   0   1     0   1
 0   1   0     0   1
 0   1   1     1   0
 1   0   0     0   1
 1   0   1     1   0
 1   1   0     1   0
 1   1   1     1   1
*/

/* Test case:
A_j B_j BO_{j-1}  BO_j S_j
 0   0   0        0   0
 0   0   1        1   1
 0   1   0        1   1
 0   1   1        1   0
 1   0   0        0   1
 1   0   1        0   0
 1   1   0        0   0
 1   1   1        1   1
*/
