// Digital circuit FullAddSub_Sign.dig as structural Verilog
module FullAddSub_Sign (
  input  A_0,
  input  B_0,
  input  A_1,
  input  B_1,
  input  A_2,
  input  B_2,
  input  A_3,
  input  B_3,
  input  S,
  output S_0,
  output S_1,
  output S_2,
  output S_3,
  output C
);

  wire add_2_c_o, add_3_c_o, add_4_c_o, xor_1_out, xor_2_out, xor_3_out, xor_4_out;

  xor xor_1 (xor_1_out, B_3, S);
  xor xor_2 (xor_2_out, B_2, S);
  xor xor_3 (xor_3_out, B_1, S);
  xor xor_4 (xor_4_out, B_0, S);
  Add add_1 (.a(A_3), .b(xor_1_out), .c_i(add_2_c_o), .s(S_3), .c_o(C));
  Add add_2 (.a(A_2), .b(xor_2_out), .c_i(add_3_c_o), .s(S_2), .c_o(add_2_c_o));
  Add add_3 (.a(A_1), .b(xor_3_out), .c_i(add_4_c_o), .s(S_1), .c_o(add_3_c_o));
  Add add_4 (.a(A_0), .b(xor_4_out), .c_i(S), .s(S_0), .c_o(add_4_c_o));

  // Notes on the sheet:
  //   S: Input with which you can toggle between 
  //   addition (S = 0) and subtraction (S = 1).
  //   {{de Eingang mit welchem zwischen Addition (S=0) und 
  //   Subtraktion (S=1) umgeschaltet werden kann.}}
endmodule

/* Test case:
            S   A_3 A_2 A_1 A_0  B_3 B_2 B_1 B_0  S_3 S_2 S_1 S_0
repeat(256) 0   bits(4,n>>4)     bits(4,n)        bits(4,(n>>4)+(n&15))
repeat(256) 1   bits(4,n>>4)     bits(4,n)        bits(4,(n>>4)-(n&15))
*/
