// Digital circuit FullAdderRC.dig as structural Verilog
// Simplified 4-bit ripple carry adder, consisting of four full adders.
// {{de Vereinfachter 4-Bit Ripple-Carry-Addierer, bestehend
// aus vier Volladdierern.}}
module FullAdderRC (
  input  A0,
  input  B0,
  input  A1,
  input  B1,
  input  A2,
  input  B2,
  input  A3,
  input  B3,
  input  C__1,
  input  A_0,
  input  B_0,
  input  A_1,
  input  B_1,
  input  A_2,
  input  B_2,
  input  A_3,
  input  B_3,
  input  BO__1,
  output S0,
  output S1,
  output S2,
  output S3,
  output C,
  output S_0,
  output S_1,
  output S_2,
  output S_3,
  output BO
);

  wire add_2_c_o, add_3_c_o, add_4_c_o, sub_2_c_o, sub_3_c_o, sub_4_c_o;

  Add add_1 (.a(A3), .b(B3), .c_i(add_2_c_o), .s(S3), .c_o(C));
  Add add_2 (.a(A2), .b(B2), .c_i(add_3_c_o), .s(S2), .c_o(add_2_c_o));
  Add add_3 (.a(A1), .b(B1), .c_i(add_4_c_o), .s(S1), .c_o(add_3_c_o));
  Add add_4 (.a(A0), .b(B0), .c_i(C__1), .s(S0), .c_o(add_4_c_o));
  Sub sub_1 (.a(A_3), .b(B_3), .c_i(sub_2_c_o), .s(S_3), .c_o(BO));
  Sub sub_2 (.a(A_2), .b(B_2), .c_i(sub_3_c_o), .s(S_2), .c_o(sub_2_c_o));
  Sub sub_3 (.a(A_1), .b(B_1), .c_i(sub_4_c_o), .s(S_1), .c_o(sub_3_c_o));
  Sub sub_4 (.a(A_0), .b(B_0), .c_i(BO__1), .s(S_0), .c_o(sub_4_c_o));
endmodule

/* Test case Adder:
# A complete test of all 512 possible additions
# All created test vectors are shown in the result table.

C_{-1}  A3 A2 A1 A0  B3 B2 B1 B0  C S3 S2 S1 S0

loop(a,16)
 loop(b,16)
  0    bits(4,a)        bits(4,b)        bits(5,a+b)
  1    bits(4,a)        bits(4,b)        bits(5,a+b+1)
 end loop
end loop
*/

/* Test case Sub:
# complete test of all 512 possible additions
BO_{-1} A_3 A_2 A_1 A_0 B_3 B_2 B_1 B_0 BO S_3 S_2 S_1 S_0

loop(a,16)
 loop(b,16)
  0    bits(4,a)        bits(4,b)        bits(5,a-b)
  1    bits(4,a)        bits(4,b)        bits(5,a-b-1)
 end loop
end loop
*/
