// Digital circuit Kogge-Stone adder.dig as structural Verilog
// Simple 4-bit multiplier built from three 4-bit adders. 
// The actual 1-bit multiplications are implemented by the AND gates.
// {{de Einfacher 4-Bit Multiplikator aufgebaut aus drei 4-Bit
// Addierern. Die eigentlichen 1-Bit Multiplikationen 
// werden durch die Und-Gatter implementiert.}}
module Kogge_Stone_adder (
  input  A3,
  input  A2,
  input  A1,
  input  A4,
  input  B3,
  input  B2,
  input  B1,
  input  B4,
  input  C0,
  output S2,
  output S1,
  output C4,
  output S3,
  output S4
);

  wire and_5_out, and_6_out, and_7_out, and_8_out, and_9_out, and_10_out, and_11_out, G1, G2, G3, G4,
       or_1_out, or_2_out, or_3_out, or_4_out, or_5_out, or_6_out, P1, P2, P3, P4;

  xor xor_1 (P4, A4, B4);
  and and_1 (G4, A4, B4);
  xor xor_2 (P3, A3, B3);
  and and_2 (G3, A3, B3);
  xor xor_3 (P2, A2, B2);
  and and_3 (G2, A2, B2);
  xor xor_4 (P1, A1, B1);
  and and_4 (G1, A1, B1);
  and and_5 (and_5_out, P4, G3);
  and and_6 (and_6_out, P3, G2);
  and and_7 (and_7_out, P2, G1);
  and and_8 (and_8_out, P1, C0);
  xor xor_5 (S1, C0, P1);
  or or_1 (or_1_out, G4, and_5_out);
  or or_2 (or_2_out, G3, and_6_out);
  or or_3 (or_3_out, G2, and_7_out);
  or or_4 (or_4_out, G1, and_8_out);
  // Probe Q(4,3) on or_1_out
  // Probe Q(3,2) on or_2_out
  // Probe Q(2,1) on or_3_out
  // Probe Q(1,0) on or_4_out
  and and_9 (and_9_out, P3, P2, or_4_out);
  and and_10 (and_10_out, P2, P1, C0);
  xor xor_6 (S2, or_4_out, P2);
  or or_5 (or_5_out, or_2_out, and_9_out);
  or or_6 (or_6_out, or_3_out, and_10_out);
  // Probe Q(3,0) on or_5_out
  // Probe Q(2,0) on or_6_out
  and and_11 (and_11_out, P3, P2, or_6_out);
  or or_7 (C4, or_1_out, and_11_out);
  xor xor_7 (S4, P4, or_5_out);
  xor xor_8 (S3, or_6_out, P3);
  // Probe Q(4,0) on C4

  // Notes on the sheet:
  //   A3: default 1
  //   A4: default 1
  //   B2: default 1
  //   B1: default 1
  //   node
endmodule
