// Digital circuit SignEx.dig as structural Verilog
module SignEx (
  input  [3:0] B,
  input  [7:0] A,
  input  C__1,
  output [7:0] S,
  output C,
  output [7:0] out_6,
  output out_7
);

  wire [3:0] multiplexer_1_out;
  wire [7:0] bitextender_1_out;

  BitExtender #(.inputBits(4), .outputBits(8)) bitextender_1 (.in(B), .out(bitextender_1_out));
  Multiplexer #(.Bits(4)) multiplexer_1 (.sel(B[3]), .in_0(4'b0000), .in_1(4'b1111), .out(multiplexer_1_out));
  // Probe on bitextender_1_out
  // Probe on {multiplexer_1_out, B}
  // Probe on multiplexer_1_out
  Add #(.Bits(8)) add_1 (.a(A), .b(bitextender_1_out), .c_i(C__1), .s(S), .c_o(C));
  Add #(.Bits(8)) add_2 (.a(A), .b({multiplexer_1_out, B}), .c_i(C__1), .s(out_6), .c_o(out_7));
endmodule
