// Digital circuit Sklansky Adder.dig as structural Verilog
// Example to compare RC and CLA adders.
// {{de Beispiel um RC- und CLA-Addierer zu vergleichen.}}
module Sklansky_Adder (
  input  A4,
  input  B4,
  input  A1,
  input  B1,
  input  A2,
  input  B2,
  input  A3,
  input  B3,
  input  C0,
  output S1,
  output S2,
  output S3,
  output S4,
  output C4
);

  wire C1_0, C1_1, C2_0, C2_1, C3_0, C3_1, C4_0, C4_1, C32_0, C32_1, multiplexer_5_out, multiplexer_8_out,
       S1_0, S1_1, S2_0, S2_1, S3_0, S3_1, S4_0, S4_1, S32_0, S32_1;

  LookUpTable #(.Bits(4)) lookuptable_1 (.in0(A4), .in1(B4), .out({C4_1, C4_0, S4_1, S4_0}));
  LookUpTable #(.Bits(4)) lookuptable_2 (.in0(A3), .in1(B3), .out({C3_1, C3_0, S3_1, S3_0}));
  LookUpTable #(.Bits(4)) lookuptable_3 (.in0(A2), .in1(B2), .out({C2_1, C2_0, S2_1, S2_0}));
  LookUpTable #(.Bits(4)) lookuptable_4 (.in0(A1), .in1(B1), .out({C1_1, C1_0, S1_1, S1_0}));
  Multiplexer multiplexer_1 (.sel(C2_0), .in_0(S3_0), .in_1(S3_1), .out(S32_0));
  Multiplexer multiplexer_2 (.sel(C2_1), .in_0(S3_0), .in_1(S3_1), .out(S32_1));
  Multiplexer multiplexer_3 (.sel(C2_0), .in_0(C3_0), .in_1(C3_1), .out(C32_0));
  Multiplexer multiplexer_4 (.sel(C2_1), .in_0(C3_0), .in_1(C3_1), .out(C32_1));
  Multiplexer multiplexer_5 (.sel(C0), .in_0(C1_0), .in_1(C1_1), .out(multiplexer_5_out));
  // Probe C1 on multiplexer_5_out
  Multiplexer multiplexer_6 (.sel(C0), .in_0(S1_0), .in_1(S1_1), .out(S1));
  Multiplexer multiplexer_7 (.sel(multiplexer_5_out), .in_0(S32_0), .in_1(S32_1), .out(S3));
  Multiplexer multiplexer_8 (.sel(multiplexer_5_out), .in_0(C32_0), .in_1(C32_1), .out(multiplexer_8_out));
  Multiplexer multiplexer_9 (.sel(multiplexer_5_out), .in_0(S2_0), .in_1(S2_1), .out(S2));
  // Probe C3 on multiplexer_8_out
  Multiplexer multiplexer_10 (.sel(multiplexer_8_out), .in_0(C4_0), .in_1(C4_1), .out(C4));
  Multiplexer multiplexer_11 (.sel(multiplexer_8_out), .in_0(S4_0), .in_1(S4_1), .out(S4));

  // Notes on the sheet:
  //   A4: default 1
  //   B1: default 1
  //   B2: default 1
  //   A3: default 1
  //   contents of lookuptable_1 (hex, n*v repeats v):
  //   4,9,9,7
  //   contents of lookuptable_2 (hex, n*v repeats v):
  //   4,9,9,7
  //   contents of lookuptable_3 (hex, n*v repeats v):
  //   4,9,9,7
  //   contents of lookuptable_4 (hex, n*v repeats v):
  //   4,9,9,7
endmodule
