// Digital circuit adder+1.dig as structural Verilog
module adder_1 (
  input  CLR,
  input  in_4,
  input  clr_2,
  input  in_8,
  output [7:0] out_2,
  output [7:0] out_3,
  output [7:0] out_5,
  output [7:0] out_6
);

  wire button_1_out, clk_out, clock_2_out, clock_out, counter_2_ovf;
  wire [0:0] add_2_c_o;
  wire [3:0] add_2_s, add_3_s, counter_2_out, counter_3_out;
  wire [7:0] add_1_s;

  Add #(.Bits(8)) add_1 (.a(out_3), .b(8'h1), .c_i(1'b0), .s(add_1_s));  // open: c_o
  Button button_1 (.out(button_1_out));
  Button clock (.out(clock_out));
  Counter #(.Bits(8)) counter_1 (.en(1'b1), .C(button_1_out), .clr(in_4), .out(out_6));  // open: ovf
  D_FF_AS #(.Bits(8)) d_ff_as_1 (.Set(1'b0), .D(add_1_s), .C(clock_out), .Clr(CLR), .Q(out_3));  // open: nQ
  Button clk (.out(clk_out));
  Counter #(.Bits(4)) counter_2 (.en(1'b1), .C(clk_out), .clr(clr_2), .out(counter_2_out), .ovf(counter_2_ovf));
  Add #(.Bits(4)) add_2 (.a(out_2[3:0]), .b(4'b0001), .c_i(1'b0), .s(add_2_s), .c_o(add_2_c_o[0]));
  Button clock_2 (.out(clock_2_out));
  Counter #(.Bits(4)) counter_3 (.en(counter_2_ovf), .C(clk_out), .clr(clr_2), .out(counter_3_out));  // open: ovf
  Add #(.Bits(4)) add_3 (.a(out_2[7:4]), .b({3'b000, add_2_c_o[0]}), .c_i(1'b0), .s(add_3_s));  // open: c_o
  D_FF_AS #(.Bits(4)) d_ff_as_2 (.Set(1'b0), .D(counter_3_out), .C(clk_out), .Clr(clr_2), .Q(out_5[7:4]));  // open: nQ
  D_FF_AS #(.Bits(4)) d_ff_as_3 (.Set(1'b0), .D(counter_2_out), .C(clk_out), .Clr(clr_2), .Q(out_5[3:0]));  // open: nQ
  D_FF_AS #(.Bits(4)) d_ff_as_4 (.Set(1'b0), .D(add_3_s), .C(clock_2_out), .Clr(in_8), .Q(out_2[7:4]));  // open: nQ
  D_FF_AS #(.Bits(4)) d_ff_as_5 (.Set(1'b0), .D(add_2_s), .C(clock_2_out), .Clr(in_8), .Q(out_2[3:0]));  // open: nQ

  // Notes on the sheet:
  //   8 bit
  //   8 bit adder+1
  //   8 bit counter
  //   (4+4) bit counter
  //   4 bit
  //   (4+4) bit adder+1
endmodule
