// Digital circuit shift register.dig as structural Verilog
module shift_register (
  input  [7:0] D_S,
  input  [4:0] shift_LL,
  input  [3:0] shift_LA,
  input  [3:0] shift_RA,
  input  [3:0] D_R,
  input  Load_L,
  input  [3:0] D_L,
  input  CLK_L,
  input  CLK_R,
  input  Load_R,
  output [7:0] Q_LL,
  output [7:0] Q_LR,
  output [7:0] Q_RA,
  output [3:0] P,
  output [3:0] Q,
  output max
);

  wire multiplexer_1_out, multiplexer_2_out, multiplexer_3_out, multiplexer_4_out, multiplexer_5_out,
       multiplexer_6_out, multiplexer_7_out, multiplexer_8_out;

  BarrelShifter #(.Bits(8), .barrelSigned("true")) barrelshifter_1 (.in(D_S), .shift(shift_LL), .out(Q_LL));
  Multiplexer multiplexer_1 (.sel(Load_L), .in_0(Q[2]), .in_1(D_L[3]), .out(multiplexer_1_out));
  Multiplexer multiplexer_2 (.sel(Load_L), .in_0(Q[1]), .in_1(D_L[2]), .out(multiplexer_2_out));
  Multiplexer multiplexer_3 (.sel(Load_L), .in_0(Q[0]), .in_1(D_L[1]), .out(multiplexer_3_out));
  Multiplexer multiplexer_4 (.sel(Load_L), .in_0(1'b0), .in_1(D_L[0]), .out(multiplexer_4_out));
  D_FF d_ff_1 (.D(multiplexer_1_out), .C(CLK_L), .Q(Q[3]));  // open: nQ
  D_FF d_ff_2 (.D(multiplexer_2_out), .C(CLK_L), .Q(Q[2]));  // open: nQ
  D_FF d_ff_3 (.D(multiplexer_3_out), .C(CLK_L), .Q(Q[1]));  // open: nQ
  D_FF d_ff_4 (.D(multiplexer_4_out), .C(CLK_L), .Q(Q[0]));  // open: nQ
  xor xor_1 (max, Q[3], Q[2]);
  BarrelShifter #(.Bits(8), .barrelShifterMode("arithmetic"), .direction("right")) barrelshifter_2 (
    .in(D_S), .shift(shift_RA), .out(Q_RA));
  Multiplexer multiplexer_5 (.sel(Load_R), .in_0(P[3]), .in_1(D_R[3]), .out(multiplexer_5_out));
  Multiplexer multiplexer_6 (.sel(Load_R), .in_0(P[3]), .in_1(D_R[2]), .out(multiplexer_6_out));
  Multiplexer multiplexer_7 (.sel(Load_R), .in_0(P[2]), .in_1(D_R[1]), .out(multiplexer_7_out));
  Multiplexer multiplexer_8 (.sel(Load_R), .in_0(P[1]), .in_1(D_R[0]), .out(multiplexer_8_out));
  BarrelShifter #(.Bits(8), .barrelShifterMode("arithmetic")) barrelshifter_3 (.in(D_S), .shift(shift_LA), .out(Q_LR));
  D_FF d_ff_5 (.D(multiplexer_5_out), .C(CLK_R), .Q(P[3]));  // open: nQ
  D_FF d_ff_6 (.D(multiplexer_6_out), .C(CLK_R), .Q(P[2]));  // open: nQ
  D_FF d_ff_7 (.D(multiplexer_7_out), .C(CLK_R), .Q(P[1]));  // open: nQ
  D_FF d_ff_8 (.D(multiplexer_8_out), .C(CLK_R), .Q(P[0]));  // open: nQ
endmodule
