// Digital circuit Division.dig as structural Verilog
module Division (
  input  X_4,
  input  X_1,
  input  X_2,
  input  X_3,
  input  X_5,
  input  Y_1,
  input  Y_2,
  input  Y_3,
  input  X_6,
  input  Y_0,
  input  X_0,
  output Q_0,
  output Q_1,
  output Q_2,
  output Q_3,
  output R_4,
  output R_5,
  output R_6
);

  wire [3:0] add_2_s, add_3_s, xor_4_out, xor_8_out, xor_11_out, xor_13_out;
  wire [3:1] add_1_s;
  wire [3:3] add_1_s_2, add_4_s;

  xor xor_1 (xor_4_out[0], Y_3, 1'b1);
  xor xor_2 (xor_4_out[1], Y_2, 1'b1);
  xor xor_3 (xor_4_out[2], Y_1, 1'b1);
  xor xor_4 (xor_4_out[3], Y_0, 1'b1);
  Add #(.Bits(4)) add_1 (.a({X_0, X_1, X_2, X_3}), .b(xor_4_out), .c_i(1'b1), .s({add_1_s_2[3], add_1_s}), .c_o(Q_0));
  xor xor_5 (xor_8_out[0], Q_0, Y_3);
  xor xor_6 (xor_8_out[1], Q_0, Y_2);
  xor xor_7 (xor_8_out[2], Q_0, Y_1);
  xor xor_8 (xor_8_out[3], Q_0, Y_0);
  Add #(.Bits(4)) add_2 (.a({add_1_s, X_4}), .b(xor_8_out), .c_i(Q_0), .s(add_2_s), .c_o(Q_1));
  xor xor_9 (xor_11_out[0], Q_1, Y_3);
  xor xor_10 (xor_11_out[1], Q_1, Y_2);
  xor xor_11 (xor_11_out[2], Q_1, Y_1);
  xor xor_12 (xor_11_out[3], Q_1, Y_0);
  Add #(.Bits(4)) add_3 (.a({add_2_s[2:0], X_5}), .b(xor_11_out), .c_i(Q_1), .s(add_3_s), .c_o(Q_2));
  xor xor_13 (xor_13_out[0], Q_2, Y_3);
  xor xor_14 (xor_13_out[1], Q_2, Y_2);
  xor xor_15 (xor_13_out[2], Q_2, Y_1);
  xor xor_16 (xor_13_out[3], Q_2, Y_0);
  Add #(.Bits(4)) add_4 (
    .a({add_3_s[2:0], X_6}), .b(xor_13_out), .c_i(Q_2), .s({add_4_s[3], R_4, R_5, R_6}), .c_o(Q_3));

  // Notes on the sheet:
  //   X_4: First number to multiply.
  //   {{de Erste zu multiplizierende 4 Bit Zahl.}}
  //   X_5: Second number to multiply.
  //   {{de Zweite zu multiplizierende 4 Bit Zahl.}}
  //   Q_0: The result of the multiply operation.
  //   {{de Das 8-Bit Ergebnis der Multiplikation}}
  //   X_6: Second number to multiply.
  //   {{de Zweite zu multiplizierende 4 Bit Zahl.}}
endmodule
