// Digital circuit DivisionRC.dig as structural Verilog
module DivisionRC (
  input  [4:0] _5_hY,
  input  [4:0] _5_hX,
  input  CLK,
  input  Init,
  output [4:0] Q,
  output [3:0] R
);

  wire not_3_out;
  wire [0:0] barrelshifter_1_out, barrelshifter_1_out_2, not_2_out;
  wire [4:0] add_1_s, d_ff_1_q, d_ff_2_q, multiplexer_1_out, multiplexer_2_out, not_1_out;

  Multiplexer #(.Bits(5)) multiplexer_1 (
    .sel(Init), .in_0({R, barrelshifter_1_out_2[0]}), .in_1(_5_hX), .out(multiplexer_1_out));
  Multiplexer #(.Bits(5)) multiplexer_2 (.sel(not_3_out), .in_0(_5_hY), .in_1(not_1_out), .out(multiplexer_2_out));
  assign not_1_out = ~_5_hY;  // Not not_1, 5 bits wide
  // Probe on multiplexer_1_out
  // Probe on multiplexer_2_out
  Add #(.Bits(5)) add_1 (.a(multiplexer_1_out), .b(multiplexer_2_out), .c_i(not_3_out), .s(add_1_s));  // open: c_o
  // Probe on add_1_s
  D_FF #(.Bits(5)) d_ff_1 (.D(add_1_s), .C(CLK), .Q(d_ff_1_q));  // open: nQ
  D_FF #(.Bits(5)) d_ff_2 (.D(Q), .C(CLK), .Q(d_ff_2_q));  // open: nQ
  not not_2 (not_2_out[0], CLK);
  // Probe on d_ff_1_q
  // Probe on d_ff_2_q
  BarrelShifter #(.Bits(10), .barrelShifterMode("rotate")) barrelshifter_1 (
    .in({d_ff_1_q, d_ff_2_q}), .shift({3'b000, not_2_out[0]}),
    .out({R, barrelshifter_1_out_2[0], Q[4:1], barrelshifter_1_out[0]}));
  not not_3 (not_3_out, barrelshifter_1_out[0]);
  xor xor_1 (Q[0], not_3_out, Init);
  // Probe on {R, barrelshifter_1_out_2[0]}
  // Probe on Q[4:1]

  // Other names for the same wires on the sheet: Ini = Init
endmodule
