// Digital circuit Multiply.dig as structural Verilog
// Simple 4-bit multiplier built from three 4-bit adders. 
// The actual 1-bit multiplications are implemented by the AND gates.
// {{de Einfacher 4-Bit Multiplikator aufgebaut aus drei 4-Bit
// Addierern. Die eigentlichen 1-Bit Multiplikationen 
// werden durch die Und-Gatter implementiert.}}
module Multiply (
  input  P_0,
  input  P_1,
  input  P_2,
  input  P_3,
  input  Q_0,
  input  Q_1,
  input  Q_2,
  input  Q_3,
  output S_0,
  output S_1,
  output S_2,
  output S_3,
  output S_4,
  output S_5,
  output S_6,
  output S_7,
  output out_17,
  output out_18,
  output out_19,
  output out_20,
  output out_21,
  output out_22,
  output out_23,
  output out_24
);

  wire [2:0] and_5_out;
  wire [3:0] add_1_c_o, and_2_out, and_3_out, and_4_out;
  wire [3:1] add_2_s;
  wire [3:3] add_2_c_o;

  and and_1 (S_0, P_0, Q_0);
  and and_2 (and_2_out[0], P_0, Q_1);
  and and_3 (and_3_out[0], P_0, Q_2);
  and and_4 (and_4_out[0], P_0, Q_3);
  and and_5 (and_5_out[0], P_1, Q_0);
  and and_6 (and_2_out[1], P_1, Q_1);
  and and_7 (and_3_out[1], P_1, Q_2);
  and and_8 (and_4_out[1], P_1, Q_3);
  and and_9 (and_5_out[1], P_2, Q_0);
  and and_10 (and_2_out[2], P_2, Q_1);
  and and_11 (and_3_out[2], P_2, Q_2);
  and and_12 (and_4_out[2], P_2, Q_3);
  and and_13 (and_5_out[2], P_3, Q_0);
  and and_14 (and_2_out[3], P_3, Q_1);
  and and_15 (and_3_out[3], P_3, Q_2);
  and and_16 (and_4_out[3], P_3, Q_3);
  Add #(.Bits(4)) add_1 (
    .a({1'b0, and_5_out}), .b(and_2_out), .c_i(1'b0), .s({add_1_c_o[2:0], S_1}), .c_o(add_1_c_o[3]));
  Add #(.Bits(4)) add_2 (.a(add_1_c_o), .b(and_3_out), .c_i(1'b0), .s({add_2_s, S_2}), .c_o(add_2_c_o[3]));
  Add #(.Bits(4)) add_3 (.a({add_2_c_o[3], add_2_s}), .b(and_4_out), .c_i(1'b0), .s({S_6, S_5, S_4, S_3}), .c_o(S_7));
  Mul #(.Bits(4)) mul_1 (
    .a({P_3, P_2, P_1, P_0}), .b({Q_3, Q_2, Q_1, Q_0}),
    .mul({out_24, out_23, out_22, out_21, out_20, out_19, out_18, out_17}));

  // Other names for the same wires on the sheet: p0 = P_0; p1 = P_1; p2 = P_2; p3 = P_3; q0 = Q_0; q1 = Q_1; q2 = Q_2;
  //   q3 = Q_3

  // Notes on the sheet:
  //   P_0: First number to multiply.
  //   {{de Erste zu multiplizierende 4 Bit Zahl.}}
  //   Q_0: Second number to multiply.
  //   {{de Zweite zu multiplizierende 4 Bit Zahl.}}
  //   S_0: The result of the multiply operation.
  //   {{de Das 8-Bit Ergebnis der Multiplikation}}
endmodule

/* Test case:
  P_3 P_2 P_1 P_0   Q_3 Q_2 Q_1 Q_0   S_7 S_6 S_5 S_4 S_3 S_2 S_1 S_0
loop(P,16)
 loop(Q,16)
  bits(4,P)         bits(4,Q)         bits(8,P*Q)
 end loop
end loop
*/
