// Digital circuit MultiplyBooth.dig as structural Verilog
module MultiplyBooth (
  input  [4:0] _5_hX,
  input  [4:0] _5_hY,
  input  CLK,
  input  Init,
  output [8:0] Z
);

  wire decoder_1_out_2;
  wire [0:0] not_2_out;
  wire [1:0] multiplexer_2_out;
  wire [4:0] add_1_s, d_ff_1_q, multiplexer_1_out, not_1_out;
  wire [5:0] barrelshifter_1_out, d_ff_2_q;

  Multiplexer #(.Selector_Bits(2), .Bits(5)) multiplexer_1 (
    .sel(multiplexer_2_out), .in_0({5{1'b0}}), .in_1(_5_hX), .in_2(not_1_out), .in_3({5{1'b0}}),
    .out(multiplexer_1_out));
  // Probe on not_1_out
  assign not_1_out = ~_5_hX;  // Not not_1, 5 bits wide
  Decoder #(.Selector_Bits(2)) decoder_1 (
    .sel(multiplexer_2_out), .out_2(decoder_1_out_2));  // open: out_0, out_1, out_3
  // Probe on multiplexer_2_out
  // Probe on multiplexer_1_out
  Add #(.Bits(5)) add_1 (.a(Z[8:4]), .b(multiplexer_1_out), .c_i(decoder_1_out_2), .s(add_1_s));  // open: c_o
  not not_2 (not_2_out[0], CLK);
  // Probe on add_1_s
  D_FF #(.Bits(5)) d_ff_1 (.D(add_1_s), .C(CLK), .Q(d_ff_1_q));  // open: nQ
  D_FF #(.Bits(6)) d_ff_2 (.D({Z[3:0], multiplexer_2_out}), .C(CLK), .Q(d_ff_2_q));  // open: nQ
  // Probe on d_ff_1_q
  // Probe on d_ff_2_q
  BarrelShifter #(.Bits(11), .barrelShifterMode("arithmetic"), .direction("right")) barrelshifter_1 (
    .in({d_ff_1_q, d_ff_2_q}), .shift({3'b000, not_2_out[0]}), .out({Z[8:4], barrelshifter_1_out}));
  // Probe on {Z[8:4], barrelshifter_1_out}
  // Probe on Z[8:4]
  Multiplexer #(.Bits(6)) multiplexer_2 (
    .sel(Init), .in_0(barrelshifter_1_out), .in_1({_5_hY, 1'b0}), .out({Z[3:0], multiplexer_2_out}));
  // Probe on {Z[3:0], multiplexer_2_out}
endmodule
