// Digital circuit MultiplyRC.dig as structural Verilog
module MultiplyRC (
  input  [3:0] _4_hX,
  input  [3:0] _4_hY,
  input  CLK,
  input  Init,
  output [7:0] Z
);

  wire [0:0] not_1_out;
  wire [3:0] d_ff_2_q, multiplexer_1_out;
  wire [4:0] add_1_s, d_ff_1_q;
  wire [8:0] barrelshifter_1_out;

  Multiplexer #(.Bits(4)) multiplexer_1 (.sel(Z[0]), .in_0(4'b0000), .in_1(_4_hX), .out(multiplexer_1_out));
  Add #(.Bits(4)) add_1 (.a(Z[7:4]), .b(multiplexer_1_out), .c_i(1'b0), .s(add_1_s[3:0]), .c_o(add_1_s[4]));
  not not_1 (not_1_out[0], CLK);
  // Probe on add_1_s[3:0]
  // Probe on Z[3:0]
  D_FF #(.Bits(5)) d_ff_1 (.D(add_1_s), .C(CLK), .Q(d_ff_1_q));  // open: nQ
  D_FF #(.Bits(4)) d_ff_2 (.D(Z[3:0]), .C(CLK), .Q(d_ff_2_q));  // open: nQ
  // Probe on d_ff_1_q
  // Probe on d_ff_2_q
  BarrelShifter #(.Bits(9), .direction("right")) barrelshifter_1 (
    .in({d_ff_1_q, d_ff_2_q}), .shift({3'b000, not_1_out[0]}),
    .out({barrelshifter_1_out[8], Z[7:4], barrelshifter_1_out[3:0]}));
  // Probe on {barrelshifter_1_out[8], Z[7:4], barrelshifter_1_out[3:0]}
  Multiplexer #(.Bits(4)) multiplexer_2 (.sel(Init), .in_0(barrelshifter_1_out[3:0]), .in_1(_4_hY), .out(Z[3:0]));
  // Probe on Z[7:4]
  // Probe on Z[3:0]
endmodule
