// Digital circuit MultiplySign.dig as structural Verilog
module MultiplySign (
  input  P_4,
  input  Q_4,
  input  P_0,
  input  P_1,
  input  P_2,
  input  P_3,
  input  Q_0,
  input  Q_1,
  input  Q_2,
  input  Q_3,
  output S_0,
  output S_1,
  output S_2,
  output S_3,
  output S_4,
  output S_5,
  output S_6,
  output S_7,
  output out_19,
  output out_20,
  output out_21,
  output out_22,
  output out_23,
  output out_24,
  output out_25,
  output out_26,
  output out_27,
  output out_28,
  output S_8,
  output S_9
);

  wire [2:0] and_13_out;
  wire [3:0] add_1_s, add_2_s, add_5_s, and_14_out, and_15_out, and_16_out, and_18_out, and_19_out,
       bitextender_1_out, bitextender_2_out;
  wire [8:0] and_17_out;
  wire [8:8] add_5_c_o;
  wire [9:0] not_1_out;

  and and_1 (and_17_out[0], P_0, Q_0);
  and and_2 (and_14_out[0], P_0, Q_1);
  and and_3 (and_15_out[0], P_0, Q_2);
  and and_4 (and_16_out[0], P_0, Q_3);
  and and_5 (and_13_out[0], P_1, Q_0);
  and and_6 (and_14_out[1], P_1, Q_1);
  and and_7 (and_15_out[1], P_1, Q_2);
  and and_8 (and_16_out[1], P_1, Q_3);
  and and_9 (and_13_out[1], P_2, Q_0);
  and and_10 (and_14_out[2], P_2, Q_1);
  and and_11 (and_15_out[2], P_2, Q_2);
  and and_12 (and_16_out[2], P_2, Q_3);
  and and_13 (and_13_out[2], P_3, Q_0);
  and and_14 (and_14_out[3], P_3, Q_1);
  and and_15 (and_15_out[3], P_3, Q_2);
  and and_16 (and_16_out[3], P_3, Q_3);
  Add #(.Bits(4)) add_1 (
    .a({1'b0, and_13_out}), .b(and_14_out), .c_i(1'b0), .s({add_1_s[2:0], and_17_out[1]}), .c_o(add_1_s[3]));
  Add #(.Bits(4)) add_2 (.a(add_1_s), .b(and_15_out), .c_i(1'b0), .s({add_2_s[2:0], and_17_out[2]}), .c_o(add_2_s[3]));
  Add #(.Bits(4)) add_3 (.a(add_2_s), .b(and_16_out), .c_i(1'b0), .s(and_17_out[6:3]), .c_o(and_17_out[7]));
  and and_17 (and_17_out[8], P_4, Q_4);
  BitExtender #(.inputBits(1), .outputBits(4)) bitextender_1 (.in(Q_4), .out(bitextender_1_out));
  BitExtender #(.inputBits(1), .outputBits(4)) bitextender_2 (.in(P_4), .out(bitextender_2_out));
  assign and_18_out = {P_3, P_2, P_1, P_0} & bitextender_1_out;  // And and_18, 4 bits wide
  assign and_19_out = {Q_3, Q_2, Q_1, Q_0} & bitextender_2_out;  // And and_19, 4 bits wide
  Add #(.Bits(10)) add_4 (
    .a({1'b0, and_17_out}), .b(not_1_out), .c_i(1'b1), .s({S_9, S_8, S_7, S_6, S_5, S_4, S_3, S_2, S_1, S_0}));  // open: c_o
  assign not_1_out = ~{1'b0, add_5_c_o[8], add_5_s, 4'b0000};  // Not not_1, 10 bits wide
  Add #(.Bits(4)) add_5 (.a(and_18_out), .b(and_19_out), .c_i(1'b0), .s(add_5_s), .c_o(add_5_c_o[8]));
  // Probe on add_5_s
  Mul #(.Signed("true"), .Bits(5)) mul_1 (
    .a({P_4, P_3, P_2, P_1, P_0}), .b({Q_4, Q_3, Q_2, Q_1, Q_0}),
    .mul({out_28, out_27, out_26, out_25, out_24, out_23, out_22, out_21, out_20, out_19}));
  // Probe on {1'b0, add_5_c_o[8], add_5_s, 4'b0000}

  // Other names for the same wires on the sheet: p0 = P_0; p1 = P_1; p2 = P_2; p3 = P_3; p4 = P_4; q0 = Q_0; q1 = Q_1;
  //   q2 = Q_2; q3 = Q_3; q4 = Q_4

  // Notes on the sheet:
  //   P_4: First number to multiply.
  //   {{de Erste zu multiplizierende 4 Bit Zahl.}}
  //   Q_4: Second number to multiply.
  //   {{de Zweite zu multiplizierende 4 Bit Zahl.}}
  //   P_0: First number to multiply.
  //   {{de Erste zu multiplizierende 4 Bit Zahl.}}
  //   Q_0: Second number to multiply.
  //   {{de Zweite zu multiplizierende 4 Bit Zahl.}}
  //   S_0: The result of the multiply operation.
  //   {{de Das 8-Bit Ergebnis der Multiplikation}}
endmodule
