// Digital circuit MultiplySign_Baugh-Wooley.dig as structural Verilog
// Simple 4-bit multiplier built from three 4-bit adders. 
// The actual 1-bit multiplications are implemented by the AND gates.
// {{de Einfacher 4-Bit Multiplikator aufgebaut aus drei 4-Bit
// Addierern. Die eigentlichen 1-Bit Multiplikationen 
// werden durch die Und-Gatter implementiert.}}
module MultiplySign_Baugh_Wooley (
  input  P_0,
  input  P_1,
  input  P_2,
  input  P_3,
  input  Q_0,
  input  Q_1,
  input  Q_2,
  input  Q_3,
  output out_9,
  output out_10,
  output out_11,
  output out_12,
  output out_13,
  output out_14,
  output out_15,
  output out_16,
  output S_0,
  output S_1,
  output S_2,
  output S_3,
  output S_4,
  output S_5,
  output S_6,
  output S_7
);

  wire add_1_c_o, add_2_c_o, add_2_s, add_3_c_o, add_3_s, add_4_c_o, add_5_c_o, add_5_s, add_6_c_o, add_6_s,
       nP0Q3, nP1Q3, nP2Q3, nP3Q0, nP3Q1, nP3Q2, P0Q1, P0Q2, P1Q0, P1Q1, P1Q2, P2Q0, P2Q1, P2Q2, P3Q3;
  wire [1:0] add_8_s;
  wire [2:0] add_7_c_o;

  and and_1 (S_0, P_0, Q_0);
  and and_2 (P0Q1, P_0, Q_1);
  and and_3 (P0Q2, P_0, Q_2);
  nand nand_1 (nP0Q3, P_0, Q_3);
  and and_4 (P1Q0, P_1, Q_0);
  and and_5 (P1Q1, P_1, Q_1);
  and and_6 (P1Q2, P_1, Q_2);
  nand nand_2 (nP1Q3, P_1, Q_3);
  and and_7 (P2Q0, P_2, Q_0);
  and and_8 (P2Q1, P_2, Q_1);
  and and_9 (P2Q2, P_2, Q_2);
  nand nand_3 (nP2Q3, P_2, Q_3);
  nand nand_4 (nP3Q0, P_3, Q_0);
  nand nand_5 (nP3Q1, P_3, Q_1);
  nand nand_6 (nP3Q2, P_3, Q_2);
  and and_10 (P3Q3, P_3, Q_3);
  Add add_1 (.a(P1Q0), .b(P0Q1), .c_i(1'b0), .s(S_1), .c_o(add_1_c_o));
  Add add_2 (.a(P2Q0), .b(P1Q1), .c_i(1'b0), .s(add_2_s), .c_o(add_2_c_o));
  Add add_3 (.a(nP3Q0), .b(P2Q1), .c_i(1'b0), .s(add_3_s), .c_o(add_3_c_o));
  Mul #(.Signed("true"), .Bits(4)) mul_1 (
    .a({P_3, P_2, P_1, P_0}), .b({Q_3, Q_2, Q_1, Q_0}),
    .mul({out_16, out_15, out_14, out_13, out_12, out_11, out_10, out_9}));
  Add add_4 (.a(P0Q2), .b(add_2_s), .c_i(add_1_c_o), .s(S_2), .c_o(add_4_c_o));
  Add add_5 (.a(P1Q2), .b(add_3_s), .c_i(add_2_c_o), .s(add_5_s), .c_o(add_5_c_o));
  Add add_6 (.a(P2Q2), .b(nP3Q1), .c_i(add_3_c_o), .s(add_6_s), .c_o(add_6_c_o));
  Add add_7 (.a(nP0Q3), .b(add_5_s), .c_i(add_4_c_o), .s(S_3), .c_o(add_7_c_o[0]));
  Add add_8 (.a(nP1Q3), .b(add_6_s), .c_i(add_5_c_o), .s(add_8_s[0]), .c_o(add_7_c_o[1]));
  Add add_9 (.a(nP2Q3), .b(nP3Q2), .c_i(add_6_c_o), .s(add_8_s[1]), .c_o(add_7_c_o[2]));
  Add #(.Bits(4)) add_10 (
    .a({1'b0, add_7_c_o}), .b({1'b1, P3Q3, add_8_s}), .c_i(1'b1), .s({S_7, S_6, S_5, S_4}));  // open: c_o

  // Other names for the same wires on the sheet: p0 = P_0; P0Q0 = S_0; p1 = P_1; p2 = P_2; p3 = P_3; q0 = Q_0;
  //   q1 = Q_1; q2 = Q_2; q3 = Q_3

  // Notes on the sheet:
  //   P_0: First number to multiply.
  //   {{de Erste zu multiplizierende 4 Bit Zahl.}}
  //   Q_0: Second number to multiply.
  //   {{de Zweite zu multiplizierende 4 Bit Zahl.}}
  //   S_0: The result of the multiply operation.
  //   {{de Das 8-Bit Ergebnis der Multiplikation}}
endmodule
