// Digital circuit Multiply_Wallace.dig as structural Verilog
// Simple 4-bit multiplier built from three 4-bit adders. 
// The actual 1-bit multiplications are implemented by the AND gates.
// {{de Einfacher 4-Bit Multiplikator aufgebaut aus drei 4-Bit
// Addierern. Die eigentlichen 1-Bit Multiplikationen 
// werden durch die Und-Gatter implementiert.}}
module Multiply_Wallace (
  input  P_0,
  input  P_1,
  input  P_2,
  input  P_3,
  input  Q_0,
  input  Q_1,
  input  Q_2,
  input  Q_3,
  output S_0,
  output S_1,
  output S_2,
  output S_3,
  output S_4,
  output S_5,
  output S_6,
  output S_7,
  output out_17,
  output out_18,
  output out_19,
  output out_20,
  output out_21,
  output out_22,
  output out_23,
  output out_24
);

  wire add_1_c_o, add_2_c_o, add_2_s, add_3_c_o, add_3_s, add_4_c_o, add_4_s, P0Q1, P0Q2, P0Q3, P1Q0, P1Q1,
       P1Q2, P1Q3, P2Q0, P2Q1, P2Q2, P2Q3, P3Q0, P3Q1, P3Q2, P3Q3;
  wire [2:0] add_6_s;
  wire [3:0] add_5_c_o;

  and and_1 (S_0, P_0, Q_0);
  and and_2 (P0Q1, P_0, Q_1);
  and and_3 (P0Q2, P_0, Q_2);
  and and_4 (P0Q3, P_0, Q_3);
  and and_5 (P1Q0, P_1, Q_0);
  and and_6 (P1Q1, P_1, Q_1);
  and and_7 (P1Q2, P_1, Q_2);
  and and_8 (P1Q3, P_1, Q_3);
  and and_9 (P2Q0, P_2, Q_0);
  and and_10 (P2Q1, P_2, Q_1);
  and and_11 (P2Q2, P_2, Q_2);
  and and_12 (P2Q3, P_2, Q_3);
  and and_13 (P3Q0, P_3, Q_0);
  and and_14 (P3Q1, P_3, Q_1);
  and and_15 (P3Q2, P_3, Q_2);
  and and_16 (P3Q3, P_3, Q_3);
  Add add_1 (.a(P1Q0), .b(P0Q1), .c_i(1'b0), .s(S_1), .c_o(add_1_c_o));
  Add add_2 (.a(P2Q0), .b(P1Q1), .c_i(P0Q2), .s(add_2_s), .c_o(add_2_c_o));
  Add add_3 (.a(P3Q0), .b(P2Q1), .c_i(P1Q2), .s(add_3_s), .c_o(add_3_c_o));
  Add add_4 (.a(P3Q1), .b(P2Q2), .c_i(1'b0), .s(add_4_s), .c_o(add_4_c_o));
  Mul #(.Bits(4)) mul_1 (
    .a({P_3, P_2, P_1, P_0}), .b({Q_3, Q_2, Q_1, Q_0}),
    .mul({out_24, out_23, out_22, out_21, out_20, out_19, out_18, out_17}));
  Add add_5 (.a(add_1_c_o), .b(add_2_s), .c_i(1'b0), .s(S_2), .c_o(add_5_c_o[0]));
  Add add_6 (.a(add_2_c_o), .b(add_3_s), .c_i(P0Q3), .s(add_6_s[0]), .c_o(add_5_c_o[1]));
  Add add_7 (.a(add_4_s), .b(add_3_c_o), .c_i(P1Q3), .s(add_6_s[1]), .c_o(add_5_c_o[2]));
  Add add_8 (.a(add_4_c_o), .b(P3Q2), .c_i(P2Q3), .s(add_6_s[2]), .c_o(add_5_c_o[3]));
  Add #(.Bits(4)) add_9 (.a(add_5_c_o), .b({P3Q3, add_6_s}), .c_i(1'b0), .s({S_6, S_5, S_4, S_3}), .c_o(S_7));

  // Other names for the same wires on the sheet: p0 = P_0; P0Q0 = S_0; p1 = P_1; p2 = P_2; p3 = P_3; q0 = Q_0;
  //   q1 = Q_1; q2 = Q_2; q3 = Q_3

  // Notes on the sheet:
  //   P_0: First number to multiply.
  //   {{de Erste zu multiplizierende 4 Bit Zahl.}}
  //   Q_0: Second number to multiply.
  //   {{de Zweite zu multiplizierende 4 Bit Zahl.}}
  //   S_0: The result of the multiply operation.
  //   {{de Das 8-Bit Ergebnis der Multiplikation}}
endmodule

/* Test case:
  P_3 P_2 P_1 P_0   Q_3 Q_2 Q_1 Q_0   S_7 S_6 S_5 S_4 S_3 S_2 S_1 S_0
loop(P,16)
 loop(Q,16)
  bits(4,P)         bits(4,Q)         bits(8,P*Q)
 end loop
end loop
*/
