// Digital circuit Multiply_absolute.dig as structural Verilog
module Multiply_absolute (
  input  P_2,
  input  Q_2,
  input  P_4,
  input  P_0,
  input  P_1,
  input  P_3,
  input  Q_0,
  input  Q_4,
  input  Q_3,
  input  Q_1,
  output S_0,
  output S_1,
  output S_2,
  output S_3,
  output S_4,
  output S_5,
  output S_6,
  output S_7,
  output out_11,
  output out_12,
  output out_13,
  output out_14,
  output out_15,
  output out_16,
  output S_8,
  output out_18,
  output out_19,
  output out_20,
  output out_21
);

  wire and_1_out, and_2_out, and_3_out, and_4_out, and_5_out, and_6_out, and_7_out, and_8_out, and_9_out,
       and_10_out, and_11_out, and_12_out, and_13_out, and_14_out, and_15_out, and_16_out, or_1_out,
       or_2_out, or_3_out, or_4_out, or_5_out, or_6_out, or_7_out, or_8_out, or_9_out, or_10_out, or_11_out,
       or_12_out, or_13_out;
  wire [3:0] xor_4_out, xor_8_out;
  wire [7:0] _4_unsign_mul;

  or or_1 (or_1_out, P_2, or_3_out);
  or or_2 (or_2_out, Q_2, or_5_out);
  or or_3 (or_3_out, P_1, or_4_out);
  or or_4 (or_4_out, P_0, 1'b0);
  or or_5 (or_5_out, Q_1, or_6_out);
  or or_6 (or_6_out, Q_0, 1'b0);
  and and_1 (and_1_out, P_4, or_1_out);
  and and_2 (and_2_out, P_4, or_3_out);
  and and_3 (and_3_out, P_4, or_4_out);
  and and_4 (and_4_out, P_4, 1'b0);
  and and_5 (and_5_out, Q_4, or_2_out);
  and and_6 (and_6_out, Q_4, or_5_out);
  and and_7 (and_7_out, Q_4, or_6_out);
  and and_8 (and_8_out, Q_4, 1'b0);
  xor xor_1 (xor_4_out[3], and_1_out, P_3);
  xor xor_2 (xor_4_out[2], and_2_out, P_2);
  xor xor_3 (xor_4_out[1], and_3_out, P_1);
  xor xor_4 (xor_4_out[0], and_4_out, P_0);
  xor xor_5 (xor_8_out[3], and_5_out, Q_3);
  xor xor_6 (xor_8_out[2], and_6_out, Q_2);
  xor xor_7 (xor_8_out[1], and_7_out, Q_1);
  xor xor_8 (xor_8_out[0], and_8_out, Q_0);
  xor xor_9 (S_8, P_4, Q_4);
  Mul #(.Signed("true"), .Bits(5)) _5_sign (
    .a({P_4, P_3, P_2, P_1, P_0}), .b({Q_4, Q_3, Q_2, Q_1, Q_0}),
    .mul({out_20, out_21, out_11, out_12, out_13, out_14, out_15, out_16, out_18, out_19}));
  Mul #(.Bits(4)) _4_unsign (.a(xor_4_out), .b(xor_8_out), .mul(_4_unsign_mul));
  or or_7 (or_7_out, _4_unsign_mul[6], or_8_out);
  or or_8 (or_8_out, _4_unsign_mul[5], or_9_out);
  or or_9 (or_9_out, _4_unsign_mul[4], or_10_out);
  or or_10 (or_10_out, _4_unsign_mul[3], or_11_out);
  or or_11 (or_11_out, _4_unsign_mul[2], or_12_out);
  or or_12 (or_12_out, _4_unsign_mul[1], or_13_out);
  or or_13 (or_13_out, _4_unsign_mul[0], 1'b0);
  and and_9 (and_9_out, S_8, or_7_out);
  and and_10 (and_10_out, S_8, or_8_out);
  and and_11 (and_11_out, S_8, or_9_out);
  and and_12 (and_12_out, S_8, or_10_out);
  and and_13 (and_13_out, S_8, or_11_out);
  and and_14 (and_14_out, S_8, or_12_out);
  and and_15 (and_15_out, S_8, or_13_out);
  and and_16 (and_16_out, S_8, 1'b0);
  xor xor_10 (S_7, and_9_out, _4_unsign_mul[7]);
  xor xor_11 (S_6, and_10_out, _4_unsign_mul[6]);
  xor xor_12 (S_5, and_11_out, _4_unsign_mul[5]);
  xor xor_13 (S_4, and_12_out, _4_unsign_mul[4]);
  xor xor_14 (S_3, and_13_out, _4_unsign_mul[3]);
  xor xor_15 (S_2, and_14_out, _4_unsign_mul[2]);
  xor xor_16 (S_1, and_15_out, _4_unsign_mul[1]);
  xor xor_17 (S_0, and_16_out, _4_unsign_mul[0]);

  // Other names for the same wires on the sheet: p0 = P_0; p1 = P_1; p2 = P_2; p3 = P_3; p4 = P_4; q0 = Q_0; q1 = Q_1;
  //   q2 = Q_2; q3 = Q_3; q4 = Q_4

  // Notes on the sheet:
  //   S_0: The result of the multiply operation.
  //   {{de Das 8-Bit Ergebnis der Multiplikation}}
  //   P_0: First number to multiply.
  //   {{de Erste zu multiplizierende 4 Bit Zahl.}}
  //   Q_0: Second number to multiply.
  //   {{de Zweite zu multiplizierende 4 Bit Zahl.}}
endmodule
