// Digital circuit adder_pipe.dig as structural Verilog
module adder_pipe (
  input  [3:0] B,
  input  [3:0] A,
  input  EN,
  output [3:0] S,
  output C
);

  wire add_1_c_o, add_1_s, add_2_c_o, add_3_c_o, add_4_c_o, clk_out, d_ff_3_q, d_ff_7_q, d_ff_11_q;
  wire [1:0] d_ff_4_q, d_ff_8_q;
  wire [2:0] d_ff_12_q;
  wire [2:2] add_3_s;
  wire [3:0] d_ff_1_q, d_ff_2_q, d_ff_5_q, d_ff_6_q, d_ff_9_q, d_ff_10_q, driver_1_out, driver_2_out;
  wire [3:3] add_4_s;

  assign driver_1_out = EN ? A : 4'bz;  // Driver driver_1
  assign driver_2_out = EN ? B : 4'bz;  // Driver driver_2
  Button clk (.out(clk_out));
  Add add_1 (.a(driver_1_out[0]), .b(driver_2_out[0]), .c_i(1'b0), .s(add_1_s), .c_o(add_1_c_o));
  D_FF #(.Bits(4)) d_ff_1 (.D(driver_1_out), .C(clk_out), .Q(d_ff_1_q));  // open: nQ
  D_FF #(.Bits(4)) d_ff_2 (.D(driver_2_out), .C(clk_out), .Q(d_ff_2_q));  // open: nQ
  D_FF d_ff_3 (.D(add_1_c_o), .C(clk_out), .Q(d_ff_3_q));  // open: nQ
  D_FF d_ff_4 (.D(add_1_s), .C(clk_out), .Q(d_ff_4_q[0]));  // open: nQ
  Add add_2 (.a(d_ff_1_q[1]), .b(d_ff_2_q[1]), .c_i(d_ff_3_q), .s(d_ff_4_q[1]), .c_o(add_2_c_o));
  D_FF #(.Bits(4)) d_ff_5 (.D(d_ff_1_q), .C(clk_out), .Q(d_ff_5_q));  // open: nQ
  D_FF #(.Bits(4)) d_ff_6 (.D(d_ff_2_q), .C(clk_out), .Q(d_ff_6_q));  // open: nQ
  // Probe on d_ff_4_q
  D_FF d_ff_7 (.D(add_2_c_o), .C(clk_out), .Q(d_ff_7_q));  // open: nQ
  D_FF #(.Bits(2)) d_ff_8 (.D(d_ff_4_q), .C(clk_out), .Q(d_ff_8_q));  // open: nQ
  Add add_3 (.a(d_ff_5_q[2]), .b(d_ff_6_q[2]), .c_i(d_ff_7_q), .s(add_3_s[2]), .c_o(add_3_c_o));
  D_FF #(.Bits(4)) d_ff_9 (.D(d_ff_5_q), .C(clk_out), .Q(d_ff_9_q));  // open: nQ
  D_FF #(.Bits(4)) d_ff_10 (.D(d_ff_6_q), .C(clk_out), .Q(d_ff_10_q));  // open: nQ
  D_FF d_ff_11 (.D(add_3_c_o), .C(clk_out), .Q(d_ff_11_q));  // open: nQ
  D_FF #(.Bits(3)) d_ff_12 (.D({add_3_s[2], d_ff_8_q}), .C(clk_out), .Q(d_ff_12_q));  // open: nQ
  // Probe on {add_3_s[2], d_ff_8_q}
  Add add_4 (.a(d_ff_9_q[3]), .b(d_ff_10_q[3]), .c_i(d_ff_11_q), .s(add_4_s[3]), .c_o(add_4_c_o));
  // Probe on {add_4_s[3], d_ff_12_q}
  D_FF d_ff_13 (.D(add_4_c_o), .C(clk_out), .Q(C));  // open: nQ
  D_FF #(.Bits(4)) d_ff_14 (.D({add_4_s[3], d_ff_12_q}), .C(clk_out), .Q(S));  // open: nQ

  // Notes on the sheet:
  //   B: default 10
  //   A: default 5
endmodule
