// Digital circuit comp_pipe.dig as structural Verilog
module comp_pipe (
  input  [7:0] P,
  input  [7:0] Q,
  output P_gt_Q
);

  wire clk, comparator_1_eq, comparator_2_eq, comparator_3_eq, comparator_4_gt, comparator_5_eq,
       comparator_6_eq, comparator_7_eq, comparator_8_gt, d_ff_3_q, multiplexer_1_out, multiplexer_2_out,
       multiplexer_3_out, multiplexer_4_out, multiplexer_5_out, multiplexer_6_out, multiplexer_7_out,
       multiplexer_8_out;
  wire [3:0] d_ff_1_q, d_ff_2_q;

  Button u_CLK (.out(clk));
  D_FF #(.Bits(4)) d_ff_1 (.D(P[7:4]), .C(clk), .Q(d_ff_1_q));  // open: nQ
  D_FF #(.Bits(4)) d_ff_2 (.D(Q[7:4]), .C(clk), .Q(d_ff_2_q));  // open: nQ
  Comparator comparator_1 (.a(P[3]), .b(Q[3]), .eq(comparator_1_eq));  // open: gt, lt
  Comparator comparator_2 (.a(P[2]), .b(Q[2]), .eq(comparator_2_eq));  // open: gt, lt
  Comparator comparator_3 (.a(P[1]), .b(Q[1]), .eq(comparator_3_eq));  // open: gt, lt
  Comparator comparator_4 (.a(P[0]), .b(Q[0]), .gt(comparator_4_gt));  // open: eq, lt
  Comparator comparator_5 (.a(d_ff_1_q[3]), .b(d_ff_2_q[3]), .eq(comparator_5_eq));  // open: gt, lt
  Comparator comparator_6 (.a(d_ff_1_q[2]), .b(d_ff_2_q[2]), .eq(comparator_6_eq));  // open: gt, lt
  Comparator comparator_7 (.a(d_ff_1_q[1]), .b(d_ff_2_q[1]), .eq(comparator_7_eq));  // open: gt, lt
  Comparator comparator_8 (.a(d_ff_1_q[0]), .b(d_ff_2_q[0]), .gt(comparator_8_gt));  // open: eq, lt
  Multiplexer multiplexer_1 (.sel(comparator_4_gt), .in_0(1'b0), .in_1(1'b1), .out(multiplexer_1_out));
  Multiplexer multiplexer_2 (.sel(comparator_8_gt), .in_0(d_ff_1_q[0]), .in_1(d_ff_3_q), .out(multiplexer_2_out));
  Multiplexer multiplexer_3 (.sel(comparator_3_eq), .in_0(P[1]), .in_1(multiplexer_1_out), .out(multiplexer_3_out));
  Multiplexer multiplexer_4 (
    .sel(comparator_7_eq), .in_0(d_ff_1_q[1]), .in_1(multiplexer_2_out), .out(multiplexer_4_out));
  Multiplexer multiplexer_5 (.sel(comparator_2_eq), .in_0(P[2]), .in_1(multiplexer_3_out), .out(multiplexer_5_out));
  Multiplexer multiplexer_6 (
    .sel(comparator_6_eq), .in_0(d_ff_1_q[2]), .in_1(multiplexer_4_out), .out(multiplexer_6_out));
  Multiplexer multiplexer_7 (.sel(comparator_1_eq), .in_0(P[3]), .in_1(multiplexer_5_out), .out(multiplexer_7_out));
  Multiplexer multiplexer_8 (
    .sel(comparator_5_eq), .in_0(d_ff_1_q[3]), .in_1(multiplexer_6_out), .out(multiplexer_8_out));
  D_FF d_ff_3 (.D(multiplexer_7_out), .C(clk), .Q(d_ff_3_q));  // open: nQ
  D_FF d_ff_4 (.D(multiplexer_8_out), .C(clk), .Q(P_gt_Q));  // open: nQ

  // Notes on the sheet:
  //   P_gt_Q: This output is high, if P>Q is valid.
  //   {{de Das Bit ist Eins, wenn P>Q gilt.}}
endmodule
