// Digital circuit division_pipe.dig as structural Verilog
module division_pipe (
  input  [7:0] _8b_A,
  input  [3:0] _4b_B,
  output [4:0] _5b_Q,
  output [3:0] _4b_R
);

  wire clk_out, comparator_2_lt;
  wire [1:0] comparator_4_lt;
  wire [2:0] d_ff_12_q;
  wire [3:0] add_5_s, comparator_3_lt, d_ff_3_q, d_ff_4_q, d_ff_7_q, d_ff_8_q, d_ff_10_q, d_ff_11_q,
       d_ff_13_q_2, d_ff_14_q, d_ff_15_q, multiplexer_1_out, multiplexer_2_out, multiplexer_3_out,
       multiplexer_4_out, multiplexer_5_out, not_1_out, not_2_out, not_3_out, not_4_out, not_5_out;
  wire [3:1] add_2_s, add_3_s, add_4_s;
  wire [3:3] add_1_s, add_2_s_2, add_3_s_2, add_4_s_2;
  wire [4:0] comparator_5_lt, not_6_out;
  wire [7:0] d_ff_2_q, d_ff_6_q, d_ff_13_q;

  Comparator #(.Bits(4)) comparator_1 (.a(d_ff_14_q), .b(d_ff_15_q), .lt(d_ff_12_q[0]));  // open: gt, eq
  Multiplexer #(.Bits(4)) multiplexer_1 (.sel(d_ff_12_q[0]), .in_0(d_ff_15_q), .in_1(4'b0000), .out(multiplexer_1_out));
  Button clk (.out(clk_out));
  Comparator #(.Bits(4)) comparator_2 (.a(_8b_A[7:4]), .b(_4b_B), .lt(comparator_2_lt));  // open: gt, eq
  // Probe on d_ff_12_q
  Add #(.Bits(4)) add_1 (.a(d_ff_14_q), .b(not_1_out), .c_i(1'b1), .s({add_1_s[3], d_ff_13_q_2[3:1]}));  // open: c_o
  assign not_1_out = ~multiplexer_1_out;  // Not not_1, 4 bits wide
  Add #(.Bits(4)) add_2 (.a(_8b_A[7:4]), .b(not_2_out), .c_i(1'b1), .s({add_2_s_2[3], add_2_s}));  // open: c_o
  Multiplexer #(.Bits(4)) multiplexer_2 (.sel(comparator_2_lt), .in_0(_4b_B), .in_1(4'b0000), .out(multiplexer_2_out));
  assign not_2_out = ~multiplexer_2_out;  // Not not_2, 4 bits wide
  // Probe on {add_1_s[3], d_ff_13_q_2[3:1]}
  // Probe on {add_2_s_2[3], add_2_s}
  D_FF #(.Bits(3)) d_ff_1 (.D(d_ff_12_q), .C(clk_out), .Q(comparator_3_lt[3:1]));  // open: nQ
  D_FF #(.Bits(8)) d_ff_2 (.D({d_ff_13_q[7:2], d_ff_13_q_2[0], d_ff_13_q[0]}), .C(clk_out), .Q(d_ff_2_q));  // open: nQ
  D_FF #(.Bits(4)) d_ff_3 (.D(d_ff_13_q_2), .C(clk_out), .Q(d_ff_3_q));  // open: nQ
  D_FF #(.Bits(4)) d_ff_4 (.D(d_ff_15_q), .C(clk_out), .Q(d_ff_4_q));  // open: nQ
  D_FF d_ff_5 (.D(comparator_2_lt), .C(clk_out), .Q(comparator_4_lt[1]));  // open: nQ
  D_FF #(.Bits(8)) d_ff_6 (.D(_8b_A), .C(clk_out), .Q(d_ff_6_q));  // open: nQ
  D_FF #(.Bits(4)) d_ff_7 (.D({add_2_s, _8b_A[3]}), .C(clk_out), .Q(d_ff_7_q));  // open: nQ
  D_FF #(.Bits(4)) d_ff_8 (.D(_4b_B), .C(clk_out), .Q(d_ff_8_q));  // open: nQ
  // Probe on d_ff_3_q
  Comparator #(.Bits(4)) comparator_3 (.a(d_ff_3_q), .b(d_ff_4_q), .lt(comparator_3_lt[0]));  // open: gt, eq
  // Probe on d_ff_7_q
  Comparator #(.Bits(4)) comparator_4 (.a(d_ff_7_q), .b(d_ff_8_q), .lt(comparator_4_lt[0]));  // open: gt, eq
  Multiplexer #(.Bits(4)) multiplexer_3 (
    .sel(comparator_3_lt[0]), .in_0(d_ff_4_q), .in_1(4'b0000), .out(multiplexer_3_out));
  Multiplexer #(.Bits(4)) multiplexer_4 (
    .sel(comparator_4_lt[0]), .in_0(d_ff_8_q), .in_1(4'b0000), .out(multiplexer_4_out));
  // Probe on comparator_3_lt
  Add #(.Bits(4)) add_3 (.a(d_ff_3_q), .b(not_3_out), .c_i(1'b1), .s({add_3_s_2[3], add_3_s}));  // open: c_o
  assign not_3_out = ~multiplexer_3_out;  // Not not_3, 4 bits wide
  Add #(.Bits(4)) add_4 (.a(d_ff_7_q), .b(not_4_out), .c_i(1'b1), .s({add_4_s_2[3], add_4_s}));  // open: c_o
  assign not_4_out = ~multiplexer_4_out;  // Not not_4, 4 bits wide
  // Probe on {add_3_s_2[3], add_3_s}
  // Probe on comparator_4_lt
  // Probe on {add_4_s_2[3], add_4_s}
  D_FF #(.Bits(4)) d_ff_9 (.D(comparator_3_lt), .C(clk_out), .Q(comparator_5_lt[4:1]));  // open: nQ
  D_FF #(.Bits(4)) d_ff_10 (.D({add_3_s, d_ff_2_q[0]}), .C(clk_out), .Q(d_ff_10_q));  // open: nQ
  D_FF #(.Bits(4)) d_ff_11 (.D(d_ff_4_q), .C(clk_out), .Q(d_ff_11_q));  // open: nQ
  // Probe on d_ff_10_q
  D_FF #(.Bits(2)) d_ff_12 (.D(comparator_4_lt), .C(clk_out), .Q(d_ff_12_q[2:1]));  // open: nQ
  D_FF #(.Bits(8)) d_ff_13 (.D(d_ff_6_q), .C(clk_out), .Q({d_ff_13_q[7:2], d_ff_13_q_2[0], d_ff_13_q[0]}));  // open: nQ
  D_FF #(.Bits(4)) d_ff_14 (.D({add_4_s, d_ff_6_q[2]}), .C(clk_out), .Q(d_ff_14_q));  // open: nQ
  D_FF #(.Bits(4)) d_ff_15 (.D(d_ff_8_q), .C(clk_out), .Q(d_ff_15_q));  // open: nQ
  Comparator #(.Bits(4)) comparator_5 (.a(d_ff_10_q), .b(d_ff_11_q), .lt(comparator_5_lt[0]));  // open: gt, eq
  // Probe on d_ff_14_q
  // Probe on comparator_5_lt
  Add #(.Bits(4)) add_5 (.a(d_ff_10_q), .b(not_5_out), .c_i(1'b1), .s(add_5_s));  // open: c_o
  Multiplexer #(.Bits(4)) multiplexer_5 (
    .sel(comparator_5_lt[0]), .in_0(d_ff_11_q), .in_1(4'b0000), .out(multiplexer_5_out));
  assign not_5_out = ~multiplexer_5_out;  // Not not_5, 4 bits wide
  // Probe on d_ff_12_q[2:1]
  assign not_6_out = ~comparator_5_lt;  // Not not_6, 5 bits wide
  D_FF #(.Bits(5)) d_ff_16 (.D(not_6_out), .C(clk_out), .Q(_5b_Q));  // open: nQ
  D_FF #(.Bits(4)) d_ff_17 (.D(add_5_s), .C(clk_out), .Q(_4b_R));  // open: nQ

  // Notes on the sheet:
  //   division pipe
  //   3 bit
  //   1 bit
  //   4 bit
  //   2 bit
  //   5 bit
endmodule
