// Digital circuit float division.dig as structural Verilog
module float_division (
  input  [31:0] A,
  input  [31:0] B,
  output [31:0] Y,
  output _0,
  output OF
);

  wire _0_check_1_zero, _0_check_2_zero, and_1_out, not_4_out;
  wire [0:0] not_3_out;
  wire [7:0] add_1_s, not_1_out;
  wire [8:8] add_1_c_o;
  wire [9:0] add_2_s;
  wire [23:0] barrelshifter_1_out;
  wire [31:31] xor_1_out;
  wire [47:0] div_1_q;

  _0_check _0_check_1 (.in({1'b0, A[30:0]}), .zero(_0_check_1_zero));  // open: out
  _0_check _0_check_2 (.in({1'b0, B[30:0]}), .zero(_0_check_2_zero));  // open: out
  assign not_1_out = ~B[30:23];  // Not not_1, 8 bits wide
  not not_2 (_0, _0_check_2_zero);
  Div #(.Bits(48)) div_1 (.a({1'b1, A[22:0], {24{1'b0}}}), .b({25'h1, B[22:0]}), .q(div_1_q));  // open: r
  not not_3 (not_3_out[0], div_1_q[24]);
  Add #(.Bits(8)) add_1 (.a(A[30:23]), .b(8'h7f), .c_i(1'b0), .s(add_1_s), .c_o(add_1_c_o[8]));
  xor xor_1 (xor_1_out[31], A[31], B[31]);
  and and_1 (and_1_out, not_4_out, _0_check_1_zero);
  Multiplexer #(.Bits(32)) multiplexer_1 (
    .sel(and_1_out), .in_0({32{1'b0}}), .in_1({xor_1_out[31], add_2_s[7:0], barrelshifter_1_out[23:1]}),
    .out(Y));
  BarrelShifter #(.Bits(24)) barrelshifter_1 (
    .in(div_1_q[23:0]), .shift({4'b0000, not_3_out[0]}), .out(barrelshifter_1_out));
  Add #(.Bits(10)) add_2 (
    .a({1'b0, add_1_c_o[8], add_1_s}), .b({2'b11, not_1_out}), .c_i(1'b1), .s(add_2_s));  // open: c_o
  and and_2 (OF, add_2_s[8], not_4_out);
  not not_4 (not_4_out, add_2_s[9]);
endmodule
