// Digital circuit float multiply.dig as structural Verilog
module float_multiply (
  input  [31:0] A,
  input  [31:0] B,
  output [31:0] Y,
  output OF
);

  wire _0_check_1_zero, _0_check_2_zero, and_1_out, not_1_out;
  wire [0:0] mul_1_mul_2;
  wire [7:0] add_2_s;
  wire [8:0] add_1_c_o;
  wire [9:8] add_2_s_2;
  wire [22:0] barrelshifter_1_out_2;
  wire [31:31] xor_1_out;
  wire [46:0] mul_1_mul;
  wire [47:0] barrelshifter_1_out;

  _0_check _0_check_1 (.in({1'b0, A[30:0]}), .zero(_0_check_1_zero));  // open: out
  _0_check _0_check_2 (.in({1'b0, B[30:0]}), .zero(_0_check_2_zero));  // open: out
  Mul #(.Bits(24)) mul_1 (.a({1'b1, A[22:0]}), .b({1'b1, B[22:0]}), .mul({mul_1_mul_2[0], mul_1_mul}));
  Add #(.Bits(8)) add_1 (.a(A[30:23]), .b(B[30:23]), .c_i(mul_1_mul_2[0]), .s(add_1_c_o[7:0]), .c_o(add_1_c_o[8]));
  not not_1 (not_1_out, add_2_s_2[9]);
  xor xor_1 (xor_1_out[31], A[31], B[31]);
  and and_1 (and_1_out, not_1_out, _0_check_1_zero, _0_check_2_zero);
  BarrelShifter #(.Bits(48), .direction("right")) barrelshifter_1 (
    .in({mul_1_mul_2[0], mul_1_mul}), .shift({{5{1'b0}}, mul_1_mul_2[0]}),
    .out({barrelshifter_1_out[47:46], barrelshifter_1_out_2, barrelshifter_1_out[22:0]}));
  and and_2 (OF, add_2_s_2[8], not_1_out);
  Add #(.Bits(10)) add_2 (.a({1'b0, add_1_c_o}), .b(10'h380), .c_i(1'b1), .s({add_2_s_2, add_2_s}));  // open: c_o
  Multiplexer #(.Bits(32)) multiplexer_1 (
    .sel(and_1_out), .in_0({32{1'b0}}), .in_1({xor_1_out[31], add_2_s, barrelshifter_1_out_2}), .out(Y));
endmodule
