// Digital circuit multiplexer_pipe.dig as structural Verilog
module multiplexer_pipe (
  input  A_0,
  input  A_1,
  input  D_0,
  input  D_1,
  input  D_2,
  input  D_3,
  output Y,
  output X
);

  wire and_1_out, and_2_out, and_3_out, and_4_out, button_1_out, d_ff_1_q, d_ff_2_q, d_ff_3_q, d_ff_4_q,
       d_ff_5_q, d_ff_6_q, not_1_out, not_2_out, xor_1_out, xor_2_out;

  not not_1 (not_1_out, A_1);
  Button button_1 (.out(button_1_out));
  not not_2 (not_2_out, A_0);
  and and_1 (and_1_out, not_2_out, not_1_out, D_0);
  and and_2 (and_2_out, A_0, not_1_out, D_1);
  and and_3 (and_3_out, not_2_out, A_1, D_2);
  and and_4 (and_4_out, A_0, A_1, D_3);
  D_FF d_ff_1 (.D(and_1_out), .C(button_1_out), .Q(d_ff_1_q));  // open: nQ
  D_FF d_ff_2 (.D(and_2_out), .C(button_1_out), .Q(d_ff_2_q));  // open: nQ
  D_FF d_ff_3 (.D(and_3_out), .C(button_1_out), .Q(d_ff_3_q));  // open: nQ
  D_FF d_ff_4 (.D(and_4_out), .C(button_1_out), .Q(d_ff_4_q));  // open: nQ
  xor xor_1 (xor_1_out, d_ff_1_q, d_ff_2_q);
  xor xor_2 (xor_2_out, d_ff_3_q, d_ff_4_q);
  Multiplexer #(.Selector_Bits(2)) multiplexer_1 (
    .sel({A_1, A_0}), .in_0(D_0), .in_1(D_1), .in_2(D_2), .in_3(D_3), .out(X));
  D_FF d_ff_5 (.D(xor_1_out), .C(button_1_out), .Q(d_ff_5_q));  // open: nQ
  D_FF d_ff_6 (.D(xor_2_out), .C(button_1_out), .Q(d_ff_6_q));  // open: nQ
  xor xor_3 (Y, d_ff_5_q, d_ff_6_q);

  // Other names for the same wires on the sheet: A0 = A_0; A1 = A_1; D0 = D_0; D1 = D_1; D2 = D_2; D3 = D_3

  // Notes on the sheet:
  //   A_0: Bit 0 of the input selection.
  //   {{de Bit 0 der Signalauswahl.}}
  //   A_1: Bit 1 of the input selection.
  //   {{de Bit 1 der Signalauswahl.}}
  //   D_0: data bit 0.
  //   {{de Das 0. Datenbit.}}
  //   D_1: data bit 1.
  //   {{de Das 1. Datenbit.}}
  //   D_2: data bit 2.
  //   {{de Das 2. Datenbit.}}
  //   D_3: data bit 3.
  //   {{de Das 3. Datenbit.}}
  //   Y: Output bit. One of the data bits is always output 
  //   here. Which one is set by the inputs A_0 and A_1.
  //   {{de Ausgangsbit. Es wird immer eines der Datenbits 
  //   hier ausgegeben. Welches das ist, legen die 
  //   Eingänge A_0 und A_1 fest.}}
endmodule
