// Digital circuit multiply pipe.dig as structural Verilog
module multiply_pipe (
  input  [3:0] A,
  input  [3:0] B,
  output [7:0] Q
);

  wire clk_out;
  wire [3:0] d_ff_1_q, d_ff_2_q, d_ff_3_q, d_ff_4_q, d_ff_6_q, d_ff_7_q, d_ff_9_q, multiplexer_1_out;
  wire [4:1] multiplexer_2_out;
  wire [5:0] add_1_s, d_ff_5_q;
  wire [5:2] multiplexer_3_out;
  wire [6:0] add_2_s, add_3_s, d_ff_8_q;
  wire [6:3] multiplexer_4_out;
  wire [7:7] add_3_c_o;

  Multiplexer #(.Bits(4)) multiplexer_1 (.sel(B[0]), .in_0(4'b0000), .in_1(A), .out(multiplexer_1_out));
  Button clk (.out(clk_out));
  D_FF #(.Bits(4)) d_ff_1 (.D(A), .C(clk_out), .Q(d_ff_1_q));  // open: nQ
  D_FF #(.Bits(4)) d_ff_2 (.D(multiplexer_1_out), .C(clk_out), .Q(d_ff_2_q));  // open: nQ
  D_FF #(.Bits(4)) d_ff_3 (.D(B), .C(clk_out), .Q(d_ff_3_q));  // open: nQ
  Multiplexer #(.Bits(4)) multiplexer_2 (.sel(d_ff_3_q[1]), .in_0(4'b0000), .in_1(d_ff_1_q), .out(multiplexer_2_out));
  // Probe on {1'b0, d_ff_2_q}
  Add #(.Bits(5)) add_1 (
    .a({1'b0, d_ff_2_q}), .b({multiplexer_2_out, 1'b0}), .c_i(1'b0), .s(add_1_s[4:0]), .c_o(add_1_s[5]));
  D_FF #(.Bits(4)) d_ff_4 (.D(d_ff_1_q), .C(clk_out), .Q(d_ff_4_q));  // open: nQ
  D_FF #(.Bits(6)) d_ff_5 (.D(add_1_s), .C(clk_out), .Q(d_ff_5_q));  // open: nQ
  // Probe on add_1_s
  D_FF #(.Bits(4)) d_ff_6 (.D(d_ff_3_q), .C(clk_out), .Q(d_ff_6_q));  // open: nQ
  Multiplexer #(.Bits(4)) multiplexer_3 (.sel(d_ff_6_q[2]), .in_0(4'b0000), .in_1(d_ff_4_q), .out(multiplexer_3_out));
  // Probe on d_ff_5_q
  Add #(.Bits(6)) add_2 (.a(d_ff_5_q), .b({multiplexer_3_out, 2'b00}), .c_i(1'b0), .s(add_2_s[5:0]), .c_o(add_2_s[6]));
  D_FF #(.Bits(4)) d_ff_7 (.D(d_ff_4_q), .C(clk_out), .Q(d_ff_7_q));  // open: nQ
  D_FF #(.Bits(7)) d_ff_8 (.D(add_2_s), .C(clk_out), .Q(d_ff_8_q));  // open: nQ
  // Probe on add_2_s
  D_FF #(.Bits(4)) d_ff_9 (.D(d_ff_6_q), .C(clk_out), .Q(d_ff_9_q));  // open: nQ
  Multiplexer #(.Bits(4)) multiplexer_4 (.sel(d_ff_9_q[3]), .in_0(4'b0000), .in_1(d_ff_7_q), .out(multiplexer_4_out));
  // Probe on d_ff_8_q
  D_FF #(.Bits(8)) d_ff_10 (.D({add_3_c_o[7], add_3_s}), .C(clk_out), .Q(Q));  // open: nQ
  // Probe on {add_3_c_o[7], add_3_s}
  Add #(.Bits(7)) add_3 (.a(d_ff_8_q), .b({multiplexer_4_out, 3'b000}), .c_i(1'b0), .s(add_3_s), .c_o(add_3_c_o[7]));

  // Notes on the sheet:
  //   multiply pipe
endmodule
