// Digital circuit multiply_booth pipe.dig as structural Verilog
module multiply_booth_pipe (
  input  [4:0] _5b_A,
  input  [4:0] _5b_B,
  output [9:0] Q
);

  wire clk_out;
  wire [1:0] d_ff_4_q_2, d_ff_8_q, d_ff_12_q_2;
  wire [2:0] d_ff_12_q;
  wire [4:0] d_ff_4_q, d_ff_16_q;
  wire [4:2] d_ff_8_q_2;
  wire [5:0] add_1_s, add_2_s, bitextender_1_out, d_ff_1_q, d_ff_2_q, d_ff_5_q, d_ff_6_q, d_ff_7_q, d_ff_9_q,
       d_ff_10_q, d_ff_13_q, d_ff_14_q, multiplexer_1_out, multiplexer_4_out, multiplexer_5_out, not_1_out,
       not_2_out;
  wire [6:0] add_4_s, bitextender_3_out, d_ff_15_q;
  wire [6:1] multiplexer_3_out;
  wire [7:0] add_6_s, bitextender_5_out, d_ff_3_q;
  wire [8:0] add_3_s, bitextender_2_out, d_ff_11_q;
  wire [8:3] multiplexer_2_out;
  wire [9:0] add_5_s, bitextender_4_out;

  Button clk (.out(clk_out));
  BitExtender #(.inputBits(5), .outputBits(6)) bitextender_1 (.in(_5b_A), .out(bitextender_1_out));
  assign not_1_out = ~bitextender_1_out;  // Not not_1, 6 bits wide
  assign not_2_out = ~bitextender_1_out;  // Not not_2, 6 bits wide
  Add #(.Bits(6)) add_1 (.a(not_1_out), .b(6'b000001), .c_i(1'b0), .s(add_1_s));  // open: c_o
  Multiplexer #(.Bits(6)) multiplexer_1 (.sel(_5b_B[0]), .in_0({6{1'b0}}), .in_1(not_2_out), .out(multiplexer_1_out));
  D_FF #(.Bits(6)) d_ff_1 (.D(d_ff_13_q), .C(clk_out), .Q(d_ff_1_q));  // open: nQ
  D_FF #(.Bits(6)) d_ff_2 (.D(d_ff_14_q), .C(clk_out), .Q(d_ff_2_q));  // open: nQ
  D_FF #(.Bits(8)) d_ff_3 (.D(add_6_s), .C(clk_out), .Q(d_ff_3_q));  // open: nQ
  D_FF #(.Bits(5)) d_ff_4 (.D(d_ff_16_q), .C(clk_out), .Q({d_ff_4_q[4], d_ff_4_q_2, d_ff_4_q[1:0]}));  // open: nQ
  Add #(.Bits(6)) add_2 (.a({6{1'b0}}), .b(multiplexer_1_out), .c_i(_5b_B[0]), .s(add_2_s));  // open: c_o
  // Probe on {d_ff_4_q[4], d_ff_4_q_2, d_ff_4_q[1:0]}
  D_FF #(.Bits(6)) d_ff_5 (.D(bitextender_1_out), .C(clk_out), .Q(d_ff_5_q));  // open: nQ
  D_FF #(.Bits(6)) d_ff_6 (.D(add_1_s), .C(clk_out), .Q(d_ff_6_q));  // open: nQ
  D_FF #(.Bits(6)) d_ff_7 (.D(add_2_s), .C(clk_out), .Q(d_ff_7_q));  // open: nQ
  D_FF #(.Bits(5)) d_ff_8 (.D(_5b_B), .C(clk_out), .Q({d_ff_8_q_2, d_ff_8_q}));  // open: nQ
  BitExtender #(.outputBits(9)) bitextender_2 (.in(d_ff_3_q), .out(bitextender_2_out));
  Multiplexer #(.Selector_Bits(2), .Bits(6)) multiplexer_2 (
    .sel(d_ff_4_q_2), .in_0({6{1'b0}}), .in_1(d_ff_1_q), .in_2(d_ff_2_q), .in_3({6{1'b0}}),
    .out(multiplexer_2_out));
  // Probe on {d_ff_8_q_2, d_ff_8_q}
  // Probe on bitextender_2_out
  // Probe on {multiplexer_2_out, 3'b000}
  Add #(.Bits(9)) add_3 (.a(bitextender_2_out), .b({multiplexer_2_out, 3'b000}), .c_i(1'b0), .s(add_3_s));  // open: c_o
  BitExtender #(.inputBits(6), .outputBits(7)) bitextender_3 (.in(d_ff_7_q), .out(bitextender_3_out));
  Multiplexer #(.Selector_Bits(2), .Bits(6)) multiplexer_3 (
    .sel(d_ff_8_q), .in_0({6{1'b0}}), .in_1(d_ff_5_q), .in_2(d_ff_6_q), .in_3({6{1'b0}}),
    .out(multiplexer_3_out));
  // Probe on bitextender_3_out
  // Probe on {multiplexer_3_out, 1'b0}
  D_FF #(.Bits(6)) d_ff_9 (.D(d_ff_1_q), .C(clk_out), .Q(d_ff_9_q));  // open: nQ
  D_FF #(.Bits(6)) d_ff_10 (.D(d_ff_2_q), .C(clk_out), .Q(d_ff_10_q));  // open: nQ
  D_FF #(.Bits(9)) d_ff_11 (.D(add_3_s), .C(clk_out), .Q(d_ff_11_q));  // open: nQ
  D_FF #(.Bits(5)) d_ff_12 (
    .D({d_ff_4_q[4], d_ff_4_q_2, d_ff_4_q[1:0]}), .C(clk_out), .Q({d_ff_12_q_2, d_ff_12_q}));  // open: nQ
  Add #(.Bits(7)) add_4 (.a(bitextender_3_out), .b({multiplexer_3_out, 1'b0}), .c_i(1'b0), .s(add_4_s));  // open: c_o
  // Probe on {d_ff_12_q_2, d_ff_12_q}
  D_FF #(.Bits(6)) d_ff_13 (.D(d_ff_5_q), .C(clk_out), .Q(d_ff_13_q));  // open: nQ
  D_FF #(.Bits(6)) d_ff_14 (.D(d_ff_6_q), .C(clk_out), .Q(d_ff_14_q));  // open: nQ
  D_FF #(.Bits(7)) d_ff_15 (.D(add_4_s), .C(clk_out), .Q(d_ff_15_q));  // open: nQ
  D_FF #(.Bits(5)) d_ff_16 (.D({d_ff_8_q_2, d_ff_8_q}), .C(clk_out), .Q(d_ff_16_q));  // open: nQ
  BitExtender #(.inputBits(9), .outputBits(10)) bitextender_4 (.in(d_ff_11_q), .out(bitextender_4_out));
  Multiplexer #(.Selector_Bits(2), .Bits(6)) multiplexer_4 (
    .sel(d_ff_12_q_2), .in_0({6{1'b0}}), .in_1(d_ff_9_q), .in_2(d_ff_10_q), .in_3({6{1'b0}}),
    .out(multiplexer_4_out));
  // Probe on d_ff_16_q
  // Probe on bitextender_4_out
  Add #(.Bits(10)) add_5 (
    .a(bitextender_4_out), .b({multiplexer_4_out, 4'b0000}), .c_i(1'b0), .s(add_5_s));  // open: c_o
  // Probe on {multiplexer_4_out, 4'b0000}
  BitExtender #(.inputBits(7), .outputBits(8)) bitextender_5 (.in(d_ff_15_q), .out(bitextender_5_out));
  Multiplexer #(.Selector_Bits(2), .Bits(6)) multiplexer_5 (
    .sel(d_ff_16_q[2:1]), .in_0({6{1'b0}}), .in_1(d_ff_13_q), .in_2(d_ff_14_q), .in_3({6{1'b0}}),
    .out(multiplexer_5_out));
  // Probe on bitextender_5_out
  // Probe on {multiplexer_5_out, 2'b00}
  D_FF #(.Bits(10)) d_ff_17 (.D(add_5_s), .C(clk_out), .Q(Q));  // open: nQ
  Add #(.Bits(8)) add_6 (.a(bitextender_5_out), .b({multiplexer_5_out, 2'b00}), .c_i(1'b0), .s(add_6_s));  // open: c_o

  // Notes on the sheet:
  //   6 bit
  //   9 bit
  //   multiply booth pipe
  //   7bit
  //   10 bit
  //   8 bit
endmodule
