// Digital circuit shift_pipe.dig as structural Verilog
module shift_pipe (
  input  [15:0] D,
  input  [15:0] D_16,
  input  [4:0] shift_5,
  input  [4:0] shift,
  output [15:0] Q,
  output [15:0] Q_16
);

  wire clk_out, d_ff_8_q;
  wire [0:0] d_ff_7_q;
  wire [1:0] d_ff_5_q, d_ff_6_q;
  wire [2:0] d_ff_3_q;
  wire [3:0] d_ff_2_q, d_ff_4_q;
  wire [7:0] d_ff_1_q, d_ff_1_q_2;
  wire [11:0] d_ff_4_q_2;
  wire [13:0] d_ff_5_q_2;
  wire [14:0] d_ff_7_q_2;
  wire [15:0] multiplexer_1_out, multiplexer_2_out, multiplexer_3_out, multiplexer_4_out, multiplexer_5_out;

  Multiplexer #(.Bits(16)) multiplexer_1 (.sel(shift[4]), .in_0(D), .in_1({16{1'b0}}), .out(multiplexer_1_out));
  Button clk (.out(clk_out));
  D_FF #(.Bits(16)) d_ff_1 (.D(multiplexer_1_out), .C(clk_out), .Q({d_ff_1_q_2, d_ff_1_q}));  // open: nQ
  D_FF #(.Bits(4)) d_ff_2 (.D(shift[3:0]), .C(clk_out), .Q(d_ff_2_q));  // open: nQ
  // Probe on {d_ff_1_q_2, d_ff_1_q}
  Multiplexer #(.Bits(16)) multiplexer_2 (
    .sel(d_ff_2_q[3]), .in_0({d_ff_1_q_2, d_ff_1_q}), .in_1({{8{1'b0}}, d_ff_1_q_2}), .out(multiplexer_2_out));
  BarrelShifter #(.Bits(16), .direction("right")) barrelshifter_1 (.in(D_16), .shift(shift_5), .out(Q_16));
  D_FF #(.Bits(3)) d_ff_3 (.D(d_ff_2_q[2:0]), .C(clk_out), .Q(d_ff_3_q));  // open: nQ
  D_FF #(.Bits(16)) d_ff_4 (.D(multiplexer_2_out), .C(clk_out), .Q({d_ff_4_q_2, d_ff_4_q}));  // open: nQ
  Multiplexer #(.Bits(16)) multiplexer_3 (
    .sel(d_ff_3_q[2]), .in_0({d_ff_4_q_2, d_ff_4_q}), .in_1({4'b0000, d_ff_4_q_2}), .out(multiplexer_3_out));
  // Probe on {d_ff_4_q_2, d_ff_4_q}
  D_FF #(.Bits(16)) d_ff_5 (.D(multiplexer_3_out), .C(clk_out), .Q({d_ff_5_q_2, d_ff_5_q}));  // open: nQ
  D_FF #(.Bits(2)) d_ff_6 (.D(d_ff_3_q[1:0]), .C(clk_out), .Q(d_ff_6_q));  // open: nQ
  // Probe on {d_ff_5_q_2, d_ff_5_q}
  Multiplexer #(.Bits(16)) multiplexer_4 (
    .sel(d_ff_6_q[1]), .in_0({d_ff_5_q_2, d_ff_5_q}), .in_1({2'b00, d_ff_5_q_2}), .out(multiplexer_4_out));
  D_FF #(.Bits(16)) d_ff_7 (.D(multiplexer_4_out), .C(clk_out), .Q({d_ff_7_q_2, d_ff_7_q[0]}));  // open: nQ
  D_FF d_ff_8 (.D(d_ff_6_q[0]), .C(clk_out), .Q(d_ff_8_q));  // open: nQ
  // Probe on {d_ff_7_q_2, d_ff_7_q[0]}
  Multiplexer #(.Bits(16)) multiplexer_5 (
    .sel(d_ff_8_q), .in_0({d_ff_7_q_2, d_ff_7_q[0]}), .in_1({1'b0, d_ff_7_q_2}), .out(multiplexer_5_out));
  D_FF #(.Bits(16)) d_ff_9 (.D(multiplexer_5_out), .C(clk_out), .Q(Q));  // open: nQ

  // Notes on the sheet:
  //   16 bit
  //   shifter pipe
endmodule
