// Digital circuit data path.dig as structural Verilog
module data_path (
  input  in_1,
  input  in_3,
  input  in_4,
  output [3:0] OP
);

  wire [3:0] ROM_d;
  wire [7:0] add_1_s, multiplexer_1_out, PC_q;

  Multiplexer #(.Bits(8)) multiplexer_1 (.sel(in_1), .in_0(add_1_s), .in_1({OP, ROM_d}), .out(multiplexer_1_out));
  // Probe on multiplexer_1_out
  Register #(.Bits(8)) PC (.D(multiplexer_1_out), .C(in_3), .en(in_4), .Q(PC_q));
  // Probe on PC_q
  Add #(.Bits(8)) add_1 (.a(8'h1), .b(PC_q), .c_i(1'b0), .s(add_1_s));  // open: c_o
  ROM #(.AddrBits(8), .Bits(8)) ROM (.A(PC_q), .sel(in_4), .D({OP, ROM_d}));
  // Probe on {OP, ROM_d}

  // Other names for the same wires on the sheet: EN = in_4; LDPC = in_1; PC_INC = in_3

  // Notes on the sheet:
  //   contents of ROM (hex, n*v repeats v):
  //   10,3,0,1,10,2
endmodule
