// Digital circuit hard logic-I.dig as structural Verilog
module hard_logic_I (
  input  clock,
  input  hand,
  input  model,
  input  reset
);

  wire and_1_out, and_3_out, break_q, clk, hlt, I_0, JMP, M1, M2, multiplexer_2_out, NOP, PC_INC;
  wire [3:0] and_4_out, counter_1_out, OP;
  wire [7:0] add_1_s, bitextender_1_out, multiplexer_1_out, PC_q, register_1_q;
  wire [7:1] ROM_d;

  // Probe on {ROM_d, I_0}
  Multiplexer #(.Bits(8)) multiplexer_1 (.sel(JMP), .in_0(add_1_s), .in_1({ROM_d, I_0}), .out(multiplexer_1_out));
  // Probe on multiplexer_1_out
  Register #(.Bits(8)) PC (.D(multiplexer_1_out), .C(clk), .en(PC_INC), .Q(PC_q));
  and and_1 (and_1_out, ~NOP, M1);  // And
  D_FF M (.D(and_1_out), .C(clk), .Q(M2), .nQ(M1));
  LED u_M1 (.in(M1));
  LED u_M2 (.in(M2));
  Multiplexer multiplexer_2 (.sel(model), .in_0(hand), .in_1(clock), .out(multiplexer_2_out));
  Add #(.Bits(8)) add_1 (.a(8'h1), .b(PC_q), .c_i(1'b0), .s(add_1_s));  // open: c_o
  or or_1 (clk, multiplexer_2_out, break_q);
  // Probe on PC_q
  Comparator #(.Bits(4)) comparator_1 (.a(OP), .b(4'b0001), .eq(JMP));  // open: gt, lt
  or or_2 (PC_INC, JMP, M1);
  and and_2 (hlt, I_0, NOP, M1);
  ROM #(.AddrBits(8), .Bits(8)) ROM (.A(PC_q), .sel(1'b1), .D({ROM_d, I_0}));
  and and_3 (and_3_out, reset, multiplexer_2_out);
  Register #(.Bits(8)) register_1 (.D({ROM_d, I_0}), .C(clk), .en(M1), .Q(register_1_q));
  BitExtender #(.inputBits(1), .outputBits(8)) bitextender_1 (.in(M2), .out(bitextender_1_out));
  Counter #(.Bits(4)) counter_1 (.en(1'b1), .C(M1), .clr(1'b0), .out(counter_1_out));  // open: ovf
  D_FF_AS \break  (.Set(1'b0), .D(hlt), .C(clk), .Clr(and_3_out), .Q(break_q));  // open: nQ
  nor nor_1 (NOP, ROM_d[4], ROM_d[5], ROM_d[6], ROM_d[7]);
  assign {OP, and_4_out} = register_1_q & bitextender_1_out;  // And and_4, 8 bits wide
  Seven_Seg_Hex seven_seg_hex_1 (.d(counter_1_out), .dp(1'b0));
  LED led_1 (.in(break_q));
  // Probe on {OP, and_4_out}

  // Other names for the same wires on the sheet: LDPC = JMP

  // Notes on the sheet:
  //   clock: Hz: 2
  //   硬布线控制器
  //   contents of ROM (hex, n*v repeats v):
  //   10,3,0,1,10,2
endmodule
