// Digital circuit logic III.dig as structural Verilog
module logic_III (
  input  [3:0] OP,
  output LDPC,
  output PC_INC,
  output P2,
  output [2:0] S,
  output [1:0] A
);

  wire and_4_out, and_5_out, and_6_out, and_7_out, and_8_out, and_9_out, and_10_out, and_11_out, and_12_out,
       and_13_out, and_15_out, and_16_out, and_17_out, and_18_out, and_19_out, and_20_out, and_21_out,
       and_22_out, not_1_out, not_2_out, not_3_out, not_4_out;

  not not_1 (not_1_out, OP[3]);
  not not_2 (not_2_out, OP[2]);
  not not_3 (not_3_out, OP[1]);
  not not_4 (not_4_out, OP[0]);
  and and_1 (LDPC, OP[0], not_3_out, not_2_out, not_1_out);
  and and_2 (S[2], OP[1], not_2_out, not_1_out);
  and and_3 (S[1], not_4_out, OP[2], not_1_out);
  and and_4 (and_4_out, not_4_out, OP[1], not_2_out);
  and and_5 (and_5_out, OP[0], OP[2]);
  and and_6 (and_6_out, OP[0], OP[3]);
  and and_7 (and_7_out, not_3_out, OP[2]);
  and and_8 (and_8_out, OP[1], OP[3]);
  and and_9 (and_9_out, OP[0], not_2_out);
  and and_10 (and_10_out, not_3_out, not_2_out, not_1_out);
  and and_11 (and_11_out, OP[1], OP[2]);
  and and_12 (and_12_out, OP[1], OP[3]);
  and and_13 (and_13_out, OP[2], OP[3]);
  and and_14 (A[1], OP[0], OP[2], not_1_out);
  and and_15 (and_15_out, OP[0], OP[3]);
  and and_16 (and_16_out, not_4_out, OP[1]);
  and and_17 (and_17_out, OP[1], not_2_out);
  and and_18 (and_18_out, not_3_out, OP[2]);
  and and_19 (and_19_out, OP[0], not_3_out, OP[3]);
  and and_20 (and_20_out, not_4_out, OP[2], OP[3]);
  and and_21 (and_21_out, OP[1], OP[2], not_1_out);
  and and_22 (and_22_out, OP[1], not_2_out, OP[3]);
  or or_1 (S[0], and_4_out, and_5_out, and_6_out, and_7_out, and_8_out);
  or or_2 (PC_INC, and_9_out, and_10_out, and_11_out, and_12_out, and_13_out);
  or or_3 (A[0], and_15_out, and_16_out, and_17_out, and_18_out);
  or or_4 (P2, and_19_out, and_20_out, and_21_out, and_22_out);

  // Other names for the same wires on the sheet: OP4 = OP[0]; OP5 = OP[1]; OP6 = OP[2]; OP7 = OP[3]
endmodule
