// Digital circuit HALT.dig as structural Verilog
module HALT (
  input  mw,
  input  mr,
  input  clk,
  output EN,
  output memw
);

  wire and_1_out, and_2_out, d_ff_as_1_q, d_ff_as_2_nq, delay1_nq, delay1_q, delay2_nq, not_1_out, or_1_out;

  or or_1 (or_1_out, mr, mw);
  and and_1 (and_1_out, and_2_out, mw);
  D_FF_AS d_ff_as_1 (.Set(1'b0), .D(and_1_out), .C(clk), .Clr(1'b0), .Q(d_ff_as_1_q));  // open: nQ
  not not_1 (not_1_out, clk);
  D_FF_AS d_ff_as_2 (.Set(1'b0), .D(or_1_out), .C(not_1_out), .Clr(1'b0), .nQ(d_ff_as_2_nq));  // open: Q
  D_FF_AS delay1 (.Set(1'b0), .D(d_ff_as_1_q), .C(not_1_out), .Clr(1'b0), .Q(delay1_q), .nQ(delay1_nq));
  D_FF_AS delay2 (.Set(1'b0), .D(delay1_q), .C(not_1_out), .Clr(1'b0), .nQ(delay2_nq));  // open: Q
  or or_2 (EN, d_ff_as_2_nq, and_2_out);
  and and_2 (and_2_out, delay1_nq, delay2_nq);
  // Probe D on and_2_out
  and and_3 (memw, and_2_out, mw);
endmodule
