// Digital circuit pcsel.dig as structural Verilog
module pcsel (
  input  OP6,
  input  OP5,
  input  OP4,
  input  OP3,
  input  OP2,
  output P1,
  output P0
);

  wire not_1_out, not_2_out;

  not not_1 (not_1_out, OP4);
  not not_2 (not_2_out, OP3);
  and and_1 (P1, OP2, not_1_out, OP5, OP6);
  and and_2 (P0, not_2_out, not_1_out, OP5, OP6);
endmodule
