// Digital circuit CSR.dig as structural Verilog
module CSR (
  input  [31:0] ins_ID,
  input  [31:0] aluR,
  input  [31:0] mepc,
  input  [11:0] Wa,
  input  clk,
  input  W_EN,
  input  EN,
  input  ExInt,
  input  [31:0] IN0,
  output [31:0] ISR,
  output [31:0] CSR,
  output INT,
  output [31:0] OUT,
  output mret,
  output [31:0] test_1,
  output [31:0] test_2
);

  wire and_1_out, and_2_out, and_3_out, and_4_out, and_5_out, and_6_out, and_7_out, and_9_out,
       comparator_1_eq, comparator_2_eq, comparator_3_eq, comparator_4_eq, comparator_5_eq, comparator_6_eq,
       comparator_7_eq, comparator_8_eq, comparator_11_eq, comparator_12_eq, comparator_13_eq,
       comparator_14_eq, comparator_15_eq, comparator_16_eq, d_ff_1_q, d_ff_as_1_q, d_ff_as_2_nq, E_int,
       MEIE, mepc_eq, MIE, mip_eq, nor_1_out, not_1_out, or_1_out, or_2_out, priorityencoder_1_any,
       register_4_q, T_int, TimeInt_eq;
  wire [1:0] comparator_9_eq;
  wire [2:0] priorityencoder_1_num;
  wire [11:7] mip;
  wire [31:0] and_8_out, bitextender_1_out, CSR_RAM_da, CSR_RAM_db, CSR_ROM_d, mie_t, mstatus,
       multiplexer_1_out;

  Comparator #(.Bits(8)) comparator_1 (.a(Wa[11:4]), .b(8'h35), .eq(comparator_1_eq));  // open: gt, lt
  Comparator #(.Bits(4)) comparator_2 (.a(ins_ID[31:28]), .b(4'b0011), .eq(comparator_2_eq));  // open: gt, lt
  Comparator #(.Bits(8)) comparator_3 (.a(ins_ID[27:20]), .b(8'h30), .eq(comparator_3_eq));  // open: gt, lt
  Comparator #(.Bits(8)) comparator_4 (.a(ins_ID[27:20]), .b(8'h3f), .eq(comparator_4_eq));  // open: gt, lt
  Comparator #(.Bits(8)) comparator_5 (.a(ins_ID[27:20]), .b(8'h6), .eq(comparator_5_eq));  // open: gt, lt
  Comparator #(.Bits(8)) comparator_6 (.a(ins_ID[27:20]), .b(8'h5), .eq(comparator_6_eq));  // open: gt, lt
  Comparator #(.Bits(8)) comparator_7 (.a(ins_ID[27:20]), .b(8'h4), .eq(comparator_7_eq));  // open: gt, lt
  Comparator #(.Bits(8)) comparator_8 (.a(ins_ID[27:20]), .b({8{1'b0}}), .eq(comparator_8_eq));  // open: gt, lt
  Comparator #(.Bits(8)) u_mip (.a(ins_ID[27:20]), .b(8'h44), .eq(mip_eq));  // open: gt, lt
  Comparator #(.Bits(8)) u_mepc (.a(ins_ID[27:20]), .b(8'h41), .eq(mepc_eq));  // open: gt, lt
  and and_1 (and_1_out, comparator_1_eq, W_EN);
  Comparator #(.Bits(8)) comparator_9 (.a(ins_ID[31:24]), .b(8'h35), .eq(comparator_9_eq[0]));  // open: gt, lt
  Comparator #(.Bits(8)) comparator_10 (.a(ins_ID[31:24]), .b(8'hf1), .eq(comparator_9_eq[1]));  // open: gt, lt
  PriorityEncoder #(.Selector_Bits(3)) priorityencoder_1 (
    .in0(comparator_3_eq), .in1(comparator_4_eq), .in2(comparator_5_eq), .in3(comparator_6_eq),
    .in4(comparator_7_eq), .in5(comparator_8_eq), .in6(mip_eq), .in7(mepc_eq), .num(priorityencoder_1_num),
    .any(priorityencoder_1_any));
  Comparator #(.Bits(4)) comparator_11 (.a(Wa[11:8]), .b(4'b0011), .eq(comparator_11_eq));  // open: gt, lt
  Comparator #(.Bits(8)) comparator_12 (.a(Wa[7:0]), .b(8'h30), .eq(comparator_12_eq));  // open: gt, lt
  Comparator #(.Bits(8)) comparator_13 (.a(Wa[7:0]), .b(8'h6), .eq(comparator_13_eq));  // open: gt, lt
  Comparator #(.Bits(8)) comparator_14 (.a(Wa[7:0]), .b(8'h5), .eq(comparator_14_eq));  // open: gt, lt
  Comparator #(.Bits(8)) comparator_15 (.a(Wa[7:0]), .b(8'h4), .eq(comparator_15_eq));  // open: gt, lt
  Comparator #(.Bits(8)) comparator_16 (.a(Wa[7:0]), .b({8{1'b0}}), .eq(comparator_16_eq));  // open: gt, lt
  RegisterFile #(.AddrBits(4), .Bits(32)) CSR_RAM (
    .Din(aluR), .we(and_1_out), .Rw(Wa[3:0]), .C(clk), .Ra(ins_ID[23:20]), .Rb(Wa[3:0]), .Da(CSR_RAM_da),
    .Db(CSR_RAM_db));
  and and_2 (and_2_out, comparator_2_eq, priorityencoder_1_any);
  Multiplexer #(.Selector_Bits(3), .Bits(32)) multiplexer_1 (
    .sel(priorityencoder_1_num), .in_0(OUT), .in_1(IN0), .in_2(test_2), .in_3(ISR),
    .in_4({mie_t[31:12], MEIE, mie_t[10:0]}), .in_5({mstatus[31:4], MIE, mstatus[2:0]}),
    .in_6({{20{1'b0}}, mip[11], 3'b000, mip[7], {7{1'b0}}}), .in_7(mepc), .out(multiplexer_1_out));
  // Probe on CSR_RAM_da
  // Probe on CSR_RAM_db
  ROM #(.AddrBits(4), .Bits(32)) CSR_ROM (.A(ins_ID[23:20]), .sel(1'b1), .D(CSR_ROM_d));
  and and_3 (and_3_out, comparator_11_eq, W_EN, comparator_12_eq);
  and and_4 (and_4_out, comparator_11_eq, W_EN, comparator_13_eq);
  and and_5 (and_5_out, comparator_11_eq, W_EN, comparator_14_eq);
  and and_6 (and_6_out, comparator_11_eq, W_EN, comparator_15_eq);
  and and_7 (and_7_out, comparator_11_eq, W_EN, comparator_16_eq);
  BitExtender #(.inputBits(1), .outputBits(32)) bitextender_1 (.in(and_2_out), .out(bitextender_1_out));
  // Probe on priorityencoder_1_num
  Multiplexer #(.Selector_Bits(2), .Bits(32)) multiplexer_2 (
    .sel(comparator_9_eq), .in_0(and_8_out), .in_1(CSR_RAM_da), .in_2(CSR_ROM_d), .in_3({32{1'b0}}), .out(CSR));
  // Probe on CSR_ROM_d
  Register #(.Bits(32)) u_out (.D(aluR), .C(clk), .en(and_3_out), .Q(OUT));
  Register #(.Bits(32)) mtimecmp (.D(aluR), .C(clk), .en(and_4_out), .Q(test_2));
  Register #(.Bits(32)) mtvec (.D(aluR), .C(clk), .en(and_5_out), .Q(ISR));
  Register #(.Bits(32)) u_mie (.D(aluR), .C(clk), .en(and_6_out), .Q({mie_t[31:12], MEIE, mie_t[10:0]}));
  Register #(.Bits(32)) u_mstatus (.D(aluR), .C(clk), .en(and_7_out), .Q({mstatus[31:4], MIE, mstatus[2:0]}));
  assign and_8_out = bitextender_1_out & multiplexer_1_out;  // And and_8, 32 bits wide
  // Probe on multiplexer_1_out
  // Probe on OUT
  // Probe on test_2
  D_FF_AS d_ff_as_1 (.Set(1'b0), .D(1'b1), .C(ExInt), .Clr(or_1_out), .Q(d_ff_as_1_q));  // open: nQ
  Register register_1 (.D(d_ff_as_1_q), .C(clk), .en(EN), .Q(E_int));
  or or_1 (or_1_out, ~MEIE, d_ff_1_q);  // Or
  CounterPreset #(.Bits(32)) mtime (
    .en(EN), .C(clk), .dir(1'b0), .in({32{1'b0}}), .ld(1'b0), .clr(~mie_t[7]), .out(test_1));  // open: ovf
  Register register_2 (.D(T_int), .C(clk), .en(INT), .Q(mip[7]));
  Register register_3 (.D(E_int), .C(clk), .en(INT), .Q(mip[11]));
  and and_9 (and_9_out, ins_ID[0], ins_ID[1], ins_ID[4], ins_ID[5], ins_ID[6]);
  nor nor_1 (nor_1_out, ins_ID[2], ins_ID[3], ins_ID[12], ins_ID[13], ins_ID[14]);
  not not_1 (not_1_out, ins_ID[20]);
  // Probe on test_1
  Comparator #(.Bits(32)) TimeInt (.a(test_1), .b(test_2), .eq(TimeInt_eq));  // open: gt, lt
  D_FF d_ff_1 (.D(E_int), .C(~clk), .Q(d_ff_1_q));  // open: nQ
  and and_10 (mret, and_9_out, nor_1_out, not_1_out);
  and and_11 (T_int, TimeInt_eq, mie_t[7]);
  and and_12 (INT, or_2_out, MIE, d_ff_as_2_nq);
  Register register_4 (.D(INT), .C(clk), .en(EN), .Q(register_4_q));
  D_FF_AS d_ff_as_2 (.Set(register_4_q), .D(1'b0), .C(1'b0), .Clr(mret), .nQ(d_ff_as_2_nq));  // open: Q
  or or_2 (or_2_out, E_int, T_int);

  // Other names for the same wires on the sheet: Din[31:0] = aluR; Dout[31:0] = CSR; Ex = ExInt; IN_0[31:0] = IN0;
  //   ins[31:0] = ins_ID; Raddr[11:0] = ins_ID[31:20]; MTIE = mie_t[7]; mie_t[11] = MEIE; mstatus[3] = MIE;
  //   mtcmp[31:0] = test_2; out0[31:0] = OUT; Waddr[11:0] = Wa; we = W_EN

  // Notes on the sheet:
  //   CSR_ROM loads instruction_monocycle.hex
endmodule
