// Digital circuit ID-EX.dig as structural Verilog
module ID_EX (
  input  clr,
  input  [31:0] PC_ID,
  input  [31:0] ins_ID,
  input  clk,
  input  EN,
  input  [31:0] RS1_ID,
  input  [31:0] RS2_ID,
  input  Flag_ID,
  input  [31:0] CSR_ID,
  input  [31:0] MEM_ID,
  input  [31:0] Addr_ID,
  output [31:0] PC_EX,
  output [31:0] ins_EX,
  output [31:0] RS1_EX,
  output [31:0] RS2_EX,
  output [31:0] CSR_EX,
  output [31:0] MEM_EX,
  output [31:0] Addr_EX,
  output Flag_EX
);

  wire [31:0] multiplexer_1_out;

  Multiplexer #(.Bits(32)) multiplexer_1 (.sel(clr), .in_0(ins_ID), .in_1({32{1'b0}}), .out(multiplexer_1_out));
  Register #(.Bits(32)) RS1 (.D(RS1_ID), .C(clk), .en(EN), .Q(RS1_EX));
  Register #(.Bits(32)) RS2 (.D(RS2_ID), .C(clk), .en(EN), .Q(RS2_EX));
  Register #(.Bits(32)) PC (.D(PC_ID), .C(clk), .en(EN), .Q(PC_EX));
  Register #(.Bits(32)) IR (.D(multiplexer_1_out), .C(clk), .en(EN), .Q(ins_EX));
  Register FLAG_jalr (.D(Flag_ID), .C(clk), .en(EN), .Q(Flag_EX));
  Register #(.Bits(32)) CSR (.D(CSR_ID), .C(clk), .en(EN), .Q(CSR_EX));
  Register #(.Bits(32)) MEM (.D(MEM_ID), .C(clk), .en(EN), .Q(MEM_EX));
  Register #(.Bits(32)) addr (.D(Addr_ID), .C(clk), .en(EN), .Q(Addr_EX));
endmodule
