// Digital circuit IF-ID.dig as structural Verilog
module IF_ID (
  input  clk,
  input  [31:0] PC_IF,
  input  [31:0] ins_IF,
  input  clr,
  input  EN,
  output [31:0] ins_ID,
  output [31:0] PC_ID
);

  wire [31:0] multiplexer_1_out;

  Multiplexer #(.Bits(32)) multiplexer_1 (.sel(clr), .in_0(ins_IF), .in_1({32{1'b0}}), .out(multiplexer_1_out));
  Register #(.Bits(32)) PC (.D(PC_IF), .C(clk), .en(EN), .Q(PC_ID));
  Register #(.Bits(32)) IR (.D(multiplexer_1_out), .C(clk), .en(EN), .Q(ins_ID));
endmodule
