// Digital circuit JALR.dig as structural Verilog
module JALR (
  input  [31:0] ins_EX,
  input  REGw,
  input  [31:0] rs1_ID,
  input  [31:0] ins_ID,
  output jump_ID,
  output [31:0] PC_jump,
  output Flag_jump
);

  wire jalr_ID_eq, not_1_out, rediect_eq;
  wire [1:0] ID_s;
  wire [19:0] bitextender_1_out;

  Comparator #(.Bits(5)) rediect (.a(ins_EX[11:7]), .b(ins_ID[19:15]), .eq(rediect_eq));  // open: gt, lt
  BitExtender #(.inputBits(1), .outputBits(20)) bitextender_1 (.in(ins_ID[31]), .out(bitextender_1_out));
  and and_1 (Flag_jump, REGw, rediect_eq);
  Comparator #(.Bits(5)) jalr_ID (.a(ins_ID[6:2]), .b(5'b11001), .eq(jalr_ID_eq));  // open: gt, lt
  Add #(.Bits(32)) ID (
    .a(rs1_ID), .b({bitextender_1_out, ins_ID[31:20]}), .c_i(1'b0), .s({PC_jump[31:2], ID_s}));  // open: c_o
  and and_2 (jump_ID, not_1_out, jalr_ID_eq);
  not not_1 (not_1_out, Flag_jump);

  assign PC_jump[1:0] = 2'b00;
endmodule
