// Digital circuit judge_branch.dig as structural Verilog
module judge_branch (
  input  [31:0] PC,
  input  [31:0] ins_EX,
  input  bxx,
  input  Flag,
  input  [31:0] rs1,
  output [31:0] PC_jump,
  output jump_EX
);

  wire and_1_out, and_2_out, bxx_eq, jalr_EX_eq, xor_1_out;
  wire [1:0] EX_bxx_s;
  wire [31:0] EX_jalr_s, multiplexer_1_out;
  wire [31:2] EX_bxx_s_2;
  wire [31:12] bitextender_1_out;
  wire [31:13] bitextender_2_out;

  BitExtender #(.inputBits(1), .outputBits(20)) bitextender_1 (.in(ins_EX[31]), .out(bitextender_1_out));
  xor xor_1 (xor_1_out, ins_EX[31], bxx);
  Comparator #(.Bits(5)) u_bxx (.a(ins_EX[6:2]), .b(5'b11000), .eq(bxx_eq));  // open: gt, lt
  Comparator #(.Bits(5)) jalr_EX (.a(ins_EX[6:2]), .b(5'b11001), .eq(jalr_EX_eq));  // open: gt, lt
  BitExtender #(.inputBits(1), .outputBits(19)) bitextender_2 (.in(ins_EX[31]), .out(bitextender_2_out));
  Add #(.Bits(32)) EX_jalr (.a({bitextender_1_out, ins_EX[31:20]}), .b(rs1), .c_i(1'b0), .s(EX_jalr_s));  // open: c_o
  Multiplexer #(.Bits(32)) multiplexer_1 (
    .sel(ins_EX[31]), .in_0({bitextender_2_out, ins_EX[31], ins_EX[7], ins_EX[30:25], ins_EX[11:9], 2'b00}),
    .in_1(32'h4), .out(multiplexer_1_out));
  and and_1 (and_1_out, xor_1_out, bxx_eq);
  and and_2 (and_2_out, Flag, jalr_EX_eq);
  Add #(.Bits(32)) EX_bxx (.a(multiplexer_1_out), .b(PC), .c_i(1'b0), .s({EX_bxx_s_2, EX_bxx_s}));  // open: c_o
  or or_1 (jump_EX, and_1_out, and_2_out);
  Multiplexer #(.Bits(32)) multiplexer_2 (
    .sel(and_1_out), .in_0({EX_jalr_s[31:2], 2'b00}), .in_1({EX_bxx_s_2, 2'b00}), .out(PC_jump));

  // Other names for the same wires on the sheet: Flag_EX = Flag; pcex[31:0] = PC; pcout[31:0] = PC_jump;
  //   rs1_EX[31:0] = rs1
endmodule
