// Digital circuit pipe-CPU-2 stage.dig as structural Verilog
module pipe_CPU_2_stage (
  input  clock,
  input  hand,
  input  model,
  input  reset,
  input  [31:0] IN,
  output [31:0] \time ,
  output [31:0] mtcmp,
  output [31:0] OUT
);

  wire and_1_out, and_2_out, break_q, brk, bxx, clk, clk_INT, CSRw, EN, ExInt, Flag_EX, Flag_ID, \int , J_EX,
       mret, mw, Mw_EX, nand_1_out, not_1_out, or_1_out, or_3_out, Rw;
  wire [2:0] wsel;
  wire [3:0] counter_1_out, ex_controller_1_aluop, ex_controller_1_alusel;
  wire [4:0] Irom_d_2, Irom_d_3, RDa;
  wire [7:0] id_ex_1_addr_ex_2;
  wire [11:0] CSRa;
  wire [31:0] branch_pre_2stage_1_mepc, branch_pre_2stage_1_pc_id, csr_1_csr, csr_1_isr, Dram_d, Drom_d,
       id_ex_1_addr_ex, id_ex_1_csr_ex, id_ex_1_ins_ex, id_ex_1_mem_ex, id_ex_1_pc_ex, id_ex_1_rs1_ex,
       id_ex_1_rs2_ex, Irom_d, judge_branch_1_pc_jump, multiplexer_2_out, prealu_1_x, prealu_1_y,
       premw_1_maddr, premw_1_mdata, prerw_1_rwdata, RS1, RS1_ID, RS2, RS2_ID;
  wire [31:1] alu_1_alur;

  Seven_Seg_Hex seven_seg_hex_1 (.d(counter_1_out), .dp(1'b0));
  Counter #(.Bits(4)) counter_1 (.en(EN), .C(clk), .clr(1'b0), .out(counter_1_out));  // open: ovf
  LED u_INT (.in(\int ));
  or or_1 (or_1_out, \int , reset);
  // Probe on judge_branch_1_pc_jump
  Multiplexer multiplexer_1 (.sel(model), .in_0(hand), .in_1(clock), .out(clk_INT));
  and and_1 (and_1_out, clk_INT, or_1_out);
  branch_pre_2stage branch_pre_2stage_1 (
    .ins_ID({Irom_d[31:25], Irom_d_3, Irom_d_2, Irom_d[14:0]}), .clk(clk), .EN(EN), .rs1(RS1_ID), .REGw(Rw),
    .RDaddr(RDa), .jump_EX(J_EX), .mret(mret), .INT(\int ), .PCjump(judge_branch_1_pc_jump), .ISR(csr_1_isr),
    .Flag_jump(Flag_ID), .pc_ID(branch_pre_2stage_1_pc_id), .mepc(branch_pre_2stage_1_mepc));
  Button key (.out(ExInt));
  LED led_1 (.in(OUT[31]));
  or or_2 (clk, clk_INT, break_q);
  D_FF_AS \break  (.Set(1'b0), .D(brk), .C(clk), .Clr(and_1_out), .Q(break_q));  // open: nQ
  // Probe on prerw_1_rwdata
  LED led_2 (.in(break_q));
  ROM #(.AddrBits(9), .Bits(32)) Irom (
    .A(branch_pre_2stage_1_pc_id[10:2]), .sel(1'b1), .D({Irom_d[31:25], Irom_d_3, Irom_d_2, Irom_d[14:0]}));
  nand nand_1 (nand_1_out, Irom_d[0], Irom_d[1]);
  RegisterFile #(.AddrBits(5), .Bits(32)) regs (
    .Din(prerw_1_rwdata), .we(Rw), .Rw(RDa), .C(clk), .Ra(Irom_d_2), .Rb(Irom_d_3), .Da(RS1_ID), .Db(RS2_ID));
  CSR csr_1 (
    .ins_ID({Irom_d[31:25], Irom_d_3, Irom_d_2, Irom_d[14:0]}), .aluR({alu_1_alur, bxx}),
    .mepc(branch_pre_2stage_1_mepc), .Wa(CSRa), .clk(clk_INT), .W_EN(CSRw), .EN(EN), .ExInt(ExInt), .IN0(IN),
    .ISR(csr_1_isr), .CSR(csr_1_csr), .INT(\int ), .OUT(OUT), .mret(mret), .test_1(\time ), .test_2(mtcmp));
  redirect redirect_1 (
    .ins_ID({Irom_d[31:25], Irom_d_3, Irom_d_2, Irom_d[14:0]}), .rs1_ID(RS1_ID), .rs2_ID(RS2_ID), .regw(Rw),
    .rd_addr(RDa), .rd_EX(prerw_1_rwdata), .RS1(RS1), .RS2(RS2));
  // Probe on {Irom_d[31:25], Irom_d_3, Irom_d_2, Irom_d[14:0]}
  or or_3 (or_3_out, nand_1_out, J_EX);
  // Probe on branch_pre_2stage_1_pc_id
  judge_branch judge_branch_1 (
    .PC(id_ex_1_pc_ex), .ins_EX(id_ex_1_ins_ex), .bxx(bxx), .Flag(Flag_EX), .rs1(id_ex_1_rs1_ex),
    .PC_jump(judge_branch_1_pc_jump), .jump_EX(J_EX));
  ID_EX id_ex_1 (
    .clr(or_3_out), .PC_ID(branch_pre_2stage_1_pc_id),
    .ins_ID({Irom_d[31:25], Irom_d_3, Irom_d_2, Irom_d[14:0]}), .clk(clk), .EN(EN), .RS1_ID(RS1),
    .RS2_ID(RS2), .Flag_ID(Flag_ID), .CSR_ID(csr_1_csr), .MEM_ID(premw_1_mdata), .Addr_ID(premw_1_maddr),
    .PC_EX(id_ex_1_pc_ex), .ins_EX(id_ex_1_ins_ex), .RS1_EX(id_ex_1_rs1_ex), .RS2_EX(id_ex_1_rs2_ex),
    .CSR_EX(id_ex_1_csr_ex), .MEM_EX(id_ex_1_mem_ex),
    .Addr_EX({id_ex_1_addr_ex[31:10], id_ex_1_addr_ex_2, id_ex_1_addr_ex[1:0]}), .Flag_EX(Flag_EX));
  preMW premw_1 (
    .ins_ID({Irom_d[31:25], Irom_d_3, Irom_d_2, Irom_d[14:0]}), .rs1(RS1), .rs2(RS2), .mData(premw_1_mdata),
    .mAddr(premw_1_maddr));
  // Probe on {Irom_d[31:25], Irom_d_3, Irom_d_2, Irom_d[14:0]}
  HALT halt_1 (
    .clk(clk), .mw_EX(Mw_EX), .ins_ID({Irom_d[31:25], Irom_d_3, Irom_d_2, Irom_d[14:0]}), .EN(EN), .memw(mw));
  // Probe on id_ex_1_ins_ex
  // Probe on id_ex_1_rs1_ex
  // Probe on id_ex_1_mem_ex
  // Probe on premw_1_maddr
  EX_controller ex_controller_1 (
    .ins_EX(id_ex_1_ins_ex), .regw(Rw), .csraddr(CSRa), .RDa(RDa), .rwsel(wsel), .brk(brk), .csrw(CSRw),
    .mw(Mw_EX), .alusel(ex_controller_1_alusel), .aluop(ex_controller_1_aluop));
  // Probe on id_ex_1_pc_ex
  preALU prealu_1 (
    .alusel(ex_controller_1_alusel), .pc_alu(id_ex_1_pc_ex), .ins_alu(id_ex_1_ins_ex), .rs1(id_ex_1_rs1_ex),
    .rs2(id_ex_1_rs2_ex), .csr(id_ex_1_csr_ex), .x(prealu_1_x), .y(prealu_1_y));
  // Probe on {id_ex_1_addr_ex[31:10], id_ex_1_addr_ex_2, id_ex_1_addr_ex[1:0]}
  not not_1 (not_1_out, clk);
  // Probe on id_ex_1_csr_ex
  // Probe on prealu_1_x
  // Probe on prealu_1_y
  ROM #(.AddrBits(8), .Bits(32)) Drom (.A(id_ex_1_addr_ex_2), .sel(1'b1), .D(Drom_d));
  RAMDualPort #(.AddrBits(8), .Bits(32)) Dram (
    .A(id_ex_1_addr_ex_2), .Din(id_ex_1_mem_ex), .str(and_2_out), .C(not_1_out), .ld(1'b1), .D(Dram_d));
  ALU alu_1 (.aluop(ex_controller_1_aluop), .x(prealu_1_x), .y(prealu_1_y), .aluR({alu_1_alur, bxx}));
  and and_2 (and_2_out, mw, id_ex_1_addr_ex[10]);
  Multiplexer #(.Bits(32)) multiplexer_2 (
    .sel(id_ex_1_addr_ex[10]), .in_0(Drom_d), .in_1(Dram_d), .out(multiplexer_2_out));
  preRW prerw_1 (
    .aluR({alu_1_alur, bxx}), .sel(wsel), .ramData(multiplexer_2_out), .csrData(id_ex_1_csr_ex),
    .rwData(prerw_1_rwdata));
  // Probe on {alu_1_alur, bxx}
  // Probe on multiplexer_2_out

  // Other names for the same wires on the sheet: in0[31:0] = IN; out0[31:0] = OUT

  // Notes on the sheet:
  //   clock: Hz: 2
  //   contents of Irom (hex, n*v repeats v):
  //   3000293,30529073,1000493,30649073,8000313,30431073,431313,30432073,30045073,13,10500073,
  //   ff9ff0ef,30001073,35009073,35129073,35231073,344022f3,18000ef,350020f3,351022f3,35202373,
  //   30045073,200073,b2d313,30c63,33002373,fff34313,33031073,fff34313,33031073,72d313,
  //   137313,2030063,1048493,30649073,330022f3,1f2d293,12b293,1f29293,33029073,80e7
  //   contents of Drom (hex, n*v repeats v):
  //   0,fffff0b7,400093,40016f,158513,feb50fe3,fff20193,318233,308023,309023,30a023,40a223,
  //   402383,800403,801403,804403,805403,802403,ff3a413,ffe3b413,fff44413,247493,249513,
  //   1f4d593,25d593,40125613,40460633,c616b3,c42733,c43733,864733,e6d7b3,40f75733,d77733,
  //   c76833,200713,11d873,11d873,810f3,710f3,a973,25973,1039f3,10f9f3,e7
endmodule
