// Digital circuit preMW.dig as structural Verilog
module preMW (
  input  [31:0] ins_ID,
  input  [31:0] rs1,
  input  [31:0] rs2,
  output [31:0] mData,
  output [31:0] mAddr
);

  wire sx_eq;
  wire [19:0] bitextender_1_out, bitextender_2_out;
  wire [31:0] multiplexer_2_out;

  BitExtender #(.inputBits(1), .outputBits(20)) bitextender_1 (.in(ins_ID[31]), .out(bitextender_1_out));
  BitExtender #(.inputBits(1), .outputBits(20)) bitextender_2 (.in(ins_ID[31]), .out(bitextender_2_out));
  Comparator #(.Bits(5)) sx (.a(ins_ID[6:2]), .b(5'b01000), .eq(sx_eq));  // open: gt, lt
  Multiplexer #(.Selector_Bits(2), .Bits(32)) multiplexer_1 (
    .sel(ins_ID[13:12]), .in_0({{24{1'b0}}, rs2[7:0]}), .in_1({{16{1'b0}}, rs2[15:0]}), .in_2(rs2),
    .in_3({32{1'b0}}), .out(mData));
  Multiplexer #(.Bits(32)) multiplexer_2 (
    .sel(sx_eq), .in_0({bitextender_1_out, ins_ID[31:20]}),
    .in_1({bitextender_2_out, ins_ID[31:25], ins_ID[11:7]}), .out(multiplexer_2_out));
  Add #(.Bits(32)) plus (.a(multiplexer_2_out), .b(rs1), .c_i(1'b0), .s(mAddr));  // open: c_o

  // Other names for the same wires on the sheet: addr[31:0] = mAddr; data[31:0] = mData; ins[31:0] = ins_ID

  // Notes on the sheet:
  //   lx
  //   sx
endmodule
