// Digital circuit preRW.dig as structural Verilog
module preRW (
  input  [31:0] aluR,
  input  [2:0] sel,
  input  [31:0] ramData,
  input  [31:0] csrData,
  output [31:0] rwData
);

  wire [15:0] bitextender_2_out, multiplexer_2_out;
  wire [23:0] bitextender_1_out, multiplexer_1_out;
  wire [31:0] multiplexer_3_out;

  BitExtender #(.inputBits(1), .outputBits(24)) bitextender_1 (.in(ramData[7]), .out(bitextender_1_out));
  BitExtender #(.inputBits(1)) bitextender_2 (.in(ramData[15]), .out(bitextender_2_out));
  Multiplexer #(.Bits(24)) multiplexer_1 (
    .sel(sel[2]), .in_0(bitextender_1_out), .in_1({24{1'b0}}), .out(multiplexer_1_out));
  Multiplexer #(.Bits(16)) multiplexer_2 (
    .sel(sel[2]), .in_0(bitextender_2_out), .in_1({16{1'b0}}), .out(multiplexer_2_out));
  Multiplexer #(.Bits(32)) multiplexer_3 (.sel(sel[2]), .in_0(csrData), .in_1(aluR), .out(multiplexer_3_out));
  Multiplexer #(.Selector_Bits(2), .Bits(32)) multiplexer_4 (
    .sel(sel[1:0]), .in_0({multiplexer_1_out, ramData[7:0]}), .in_1({multiplexer_2_out, ramData[15:0]}),
    .in_2(ramData), .in_3(multiplexer_3_out), .out(rwData));

  // Other names for the same wires on the sheet: aluD[31:0] = aluR; csrD[31:0] = csrData; ramD[31:0] = ramData;
  //   regD[31:0] = rwData
endmodule
