// Digital circuit FSM.dig as structural Verilog
module FSM (
  input  done,
  input  rdy,
  input  start,
  input  stop,
  input  C,
  output sign
);

  wire and_1_out, and_2_out, and_3_out, not_1_out, not_2_out, not_3_out, or_1_out, Z_0_n;

  not not_1 (not_1_out, done);
  not not_2 (not_2_out, rdy);
  not not_3 (not_3_out, stop);
  not not_4 (sign, Z_0_n);
  and and_1 (and_1_out, sign, not_2_out, start);
  and and_2 (and_2_out, Z_0_n, not_3_out);
  and and_3 (and_3_out, Z_0_n, not_1_out);
  or or_1 (or_1_out, and_1_out, and_2_out, and_3_out);
  D_FF u_Z_0_n (.D(or_1_out), .C(C), .Q(Z_0_n));  // open: nQ

  // Notes on the sheet:
  //   C: Hz: 2
endmodule
