// Digital circuit iic.dig as structural Verilog
module iic (
  input  SDA_in,
  input  [7:0] Txdata,
  input  W_nR,
  input  [7:0] rate,
  input  EN,
  input  SDAout,
  input  START,
  input  STOP,
  input  clk,
  output SDA_out,
  output [7:0] rdata,
  output SCL,
  output rdy,
  output dev_ack,
  output IIC_port,
  output SDAin
);

  wire and_1_out, and_2_out, and_3_out, and_4_out, and_5_out, comparator_1_eq, DACK, done, jk_ff_1_q, q0, q1,
       q2, q3, q4, q5, q6, q7, que1_ovf;
  wire [0:0] undriven;
  wire [3:0] sel;
  wire [7:0] CNT1_out;

  and and_1 (and_1_out, ~W_nR, SCL);  // And
  and and_2 (and_2_out, SCL, DACK);
  and and_3 (and_3_out, rdy, EN);
  D_FF d_ff_1 (.D(SDA_in), .C(and_1_out), .Q(q0));  // open: nQ
  D_FF d_ff_2 (.D(SDA_in), .C(and_2_out), .nQ(dev_ack));  // open: Q
  JK_FF jk_ff_1 (.J(and_3_out), .C(clk), .K(done), .Q(jk_ff_1_q), .nQ(rdy));
  D_FF d_ff_3 (.D(q0), .C(and_1_out), .Q(q1));  // open: nQ
  FSM fsm_1 (.done(done), .rdy(rdy), .start(START), .stop(STOP), .C(clk));  // open: sign
  D_FF d_ff_4 (.D(q1), .C(and_1_out), .Q(q2));  // open: nQ
  Counter #(.Bits(8)) CNT1 (.en(jk_ff_1_q), .C(clk), .clr(comparator_1_eq), .out(CNT1_out));  // open: ovf
  D_FF d_ff_5 (.D(q2), .C(and_1_out), .Q(q3));  // open: nQ
  // Probe on CNT1_out
  Comparator #(.Bits(8)) comparator_1 (.a(CNT1_out), .b({1'b0, rate[7:1]}), .eq(comparator_1_eq));  // open: gt, lt
  // Probe on {1'b0, rate[7:1]}
  D_FF d_ff_6 (.D(q3), .C(and_1_out), .Q(q4));  // open: nQ
  JK_FF_AS jk_ff_as_1 (.Set(1'b0), .J(comparator_1_eq), .C(clk), .K(comparator_1_eq), .Clr(rdy), .nQ(SCL));  // open: Q
  BitSelector #(.Selector_Bits(4)) bitselector_1 (
    .in({{6{1'b0}}, Txdata, 1'b1, undriven[0]}), .sel(sel), .out(SDA_out));
  // Probe on sel
  D_FF d_ff_7 (.D(q4), .C(and_1_out), .Q(q5));  // open: nQ
  D_FF d_ff_8 (.D(q5), .C(and_1_out), .Q(q6));  // open: nQ
  D_FF d_ff_9 (.D(q6), .C(and_1_out), .Q(q7));  // open: nQ
  CounterPreset #(.maxValue(9), .Bits(4)) que1 (
    .en(1'b1), .C(~SCL), .dir(1'b1), .in(4'b0000), .ld(1'b0), .clr(rdy), .out(sel), .ovf(que1_ovf));
  and and_4 (and_4_out, ~DACK, W_nR);  // And
  // PinControl pincontrol_1: pin names not known; wires that end beside it: SDAout, and_4_out, SDAin, IIC_port
  Comparator #(.Bits(4)) comparator_2 (.a(sel), .b(4'b0001), .eq(DACK));  // open: gt, lt
  D_FF_AS d_ff_as_1 (.Set(1'b0), .D(que1_ovf), .C(SCL), .Clr(rdy), .Q(done));  // open: nQ
  D_FF #(.Bits(8)) d_ff_10 (.D({q7, q6, q5, q4, q3, q2, q1, q0}), .C(and_5_out), .Q(rdata));  // open: nQ
  and and_5 (and_5_out, ~W_nR, DACK);  // And

  // Other names for the same wires on the sheet: rate_t[6:0] = rate[7:1]

  // Notes on the sheet:
  //   rate: default 2
endmodule
