// Digital circuit spi.dig as structural Verilog
module spi (
  input  [7:0] txdata,
  input  [7:0] rate,
  input  clk,
  input  MISO,
  input  EN,
  output rdy,
  output SCK,
  output MOSI,
  output [7:0] rxdata,
  output [3:0] CNT
);

  wire and_1_out, and_2_out, comparator_2_eq, d_ff_1_q, d_ff_2_q, d_ff_3_q, d_ff_4_q, d_ff_5_q, d_ff_6_q,
       d_ff_7_q, d_ff_8_q, d_ff_9_q, done, jk_ff_1_q, load, que1_ovf;
  wire [7:0] CNT1_out, multiplexer_1_out;

  D_FF d_ff_1 (.D(MISO), .C(SCK), .Q(d_ff_1_q));  // open: nQ
  Multiplexer multiplexer_1 (.sel(load), .in_0(txdata[0]), .in_1(d_ff_1_q), .out(multiplexer_1_out[0]));
  and and_1 (and_1_out, ~SCK, ~rdy);  // And
  D_FF d_ff_2 (.D(multiplexer_1_out[0]), .C(and_1_out), .Q(d_ff_2_q));  // open: nQ
  Multiplexer multiplexer_2 (.sel(load), .in_0(txdata[1]), .in_1(d_ff_2_q), .out(multiplexer_1_out[1]));
  CounterPreset #(.maxValue(8), .Bits(4)) que1 (
    .en(1'b1), .C(~SCK), .dir(1'b0), .in(4'b0000), .ld(1'b0), .clr(rdy), .out(CNT), .ovf(que1_ovf));
  D_FF d_ff_3 (.D(multiplexer_1_out[1]), .C(and_1_out), .Q(d_ff_3_q));  // open: nQ
  D_FF_AS d_ff_as_1 (.Set(1'b0), .D(que1_ovf), .C(~SCK), .Clr(rdy), .Q(done));  // open: nQ
  Multiplexer multiplexer_3 (.sel(load), .in_0(txdata[2]), .in_1(d_ff_3_q), .out(multiplexer_1_out[2]));
  D_FF d_ff_4 (.D(multiplexer_1_out[2]), .C(and_1_out), .Q(d_ff_4_q));  // open: nQ
  Comparator #(.Bits(4)) comparator_1 (.a(CNT), .b(4'b0000), .gt(load));  // open: eq, lt
  Multiplexer multiplexer_4 (.sel(load), .in_0(txdata[3]), .in_1(d_ff_4_q), .out(multiplexer_1_out[3]));
  D_FF d_ff_5 (.D(multiplexer_1_out[3]), .C(and_1_out), .Q(d_ff_5_q));  // open: nQ
  Multiplexer multiplexer_5 (.sel(load), .in_0(txdata[4]), .in_1(d_ff_5_q), .out(multiplexer_1_out[4]));
  D_FF d_ff_6 (.D(multiplexer_1_out[4]), .C(and_1_out), .Q(d_ff_6_q));  // open: nQ
  and and_2 (and_2_out, rdy, EN);
  Multiplexer multiplexer_6 (.sel(load), .in_0(txdata[5]), .in_1(d_ff_6_q), .out(multiplexer_1_out[5]));
  JK_FF jk_ff_1 (.J(and_2_out), .C(clk), .K(done), .Q(jk_ff_1_q), .nQ(rdy));
  D_FF d_ff_7 (.D(multiplexer_1_out[5]), .C(and_1_out), .Q(d_ff_7_q));  // open: nQ
  Multiplexer multiplexer_7 (.sel(load), .in_0(txdata[6]), .in_1(d_ff_7_q), .out(multiplexer_1_out[6]));
  Counter #(.Bits(8)) CNT1 (.en(jk_ff_1_q), .C(clk), .clr(comparator_2_eq), .out(CNT1_out));  // open: ovf
  D_FF d_ff_8 (.D(multiplexer_1_out[6]), .C(and_1_out), .Q(d_ff_8_q));  // open: nQ
  // Probe on CNT1_out
  Comparator #(.Bits(8)) comparator_2 (.a(CNT1_out), .b({1'b0, rate[7:1]}), .eq(comparator_2_eq));  // open: gt, lt
  // Probe on {1'b0, rate[7:1]}
  Multiplexer multiplexer_8 (.sel(load), .in_0(txdata[7]), .in_1(d_ff_8_q), .out(multiplexer_1_out[7]));
  D_FF d_ff_9 (.D(multiplexer_1_out[7]), .C(and_1_out), .Q(d_ff_9_q));  // open: nQ
  JK_FF_AS jk_ff_as_1 (.Set(1'b0), .J(comparator_2_eq), .C(clk), .K(comparator_2_eq), .Clr(rdy), .nQ(SCK));  // open: Q
  Multiplexer multiplexer_9 (.sel(load), .in_0(1'b1), .in_1(d_ff_9_q), .out(MOSI));
  D_FF #(.Bits(8)) d_ff_10 (.D(multiplexer_1_out), .C(done), .Q(rxdata));  // open: nQ

  // Other names for the same wires on the sheet: rate_t[6:0] = rate[7:1]

  // Notes on the sheet:
  //   txdata: default 170
  //   rate: default 2
  //   MISO: default 1
  //   Master {{de Master}}
endmodule
