// Digital circuit VGA.dig as structural Verilog
// Designed for a 
// 25.175MHz clock.
// Generates 
// 640x480@60Hz
// {{de Ausgelegt für einen 
// 25.175MHz Takt.
// Erzeugt
// 640x480@60Hz}}
module VGA (
  input  CLK,
  input  RST
);

  wire undriven, undriven_2, vld;
  wire [19:0] counterpreset_1_out;
  wire [23:0] multiplexer_1_out, rom_1_d;

  CounterPreset #(.maxValue(307200), .Bits(20)) counterpreset_1 (
    .en(vld), .C(CLK), .dir(1'b0), .in({20{1'b0}}), .ld(1'b0), .clr(RST), .out(counterpreset_1_out));  // open: ovf
  // Probe on counterpreset_1_out
  ROM #(.AddrBits(20), .Bits(24)) rom_1 (.A(counterpreset_1_out), .sel(1'b1), .D(rom_1_d));
  sync sync_1 (.RST(CLK), .C(RST), .vld(vld));  // open: H, V
  Multiplexer #(.Bits(24)) multiplexer_1 (.sel(vld), .in_0({24{1'b0}}), .in_1(rom_1_d), .out(multiplexer_1_out));
  VGA vga_1 (
    .R(multiplexer_1_out[7:0]), .G(multiplexer_1_out[15:8]), .B(multiplexer_1_out[23:16]), .H(undriven),
    .V(undriven_2), .C(CLK));

  // Other names for the same wires on the sheet: c = CLK

  // Notes on the sheet:
  //   CLK: Hz: 25000000
  //   contents of rom_1 (hex, n*v repeats v):
  //   ff0000,ff0000,ff0000,ff0000,ff0000,ff0000,ff0000,ff0000,ff0000,ff0000,ff0000,ff0000,
  //   ff0000,ff0000,ff0000,ff0000,ff0000,ff0000,ff0000,ff0000,ff0000,ff0000,ff0000,ff0000,
  //   ff0000,ff0000,ff0000,ff0000,ff0000,ff0000,ff0000,ff0000,ff0000,ff0000,ff0000,ff0000,
  //   ff0000,ff0000,ff0000,ff0000,ff0000,ff0000,ff0000,ff0000,ff0000,ff0000,ff0000,ff0000,
  //   ff0000,ff0000,ff0000,ff0000,ff0000,ff0000,ff0000,ff0000,ff0000,ff0000,ff0000,ff0000,
  //   ff0000,ff0000,ff0000,ff0000,ff0000,ff0000,ff0000,ff0000,ff0000,ff0000,ff0000,ff0000,
  //   ff0000,ff0000,ff0000,ff0000,ff0000,ff0000,ff0000,ff0000,ff0000,ff0000,ff0000,ff0000,
  //   ff0000,ff0000,ff0000,ff0000,ff0000,ff0000,ff0000,ff0000,ff0000,ff0000,ff0000,ff0000,
  //   ff0000,ff0000,ff0000,ff0000,ff0000,ff0000,ff0000,ff0000,ff0000,ff0000,ff0000,ff0000,
  //   ff0000,ff0000,ff0000,ff0000,ff0000,ff0000,ff0000,ff0000,ff0000,ff0000,ff0000,ff0000,
  //   ff0000,ff0000,ff0000,ff0000,ff0000,ff0000,ff0000,ff0000,ff0000,ff0000,ff0000,ff0000,
  //   ff0000,ff0000,ff0000,ff0000,ff0000,ff0000,ff0000,ff0000,ff0000,ff0000,ff0000,ff0000,
  //   ff0000,ff0000,ff0000,ff0000,ff0000,ff0000,ff0000,ff0000,ff0000,ff0000,ff0000,ff0000,
  //   ff0000,ff0000,ff0000,ff0000,ff0000,ff0000,ff0000,ff0000,ff0000,ff0000,ff0000,ff0000,
  //   ff0000,ff0000,ff0000,ff0000,ff0000,ff0000,ff0000,ff0000,ff0000,ff0000,ff0000,ff0000,
  //   ff0000,ff0000,ff0000,ff0000,ff0000,ff0000,ff0000,ff0000,ff0000,ff0000,ff0000,ff0000,
  //   ff0000,ff0000,ff0000,ff0000,ff0000,ff0000,ff0000,ff0000,ff0000,ff0000,ff0000,ff0000,
  //   ff0000,ff0000,ff0000,ff0000,ff0000,ff0000,ff0000,ff0000,ff0000,ff0000,ff0000,ff0000,
  //   ff0000,ff0000,ff0000,ff0000,ff0000,ff0000,ff0000,ff0000,ff0000,ff0000,ff0000,ff0000,
  //   ff0000,ff0000,ff0000,ff0000,ff0000,ff0000,ff0000,ff0000,ff0000,ff0000,ff0000,ff0000,
  //   ff0000,ff0000,ff0000,ff0000,ff0000,ff0000,ff0000,ff0000,ff0000,ff0000,ff0000,ff0000,
  //   ff0000,ff0000,ff0000,ff0000,ff0000,ff0000,ff0000,ff0000,ff0000,ff0000,ff0000,ff0000,
  //   ff0000,ff0000,ff0000,ff0000,ff0000,ff0000,ff0000,ff0000,ff0000,ff0000,ff0000,ff0000,
  //   ff0000,ff0000,ff0000,ff0000,ff0000,ff0000,ff0000,ff0000,ff0000,ff0000,ff0000,ff0000,
  //   ff0000,ff0000,ff0000,ff0000,ff0000,ff0000,ff0000,ff0000,ff0000,ff0000,ff0000,ff0000,
  //   ff0000,ff0000,ff0000,ff0000,ff0000,ff0000,ff0000,ff0000,ff0000,ff0000,ff0000,ff0000,
  //   ff0000,ff0000,ff0000,ff0000,ff0000,ff0000,ff0000,ff0000,ff0000,ff0000,ff0000,ff0000,
  //   ff0000,ff0000,ff0000,ff0000,ff0000,ff0000,ff0000,ff0000,ff0000,ff0000,ff0000,ff0000,
  //   ff0000,ff0000,ff0000,ff0000,ff0000,ff0000,ff0000,ff0000,ff0000,ff0000,ff0000,ff0000,
  //   ff0000,ff0000,ff0000,ff0000,ff0000,ff0000,ff0000,ff0000,ff0000,ff0000,ff0000,ff0000,
  //   ff0000,ff0000,ff0000,ff0000,ff0000,ff0000,ff0000,ff0000,ff0000,ff0000,ff0000,ff0000,
  //   ff0000,ff0000,ff0000,ff0000,ff0000,ff0000,ff0000,ff0000,ff0000,ff0000,ff0000,ff0000,
  //   ff0000,ff0000,ff0000,ff0000,ff0000,ff0000,ff0000,ff0000,ff0000,ff0000,ff0000,ff0000,
  //   ff0000,ff0000,ff0000,ff0000,ff0000,ff0000,ff0000,ff0000,ff0000,ff0000,ff0000,ff0000,
  //   ff0000,ff0000,ff0000,ff0000,ff0000,ff0000,ff0000,ff0000,ff0000,ff0000,ff0000,ff0000,
  //   ff0000,ff0000,ff0000,ff0000,ff0000,ff0000,ff0000,ff0000,ff0000,ff0000,ff0000,ff0000,
  //   ff0000,ff0000,ff0000,ff0000,ff0000,ff0000,ff0000,ff0000,ff0000,ff0000,ff0000,ff0000,
  //   ff0000,ff0000,ff0000,ff0000,ff0000,ff0000,ff0000,ff0000,ff0000,ff0000,ff0000,ff0000,
  //   ff0000,ff0000,ff0000,ff0000,ff0000,ff0000,ff0000,ff0000,ff0000,ff0000,ff0000,ff0000,
  //   ff0000,ff0000,ff0000,ff0000,ff0000,ff0000,ff0000,ff0000,ff0000,ff0000,ff0000,ff0000,
  //   ff0000,ff0000,ff0000,ff0000,ff0000,ff0000,ff0000,ff0000,ff0000,ff0000,ff0000,ff0000,
  //   ff0000,ff0000,ff0000,ff0000,ff0000,ff0000,ff0000,ff0000,ff0000,ff0000,ff0000,ff0000,
  //   ff0000,ff0000,ff0000,ff0000,ff0000,ff0000,ff0000,ff0000,ff0000,ff0000,ff0000,ff0000,
  //   ff0000,ff0000,ff0000,ff0000,ff0000,ff0000,ff0000,ff0000,ff0000,ff0000,ff0000,ff0000,
  //   ff0000,ff0000,ff0000,ff0000,ff0000,ff0000,ff0000,ff0000,ff0000,ff0000,ff0000,ff0000,
  //   ff0000,ff0000,ff0000,ff0000,ff0000,ff0000,ff0000,ff0000,ff0000,ff0000,ff0000,ff0000,
  //   ff0000,ff0000,ff0000,ff0000,ff0000,ff0000,ff0000,ff0000,ff0000,ff0000,ff0000,ff0000,
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endmodule
