// Digital circuit VGA_sync.dig as structural Verilog
// Designed for a 
// 25.175MHz clock.
// Generates 
// 640x480@60Hz
// {{de Ausgelegt für einen 
// 25.175MHz Takt.
// Erzeugt
// 640x480@60Hz}}
module VGA_sync (
  input  RST,
  input  clk,
  output vld,
  output H,
  output V
);

  wire and_1_out, and_2_out, and_3_out, and_4_out, comparator_1_eq, comparator_2_eq, comparator_3_eq,
       comparator_4_eq, comparator_5_eq, comparator_6_eq, comparator_7_eq, comparator_8_eq, jk_ff_as_2_nq,
       jk_ff_as_3_nq, or_1_out, or_2_out;
  wire [9:0] h_cnt_out, v_cnt_out;

  Counter #(.Bits(10)) h_cnt (.en(1'b1), .C(clk), .clr(or_1_out), .out(h_cnt_out));  // open: ovf
  or or_1 (or_1_out, RST, comparator_4_eq);
  // Probe X on h_cnt_out
  Comparator #(.Bits(10)) comparator_1 (.a(h_cnt_out), .b(10'h28f), .eq(comparator_1_eq));  // open: gt, lt
  Comparator #(.Bits(10)) comparator_2 (.a(h_cnt_out), .b(10'h2ef), .eq(comparator_2_eq));  // open: gt, lt
  Comparator #(.Bits(10)) comparator_3 (.a(h_cnt_out), .b(10'h27f), .eq(comparator_3_eq));  // open: gt, lt
  Comparator #(.Bits(10)) comparator_4 (.a(h_cnt_out), .b(10'h31f), .eq(comparator_4_eq));  // open: gt, lt
  Counter #(.Bits(10)) v_cnt (.en(comparator_4_eq), .C(clk), .clr(or_2_out), .out(v_cnt_out));  // open: ovf
  or or_2 (or_2_out, RST, and_2_out);
  JK_FF_AS jk_ff_as_1 (.Set(1'b0), .J(comparator_1_eq), .C(clk), .K(comparator_2_eq), .Clr(RST), .nQ(H));  // open: Q
  JK_FF_AS jk_ff_as_2 (
    .Set(1'b0), .J(comparator_3_eq), .C(clk), .K(comparator_4_eq), .Clr(RST), .nQ(jk_ff_as_2_nq));  // open: Q
  // Probe Y on v_cnt_out
  Comparator #(.Bits(10)) comparator_5 (.a(v_cnt_out), .b(10'h1df), .eq(comparator_5_eq));  // open: gt, lt
  Comparator #(.Bits(10)) comparator_6 (.a(v_cnt_out), .b(10'h20c), .eq(comparator_6_eq));  // open: gt, lt
  Comparator #(.Bits(10)) comparator_7 (.a(v_cnt_out), .b(10'h1e9), .eq(comparator_7_eq));  // open: gt, lt
  Comparator #(.Bits(10)) comparator_8 (.a(v_cnt_out), .b(10'h1eb), .eq(comparator_8_eq));  // open: gt, lt
  and and_1 (and_1_out, comparator_4_eq, comparator_5_eq);
  and and_2 (and_2_out, comparator_4_eq, comparator_6_eq);
  and and_3 (and_3_out, comparator_4_eq, comparator_7_eq);
  and and_4 (and_4_out, comparator_4_eq, comparator_8_eq);
  and and_5 (vld, jk_ff_as_2_nq, jk_ff_as_3_nq);
  JK_FF_AS jk_ff_as_3 (.Set(1'b0), .J(and_1_out), .C(clk), .K(and_2_out), .Clr(RST), .nQ(jk_ff_as_3_nq));  // open: Q
  JK_FF_AS jk_ff_as_4 (.Set(1'b0), .J(and_3_out), .C(clk), .K(and_4_out), .Clr(RST), .nQ(V));  // open: Q

  // Other names for the same wires on the sheet: C = clk; CLR = RST

  // Notes on the sheet:
  //   clk: Hz: 20
endmodule

/* Test case H:
clk H vld X

repeat(799) C x x  x

loop (n,3)
loop (p,800)
C  ((p<640+16)|(p>=640+16+96)) (p<640) (p)
end loop
end loop
*/

/* Test case X-Y:
C X Y oe H-sync V-sync

# skip first image
repeat(419999) C x x x x x

# test second image coordiates
loop (i,2)
  loop (y,525)
    loop (x,800)
      C (x) (y) ((x<640)&(y<480)) ((x<640+16)|(x>=640+16+96)) ((y<480+10)|(y>=480+12))
    end loop
  end loop
end loop
*/
