// Digital circuit IO.dig as structural Verilog
module IO (
  input  [31:0] aluR,
  input  [11:0] csrAddr,
  input  clk,
  input  W_EN,
  input  RX,
  input  [31:0] IN0,
  output IOint,
  output [31:0] ioData,
  output [31:0] OUT,
  output TX
);

  wire and_1_out, and_2_out, and_3_out, and_4_out, and_5_out, and_6_out, and_7_out, and_8_out, and_9_out,
       comparator_1_eq, comparator_2_eq, comparator_3_eq, comparator_4_eq, comparator_5_eq, comparator_6_eq,
       comparator_7_eq, TXvld;
  wire [1:0] iostatus;
  wire [2:0] priorityencoder_1_num;
  wire [7:0] RXdata, TXdata;
  wire [15:0] TXrate;
  wire [15:1] uConfig;
  wire [31:8] uTX;

  uart uart_1 (
    .CLK(clk), .TX_vld(TXvld), .RATE(TXrate), .TX_data(TXdata), .RX(RX));  // open: RX_data, RX_rdy, RX_vld, TX_rdy, TX
  Comparator #(.Bits(4)) comparator_1 (.a(csrAddr[11:8]), .b(4'b0011), .eq(comparator_1_eq));  // open: gt, lt
  Comparator #(.Bits(8)) comparator_2 (.a(csrAddr[7:0]), .b(8'h30), .eq(comparator_2_eq));  // open: gt, lt
  Comparator #(.Bits(8)) comparator_3 (.a(csrAddr[7:0]), .b(8'h31), .eq(comparator_3_eq));  // open: gt, lt
  Comparator #(.Bits(8)) comparator_4 (.a(csrAddr[7:0]), .b(8'h32), .eq(comparator_4_eq));  // open: gt, lt
  Comparator #(.Bits(8)) comparator_5 (.a(csrAddr[7:0]), .b(8'h33), .eq(comparator_5_eq));  // open: gt, lt
  Comparator #(.Bits(8)) comparator_6 (.a(csrAddr[7:0]), .b(8'h34), .eq(comparator_6_eq));  // open: gt, lt
  Comparator #(.Bits(8)) comparator_7 (.a(csrAddr[7:0]), .b(8'h3f), .eq(comparator_7_eq));  // open: gt, lt
  and and_1 (and_1_out, comparator_1_eq, comparator_2_eq);
  and and_2 (and_2_out, comparator_1_eq, comparator_3_eq);
  and and_3 (and_3_out, comparator_1_eq, comparator_4_eq);
  and and_4 (and_4_out, comparator_1_eq, comparator_5_eq);
  and and_5 (and_5_out, comparator_1_eq, comparator_6_eq);
  and and_6 (and_6_out, comparator_1_eq, comparator_7_eq);
  and and_7 (and_7_out, and_1_out, W_EN);
  and and_8 (and_8_out, and_3_out, W_EN);
  and and_9 (and_9_out, and_4_out, W_EN);
  PriorityEncoder #(.Selector_Bits(3)) priorityencoder_1 (
    .in0(1'b0), .in1(and_1_out), .in2(and_2_out), .in3(and_3_out), .in4(and_4_out), .in5(and_5_out),
    .in6(and_6_out), .in7(1'b0), .num(priorityencoder_1_num));  // open: any
  Register #(.Bits(32)) u_out (.D(aluR), .C(clk), .en(and_7_out), .Q(OUT));
  Register #(.Bits(32)) u_uConfig (.D(aluR), .C(clk), .en(and_8_out), .Q({TXrate, uConfig, TXvld}));
  Register #(.Bits(32)) uTXdata (.D(aluR), .C(clk), .en(and_9_out), .Q({uTX, TXdata}));
  // Probe on OUT
  // Probe on priorityencoder_1_num
  Multiplexer #(.Selector_Bits(3), .Bits(32)) multiplexer_1 (
    .sel(priorityencoder_1_num), .in_0({32{1'b0}}), .in_1(OUT), .in_2({{30{1'b0}}, iostatus}),
    .in_3({TXrate, uConfig, TXvld}), .in_4({uTX, TXdata}), .in_5({{24{1'b0}}, RXdata}), .in_6(IN0),
    .in_7({32{1'b0}}), .out(ioData));
  // Probe on ioData

  // Other names for the same wires on the sheet: addr[11:0] = csrAddr; Din[31:0] = aluR; Dout[31:0] = ioData;
  //   IN_0[31:0] = IN0; out0[31:0] = OUT; RXrdy = iostatus[1]; RXvld = IOint; TXrdy = iostatus[0];
  //   uConfig (some bits) = {TXrate, TXvld}; uTX[7:0] = TXdata; we = W_EN
endmodule
