// Digital circuit mono-controller.dig as structural Verilog
module mono_controller (
  input  [31:0] ins,
  output [1:0] pcsel,
  output [3:0] aluop,
  output [3:0] alusel,
  output [2:0] wsel,
  output rw,
  output brk,
  output csrw,
  output mw,
  output mr,
  output mret
);

  wire and_3_out, or_1_out, or_2_out, or_3_out, r_w_1_csrw, r_w_1_mr, r_w_1_mw, r_w_1_rw, RV32;
  wire [2:0] and_1_out, and_2_out, bitextender_1_out, bitextender_2_out;

  or or_1 (or_1_out, r_w_1_mw, r_w_1_mr);
  r_w r_w_1 (
    .OP6(ins[6]), .OP5(ins[5]), .OP4(ins[4]), .OP3(ins[3]), .OP2(ins[2]), .mr(r_w_1_mr), .mw(r_w_1_mw),
    .csrw(r_w_1_csrw), .rw(r_w_1_rw));
  or or_2 (or_2_out, ins[7], ins[8], ins[9], ins[10], ins[11]);
  BitExtender #(.inputBits(1), .outputBits(3)) bitextender_1 (.in(csrw), .out(bitextender_1_out));
  BitExtender #(.inputBits(1), .outputBits(3)) bitextender_2 (.in(or_1_out), .out(bitextender_2_out));
  assign and_1_out = 3'b100 & bitextender_1_out;  // And and_1, 3 bits wide
  assign and_2_out = ~ins[14:12] & bitextender_2_out;  // And and_2, 3 bits wide
  and and_3 (and_3_out, ~or_3_out, r_w_1_csrw, RV32);  // And
  and and_4 (rw, r_w_1_rw, or_2_out, RV32);
  assign wsel = ~(and_1_out | and_2_out);  // NOr nor_1, 3 bits wide
  and and_5 (mr, r_w_1_mr, RV32);
  and and_6 (mw, r_w_1_mw, RV32);
  or or_3 (or_3_out, ins[12], ins[13], ins[14]);
  and and_7 (RV32, ins[0], ins[1]);
  and and_8 (csrw, RV32, r_w_1_csrw, or_3_out);
  and and_9 (brk, and_3_out, ins[20]);
  and and_10 (mret, and_3_out, ~ins[20]);  // And
  pcsel pcsel_1 (.OP6(ins[6]), .OP5(ins[5]), .OP4(ins[4]), .OP3(ins[3]), .OP2(ins[2]), .P1(pcsel[1]), .P0(pcsel[0]));
  alusel alusel_1 (
    .op6(ins[6]), .op5(ins[5]), .op4(ins[4]), .op3(ins[3]), .op2(ins[2]), .F2(ins[14]), .F1(ins[13]),
    .F0(ins[12]), .asel3(alusel[3]), .asel2(alusel[2]), .asel1(alusel[1]), .asel0(alusel[0]));
  aluop aluop_1 (
    .op6(ins[6]), .op5(ins[5]), .op4(ins[4]), .op3(ins[3]), .op2(ins[2]), .F2(ins[14]), .F1(ins[13]),
    .F0(ins[12]), .b(ins[30]), .aop3(aluop[3]), .aop2(aluop[2]), .aop1(aluop[1]), .aop0(aluop[0]));

  // Other names for the same wires on the sheet: op[4:0] = ins[6:2]; rd[4:0] = ins[11:7]; funct3[2:0] = ins[14:12];
  //   break = ins[20]; branch = ins[30]
endmodule
