// Digital circuit branch-PC.dig as structural Verilog
module branch_PC (
  input  [1:0] pcsel,
  input  [31:0] ins_pc,
  input  mret,
  input  clk,
  input  EN,
  input  INT,
  input  bxx,
  input  [31:0] ISR,
  input  [31:0] rs1,
  output [31:0] pc,
  output [31:0] mepc,
  output [1:0] test3
);

  wire d_ff_1_q, d_ff_as_1_nq, or_1_out;
  wire [1:0] add_1_s;
  wire [31:0] multiplexer_1_out, multiplexer_2_out, multiplexer_3_out, multiplexer_4_out, nextpc;
  wire [31:2] add_1_s_2;
  wire [31:12] bitextender_2_out;
  wire [31:13] bitextender_1_out;
  wire [31:21] bitextender_3_out;

  BitExtender #(.inputBits(1), .outputBits(19)) bitextender_1 (.in(ins_pc[31]), .out(bitextender_1_out));
  BitExtender #(.inputBits(1), .outputBits(20)) bitextender_2 (.in(ins_pc[31]), .out(bitextender_2_out));
  BitExtender #(.inputBits(1), .outputBits(11)) bitextender_3 (.in(ins_pc[31]), .out(bitextender_3_out));
  Multiplexer #(.Bits(32)) multiplexer_1 (
    .sel(bxx), .in_0(32'h4),
    .in_1({bitextender_1_out, ins_pc[31], ins_pc[7], ins_pc[30:25], ins_pc[11:8], 1'b0}),
    .out(multiplexer_1_out));
  Multiplexer #(.Selector_Bits(2), .Bits(32)) multiplexer_2 (
    .sel(pcsel), .in_0(pc), .in_1(pc), .in_2(pc), .in_3(rs1), .out(multiplexer_2_out));
  Multiplexer #(.Selector_Bits(2), .Bits(32)) multiplexer_3 (
    .sel(pcsel), .in_0(32'h4), .in_1(multiplexer_1_out),
    .in_2({bitextender_3_out, ins_pc[31], ins_pc[19:12], ins_pc[20], ins_pc[30:21], 1'b0}),
    .in_3({bitextender_2_out, ins_pc[31:20]}), .out(multiplexer_3_out));
  Add #(.Bits(32)) add_1 (
    .a(multiplexer_2_out), .b(multiplexer_3_out), .c_i(1'b0), .s({add_1_s_2, add_1_s}));  // open: c_o
  Multiplexer #(.Bits(32)) multiplexer_4 (.sel(INT), .in_0(nextpc), .in_1(ISR), .out(multiplexer_4_out));
  Multiplexer #(.Bits(32)) multiplexer_5 (.sel(mret), .in_0({add_1_s_2, 2'b00}), .in_1(mepc), .out(nextpc));
  Register #(.Bits(32)) u_pc (.D(multiplexer_4_out), .C(clk), .en(EN), .Q(pc));
  D_FF d_ff_1 (.D(INT), .C(clk), .Q(d_ff_1_q));  // open: nQ
  D_FF_AS d_ff_as_1 (.Set(d_ff_1_q), .D(1'b0), .C(1'b0), .Clr(mret), .nQ(d_ff_as_1_nq));  // open: Q
  or or_1 (or_1_out, mret, d_ff_1_q);
  RegisterFile #(.Bits(32)) BP_stack (
    .Din(nextpc), .we(INT), .Rw(test3), .C(clk), .Ra(test3), .Rb(2'b00), .Da(mepc));  // open: Db
  // Probe on mepc
  CounterPreset #(.Bits(2)) PC_sp (
    .en(or_1_out), .C(~clk), .dir(d_ff_as_1_nq), .in(2'b00), .ld(1'b0), .clr(1'b0), .out(test3));  // open: ovf
  // Probe on test3

  // Other names for the same wires on the sheet: clock = clk; instr[31:0] = ins_pc; pcout[31:0] = pc;
  //   sel[1:0] = pcsel; sp[1:0] = test3

  // Notes on the sheet:
  //   bxx
  //   jal
  //   jalr
endmodule
