// Digital circuit microp-CPU.dig as structural Verilog
module microp_CPU (
  input  clock,
  input  hand,
  input  model,
  input  reset,
  input  key0,
  input  key1,
  input  RX,
  input  [31:0] IN,
  output [31:0] \time ,
  output [31:0] mtcmp,
  output [31:0] OUT,
  output TX,
  output [31:0] int_mesh,
  output [1:0] mesh_addr,
  output [1:0] SP_PC
);

  wire and_1_out, and_2_out, break_q, brk, clk, clk_INT, csrw, EN, \int , memw, mr, mret, mw, or_2_out, regw,
       undriven_3;
  wire [1:0] microp_controller_1_pcsel, undriven;
  wire [2:0] csr_1_meiex, microp_controller_1_wsel;
  wire [3:0] microp_controller_1_aluop, microp_controller_1_alusel;
  wire [4:0] Irom_d_2, Irom_d_3;
  wire [7:0] alu_1_alur_2;
  wire [8:0] branch_pc_1_pc_2;
  wire [11:0] Irom_d_4;
  wire [14:0] Irom_d;
  wire [31:0] alu_1_alur, branch_pc_1_mepc, branch_pc_1_pc, csr_1_csrdata, csr_1_isr, Dram_d, Drom_d,
       multiplexer_2_out, prealu_1_x, prealu_1_y, premw_1_mwdata, prerw_1_rwdata, regs_da, regs_db,
       undriven_2;

  // Probe on {Irom_d_4, Irom_d_3, Irom_d[14:12], Irom_d_2, Irom_d[6:0]}
  branch_PC branch_pc_1 (
    .pcsel(microp_controller_1_pcsel), .ins_pc({Irom_d_4, Irom_d_3, Irom_d[14:12], Irom_d_2, Irom_d[6:0]}),
    .mret(mret), .clk(clk), .EN(EN), .INT(\int ), .bxx(alu_1_alur[0]), .ISR(csr_1_isr), .rs1(regs_da),
    .pc({branch_pc_1_pc[31:11], branch_pc_1_pc_2, branch_pc_1_pc[1:0]}), .mepc(branch_pc_1_mepc),
    .test3(SP_PC));
  microp_controller microp_controller_1 (
    .ins({Irom_d_4, Irom_d_3, Irom_d[14:12], Irom_d_2, Irom_d[6:0]}), .pcsel(microp_controller_1_pcsel),
    .aluop(microp_controller_1_aluop), .alusel(microp_controller_1_alusel), .wsel(microp_controller_1_wsel),
    .rw(regw), .brk(brk), .csrw(csrw), .mw(mw), .mr(mr), .mret(mret));
  // Probe on {branch_pc_1_pc[31:11], branch_pc_1_pc_2, branch_pc_1_pc[1:0]}
  RegisterFile #(.AddrBits(5), .Bits(32)) regs (
    .Din(prerw_1_rwdata), .we(regw), .Rw(Irom_d_2), .C(clk), .Ra(Irom_d_3), .Rb(Irom_d_4[4:0]), .Da(regs_da),
    .Db(regs_db));
  CSR csr_1 (
    .aluR({alu_1_alur[31:10], alu_1_alur_2, alu_1_alur[1:0]}), .csrAddr(Irom_d_4), .mepc(branch_pc_1_mepc),
    .clk(clk_INT), .W_EN(csrw), .EN(EN), .ExInt(undriven_3), .IOdata(undriven_2), .INT_n(undriven),
    .csrData(csr_1_csrdata), .INT(\int ), .ISR(csr_1_isr), .test_1(\time ), .test_2(mtcmp),
    .MEIEx(csr_1_meiex));
  IO io_1 (
    .MEIEx(csr_1_meiex), .aluR({alu_1_alur[31:10], alu_1_alur_2, alu_1_alur[1:0]}), .csrAddr(Irom_d_4),
    .clk(clk_INT), .INT(\int ), .W_EN(csrw), .MRET(mret), .EN(EN), .RX(RX), .ExINT0(key0), .ExINT1(key1),
    .IN0(IN));  // open: IOint, ioData, int_n, OUT, TX, test2, test1
  ROM #(.AddrBits(9), .Bits(32)) Irom (
    .A(branch_pc_1_pc_2), .sel(1'b1), .D({Irom_d_4, Irom_d_3, Irom_d[14:12], Irom_d_2, Irom_d[6:0]}));
  // Probe on {alu_1_alur[31:10], alu_1_alur_2, alu_1_alur[1:0]}
  preALU prealu_1 (
    .alusel(microp_controller_1_alusel),
    .pc_alu({branch_pc_1_pc[31:11], branch_pc_1_pc_2, branch_pc_1_pc[1:0]}),
    .ins_alu({Irom_d_4, Irom_d_3, Irom_d[14:12], Irom_d_2, Irom_d[6:0]}), .rs1(regs_da), .rs2(regs_db),
    .csr(csr_1_csrdata), .x(prealu_1_x), .y(prealu_1_y));
  // Probe on csr_1_csrdata
  preRW prerw_1 (
    .sel(microp_controller_1_wsel), .aluR({alu_1_alur[31:10], alu_1_alur_2, alu_1_alur[1:0]}),
    .csrData(csr_1_csrdata), .ramData(multiplexer_2_out), .rwData(prerw_1_rwdata));
  Multiplexer multiplexer_1 (.sel(model), .in_0(hand), .in_1(clock), .out(clk_INT));
  ALU alu_1 (
    .aluop(microp_controller_1_aluop), .x(prealu_1_x), .y(prealu_1_y),
    .aluR({alu_1_alur[31:10], alu_1_alur_2, alu_1_alur[1:0]}));
  or or_1 (clk, clk_INT, break_q);
  or or_2 (or_2_out, reset, \int );
  preMW premw_1 (.rs2(regs_db), .sel(microp_controller_1_wsel), .mwData(premw_1_mwdata));
  HALT halt_1 (.mw(mw), .mr(mr), .clk(clk), .EN(EN), .memw(memw));
  and and_1 (and_1_out, or_2_out, clk_INT);
  and and_2 (and_2_out, memw, alu_1_alur[10]);
  ROM #(.AddrBits(8), .Bits(32)) Drom (.A(alu_1_alur_2), .sel(1'b1), .D(Drom_d));
  RAMDualPort #(.AddrBits(8), .Bits(32)) Dram (
    .A(alu_1_alur_2), .Din(premw_1_mwdata), .str(and_2_out), .C(clk), .ld(1'b1), .D(Dram_d));
  Multiplexer #(.Bits(32)) multiplexer_2 (.sel(alu_1_alur[10]), .in_0(Drom_d), .in_1(Dram_d), .out(multiplexer_2_out));
  D_FF_AS \break  (.Set(1'b0), .D(brk), .C(clk), .Clr(and_1_out), .Q(break_q));  // open: nQ

  // Other names for the same wires on the sheet: K0 = key0; K1 = key1

  // Notes on the sheet:
  //   clock: Hz: 2
  //   RX: default 1
  //   contents of Irom (hex, n*v repeats v):
  //   4400293,36129073,5400313,36231073,6400393,36339073,3711e073,37216073,3733e073,4e204b7,
  //   33249073,78000e13,4e1e13,304e1073,30045073,10500073,ffdff0ef,33029073,fff2c293,33029073,
  //   200073,33031073,fff34313,33031073,200073,334023f3,33039073,33339073,3320e073,13,13,
  //   3320f073,200073
  //   contents of Drom (hex, n*v repeats v):
  //   0,fffff0b7,400093,40016f,158513,feb50fe3,fff20193,318233,308023,309023,30a023,40a223,
  //   402383,800403,801403,804403,805403,802403,ff3a413,ffe3b413,fff44413,247493,249513,
  //   1f4d593,25d593,40125613,40460633,c616b3,c42733,c43733,864733,e6d7b3,40f75733,d77733,
  //   c76833,200713,11d873,11d873,810f3,710f3,a973,25973,1039f3,10f9f3,e7
endmodule
