// Digital circuit r&w.dig as structural Verilog
module r_w (
  input  OP6,
  input  OP5,
  input  OP4,
  input  OP3,
  input  OP2,
  output mr,
  output mw,
  output csrw,
  output rw
);

  wire and_4_out, and_5_out, and_6_out, and_7_out, not_1_out, not_2_out, not_3_out, not_4_out, not_5_out;

  not not_1 (not_1_out, OP6);
  not not_2 (not_2_out, OP5);
  not not_3 (not_3_out, OP4);
  not not_4 (not_4_out, OP3);
  not not_5 (not_5_out, OP2);
  and and_1 (mr, not_5_out, not_4_out, not_3_out, not_2_out, not_1_out);
  and and_2 (mw, not_5_out, not_4_out, not_3_out, OP5, not_1_out);
  and and_3 (csrw, not_5_out, not_4_out, OP4, OP5, OP6);
  and and_4 (and_4_out, not_5_out, not_4_out, OP4, OP5);
  and and_5 (and_5_out, not_5_out, not_4_out, not_2_out, not_1_out);
  and and_6 (and_6_out, OP2, not_3_out, OP5, OP6);
  and and_7 (and_7_out, not_4_out, OP4, not_1_out);
  or or_1 (rw, and_4_out, and_5_out, and_6_out, and_7_out);
endmodule
