// Digital circuit ALU.dig as structural Verilog
module ALU (
  input  [3:0] aluop,
  input  [31:0] x,
  input  [31:0] y,
  output [31:0] aluR
);

  wire gt__eq__lt_eq, gt__eq__lt_gt, s_gt__eq__lt_gt;
  wire [0:0] beq, bge, bgeu, bne, sltx_blt, sltxu_bltu;
  wire [31:0] addx, andx, orx, sllx, srax, srlx, sub, xorx;

  Add #(.Bits(32)) plus (.a(x), .b(y), .c_i(1'b0), .s(addx));  // open: c_o
  Sub #(.Bits(32)) u_sub (.a(x), .b(y), .c_i(1'b0), .s(sub));  // open: c_o
  BarrelShifter #(.Bits(32)) LeftL (.in(x), .shift(y[5:0]), .out(sllx));
  BarrelShifter #(.Bits(32), .direction("right")) RightL (.in(x), .shift(y[5:0]), .out(srlx));
  BarrelShifter #(.Bits(32), .barrelShifterMode("arithmetic"), .direction("right")) RightA (
    .in(x), .shift(y[5:0]), .out(srax));
  assign andx = x & y;  // And and_1, 32 bits wide
  assign orx = x | y;  // Or or_1, 32 bits wide
  assign xorx = x ^ y;  // XOr xor_1, 32 bits wide
  Comparator #(.Signed("true"), .Bits(32)) s_gt__eq__lt (
    .a(x), .b(y), .gt(s_gt__eq__lt_gt), .eq(beq[0]), .lt(sltx_blt[0]));
  Comparator #(.Bits(32)) gt__eq__lt (.a(x), .b(y), .gt(gt__eq__lt_gt), .eq(gt__eq__lt_eq), .lt(sltxu_bltu[0]));
  or or_2 (bge[0], s_gt__eq__lt_gt, beq[0]);
  or or_3 (bgeu[0], gt__eq__lt_gt, gt__eq__lt_eq);
  not not_1 (bne[0], gt__eq__lt_eq);
  Multiplexer #(.Selector_Bits(4), .Bits(32)) multiplexer_1 (
    .sel(aluop), .in_0(addx), .in_1(sllx), .in_2({{31{1'b0}}, sltx_blt[0]}),
    .in_3({{31{1'b0}}, sltxu_bltu[0]}), .in_4(xorx), .in_5(srlx), .in_6(orx), .in_7(andx), .in_8(sub),
    .in_9(x), .in_10({{31{1'b0}}, bge[0]}), .in_11({{31{1'b0}}, bgeu[0]}), .in_12({{31{1'b0}}, bne[0]}),
    .in_13(srax), .in_14({{31{1'b0}}, beq[0]}), .in_15(y), .out(aluR));

  // Other names for the same wires on the sheet: XIN[31:0] = x; YIN[31:0] = y
endmodule
