// Digital circuit CSR.dig as structural Verilog
module CSR (
  input  [31:0] ins_ID,
  input  [31:0] aluR,
  input  [31:0] mepc,
  input  [11:0] Wa,
  input  clk,
  input  W_EN,
  input  EN,
  input  ExInt,
  input  [31:0] IOdata,
  input  [1:0] INT_n,
  output [31:0] ISR,
  output [31:0] CSR,
  output INT,
  output mret,
  output [31:0] test_1,
  output [31:0] test_2,
  output [2:0] MEIEx
);

  wire and_1_out, and_2_out, and_3_out, and_4_out, and_5_out, and_6_out, and_7_out, and_10_out,
       comparator_1_eq, comparator_2_eq, comparator_3_eq, comparator_4_eq, comparator_5_eq, comparator_6_eq,
       comparator_7_eq, comparator_8_eq, comparator_9_eq, comparator_10_eq, comparator_11_eq,
       comparator_12_eq, comparator_13_eq, comparator_14_eq, comparator_15_eq, MEIE, mepc_eq, MIE, mip_eq,
       nor_1_out, not_1_out, not_2_out, or_1_out, priorityencoder_1_any, register_1_q, T_int, TimeInt_eq;
  wire [2:0] bitextender_1_out, ExINT_EN, priorityencoder_1_num;
  wire [11:7] mip;
  wire [31:0] CSR_RAM_da, CSR_ROM_d, INT_VTR_da, mie_t, mstatus, mtvec, multiplexer_1_out, multiplexer_3_out;

  Comparator #(.Bits(8)) comparator_1 (.a(Wa[11:4]), .b(8'h35), .eq(comparator_1_eq));  // open: gt, lt
  Comparator #(.Bits(4)) comparator_2 (.a(ins_ID[31:28]), .b(4'b0011), .eq(comparator_2_eq));  // open: gt, lt
  Comparator #(.Bits(8)) comparator_3 (.a(ins_ID[27:20]), .b(8'h6), .eq(comparator_3_eq));  // open: gt, lt
  Comparator #(.Bits(8)) comparator_4 (.a(ins_ID[27:20]), .b(8'h5), .eq(comparator_4_eq));  // open: gt, lt
  Comparator #(.Bits(8)) comparator_5 (.a(ins_ID[27:20]), .b(8'h4), .eq(comparator_5_eq));  // open: gt, lt
  Comparator #(.Bits(8)) comparator_6 (.a(ins_ID[27:20]), .b({8{1'b0}}), .eq(comparator_6_eq));  // open: gt, lt
  Comparator #(.Bits(8)) u_mip (.a(ins_ID[27:20]), .b(8'h44), .eq(mip_eq));  // open: gt, lt
  Comparator #(.Bits(8)) u_mepc (.a(ins_ID[27:20]), .b(8'h41), .eq(mepc_eq));  // open: gt, lt
  Comparator #(.Bits(8)) comparator_7 (.a(ins_ID[31:24]), .b(8'h35), .eq(comparator_7_eq));  // open: gt, lt
  Comparator #(.Bits(8)) comparator_8 (.a(ins_ID[31:24]), .b(8'hf1), .eq(comparator_8_eq));  // open: gt, lt
  and and_1 (and_1_out, comparator_1_eq, W_EN);
  Comparator #(.Bits(8)) comparator_9 (.a(Wa[11:4]), .b(8'h36), .eq(comparator_9_eq));  // open: gt, lt
  and and_2 (and_2_out, comparator_9_eq, W_EN);
  RegisterFile #(.AddrBits(4), .Bits(32)) CSR_RAM (
    .Din(aluR), .we(and_1_out), .Rw(Wa[3:0]), .C(clk), .Ra(ins_ID[23:20]), .Rb(ins_ID[23:20]), .Da(CSR_RAM_da));  // open: Db
  PriorityEncoder #(.Selector_Bits(3)) priorityencoder_1 (
    .in0(comparator_3_eq), .in1(comparator_4_eq), .in2(comparator_5_eq), .in3(comparator_6_eq), .in4(mip_eq),
    .in5(mepc_eq), .in6(comparator_7_eq), .in7(comparator_8_eq), .num(priorityencoder_1_num),
    .any(priorityencoder_1_any));
  RegisterFile #(.AddrBits(3), .Bits(32)) INT_VTR (
    .Din(aluR), .we(and_2_out), .Rw(Wa[2:0]), .C(clk), .Ra({1'b0, INT_n}), .Rb({1'b0, INT_n}), .Da(INT_VTR_da));  // open: Db
  ROM #(.AddrBits(4), .Bits(32)) CSR_ROM (.A(ins_ID[23:20]), .sel(1'b1), .D(CSR_ROM_d));
  // Probe on ins_ID[23:20]
  Comparator #(.Bits(4)) comparator_10 (.a(Wa[11:8]), .b(4'b0011), .eq(comparator_10_eq));  // open: gt, lt
  Comparator #(.Bits(8)) comparator_11 (.a(Wa[7:0]), .b(8'h6), .eq(comparator_11_eq));  // open: gt, lt
  Comparator #(.Bits(8)) comparator_12 (.a(Wa[7:0]), .b(8'h5), .eq(comparator_12_eq));  // open: gt, lt
  Comparator #(.Bits(8)) comparator_13 (.a(Wa[7:0]), .b(8'h4), .eq(comparator_13_eq));  // open: gt, lt
  Comparator #(.Bits(8)) comparator_14 (.a(Wa[7:0]), .b({8{1'b0}}), .eq(comparator_14_eq));  // open: gt, lt
  and and_3 (and_3_out, comparator_2_eq, priorityencoder_1_any);
  Multiplexer #(.Selector_Bits(3), .Bits(32)) multiplexer_1 (
    .sel(priorityencoder_1_num), .in_0(test_2), .in_1(ISR),
    .in_2({mie_t[31:15], ExINT_EN, MEIE, mie_t[10:0]}), .in_3({mstatus[31:4], MIE, mstatus[2:0]}),
    .in_4({{20{1'b0}}, mip[11], 3'b000, mip[7], {7{1'b0}}}), .in_5(mepc), .in_6(CSR_RAM_da),
    .in_7(CSR_ROM_d), .out(multiplexer_1_out));
  Multiplexer #(.Bits(32)) multiplexer_2 (.sel(T_int), .in_0(INT_VTR_da), .in_1(mtvec), .out(ISR));
  and and_4 (and_4_out, comparator_10_eq, W_EN, comparator_11_eq);
  and and_5 (and_5_out, comparator_10_eq, W_EN, comparator_12_eq);
  and and_6 (and_6_out, comparator_10_eq, W_EN, comparator_13_eq);
  and and_7 (and_7_out, comparator_10_eq, W_EN, comparator_14_eq);
  // Probe on priorityencoder_1_num
  Comparator #(.Bits(12)) comparator_15 (.a(Wa), .b(ins_ID[31:20]), .eq(comparator_15_eq));  // open: gt, lt
  Multiplexer #(.Bits(32)) multiplexer_3 (
    .sel(and_3_out), .in_0(IOdata), .in_1(multiplexer_1_out), .out(multiplexer_3_out));
  // Probe on multiplexer_1_out
  Multiplexer #(.Bits(32)) multiplexer_4 (.sel(comparator_15_eq), .in_0(multiplexer_3_out), .in_1(aluR), .out(CSR));
  Register #(.Bits(32)) mtimecmp (.D(aluR), .C(clk), .en(and_4_out), .Q(test_2));
  Register #(.Bits(32)) u_mtvec (.D(aluR), .C(clk), .en(and_5_out), .Q(mtvec));
  Register #(.Bits(32)) u_mie (.D(aluR), .C(clk), .en(and_6_out), .Q({mie_t[31:15], ExINT_EN, MEIE, mie_t[10:0]}));
  Register #(.Bits(32)) u_mstatus (.D(aluR), .C(clk), .en(and_7_out), .Q({mstatus[31:4], MIE, mstatus[2:0]}));
  // Probe on test_2
  BitExtender #(.inputBits(1), .outputBits(3)) bitextender_1 (.in(MEIE), .out(bitextender_1_out));
  Register register_1 (.D(INT), .C(clk), .en(EN), .Q(register_1_q));
  assign MEIEx = bitextender_1_out & ExINT_EN;  // And and_8, 3 bits wide
  and and_9 (INT, or_1_out, MIE, not_1_out);
  not not_1 (not_1_out, register_1_q);
  and and_10 (and_10_out, ins_ID[0], ins_ID[1], ins_ID[4], ins_ID[5], ins_ID[6]);
  nor nor_1 (nor_1_out, ins_ID[2], ins_ID[3], ins_ID[12], ins_ID[13], ins_ID[14]);
  CounterPreset #(.Bits(32)) mtime (
    .en(EN), .C(clk), .dir(1'b0), .in({32{1'b0}}), .ld(1'b0), .clr(~mie_t[7]), .out(test_1));  // open: ovf
  Register register_2 (.D(T_int), .C(clk), .en(INT), .Q(mip[7]));
  Register register_3 (.D(ExInt), .C(clk), .en(INT), .Q(mip[11]));
  or or_1 (or_1_out, ExInt, T_int);
  not not_2 (not_2_out, ins_ID[20]);
  // Probe on test_1
  Comparator #(.Bits(32)) TimeInt (.a(test_1), .b(test_2), .eq(TimeInt_eq));  // open: gt, lt
  and and_11 (mret, and_10_out, nor_1_out, not_2_out);
  and and_12 (T_int, TimeInt_eq, mie_t[7]);

  // Other names for the same wires on the sheet: Din[31:0] = aluR; Dout[31:0] = CSR; E_int = ExInt;
  //   ins[31:0] = ins_ID; Raddr[11:0] = ins_ID[31:20]; INTn[1:0] = INT_n; IO_data[31:0] = IOdata; MTIE = mie_t[7];
  //   mie_t[14:11] = {ExINT_EN, MEIE}; mstatus[3] = MIE; mtcmp[31:0] = test_2; Waddr[11:0] = Wa; we = W_EN

  // Notes on the sheet:
  //   CSR_ROM loads instruction_monocycle.hex
endmodule
