// Digital circuit EX-controller.dig as structural Verilog
module EX_controller (
  input  [31:0] ins_EX,
  output regw,
  output [11:0] csraddr,
  output [4:0] RDa,
  output [2:0] rwsel,
  output brk,
  output csrw,
  output mw,
  output [3:0] alusel,
  output [3:0] aluop
);

  wire or_1_out, or_2_out, or_3_out, r_w_1_csrw, r_w_1_mr, r_w_1_rw;
  wire [2:0] and_1_out, and_2_out, bitextender_1_out, bitextender_2_out, not_1_out;

  BitExtender #(.inputBits(1), .outputBits(3)) bitextender_1 (.in(csrw), .out(bitextender_1_out));
  r_w r_w_1 (
    .OP6(ins_EX[6]), .OP5(ins_EX[5]), .OP4(ins_EX[4]), .OP3(ins_EX[3]), .OP2(ins_EX[2]), .mr(r_w_1_mr),
    .mw(mw), .csrw(r_w_1_csrw), .rw(r_w_1_rw));
  assign and_1_out = 3'b100 & bitextender_1_out;  // And and_1, 3 bits wide
  assign not_1_out = ~ins_EX[14:12];  // Not not_1, 3 bits wide
  assign and_2_out = not_1_out & bitextender_2_out;  // And and_2, 3 bits wide
  assign rwsel = ~(and_1_out | and_2_out);  // NOr nor_1, 3 bits wide
  or or_1 (or_1_out, r_w_1_mr, mw);
  or or_2 (or_2_out, ins_EX[12], ins_EX[13], ins_EX[14]);
  or or_3 (or_3_out, ins_EX[7], ins_EX[8], ins_EX[9], ins_EX[10], ins_EX[11]);
  BitExtender #(.inputBits(1), .outputBits(3)) bitextender_2 (.in(or_1_out), .out(bitextender_2_out));
  and and_3 (regw, r_w_1_rw, or_3_out);
  and and_4 (csrw, r_w_1_csrw, or_2_out);
  and and_5 (brk, ~or_2_out, r_w_1_csrw, ins_EX[20]);  // And
  alusel alusel_1 (
    .op6(ins_EX[6]), .op5(ins_EX[5]), .op4(ins_EX[4]), .op3(ins_EX[3]), .op2(ins_EX[2]), .F2(ins_EX[14]),
    .F1(ins_EX[13]), .F0(ins_EX[12]), .asel3(alusel[3]), .asel2(alusel[2]), .asel1(alusel[1]),
    .asel0(alusel[0]));
  aluop aluop_1 (
    .op6(ins_EX[6]), .op5(ins_EX[5]), .op4(ins_EX[4]), .op3(ins_EX[3]), .op2(ins_EX[2]), .F2(ins_EX[14]),
    .F1(ins_EX[13]), .F0(ins_EX[12]), .b(ins_EX[30]), .aop3(aluop[3]), .aop2(aluop[2]), .aop1(aluop[1]),
    .aop0(aluop[0]));

  assign csraddr = ins_EX[31:20];
  assign RDa = ins_EX[11:7];

  // Other names for the same wires on the sheet: op[4:0] = ins_EX[6:2]; rd_addr[4:0] = ins_EX[11:7];
  //   funct3[2:0] = ins_EX[14:12]; break = ins_EX[20]; csr_addr[11:0] = ins_EX[31:20]; branch = ins_EX[30]
endmodule
