// Digital circuit HALT.dig as structural Verilog
module HALT (
  input  clk,
  input  mw_EX,
  input  [31:0] ins_ID,
  output EN,
  output memw
);

  wire and_1_out, and_2_out, d_ff_as_1_nq, delay1_nq, delay1_q, delay2_nq, lx_eq, not_1_out, or_1_out, sx_eq;

  Comparator #(.Bits(5)) sx (.a(ins_ID[6:2]), .b(5'b01000), .eq(sx_eq));  // open: gt, lt
  Comparator #(.Bits(5)) lx (.a(ins_ID[6:2]), .b({5{1'b0}}), .eq(lx_eq));  // open: gt, lt
  or or_1 (or_1_out, sx_eq, lx_eq);
  and and_1 (and_1_out, and_2_out, mw_EX);
  not not_1 (not_1_out, clk);
  D_FF_AS d_ff_as_1 (.Set(1'b0), .D(or_1_out), .C(not_1_out), .Clr(1'b0), .nQ(d_ff_as_1_nq));  // open: Q
  D_FF_AS delay1 (.Set(1'b0), .D(and_1_out), .C(not_1_out), .Clr(1'b0), .Q(delay1_q), .nQ(delay1_nq));
  D_FF_AS delay2 (.Set(1'b0), .D(delay1_q), .C(not_1_out), .Clr(1'b0), .nQ(delay2_nq));  // open: Q
  or or_2 (EN, d_ff_as_1_nq, and_2_out);
  and and_2 (and_2_out, delay1_nq, delay2_nq);
  and and_3 (memw, and_2_out, mw_EX);
  // Probe D on and_2_out

  // Other names for the same wires on the sheet: clock = clk; op[4:0] = ins_ID[6:2]
endmodule
