// Digital circuit ID-controller.dig as structural Verilog
module ID_controller (
  input  [31:0] ins_ctl,
  output mw,
  output \break ,
  output [2:0] memwsel
);

  wire comparator_1_eq, csrx_eq;

  Comparator #(.Bits(5)) csrx (.a(ins_ctl[6:2]), .b(5'b11100), .eq(csrx_eq));  // open: gt, lt
  Comparator #(.Bits(5)) sx (.a(ins_ctl[6:2]), .b(5'b01000), .eq(mw));  // open: gt, lt
  Comparator #(.Bits(3)) comparator_1 (.a(ins_ctl[14:12]), .b(3'b000), .eq(comparator_1_eq));  // open: gt, lt
  and and_1 (\break , comparator_1_eq, ins_ctl[20], csrx_eq);

  assign memwsel = ins_ctl[14:12];

  // Other names for the same wires on the sheet: op[4:0] = ins_ctl[6:2]; funct3[2:0] = ins_ctl[14:12];
  //   break_t = ins_ctl[20]
endmodule
