// Digital circuit IO.dig as structural Verilog
module IO (
  input  [2:0] MEIEx,
  input  [31:0] aluR,
  input  [11:0] Raddr,
  input  [11:0] Waddr,
  input  clk,
  input  INT,
  input  W_EN,
  input  EN,
  input  MRET,
  input  RX,
  input  ExINT0,
  input  ExINT1,
  input  [31:0] IN0,
  output IOint,
  output [31:0] ioData,
  output [1:0] int_n,
  output TX,
  output [31:0] OUT,
  output [31:0] test1,
  output [1:0] test2
);

  wire and_1_out, and_2_out, and_3_out, and_4_out, and_5_out, and_6_out, and_7_out, and_8_out, and_9_out,
       and_10_out, comparator_1_eq, comparator_2_eq, comparator_3_eq, comparator_4_eq, comparator_5_eq,
       comparator_6_eq, comparator_7_eq, comparator_8_eq, comparator_9_eq, comparator_10_eq,
       comparator_11_eq, comparator_12_eq, comparator_13_eq, d_ff_as_1_nq, d_ff_as_2_q, d_ff_as_3_q,
       d_ff_as_4_q, int0, int0_CLR, int1, int1_CLR, int2, int2_CLR, mesh0, mesh1, mesh2, or_1_out, or_2_out,
       or_3_out, or_4_out, register_2_q, register_3_q, register_4_q, register_5_q, register_6_q,
       register_7_q, RXvld, TXvld;
  wire [1:0] iostatus, mesh_stack_da, sp_mesh;
  wire [2:0] priorityencoder_1_num;
  wire [7:0] RXdata, TXdata;
  wire [15:0] TXrate;
  wire [15:1] uConfig;
  wire [31:0] multiplexer_1_out;
  wire [31:3] not_1_out;
  wire [31:8] uTX;

  uart uart_1 (
    .CLK(clk), .TX_vld(TXvld), .TX_data(TXdata), .RATE(TXrate), .RX(RX));  // open: RX_data, RX_rdy, TX_rdy, RX_vld, TX
  RegisterFile #(.Bits(2)) mesh_stack (
    .Din(int_n), .we(INT), .Rw(sp_mesh), .C(clk), .Ra(sp_mesh), .Rb(2'b00), .Da(mesh_stack_da));  // open: Db
  Comparator #(.Bits(4)) comparator_1 (.a(Raddr[11:8]), .b(4'b0011), .eq(comparator_1_eq));  // open: gt, lt
  Comparator #(.Bits(8)) comparator_2 (.a(Raddr[7:0]), .b(8'h30), .eq(comparator_2_eq));  // open: gt, lt
  Comparator #(.Bits(8)) comparator_3 (.a(Raddr[7:0]), .b(8'h31), .eq(comparator_3_eq));  // open: gt, lt
  Comparator #(.Bits(8)) comparator_4 (.a(Raddr[7:0]), .b(8'h32), .eq(comparator_4_eq));  // open: gt, lt
  Comparator #(.Bits(8)) comparator_5 (.a(Raddr[7:0]), .b(8'h33), .eq(comparator_5_eq));  // open: gt, lt
  Comparator #(.Bits(8)) comparator_6 (.a(Raddr[7:0]), .b(8'h34), .eq(comparator_6_eq));  // open: gt, lt
  Comparator #(.Bits(8)) comparator_7 (.a(Raddr[7:0]), .b(8'h3f), .eq(comparator_7_eq));  // open: gt, lt
  Register #(.Bits(2)) register_1 (.D(mesh_stack_da), .C(clk), .en(EN), .Q(test2));
  and and_1 (and_1_out, comparator_1_eq, comparator_2_eq);
  and and_2 (and_2_out, comparator_1_eq, comparator_3_eq);
  and and_3 (and_3_out, comparator_1_eq, comparator_4_eq);
  and and_4 (and_4_out, comparator_1_eq, comparator_5_eq);
  and and_5 (and_5_out, comparator_1_eq, comparator_6_eq);
  and and_6 (and_6_out, comparator_1_eq, comparator_7_eq);
  // Probe on test2
  Comparator #(.Bits(8)) comparator_8 (.a(Waddr[11:4]), .b(8'h37), .eq(comparator_8_eq));  // open: gt, lt
  and and_7 (and_7_out, comparator_8_eq, W_EN);
  Comparator #(.Bits(4)) comparator_9 (.a(Waddr[11:8]), .b(4'b0011), .eq(comparator_9_eq));  // open: gt, lt
  Comparator #(.Bits(8)) comparator_10 (.a(Waddr[7:0]), .b(8'h30), .eq(comparator_10_eq));  // open: gt, lt
  Comparator #(.Bits(8)) comparator_11 (.a(Waddr[7:0]), .b(8'h32), .eq(comparator_11_eq));  // open: gt, lt
  Comparator #(.Bits(8)) comparator_12 (.a(Waddr[7:0]), .b(8'h33), .eq(comparator_12_eq));  // open: gt, lt
  PriorityEncoder #(.Selector_Bits(3)) priorityencoder_1 (
    .in0(1'b0), .in1(and_1_out), .in2(and_2_out), .in3(and_3_out), .in4(and_4_out), .in5(and_5_out),
    .in6(and_6_out), .in7(1'b0), .num(priorityencoder_1_num));  // open: any
  Demultiplexer #(.Selector_Bits(2)) demultiplexer_1 (
    .sel(int_n), .in(INT), .out_1(int0_CLR), .out_2(int1_CLR), .out_3(int2_CLR));  // open: out_0
  RegisterFile #(.AddrBits(3), .Bits(32)) INT_mesh (
    .Din(aluR), .we(and_7_out), .Rw(Waddr[2:0]), .C(clk), .Ra({1'b0, test2}), .Rb({1'b0, test2}), .Da(test1));  // open: Db
  and and_8 (and_8_out, comparator_9_eq, comparator_10_eq, W_EN);
  and and_9 (and_9_out, comparator_9_eq, comparator_11_eq, W_EN);
  and and_10 (and_10_out, comparator_9_eq, comparator_12_eq, W_EN);
  Register #(.Bits(32)) u_out (.D(aluR), .C(clk), .en(and_8_out), .Q(OUT));
  Register #(.Bits(32)) u_uConfig (.D(aluR), .C(clk), .en(and_9_out), .Q({TXrate, uConfig, TXvld}));
  Register #(.Bits(32)) uTXdata (.D(aluR), .C(clk), .en(and_10_out), .Q({uTX, TXdata}));
  // Probe on priorityencoder_1_num
  Multiplexer #(.Selector_Bits(3), .Bits(32)) multiplexer_1 (
    .sel(priorityencoder_1_num), .in_0({32{1'b0}}), .in_1(OUT), .in_2({{30{1'b0}}, iostatus}),
    .in_3({TXrate, uConfig, TXvld}), .in_4({uTX, TXdata}), .in_5({{24{1'b0}}, RXdata}), .in_6(IN0),
    .in_7({32{1'b0}}), .out(multiplexer_1_out));
  assign {not_1_out, mesh2, mesh1, mesh0} = ~test1;  // Not not_1, 32 bits wide
  // Probe on test1
  // Probe on OUT
  // Probe on multiplexer_1_out
  Multiplexer #(.Bits(32)) multiplexer_2 (.sel(comparator_13_eq), .in_0(multiplexer_1_out), .in_1(aluR), .out(ioData));
  Comparator #(.Bits(12)) comparator_13 (.a(Waddr), .b(Raddr), .eq(comparator_13_eq));  // open: gt, lt
  D_FF_AS d_ff_as_1 (.Set(INT), .D(1'b0), .C(1'b0), .Clr(MRET), .nQ(d_ff_as_1_nq));  // open: Q
  PriorityEncoder #(.Selector_Bits(2)) priorityencoder_2 (
    .in0(1'b0), .in1(int0), .in2(int1), .in3(int2), .num(int_n));  // open: any
  D_FF_AS d_ff_as_2 (.Set(1'b0), .D(1'b1), .C(ExINT0), .Clr(register_5_q), .Q(d_ff_as_2_q));  // open: nQ
  D_FF_AS d_ff_as_3 (.Set(1'b0), .D(1'b1), .C(ExINT1), .Clr(register_6_q), .Q(d_ff_as_3_q));  // open: nQ
  D_FF_AS d_ff_as_4 (.Set(1'b0), .D(1'b1), .C(RXvld), .Clr(register_7_q), .Q(d_ff_as_4_q));  // open: nQ
  or or_1 (or_1_out, MRET, INT);
  or or_2 (or_2_out, ~MEIEx[0], int0_CLR);  // Or
  or or_3 (or_3_out, ~MEIEx[1], int1_CLR);  // Or
  or or_4 (or_4_out, ~MEIEx[2], int2_CLR);  // Or
  CounterPreset #(.Bits(2)) mesh_sp (
    .en(or_1_out), .C(~clk), .dir(d_ff_as_1_nq), .in(2'b00), .ld(1'b0), .clr(1'b0), .out(sp_mesh));  // open: ovf
  or or_5 (IOint, int0, int1, int2);
  Register register_2 (.D(d_ff_as_2_q), .C(clk), .en(EN), .Q(register_2_q));
  Register register_3 (.D(d_ff_as_3_q), .C(clk), .en(EN), .Q(register_3_q));
  Register register_4 (.D(d_ff_as_4_q), .C(clk), .en(EN), .Q(register_4_q));
  // Probe on sp_mesh
  and and_11 (int0, register_2_q, mesh0);
  Register register_5 (.D(or_2_out), .C(~clk), .en(EN), .Q(register_5_q));
  and and_12 (int1, register_3_q, mesh1);
  Register register_6 (.D(or_3_out), .C(~clk), .en(EN), .Q(register_6_q));
  and and_13 (int2, register_4_q, mesh2);
  Register register_7 (.D(or_4_out), .C(~clk), .en(EN), .Q(register_7_q));

  // Other names for the same wires on the sheet: Din[31:0] = aluR; Dout[31:0] = ioData; IN_0[31:0] = IN0;
  //   INTn[1:0] = int_n; ExI0_EN = MEIEx[0]; ExI1_EN = MEIEx[1]; uart_EN = MEIEx[2]; mesh_addr[1:0] = test2;
  //   out0[31:0] = OUT; RXrdy = iostatus[1]; TXrdy = iostatus[0]; uConfig (some bits) = {TXrate, TXvld};
  //   uTX[7:0] = TXdata; we = W_EN
endmodule
