// Digital circuit branch-pre-2stage.dig as structural Verilog
module branch_pre_2stage (
  input  [31:0] ins_ID,
  input  clk,
  input  EN,
  input  [31:0] rs1,
  input  REGw,
  input  [4:0] RDaddr,
  input  jump_EX,
  input  mret,
  input  INT,
  input  [31:0] PCjump,
  input  [31:0] ISR,
  output Flag_jump,
  output [31:0] pc_ID,
  output [31:0] mepc,
  output [1:0] test3
);

  wire and_2_out, bxx_eq, d_ff_1_q, d_ff_as_1_nq, int_sel, jal_eq, jalr_eq, or_2_out, rediect_eq,
       register_1_q;
  wire [1:0] add_1_s, sel;
  wire [10:0] bitextender_3_out;
  wire [18:0] bitextender_2_out;
  wire [19:0] bitextender_1_out;
  wire [31:0] multiplexer_1_out, multiplexer_2_out, multiplexer_3_out, multiplexer_4_out, multiplexer_5_out,
       nextpc;
  wire [31:2] add_1_s_2;

  BitExtender #(.inputBits(1), .outputBits(20)) bitextender_1 (.in(ins_ID[31]), .out(bitextender_1_out));
  BitExtender #(.inputBits(1), .outputBits(19)) bitextender_2 (.in(ins_ID[31]), .out(bitextender_2_out));
  Comparator #(.Bits(5)) bxx (.a(ins_ID[6:2]), .b(5'b11000), .eq(bxx_eq));  // open: gt, lt
  Comparator #(.Bits(5)) jal (.a(ins_ID[6:2]), .b(5'b11011), .eq(jal_eq));  // open: gt, lt
  Comparator #(.Bits(5)) jalr (.a(ins_ID[6:2]), .b(5'b11001), .eq(jalr_eq));  // open: gt, lt
  BitExtender #(.inputBits(1), .outputBits(11)) bitextender_3 (.in(ins_ID[31]), .out(bitextender_3_out));
  Multiplexer #(.Bits(32)) multiplexer_1 (
    .sel(ins_ID[31]), .in_0(32'h4),
    .in_1({bitextender_2_out, ins_ID[31], ins_ID[7], ins_ID[30:25], ins_ID[11:8], 1'b0}),
    .out(multiplexer_1_out));
  PriorityEncoder #(.Selector_Bits(2)) PCsel (
    .in0(1'b0), .in1(bxx_eq), .in2(jal_eq), .in3(jalr_eq), .num(sel));  // open: any
  Multiplexer #(.Selector_Bits(2), .Bits(32)) multiplexer_2 (
    .sel(sel), .in_0(pc_ID), .in_1(pc_ID), .in_2(pc_ID), .in_3(rs1), .out(multiplexer_2_out));
  Multiplexer #(.Selector_Bits(2), .Bits(32)) multiplexer_3 (
    .sel(sel), .in_0(32'h4), .in_1(multiplexer_1_out),
    .in_2({bitextender_3_out, ins_ID[31], ins_ID[19:12], ins_ID[20], ins_ID[30:21], 1'b0}),
    .in_3({bitextender_1_out, ins_ID[31:20]}), .out(multiplexer_3_out));
  Comparator #(.Bits(5)) rediect (.a(ins_ID[19:15]), .b(RDaddr), .eq(rediect_eq));  // open: gt, lt
  Add #(.Bits(32)) add_1 (
    .a(multiplexer_2_out), .b(multiplexer_3_out), .c_i(1'b0), .s({add_1_s_2, add_1_s}));  // open: c_o
  Multiplexer #(.Bits(32)) multiplexer_4 (.sel(int_sel), .in_0(nextpc), .in_1(ISR), .out(multiplexer_4_out));
  Multiplexer #(.Bits(32)) multiplexer_5 (
    .sel(jump_EX), .in_0({add_1_s_2, 2'b00}), .in_1(PCjump), .out(multiplexer_5_out));
  Multiplexer #(.Bits(32)) multiplexer_6 (.sel(mret), .in_0(multiplexer_5_out), .in_1(mepc), .out(nextpc));
  and and_1 (Flag_jump, REGw, rediect_eq);
  Register #(.Bits(32)) pc (.D(multiplexer_4_out), .C(clk), .en(EN), .Q(pc_ID));
  Register register_1 (.D(INT), .C(clk), .en(EN), .Q(register_1_q));
  and and_2 (and_2_out, register_1_q, jump_EX);
  or or_1 (int_sel, INT, and_2_out);
  D_FF d_ff_1 (.D(int_sel), .C(clk), .Q(d_ff_1_q));  // open: nQ
  D_FF_AS d_ff_as_1 (.Set(d_ff_1_q), .D(1'b0), .C(1'b0), .Clr(mret), .nQ(d_ff_as_1_nq));  // open: Q
  RegisterFile #(.Bits(32)) BP_stack (
    .Din(nextpc), .we(int_sel), .Rw(test3), .C(clk), .Ra(test3), .Rb(2'b00), .Da(mepc));  // open: Db
  or or_2 (or_2_out, mret, d_ff_1_q);
  // Probe on mepc
  CounterPreset #(.Bits(2)) counterpreset_1 (
    .en(or_2_out), .C(~clk), .dir(d_ff_as_1_nq), .in(2'b00), .ld(1'b0), .clr(1'b0), .out(test3));  // open: ovf
  // Probe on test3

  // Other names for the same wires on the sheet: clock = clk; instr[31:0] = ins_ID; J_EX = jump_EX;
  //   pc_EX[31:0] = PCjump; pcout[31:0] = pc_ID; sp[1:0] = test3

  // Notes on the sheet:
  //   bxx
  //   jal
  //   jalr
  //   rs1addr
endmodule
