// Digital circuit branch-pre.dig as structural Verilog
module branch_pre (
  input  [31:0] ins_IF,
  input  jump_ID,
  input  [31:0] PC_ID,
  input  jump_EX,
  input  [31:0] PC_EX,
  input  clk,
  input  EN,
  input  mret,
  input  INT,
  input  [31:0] ISR,
  output [31:0] PC_IF,
  output [31:0] mepc,
  output [1:0] test3
);

  wire and_1_out, and_2_out, bxx_eq, d_ff_1_q, d_ff_as_1_nq, int_sel, jal_eq, jump_any, or_1_out, or_3_out,
       register_1_q, register_2_q, sel;
  wire [31:0] add_1_s, multiplexer_1_out, multiplexer_2_out, multiplexer_3_out, multiplexer_4_out,
       multiplexer_5_out, multiplexer_6_out, nextpc;
  wire [31:13] bitextender_1_out;
  wire [31:21] bitextender_2_out;

  Comparator #(.Bits(5)) bxx (.a(ins_IF[6:2]), .b(5'b11000), .eq(bxx_eq));  // open: gt, lt
  Comparator #(.Bits(5)) jal (.a(ins_IF[6:2]), .b(5'b11011), .eq(jal_eq));  // open: gt, lt
  BitExtender #(.inputBits(1), .outputBits(19)) bitextender_1 (.in(ins_IF[31]), .out(bitextender_1_out));
  Register register_1 (.D(INT), .C(clk), .en(EN), .Q(register_1_q));
  or or_1 (or_1_out, jump_ID, jump_EX);
  PriorityEncoder jump (.in0(bxx_eq), .in1(jal_eq), .num(sel), .any(jump_any));
  BitExtender #(.inputBits(1), .outputBits(11)) bitextender_2 (.in(ins_IF[31]), .out(bitextender_2_out));
  Multiplexer #(.Bits(32)) multiplexer_1 (
    .sel(ins_IF[31]), .in_0(32'h4),
    .in_1({bitextender_1_out, ins_IF[31], ins_IF[7], ins_IF[30:25], ins_IF[11:8], 1'b0}),
    .out(multiplexer_1_out));
  and and_1 (and_1_out, register_1_q, or_1_out);
  Multiplexer #(.Bits(32)) multiplexer_2 (
    .sel(sel), .in_0(multiplexer_1_out),
    .in_1({bitextender_2_out, ins_IF[31], ins_IF[19:12], ins_IF[20], ins_IF[30:21], 1'b0}),
    .out(multiplexer_2_out));
  Register register_2 (.D(and_1_out), .C(clk), .en(EN), .Q(register_2_q));
  Add #(.Bits(32)) add_1 (.a(PC_IF), .b(multiplexer_3_out), .c_i(1'b0), .s(add_1_s));  // open: c_o
  Multiplexer #(.Bits(32)) multiplexer_3 (
    .sel(jump_any), .in_0(32'h4), .in_1(multiplexer_2_out), .out(multiplexer_3_out));
  and and_2 (and_2_out, register_2_q, jump_EX);
  or or_2 (int_sel, INT, and_1_out, and_2_out);
  Multiplexer #(.Bits(32)) multiplexer_4 (
    .sel(jump_ID), .in_0({add_1_s[31:2], 2'b00}), .in_1(PC_ID), .out(multiplexer_4_out));
  Multiplexer #(.Bits(32)) multiplexer_5 (.sel(int_sel), .in_0(nextpc), .in_1(ISR), .out(multiplexer_5_out));
  Multiplexer #(.Bits(32)) multiplexer_6 (
    .sel(jump_EX), .in_0(multiplexer_4_out), .in_1(PC_EX), .out(multiplexer_6_out));
  Multiplexer #(.Bits(32)) multiplexer_7 (.sel(mret), .in_0(multiplexer_6_out), .in_1(mepc), .out(nextpc));
  Register #(.Bits(32)) pc (.D(multiplexer_5_out), .C(clk), .en(EN), .Q(PC_IF));
  D_FF d_ff_1 (.D(int_sel), .C(clk), .Q(d_ff_1_q));  // open: nQ
  D_FF_AS d_ff_as_1 (.Set(d_ff_1_q), .D(1'b0), .C(1'b0), .Clr(mret), .nQ(d_ff_as_1_nq));  // open: Q
  RegisterFile #(.Bits(32)) BP_stack (
    .Din(nextpc), .we(int_sel), .Rw(test3), .C(clk), .Ra(test3), .Rb(2'b00), .Da(mepc));  // open: Db
  or or_3 (or_3_out, mret, d_ff_1_q);
  CounterPreset #(.Bits(2)) counterpreset_1 (
    .en(or_3_out), .C(~clk), .dir(d_ff_as_1_nq), .in(2'b00), .ld(1'b0), .clr(1'b0), .out(test3));  // open: ovf
  // Probe on mepc
  // Probe on test3

  // Other names for the same wires on the sheet: clock = clk; instr[31:0] = ins_IF; J_EX = jump_EX; J_ID = jump_ID;
  //   pcout[31:0] = PC_IF; sp[1:0] = test3

  // Notes on the sheet:
  //   bxx
  //   jal
endmodule
