// Digital circuit pipe-CPU.dig as structural Verilog
module pipe_CPU (
  input  clock,
  input  hand,
  input  model,
  input  reset,
  input  key0,
  input  key1,
  input  RX,
  input  [31:0] IN,
  output [31:0] \time ,
  output [31:0] mtcmp,
  output [31:0] OUT,
  output TX,
  output [31:0] int_mesh,
  output [1:0] mesh_addr,
  output [1:0] SP_PC
);

  wire and_1_out, and_2_out, and_3_out, break_q, brk, bxx, clk, clk_INT, CSRw, EN, Flag_EX, Flag_ID, \int ,
       J_EX, J_ID, mret, mw, Mw_EX, not_1_out, or_1_out, or_2_out, Rw, undriven_3;
  wire [1:0] undriven;
  wire [2:0] csr_1_meiex, wsel;
  wire [3:0] ex_controller_1_aluop, ex_controller_1_alusel;
  wire [4:0] if_id_1_ins_id_2, if_id_1_ins_id_3, RDa;
  wire [7:0] id_ex_1_addr_ex_2;
  wire [8:0] branch_pre_1_pc_if_2;
  wire [11:0] CSRa;
  wire [11:5] if_id_1_ins_id_4;
  wire [14:0] if_id_1_ins_id;
  wire [31:0] branch_pre_1_mepc, branch_pre_1_pc_if, csr_1_csr, csr_1_isr, Dram_d, Drom_d, id_ex_1_addr_ex,
       id_ex_1_csr_ex, id_ex_1_ins_ex, id_ex_1_mem_ex, id_ex_1_pc_ex, id_ex_1_rs1_ex, id_ex_1_rs2_ex,
       if_id_1_pc_id, Irom_d, jalr_1_pc_jump, judge_branch_1_pc_jump, multiplexer_2_out, prealu_1_x,
       prealu_1_y, premw_1_maddr, premw_1_mdata, prerw_1_rwdata, RS1, RS1_ID, RS2, RS2_ID, undriven_2;
  wire [31:1] alu_1_alur;

  // Probe on judge_branch_1_pc_jump
  // Probe on jalr_1_pc_jump
  branch_pre branch_pre_1 (
    .ins_IF(Irom_d), .jump_ID(J_ID), .PC_ID(jalr_1_pc_jump), .jump_EX(J_EX), .PC_EX(judge_branch_1_pc_jump),
    .clk(clk), .EN(EN), .mret(mret), .INT(\int ), .ISR(csr_1_isr),
    .PC_IF({branch_pre_1_pc_if[31:11], branch_pre_1_pc_if_2, branch_pre_1_pc_if[1:0]}),
    .mepc(branch_pre_1_mepc), .test3(SP_PC));
  // Probe on {branch_pre_1_pc_if[31:11], branch_pre_1_pc_if_2, branch_pre_1_pc_if[1:0]}
  or or_1 (or_1_out, \int , reset);
  ROM #(.AddrBits(9), .Bits(32)) Irom (.A(branch_pre_1_pc_if_2), .sel(1'b1), .D(Irom_d));
  and and_1 (and_1_out, Irom_d[0], Irom_d[1]);
  or or_2 (or_2_out, ~and_1_out, mret, J_ID, J_EX);  // Or
  Multiplexer multiplexer_1 (.sel(model), .in_0(hand), .in_1(clock), .out(clk_INT));
  and and_2 (and_2_out, clk_INT, or_1_out);
  // Probe on Irom_d
  or or_3 (clk, clk_INT, break_q);
  IF_ID if_id_1 (
    .clk(clk), .PC_IF({branch_pre_1_pc_if[31:11], branch_pre_1_pc_if_2, branch_pre_1_pc_if[1:0]}),
    .ins_IF(Irom_d), .clr(or_2_out), .EN(EN),
    .ins_ID({if_id_1_ins_id_4, if_id_1_ins_id_3, if_id_1_ins_id_2, if_id_1_ins_id}), .PC_ID(if_id_1_pc_id));
  D_FF_AS \break  (.Set(1'b0), .D(brk), .C(clk), .Clr(and_2_out), .Q(break_q));  // open: nQ
  // Probe on {if_id_1_ins_id_4, if_id_1_ins_id_3, if_id_1_ins_id_2, if_id_1_ins_id}
  // Probe on prerw_1_rwdata
  // Probe on if_id_1_pc_id
  JALR jalr_1 (
    .ins_EX(id_ex_1_ins_ex), .REGw(Rw), .rs1_ID(RS1_ID),
    .ins_ID({if_id_1_ins_id_4, if_id_1_ins_id_3, if_id_1_ins_id_2, if_id_1_ins_id}), .jump_ID(J_ID),
    .PC_jump(jalr_1_pc_jump), .Flag_jump(Flag_ID));
  RegisterFile #(.AddrBits(5), .Bits(32)) regs (
    .Din(prerw_1_rwdata), .we(Rw), .Rw(RDa), .C(clk), .Ra(if_id_1_ins_id_2), .Rb(if_id_1_ins_id_3),
    .Da(RS1_ID), .Db(RS2_ID));
  CSR csr_1 (
    .ins_ID({if_id_1_ins_id_4, if_id_1_ins_id_3, if_id_1_ins_id_2, if_id_1_ins_id}),
    .aluR({alu_1_alur, bxx}), .mepc(branch_pre_1_mepc), .Wa(CSRa), .clk(clk_INT), .W_EN(CSRw), .EN(EN),
    .ExInt(undriven_3), .IOdata(undriven_2), .INT_n(undriven), .ISR(csr_1_isr), .CSR(csr_1_csr), .INT(\int ),
    .mret(mret), .test_1(\time ), .test_2(mtcmp), .MEIEx(csr_1_meiex));
  IO io_1 (
    .MEIEx(csr_1_meiex), .aluR({alu_1_alur, bxx}), .Raddr({if_id_1_ins_id_4, if_id_1_ins_id_3}),
    .Waddr(CSRa), .clk(clk_INT), .INT(\int ), .W_EN(CSRw), .EN(EN), .MRET(mret), .RX(RX), .ExINT0(key0),
    .ExINT1(key1), .IN0(IN));  // open: IOint, ioData, int_n, TX, OUT, test1, test2
  judge_branch judge_branch_1 (
    .PC(id_ex_1_pc_ex), .ins_EX(id_ex_1_ins_ex), .bxx(bxx), .Flag(Flag_EX), .rs1(id_ex_1_rs1_ex),
    .PC_jump(judge_branch_1_pc_jump), .jump_EX(J_EX));
  ID_EX id_ex_1 (
    .clr(J_EX), .PC_ID(if_id_1_pc_id),
    .ins_ID({if_id_1_ins_id_4, if_id_1_ins_id_3, if_id_1_ins_id_2, if_id_1_ins_id}), .clk(clk), .EN(EN),
    .RS1_ID(RS1), .RS2_ID(RS2), .Flag_ID(Flag_ID), .CSR_ID(csr_1_csr), .MEM_ID(premw_1_mdata),
    .Addr_ID(premw_1_maddr), .PC_EX(id_ex_1_pc_ex), .ins_EX(id_ex_1_ins_ex), .RS1_EX(id_ex_1_rs1_ex),
    .RS2_EX(id_ex_1_rs2_ex), .CSR_EX(id_ex_1_csr_ex), .MEM_EX(id_ex_1_mem_ex),
    .Addr_EX({id_ex_1_addr_ex[31:10], id_ex_1_addr_ex_2, id_ex_1_addr_ex[1:0]}), .Flag_EX(Flag_EX));
  preMW premw_1 (
    .ins_ID({if_id_1_ins_id_4, if_id_1_ins_id_3, if_id_1_ins_id_2, if_id_1_ins_id}), .rs1(RS1), .rs2(RS2),
    .mData(premw_1_mdata), .mAddr(premw_1_maddr));
  // Probe on {if_id_1_ins_id_4, if_id_1_ins_id_3, if_id_1_ins_id_2, if_id_1_ins_id}
  redirect redirect_1 (
    .ins_ID({if_id_1_ins_id_4, if_id_1_ins_id_3, if_id_1_ins_id_2, if_id_1_ins_id}), .rs1_ID(RS1_ID),
    .rs2_ID(RS2_ID), .regw(Rw), .rd_addr(RDa), .rd_EX(prerw_1_rwdata), .RS1(RS1), .RS2(RS2));
  // Probe on id_ex_1_ins_ex
  // Probe on id_ex_1_rs1_ex
  // Probe on id_ex_1_mem_ex
  HALT halt_1 (
    .clk(clk), .mw_EX(Mw_EX),
    .ins_ID({if_id_1_ins_id_4, if_id_1_ins_id_3, if_id_1_ins_id_2, if_id_1_ins_id}), .EN(EN), .memw(mw));
  EX_controller ex_controller_1 (
    .ins_EX(id_ex_1_ins_ex), .regw(Rw), .csraddr(CSRa), .RDa(RDa), .rwsel(wsel), .brk(brk), .csrw(CSRw),
    .mw(Mw_EX), .alusel(ex_controller_1_alusel), .aluop(ex_controller_1_aluop));
  // Probe on id_ex_1_pc_ex
  preALU prealu_1 (
    .alusel(ex_controller_1_alusel), .pc_alu(id_ex_1_pc_ex), .ins_alu(id_ex_1_ins_ex), .rs1(id_ex_1_rs1_ex),
    .rs2(id_ex_1_rs2_ex), .csr(id_ex_1_csr_ex), .x(prealu_1_x), .y(prealu_1_y));
  // Probe on {id_ex_1_addr_ex[31:10], id_ex_1_addr_ex_2, id_ex_1_addr_ex[1:0]}
  not not_1 (not_1_out, clk);
  // Probe on id_ex_1_csr_ex
  // Probe on prealu_1_x
  // Probe on prealu_1_y
  ROM #(.AddrBits(8), .Bits(32)) Drom (.A(id_ex_1_addr_ex_2), .sel(1'b1), .D(Drom_d));
  RAMDualPort #(.AddrBits(8), .Bits(32)) Dram (
    .A(id_ex_1_addr_ex_2), .Din(id_ex_1_mem_ex), .str(and_3_out), .C(not_1_out), .ld(1'b1), .D(Dram_d));
  ALU alu_1 (.aluop(ex_controller_1_aluop), .x(prealu_1_x), .y(prealu_1_y), .aluR({alu_1_alur, bxx}));
  and and_3 (and_3_out, mw, id_ex_1_addr_ex[10]);
  Multiplexer #(.Bits(32)) multiplexer_2 (
    .sel(id_ex_1_addr_ex[10]), .in_0(Drom_d), .in_1(Dram_d), .out(multiplexer_2_out));
  preRW prerw_1 (
    .aluR({alu_1_alur, bxx}), .sel(wsel), .ramData(multiplexer_2_out), .csrData(id_ex_1_csr_ex),
    .rwData(prerw_1_rwdata));
  // Probe on {alu_1_alur, bxx}
  // Probe on multiplexer_2_out

  // Other names for the same wires on the sheet: in0[31:0] = IN; K0 = key0; K1 = key1; out0[31:0] = OUT

  // Notes on the sheet:
  //   clock: Hz: 2
  //   RX: default 1
  //   contents of Irom (hex, n*v repeats v):
  //   4c00293,36129073,5c00313,36231073,6c00393,36339073,3711e073,37216073,3733e073,4e204b7,
  //   33249073,78000e13,4e1e13,304e1073,30045073,13,13,10500073,ff5ff0ef,33029073,fff2c293,
  //   33029073,200073,33031073,fff34313,33031073,200073,334023f3,33039073,33339073,3320e073,
  //   13,13,3320f073,200073
  //   contents of Drom (hex, n*v repeats v):
  //   0,fffff0b7,400093,40016f,158513,feb50fe3,fff20193,318233,308023,309023,30a023,40a223,
  //   402383,800403,801403,804403,805403,802403,ff3a413,ffe3b413,fff44413,247493,249513,
  //   1f4d593,25d593,40125613,40460633,c616b3,c42733,c43733,864733,e6d7b3,40f75733,d77733,
  //   c76833,200713,11d873,11d873,810f3,710f3,a973,25973,1039f3,10f9f3,e7
endmodule
