// Digital circuit redirect.dig as structural Verilog
module redirect (
  input  [31:0] ins_ID,
  input  [31:0] rs1_ID,
  input  [31:0] rs2_ID,
  input  regw,
  input  [4:0] rd_addr,
  input  [31:0] rd_EX,
  output [31:0] RS1,
  output [31:0] RS2
);

  wire and_1_out, and_2_out, comparator_1_eq, comparator_2_eq;

  Comparator #(.Bits(5)) comparator_1 (.a(ins_ID[19:15]), .b(rd_addr), .eq(comparator_1_eq));  // open: gt, lt
  Comparator #(.Bits(5)) comparator_2 (.a(ins_ID[24:20]), .b(rd_addr), .eq(comparator_2_eq));  // open: gt, lt
  and and_1 (and_1_out, regw, comparator_1_eq);
  and and_2 (and_2_out, regw, comparator_2_eq);
  Multiplexer #(.Bits(32)) multiplexer_1 (.sel(and_1_out), .in_0(rs1_ID), .in_1(rd_EX), .out(RS1));
  Multiplexer #(.Bits(32)) multiplexer_2 (.sel(and_2_out), .in_0(rs2_ID), .in_1(rd_EX), .out(RS2));

  // Other names for the same wires on the sheet: ins[31:0] = ins_ID
endmodule
