// Digital circuit uart.dig as structural Verilog
module uart (
  input  CLK,
  input  TX_vld,
  input  [7:0] TX_data,
  input  [15:0] RATE,
  input  RX,
  output [7:0] RX_data,
  output RX_rdy,
  output TX_rdy,
  output RX_vld,
  output TX
);

  wire and_1_out, and_2_out, and_3_out, cnt_rx, cnt_tx, comparator_1_eq, comparator_2_eq, d_ff_4_q,
       d_ff_as_1_q, jk_ff_1_q, nand_1_out, not_1_out, or_1_out, q0, q1, q2, q3, q4, q5, q6, q7, que1_ovf,
       que2_ovf, tx_done;
  wire [3:0] que2_out, sel;
  wire [9:2] a2_q;
  wire [15:0] CNT_RX_out, CNT_TX_out;

  and and_1 (and_1_out, TX_rdy, TX_vld);
  D_FF_AS d_ff_as_1 (.Set(1'b0), .D(1'b1), .C(cnt_rx), .Clr(RX_vld), .Q(d_ff_as_1_q));  // open: nQ
  D_FF d_ff_1 (.D(RX), .C(cnt_rx), .Q(q7));  // open: nQ
  JK_FF jk_ff_1 (.J(and_1_out), .C(CLK), .K(tx_done), .Q(jk_ff_1_q), .nQ(TX_rdy));
  D_FF d_ff_2 (.D(q7), .C(cnt_rx), .Q(q6));  // open: nQ
  nand nand_1 (nand_1_out, RX, ~d_ff_as_1_q);  // NAnd
  Counter #(.Bits(16)) u_CNT_TX (.en(jk_ff_1_q), .C(CLK), .clr(comparator_1_eq), .out(CNT_TX_out));  // open: ovf
  D_FF d_ff_3 (.D(q6), .C(cnt_rx), .Q(q5));  // open: nQ
  D_FF d_ff_4 (.D(nand_1_out), .C(CLK), .Q(d_ff_4_q), .nQ(RX_rdy));
  // Probe on CNT_TX_out
  Comparator #(.Bits(16)) comparator_1 (.a(CNT_TX_out), .b({1'b0, RATE[15:1]}), .eq(comparator_1_eq));  // open: gt, lt
  // Probe on {1'b0, RATE[15:1]}
  D_FF d_ff_5 (.D(q5), .C(cnt_rx), .Q(q4));  // open: nQ
  Counter #(.Bits(16)) u_CNT_RX (.en(d_ff_4_q), .C(CLK), .clr(or_1_out), .out(CNT_RX_out));  // open: ovf
  JK_FF_AS jk_ff_as_1 (
    .Set(1'b0), .J(comparator_1_eq), .C(CLK), .K(comparator_1_eq), .Clr(TX_rdy), .Q(cnt_tx));  // open: nQ
  D_FF d_ff_6 (.D(q4), .C(cnt_rx), .Q(q3));  // open: nQ
  // Probe on CNT_RX_out
  Comparator #(.Bits(16)) comparator_2 (.a(CNT_RX_out), .b({1'b0, RATE[15:1]}), .eq(comparator_2_eq));  // open: gt, lt
  // Probe on {1'b0, RATE[15:1]}
  or or_1 (or_1_out, RX_rdy, comparator_2_eq);
  D_FF d_ff_7 (.D(q3), .C(cnt_rx), .Q(q2));  // open: nQ
  D_FF d_ff_8 (.D(q2), .C(cnt_rx), .Q(q1));  // open: nQ
  JK_FF_AS jk_ff_as_2 (
    .Set(1'b0), .J(comparator_2_eq), .C(CLK), .K(comparator_2_eq), .Clr(RX_rdy), .Q(cnt_rx));  // open: nQ
  CounterPreset #(.maxValue(10), .Bits(4)) que1 (
    .en(1'b1), .C(cnt_tx), .dir(1'b0), .in(4'b0000), .ld(1'b0), .clr(TX_rdy), .out(sel), .ovf(que1_ovf));
  D_FF #(.Bits(8)) a2 (.D(TX_data), .C(TX_vld), .Q(a2_q));  // open: nQ
  D_FF d_ff_9 (.D(q1), .C(cnt_rx), .Q(q0));  // open: nQ
  and and_2 (and_2_out, que1_ovf, ~cnt_tx);  // And
  D_FF_AS d_ff_as_2 (.Set(1'b0), .D(1'b1), .C(and_2_out), .Clr(TX_rdy), .Q(tx_done));  // open: nQ
  BitSelector #(.Selector_Bits(4)) bitselector_1 (.in({{6{1'b1}}, a2_q, 2'b01}), .sel(sel), .out(TX));
  // Probe on sel
  CounterPreset #(.maxValue(9), .Bits(4)) que2 (
    .en(1'b1), .C(cnt_rx), .dir(1'b0), .in(4'b0000), .ld(1'b0), .clr(RX_rdy), .out(que2_out), .ovf(que2_ovf));
  not not_1 (not_1_out, cnt_rx);
  D_FF #(.Bits(8)) d_ff_10 (.D({q7, q6, q5, q4, q3, q2, q1, q0}), .C(and_3_out), .Q(RX_data));  // open: nQ
  // Probe on que2_out
  and and_3 (and_3_out, que2_ovf, not_1_out);
  D_FF_AS d_ff_as_3 (.Set(1'b0), .D(1'b1), .C(and_3_out), .Clr(RX_rdy), .Q(RX_vld));  // open: nQ

  // Other names for the same wires on the sheet: rate_t[14:0] = RATE[15:1]

  // Notes on the sheet:
  //   CLK: Hz: 2
  //   RATE: default 2
  //   RX: default 1
endmodule
