// Digital circuit wishbone.dig as structural Verilog
module wishbone (
  input  Rst,
  input  [7:0] DataIn,
  input  Ack,
  input  Clk,
  output [7:0] Addr,
  output [7:0] DataOut,
  output We,
  output Stb,
  output Cyc,
  output [7:0] Datsave
);

  wire and_2_out, and_3_out, clk_t, comp2_lt, comp3_lt, counter4_out, dff3_q, multiplexer_1_out,
       multiplexer_2_out, multiplexer_3_out, not_2_out, not_3_out, not_4_out, rst_t;
  wire [7:0] counter1_out, counter2_out, counter3_out;

  not not_1 (rst_t, Rst);
  Comparator #(.Bits(8)) comp3 (.a(counter1_out), .b(8'h11), .lt(comp3_lt));  // open: gt, eq
  not not_2 (not_2_out, Ack);
  and and_1 (clk_t, Clk, comp3_lt);
  Counter counter4 (.en(1'b1), .C(not_2_out), .clr(rst_t), .out(counter4_out));  // open: ovf
  D_FF_AS dff3 (.Set(1'b0), .D(Ack), .C(clk_t), .Clr(rst_t), .Q(dff3_q));  // open: nQ
  Multiplexer multiplexer_1 (.sel(dff3_q), .in_0(counter4_out), .in_1(1'b0), .out(multiplexer_1_out));
  Multiplexer multiplexer_2 (.sel(dff3_q), .in_0(1'b1), .in_1(1'b0), .out(multiplexer_2_out));
  D_FF_AS dff1 (.Set(1'b0), .D(multiplexer_1_out), .C(clk_t), .Clr(rst_t), .Q(We));  // open: nQ
  D_FF_AS dff2 (.Set(1'b0), .D(multiplexer_2_out), .C(clk_t), .Clr(rst_t), .Q(Cyc));  // open: nQ
  not not_3 (not_3_out, Ack);
  Counter #(.Bits(8)) counter1 (.en(1'b1), .C(not_3_out), .clr(rst_t), .out(counter1_out));  // open: ovf
  Comparator #(.Bits(8)) comp2 (.a(counter1_out), .b(8'h11), .lt(comp2_lt));  // open: gt, eq
  Counter #(.Bits(8)) counter2 (.en(1'b1), .C(We), .clr(rst_t), .out(counter2_out));  // open: ovf
  not not_4 (not_4_out, We);
  Multiplexer multiplexer_3 (.sel(comp2_lt), .in_0(1'b0), .in_1(1'b1), .out(multiplexer_3_out));
  and and_2 (and_2_out, Ack, Cyc, not_4_out);
  and and_3 (and_3_out, 1'b1, Cyc);
  Counter #(.Bits(8)) counter3 (.en(1'b1), .C(and_2_out), .clr(rst_t), .out(counter3_out));  // open: ovf
  // Probe on counter3_out

  assign Stb = Cyc;

  // Other names for the same wires on the sheet: acki = Ack; addro[7:0] = Addr; dati[7:0] = DataIn;
  //   dato[7:0] = DataOut; dats[7:0] = Datsave; cyco = Cyc; stbo = Cyc; weo = We

  // Notes on the sheet:
  //   R/W
  //   clk can be optimized
  //   clk can be optimized-->resolved
endmodule
