// Digital circuit AXI4-lite.dig as structural Verilog
module AXI4_lite (
  input  [31:0] aluR,
  input  [11:0] csrAddr,
  input  clk,
  input  W_EN,
  input  [31:0] IN0,
  input  [31:0] RDATA,
  input  ARREADY,
  input  RREADY,
  input  AWREADY,
  input  WREADY,
  input  BVALID,
  input  [1:0] BRESP,
  output [31:0] ioData,
  output [31:0] OUT,
  output [31:0] AWADDR,
  output AWVALID,
  output [31:0] WDATA,
  output [31:0] ARADDR,
  output WVALID,
  output RVALID,
  output ARVALID,
  output BREADY
);

  wire and_1_out, and_2_out, and_3_out, and_4_out, and_5_out, and_6_out, and_7_out, and_8_out, and_11_out,
       and_12_out, and_13_out, and_14_out, and_15_out, arOK, comparator_1_eq, comparator_2_eq,
       comparator_3_eq, comparator_4_eq, comparator_5_eq, comparator_6_eq, comparator_7_eq, comparator_8_eq,
       comparator_9_eq, priorityencoder_1_any;
  wire [2:0] priorityencoder_1_num;
  wire [6:1] AxiStatus;
  wire [31:0] bitextender_1_out, multiplexer_1_out, rDATA_t;
  wire [31:1] AxiConfig;

  Comparator #(.Bits(4)) comparator_1 (.a(csrAddr[11:8]), .b(4'b0011), .eq(comparator_1_eq));  // open: gt, lt
  Comparator #(.Bits(8)) comparator_2 (.a(csrAddr[7:0]), .b(8'h30), .eq(comparator_2_eq));  // open: gt, lt
  Comparator #(.Bits(8)) comparator_3 (.a(csrAddr[7:0]), .b(8'h3f), .eq(comparator_3_eq));  // open: gt, lt
  Comparator #(.Bits(8)) comparator_4 (.a(csrAddr[7:0]), .b(8'h2a), .eq(comparator_4_eq));  // open: gt, lt
  Comparator #(.Bits(8)) comparator_5 (.a(csrAddr[7:0]), .b(8'h2b), .eq(comparator_5_eq));  // open: gt, lt
  Comparator #(.Bits(8)) comparator_6 (.a(csrAddr[7:0]), .b(8'h2c), .eq(comparator_6_eq));  // open: gt, lt
  Comparator #(.Bits(8)) comparator_7 (.a(csrAddr[7:0]), .b(8'h2d), .eq(comparator_7_eq));  // open: gt, lt
  Comparator #(.Bits(8)) comparator_8 (.a(csrAddr[7:0]), .b(8'h2e), .eq(comparator_8_eq));  // open: gt, lt
  Comparator #(.Bits(8)) comparator_9 (.a(csrAddr[7:0]), .b(8'h2f), .eq(comparator_9_eq));  // open: gt, lt
  and and_1 (and_1_out, comparator_1_eq, W_EN, comparator_2_eq);
  and and_2 (and_2_out, comparator_1_eq, W_EN, comparator_3_eq);
  and and_3 (and_3_out, comparator_1_eq, W_EN, comparator_4_eq);
  and and_4 (and_4_out, comparator_1_eq, W_EN, comparator_5_eq);
  and and_5 (and_5_out, comparator_1_eq, W_EN, comparator_6_eq);
  and and_6 (and_6_out, comparator_1_eq, W_EN, comparator_7_eq);
  and and_7 (and_7_out, comparator_1_eq, W_EN, comparator_8_eq);
  and and_8 (and_8_out, comparator_1_eq, W_EN, comparator_9_eq);
  Register #(.Bits(32)) u_out (.D(aluR), .C(clk), .en(and_1_out), .Q(OUT));
  // Probe on OUT
  Register #(.Bits(32)) DATAout (.D(aluR), .C(clk), .en(and_8_out), .Q(WDATA));
  Register #(.Bits(32)) Config (
    .D(aluR), .C(clk), .en(and_3_out), .Q({AxiConfig[31:5], BREADY, WVALID, AWVALID, AxiConfig[1], ARVALID}));
  Register #(.Bits(32)) RADDR (.D(aluR), .C(clk), .en(and_4_out), .Q(ARADDR));
  Register #(.Bits(32)) WADDR (.D(aluR), .C(clk), .en(and_5_out), .Q(AWADDR));
  PriorityEncoder #(.Selector_Bits(3)) priorityencoder_1 (
    .in0(and_1_out), .in1(and_2_out), .in2(and_3_out), .in3(and_4_out), .in4(and_5_out), .in5(and_6_out),
    .in6(and_7_out), .in7(and_8_out), .num(priorityencoder_1_num), .any(priorityencoder_1_any));
  and and_9 (RVALID, arOK, AxiConfig[1]);
  BitExtender #(.inputBits(1), .outputBits(32)) bitextender_1 (.in(priorityencoder_1_any), .out(bitextender_1_out));
  Multiplexer #(.Selector_Bits(3), .Bits(32)) multiplexer_1 (
    .sel(priorityencoder_1_num), .in_0(OUT), .in_1(IN0),
    .in_2({AxiConfig[31:5], BREADY, WVALID, AWVALID, AxiConfig[1], ARVALID}), .in_3(ARADDR), .in_4(AWADDR),
    .in_5({{25{1'b0}}, AxiStatus, arOK}), .in_6(rDATA_t), .in_7(WDATA), .out(multiplexer_1_out));
  // Probe on priorityencoder_1_num
  assign ioData = bitextender_1_out & multiplexer_1_out;  // And and_10, 32 bits wide
  and and_11 (and_11_out, BREADY, BVALID);
  and and_12 (and_12_out, RVALID, RREADY);
  and and_13 (and_13_out, WVALID, WREADY);
  Register #(.Bits(32)) DATAin (.D(RDATA), .C(clk), .en(and_12_out), .Q(rDATA_t));
  and and_14 (and_14_out, ARREADY, ARVALID);
  and and_15 (and_15_out, AWREADY, AWVALID);
  D_FF_AS #(.Bits(2)) d_ff_as_1 (
    .Set(1'b1), .D(BRESP), .C(and_11_out), .Clr(AxiConfig[5]), .Q(AxiStatus[5:4]));  // open: nQ
  D_FF_AS d_ff_as_2 (.Set(1'b1), .D(1'b1), .C(and_11_out), .Clr(AxiConfig[5]), .Q(AxiStatus[6]));  // open: nQ
  D_FF_AS d_ff_as_3 (.Set(1'b1), .D(1'b1), .C(and_13_out), .Clr(AxiConfig[5]), .Q(AxiStatus[3]));  // open: nQ
  D_FF_AS d_ff_as_4 (.Set(1'b1), .D(1'b1), .C(and_12_out), .Clr(AxiConfig[5]), .Q(AxiStatus[1]));  // open: nQ
  D_FF_AS d_ff_as_5 (.Set(1'b1), .D(1'b1), .C(and_14_out), .Clr(AxiConfig[5]), .Q(arOK));  // open: nQ
  D_FF_AS d_ff_as_6 (.Set(1'b1), .D(1'b1), .C(and_15_out), .Clr(AxiConfig[5]), .Q(AxiStatus[2]));  // open: nQ

  // Other names for the same wires on the sheet: addr[11:0] = csrAddr; AxiStatus[0] = arOK;
  //   AxiConfig (some bits) = {BREADY, WVALID, AWVALID, ARVALID}; rVALID_t = AxiConfig[1]; status_clr = AxiConfig[5];
  //   Din[31:0] = aluR; Dout[31:0] = ioData; IN_0[31:0] = IN0; out0[31:0] = OUT; rADDR[31:0] = ARADDR;
  //   wADDR[31:0] = AWADDR; we = W_EN

  // Notes on the sheet:
  //   bresp
  //   bOK
  //   awOK
  //   rOK
  //   arOK
  //   wOK
endmodule
