// Digital circuit microp-controller.dig as structural Verilog
module microp_controller (
  input  [31:0] ins,
  output [1:0] pcsel,
  output [3:0] aluop,
  output [3:0] alusel,
  output [2:0] wsel,
  output rw,
  output brk,
  output csrw,
  output mw,
  output mr,
  output mret
);

  wire aluix_eq, alux_eq, and_1_out, auipc_eq, bxx_eq, comparator_1_eq, comparator_2_eq, comparator_3_eq,
       csrw_t, csrx_eq, demultiplexer_1_out_0, demultiplexer_1_out_1, demultiplexer_2_out_0,
       demultiplexer_2_out_1, jal_eq, jalr_eq, lui_eq, lx_eq, multi_any, RV32, rw_t, single_any, sx_eq, sys;
  wire [3:0] bitextender_1_out;
  wire [5:0] and_3_out, multiplexer_1_out;
  wire [5:3] multi_num;
  wire [10:10] MROM_d;

  Comparator #(.Bits(3)) comparator_1 (.a(ins[14:12]), .b(3'b101), .eq(comparator_1_eq));  // open: gt, lt
  Comparator #(.Bits(5)) lui (.a(ins[6:2]), .b(5'b01101), .eq(lui_eq));  // open: gt, lt
  Comparator #(.Bits(5)) auipc (.a(ins[6:2]), .b(5'b00101), .eq(auipc_eq));  // open: gt, lt
  Comparator #(.Bits(5)) jal (.a(ins[6:2]), .b(5'b11011), .eq(jal_eq));  // open: gt, lt
  Comparator #(.Bits(5)) jalr (.a(ins[6:2]), .b(5'b11001), .eq(jalr_eq));  // open: gt, lt
  Comparator #(.Bits(5)) csrx (.a(ins[6:2]), .b(5'b11100), .eq(csrx_eq));  // open: gt, lt
  Comparator #(.Bits(5)) bxx (.a(ins[6:2]), .b(5'b11000), .eq(bxx_eq));  // open: gt, lt
  Comparator #(.Bits(5)) lx (.a(ins[6:2]), .b({5{1'b0}}), .eq(lx_eq));  // open: gt, lt
  Comparator #(.Bits(5)) sx (.a(ins[6:2]), .b(5'b01000), .eq(sx_eq));  // open: gt, lt
  Comparator #(.Bits(5)) alux (.a(ins[6:2]), .b(5'b01100), .eq(alux_eq));  // open: gt, lt
  Comparator #(.Bits(5)) aluix (.a(ins[6:2]), .b(5'b00100), .eq(aluix_eq));  // open: gt, lt
  and and_1 (and_1_out, comparator_1_eq, ins[30]);
  PriorityEncoder #(.Selector_Bits(2)) single (
    .in0(lui_eq), .in1(auipc_eq), .in2(jal_eq), .in3(jalr_eq), .num(and_3_out[1:0]), .any(single_any));
  Demultiplexer demultiplexer_1 (
    .sel(ins[30]), .in(alux_eq), .out_0(demultiplexer_1_out_0), .out_1(demultiplexer_1_out_1));
  Demultiplexer demultiplexer_2 (
    .sel(and_1_out), .in(aluix_eq), .out_0(demultiplexer_2_out_0), .out_1(demultiplexer_2_out_1));
  Comparator #(.Bits(3)) comparator_2 (.a(ins[14:12]), .b(3'b000), .eq(comparator_2_eq));  // open: gt, lt
  BitExtender #(.inputBits(1), .outputBits(4)) bitextender_1 (.in(single_any), .out(bitextender_1_out));
  and and_2 (sys, comparator_2_eq, csrx_eq);
  PriorityEncoder #(.Selector_Bits(3)) multi (
    .in0(csrx_eq), .in1(bxx_eq), .in2(lx_eq), .in3(sx_eq), .in4(demultiplexer_1_out_0),
    .in5(demultiplexer_1_out_1), .in6(demultiplexer_2_out_0), .in7(demultiplexer_2_out_1), .num(multi_num),
    .any(multi_any));
  assign and_3_out[5:2] = bitextender_1_out & 4'b0111;  // And and_3, 4 bits wide
  and and_4 (mr, lx_eq, RV32);
  and and_5 (mw, RV32, sx_eq);
  Multiplexer #(.Bits(6)) multiplexer_1 (
    .sel(multi_any), .in_0(and_3_out), .in_1({multi_num, ins[14:12]}), .out(multiplexer_1_out));
  // Probe on multiplexer_1_out
  ROM #(.AddrBits(6), .Bits(16), .Addr_Bits(6)) MROM (
    .A(multiplexer_1_out), .sel(1'b1), .D({rw_t, wsel, csrw_t, MROM_d[10], pcsel, alusel, aluop}));
  Comparator #(.Bits(5)) comparator_3 (.a(ins[11:7]), .b({5{1'b0}}), .eq(comparator_3_eq));  // open: gt, lt
  and and_6 (mret, sys, ~ins[20], RV32);  // And
  and and_7 (brk, sys, ins[20], RV32);
  and and_8 (csrw, RV32, csrw_t);
  and and_9 (rw, RV32, ~comparator_3_eq, rw_t);  // And
  and and_10 (RV32, ins[0], ins[1]);

  // Other names for the same wires on the sheet: op[4:0] = ins[6:2]; rd[4:0] = ins[11:7]; funct3[2:0] = ins[14:12];
  //   break = ins[20]; branch = ins[30]

  // Notes on the sheet:
  //   contents of MROM (hex, n*v repeats v):
  //   7000,b869,b866,b877,0,b849,b846,b857,71ce,71cc,0,0,71c2,71ca,71c3,71cb,8080,9080,
  //   a080,0,c080,d080,e080,0,a0,10a0,20a0,0,f0ef,f0e0,f2f0,f3f0,f0c0,f0d1,f0c2,f0c3,f0c4,
  //   f0d5,f0c6,f0c7,f0c8,0,0,0,0,f0dd,0,0,f080,f0b1,f082,f083,f084,f085,f086,f087,0,0,
  //   0,0,0,f0bd
endmodule
