// Digital circuit preALU.dig as structural Verilog
module preALU (
  input  [3:0] alusel,
  input  [31:0] pc_alu,
  input  [31:0] ins_alu,
  input  [31:0] rs1,
  input  [31:0] rs2,
  input  [31:0] csrData,
  output [31:0] x,
  output [31:0] y
);

  wire [31:0] multiplexer_1_out, multiplexer_2_out, multiplexer_4_out, multiplexer_5_out, multiplexer_6_out,
       multiplexer_7_out, not_1_out, not_2_out;
  wire [31:12] bitextender_1_out, bitextender_2_out;

  assign not_1_out = ~{{27{1'b0}}, ins_alu[19:15]};  // Not not_1, 32 bits wide
  assign not_2_out = ~rs1;  // Not not_2, 32 bits wide
  Multiplexer #(.Selector_Bits(2), .Bits(32)) multiplexer_1 (
    .sel(alusel[1:0]), .in_0({{27{1'b0}}, ins_alu[19:15]}), .in_1(not_1_out), .in_2(rs1), .in_3(not_2_out),
    .out(multiplexer_1_out));
  Multiplexer #(.Bits(32)) multiplexer_2 (.sel(alusel[1]), .in_0(rs1), .in_1(pc_alu), .out(multiplexer_2_out));
  Multiplexer #(.Selector_Bits(2), .Bits(32)) multiplexer_3 (
    .sel(alusel[3:2]), .in_0({32{1'b0}}), .in_1(multiplexer_1_out), .in_2(rs1), .in_3(multiplexer_2_out),
    .out(x));
  BitExtender #(.inputBits(1), .outputBits(20)) bitextender_1 (.in(ins_alu[31]), .out(bitextender_1_out));
  BitExtender #(.inputBits(1), .outputBits(20)) bitextender_2 (.in(ins_alu[31]), .out(bitextender_2_out));
  Multiplexer #(.Bits(32)) multiplexer_4 (
    .sel(alusel[0]), .in_0(rs2), .in_1({{27{1'b0}}, rs2[4:0]}), .out(multiplexer_4_out));
  Multiplexer #(.Bits(32)) multiplexer_5 (
    .sel(alusel[0]), .in_0({ins_alu[31:12], {12{1'b0}}}), .in_1(32'h4), .out(multiplexer_5_out));
  Multiplexer #(.Selector_Bits(2), .Bits(32)) multiplexer_6 (
    .sel(alusel[1:0]), .in_0({bitextender_1_out, ins_alu[31:20]}), .in_1({32{1'b0}}),
    .in_2({bitextender_2_out, ins_alu[31:25], ins_alu[11:7]}), .in_3({{27{1'b0}}, ins_alu[24:20]}),
    .out(multiplexer_6_out));
  Multiplexer #(.Bits(32)) multiplexer_7 (
    .sel(alusel[1]), .in_0(multiplexer_4_out), .in_1(multiplexer_5_out), .out(multiplexer_7_out));
  Multiplexer #(.Selector_Bits(2), .Bits(32)) multiplexer_8 (
    .sel(alusel[3:2]), .in_0({32{1'b0}}), .in_1(csrData), .in_2(multiplexer_6_out), .in_3(multiplexer_7_out),
    .out(y));

  // Other names for the same wires on the sheet: csr[31:0] = csrData; ins[31:0] = ins_alu; opc[31:0] = pc_alu

  // Notes on the sheet:
  //   alusel: aluX input
  //   ins_alu: instruction
  //   ZEimm
  //   alui,lx
  //   lui,auipc
  //   sx
  //   shifti
  //   alu,bxx
  //   shift
  //   jalx
  //   csrx
endmodule
