// Digital circuit DMAC.dig as structural Verilog
module DMAC (
  input  [31:0] aluR,
  input  [11:0] csrAddr,
  input  clk,
  input  W_EN,
  input  [31:0] DAT_I,
  input  ACK_I,
  input  DREQ,
  output [31:0] ioData,
  output [31:0] ADR_O,
  output [31:0] DAT_O,
  output WE_O,
  output CYCSTB_O,
  output [3:0] SEL_O,
  output DACK,
  output HOLD_INTR,
  output [7:0] test_CNT,
  output DMA_int,
  output DMA_EN
);

  wire and_1_out, and_2_out, and_3_out, and_4_out, and_5_out, and_7_out, and_8_out, comparator_1_eq,
       comparator_2_eq, comparator_3_eq, comparator_4_eq, comparator_5_eq, comparator_6_eq, counter_ovf,
       jk_ff_as_1_q, priorityencoder_1_any;
  wire [1:0] priorityencoder_1_num;
  wire [7:0] cnt;
  wire [31:0] bitextender_1_out, multiplexer_1_out, rADR, rADR_q, wADR, wADR_q;
  wire [31:2] \config ;

  and and_1 (and_1_out, DREQ, DMA_EN);
  Comparator #(.Bits(4)) comparator_1 (.a(csrAddr[11:8]), .b(4'b0011), .eq(comparator_1_eq));  // open: gt, lt
  Comparator #(.Bits(8)) comparator_2 (.a(csrAddr[7:0]), .b(8'h26), .eq(comparator_2_eq));  // open: gt, lt
  Comparator #(.Bits(8)) comparator_3 (.a(csrAddr[7:0]), .b(8'h27), .eq(comparator_3_eq));  // open: gt, lt
  Comparator #(.Bits(8)) comparator_4 (.a(csrAddr[7:0]), .b(8'h28), .eq(comparator_4_eq));  // open: gt, lt
  Comparator #(.Bits(8)) comparator_5 (.a(csrAddr[7:0]), .b(8'h29), .eq(comparator_5_eq));  // open: gt, lt
  D_FF_AS d_ff_as_1 (.Set(1'b0), .D(and_1_out), .C(clk), .Clr(CYCSTB_O), .Q(DACK));  // open: nQ
  or or_1 (HOLD_INTR, DACK, DMA_int);
  and and_2 (and_2_out, comparator_1_eq, W_EN, comparator_2_eq);
  and and_3 (and_3_out, comparator_1_eq, W_EN, comparator_3_eq);
  and and_4 (and_4_out, comparator_1_eq, W_EN, comparator_4_eq);
  and and_5 (and_5_out, comparator_1_eq, W_EN, comparator_5_eq);
  Register #(.Bits(32)) u_Config (
    .D(aluR), .C(clk), .en(and_2_out), .Q({\config [31:16], cnt, SEL_O, \config [3:2], DMA_EN, CYCSTB_O}));
  Register #(.Bits(32)) u_rADR (.D(aluR), .C(clk), .en(and_4_out), .Q(rADR_q));
  Register #(.Bits(32)) u_wADR (.D(aluR), .C(clk), .en(and_5_out), .Q(wADR_q));
  PriorityEncoder #(.Selector_Bits(2)) priorityencoder_1 (
    .in0(and_2_out), .in1(and_3_out), .in2(and_4_out), .in3(and_5_out), .num(priorityencoder_1_num),
    .any(priorityencoder_1_any));
  Add #(.Bits(32)) add_1 (.a({{24{1'b0}}, test_CNT}), .b(rADR_q), .c_i(1'b0), .s(rADR));  // open: c_o
  Add #(.Bits(32)) add_2 (.a({{24{1'b0}}, test_CNT}), .b(wADR_q), .c_i(1'b0), .s(wADR));  // open: c_o
  Multiplexer #(.Selector_Bits(2), .Bits(32)) multiplexer_1 (
    .sel(priorityencoder_1_num), .in_0({\config [31:16], cnt, SEL_O, \config [3:2], DMA_EN, CYCSTB_O}),
    .in_1({{31{1'b0}}, DACK}), .in_2(rADR), .in_3(wADR), .out(multiplexer_1_out));
  BitExtender #(.inputBits(1), .outputBits(32)) bitextender_1 (.in(priorityencoder_1_any), .out(bitextender_1_out));
  // Probe on priorityencoder_1_num
  // Probe on multiplexer_1_out
  assign ioData = multiplexer_1_out & bitextender_1_out;  // And and_6, 32 bits wide
  and and_7 (and_7_out, ~WE_O, ~DMA_int, ACK_I);  // And
  and and_8 (and_8_out, WE_O, ~DMA_int, ACK_I);  // And
  CounterPreset #(.Bits(8)) counter (
    .en(and_8_out), .C(clk), .dir(1'b0), .in({8{1'b0}}), .ld(1'b0), .clr(~CYCSTB_O), .out(test_CNT),
    .ovf(counter_ovf));
  JK_FF_AS jk_ff_as_1 (.Set(1'b0), .J(ACK_I), .C(clk), .K(ACK_I), .Clr(~CYCSTB_O), .Q(jk_ff_as_1_q));  // open: nQ
  Register #(.Bits(32)) register_1 (.D(DAT_I), .C(clk), .en(and_7_out), .Q(DAT_O));
  Comparator #(.Bits(8)) comparator_6 (.a(test_CNT), .b(cnt), .eq(comparator_6_eq));  // open: gt, lt
  // Probe on counter_ovf
  and and_9 (WE_O, jk_ff_as_1_q, ~DMA_int);  // And
  Multiplexer #(.Bits(32)) multiplexer_2 (.sel(WE_O), .in_0(rADR), .in_1(wADR), .out(ADR_O));
  and and_10 (DMA_int, comparator_6_eq, CYCSTB_O);

  // Other names for the same wires on the sheet: acki = ACK_I; addr[11:0] = csrAddr; ADR_CNT[7:0] = test_CNT;
  //   config (some bits) = {cnt, SEL_O, DMA_EN, CYCSTB_O}; HLDA = CYCSTB_O; Din[31:0] = aluR; DMA_WE = WE_O;
  //   Dout[31:0] = ioData; hold = DACK; status[0] = DACK; we = W_EN
endmodule
