// Digital circuit alusel.dig as structural Verilog
module alusel (
  input  op6,
  input  op5,
  input  op4,
  input  op3,
  input  op2,
  input  F2,
  input  F1,
  input  F0,
  output asel3,
  output asel2,
  output asel1,
  output asel0
);

  wire and_1_out, and_2_out, and_3_out, and_4_out, and_5_out, and_6_out, and_7_out, and_8_out, and_9_out,
       and_10_out, and_11_out, and_12_out, and_13_out, and_14_out, and_15_out, and_16_out, and_17_out,
       and_18_out, and_19_out, and_20_out, and_21_out, and_22_out, and_23_out, and_24_out, not_1_out,
       not_2_out, not_3_out, not_4_out, not_5_out, not_6_out, not_7_out, not_8_out;

  not not_1 (not_1_out, op6);
  not not_2 (not_2_out, op5);
  not not_3 (not_3_out, op4);
  not not_4 (not_4_out, op3);
  not not_5 (not_5_out, op2);
  not not_6 (not_6_out, F2);
  not not_7 (not_7_out, F1);
  not not_8 (not_8_out, F0);
  and and_1 (and_1_out, not_8_out, not_6_out, not_5_out, not_4_out, not_1_out);
  and and_2 (and_2_out, not_8_out, not_5_out, not_4_out, not_2_out, not_1_out);
  and and_3 (and_3_out, not_7_out, not_6_out, not_5_out, not_4_out, not_3_out, op5);
  and and_4 (and_4_out, not_7_out, not_5_out, not_4_out, not_2_out, not_1_out);
  and and_5 (and_5_out, F2, not_4_out, not_3_out, op5, op6);
  and and_6 (and_6_out, op2, not_3_out, op5, op6);
  and and_7 (and_7_out, not_4_out, op4, not_1_out);
  and and_8 (and_8_out, F0, not_7_out, not_5_out, not_4_out, op5, op6);
  and and_9 (and_9_out, F1, F2, not_5_out, not_4_out, op5, op6);
  and and_10 (and_10_out, F1, not_5_out, not_4_out, op4, op5);
  and and_11 (and_11_out, not_7_out, not_4_out, not_3_out, op5, op6);
  and and_12 (and_12_out, op2, not_4_out, op4, not_1_out);
  and and_13 (and_13_out, op2, not_3_out, op5, op6);
  and and_14 (and_14_out, not_4_out, op4, op5, not_1_out);
  and and_15 (and_15_out, not_8_out, not_6_out, not_5_out, not_4_out, not_3_out, op5, not_1_out);
  and and_16 (and_16_out, F0, not_6_out, not_5_out, not_4_out, op4, op5, op6);
  and and_17 (and_17_out, F0, not_7_out, not_4_out, op4, not_2_out, not_1_out);
  and and_18 (and_18_out, not_7_out, not_6_out, not_5_out, not_4_out, not_3_out, op5, not_1_out);
  and and_19 (and_19_out, F1, not_6_out, not_5_out, not_4_out, op4, op5, op6);
  and and_20 (and_20_out, op2, not_4_out, op4, not_1_out);
  and and_21 (and_21_out, op2, not_3_out, op5, op6);
  and and_22 (and_22_out, F0, F1, not_5_out, not_4_out, op4, op5, op6);
  and and_23 (and_23_out, F0, not_7_out, not_5_out, not_4_out, op4, not_1_out);
  and and_24 (and_24_out, op2, not_3_out, op5, op6);
  or or_1 (asel0, and_22_out, and_23_out, and_24_out);
  or or_2 (asel3, and_1_out, and_2_out, and_3_out, and_4_out, and_5_out, and_6_out, and_7_out);
  or or_3 (asel2, and_8_out, and_9_out, and_10_out, and_11_out, and_12_out, and_13_out, and_14_out);
  or or_4 (asel1, and_15_out, and_16_out, and_17_out, and_18_out, and_19_out, and_20_out, and_21_out);
endmodule
