// Digital circuit microp-CPU.dig as structural Verilog
module microp_CPU (
  input  clock,
  input  hand,
  input  model,
  input  reset,
  input  [31:0] IN_dev,
  input  [31:0] IN,
  input  DREQ,
  output [31:0] \time ,
  output [31:0] mtcmp,
  output [31:0] OUT,
  output [7:0] out_11
);

  wire and_1_out, and_2_out, and_3_out, and_4_out, break_q, brk, clk, clk_INT, comparator_1_gt, csrw,
       demultiplexer_4_out_0, dmac_1_p6, dmac_1_p14, dmac_1_p20, dmac_1_p21, dmac_1_p22, EN, \int , memw, mr,
       mret, multiplexer_5_out, mw, or_2_out, regw;
  wire [1:0] demultiplexer_3_out_0, demultiplexer_3_out_1, dmac_1_p13, dmac_1_p19, microp_controller_1_pcsel,
       multiplexer_4_out;
  wire [2:0] microp_controller_1_wsel;
  wire [3:0] microp_controller_1_aluop, microp_controller_1_alusel;
  wire [4:0] Irom_d_2, Irom_d_3;
  wire [7:0] demultiplexer_1_out_0, dmac_1_p1_2, multiplexer_2_out;
  wire [8:0] branch_pc_1_pc_2;
  wire [11:0] dmac_1_p2;
  wire [14:0] Irom_d;
  wire [23:0] multiplexer_2_out_2;
  wire [31:0] branch_pc_1_mepc, branch_pc_1_pc, csr_1_csrdata, csr_1_isr, d_ff_1_q, demultiplexer_1_out_1,
       demultiplexer_2_out_0, demultiplexer_2_out_1, demultiplexer_5_out_0, dmac_1_p1, dmac_1_p5, dmac_1_p8,
       dmac_1_p10, dmac_1_p11, dmac_1_p15, dmac_1_p16, dmac_1_p17, Dram_d, Drom_d, multiplexer_3_out,
       multiplexer_6_out, multiplexer_7_out, prealu_1_x, prealu_1_y, premw_1_mwdata, prerw_1_rwdata, RAM_L_d,
       regs_da, regs_db;
  wire [31:8] demultiplexer_1_out_0_2;

  // Probe on {dmac_1_p2, Irom_d_3, Irom_d[14:12], Irom_d_2, Irom_d[6:0]}
  branch_PC branch_pc_1 (
    .pcsel(microp_controller_1_pcsel), .ins_pc({dmac_1_p2, Irom_d_3, Irom_d[14:12], Irom_d_2, Irom_d[6:0]}),
    .mret(mret), .clk(clk), .EN(EN), .INT(\int ), .bxx(dmac_1_p1[0]), .ISR(csr_1_isr), .rs1(regs_da),
    .pc({branch_pc_1_pc[31:11], branch_pc_1_pc_2, branch_pc_1_pc[1:0]}), .mepc(branch_pc_1_mepc));
  // Probe on {dmac_1_p2, Irom_d_3, Irom_d[14:12], Irom_d_2, Irom_d[6:0]}
  microp_controller microp_controller_1 (
    .ins({dmac_1_p2, Irom_d_3, Irom_d[14:12], Irom_d_2, Irom_d[6:0]}), .pcsel(microp_controller_1_pcsel),
    .aluop(microp_controller_1_aluop), .alusel(microp_controller_1_alusel), .wsel(microp_controller_1_wsel),
    .rw(regw), .brk(brk), .csrw(csrw), .mw(mw), .mr(mr), .mret(mret));
  // Probe on {branch_pc_1_pc[31:11], branch_pc_1_pc_2, branch_pc_1_pc[1:0]}
  RegisterFile #(.AddrBits(5), .Bits(32)) regs (
    .Din(prerw_1_rwdata), .we(regw), .Rw(Irom_d_2), .C(clk), .Ra(Irom_d_3), .Rb(dmac_1_p2[4:0]),
    .Da(regs_da), .Db(regs_db));
  CSR csr_1 (
    .aluR({dmac_1_p1[31:10], dmac_1_p1_2, dmac_1_p1[1:0]}), .csrAddr(dmac_1_p2), .mepc(branch_pc_1_mepc),
    .clk(clk_INT), .W_EN(csrw), .EN(EN), .mret(mret), .ExInt(dmac_1_p22), .IOdata(dmac_1_p8),
    .csrData(csr_1_csrdata), .INT(\int ), .ISR(csr_1_isr), .test_1(\time ), .test_2(mtcmp));
  wishbone_BUS wishbone_bus_1 (
    .aluR({dmac_1_p1[31:10], dmac_1_p1_2, dmac_1_p1[1:0]}), .csrAddr(dmac_1_p2), .clk(clk_INT), .W_EN(csrw),
    .IN0(IN), .DAT_I(demultiplexer_5_out_0), .ACK_I(demultiplexer_4_out_0), .DMAdata(dmac_1_p15));  // open: ioData, OUT, ADR_O, DAT_O, WE_O, CYCSTB_O, SEL_O
  // DMAC dmac_1: pin names not known; wires that end beside it: {dmac_1_p1[31:10], dmac_1_p1_2, dmac_1_p1[1:0]}, dmac_1_p2, clk_INT, csrw, dmac_1_p5, dmac_1_p6, DREQ, dmac_1_p8, OUT, dmac_1_p10, dmac_1_p11, dmac_1_p13[0], dmac_1_p13[1], dmac_1_p14, dmac_1_p15, dmac_1_p16, dmac_1_p17, dmac_1_p19[0], dmac_1_p19[1], dmac_1_p20, dmac_1_p21, dmac_1_p22, out_11
  ROM #(.AddrBits(9), .Bits(32)) Irom (
    .A(branch_pc_1_pc_2), .sel(1'b1), .D({dmac_1_p2, Irom_d_3, Irom_d[14:12], Irom_d_2, Irom_d[6:0]}));
  // Probe on {dmac_1_p1[31:10], dmac_1_p1_2, dmac_1_p1[1:0]}
  // Probe on dmac_1_p14
  // Probe on dmac_1_p20
  // Probe on dmac_1_p21
  preALU prealu_1 (
    .alusel(microp_controller_1_alusel),
    .pc_alu({branch_pc_1_pc[31:11], branch_pc_1_pc_2, branch_pc_1_pc[1:0]}),
    .ins_alu({dmac_1_p2, Irom_d_3, Irom_d[14:12], Irom_d_2, Irom_d[6:0]}), .rs1(regs_da), .rs2(regs_db),
    .csrData(csr_1_csrdata), .x(prealu_1_x), .y(prealu_1_y));
  // Probe on csr_1_csrdata
  // Probe on dmac_1_p16
  // Probe on dmac_1_p17
  preRW prerw_1 (
    .sel(microp_controller_1_wsel), .aluR({dmac_1_p1[31:10], dmac_1_p1_2, dmac_1_p1[1:0]}),
    .csrData(csr_1_csrdata), .ramData(multiplexer_7_out), .rwData(prerw_1_rwdata));
  Multiplexer multiplexer_1 (.sel(model), .in_0(hand), .in_1(clock), .out(clk_INT));
  Multiplexer #(.Bits(32)) multiplexer_2 (
    .sel(dmac_1_p19[1]), .in_0(dmac_1_p10), .in_1(dmac_1_p16), .out({multiplexer_2_out_2, multiplexer_2_out}));
  Multiplexer #(.Bits(32)) multiplexer_3 (
    .sel(dmac_1_p19[1]), .in_0(dmac_1_p11), .in_1(dmac_1_p17), .out(multiplexer_3_out));
  Multiplexer #(.Bits(2)) multiplexer_4 (
    .sel(dmac_1_p19[1]), .in_0(dmac_1_p13), .in_1(dmac_1_p19), .out(multiplexer_4_out));
  // Probe on dmac_1_p5
  ALU alu_1 (
    .aluop(microp_controller_1_aluop), .x(prealu_1_x), .y(prealu_1_y),
    .aluR({dmac_1_p1[31:10], dmac_1_p1_2, dmac_1_p1[1:0]}));
  or or_1 (clk, clk_INT, break_q);
  Comparator #(.Bits(24)) comparator_1 (.a(multiplexer_2_out_2), .b({24{1'b0}}), .gt(comparator_1_gt));  // open: eq, lt
  Demultiplexer #(.Bits(32)) demultiplexer_1 (
    .sel(comparator_1_gt), .in({multiplexer_2_out_2, multiplexer_2_out}),
    .out_0({demultiplexer_1_out_0_2, demultiplexer_1_out_0}), .out_1(demultiplexer_1_out_1));
  Demultiplexer #(.Bits(32)) demultiplexer_2 (
    .sel(comparator_1_gt), .in(multiplexer_3_out), .out_0(demultiplexer_2_out_0),
    .out_1(demultiplexer_2_out_1));
  Demultiplexer #(.Bits(2)) demultiplexer_3 (
    .sel(comparator_1_gt), .in(multiplexer_4_out), .out_0(demultiplexer_3_out_0),
    .out_1(demultiplexer_3_out_1));
  Demultiplexer demultiplexer_4 (
    .sel(dmac_1_p19[1]), .in(multiplexer_5_out), .out_0(demultiplexer_4_out_0), .out_1(dmac_1_p6));
  Demultiplexer #(.Bits(32)) demultiplexer_5 (
    .sel(dmac_1_p19[1]), .in(multiplexer_6_out), .out_0(demultiplexer_5_out_0), .out_1(dmac_1_p5));
  or or_2 (or_2_out, reset, \int );
  // Probe on demultiplexer_1_out_1
  // Probe on demultiplexer_2_out_1
  Multiplexer multiplexer_5 (
    .sel(comparator_1_gt), .in_0(demultiplexer_3_out_0[1]), .in_1(demultiplexer_3_out_1[1]),
    .out(multiplexer_5_out));
  // Probe on d_ff_1_q
  // Probe on RAM_L_d
  Multiplexer #(.Bits(32)) multiplexer_6 (
    .sel(comparator_1_gt), .in_0(RAM_L_d), .in_1(d_ff_1_q), .out(multiplexer_6_out));
  preMW premw_1 (.rs2(regs_db), .sel(microp_controller_1_wsel), .mwData(premw_1_mwdata));
  HALT halt_1 (.mw(mw), .mr(mr), .clk(clk), .EN(EN), .memw(memw));
  and and_1 (and_1_out, or_2_out, clk_INT);
  // Probe on {demultiplexer_1_out_0_2, demultiplexer_1_out_0}
  // Probe on demultiplexer_2_out_0
  and and_2 (and_2_out, demultiplexer_3_out_1[1], comparator_1_gt);
  and and_3 (and_3_out, memw, dmac_1_p1[10]);
  ROM #(.AddrBits(8), .Bits(32)) Drom (.A(dmac_1_p1_2), .sel(1'b1), .D(Drom_d));
  RAMDualPort #(.AddrBits(8), .Bits(32)) Dram (
    .A(dmac_1_p1_2), .Din(premw_1_mwdata), .str(and_3_out), .C(clk), .ld(1'b1), .D(Dram_d));
  and and_4 (and_4_out, demultiplexer_3_out_0[0], demultiplexer_3_out_0[1]);
  Multiplexer #(.Bits(32)) multiplexer_7 (.sel(dmac_1_p1[10]), .in_0(Drom_d), .in_1(Dram_d), .out(multiplexer_7_out));
  D_FF_AS \break  (.Set(1'b0), .D(brk), .C(clk), .Clr(and_1_out), .Q(break_q));  // open: nQ
  RAMDualPort #(.AddrBits(8), .Bits(32)) RAM_L (
    .A(demultiplexer_1_out_0), .Din(demultiplexer_2_out_0), .str(and_4_out), .C(clk_INT),
    .ld(demultiplexer_3_out_0[1]), .D(RAM_L_d));
  D_FF #(.Bits(32)) d_ff_1 (.D(IN_dev), .C(and_2_out), .Q(d_ff_1_q));  // open: nQ

  // Notes on the sheet:
  //   clock: Hz: 2
  //   contents of Irom (hex, n*v repeats v):
  //   3800293,30529073,10000293,32829073,100293,32929073,4f200513,32651073,8000313,431313,
  //   30431073,30045073,10500073,ffdff0ef,30001073,35009073,327025f3,58863,100293,3262a073,
  //   8000ef,32601073,350020f3,30045073,200073
  //   interconnect
  //   WE/CYCSTB
  //   ADR
  //   DATo
  //   ACK
  //   DATi
  //   wishbone device0
  //   wishbone device1
  //   contents of Drom (hex, n*v repeats v):
  //   0,fffff0b7,400093,40016f,158513,feb50fe3,fff20193,318233,308023,309023,30a023,40a223,
  //   402383,800403,801403,804403,805403,802403,ff3a413,ffe3b413,fff44413,247493,249513,
  //   1f4d593,25d593,40125613,40460633,c616b3,c42733,c43733,864733,e6d7b3,40f75733,d77733,
  //   c76833,200713,11d873,11d873,810f3,710f3,a973,25973,1039f3,10f9f3,e7
endmodule
