// Digital circuit CSR.dig as structural Verilog
module CSR (
  input  [31:0] aluR,
  input  [11:0] csrAddr,
  input  [31:0] mepc,
  input  clk,
  input  W_EN,
  input  EN,
  input  mret,
  input  ExInt,
  input  [31:0] IOdata,
  output [31:0] csrData,
  output INT,
  output [31:0] ISR,
  output [31:0] test_1,
  output [31:0] test_2
);

  wire and_1_out, and_2_out, and_3_out, and_4_out, and_5_out, and_6_out, and_7_out, and_8_out, and_9_out,
       and_10_out, and_11_out, comparator_1_eq, comparator_2_eq, comparator_3_eq, comparator_4_eq,
       comparator_5_eq, comparator_6_eq, comparator_7_eq, Dc1_nq, Dc2_q, Dc3_q, E_int, MEIE, mepc_eq, MIE,
       mip_eq, not_1_out, or_1_out, or_2_out, priorityencoder_1_any, Rc1_q, T_int, TimeInt_eq;
  wire [2:0] priorityencoder_1_num;
  wire [11:7] mip;
  wire [31:0] CSR_RAM_d, CSR_ROM_d, mie_t, mstatus, multiplexer_1_out;

  Comparator #(.Bits(4)) comparator_1 (.a(csrAddr[11:8]), .b(4'b0011), .eq(comparator_1_eq));  // open: gt, lt
  Comparator #(.Bits(8)) comparator_2 (.a(csrAddr[7:0]), .b(8'h6), .eq(comparator_2_eq));  // open: gt, lt
  Comparator #(.Bits(8)) comparator_3 (.a(csrAddr[7:0]), .b(8'h5), .eq(comparator_3_eq));  // open: gt, lt
  Comparator #(.Bits(8)) comparator_4 (.a(csrAddr[7:0]), .b(8'h4), .eq(comparator_4_eq));  // open: gt, lt
  Comparator #(.Bits(8)) comparator_5 (.a(csrAddr[7:0]), .b({8{1'b0}}), .eq(comparator_5_eq));  // open: gt, lt
  Comparator #(.Bits(8)) u_mip (.a(csrAddr[7:0]), .b(8'h44), .eq(mip_eq));  // open: gt, lt
  Comparator #(.Bits(8)) u_mepc (.a(csrAddr[7:0]), .b(8'h41), .eq(mepc_eq));  // open: gt, lt
  Comparator #(.Bits(8)) comparator_6 (.a(csrAddr[11:4]), .b(8'hf1), .eq(comparator_6_eq));  // open: gt, lt
  and and_1 (and_1_out, comparator_1_eq, comparator_2_eq);
  and and_2 (and_2_out, comparator_1_eq, comparator_3_eq);
  and and_3 (and_3_out, comparator_1_eq, comparator_4_eq);
  and and_4 (and_4_out, comparator_1_eq, comparator_5_eq);
  and and_5 (and_5_out, comparator_1_eq, mip_eq);
  and and_6 (and_6_out, comparator_1_eq, mepc_eq);
  Comparator #(.Bits(8)) comparator_7 (.a(csrAddr[11:4]), .b(8'h35), .eq(comparator_7_eq));  // open: gt, lt
  // Probe on csrAddr[3:0]
  and and_7 (and_7_out, comparator_7_eq, W_EN);
  and and_8 (and_8_out, and_1_out, W_EN);
  and and_9 (and_9_out, and_2_out, W_EN);
  and and_10 (and_10_out, and_3_out, W_EN);
  and and_11 (and_11_out, and_4_out, W_EN);
  PriorityEncoder #(.Selector_Bits(3)) priorityencoder_1 (
    .in0(and_1_out), .in1(and_2_out), .in2(and_3_out), .in3(and_4_out), .in4(and_5_out), .in5(and_6_out),
    .in6(comparator_7_eq), .in7(comparator_6_eq), .num(priorityencoder_1_num), .any(priorityencoder_1_any));
  RAMDualPort #(.AddrBits(4), .Bits(32)) CSR_RAM (
    .A(csrAddr[3:0]), .Din(aluR), .str(and_7_out), .C(clk), .ld(1'b1), .D(CSR_RAM_d));
  not not_1 (not_1_out, priorityencoder_1_any);
  ROM #(.AddrBits(4), .Bits(32)) CSR_ROM (.A(csrAddr[3:0]), .sel(1'b1), .D(CSR_ROM_d));
  Register #(.Bits(32)) mtimecmp (.D(aluR), .C(clk), .en(and_8_out), .Q(test_2));
  Register #(.Bits(32)) mtvec (.D(aluR), .C(clk), .en(and_9_out), .Q(ISR));
  Register #(.Bits(32)) u_mie (.D(aluR), .C(clk), .en(and_10_out), .Q({mie_t[31:12], MEIE, mie_t[10:0]}));
  Register #(.Bits(32)) u_mstatus (.D(aluR), .C(clk), .en(and_11_out), .Q({mstatus[31:4], MIE, mstatus[2:0]}));
  // Probe on priorityencoder_1_num
  Multiplexer #(.Selector_Bits(3), .Bits(32)) multiplexer_1 (
    .sel(priorityencoder_1_num), .in_0(test_2), .in_1(ISR), .in_2({mie_t[31:12], MEIE, mie_t[10:0]}),
    .in_3({mstatus[31:4], MIE, mstatus[2:0]}), .in_4({{20{1'b0}}, mip[11], 3'b000, mip[7], {7{1'b0}}}),
    .in_5(mepc), .in_6(CSR_RAM_d), .in_7(CSR_ROM_d), .out(multiplexer_1_out));
  // Probe on CSR_RAM_d
  // Probe on CSR_ROM_d
  // Probe on test_2
  // Probe on multiplexer_1_out
  Multiplexer #(.Bits(32)) multiplexer_2 (.sel(not_1_out), .in_0(multiplexer_1_out), .in_1(IOdata), .out(csrData));
  D_FF_AS Dc2 (.Set(1'b0), .D(1'b1), .C(ExInt), .Clr(or_1_out), .Q(Dc2_q));  // open: nQ
  CounterPreset #(.Bits(32)) mtime (
    .en(EN), .C(clk), .dir(1'b0), .in({32{1'b0}}), .ld(1'b0), .clr(~mie_t[7]), .out(test_1));  // open: ovf
  or or_1 (or_1_out, ~MEIE, Dc3_q);  // Or
  // Probe on test_1
  Comparator #(.Bits(32)) TimeInt (.a(test_1), .b(test_2), .eq(TimeInt_eq));  // open: gt, lt
  and and_12 (INT, or_2_out, MIE, Dc1_nq);
  Register Rc1 (.D(INT), .C(clk), .en(EN), .Q(Rc1_q));
  Register Rc2 (.D(T_int), .C(clk), .en(INT), .Q(mip[7]));
  Register Rc3 (.D(E_int), .C(clk), .en(INT), .Q(mip[11]));
  Register Rc4 (.D(Dc2_q), .C(clk), .en(EN), .Q(E_int));
  D_FF_AS Dc1 (.Set(Rc1_q), .D(1'b0), .C(1'b0), .Clr(mret), .nQ(Dc1_nq));  // open: Q
  D_FF Dc3 (.D(E_int), .C(~clk), .Q(Dc3_q));  // open: nQ
  and and_13 (T_int, TimeInt_eq, mie_t[7]);
  or or_2 (or_2_out, E_int, T_int);

  // Other names for the same wires on the sheet: addr[11:0] = csrAddr; Din[31:0] = aluR; Dout[31:0] = csrData;
  //   Ex = ExInt; IO_data[31:0] = IOdata; MTIE = mie_t[7]; mie_t[11] = MEIE; mstatus[3] = MIE; mtcmp[31:0] = test_2;
  //   we = W_EN

  // Notes on the sheet:
  //   CSR_ROM loads instruction_monocycle.hex
endmodule
