// Digital circuit mono-CPU.dig as structural Verilog
module mono_CPU (
  input  clock,
  input  hand,
  input  model,
  input  reset,
  input  [31:0] IN,
  output [31:0] \time ,
  output [31:0] mtcmp,
  output [31:0] OUT
);

  wire and_1_out, and_2_out, and_3_out, and_4_out, and_5_out, and_6_out, and_7_out, break_q, brk,
       button_1_out, clk, clk_INT, comparator_1_eq, csrw, EN, \int , memw, mr, mret, mw, or_2_out, regw,
       undriven_4, undriven_5;
  wire [1:0] mono_controller_1_pcsel, undriven_3;
  wire [2:0] mono_controller_1_wsel;
  wire [3:0] mono_controller_1_aluop, mono_controller_1_alusel;
  wire [4:0] Irom_d_2, Irom_d_3;
  wire [7:0] alu_1_alur_2, undriven, undriven_6, undriven_7;
  wire [8:0] branch_pc_1_pc_2;
  wire [11:0] Irom_d_4;
  wire [14:0] Irom_d;
  wire [15:0] RAM_H_d;
  wire [23:0] undriven_2;
  wire [31:0] alu_1_alur, branch_pc_1_mepc, branch_pc_1_pc, csr_1_csrdata, csr_1_isr, Dram_d, Drom_d,
       multiplexer_2_out, prealu_1_x, prealu_1_y, premw_1_mwdata, prerw_1_rwdata, regs_da, regs_db,
       undriven_8;

  // Probe on {Irom_d_4, Irom_d_3, Irom_d[14:12], Irom_d_2, Irom_d[6:0]}
  branch_PC branch_pc_1 (
    .pcsel(mono_controller_1_pcsel), .ins_pc({Irom_d_4, Irom_d_3, Irom_d[14:12], Irom_d_2, Irom_d[6:0]}),
    .mret(mret), .clk(clk), .EN(EN), .INT(\int ), .bxx(alu_1_alur[0]), .ISR(csr_1_isr), .rs1(regs_da),
    .pc({branch_pc_1_pc[31:11], branch_pc_1_pc_2, branch_pc_1_pc[1:0]}), .mepc(branch_pc_1_mepc));
  Button button_1 (.out(button_1_out));
  CSR csr_1 (
    .aluR({alu_1_alur[31:10], alu_1_alur_2, alu_1_alur[1:0]}), .csrAddr(Irom_d_4), .mepc(branch_pc_1_mepc),
    .clk(clk_INT), .W_EN(csrw), .EN(EN), .mret(mret), .ExInt(button_1_out), .IOdata(undriven_8),
    .csrData(csr_1_csrdata), .INT(\int ), .ISR(csr_1_isr), .test_1(\time ), .test_2(mtcmp));
  wishbone_BUS wishbone_bus_1 (
    .aluR({alu_1_alur[31:10], alu_1_alur_2, alu_1_alur[1:0]}), .csrAddr(Irom_d_4), .clk(clk_INT),
    .W_EN(csrw), .IN0(IN), .DAT_I({{16{1'b0}}, RAM_H_d}), .ACK_I(and_1_out));  // open: ioData, OUT, ADR_O, DAT_O, WE_O, CYCSTB_O, SEL_O
  mono_controller mono_controller_1 (
    .ins({Irom_d_4, Irom_d_3, Irom_d[14:12], Irom_d_2, Irom_d[6:0]}), .pcsel(mono_controller_1_pcsel),
    .aluop(mono_controller_1_aluop), .alusel(mono_controller_1_alusel), .wsel(mono_controller_1_wsel),
    .rw(regw), .brk(brk), .csrw(csrw), .mw(mw), .mr(mr), .mret(mret));
  // Probe on {branch_pc_1_pc[31:11], branch_pc_1_pc_2, branch_pc_1_pc[1:0]}
  RegisterFile #(.AddrBits(5), .Bits(32)) regs (
    .Din(prerw_1_rwdata), .we(regw), .Rw(Irom_d_2), .C(clk), .Ra(Irom_d_3), .Rb(Irom_d_4[4:0]), .Da(regs_da),
    .Db(regs_db));
  ROM #(.AddrBits(9), .Bits(32)) Irom (
    .A(branch_pc_1_pc_2), .sel(1'b1), .D({Irom_d_4, Irom_d_3, Irom_d[14:12], Irom_d_2, Irom_d[6:0]}));
  // Probe on {alu_1_alur[31:10], alu_1_alur_2, alu_1_alur[1:0]}
  Comparator #(.Bits(24)) comparator_1 (.a(undriven_2), .b({24{1'b0}}), .eq(comparator_1_eq));  // open: gt, lt
  preALU prealu_1 (
    .alusel(mono_controller_1_alusel),
    .pc_alu({branch_pc_1_pc[31:11], branch_pc_1_pc_2, branch_pc_1_pc[1:0]}),
    .ins_alu({Irom_d_4, Irom_d_3, Irom_d[14:12], Irom_d_2, Irom_d[6:0]}), .rs1(regs_da), .rs2(regs_db),
    .csrData(csr_1_csrdata), .x(prealu_1_x), .y(prealu_1_y));
  // Probe on csr_1_csrdata
  and and_1 (and_1_out, undriven_4, comparator_1_eq);
  preRW prerw_1 (
    .sel(mono_controller_1_wsel), .aluR({alu_1_alur[31:10], alu_1_alur_2, alu_1_alur[1:0]}),
    .csrData(csr_1_csrdata), .ramData(multiplexer_2_out), .rwData(prerw_1_rwdata));
  Multiplexer multiplexer_1 (.sel(model), .in_0(hand), .in_1(clock), .out(clk_INT));
  ALU alu_1 (
    .aluop(mono_controller_1_aluop), .x(prealu_1_x), .y(prealu_1_y),
    .aluR({alu_1_alur[31:10], alu_1_alur_2, alu_1_alur[1:0]}));
  or or_1 (clk, clk_INT, break_q);
  and and_2 (and_2_out, undriven_5, and_3_out);
  and and_3 (and_3_out, and_1_out, undriven_3[0]);
  and and_4 (and_4_out, and_1_out, undriven_3[1]);
  or or_2 (or_2_out, reset, \int );
  and and_5 (and_5_out, undriven_5, and_4_out);
  preMW premw_1 (.rs2(regs_db), .sel(mono_controller_1_wsel), .mwData(premw_1_mwdata));
  HALT halt_1 (.mw(mw), .mr(mr), .clk(clk), .EN(EN), .memw(memw));
  and and_6 (and_6_out, or_2_out, clk_INT);
  and and_7 (and_7_out, memw, alu_1_alur[10]);
  ROM #(.AddrBits(8), .Bits(32)) Drom (.A(alu_1_alur_2), .sel(1'b1), .D(Drom_d));
  RAMDualPort #(.AddrBits(8), .Bits(32)) Dram (
    .A(alu_1_alur_2), .Din(premw_1_mwdata), .str(and_7_out), .C(clk), .ld(1'b1), .D(Dram_d));
  D_FF_AS \break  (.Set(1'b0), .D(brk), .C(clk), .Clr(and_6_out), .Q(break_q));  // open: nQ
  RAMDualPort #(.AddrBits(8), .Bits(8)) RAM_L (
    .A(undriven), .Din(undriven_6), .str(and_2_out), .C(clk), .ld(and_3_out), .D(RAM_H_d[7:0]));
  RAMDualPort #(.AddrBits(8), .Bits(8)) RAM_H (
    .A(undriven), .Din(undriven_7), .str(and_5_out), .C(clk), .ld(and_4_out), .D(RAM_H_d[15:8]));
  Multiplexer #(.Bits(32)) multiplexer_2 (.sel(alu_1_alur[10]), .in_0(Drom_d), .in_1(Dram_d), .out(multiplexer_2_out));

  // Notes on the sheet:
  //   clock: Hz: 2
  //   contents of Irom (hex, n*v repeats v):
  //   3000293,30529073,1000493,30649073,8000313,30431073,431313,30432073,30045073,13,10500073,
  //   ff9ff0ef,30001073,35009073,35129073,35231073,344022f3,18000ef,350020f3,351022f3,35202373,
  //   30045073,200073,b2d313,30c63,33002373,fff34313,33031073,fff34313,33031073,72d313,
  //   137313,2030063,1048493,30649073,330022f3,1f2d293,12b293,1f29293,33029073,80e7
  //   wishbone device
  //   contents of Drom (hex, n*v repeats v):
  //   0,fffff0b7,400093,40016f,158513,feb50fe3,fff20193,318233,308023,309023,30a023,40a223,
  //   402383,800403,801403,804403,805403,802403,ff3a413,ffe3b413,fff44413,247493,249513,
  //   1f4d593,25d593,40125613,40460633,c616b3,c42733,c43733,864733,e6d7b3,40f75733,d77733,
  //   c76833,200713,11d873,11d873,810f3,710f3,a973,25973,1039f3,10f9f3,e7
endmodule
