// Digital circuit preMW.dig as structural Verilog
module preMW (
  input  [31:0] rs2,
  input  [2:0] sel,
  output [31:0] mwData
);

  Multiplexer #(.Selector_Bits(2), .Bits(32)) multiplexer_1 (
    .sel(sel[1:0]), .in_0({{24{1'b0}}, rs2[7:0]}), .in_1({{16{1'b0}}, rs2[15:0]}), .in_2(rs2),
    .in_3({32{1'b0}}), .out(mwData));

  // Other names for the same wires on the sheet: memD[31:0] = mwData
endmodule
