// Digital circuit wishbone BUS.dig as structural Verilog
module wishbone_BUS (
  input  [31:0] aluR,
  input  [11:0] csrAddr,
  input  clk,
  input  W_EN,
  input  [31:0] IN0,
  input  [31:0] DAT_I,
  input  ACK_I,
  output [31:0] ioData,
  output [31:0] OUT,
  output [31:0] ADR_O,
  output [31:0] DAT_O,
  output WE_O,
  output CYCSTB_O,
  output [3:0] SEL_O
);

  wire and_1_out, and_2_out, and_3_out, and_4_out, and_5_out, and_6_out, and_7_out, and_8_out,
       comparator_1_eq, comparator_2_eq, comparator_3_eq, comparator_4_eq, comparator_5_eq, comparator_6_eq,
       comparator_7_eq, comparator_8_eq;
  wire [2:0] priorityencoder_1_num;
  wire [31:0] DATin;
  wire [31:2] wConfig;

  Comparator #(.Bits(4)) comparator_1 (.a(csrAddr[11:8]), .b(4'b0011), .eq(comparator_1_eq));  // open: gt, lt
  Comparator #(.Bits(8)) comparator_2 (.a(csrAddr[7:0]), .b(8'h30), .eq(comparator_2_eq));  // open: gt, lt
  Comparator #(.Bits(8)) comparator_3 (.a(csrAddr[7:0]), .b(8'h3f), .eq(comparator_3_eq));  // open: gt, lt
  Comparator #(.Bits(8)) comparator_4 (.a(csrAddr[7:0]), .b(8'h21), .eq(comparator_4_eq));  // open: gt, lt
  Comparator #(.Bits(8)) comparator_5 (.a(csrAddr[7:0]), .b(8'h22), .eq(comparator_5_eq));  // open: gt, lt
  Comparator #(.Bits(8)) comparator_6 (.a(csrAddr[7:0]), .b(8'h23), .eq(comparator_6_eq));  // open: gt, lt
  Comparator #(.Bits(8)) comparator_7 (.a(csrAddr[7:0]), .b(8'h24), .eq(comparator_7_eq));  // open: gt, lt
  Comparator #(.Bits(8)) comparator_8 (.a(csrAddr[7:0]), .b(8'h25), .eq(comparator_8_eq));  // open: gt, lt
  and and_1 (and_1_out, comparator_1_eq, W_EN, comparator_2_eq);
  and and_2 (and_2_out, comparator_1_eq, W_EN, comparator_3_eq);
  and and_3 (and_3_out, comparator_1_eq, W_EN, comparator_4_eq);
  and and_4 (and_4_out, comparator_1_eq, W_EN, comparator_5_eq);
  and and_5 (and_5_out, comparator_1_eq, W_EN, comparator_6_eq);
  and and_6 (and_6_out, comparator_1_eq, W_EN, comparator_7_eq);
  and and_7 (and_7_out, comparator_1_eq, W_EN, comparator_8_eq);
  Register #(.Bits(32)) u_out (.D(aluR), .C(clk), .en(and_1_out), .Q(OUT));
  // Probe on OUT
  Register #(.Bits(32)) Config (
    .D(aluR), .C(clk), .en(and_3_out), .Q({wConfig[31:8], SEL_O, wConfig[3:2], WE_O, CYCSTB_O}));
  Register #(.Bits(32)) ADDR (.D(aluR), .C(clk), .en(and_4_out), .Q(ADR_O));
  Register #(.Bits(32)) DATAo (.D(aluR), .C(clk), .en(and_5_out), .Q(DAT_O));
  PriorityEncoder #(.Selector_Bits(3)) priorityencoder_1 (
    .in0(1'b0), .in1(and_1_out), .in2(and_2_out), .in3(and_3_out), .in4(and_4_out), .in5(and_5_out),
    .in6(and_6_out), .in7(and_7_out), .num(priorityencoder_1_num));  // open: any
  Register #(.Bits(32)) DATAin (.D(DAT_I), .C(clk), .en(and_8_out), .Q(DATin));
  and and_8 (and_8_out, ACK_I, CYCSTB_O, ~WE_O);  // And
  Multiplexer #(.Selector_Bits(3), .Bits(32)) multiplexer_1 (
    .sel(priorityencoder_1_num), .in_0({32{1'b0}}), .in_1(OUT), .in_2(IN0),
    .in_3({wConfig[31:8], SEL_O, wConfig[3:2], WE_O, CYCSTB_O}), .in_4(ADR_O), .in_5(DAT_O), .in_6(DATin),
    .in_7({{31{1'b0}}, ACK_I}), .out(ioData));
  // Probe on priorityencoder_1_num
  // Probe on ioData

  // Other names for the same wires on the sheet: wStatus[0] = ACK_I; addr[11:0] = csrAddr; ADRout[31:0] = ADR_O;
  //   DATout[31:0] = DAT_O; Din[31:0] = aluR; Dout[31:0] = ioData; IN_0[31:0] = IN0; out0[31:0] = OUT;
  //   wConfig (some bits) = {SEL_O, WE_O, CYCSTB_O}; we = W_EN
endmodule
