// Digital circuit circular_cordic.dig as structural Verilog
module circular_cordic (
  input  [8:0] X_0,
  input  [8:0] Y_0,
  input  [8:0] Z_0,
  input  nR_V,
  output [8:0] Y_N,
  output [8:0] Z_N,
  output [8:0] X_N
);

  wire [8:0] circular_order_1_x_n, circular_order_1_y_n, circular_order_1_z_n, circular_order_2_x_n,
       circular_order_2_y_n, circular_order_2_z_n, circular_order_3_x_n, circular_order_3_y_n,
       circular_order_3_z_n, circular_order_4_x_n, circular_order_4_y_n, circular_order_4_z_n,
       circular_order_5_x_n, circular_order_5_y_n, circular_order_5_z_n, circular_order_6_x_n,
       circular_order_6_y_n, circular_order_6_z_n, circular_order_7_x_n, circular_order_7_y_n,
       circular_order_7_z_n;

  circular_order circular_order_1 (
    .x(X_0), .y(Y_0), .z(Z_0), .e_k(8'h80), .order(4'b0000), .dk(nR_V), .x_n(circular_order_1_x_n),
    .y_n(circular_order_1_y_n), .z_n(circular_order_1_z_n));
  // Probe on circular_order_1_x_n
  // Probe on circular_order_1_y_n
  // Probe on circular_order_1_z_n
  circular_order circular_order_2 (
    .x(circular_order_1_x_n), .y(circular_order_1_y_n), .z(circular_order_1_z_n), .e_k(8'h4b),
    .order(4'b0001), .dk(nR_V), .x_n(circular_order_2_x_n), .y_n(circular_order_2_y_n),
    .z_n(circular_order_2_z_n));
  // Probe on circular_order_2_x_n
  // Probe on circular_order_2_y_n
  // Probe on circular_order_2_z_n
  circular_order circular_order_3 (
    .x(circular_order_2_x_n), .y(circular_order_2_y_n), .z(circular_order_2_z_n), .e_k(8'h28),
    .order(4'b0010), .dk(nR_V), .x_n(circular_order_3_x_n), .y_n(circular_order_3_y_n),
    .z_n(circular_order_3_z_n));
  // Probe on circular_order_3_x_n
  // Probe on circular_order_3_y_n
  // Probe on circular_order_3_z_n
  circular_order circular_order_4 (
    .x(circular_order_3_x_n), .y(circular_order_3_y_n), .z(circular_order_3_z_n), .e_k(8'h14),
    .order(4'b0011), .dk(nR_V), .x_n(circular_order_4_x_n), .y_n(circular_order_4_y_n),
    .z_n(circular_order_4_z_n));
  // Probe on circular_order_4_x_n
  // Probe on circular_order_4_y_n
  // Probe on circular_order_4_z_n
  circular_order circular_order_5 (
    .x(circular_order_4_x_n), .y(circular_order_4_y_n), .z(circular_order_4_z_n), .e_k(8'ha),
    .order(4'b0100), .dk(nR_V), .x_n(circular_order_5_x_n), .y_n(circular_order_5_y_n),
    .z_n(circular_order_5_z_n));
  // Probe on circular_order_5_x_n
  // Probe on circular_order_5_y_n
  // Probe on circular_order_5_z_n
  circular_order circular_order_6 (
    .x(circular_order_5_x_n), .y(circular_order_5_y_n), .z(circular_order_5_z_n), .e_k(8'h5),
    .order(4'b0101), .dk(nR_V), .x_n(circular_order_6_x_n), .y_n(circular_order_6_y_n),
    .z_n(circular_order_6_z_n));
  // Probe on circular_order_6_x_n
  // Probe on circular_order_6_y_n
  // Probe on circular_order_6_z_n
  circular_order circular_order_7 (
    .x(circular_order_6_x_n), .y(circular_order_6_y_n), .z(circular_order_6_z_n), .e_k(8'h3),
    .order(4'b0110), .dk(nR_V), .x_n(circular_order_7_x_n), .y_n(circular_order_7_y_n),
    .z_n(circular_order_7_z_n));
  // Probe on circular_order_7_x_n
  // Probe on circular_order_7_y_n
  // Probe on circular_order_7_z_n
  circular_order circular_order_8 (
    .x(circular_order_7_x_n), .y(circular_order_7_y_n), .z(circular_order_7_z_n), .e_k(8'h1),
    .order(4'b0111), .dk(nR_V), .x_n(X_N), .y_n(Y_N), .z_n(Z_N));
endmodule
