// Digital circuit circular_order.dig as structural Verilog
module circular_order (
  input  [8:0] x,
  input  [8:0] y,
  input  [8:0] z,
  input  [7:0] e_k,
  input  [3:0] order,
  input  dk,
  output [8:0] x_n,
  output [8:0] y_n,
  output [8:0] z_n
);

  wire multiplexer_1_out, multiplexer_2_out, multiplexer_3_out, not_1_out, not_2_out, not_3_out;
  wire [8:0] add_1_s, add_2_s, add_3_s, barrelshifter_1_out, barrelshifter_2_out, sub_1_s, sub_2_s, sub_3_s;

  BarrelShifter #(.Bits(9), .barrelShifterMode("arithmetic"), .direction("right")) barrelshifter_1 (
    .in(x), .shift(order), .out(barrelshifter_1_out));
  BarrelShifter #(.Bits(9), .barrelShifterMode("arithmetic"), .direction("right")) barrelshifter_2 (
    .in(y), .shift(order), .out(barrelshifter_2_out));
  Multiplexer multiplexer_1 (.sel(dk), .in_0(not_1_out), .in_1(y[8]), .out(multiplexer_1_out));
  not not_1 (not_1_out, z[8]);
  Add #(.Bits(9)) add_1 (.a(z), .b({1'b0, e_k}), .c_i(1'b0), .s(add_1_s));  // open: c_o
  Sub #(.Bits(9)) sub_1 (.a(z), .b({1'b0, e_k}), .c_i(1'b0), .s(sub_1_s));  // open: c_o
  Multiplexer multiplexer_2 (.sel(dk), .in_0(z[8]), .in_1(not_2_out), .out(multiplexer_2_out));
  not not_2 (not_2_out, y[8]);
  Add #(.Bits(9)) add_2 (.a(y), .b(barrelshifter_1_out), .c_i(1'b0), .s(add_2_s));  // open: c_o
  Sub #(.Bits(9)) sub_2 (.a(y), .b(barrelshifter_1_out), .c_i(1'b0), .s(sub_2_s));  // open: c_o
  Multiplexer multiplexer_3 (.sel(dk), .in_0(not_3_out), .in_1(y[8]), .out(multiplexer_3_out));
  not not_3 (not_3_out, z[8]);
  Add #(.Bits(9)) add_3 (.a(x), .b(barrelshifter_2_out), .c_i(1'b0), .s(add_3_s));  // open: c_o
  Sub #(.Bits(9)) sub_3 (.a(x), .b(barrelshifter_2_out), .c_i(1'b0), .s(sub_3_s));  // open: c_o
  Multiplexer #(.Bits(9)) multiplexer_4 (.sel(multiplexer_1_out), .in_0(add_1_s), .in_1(sub_1_s), .out(z_n));
  Multiplexer #(.Bits(9)) multiplexer_5 (.sel(multiplexer_2_out), .in_0(add_2_s), .in_1(sub_2_s), .out(y_n));
  Multiplexer #(.Bits(9)) multiplexer_6 (.sel(multiplexer_3_out), .in_0(add_3_s), .in_1(sub_3_s), .out(x_n));
endmodule
