// Digital circuit hyperbolic_cordic.dig as structural Verilog
module hyperbolic_cordic (
  input  [8:0] X_0,
  input  [8:0] Y_0,
  input  [8:0] Z_0,
  input  nR_V,
  output [8:0] Y_N,
  output [8:0] Z_N,
  output [8:0] X_N
);

  wire [8:0] hyperbolic_order_1_x_n, hyperbolic_order_1_y_n, hyperbolic_order_1_z_n, hyperbolic_order_2_x_n,
       hyperbolic_order_2_y_n, hyperbolic_order_2_z_n, hyperbolic_order_3_x_n, hyperbolic_order_3_y_n,
       hyperbolic_order_3_z_n, hyperbolic_order_4_x_n, hyperbolic_order_4_y_n, hyperbolic_order_4_z_n,
       hyperbolic_order_5_x_n, hyperbolic_order_5_y_n, hyperbolic_order_5_z_n, hyperbolic_order_6_x_n,
       hyperbolic_order_6_y_n, hyperbolic_order_6_z_n, hyperbolic_order_7_x_n, hyperbolic_order_7_y_n,
       hyperbolic_order_7_z_n, hyperbolic_order_8_x_n, hyperbolic_order_8_y_n, hyperbolic_order_8_z_n;

  hyperbolic_order hyperbolic_order_1 (
    .x(X_0), .y(Y_0), .z(Z_0), .e_k(8'h46), .order(4'b0001), .dk(nR_V), .x_n(hyperbolic_order_1_x_n),
    .y_n(hyperbolic_order_1_y_n), .z_n(hyperbolic_order_1_z_n));
  // Probe on hyperbolic_order_1_x_n
  // Probe on hyperbolic_order_1_y_n
  // Probe on hyperbolic_order_1_z_n
  hyperbolic_order hyperbolic_order_2 (
    .x(hyperbolic_order_1_x_n), .y(hyperbolic_order_1_y_n), .z(hyperbolic_order_1_z_n), .e_k(8'h20),
    .order(4'b0010), .dk(nR_V), .x_n(hyperbolic_order_2_x_n), .y_n(hyperbolic_order_2_y_n),
    .z_n(hyperbolic_order_2_z_n));
  // Probe on hyperbolic_order_2_x_n
  // Probe on hyperbolic_order_2_y_n
  // Probe on hyperbolic_order_2_z_n
  hyperbolic_order hyperbolic_order_3 (
    .x(hyperbolic_order_2_x_n), .y(hyperbolic_order_2_y_n), .z(hyperbolic_order_2_z_n), .e_k(8'h10),
    .order(4'b0011), .dk(nR_V), .x_n(hyperbolic_order_3_x_n), .y_n(hyperbolic_order_3_y_n),
    .z_n(hyperbolic_order_3_z_n));
  // Probe on hyperbolic_order_3_x_n
  // Probe on hyperbolic_order_3_y_n
  // Probe on hyperbolic_order_3_z_n
  hyperbolic_order hyperbolic_order_4 (
    .x(hyperbolic_order_3_x_n), .y(hyperbolic_order_3_y_n), .z(hyperbolic_order_3_z_n), .e_k(8'h8),
    .order(4'b0100), .dk(nR_V), .x_n(hyperbolic_order_4_x_n), .y_n(hyperbolic_order_4_y_n),
    .z_n(hyperbolic_order_4_z_n));
  // Probe on hyperbolic_order_4_x_n
  // Probe on hyperbolic_order_4_y_n
  // Probe on hyperbolic_order_4_z_n
  hyperbolic_order hyperbolic_order_5 (
    .x(hyperbolic_order_4_x_n), .y(hyperbolic_order_4_y_n), .z(hyperbolic_order_4_z_n), .e_k(8'h8),
    .order(4'b0100), .dk(nR_V), .x_n(hyperbolic_order_5_x_n), .y_n(hyperbolic_order_5_y_n),
    .z_n(hyperbolic_order_5_z_n));
  // Probe on hyperbolic_order_5_x_n
  // Probe on hyperbolic_order_5_y_n
  // Probe on hyperbolic_order_5_z_n
  hyperbolic_order hyperbolic_order_6 (
    .x(hyperbolic_order_5_x_n), .y(hyperbolic_order_5_y_n), .z(hyperbolic_order_5_z_n), .e_k(8'h4),
    .order(4'b0101), .dk(nR_V), .x_n(hyperbolic_order_6_x_n), .y_n(hyperbolic_order_6_y_n),
    .z_n(hyperbolic_order_6_z_n));
  // Probe on hyperbolic_order_6_x_n
  // Probe on hyperbolic_order_6_y_n
  // Probe on hyperbolic_order_6_z_n
  hyperbolic_order hyperbolic_order_7 (
    .x(hyperbolic_order_6_x_n), .y(hyperbolic_order_6_y_n), .z(hyperbolic_order_6_z_n), .e_k(8'h2),
    .order(4'b0110), .dk(nR_V), .x_n(hyperbolic_order_7_x_n), .y_n(hyperbolic_order_7_y_n),
    .z_n(hyperbolic_order_7_z_n));
  // Probe on hyperbolic_order_7_x_n
  // Probe on hyperbolic_order_7_y_n
  // Probe on hyperbolic_order_7_z_n
  hyperbolic_order hyperbolic_order_8 (
    .x(hyperbolic_order_7_x_n), .y(hyperbolic_order_7_y_n), .z(hyperbolic_order_7_z_n), .e_k(8'h1),
    .order(4'b0111), .dk(nR_V), .x_n(hyperbolic_order_8_x_n), .y_n(hyperbolic_order_8_y_n),
    .z_n(hyperbolic_order_8_z_n));
  // Probe on hyperbolic_order_8_x_n
  // Probe on hyperbolic_order_8_y_n
  // Probe on hyperbolic_order_8_z_n
  hyperbolic_order hyperbolic_order_9 (
    .x(hyperbolic_order_8_x_n), .y(hyperbolic_order_8_y_n), .z(hyperbolic_order_8_z_n), .e_k(8'h1),
    .order(4'b0111), .dk(nR_V), .x_n(X_N), .y_n(Y_N), .z_n(Z_N));
endmodule
