// Digital circuit linear_cordic.dig as structural Verilog
module linear_cordic (
  input  [8:0] X_0,
  input  [8:0] Y_0,
  input  [8:0] Z_0,
  input  nR_V,
  input  [8:0] x_r,
  input  [8:0] z_r,
  input  [8:0] y_v,
  input  [8:0] x_v,
  output [8:0] Y_N,
  output [8:0] Z_N,
  output [9:0] mul_10,
  output [8:0] q_9,
  output [8:0] r_9
);

  wire [7:0] sign_Mul_mul;
  wire [8:0] linear_order_1_y_n, linear_order_1_z_n, linear_order_2_y_n, linear_order_2_z_n,
       linear_order_3_y_n, linear_order_3_z_n, linear_order_4_y_n, linear_order_4_z_n, linear_order_5_y_n,
       linear_order_5_z_n, linear_order_6_y_n, linear_order_6_z_n, linear_order_7_y_n, linear_order_7_z_n;

  Mul #(.Signed("true"), .Bits(9)) sign_Mul (.a(x_r), .b(z_r), .mul({mul_10, sign_Mul_mul}));
  linear_order linear_order_1 (
    .x(X_0), .y(Y_0), .z(Z_0), .e_k(8'h80), .order(4'b0001), .dk(nR_V), .y_n(linear_order_1_y_n),
    .z_n(linear_order_1_z_n));
  // Probe on linear_order_1_z_n
  // Probe on linear_order_1_y_n
  linear_order linear_order_2 (
    .x(X_0), .y(linear_order_1_y_n), .z(linear_order_1_z_n), .e_k(8'h40), .order(4'b0010), .dk(nR_V),
    .y_n(linear_order_2_y_n), .z_n(linear_order_2_z_n));
  // Probe on linear_order_2_z_n
  // Probe on linear_order_2_y_n
  linear_order linear_order_3 (
    .x(X_0), .y(linear_order_2_y_n), .z(linear_order_2_z_n), .e_k(8'h20), .order(4'b0011), .dk(nR_V),
    .y_n(linear_order_3_y_n), .z_n(linear_order_3_z_n));
  // Probe on linear_order_3_z_n
  Div #(.Bits(9)) Int_Div (.a(y_v), .b(x_v), .q(q_9), .r(r_9));
  // Probe on linear_order_3_y_n
  linear_order linear_order_4 (
    .x(X_0), .y(linear_order_3_y_n), .z(linear_order_3_z_n), .e_k(8'h10), .order(4'b0100), .dk(nR_V),
    .y_n(linear_order_4_y_n), .z_n(linear_order_4_z_n));
  // Probe on linear_order_4_z_n
  // Probe on linear_order_4_y_n
  linear_order linear_order_5 (
    .x(X_0), .y(linear_order_4_y_n), .z(linear_order_4_z_n), .e_k(8'h8), .order(4'b0101), .dk(nR_V),
    .y_n(linear_order_5_y_n), .z_n(linear_order_5_z_n));
  // Probe on linear_order_5_z_n
  // Probe on linear_order_5_y_n
  linear_order linear_order_6 (
    .x(X_0), .y(linear_order_5_y_n), .z(linear_order_5_z_n), .e_k(8'h4), .order(4'b0110), .dk(nR_V),
    .y_n(linear_order_6_y_n), .z_n(linear_order_6_z_n));
  // Probe on linear_order_6_z_n
  // Probe on linear_order_6_y_n
  linear_order linear_order_7 (
    .x(X_0), .y(linear_order_6_y_n), .z(linear_order_6_z_n), .e_k(8'h2), .order(4'b0111), .dk(nR_V),
    .y_n(linear_order_7_y_n), .z_n(linear_order_7_z_n));
  // Probe on linear_order_7_z_n
  // Probe on linear_order_7_y_n
  linear_order linear_order_8 (
    .x(X_0), .y(linear_order_7_y_n), .z(linear_order_7_z_n), .e_k(8'h1), .order(4'b1000), .dk(nR_V),
    .y_n(Y_N), .z_n(Z_N));
endmodule
