// Digital circuit DDS_table.dig as structural Verilog
module DDS_table (
  input  [5:0] addr,
  input  sin_cos,
  input  [7:0] ADDR_2,
  input  Sin_Cos_2,
  output [7:0] out_4,
  output [7:0] out_6
);

  wire [1:0] add_1_s, add_2_s;
  wire [3:0] A_f_d, multiplexer_1_out, not_1_out;
  wire [5:0] multiplexer_2_out, not_2_out;
  wire [7:0] add_3_s, add_4_s, add_5_s, B_f_d, mul_1_mul, not_3_out, not_4_out, rom_1_d;

  // Probe on addr[5:4]
  // Probe on addr[3:0]
  assign not_1_out = ~addr[3:0];  // Not not_1, 4 bits wide
  Add #(.Bits(2)) add_1 (.a(addr[5:4]), .b(2'b00), .c_i(sin_cos), .s(add_1_s));  // open: c_o
  // Probe on ADDR_2[5:0]
  assign not_2_out = ~ADDR_2[5:0];  // Not not_2, 6 bits wide
  // Probe on ADDR_2[7:6]
  Add #(.Bits(2)) add_2 (.a(ADDR_2[7:6]), .b(2'b00), .c_i(Sin_Cos_2), .s(add_2_s));  // open: c_o
  Multiplexer #(.Bits(4)) multiplexer_1 (.sel(add_1_s[0]), .in_0(addr[3:0]), .in_1(not_1_out), .out(multiplexer_1_out));
  Multiplexer #(.Bits(6)) multiplexer_2 (
    .sel(add_2_s[0]), .in_0(ADDR_2[5:0]), .in_1(not_2_out), .out(multiplexer_2_out));
  // Probe on multiplexer_1_out
  ROM #(.AddrBits(4), .Bits(8)) rom_1 (.A(multiplexer_1_out), .sel(1'b1), .D(rom_1_d));
  // Probe on multiplexer_2_out
  // Probe on rom_1_d
  assign not_3_out = ~rom_1_d;  // Not not_3, 8 bits wide
  // Probe on multiplexer_2_out[5:2]
  ROM #(.AddrBits(4), .Bits(4)) A_f (.A(multiplexer_2_out[5:2]), .sel(1'b1), .D(A_f_d));
  ROM #(.AddrBits(4), .Bits(8)) B_f (.A(multiplexer_2_out[5:2]), .sel(1'b1), .D(B_f_d));
  Add #(.Bits(8)) add_3 (.a({8{1'b0}}), .b(not_3_out), .c_i(1'b1), .s(add_3_s));  // open: c_o
  // Probe on {2'b00, multiplexer_2_out[1:0]}
  // Probe on A_f_d
  // Probe on B_f_d
  Multiplexer #(.Bits(8)) multiplexer_3 (.sel(add_1_s[1]), .in_0(rom_1_d), .in_1(add_3_s), .out(out_6));
  // Probe on add_3_s
  Mul #(.Bits(4)) mul_1 (.a({2'b00, multiplexer_2_out[1:0]}), .b(A_f_d), .mul(mul_1_mul));
  Add #(.Bits(8)) add_4 (.a(mul_1_mul), .b(B_f_d), .c_i(1'b0), .s(add_4_s));  // open: c_o
  // Probe on add_4_s
  assign not_4_out = ~add_4_s;  // Not not_4, 8 bits wide
  Add #(.Bits(8)) add_5 (.a({8{1'b0}}), .b(not_4_out), .c_i(1'b1), .s(add_5_s));  // open: c_o
  Multiplexer #(.Bits(8)) multiplexer_4 (.sel(add_2_s[1]), .in_0(add_4_s), .in_1(add_5_s), .out(out_4));
  // Probe on add_5_s

  // Notes on the sheet:
  //   Table
  //   Table+Inter.
  //   contents of rom_1 (hex, n*v repeats v):
  //   0,d,1a,27,34,40,4b,55,5f,67,6e,74,79,7d,7e,7f
  //   contents of A_f (hex, n*v repeats v):
  //   3,3,3,3,3,3,2,2,2,2,1,1,1,1
  //   contents of B_f (hex, n*v repeats v):
  //   0,d,1a,27,34,40,4b,55,5f,67,6e,74,79,7d,7e,7f
endmodule
