// Digital circuit LCG.dig as structural Verilog
module LCG (
  input  [19:0] m,
  input  [19:0] c,
  input  [19:0] a,
  input  [19:0] X_0,
  input  init,
  output [19:0] out_1
);

  wire clock_out;
  wire [19:0] d_ff_1_q, multiplexer_1_out;
  wire [39:0] add_1_s, mul_1_mul;
  wire [39:20] div_1_r;

  D_FF #(.Bits(20)) d_ff_1 (.D(out_1), .C(clock_out), .Q(d_ff_1_q));  // open: nQ
  // Probe on d_ff_1_q
  Button clock (.out(clock_out));
  Multiplexer #(.Bits(20)) multiplexer_1 (.sel(init), .in_0(d_ff_1_q), .in_1(X_0), .out(multiplexer_1_out));
  Mul #(.Bits(20)) mul_1 (.a(multiplexer_1_out), .b(a), .mul(mul_1_mul));
  Add #(.Bits(40)) add_1 (.a(mul_1_mul), .b({{20{1'b0}}, c}), .c_i(1'b0), .s(add_1_s));  // open: c_o
  Div #(.Bits(40)) div_1 (.a(add_1_s), .b({{20{1'b0}}, m}), .r({div_1_r, out_1}));  // open: q
endmodule
