// Digital circuit LFSR.dig as structural Verilog
module LFSR (
  input  init,
  input  [2:0] X_0,
  output [2:0] X_n
);

  wire CLK_out, multiplexer_1_out, multiplexer_2_out, multiplexer_3_out, xor_1_out;

  Button CLK (.out(CLK_out));
  D_FF Q_1 (.D(multiplexer_1_out), .C(CLK_out), .Q(X_n[0]));  // open: nQ
  Multiplexer multiplexer_1 (.sel(init), .in_0(X_n[2]), .in_1(X_0[0]), .out(multiplexer_1_out));
  xor xor_1 (xor_1_out, X_n[2], X_n[0]);
  Multiplexer multiplexer_2 (.sel(init), .in_0(xor_1_out), .in_1(X_0[1]), .out(multiplexer_2_out));
  D_FF Q_2 (.D(multiplexer_2_out), .C(CLK_out), .Q(X_n[1]));  // open: nQ
  Multiplexer multiplexer_3 (.sel(init), .in_0(X_n[1]), .in_1(X_0[2]), .out(multiplexer_3_out));
  D_FF Q_3 (.D(multiplexer_3_out), .C(CLK_out), .Q(X_n[2]));  // open: nQ
endmodule
