// Digital circuit Newton method div.dig as structural Verilog
module Newton_method_div (
  input  [15:0] Init_16,
  input  sel,
  input  [15:0] c,
  input  [15:0] in_6,
  output [15:0] out_4,
  output [15:0] out_5
);

  wire clk_out;
  wire [15:0] d_ff_1_q, multiplexer_1_out, sub_1_s;
  wire [31:0] mul_1_mul, mul_2_mul;

  Button clk (.out(clk_out));
  D_FF #(.Bits(16)) d_ff_1 (.D(out_5), .C(clk_out), .Q(d_ff_1_q));  // open: nQ
  Div #(.Bits(16)) div_1 (.a(16'h100), .b(in_6), .q(out_4));  // open: r
  Multiplexer #(.Bits(16)) multiplexer_1 (.sel(sel), .in_0(Init_16), .in_1(d_ff_1_q), .out(multiplexer_1_out));
  // Probe on multiplexer_1_out
  Mul #(.Bits(16)) mul_1 (.a(c), .b(multiplexer_1_out), .mul(mul_1_mul));
  // Probe on mul_1_mul[23:8]
  Sub #(.Bits(16)) sub_1 (.a(16'h200), .b(mul_1_mul[23:8]), .c_i(1'b0), .s(sub_1_s));  // open: c_o
  // Probe on sub_1_s
  Mul #(.Bits(16)) mul_2 (.a(sub_1_s), .b(multiplexer_1_out), .mul({mul_2_mul[31:24], out_5, mul_2_mul[7:0]}));
endmodule
