// Digital circuit 0 check.dig as structural Verilog
module _0_check (
  input  [31:0] in,
  output [4:0] out,
  output zero
);

  PriorityEncoder #(.Selector_Bits(5)) priorityencoder_1 (
    .in0(in[0]), .in1(in[1]), .in2(in[2]), .in3(in[3]), .in4(in[4]), .in5(in[5]), .in6(in[6]), .in7(in[7]),
    .in8(in[8]), .in9(in[9]), .in10(in[10]), .in11(in[11]), .in12(in[12]), .in13(in[13]), .in14(in[14]),
    .in15(in[15]), .in16(in[16]), .in17(in[17]), .in18(in[18]), .in19(in[19]), .in20(in[20]), .in21(in[21]),
    .in22(in[22]), .in23(in[23]), .in24(in[24]), .in25(in[25]), .in26(in[26]), .in27(in[27]), .in28(in[28]),
    .in29(in[29]), .in30(in[30]), .in31(in[31]), .num(out), .any(zero));
endmodule
