// Digital circuit carmark.dig as structural Verilog
module carmark (
  input  [31:0] magic_N,
  input  [31:0] in_5,
  input  [31:0] Init,
  output [31:0] Y,
  output out_3,
  output out_4,
  output out_6,
  output out_8
);

  wire [7:0] sub_1_s;
  wire [31:0] float_adder_1_y, float_multiply_1_y, float_multiply_2_y, sub_2_s;

  Sub #(.Bits(8)) sub_1 (.a(Init[30:23]), .b(8'h1), .c_i(1'b0), .s(sub_1_s));  // open: c_o
  Sub #(.Bits(32)) sub_2 (.a(magic_N), .b({1'b0, Init[31:1]}), .c_i(1'b0), .s(sub_2_s));  // open: c_o
  float_multiply float_multiply_1 (.A(sub_2_s), .B(sub_2_s), .Y(float_multiply_1_y), .OF(out_3));
  float_multiply float_multiply_2 (
    .A(float_multiply_1_y), .B({Init[31], sub_1_s, Init[22:0]}), .Y(float_multiply_2_y), .OF(out_4));
  // Probe on sub_2_s
  // Probe on float_multiply_2_y
  // Probe on float_multiply_1_y
  float_adder float_adder_1 (.A(in_5), .B(float_multiply_2_y), .OP(1'b1), .Y(float_adder_1_y), .OF(out_8));
  float_multiply float_multiply_3 (.A(sub_2_s), .B(float_adder_1_y), .Y(Y), .OF(out_6));
  // Probe on float_adder_1_y

  // Notes on the sheet:
  //   magic_N: default 1597463007
  //   in_5: default 1069547520
endmodule
