// Digital circuit float adder.dig as structural Verilog
module float_adder (
  input  [31:0] A,
  input  [31:0] B,
  input  OP,
  output [31:0] Y,
  output OF
);

  wire _0_check_1_zero, _0_check_2_zero, _0_check_3_zero, and_1_out, comparator_1_lt, comparator_2_lt,
       multiplexer_4_out, multiplexer_5_out, not_1_out, xor_1_out, xor_2_out;
  wire [4:0] _0_check_3_out;
  wire [5:0] add_5_s, not_3_out;
  wire [6:0] bitextender_6_out;
  wire [7:0] add_1_s, bitextender_1_out, bitextender_2_out, multiplexer_3_out, xor_3_out, xor_4_out;
  wire [8:0] bitextender_5_out, not_2_out;
  wire [22:0] barrelshifter_1_out;
  wire [23:0] multiplexer_1_out, multiplexer_2_out, multiplexer_7_out;
  wire [24:0] add_2_s, add_3_s, barrelshifter_1_out_2, bitextender_3_out, bitextender_4_out, xor_5_out,
       xor_6_out;
  wire [31:0] add_4_s, multiplexer_9_out, multiplexer_10_out;
  wire [46:23] multiplexer_6_out;
  wire [47:0] barrelshifter_2_out;

  xor xor_1 (xor_1_out, B[31], OP);
  _0_check _0_check_1 (.in({1'b0, A[30:0]}), .zero(_0_check_1_zero));  // open: out
  _0_check _0_check_2 (.in({1'b0, B[30:0]}), .zero(_0_check_2_zero));  // open: out
  Multiplexer #(.Bits(24)) multiplexer_1 (
    .sel(_0_check_1_zero), .in_0({24{1'b0}}), .in_1({1'b1, A[22:0]}), .out(multiplexer_1_out));
  Multiplexer #(.Bits(24)) multiplexer_2 (
    .sel(_0_check_2_zero), .in_0({24{1'b0}}), .in_1({1'b1, B[22:0]}), .out(multiplexer_2_out));
  Comparator #(.Bits(8)) comparator_1 (.a(A[30:23]), .b(B[30:23]), .lt(comparator_1_lt));  // open: gt, eq
  Multiplexer #(.Bits(8)) multiplexer_3 (
    .sel(comparator_1_lt), .in_0(A[30:23]), .in_1(B[30:23]), .out(multiplexer_3_out));
  Multiplexer multiplexer_4 (.sel(comparator_1_lt), .in_0(xor_1_out), .in_1(A[31]), .out(multiplexer_4_out));
  Multiplexer multiplexer_5 (.sel(comparator_1_lt), .in_0(A[31]), .in_1(xor_1_out), .out(multiplexer_5_out));
  not not_1 (not_1_out, comparator_1_lt);
  Multiplexer #(.Bits(24)) multiplexer_6 (
    .sel(comparator_1_lt), .in_0(multiplexer_2_out), .in_1(multiplexer_1_out), .out(multiplexer_6_out));
  Multiplexer #(.Bits(24)) multiplexer_7 (
    .sel(comparator_1_lt), .in_0(multiplexer_1_out), .in_1(multiplexer_2_out), .out(multiplexer_7_out));
  xor xor_2 (xor_2_out, multiplexer_4_out, multiplexer_5_out);
  BitExtender #(.inputBits(1), .outputBits(8)) bitextender_1 (.in(comparator_1_lt), .out(bitextender_1_out));
  BitExtender #(.inputBits(1), .outputBits(8)) bitextender_2 (.in(not_1_out), .out(bitextender_2_out));
  assign xor_3_out = bitextender_1_out ^ A[30:23];  // XOr xor_3, 8 bits wide
  assign xor_4_out = bitextender_2_out ^ B[30:23];  // XOr xor_4, 8 bits wide
  BitExtender #(.inputBits(1), .outputBits(25)) bitextender_3 (.in(xor_2_out), .out(bitextender_3_out));
  Add #(.Bits(8)) add_1 (.a(xor_3_out), .b(xor_4_out), .c_i(1'b1), .s(add_1_s));  // open: c_o
  BarrelShifter #(.Bits(48), .direction("right")) barrelshifter_1 (
    .in({1'b0, multiplexer_6_out, {23{1'b0}}}), .shift(add_1_s[5:0]),
    .out({barrelshifter_1_out_2, barrelshifter_1_out}));
  assign xor_5_out = {1'b0, multiplexer_7_out} ^ bitextender_3_out;  // XOr xor_5, 25 bits wide
  Comparator #(.Bits(8)) comparator_2 (.a(add_1_s), .b(8'h18), .lt(comparator_2_lt));  // open: gt, eq
  Add #(.Bits(25)) add_2 (.a(barrelshifter_1_out_2), .b(xor_5_out), .c_i(xor_2_out), .s(add_2_s));  // open: c_o
  and and_1 (and_1_out, add_2_s[24], xor_2_out);
  Multiplexer multiplexer_8 (.sel(and_1_out), .in_0(multiplexer_4_out), .in_1(multiplexer_5_out), .out(add_4_s[31]));
  Multiplexer #(.Bits(32)) multiplexer_9 (.sel(comparator_1_lt), .in_0(A), .in_1(B), .out(multiplexer_9_out));
  assign xor_6_out = add_2_s ^ bitextender_4_out;  // XOr xor_6, 25 bits wide
  BitExtender #(.inputBits(1), .outputBits(25)) bitextender_4 (.in(and_1_out), .out(bitextender_4_out));
  Add #(.Bits(25)) add_3 (.a(xor_6_out), .b({25{1'b0}}), .c_i(and_1_out), .s(add_3_s));  // open: c_o
  _0_check _0_check_3 (.in({{7{1'b0}}, add_3_s}), .out(_0_check_3_out), .zero(_0_check_3_zero));
  BitExtender #(.inputBits(6), .outputBits(9)) bitextender_5 (.in(add_5_s), .out(bitextender_5_out));
  Multiplexer #(.Bits(32)) multiplexer_10 (
    .sel(_0_check_3_zero), .in_0({32{1'b0}}), .in_1(add_4_s), .out(multiplexer_10_out));
  BarrelShifter #(.Bits(48), .barrelSigned("true")) barrelshifter_2 (
    .in({add_3_s, barrelshifter_1_out}), .shift(bitextender_6_out),
    .out({barrelshifter_2_out[47:46], add_4_s[22:0], barrelshifter_2_out[22:0]}));
  Add #(.Bits(9)) add_4 (
    .a({1'b0, multiplexer_3_out}), .b(not_2_out), .c_i(1'b1), .s({OF, add_4_s[30:23]}));  // open: c_o
  assign not_2_out = ~bitextender_5_out;  // Not not_2, 9 bits wide
  Multiplexer #(.Bits(32)) multiplexer_11 (
    .sel(comparator_2_lt), .in_0(multiplexer_9_out), .in_1(multiplexer_10_out), .out(Y));
  Add #(.Bits(6)) add_5 (.a(6'b010111), .b(not_3_out), .c_i(1'b1), .s(add_5_s));  // open: c_o
  assign not_3_out = ~{1'b0, _0_check_3_out};  // Not not_3, 6 bits wide
  BitExtender #(.inputBits(6), .outputBits(7)) bitextender_6 (.in(add_5_s), .out(bitextender_6_out));

  // Notes on the sheet:
  //   A: default 1624647376
endmodule
