// Digital circuit iteration square.dig as structural Verilog
module iteration_square (
  input  [15:0] Init_16,
  input  sel,
  input  [15:0] c,
  output [15:0] out_4
);

  wire clk_out;
  wire [15:0] add_1_s, d_ff_1_q, multiplexer_1_out;
  wire [31:0] mul_1_mul;

  D_FF #(.Bits(16)) d_ff_1 (.D(out_4), .C(clk_out), .Q(d_ff_1_q));  // open: nQ
  Button clk (.out(clk_out));
  Multiplexer #(.Bits(16)) multiplexer_1 (.sel(sel), .in_0(Init_16), .in_1(d_ff_1_q), .out(multiplexer_1_out));
  Mul #(.Bits(16)) mul_1 (.a(multiplexer_1_out), .b(multiplexer_1_out), .mul(mul_1_mul));
  // Probe on multiplexer_1_out
  // Probe on mul_1_mul
  Add #(.Bits(16)) add_1 (.a(multiplexer_1_out), .b({1'b0, c[15:1]}), .c_i(1'b0), .s(add_1_s));  // open: c_o
  // Probe on add_1_s
  Sub #(.Bits(16)) sub_1 (.a(add_1_s), .b({1'b0, mul_1_mul[23:9]}), .c_i(1'b0), .s(out_4));  // open: c_o
  // Probe on {1'b0, mul_1_mul[23:9]}
endmodule
