// Digital circuit linear inter.dig as structural Verilog
module linear_inter (
  input  [7:0] ADDR,
  output [7:0] out_2
);

  wire [3:0] add_1_s;
  wire [4:0] sub_1_s;
  wire [7:0] registerfile_1_da, registerfile_1_db;
  wire [15:0] add_2_s, mul_1_mul, mul_2_mul;

  // Probe on ADDR[3:0]
  Add #(.Bits(4)) add_1 (.a(ADDR[7:4]), .b(4'b0001), .c_i(1'b0), .s(add_1_s));  // open: c_o
  Sub #(.Bits(5)) sub_1 (.a(5'b10000), .b({1'b0, ADDR[3:0]}), .c_i(1'b0), .s(sub_1_s));  // open: c_o
  RegisterFile #(.AddrBits(4), .Bits(8)) registerfile_1 (
    .Din({8{1'b0}}), .we(1'b0), .Rw(4'b0000), .C(1'b0), .Ra(ADDR[7:4]), .Rb(add_1_s), .Da(registerfile_1_da),
    .Db(registerfile_1_db));
  // Probe on registerfile_1_db
  // Probe on sub_1_s
  Mul #(.Bits(8)) mul_1 (.a({3'b000, sub_1_s}), .b(registerfile_1_da), .mul(mul_1_mul));
  // Probe on registerfile_1_da
  Mul #(.Bits(8)) mul_2 (.a(registerfile_1_db), .b({4'b0000, ADDR[3:0]}), .mul(mul_2_mul));
  // Probe on mul_1_mul
  Add #(.Bits(16)) add_2 (
    .a(mul_1_mul), .b(mul_2_mul), .c_i(1'b0), .s({add_2_s[15:12], out_2, add_2_s[3:0]}));  // open: c_o
  // Probe on mul_2_mul
  // Probe on {add_2_s[15:12], out_2, add_2_s[3:0]}
endmodule
