// Digital circuit logarithm.dig as structural Verilog
module logarithm (
  input  [7:0] in_1,
  output [7:0] out_2,
  output ERROR
);

  wire priorityencoder_1_any;
  wire [2:0] priorityencoder_1_num, sub_1_s;
  wire [7:0] barrelshifter_1_out;

  PriorityEncoder #(.Selector_Bits(3)) priorityencoder_1 (
    .in0(in_1[0]), .in1(in_1[1]), .in2(in_1[2]), .in3(in_1[3]), .in4(in_1[4]), .in5(in_1[5]), .in6(in_1[6]),
    .in7(in_1[7]), .num(priorityencoder_1_num), .any(priorityencoder_1_any));
  Sub #(.Bits(3)) sub_1 (.a(3'b111), .b(priorityencoder_1_num), .c_i(1'b0), .s(sub_1_s));  // open: c_o
  not not_1 (ERROR, priorityencoder_1_any);
  BarrelShifter #(.Bits(8)) barrelshifter_1 (.in(in_1), .shift({1'b0, sub_1_s}), .out(barrelshifter_1_out));
  // Probe on barrelshifter_1_out
  assign out_2[7:5] = priorityencoder_1_any ? priorityencoder_1_num : 3'bz;  // Driver driver_1
  ROM #(.AddrBits(4), .Bits(5)) rom_1 (.A(barrelshifter_1_out[6:3]), .sel(priorityencoder_1_any), .D(out_2[4:0]));
  // Probe on out_2[4:0]
  // Probe on out_2[7:5]

  // Notes on the sheet:
  //   contents of rom_1 (hex, n*v repeats v):
  //   0,2,5,7,a,c,e,10,12,14,16,18,19,1b,1d,1e
endmodule
