// Digital circuit ledmatix.dig as structural Verilog
module ledmatix (
  input  Sclk,
  input  in_5,
  input  en,
  input  clk,
  output done,
  output idel,
  output ready,
  output [1:0] out_6,
  output [4:0] out_7
);

  wire dir_vld, off_vld, start;
  wire [1:0] dir;
  wire [4:0] counter_1_out, off;
  wire [31:0] rom_1_d;

  and and_1 (start, en, clk);
  Counter #(.Bits(5)) counter_1 (.en(en), .C(start), .clr(1'b0), .out(counter_1_out));  // open: ovf
  ROM #(.AddrBits(5), .Bits(32)) rom_1 (.A(counter_1_out), .sel(en), .D(rom_1_d));
  LedMatrix #(.colAddrBits(5), .rowDataBits(32)) ledmatrix_1 (.rows(rom_1_d), .column(counter_1_out));
  track #(.applicationType("IVERILOG")) u_track (
    .ap_clk(Sclk), .ap_rst(in_5), .ap_start(start), .pos_r(counter_1_out), .value_r(rom_1_d), .ap_done(done),
    .ap_idle(idel), .ap_ready(ready), .direction(dir), .direction_ap_vld(dir_vld), .offset(off),
    .offset_ap_vld(off_vld));
  Register #(.Bits(2)) direction (.D(dir), .C(dir_vld), .en(1'b1), .Q(out_6));
  Register #(.Bits(5)) offest (.D(off), .C(off_vld), .en(1'b1), .Q(out_7));

  // Notes on the sheet:
  //   Sclk: Hz: 5
  //   contents of rom_1 (hex, n*v repeats v):
  //   10000,10000,10000,8000,8000,8000,8000,8000,4000,4000,4000,4000,2000,1000,800,800,
  //   1000,2000,4000,8000,10000,10000,10000,10000,20000,40000,40000,80000,100000,200000,
  //   200000,200000
  //   0--measns on the line
  //   1--means on the left
  //   2--means on the right
endmodule

/* Code of track:
// ==============================================================
// RTL generated by Vivado(TM) HLS - High-Level Synthesis from C, C++ and SystemC
// Version: 2018.3
// Copyright (C) 1986-2018 Xilinx, Inc. All Rights Reserved.
// 
// ===========================================================

//`timescale 1 ns / 1 ps 

//(* CORE_GENERATION_INFO="track,hls_ip_2018_3,{HLS_INPUT_TYPE=c,HLS_INPUT_FLOAT=0,HLS_INPUT_FIXED=1,HLS_INPUT_PART=xa7a12tcsg325-1q,HLS_INPUT_CLOCK=10.000000,HLS_INPUT_ARCH=others,HLS_SYN_CLOCK=3.570250,HLS_SYN_LAT=-1,HLS_SYN_TPT=none,HLS_SYN_MEM=0,HLS_SYN_DSP=0,HLS_SYN_FF=131,HLS_SYN_LUT=250,HLS_VERSION=2018_3}" *)

module track (
        ap_clk,
        ap_rst,
        ap_start,
        ap_done,
        ap_idle,
        ap_ready,
        pos_r,
        value_r,
        direction,
        direction_ap_vld,
        offset,
        offset_ap_vld
);

parameter    ap_ST_fsm_state1 = 3'd1;
parameter    ap_ST_fsm_state2 = 3'd2;
parameter    ap_ST_fsm_state3 = 3'd4;

input   ap_clk;
input   ap_rst;
input   ap_start;
output   ap_done;
output   ap_idle;
output   ap_ready;
input  [4:0] pos_r;
input  [31:0] value_r;
output  [1:0] direction;
output   direction_ap_vld;
output  [4:0] offset;
output   offset_ap_vld;

reg ap_done;
reg ap_idle;
reg ap_ready;
reg[1:0] direction;
reg direction_ap_vld;
reg offset_ap_vld;

(* fsm_encoding = "none" *) reg   [2:0] ap_CS_fsm;
wire    ap_CS_fsm_state1;
wire   [31:0] count_fu_136_p2;
wire    ap_CS_fsm_state2;
wire   [0:0] tmp_1_i_fu_130_p2;
wire   [31:0] tmp_3_fu_152_p1;
wire   [31:0] count_1_fu_160_p2;
wire    ap_CS_fsm_state3;
wire   [0:0] tmp_5_fu_156_p1;
wire   [31:0] tmp_4_fu_176_p1;
reg   [31:0] p_0_i_reg_71;
reg   [31:0] count_i_reg_81;
reg   [31:0] p_1_i_reg_93;
reg   [31:0] roadxy_y_reg_103;
reg   [4:0] ap_phi_mux_storemerge1_phi_fu_116_p6;
wire   [0:0] tmp_fu_180_p2;
wire   [4:0] tmp_2_fu_206_p2;
wire   [0:0] icmp_fu_196_p2;
wire   [4:0] tmp_s_fu_217_p2;
wire   [3:0] tmp_1_fu_126_p1;
wire   [27:0] value_assign_fu_142_p4;
wire   [30:0] value_assign_1_fu_166_p4;
wire   [27:0] tmp_6_fu_186_p4;
wire   [4:0] tmp_8_fu_202_p1;
wire   [4:0] tmp_7_fu_213_p1;
reg   [2:0] ap_NS_fsm;

// power-on initialization
initial begin
#0 ap_CS_fsm = 3'd1;
end

always @ (posedge ap_clk) begin
    if (ap_rst == 1'b1) begin
        ap_CS_fsm <= ap_ST_fsm_state1;
    end else begin
        ap_CS_fsm <= ap_NS_fsm;
    end
end

always @ (posedge ap_clk) begin
    if (((tmp_1_i_fu_130_p2 == 1'd1) & (1'b1 == ap_CS_fsm_state2))) begin
        count_i_reg_81 <= count_fu_136_p2;
    end else if (((ap_start == 1'b1) & (1'b1 == ap_CS_fsm_state1))) begin
        count_i_reg_81 <= 32'd0;
    end
end

always @ (posedge ap_clk) begin
    if (((tmp_1_i_fu_130_p2 == 1'd1) & (1'b1 == ap_CS_fsm_state2))) begin
        p_0_i_reg_71 <= tmp_3_fu_152_p1;
    end else if (((ap_start == 1'b1) & (1'b1 == ap_CS_fsm_state1))) begin
        p_0_i_reg_71 <= value_r;
    end
end

always @ (posedge ap_clk) begin
    if (((tmp_1_i_fu_130_p2 == 1'd0) & (1'b1 == ap_CS_fsm_state2))) begin
        p_1_i_reg_93 <= p_0_i_reg_71;
    end else if (((tmp_5_fu_156_p1 == 1'd0) & (1'b1 == ap_CS_fsm_state3))) begin
        p_1_i_reg_93 <= tmp_4_fu_176_p1;
    end
end

always @ (posedge ap_clk) begin
    if (((tmp_1_i_fu_130_p2 == 1'd0) & (1'b1 == ap_CS_fsm_state2))) begin
        roadxy_y_reg_103 <= count_i_reg_81;
    end else if (((tmp_5_fu_156_p1 == 1'd0) & (1'b1 == ap_CS_fsm_state3))) begin
        roadxy_y_reg_103 <= count_1_fu_160_p2;
    end
end

always @ (*) begin
    if (((tmp_5_fu_156_p1 == 1'd1) & (1'b1 == ap_CS_fsm_state3))) begin
        ap_done = 1'b1;
    end else begin
        ap_done = 1'b0;
    end
end

always @ (*) begin
    if (((ap_start == 1'b0) & (1'b1 == ap_CS_fsm_state1))) begin
        ap_idle = 1'b1;
    end else begin
        ap_idle = 1'b0;
    end
end

always @ (*) begin
    if (((tmp_5_fu_156_p1 == 1'd1) & (1'b1 == ap_CS_fsm_state3))) begin
        if (((tmp_fu_180_p2 == 1'd0) & (icmp_fu_196_p2 == 1'd1))) begin
            ap_phi_mux_storemerge1_phi_fu_116_p6 = tmp_s_fu_217_p2;
        end else if (((icmp_fu_196_p2 == 1'd0) & (tmp_fu_180_p2 == 1'd0))) begin
            ap_phi_mux_storemerge1_phi_fu_116_p6 = tmp_2_fu_206_p2;
        end else if ((tmp_fu_180_p2 == 1'd1)) begin
            ap_phi_mux_storemerge1_phi_fu_116_p6 = 5'd0;
        end else begin
            ap_phi_mux_storemerge1_phi_fu_116_p6 = 'bx;
        end
    end else begin
        ap_phi_mux_storemerge1_phi_fu_116_p6 = 'bx;
    end
end

always @ (*) begin
    if (((tmp_5_fu_156_p1 == 1'd1) & (1'b1 == ap_CS_fsm_state3))) begin
        ap_ready = 1'b1;
    end else begin
        ap_ready = 1'b0;
    end
end

always @ (*) begin
    if (((tmp_5_fu_156_p1 == 1'd1) & (1'b1 == ap_CS_fsm_state3))) begin
        if ((tmp_fu_180_p2 == 1'd1)) begin
            direction = 2'd0;
        end else if (((tmp_fu_180_p2 == 1'd0) & (icmp_fu_196_p2 == 1'd1))) begin
            direction = 2'd1;
        end else if (((icmp_fu_196_p2 == 1'd0) & (tmp_fu_180_p2 == 1'd0))) begin
            direction = 2'd2;
        end else begin
            direction = 'bx;
        end
    end else begin
        direction = 'bx;
    end
end

always @ (*) begin
    if ((((tmp_fu_180_p2 == 1'd0) & (icmp_fu_196_p2 == 1'd1) & (tmp_5_fu_156_p1 == 1'd1) & (1'b1 == ap_CS_fsm_state3)) | ((icmp_fu_196_p2 == 1'd0) & (tmp_fu_180_p2 == 1'd0) & (tmp_5_fu_156_p1 == 1'd1) & (1'b1 == ap_CS_fsm_state3)) | ((tmp_fu_180_p2 == 1'd1) & (tmp_5_fu_156_p1 == 1'd1) & (1'b1 == ap_CS_fsm_state3)))) begin
        direction_ap_vld = 1'b1;
    end else begin
        direction_ap_vld = 1'b0;
    end
end

always @ (*) begin
    if (((tmp_5_fu_156_p1 == 1'd1) & (1'b1 == ap_CS_fsm_state3))) begin
        offset_ap_vld = 1'b1;
    end else begin
        offset_ap_vld = 1'b0;
    end
end

always @ (*) begin
    case (ap_CS_fsm)
        ap_ST_fsm_state1 : begin
            if (((ap_start == 1'b1) & (1'b1 == ap_CS_fsm_state1))) begin
                ap_NS_fsm = ap_ST_fsm_state2;
            end else begin
                ap_NS_fsm = ap_ST_fsm_state1;
            end
        end
        ap_ST_fsm_state2 : begin
            if (((tmp_1_i_fu_130_p2 == 1'd0) & (1'b1 == ap_CS_fsm_state2))) begin
                ap_NS_fsm = ap_ST_fsm_state3;
            end else begin
                ap_NS_fsm = ap_ST_fsm_state2;
            end
        end
        ap_ST_fsm_state3 : begin
            if (((tmp_5_fu_156_p1 == 1'd1) & (1'b1 == ap_CS_fsm_state3))) begin
                ap_NS_fsm = ap_ST_fsm_state1;
            end else begin
                ap_NS_fsm = ap_ST_fsm_state3;
            end
        end
        default : begin
            ap_NS_fsm = 'bx;
        end
    endcase
end

assign ap_CS_fsm_state1 = ap_CS_fsm[32'd0];

assign ap_CS_fsm_state2 = ap_CS_fsm[32'd1];

assign ap_CS_fsm_state3 = ap_CS_fsm[32'd2];

assign count_1_fu_160_p2 = (roadxy_y_reg_103 + 32'd1);

assign count_fu_136_p2 = (count_i_reg_81 + 32'd4);

assign icmp_fu_196_p2 = ((tmp_6_fu_186_p4 == 28'd0) ? 1'b1 : 1'b0);

assign offset = ap_phi_mux_storemerge1_phi_fu_116_p6;

assign tmp_1_fu_126_p1 = p_0_i_reg_71[3:0];

assign tmp_1_i_fu_130_p2 = ((tmp_1_fu_126_p1 == 4'd0) ? 1'b1 : 1'b0);

assign tmp_2_fu_206_p2 = (tmp_8_fu_202_p1 ^ 5'd16);

assign tmp_3_fu_152_p1 = value_assign_fu_142_p4;

assign tmp_4_fu_176_p1 = value_assign_1_fu_166_p4;

assign tmp_5_fu_156_p1 = p_1_i_reg_93[0:0];

assign tmp_6_fu_186_p4 = {{roadxy_y_reg_103[31:4]}};

assign tmp_7_fu_213_p1 = roadxy_y_reg_103[4:0];

assign tmp_8_fu_202_p1 = roadxy_y_reg_103[4:0];

assign tmp_fu_180_p2 = ((roadxy_y_reg_103 == 32'd16) ? 1'b1 : 1'b0);

assign tmp_s_fu_217_p2 = ($signed(5'd16) - $signed(tmp_7_fu_213_p1));

assign value_assign_1_fu_166_p4 = {{p_1_i_reg_93[31:1]}};

assign value_assign_fu_142_p4 = {{p_0_i_reg_71[31:4]}};

endmodule //track
*/
