// Digital circuit fir_first.dig as structural Verilog
module fir_first (
  input  [23:0] x_i,
  input  CLK,
  input  LOAD,
  input  [15:0] sum,
  input  valid,
  input  [7:0] b,
  input  Clr,
  output [23:0] z_1,
  output [15:0] q,
  output done,
  output [7:0] z_b
);

  wire and_1_out, and_2_out, not_1_out;
  wire [7:0] d_ff_as_1_q, d_ff_as_2_q;
  wire [15:0] mul_1_mul, mul_2_mul, mul_3_mul;

  D_FF_AS #(.Bits(24)) DELAY (.Set(1'b0), .D(x_i), .C(CLK), .Clr(LOAD), .Q(z_1));  // open: nQ
  and and_1 (and_1_out, CLK, LOAD);
  not not_1 (not_1_out, LOAD);
  and and_2 (and_2_out, not_1_out, CLK);
  D_FF_AS #(.Bits(8)) d_ff_as_1 (.Set(1'b0), .D(b), .C(and_1_out), .Clr(Clr), .Q(d_ff_as_1_q));  // open: nQ
  D_FF_AS #(.Bits(8)) d_ff_as_2 (.Set(1'b0), .D(d_ff_as_1_q), .C(and_1_out), .Clr(Clr), .Q(d_ff_as_2_q));  // open: nQ
  D_FF_AS #(.Bits(8)) d_ff_as_3 (.Set(1'b0), .D(d_ff_as_2_q), .C(and_1_out), .Clr(Clr), .Q(z_b));  // open: nQ
  Mul #(.Bits(8)) mul_1 (.a(d_ff_as_1_q), .b(z_1[23:16]), .mul(mul_1_mul));
  Mul #(.Bits(8)) mul_2 (.a(d_ff_as_2_q), .b(z_1[15:8]), .mul(mul_2_mul));
  Mul #(.Bits(8)) mul_3 (.a(z_b), .b(z_1[7:0]), .mul(mul_3_mul));
  add #(.applicationType("IVERILOG")) u_add (
    .a(mul_1_mul), .b(mul_2_mul), .c(mul_3_mul), .c0(sum), .clk(and_2_out), .valid(valid), .sum(q),
    .out_valid(done));
endmodule

/* Code of add:
module add (
	input [15:0] a,
	input [15:0] b,
	input [15:0] c,
	input [15:0] c0,
	input clk,
	input valid,
	 
	
	output 	 [15:0] sum,
	output   reg out_valid
); 

assign sum=a+b+c+c0;

always @(posedge clk  ) begin
	 
	 out_valid<=valid;
end

endmodule
*/
