// Digital circuit fir_inc.dig as structural Verilog
module fir_inc (
  input  [23:0] x_i,
  input  CLK,
  input  load,
  input  [15:0] sum,
  input  valid,
  input  [7:0] b,
  input  Clr,
  output [23:0] Z_1,
  output [15:0] Q,
  output done,
  output [7:0] Z_B
);

  wire and_1_out, fir_first_1_done, not_1_out, undriven;
  wire [7:0] d_ff_as_1_q, d_ff_as_2_q, fir_first_1_z_b;
  wire [15:0] fir_first_1_q, mul_1_mul, mul_2_mul, mul_3_mul;
  wire [23:0] fir_first_1_z_1;

  fir_first #(.generic("if (isPresent(args)) { if (args.order>2) { export order := args.order-1; setCircuit(\"fir_inc.dig\"); } } else { export order := 2; }")) fir_first_1 (
    .x_i(x_i), .CLK(CLK), .LOAD(load), .sum(sum), .valid(valid), .b(b), .Clr(Clr), .z_1(fir_first_1_z_1),
    .q(fir_first_1_q), .done(fir_first_1_done), .z_b(fir_first_1_z_b));
  not not_1 (not_1_out, load);
  and and_1 (and_1_out, not_1_out, CLK);
  D_FF_AS #(.Bits(24)) DELAY (.Set(1'b0), .D(fir_first_1_z_1), .C(CLK), .Clr(load), .Q(Z_1));  // open: nQ
  // And and_2 has open pins: In_1=load, In_2=CLK, out=open
  D_FF_AS #(.Bits(8)) d_ff_as_1 (
    .Set(1'b0), .D(fir_first_1_z_b), .C(undriven), .Clr(Clr), .Q(d_ff_as_1_q));  // open: nQ
  D_FF_AS #(.Bits(8)) d_ff_as_2 (.Set(1'b0), .D(d_ff_as_1_q), .C(undriven), .Clr(Clr), .Q(d_ff_as_2_q));  // open: nQ
  D_FF_AS #(.Bits(8)) d_ff_as_3 (.Set(1'b0), .D(d_ff_as_2_q), .C(undriven), .Clr(Clr), .Q(Z_B));  // open: nQ
  Mul #(.Bits(8)) mul_1 (.a(d_ff_as_1_q), .b(Z_1[23:16]), .mul(mul_1_mul));
  Mul #(.Bits(8)) mul_2 (.a(d_ff_as_2_q), .b(Z_1[15:8]), .mul(mul_2_mul));
  Mul #(.Bits(8)) mul_3 (.a(Z_B), .b(Z_1[7:0]), .mul(mul_3_mul));
  add #(.applicationType("IVERILOG")) u_add (
    .a(mul_1_mul), .b(mul_2_mul), .c(mul_3_mul), .c0(fir_first_1_q), .clk(and_1_out),
    .valid(fir_first_1_done), .sum(Q), .out_valid(done));
endmodule

/* Code of add:
module add (
	input [15:0] a,
	input [15:0] b,
	input [15:0] c,
	input [15:0] c0,
	input clk,
	input valid,
	 
	
	output 	 [15:0] sum,
	output   reg out_valid
); 

assign sum=a+b+c+c0;

always @(posedge clk  ) begin
	 
	 out_valid<=valid;
end

endmodule
*/
