// Digital circuit TEST.dig as structural Verilog
module TEST (
  input  [7:0] P,
  output [7:0] Q
);

  // absolute #(.generic("dataBits :=8;")) absolute_1: pin names not known; wires that end beside it: P, Q
endmodule
