// Digital circuit fir_inc.dig as structural Verilog
module fir_inc (
  input  [23:0] x_i,
  input  CLK,
  input  load,
  input  [15:0] sum,
  input  valid,
  input  [7:0] b,
  input  Clr,
  output [23:0] Z_1,
  output [15:0] Q,
  output done,
  output [7:0] Z_B
);

  wire add_1_c_o, add_2_c_o, and_1_out, fir_first_1_done, not_1_out, undriven;
  wire [7:0] d_ff_as_1_q, d_ff_as_2_q, fir_first_1_z_b;
  wire [15:0] add_1_s, add_2_s, fir_first_1_q, mul_1_mul, mul_2_mul, mul_3_mul;
  wire [23:0] fir_first_1_z_1;

  fir_first #(.generic("if (isPresent(args)) { if (args.order>2) { export order := args.order-1; setCircuit(\"fir_inc.dig\"); } } else { export order := 2; }")) fir_first_1 (
    .x_i(x_i), .CLK(CLK), .LOAD(load), .sum(sum), .valid(valid), .b(b), .Clr(Clr), .z_1(fir_first_1_z_1),
    .q(fir_first_1_q), .done(fir_first_1_done), .z_b(fir_first_1_z_b));
  not not_1 (not_1_out, load);
  and and_1 (and_1_out, not_1_out, CLK);
  D_FF_AS #(.Bits(24)) DELAY (.Set(1'b0), .D(fir_first_1_z_1), .C(CLK), .Clr(load), .Q(Z_1));  // open: nQ
  // And and_2 has open pins: In_1=load, In_2=CLK, out=open
  D_FF_AS #(.Bits(8)) d_ff_as_1 (
    .Set(1'b0), .D(fir_first_1_z_b), .C(undriven), .Clr(Clr), .Q(d_ff_as_1_q));  // open: nQ
  D_FF_AS #(.Bits(8)) d_ff_as_2 (.Set(1'b0), .D(d_ff_as_1_q), .C(undriven), .Clr(Clr), .Q(d_ff_as_2_q));  // open: nQ
  D_FF_AS #(.Bits(8)) d_ff_as_3 (.Set(1'b0), .D(d_ff_as_2_q), .C(undriven), .Clr(Clr), .Q(Z_B));  // open: nQ
  Mul #(.Bits(8)) mul_1 (.a(d_ff_as_1_q), .b(Z_1[23:16]), .mul(mul_1_mul));
  Mul #(.Bits(8)) mul_2 (.a(d_ff_as_2_q), .b(Z_1[15:8]), .mul(mul_2_mul));
  Mul #(.Bits(8)) mul_3 (.a(Z_B), .b(Z_1[7:0]), .mul(mul_3_mul));
  Add #(.Bits(16)) add_1 (.a(mul_1_mul), .b(mul_2_mul), .c_i(1'b0), .s(add_1_s), .c_o(add_1_c_o));
  D_FF d_ff_1 (.D(fir_first_1_done), .C(and_1_out), .Q(done));  // open: nQ
  Add #(.Bits(16)) add_2 (.a(add_1_s), .b(mul_3_mul), .c_i(add_1_c_o), .s(add_2_s), .c_o(add_2_c_o));
  Add #(.Bits(16)) add_3 (.a(add_2_s), .b(fir_first_1_q), .c_i(add_2_c_o), .s(Q));  // open: c_o
endmodule
