// Digital circuit TEST.dig as structural Verilog
module TEST (
  input  clk,
  input  [15:0] b,
  output [31:0] Q
);

  wire [7:0] counter_1_out;
  wire [15:0] rom_1_d;

  Counter #(.Bits(8)) counter_1 (.en(1'b1), .C(clk), .clr(1'b0), .out(counter_1_out));  // open: ovf
  ROM #(.AddrBits(8), .Bits(16)) rom_1 (.A(counter_1_out), .sel(1'b1), .D(rom_1_d));
  fir #(.generic("order := 11;")) fir_1 (.x_i(rom_1_d), .b(b), .clk(clk), .Q(Q));

  // Notes on the sheet:
  //   contents of rom_1 (hex, n*v repeats v):
  //   0,19,12,fe,4,20,26,d,fb,9,19,a,ec,e6,fb,1,ea,d8,e8,2,0,ec,ee,c,1d,e,fe,c,25,21,4,
  //   fa,c,16,ff,e4,e9,fe,fc,e2,da,f2,7,fd,eb,f7,16,1e,a,0,14,27,18,fc,fb,f,10,f3,df,ed,
  //   0,f6,dd,df,fc,a,fa,ee,2,1e,1c,5,3,1b,25,e,f6,fd,10,7,e8,de,f2,0,ef,db,e8,5,a,f7,f3,
  //   e,23,17,2,8,20,20,3,f2,0,e,fd,e0,e0,f8,fe,e9,dd,f2,d,9,f6,fb,18,25,11,0,e,22,18,f9,
  //   f0,3,a,f2,db,e5,fd,fb,e4,e2,fe,12,6,f6,4,21,23,a,0,13,21,d,f0,f1,5,4,e8,d9,ec,0,f6,
  //   e2,ea,9,15,3,f9,e,26,1e,4,2,17,1c,1,ea,f4,6,fc,df,db,f4,2,f2,e3,f4,12,14,0,fe,18,
  //   28,16,ff,5,1a,14,f6,e7,f7,5,f3,da,e0,fc,2,ee,e7,0,19,12,fe,4,20,26,d,fb,9,19,a,ec,
  //   e6,fb,1,ea,d8,e8,2,0,ec,ee,c,1d,e,fe,c,25,21,4,fa,c,16,ff,e4,e9,fe,fc,e2,da,f2,7,
  //   fd,eb,f7,16,1e,a,0,14,27,18,fc,fb,f
endmodule
