// Digital circuit fir.dig as structural Verilog
module fir (
  input  [15:0] x_i,
  input  [15:0] b,
  input  clk,
  output [31:0] Q
);

  fir_first #(.generic("if (isPresent(args)) { if (args.order>1) { setCircuit(\"fir_inc.dig\"); } } else { export order:=1; }")) fir_first_1 (
    .x_i(x_i), .b(b), .CLK(clk), .sum({32{1'b0}}), .q(Q));  // open: z
endmodule
