// Digital circuit fir_first.dig as structural Verilog
module fir_first (
  input  [15:0] x_i,
  input  [15:0] b,
  input  CLK,
  input  [31:0] sum,
  output [15:0] z,
  output [31:0] q
);

  wire [31:0] mul_1_mul;

  D_FF #(.Bits(16)) d_ff_1 (.D(x_i), .C(CLK), .Q(z));  // open: nQ
  Mul #(.Bits(16)) mul_1 (.a(z), .b(b), .mul(mul_1_mul));
  Add #(.Bits(32)) add_1 (.a(mul_1_mul), .b(sum), .c_i(1'b0), .s(q));  // open: c_o
endmodule
