// Digital circuit fir_inc.dig as structural Verilog
module fir_inc (
  input  [15:0] x_i,
  input  [15:0] b,
  input  CLK,
  input  [31:0] sum,
  output [15:0] Z,
  output [31:0] Q
);

  wire [15:0] fir_first_1_z;
  wire [31:0] fir_first_1_q, mul_1_mul;

  fir_first #(.generic("if (isPresent(args)) { if (args.order>2) { export order := args.order-1; setCircuit(\"fir_inc.dig\"); } } else { export order := 2; }")) fir_first_1 (
    .x_i(x_i), .b(b), .CLK(CLK), .sum(sum), .z(fir_first_1_z), .q(fir_first_1_q));
  D_FF #(.Bits(16)) d_ff_1 (.D(fir_first_1_z), .C(CLK), .Q(Z));  // open: nQ
  Mul #(.Bits(16)) mul_1 (.a(Z), .b(b), .mul(mul_1_mul));
  Add #(.Bits(32)) add_1 (.a(mul_1_mul), .b(fir_first_1_q), .c_i(1'b0), .s(Q));  // open: c_o
endmodule
