// Digital circuit fir-expand.dig as structural Verilog
module fir_expand (
  input  clk,
  input  load,
  input  [15:0] b,
  input  [15:0] x_i,
  output [31:0] q
);

  wire and_1_out, fir_base_1_p6, fir_base_1_p7, fir_base_1_p8, fir_base_2_p1, fir_base_2_p2, fir_base_2_p4,
       fir_base_2_p6, fir_base_2_p7, fir_base_2_p8, fir_base_3_p6, fir_base_3_p7, fir_base_3_p8,
       fir_base_4_p6, fir_base_4_p7, fir_base_4_p8, fir_base_5_p6, fir_base_5_p7, fir_base_5_p8,
       fir_base_6_p6, fir_base_6_p7, fir_base_6_p8, fir_base_7_p6, fir_base_7_p7, fir_base_7_p8,
       fir_base_8_p6, fir_base_8_p7, fir_base_8_p8;
  wire [15:0] d_ff_1_q;
  wire [31:0] mul_1_mul;

  and and_1 (and_1_out, clk, load);
  D_FF #(.Bits(16)) d_ff_1 (.D(b), .C(and_1_out), .Q(d_ff_1_q));  // open: nQ
  Mul #(.Bits(16)) mul_1 (.a(x_i), .b(d_ff_1_q), .mul(mul_1_mul));
  // fir_base fir_base_1: pin names not known; wires that end beside it: x_i, d_ff_1_q, clk, mul_1_mul, load, fir_base_1_p6, fir_base_1_p7, fir_base_1_p8
  // fir_base fir_base_2: pin names not known; wires that end beside it: fir_base_2_p1, fir_base_2_p2, clk, fir_base_2_p4, load, fir_base_2_p6, fir_base_2_p7, fir_base_2_p8
  // fir_base fir_base_3: pin names not known; wires that end beside it: fir_base_1_p6, fir_base_1_p8, clk, fir_base_1_p7, load, fir_base_3_p6, fir_base_3_p7, fir_base_3_p8
  // fir_base fir_base_4: pin names not known; wires that end beside it: fir_base_2_p6, fir_base_2_p8, clk, fir_base_2_p7, load, fir_base_4_p6, fir_base_4_p7, fir_base_4_p8
  // fir_base fir_base_5: pin names not known; wires that end beside it: fir_base_3_p6, fir_base_3_p8, clk, fir_base_3_p7, load, fir_base_5_p6, fir_base_5_p7, fir_base_5_p8
  // fir_base fir_base_6: pin names not known; wires that end beside it: fir_base_4_p6, fir_base_4_p8, clk, fir_base_4_p7, load, fir_base_6_p6, fir_base_6_p7, fir_base_6_p8
  // fir_base fir_base_7: pin names not known; wires that end beside it: fir_base_5_p6, fir_base_5_p8, clk, fir_base_5_p7, load, fir_base_7_p6, fir_base_7_p7, fir_base_7_p8
  // fir_base fir_base_8: pin names not known; wires that end beside it: fir_base_6_p6, fir_base_6_p8, clk, fir_base_6_p7, load, fir_base_8_p6, fir_base_8_p7, fir_base_8_p8
  // fir_base fir_base_9: pin names not known; wires that end beside it: fir_base_7_p6, fir_base_7_p8, clk, fir_base_7_p7, load, fir_base_2_p1, fir_base_2_p4, fir_base_2_p2
  // fir_base fir_base_10: pin names not known; wires that end beside it: fir_base_8_p6, fir_base_8_p8, clk, fir_base_8_p7, load, q
endmodule
