// Digital circuit TEST.dig as structural Verilog
module TEST (
  input  LOAD,
  input  clk,
  output [31:0] Q
);

  wire c, clk_t, done, en_out, or_1_out, or_2_out, t_ff_1_q;
  wire [3:0] counterpreset_1_out;
  wire [8:0] counterpreset_2_out;
  wire [15:0] coeff_d, data_d;

  Button u_c (.out(c));
  CounterPreset #(.maxValue(11), .Bits(4)) counterpreset_1 (
    .en(1'b1), .C(c), .dir(1'b0), .in(4'b0000), .ld(1'b0), .clr(1'b0), .out(counterpreset_1_out));  // open: ovf
  CounterPreset #(.maxValue(265), .Bits(9)) counterpreset_2 (
    .en(1'b1), .C(clk_t), .dir(1'b0), .in({9{1'b0}}), .ld(1'b0), .clr(1'b0), .out(counterpreset_2_out),
    .ovf(done));
  ROM #(.AddrBits(4), .Bits(16)) coeff (.A(counterpreset_1_out), .sel(1'b1), .D(coeff_d));
  ROM #(.AddrBits(9), .Bits(16)) data (.A(counterpreset_2_out), .sel(1'b1), .D(data_d));
  or or_1 (or_1_out, c, clk_t);
  Button en (.out(en_out));
  or or_2 (or_2_out, en_out, done);
  fir #(.generic("order := 10;")) fir_1 (.xi(data_d), .b(coeff_d), .clk(or_1_out), .load(LOAD), .Q(Q));
  T_FF t_ff_1 (.T(1'b1), .C(or_2_out), .Q(t_ff_1_q));  // open: nQ
  and and_1 (clk_t, t_ff_1_q, clk);
  EEPROMDualPort #(.AddrBits(9), .Bits(32)) eepromdualport_1 (
    .A(counterpreset_2_out), .Din(Q), .str(1'b1), .C(clk_t), .ld(1'b0));  // open: D

  // Notes on the sheet:
  //   clk: Hz: 20
  //   contents of coeff (hex, n*v repeats v):
  //   0,2,8,13,20,2c,30,2c,20,13,8,2,0,0,0,1
  //   contents of data (hex, n*v repeats v):
  //   0,19,12,fe,4,20,26,d,fb,9,19,a,ec,e6,fb,1,ea,d8,e8,2,0,ec,ee,c,1d,e,fe,c,25,21,4,
  //   fa,c,16,ff,e4,e9,fe,fc,e2,da,f2,7,fd,eb,f7,16,1e,a,0,14,27,18,fc,fb,f,10,f3,df,ed,
  //   0,f6,dd,df,fc,a,fa,ee,2,1e,1c,5,3,1b,25,e,f6,fd,10,7,e8,de,f2,0,ef,db,e8,5,a,f7,f3,
  //   e,23,17,2,8,20,20,3,f2,0,e,fd,e0,e0,f8,fe,e9,dd,f2,d,9,f6,fb,18,25,11,0,e,22,18,f9,
  //   f0,3,a,f2,db,e5,fd,fb,e4,e2,fe,12,6,f6,4,21,23,a,0,13,21,d,f0,f1,5,4,e8,d9,ec,0,f6,
  //   e2,ea,9,15,3,f9,e,26,1e,4,2,17,1c,1,ea,f4,6,fc,df,db,f4,2,f2,e3,f4,12,14,0,fe,18,
  //   28,16,ff,5,1a,14,f6,e7,f7,5,f3,da,e0,fc,2,ee,e7,0,19,12,fe,4,20,26,d,fb,9,19,a,ec,
  //   e6,fb,1,ea,d8,e8,2,0,ec,ee,c,1d,e,fe,c,25,21,4,fa,c,16,ff,e4,e9,fe,fc,e2,da,f2,7,
  //   fd,eb,f7,16,1e,a,0,14,27,18,fc,fb,f
  //   contents of eepromdualport_1 (hex, n*v repeats v):
  //   0,32,ec,467,c6e,19c6,2920,377e,3fb8,43a4,43d1,43df,459f,491e,5284,6027,746e,89b0,
  //   9e3b,aa68,ae9a,a810,9ddd,90fb,8660,7cea,7547,6d08,64c8,5b3e,531d,4b0b,46bb,4410,4512,
  //   4bd6,597a,6f43,8a95,a8d6,c554,db58,e73d,e758,ddd4,d1a7,c5b7,bce7,b204,a2b4,888b,682d,
  //   464b,2d8c,2496,2e36,4373,5c73,715a,8054,89b1,91dd,9a3f,a425,acd9,b5ac,bad9,be6b,be44,
  //   b83e,ab2d,95c5,7a98,5c39,3f59,28b7,1c09,1d0a,2ba2,41ec,5a15,6e48,7cc1,85e2,8e20,96dd,
  //   a161,a8f2,acd0,a819,9fb6,9475,8b28,8299,796f,6b36,5784,4013,2aa7,1d00,1af0,227b,2ed2,
  //   3f30,51cf,6900,8431,a2d0,c02e,d785,e510,e500,d759,c1ed,aa7c,96ca,8891,7d67,6ed8,5a8b,
  //   424a,2de7,2530,2d0e,409f,5823,6be0,7a1e,853f,93b8,a7eb,c014,d65e,e4f6,e5f7,d949,c2a7,
  //   a5c7,8768,6c3b,54d3,41c2,30bc,2395,1b27,1c54,2927,3ddb,54c1,6823,764f,7fac,88a6,928d,
  //   9e8d,a7ca,ad6a,a874,9bb5,86d3,7175,5d4c,4ffc,4519,3c49,3059,242c,1aa8,1ac3,26a8,3cac,
  //   592a,776b,92bd,a886,b62a,bcee,bdf0,bb45,b6f5,ace3,9ec2,8a38,74f8,60b9,5516,4fa0,5105,
  //   5123,51f0,5166,5798,63c5,7850,8d92,a1d9,af7c,b8e2,bc61,be21,bc2f,b48e,a634,91e9,7c4e,
  //   6900,59b2,5017,48cc,4572,43d1,43df,459f,491e,5284,6027,746e,89b0,9e3b,aa68,ae9a,a810,
  //   9ddd,90fb,8660,7cea,7547,6d08,64c8,5b3e,531d,4b0b,46bb,4410,4512,4bd6,597a,6f43,8a95,
  //   a8d6,c554,db58,e73d,e758,ddd4,d1a7,c5b7,bce7,b204,a2b4,888b,682d,464b,2d8c,2496,2e36,
  //   4353,5a0d,66d4,6379,509c,35b6,1c91,aed,26e
endmodule
