// Digital circuit fir.dig as structural Verilog
module fir (
  input  [15:0] xi,
  input  [15:0] b,
  input  clk,
  input  load,
  output [31:0] Q
);

  wire and_1_out;
  wire [15:0] d_ff_1_q;
  wire [31:0] mul_1_mul;

  and and_1 (and_1_out, clk, load);
  D_FF #(.Bits(16)) d_ff_1 (.D(b), .C(and_1_out), .Q(d_ff_1_q));  // open: nQ
  Mul #(.Bits(16)) mul_1 (.a(xi), .b(d_ff_1_q), .mul(mul_1_mul));
  fir_first #(.generic("if (isPresent(args)) { if (args.order>1) { setCircuit(\"fir_inc.dig\"); } }")) fir_first_1 (
    .x_i(xi), .b(d_ff_1_q), .CLK(clk), .sum(mul_1_mul), .LOAD(load), .q(Q));  // open: z_xi, z_b
endmodule
