// Digital circuit fir_first.dig as structural Verilog
module fir_first (
  input  [15:0] x_i,
  input  [15:0] b,
  input  CLK,
  input  [31:0] sum,
  input  LOAD,
  output [15:0] z_xi,
  output [31:0] q,
  output [15:0] z_b
);

  wire and_1_out;
  wire [31:0] mul_1_mul;

  D_FF_AS #(.Bits(16)) d_ff_as_1 (.Set(1'b0), .D(x_i), .C(CLK), .Clr(LOAD), .Q(z_xi));  // open: nQ
  and and_1 (and_1_out, LOAD, CLK);
  D_FF #(.Bits(16)) d_ff_1 (.D(b), .C(and_1_out), .Q(z_b));  // open: nQ
  Mul #(.Bits(16)) mul_1 (.a(z_xi), .b(z_b), .mul(mul_1_mul));
  Add #(.Bits(32)) add_1 (.a(mul_1_mul), .b(sum), .c_i(1'b0), .s(q));  // open: c_o
endmodule
