// Digital circuit fir_inc.dig as structural Verilog
module fir_inc (
  input  [15:0] x_i,
  input  [15:0] b_0,
  input  CLK,
  input  [31:0] sum,
  input  LOAD,
  output [15:0] Z_xi,
  output [31:0] Q,
  output [15:0] Z_B
);

  wire and_1_out;
  wire [15:0] fir_first_1_z_b, fir_first_1_z_xi;
  wire [31:0] fir_first_1_q, mul_1_mul;

  fir_first #(.generic("if (isPresent(args)) { if (args.order>2) { export order := args.order-1; setCircuit(\"fir_inc.dig\"); } } else { export order := 2; }")) fir_first_1 (
    .x_i(x_i), .b(b_0), .CLK(CLK), .sum(sum), .LOAD(LOAD), .z_xi(fir_first_1_z_xi), .q(fir_first_1_q),
    .z_b(fir_first_1_z_b));
  D_FF_AS #(.Bits(16)) d_ff_as_1 (.Set(1'b0), .D(fir_first_1_z_xi), .C(CLK), .Clr(LOAD), .Q(Z_xi));  // open: nQ
  and and_1 (and_1_out, CLK, LOAD);
  D_FF #(.Bits(16)) d_ff_1 (.D(fir_first_1_z_b), .C(and_1_out), .Q(Z_B));  // open: nQ
  Mul #(.Bits(16)) mul_1 (.a(Z_xi), .b(Z_B), .mul(mul_1_mul));
  Add #(.Bits(32)) add_1 (.a(mul_1_mul), .b(fir_first_1_q), .c_i(1'b0), .s(Q));  // open: c_o
endmodule
