// Digital circuit gray.dig as structural Verilog
module gray (
  input  rst,
  input  valid,
  input  [7:0] data,
  input  clk,
  output valid_out,
  output [7:0] gray
);

  wire add_1_c_o, comparator_1_gt, demultiplexer_2_out_0, valid_in;
  wire [7:0] blue, d_ff_1_q, green, multiplexer_1_out, red;
  wire [15:0] add_1_s, add_2_s, barrelshifter_1_out, mul_1_mul, mul_2_mul, mul_3_mul;
  wire [31:0] div_1_r, index;

  Mul #(.Bits(8)) mul_1 (.a(red), .b(8'h4d), .mul(mul_1_mul));
  Mul #(.Bits(8)) mul_2 (.a(green), .b(8'h96), .mul(mul_2_mul));
  Mul #(.Bits(8)) mul_3 (.a(blue), .b(8'h1d), .mul(mul_3_mul));
  Add #(.Bits(16)) add_1 (.a(mul_1_mul), .b(mul_2_mul), .c_i(1'b0), .s(add_1_s), .c_o(add_1_c_o));
  Counter #(.Bits(32)) counter_1 (.en(valid_in), .C(clk), .clr(~rst), .out(index));  // open: ovf
  Add #(.Bits(16)) add_2 (.a(add_1_s), .b(mul_3_mul), .c_i(add_1_c_o), .s(add_2_s));  // open: c_o
  Div #(.Bits(32)) div_1 (.a(index), .b(32'h3), .r(div_1_r));  // open: q
  Comparator #(.Bits(32)) comparator_1 (.a(index), .b({32{1'b0}}), .gt(comparator_1_gt));  // open: eq, lt
  BarrelShifter #(.Bits(16), .direction("right")) barrelshifter_1 (
    .in(add_2_s), .shift(5'b01000), .out(barrelshifter_1_out));
  Demultiplexer #(.Selector_Bits(2), .Bits(8)) demultiplexer_1 (
    .sel(div_1_r[1:0]), .in(data), .out_0(blue), .out_1(green), .out_2(red));  // open: out_3
  Demultiplexer #(.Selector_Bits(2)) demultiplexer_2 (
    .sel(div_1_r[1:0]), .in(1'b1), .out_0(demultiplexer_2_out_0));  // open: out_1, out_2, out_3
  Multiplexer #(.Bits(8)) multiplexer_1 (
    .sel(valid_out), .in_0(d_ff_1_q), .in_1(barrelshifter_1_out[7:0]), .out(multiplexer_1_out));
  D_FF_AS d_ff_as_1 (.Set(1'b0), .D(valid), .C(clk), .Clr(~rst), .Q(valid_in));  // open: nQ
  and and_1 (valid_out, demultiplexer_2_out_0, comparator_1_gt);
  Multiplexer #(.Bits(8)) multiplexer_2 (.sel(valid_in), .in_0({8{1'b0}}), .in_1(multiplexer_1_out), .out(gray));
  D_FF #(.Bits(8)) d_ff_1 (.D(multiplexer_1_out), .C(~valid_out), .Q(d_ff_1_q));  // open: nQ
endmodule
