// Digital circuit graphic-base.dig as structural Verilog
module graphic_base (
  input  [23:0] x_i,
  input  CLK,
  input  LOAD,
  input  [15:0] sum,
  input  valid,
  input  [7:0] b,
  input  Clr,
  output [23:0] z_1,
  output [15:0] q,
  output done,
  output [7:0] z_b
);

  wire add_1_c_o, add_2_c_o, and_1_out, and_2_out, not_1_out;
  wire [7:0] d_ff_as_1_q, d_ff_as_2_q;
  wire [15:0] add_1_s, add_2_s, mul_1_mul, mul_2_mul, mul_3_mul;

  D_FF_AS #(.Bits(24)) DELAY (.Set(1'b0), .D(x_i), .C(CLK), .Clr(LOAD), .Q(z_1));  // open: nQ
  and and_1 (and_1_out, CLK, LOAD);
  not not_1 (not_1_out, LOAD);
  and and_2 (and_2_out, not_1_out, CLK);
  D_FF_AS #(.Bits(8)) d_ff_as_1 (.Set(1'b0), .D(b), .C(and_1_out), .Clr(Clr), .Q(d_ff_as_1_q));  // open: nQ
  D_FF_AS #(.Bits(8)) d_ff_as_2 (.Set(1'b0), .D(d_ff_as_1_q), .C(and_1_out), .Clr(Clr), .Q(d_ff_as_2_q));  // open: nQ
  D_FF_AS #(.Bits(8)) d_ff_as_3 (.Set(1'b0), .D(d_ff_as_2_q), .C(and_1_out), .Clr(Clr), .Q(z_b));  // open: nQ
  Mul #(.Bits(8)) mul_1 (.a(d_ff_as_1_q), .b(z_1[23:16]), .mul(mul_1_mul));
  Mul #(.Bits(8)) mul_2 (.a(d_ff_as_2_q), .b(z_1[15:8]), .mul(mul_2_mul));
  Mul #(.Bits(8)) mul_3 (.a(z_b), .b(z_1[7:0]), .mul(mul_3_mul));
  Add #(.Bits(16)) add_1 (.a(mul_1_mul), .b(mul_2_mul), .c_i(1'b0), .s(add_1_s), .c_o(add_1_c_o));
  Add #(.Bits(16)) add_2 (.a(add_1_s), .b(mul_3_mul), .c_i(add_1_c_o), .s(add_2_s), .c_o(add_2_c_o));
  D_FF d_ff_1 (.D(valid), .C(and_2_out), .Q(done));  // open: nQ
  Add #(.Bits(16)) add_3 (.a(add_2_s), .b(sum), .c_i(add_2_c_o), .s(q));  // open: c_o
endmodule
