// Digital circuit graphic-expand.dig as structural Verilog
module graphic_expand (
  input  clk,
  input  [23:0] x_i,
  input  load,
  input  valid,
  input  [7:0] b,
  input  clr,
  output [7:0] dout,
  output done
);

  wire and_1_out, comparator_1_gt, comparator_2_gt, undriven_3, undriven_7;
  wire [7:0] multiplexer_2_out, undriven_4, undriven_8;
  wire [15:0] undriven_2, undriven_6, undriven_9;
  wire [23:0] undriven, undriven_5;

  graphic_base graphic_base_1 (
    .x_i(x_i), .CLK(clk), .LOAD(load), .sum({16{1'b0}}), .valid(valid), .b(b), .Clr(clr));  // open: z_1, q, done, z_b
  graphic_base graphic_base_2 (
    .x_i(undriven), .CLK(clk), .LOAD(load), .sum(undriven_2), .valid(undriven_3), .b(undriven_4), .Clr(clr));  // open: z_1, q, done, z_b
  graphic_base graphic_base_3 (
    .x_i(undriven_5), .CLK(clk), .LOAD(load), .sum(undriven_6), .valid(undriven_7), .b(undriven_8), .Clr(clr));  // open: z_1, q, done, z_b
  Comparator #(.Bits(16)) comparator_1 (.a(undriven_9), .b(16'h7fff), .gt(comparator_1_gt));  // open: eq, lt
  Comparator #(.Bits(16)) comparator_2 (.a(undriven_9), .b(16'hff), .gt(comparator_2_gt));  // open: eq, lt
  and and_1 (and_1_out, comparator_1_gt, comparator_2_gt);
  Multiplexer #(.Bits(8)) multiplexer_1 (
    .sel(comparator_2_gt), .in_0(undriven_9[7:0]), .in_1(multiplexer_2_out), .out(dout));
  Multiplexer #(.Bits(8)) multiplexer_2 (.sel(and_1_out), .in_0({8{1'b1}}), .in_1({8{1'b0}}), .out(multiplexer_2_out));
endmodule
