// Digital circuit fir.dig as structural Verilog
module fir (
  input  [23:0] x_i,
  input  [7:0] b,
  input  clk,
  input  LOAD,
  input  Clr,
  input  valid,
  output [7:0] dout,
  output done
);

  wire and_1_out, comparator_1_gt, comparator_2_gt;
  wire [7:0] multiplexer_2_out;
  wire [15:0] fir_first_1_q;

  fir_first #(.generic("if (isPresent(args)) { if (args.order>1) { setCircuit(\"fir_inc.dig\"); } } else { export order:=1; }")) fir_first_1 (
    .x_i(x_i), .CLK(clk), .LOAD(LOAD), .sum({16{1'b0}}), .valid(valid), .b(b), .Clr(Clr), .q(fir_first_1_q),
    .done(done));  // open: z_1, z_b
  Comparator #(.Bits(16)) comparator_1 (.a(fir_first_1_q), .b(16'h7fff), .gt(comparator_1_gt));  // open: eq, lt
  Comparator #(.Bits(16)) comparator_2 (.a(fir_first_1_q), .b(16'hff), .gt(comparator_2_gt));  // open: eq, lt
  and and_1 (and_1_out, comparator_1_gt, comparator_2_gt);
  Multiplexer #(.Bits(8)) multiplexer_1 (
    .sel(comparator_2_gt), .in_0(fir_first_1_q[7:0]), .in_1(multiplexer_2_out), .out(dout));
  Multiplexer #(.Bits(8)) multiplexer_2 (.sel(and_1_out), .in_0({8{1'b1}}), .in_1({8{1'b0}}), .out(multiplexer_2_out));
endmodule
