// Digital circuit absolute-expand.dig as structural Verilog
module absolute_expand (
  input  P_0,
  input  P_1,
  input  P_2,
  input  P_3,
  input  P_4,
  output Q0,
  output Q1,
  output Q2,
  output Q3,
  output Q_4
);

  wire and_1_out, and_2_out, and_3_out, and_4_out, and_5_out, or_1_out, or_2_out, or_3_out, or_4_out;

  or or_1 (or_1_out, P_3, or_2_out);
  or or_2 (or_2_out, P_2, or_3_out);
  or or_3 (or_3_out, P_1, or_4_out);
  or or_4 (or_4_out, P_0, 1'b0);
  and and_1 (and_1_out, 1'b1, or_1_out);
  and and_2 (and_2_out, 1'b1, or_2_out);
  and and_3 (and_3_out, 1'b1, or_3_out);
  and and_4 (and_4_out, 1'b1, or_4_out);
  and and_5 (and_5_out, 1'b1, 1'b0);
  xor xor_1 (Q_4, and_1_out, P_4);
  xor xor_2 (Q3, and_2_out, P_3);
  xor xor_3 (Q2, and_3_out, P_2);
  xor xor_4 (Q1, and_4_out, P_1);
  xor xor_5 (Q0, and_5_out, P_0);

  // Notes on the sheet:
  //   P_0: First number to multiply.
  //   {{de Erste zu multiplizierende 4 Bit Zahl.}}
endmodule
