// Digital circuit TEST.dig as structural Verilog
module TEST (
  input  [4:0] P,
  output [4:0] Q
);

  // absolute #(.generic("dataBits :=5;")) absolute_1: pin names not known; wires that end beside it: P, Q
endmodule
