// Digital circuit absolute-final-inc.dig as structural Verilog
module absolute_final_inc (
  input  EN,
  input  [1:0] P,
  output [1:0] Q,
  output OT
);

  wire and_1_out, and_2_out;

  or or_1 (OT, P[0], 1'b0);
  and and_1 (and_1_out, EN, OT);
  and and_2 (and_2_out, EN, 1'b0);
  xor xor_1 (Q[1], and_1_out, P[1]);
  xor xor_2 (Q[0], and_2_out, P[0]);
endmodule
