// Digital circuit absolute-inc.dig as structural Verilog
module absolute_inc (
  input  EN,
  input  [2:0] P,
  output [2:0] Q,
  output OT
);

  wire absolute_final_inc_1_ot, and_1_out;

  or or_1 (OT, P[1], absolute_final_inc_1_ot);
  and and_1 (and_1_out, EN, OT);
  absolute_final_inc #(.generic("if (isPresent(args)) { if (args.dataBits>3) { export dataBits := args.dataBits-1; setCircuit(\"absolute-inc.dig\"); } } else { export dataBits := 3; }")) absolute_final_inc_1 (
    .EN(EN), .P(P[1:0]), .Q(Q[1:0]), .OT(absolute_final_inc_1_ot));
  xor xor_1 (Q[2], and_1_out, P[2]);
endmodule
