// Digital circuit absolute.dig as structural Verilog
module absolute (
  input  [1:0] P,
  output [1:0] Q
);

  absolute_final_inc #(.generic("if (isPresent(args)) { if (args.dataBits>2) { setCircuit(\"absolute-inc.dig\"); } else { export dataBits := args.dataBits+1; } } else { export dataBits:=3; }")) absolute_final_inc_1 (
    .EN(1'b1), .P(P), .Q(Q));  // open: OT
endmodule
