// Digital circuit ARMv8 CPU-II.dig as structural Verilog
module ARMv8_CPU_II (
  input  clock,
  input  hand,
  input  model,
  input  reset
);

  wire and_1_out, and_2_out, and_4_out, and_5_out, and_6_out, and_7_out, and_8_out, and_9_out, and_10_out,
       and_11_out, break_q, brk, C, C_plus, C_t, clk, comparator_1_eq, Dsel, multiplexer_13_out,
       multiplexer_16_out, N, N1, N2, nor_1_out, nor_2_out, nor_3_out, not_1_out, or_1_out, or_6_out,
       or_7_out, regw, V, xor_2_out, xor_3_out, Z, zero;
  wire [1:0] hw, pcsel;
  wire [1:1] shift;
  wire [2:0] cond;
  wire [3:0] aluop, VNCZ_q;
  wire [4:0] imm16, Irom_d, multiplexer_15_out;
  wire [5:0] imm6_s;
  wire [6:0] multiplexer_1_out;
  wire [10:6] imm12;
  wire [19:0] pc_q;
  wire [25:0] bitextender_1_out, multiplexer_2_out, multiplexer_5_out;
  wire [25:24] Irom_d_2;
  wire [31:26] Irom_d_3;
  wire [62:0] multiplexer_7_out, multiplexer_11_out, rs1;
  wire [63:0] add_1_s, add_2_s, and_3_out, ASR_out, bitextender_2_out, bitextender_3_out, LSL_MOV_out,
       LSL_out, LSR_out, multiplexer_3_out, multiplexer_4_out, multiplexer_6_out, multiplexer_8_out,
       multiplexer_9_out, multiplexer_10_out, multiplexer_12_out, multiplexer_14_out, or_2_out, plus_s,
       ROR_out, rs2, sub_s, xor_1_out;
  wire [63:20] pc_q_2;

  Multiplexer #(.Bits(7)) multiplexer_1 (
    .sel(aluop[3]), .in_0({1'b0, imm6_s}), .in_1({7{1'b0}}), .out(multiplexer_1_out));
  BitExtender #(.inputBits(19), .outputBits(26)) bitextender_1 (
    .in({shift[1], hw, imm12, imm6_s, imm16}), .out(bitextender_1_out));
  Register #(.Bits(4)) VNCZ (.D({V, N, C, Z}), .C(clk), .en(or_1_out), .Q(VNCZ_q));
  and and_1 (and_1_out, aluop[3], ~aluop[2]);  // And
  nor nor_1 (nor_1_out, aluop[3], aluop[2], ~aluop[1]);  // NOr
  BarrelShifter #(.Bits(64)) LSL (.in(rs2), .shift({1'b0, imm6_s}), .out(LSL_out));
  BarrelShifter #(.Bits(64), .direction("right")) LSR (.in(rs2), .shift({1'b0, imm6_s}), .out(LSR_out));
  BarrelShifter #(.Bits(64), .barrelShifterMode("arithmetic"), .direction("right")) ASR (
    .in(rs2), .shift({1'b0, imm6_s}), .out(ASR_out));
  BarrelShifter #(.Bits(64), .barrelShifterMode("rotate"), .direction("right")) ROR (
    .in(rs2), .shift(multiplexer_1_out), .out(ROR_out));
  Multiplexer #(.Bits(26)) multiplexer_2 (
    .sel(multiplexer_13_out), .in_0(26'h1), .in_1(bitextender_1_out), .out(multiplexer_2_out));
  or or_1 (or_1_out, and_1_out, nor_1_out);
  Multiplexer #(.Selector_Bits(2), .Bits(64)) multiplexer_3 (
    .sel({shift[1], hw[1]}), .in_0(LSL_out), .in_1(LSR_out), .in_2(ASR_out), .in_3(ROR_out),
    .out(multiplexer_3_out));
  BitExtender #(.inputBits(13), .outputBits(64)) bitextender_2 (.in({hw, imm12, imm6_s}), .out(bitextender_2_out));
  Multiplexer #(.Bits(64)) multiplexer_4 (
    .sel(hw[1]), .in_0({{52{1'b0}}, hw[0], imm12, imm6_s}),
    .in_1({{40{1'b0}}, hw[0], imm12, imm6_s, {12{1'b0}}}), .out(multiplexer_4_out));
  Multiplexer #(.Selector_Bits(2), .Bits(26)) multiplexer_5 (
    .sel(pcsel), .in_0(26'h1),
    .in_1({Irom_d_2, shift[1], hw, imm12, imm6_s, imm16, Irom_d[4], cond, Irom_d[0]}),
    .in_2(multiplexer_2_out), .in_3({26{1'b0}}), .out(multiplexer_5_out));
  BarrelShifter #(.Bits(64)) LSL_MOV (
    .in({{48{1'b0}}, imm12, imm6_s, imm16}), .shift({1'b0, hw, 4'b0000}), .out(LSL_MOV_out));
  Multiplexer #(.Bits(64)) multiplexer_6 (
    .sel(aluop[0]), .in_0(multiplexer_3_out), .in_1(bitextender_2_out), .out(multiplexer_6_out));
  Multiplexer #(.Bits(64)) multiplexer_7 (
    .sel(aluop[0]), .in_0(multiplexer_3_out), .in_1(multiplexer_4_out), .out({N2, multiplexer_7_out}));
  Multiplexer #(.Selector_Bits(2), .Bits(64)) multiplexer_8 (
    .sel(pcsel), .in_0({pc_q_2, pc_q}), .in_1({pc_q_2, pc_q}), .in_2({pc_q_2, pc_q}), .in_3({N1, rs1}),
    .out(multiplexer_8_out));
  BitExtender #(.inputBits(26), .outputBits(64)) bitextender_3 (.in(multiplexer_5_out), .out(bitextender_3_out));
  and and_2 (and_2_out, VNCZ_q[0], VNCZ_q[3]);
  nor nor_2 (nor_2_out, VNCZ_q[2], and_2_out);
  assign and_3_out = {N1, rs1} & multiplexer_6_out;  // And and_3, 64 bits wide
  assign or_2_out = {N1, rs1} | multiplexer_6_out;  // Or or_2, 64 bits wide
  assign xor_1_out = {N1, rs1} ^ multiplexer_6_out;  // XOr xor_1, 64 bits wide
  // Probe on bitextender_3_out
  // Probe on pcsel
  Comparator comparator_1 (.a(VNCZ_q[3]), .b(VNCZ_q[2]), .eq(comparator_1_eq));  // open: gt, lt
  Multiplexer #(.Bits(64)) multiplexer_9 (
    .sel(aluop[0]), .in_0({64{1'b0}}), .in_1(LSL_MOV_out), .out(multiplexer_9_out));
  Add #(.Bits(64)) plus (.a({N1, rs1}), .b({N2, multiplexer_7_out}), .c_i(1'b0), .s(plus_s), .c_o(C_plus));
  Sub #(.Bits(64)) sub (.a({N1, rs1}), .b({N2, multiplexer_7_out}), .c_i(1'b0), .s(sub_s), .c_o(C_t));
  Add #(.Bits(64)) add_1 (.a(multiplexer_8_out), .b(bitextender_3_out), .c_i(1'b0), .s(add_1_s));  // open: c_o
  Multiplexer #(.Selector_Bits(2), .Bits(64)) multiplexer_10 (
    .sel(aluop[2:1]), .in_0(multiplexer_9_out), .in_1(and_3_out), .in_2(or_2_out), .in_3(xor_1_out),
    .out(multiplexer_10_out));
  // Probe on aluop[2:1]
  // Probe on add_1_s
  Register #(.Bits(64)) pc (.D(add_1_s), .C(clk), .en(1'b1), .Q({pc_q_2, pc_q}));
  and and_4 (and_4_out, ~VNCZ_q[0], VNCZ_q[1]);  // And
  Multiplexer #(.Bits(64)) multiplexer_11 (
    .sel(aluop[3]), .in_0(multiplexer_10_out), .in_1(multiplexer_12_out), .out({N, multiplexer_11_out}));
  Multiplexer #(.Selector_Bits(2), .Bits(64)) multiplexer_12 (
    .sel(aluop[2:1]), .in_0(plus_s), .in_1(sub_s), .in_2({64{1'b0}}), .in_3({64{1'b0}}),
    .out(multiplexer_12_out));
  // Probe on {pc_q_2, pc_q}
  // Probe on {N, multiplexer_11_out}
  Add #(.Bits(64)) add_2 (.a({pc_q_2, pc_q}), .b(64'h1), .c_i(1'b0), .s(add_2_s));  // open: c_o
  // Probe on pc_q
  ROM #(.AddrBits(20), .Bits(32)) Irom (
    .A(pc_q), .sel(1'b1),
    .D({Irom_d_3, Irom_d_2, shift[1], hw, imm12, imm6_s, imm16, Irom_d[4], cond, Irom_d[0]}));
  Multiplexer #(.Selector_Bits(3)) multiplexer_13 (
    .sel(cond), .in_0(VNCZ_q[0]), .in_1(VNCZ_q[1]), .in_2(VNCZ_q[2]), .in_3(VNCZ_q[3]), .in_4(and_4_out),
    .in_5(comparator_1_eq), .in_6(nor_2_out), .in_7(1'b0), .out(multiplexer_13_out));
  Comparator #(.Bits(64)) comparator_2 (.a({64{1'b0}}), .b({N, multiplexer_11_out}), .eq(Z));  // open: gt, lt
  xor xor_2 (xor_2_out, N1, N2);
  Multiplexer #(.Bits(64)) multiplexer_14 (
    .sel(Dsel), .in_0({N, multiplexer_11_out}), .in_1(add_2_s), .out(multiplexer_14_out));
  // Probe on cond
  xor xor_3 (xor_3_out, N, N1);
  not not_1 (not_1_out, xor_2_out);
  and and_5 (and_5_out, aluop[3], ~aluop[2], aluop[1]);  // And
  and and_6 (and_6_out, aluop[3], aluop[2], ~aluop[1]);  // And
  Multiplexer #(.Bits(5)) multiplexer_15 (
    .sel(Dsel), .in_0({Irom_d[4], cond, Irom_d[0]}), .in_1(5'b11110), .out(multiplexer_15_out));
  and and_7 (and_7_out, reset, multiplexer_16_out);
  Multiplexer multiplexer_16 (.sel(model), .in_0(hand), .in_1(clock), .out(multiplexer_16_out));
  and and_8 (and_8_out, xor_3_out, not_1_out, and_5_out);
  and and_9 (and_9_out, xor_3_out, xor_2_out, and_6_out);
  and and_10 (and_10_out, and_5_out, C_plus);
  and and_11 (and_11_out, and_6_out, C_t);
  RegisterFile #(.AddrBits(5), .Bits(64)) regs (
    .Din(multiplexer_14_out), .we(regw), .Rw(multiplexer_15_out), .C(clk), .Ra(imm16), .Rb(imm12),
    .Da({N1, rs1}), .Db(rs2));
  // Probe on {Irom_d_3, Irom_d_2, shift[1], hw, imm12, imm6_s, imm16, Irom_d[4], cond, Irom_d[0]}
  or or_3 (clk, break_q, multiplexer_16_out);
  or or_4 (V, and_8_out, and_9_out);
  or or_5 (C, and_10_out, and_11_out);
  D_FF_AS \break  (.Set(1'b0), .D(brk), .C(clk), .Clr(and_7_out), .Q(break_q));  // open: nQ
  // Probe on {N1, rs1}
  LED led_1 (.in(break_q));
  Comparator #(.Bits(5)) comparator_3 (.a({Irom_d[4], cond, Irom_d[0]}), .b({5{1'b1}}), .eq(zero));  // open: gt, lt
  aluop_II aluop_ii_1 (
    ._30(Irom_d_3[30]), ._29(Irom_d_3[29]), ._28(Irom_d_3[28]), ._27(Irom_d_3[27]), ._26(Irom_d_3[26]),
    ._25(Irom_d_2[25]), ._24(Irom_d_2[24]), ._23(shift[1]), ._3(aluop[3]), ._2(aluop[2]), ._1(aluop[1]),
    ._0(aluop[0]));
  and and_12 (brk, Irom_d_3[31], Irom_d_3[30], Irom_d_3[28], Irom_d_3[26], nor_3_out);
  nor nor_3 (nor_3_out, Irom_d_3[29], Irom_d_3[27], Irom_d_2[25]);
  or or_6 (or_6_out, aluop[3], aluop[2], aluop[1], aluop[0]);
  Dsel dsel_1 (
    ._31(Irom_d_3[31]), ._30(Irom_d_3[30]), ._29(Irom_d_3[29]), ._28(Irom_d_3[28]), ._27(Irom_d_3[27]),
    ._26(Irom_d_3[26]), ._25(Irom_d_2[25]), ._21(hw[0]), .Y(Dsel));
  pcsel pcsel_1 (
    ._31(Irom_d_3[31]), ._30(Irom_d_3[30]), ._29(Irom_d_3[29]), ._28(Irom_d_3[28]), ._27(Irom_d_3[27]),
    ._26(Irom_d_3[26]), ._25(Irom_d_2[25]), ._1(pcsel[1]), ._0(pcsel[0]));
  and and_13 (regw, ~zero, or_7_out);  // And
  or or_7 (or_7_out, or_6_out, Dsel);

  // Other names for the same wires on the sheet: imm12 (some bits) = {hw[0], imm6_s}; imm16[15:5] = {imm12, imm6_s};
  //   immr[5:0] = {hw[0], imm12}; sh_N = hw[1]; shift[0] = hw[1]; rs1[63] = N1

  // Notes on the sheet:
  //   clock: Hz: 2
  //   ALU
  //   PC
  //   B
  //   B.cond
  //   BR
  //   MOVZ
  //   contents of Irom (hex, n*v repeats v):
  //   d2800020,d2800021,d2800082,b1000421,ab010000,f1000442,54000040,97fffffc,d4200000
  //   controller II
endmodule
