// Digital circuit Dsel.dig as structural Verilog
module Dsel (
  input  _31,
  input  _30,
  input  _29,
  input  _28,
  input  _27,
  input  _26,
  input  _25,
  input  _21,
  output Y
);

  wire and_1_out, and_2_out, not_1_out, not_2_out, not_3_out;

  not not_1 (not_1_out, _30);
  not not_2 (not_2_out, _29);
  not not_3 (not_3_out, _27);
  and and_1 (and_1_out, _21, _25, _26, not_3_out, _28, not_2_out, _31);
  and and_2 (and_2_out, _26, not_3_out, _28, not_2_out, not_1_out, _31);
  or or_1 (Y, and_1_out, and_2_out);
endmodule
