// Digital circuit aluop III.dig as structural Verilog
module aluop_III (
  input  _30,
  input  _29,
  input  _28,
  input  _27,
  input  _26,
  input  _25,
  input  _24,
  input  _23,
  output _3,
  output _2,
  output _1,
  output _0
);

  wire and_1_out, and_2_out, and_3_out, and_4_out, and_5_out, and_6_out, and_7_out, and_8_out, and_9_out,
       and_10_out, and_11_out, and_12_out, and_13_out, and_14_out, and_15_out, and_16_out, and_17_out,
       and_18_out, not_1_out, not_2_out, not_3_out, not_4_out, not_5_out, not_6_out, not_7_out, not_8_out;

  not not_1 (not_1_out, _30);
  not not_2 (not_2_out, _29);
  not not_3 (not_3_out, _28);
  not not_4 (not_4_out, _27);
  not not_5 (not_5_out, _26);
  not not_6 (not_6_out, _25);
  not not_7 (not_7_out, _24);
  not not_8 (not_8_out, _23);
  and and_1 (and_1_out, not_8_out, not_6_out, not_5_out, _27, _28, _29);
  and and_2 (and_2_out, _24, _25, not_5_out, _27, not_3_out, _29);
  and and_3 (and_3_out, _24, not_6_out, not_5_out, not_4_out, _28, _29);
  and and_4 (and_4_out, not_8_out, not_7_out, _25, not_5_out, not_4_out, _28, not_2_out, _30);
  and and_5 (and_5_out, not_8_out, not_6_out, not_5_out, _27, _28, _29);
  and and_6 (and_6_out, not_7_out, _25, not_5_out, _27, not_3_out, _29, not_1_out);
  and and_7 (and_7_out, not_7_out, _25, not_5_out, not_4_out, _28, _29, not_1_out);
  and and_8 (and_8_out, not_7_out, _25, not_5_out, _27, not_3_out, not_2_out, _30);
  and and_9 (and_9_out, not_8_out, not_7_out, _25, not_5_out, not_4_out, _28, _30);
  and and_10 (and_10_out, not_8_out, not_6_out, not_5_out, _27, _28, _29);
  and and_11 (and_11_out, _24, not_6_out, not_5_out, not_4_out, _28, _29, _30);
  and and_12 (and_12_out, not_7_out, _25, not_5_out, not_4_out, _28, _29, _30);
  and and_13 (and_13_out, not_7_out, _25, not_5_out, _27, not_3_out, _30);
  and and_14 (and_14_out, _25, not_5_out, _27, not_3_out, _29, _30);
  and and_15 (and_15_out, not_8_out, not_6_out, not_5_out, _27, _28, _29);
  and and_16 (and_16_out, _24, not_6_out, not_5_out, not_4_out, _28, _29);
  and and_17 (and_17_out, not_7_out, _25, not_5_out, not_4_out, _28, _29);
  and and_18 (and_18_out, not_7_out, _25, not_5_out, not_4_out, _28, _30);
  or or_1 (_3, and_1_out, and_2_out, and_3_out);
  or or_2 (_2, and_4_out, and_5_out, and_6_out, and_7_out, and_8_out);
  or or_3 (_0, and_15_out, and_16_out, and_17_out, and_18_out);
  or or_4 (_1, and_9_out, and_10_out, and_11_out, and_12_out, and_13_out, and_14_out);
endmodule
