// Digital circuit mem.dig as structural Verilog
module mem (
  input  _29,
  input  _28,
  input  _27,
  input  _24,
  input  _22,
  input  _11,
  input  _10,
  input  M2,
  output memw,
  output index1,
  output index0,
  output rwsel1,
  output rwsel0
);

  wire and_1_out, and_2_out, and_3_out, and_4_out, and_5_out, and_6_out, and_7_out, not_1_out, not_2_out,
       not_3_out, not_4_out;

  not not_1 (not_1_out, _24);
  not not_2 (not_2_out, _22);
  not not_3 (not_3_out, _11);
  not not_4 (not_4_out, M2);
  and and_1 (and_1_out, _10, not_2_out, _27, _28, _29, not_4_out);
  and and_2 (and_2_out, not_2_out, _24, _27, _28, _29, not_4_out);
  and and_3 (and_3_out, _10, not_3_out, _27, _28, _29, not_4_out);
  and and_4 (and_4_out, _24, _27, _28, _29, not_4_out);
  and and_5 (and_5_out, _10, _11, _27, _28, _29, not_4_out);
  and and_6 (and_6_out, _10, not_1_out, _27, _28, _29, M2);
  and and_7 (and_7_out, _24, _27, _28, _29, not_4_out);
  and and_8 (rwsel1, _10, not_1_out, _27, _28, _29, M2);
  or or_1 (memw, and_1_out, and_2_out);
  or or_2 (index1, and_3_out, and_4_out);
  or or_3 (index0, and_5_out, and_6_out, and_7_out);

  assign rwsel0 = 1'b0;
endmodule
