// Digital circuit pcsel.dig as structural Verilog
module pcsel (
  input  _31,
  input  _30,
  input  _29,
  input  _28,
  input  _27,
  input  _26,
  input  _25,
  output _1,
  output _0
);

  wire and_1_out, and_2_out, and_3_out, and_4_out, not_1_out, not_2_out, not_3_out, not_4_out, not_5_out;

  not not_1 (not_1_out, _31);
  not not_2 (not_2_out, _30);
  not not_3 (not_3_out, _29);
  not not_4 (not_4_out, _27);
  not not_5 (not_5_out, _25);
  and and_1 (and_1_out, not_5_out, _26, not_4_out, _28, not_3_out, _30, not_1_out);
  and and_2 (and_2_out, _25, _26, not_4_out, _28, not_3_out, _30, _31);
  and and_3 (and_3_out, _25, _26, not_4_out, _28, not_3_out, _31);
  and and_4 (and_4_out, _26, not_4_out, _28, not_3_out, not_2_out);
  or or_1 (_1, and_1_out, and_2_out);
  or or_2 (_0, and_3_out, and_4_out);
endmodule
