// Digital circuit jk.dig as structural Verilog
module jk (
  input  Set,
  input  en,
  input  J,
  input  C,
  input  K,
  input  Clr,
  output Q,
  output nQ
);

  wire and_1_out, and_2_out;

  and and_1 (and_1_out, J, en);
  and and_2 (and_2_out, en, K);
  JK_FF_AS jk_ff_as_1 (.Set(Set), .J(and_1_out), .C(C), .K(and_2_out), .Clr(Clr), .Q(Q), .nQ(nQ));
endmodule
