// Digital circuit sync.dig as structural Verilog
// Designed for a 
// 25.175MHz clock.
// Generates 
// 640x480@60Hz
// {{de Ausgelegt für einen 
// 25.175MHz Takt.
// Erzeugt
// 640x480@60Hz}}
module sync (
  input  RST,
  input  C,
  output vld,
  output H,
  output V
);

  wire and_1_out, comparator_1_eq, comparator_2_eq, comparator_3_eq, comparator_4_eq, comparator_5_eq,
       comparator_6_eq, comparator_7_eq, comparator_8_eq, jk_1_q, jk_ff_1_q, not_1_out, or_1_out, or_2_out;
  wire [9:0] h_cnt_out, v_cnt_out;

  or or_1 (or_1_out, ~RST, comparator_2_eq);  // Or
  Counter #(.Bits(10)) h_cnt (.en(1'b1), .C(C), .clr(or_1_out), .out(h_cnt_out));  // open: ovf
  Comparator #(.Bits(10)) comparator_1 (.a(h_cnt_out), .b(10'h2bf), .eq(comparator_1_eq));  // open: gt, lt
  Comparator #(.Bits(10)) comparator_2 (.a(h_cnt_out), .b(10'h31f), .eq(comparator_2_eq));  // open: gt, lt
  Comparator #(.Bits(10)) comparator_3 (.a(h_cnt_out), .b(10'h2b2), .eq(comparator_3_eq));  // open: gt, lt
  Comparator #(.Bits(10)) comparator_4 (.a(h_cnt_out), .b(10'h2c), .eq(comparator_4_eq));  // open: gt, lt
  and and_1 (and_1_out, comparator_2_eq, comparator_8_eq);
  or or_2 (or_2_out, and_1_out, ~RST);  // Or
  JK_FF_AS jk_ff_as_1 (.Set(1'b0), .J(comparator_1_eq), .C(C), .K(comparator_2_eq), .Clr(~RST), .nQ(H));  // open: Q
  JK_FF jk_ff_1 (.J(comparator_4_eq), .C(C), .K(comparator_3_eq), .Q(jk_ff_1_q));  // open: nQ
  Counter #(.Bits(10)) v_cnt (.en(comparator_2_eq), .C(C), .clr(or_2_out), .out(v_cnt_out));  // open: ovf
  not not_1 (not_1_out, RST);
  Comparator #(.Bits(10)) comparator_5 (.a(v_cnt_out), .b(10'h1d), .eq(comparator_5_eq));  // open: gt, lt
  Comparator #(.Bits(10)) comparator_6 (.a(v_cnt_out), .b(10'h201), .eq(comparator_6_eq));  // open: gt, lt
  Comparator #(.Bits(10)) comparator_7 (.a(v_cnt_out), .b(10'h20a), .eq(comparator_7_eq));  // open: gt, lt
  Comparator #(.Bits(10)) comparator_8 (.a(v_cnt_out), .b(10'h20c), .eq(comparator_8_eq));  // open: gt, lt
  jk jk_1 (
    .Set(1'b0), .en(comparator_2_eq), .J(comparator_5_eq), .C(C), .K(comparator_6_eq), .Clr(1'b0), .Q(jk_1_q));  // open: nQ
  jk jk_2 (
    .Set(1'b0), .en(comparator_2_eq), .J(comparator_7_eq), .C(C), .K(comparator_8_eq), .Clr(not_1_out), .nQ(V));  // open: Q
  and and_2 (vld, jk_ff_1_q, jk_1_q);
endmodule
