// Digital circuit CORDIC_0_90.dig as structural Verilog
module CORDIC_0_90 (
  input  clk,
  input  RESET,
  input  [6:0] address,
  output [6:0] value
);

  wire not_1_out;
  wire [5:0] d_ff_as_1_q, multiplexer_1_out;
  wire [6:0] cordic_element_1_z_k1, cordic_element_2_z_k1, cordic_element_3_z_k1, cordic_element_4_z_k1,
       cordic_element_5_z_k1, cordic_element_6_z_k1;
  wire [9:0] cordic_element_1_x_k1, cordic_element_1_y_k1, cordic_element_2_x_k1, cordic_element_2_y_k1,
       cordic_element_3_x_k1, cordic_element_3_y_k1, cordic_element_4_x_k1, cordic_element_4_y_k1,
       cordic_element_5_x_k1, cordic_element_5_y_k1, cordic_element_6_x_k1, cordic_element_6_y_k1,
       cordic_element_7_y_k1;

  not not_1 (not_1_out, RESET);
  Multiplexer #(.Bits(6)) multiplexer_1 (
    .sel(address[6]), .in_0(address[5:0]), .in_1({6{1'b1}}), .out(multiplexer_1_out));
  D_FF_AS #(.Bits(6)) d_ff_as_1 (
    .Set(1'b0), .D(multiplexer_1_out), .C(clk), .Clr(not_1_out), .Q(d_ff_as_1_q));  // open: nQ
  CORDIC_element cordic_element_1 (
    .x_k(10'h136), .y_k({10{1'b0}}), .z_k({1'b0, d_ff_as_1_q}), .clk(clk), .RESET(not_1_out), .order(3'b000),
    .e_k(6'b100000), .x_k1(cordic_element_1_x_k1), .y_k1(cordic_element_1_y_k1), .z_k1(cordic_element_1_z_k1));
  CORDIC_element cordic_element_2 (
    .x_k(cordic_element_1_x_k1), .y_k(cordic_element_1_y_k1), .z_k(cordic_element_1_z_k1), .clk(clk),
    .RESET(not_1_out), .order(3'b001), .e_k(6'b010011), .x_k1(cordic_element_2_x_k1),
    .y_k1(cordic_element_2_y_k1), .z_k1(cordic_element_2_z_k1));
  CORDIC_element cordic_element_3 (
    .x_k(cordic_element_2_x_k1), .y_k(cordic_element_2_y_k1), .z_k(cordic_element_2_z_k1), .clk(clk),
    .RESET(not_1_out), .order(3'b010), .e_k(6'b001010), .x_k1(cordic_element_3_x_k1),
    .y_k1(cordic_element_3_y_k1), .z_k1(cordic_element_3_z_k1));
  CORDIC_element cordic_element_4 (
    .x_k(cordic_element_3_x_k1), .y_k(cordic_element_3_y_k1), .z_k(cordic_element_3_z_k1), .clk(clk),
    .RESET(not_1_out), .order(3'b011), .e_k(6'b000101), .x_k1(cordic_element_4_x_k1),
    .y_k1(cordic_element_4_y_k1), .z_k1(cordic_element_4_z_k1));
  CORDIC_element cordic_element_5 (
    .x_k(cordic_element_4_x_k1), .y_k(cordic_element_4_y_k1), .z_k(cordic_element_4_z_k1), .clk(clk),
    .RESET(not_1_out), .order(3'b100), .e_k(6'b000011), .x_k1(cordic_element_5_x_k1),
    .y_k1(cordic_element_5_y_k1), .z_k1(cordic_element_5_z_k1));
  CORDIC_element cordic_element_6 (
    .x_k(cordic_element_5_x_k1), .y_k(cordic_element_5_y_k1), .z_k(cordic_element_5_z_k1), .clk(clk),
    .RESET(not_1_out), .order(3'b101), .e_k(6'b000001), .x_k1(cordic_element_6_x_k1),
    .y_k1(cordic_element_6_y_k1), .z_k1(cordic_element_6_z_k1));
  CORDIC_element cordic_element_7 (
    .x_k(cordic_element_6_x_k1), .y_k(cordic_element_6_y_k1), .z_k(cordic_element_6_z_k1), .clk(clk),
    .RESET(not_1_out), .order(3'b110), .e_k(6'b000001), .y_k1(cordic_element_7_y_k1));  // open: x_k1, z_k1
  D_FF_AS #(.Bits(7)) d_ff_as_2 (
    .Set(1'b0), .D(cordic_element_7_y_k1[8:2]), .C(clk), .Clr(not_1_out), .Q(value));  // open: nQ
endmodule

/* Test case:
clk 	RESET	address		value		
0	1	0b1000000	0b0000000	
1	1	0b1000000	0b0000000	
0	1	0b0111111	0b0000000	
1	1	0b0111111	0b0000000	
0	1	0b0111110	0b0000000	
1	1	0b0111110	0b0000000	
0	1	0b0111101	0b0000000	
1	1	0b0111101	0b0000000	
0	1	0b0111100	0b0000000	
1	1	0b0111100	0b0000000	
0	1	0b1000000	0b0000000	
1	1	0b1000000	0b0000000	
0	1	0b1000000	0b0000000	
1	1	0b1000000	0b0000000	
0	1	0b1000000	0b0000000	
1	1	0b1000000	0b0000000	
0	1	0b0000100	0b0000000	
1	1	0b0000100	0b0000000	
0	1	0b0001001	0b0000000	
1	1	0b0001001	0b0000000	
0	1	0b0001010	0b0000000	
1	1	0b0001010	0b0000000	
0	1	0b0001011	0b0000000	
1	1	0b0001011	0b0000000	
0	1	0b0001100	0b0000000	
1	1	0b0001100	0b0000000	
0	1	0b0001101	0b0000000	
1	1	0b0001101	0b0000000	
0	1	0b0001110	0b0000000	
1	1	0b0001110	0b0000000	
0	1	0b0001111	0b0000000	
1	1	0b0001111	0b0000000	
*/
