// Digital circuit CORDIC_element.dig as structural Verilog
module CORDIC_element (
  input  [9:0] x_k,
  input  [9:0] y_k,
  input  [6:0] z_k,
  input  clk,
  input  RESET,
  input  [2:0] order,
  input  [5:0] e_k,
  output [9:0] x_k1,
  output [9:0] y_k1,
  output [6:0] z_k1
);

  wire [6:0] add_3_s, multiplexer_2_out, sub_3_s;
  wire [9:0] add_1_s, add_2_s, multiplexer_1_out, multiplexer_3_out, shift_right_1_shifted,
       shift_right_2_shifted, sub_1_s, sub_2_s;

  shift_right shift_right_1 (.x(x_k), .order(order), .shifted(shift_right_1_shifted));
  shift_right shift_right_2 (.x(y_k), .order(order), .shifted(shift_right_2_shifted));
  Sub #(.Bits(10)) sub_1 (.a(x_k), .b(shift_right_2_shifted), .c_i(1'b0), .s(sub_1_s));  // open: c_o
  Add #(.Bits(10)) add_1 (.a(x_k), .b(shift_right_2_shifted), .c_i(1'b0), .s(add_1_s));  // open: c_o
  Add #(.Bits(10)) add_2 (.a(y_k), .b(shift_right_1_shifted), .c_i(1'b0), .s(add_2_s));  // open: c_o
  Sub #(.Bits(10)) sub_2 (.a(y_k), .b(shift_right_1_shifted), .c_i(1'b0), .s(sub_2_s));  // open: c_o
  Sub #(.Bits(7)) sub_3 (.a(z_k), .b({1'b0, e_k}), .c_i(1'b0), .s(sub_3_s));  // open: c_o
  Add #(.Bits(7)) add_3 (.a(z_k), .b({1'b0, e_k}), .c_i(1'b0), .s(add_3_s));  // open: c_o
  Multiplexer #(.Bits(10)) multiplexer_1 (.sel(z_k[6]), .in_0(sub_1_s), .in_1(add_1_s), .out(multiplexer_1_out));
  Multiplexer #(.Bits(7)) multiplexer_2 (.sel(z_k[6]), .in_0(sub_3_s), .in_1(add_3_s), .out(multiplexer_2_out));
  Multiplexer #(.Bits(10)) multiplexer_3 (.sel(z_k[6]), .in_0(add_2_s), .in_1(sub_2_s), .out(multiplexer_3_out));
  D_FF_AS #(.Bits(10)) d_ff_as_1 (.Set(1'b0), .D(multiplexer_1_out), .C(clk), .Clr(RESET), .Q(x_k1));  // open: nQ
  D_FF_AS #(.Bits(10)) d_ff_as_2 (.Set(1'b0), .D(multiplexer_3_out), .C(clk), .Clr(RESET), .Q(y_k1));  // open: nQ
  D_FF_AS #(.Bits(7)) d_ff_as_3 (.Set(1'b0), .D(multiplexer_2_out), .C(clk), .Clr(RESET), .Q(z_k1));  // open: nQ
endmodule

/* Test case:
clk	RESET	order	x_k		y_k		z_k		x_k1		y_k1		z_k1		
0	0	0	0b0100110110	0b0000000000	0b0000000	0b0000000000	0b0000000000	0b000000	
1	0	0	0b0100110110	0b0000000000	0b0000000	0b0000000000	0b0000000000	0b000000	
0	0	0	0b0100110110	0b0000000000	0b0000001	0b0000000000	0b0000000000	0b000000	
1	0	0	0b0100110110	0b0000000000	0b0000001	0b0000000000	0b0000000000	0b000000	
0	0	0	0b0100110110	0b0000000000	0b0000010	0b0000000000	0b0000000000	0b000000	
1	0	0	0b0100110110	0b0000000000	0b0000010	0b0000000000	0b0000000000	0b000000	
0	0	0	0b0100110110	0b0000000000	0b0000010	0b0000000000	0b0000000000	0b000000	
1	0	0	0b0100110110	0b0000000000	0b0000010	0b0000000000	0b0000000000	0b000000	
*/
