// Digital circuit DDS_CORDIC.dig as structural Verilog
module DDS_CORDIC (
  input  clk,
  input  RESET,
  input  SET,
  input  [7:0] step_in,
  output [7:0] value,
  output zero_address
);

  wire [6:0] cordic_0_90_1_value, dds_without_valuetable_1_table_address;

  CORDIC_0_90 cordic_0_90_1 (
    .clk(clk), .RESET(RESET), .address(dds_without_valuetable_1_table_address), .value(cordic_0_90_1_value));
  DDS_without_ValueTable dds_without_valuetable_1 (
    .clk(clk), .RESET(RESET), .SET(SET), .step_in(step_in), .table_value(cordic_0_90_1_value),
    .table_address(dds_without_valuetable_1_table_address), .value(value), .zero_address(zero_address));
endmodule
