// Digital circuit DDS_Line.dig as structural Verilog
module DDS_Line (
  input  clk,
  input  RESET,
  input  SET,
  input  [7:0] step_in,
  output [7:0] value,
  output zero_address
);

  wire [6:0] dds_without_valuetable_1_table_address, line_sin_0_90_1_value;

  Line_sin_0_90 line_sin_0_90_1 (
    .address(dds_without_valuetable_1_table_address), .clk(clk), .RESET(RESET), .value(line_sin_0_90_1_value));
  DDS_without_ValueTable dds_without_valuetable_1 (
    .clk(clk), .RESET(RESET), .SET(SET), .step_in(step_in), .table_value(line_sin_0_90_1_value),
    .table_address(dds_without_valuetable_1_table_address));  // open: value, zero_address
endmodule

/* Test case:
clk	RESET	SET	step_in		zero_address	value
0	1	0	0b00000001	0		0b0000000
1	1	0	0b00000001	0		0b0000000
0	1	0	0b00000001	0		0b0000000
1	1	0	0b00000001	0		0b0000000
0	1	0	0b00000001	0		0b0000000
1	1	0	0b00000001	0		0b0000000
0	1	0	0b00000001	0		0b0000000
1	1	0	0b00000001	0		0b0000000
0	1	0	0b00000001	0		0b0000000
1	1	0	0b00000001	0		0b0000000
0	1	0	0b00000001	0		0b0000000
1	1	0	0b00000001	0		0b0000000
0	1	0	0b00000001	0		0b0000000
1	1	0	0b00000001	0		0b0000000
0	1	0	0b00000001	0		0b0000000
1	1	0	0b00000001	0		0b0000000
0	1	0	0b00000001	0		0b0000000
1	1	0	0b00000001	0		0b0000000
0	1	0	0b00000001	0		0b0000000
1	1	0	0b00000001	0		0b0000000
0	1	0	0b00000001	0		0b0000000
1	1	0	0b00000001	0		0b0000000
0	1	0	0b00000001	0		0b0000000
1	1	0	0b00000001	0		0b0000000
0	1	0	0b00000001	0		0b0000000
1	1	0	0b00000001	0		0b0000000
0	1	0	0b00000001	0		0b0000000
1	1	0	0b00000001	0		0b0000000
0	1	0	0b00000001	0		0b0000000
1	1	0	0b00000001	0		0b0000000
0	1	0	0b00000001	0		0b0000000
1	1	0	0b00000001	0		0b0000000
0	1	0	0b00000001	0		0b0000000
1	1	0	0b00000001	0		0b0000000
0	1	0	0b00000001	0		0b0000000
1	1	0	0b00000001	0		0b0000000
0	1	0	0b00000001	0		0b0000000
1	1	0	0b00000001	0		0b0000000
0	1	0	0b00000001	0		0b0000000
1	1	0	0b00000001	0		0b0000000
0	1	0	0b00000001	0		0b0000000
1	1	0	0b00000001	0		0b0000000
0	1	0	0b00000001	0		0b0000000
1	1	0	0b00000001	0		0b0000000
0	1	0	0b00000001	0		0b0000000
1	1	0	0b00000001	0		0b0000000
0	1	0	0b00000001	0		0b0000000
1	1	0	0b00000001	0		0b0000000
0	1	0	0b00000001	0		0b0000000
1	1	0	0b00000001	0		0b0000000
0	1	0	0b00000001	0		0b0000000
1	1	0	0b00000001	0		0b0000000
0	1	0	0b00000001	0		0b0000000
1	1	0	0b00000001	0		0b0000000
0	1	0	0b00000001	0		0b0000000
1	1	0	0b00000001	0		0b0000000
0	1	0	0b00000001	0		0b0000000
1	1	0	0b00000001	0		0b0000000
0	1	0	0b00000001	0		0b0000000
1	1	0	0b00000001	0		0b0000000
0	1	0	0b00000001	0		0b0000000
1	1	0	0b00000001	0		0b0000000
0	1	0	0b00000001	0		0b0000000
1	1	0	0b00000001	0		0b0000000
0	1	0	0b00000001	0		0b0000000
1	1	0	0b00000001	0		0b0000000
0	1	0	0b00000001	0		0b0000000
1	1	0	0b00000001	0		0b0000000
0	1	0	0b00000001	0		0b0000000
1	1	0	0b00000001	0		0b0000000
0	1	0	0b00000001	0		0b0000000
1	1	0	0b00000001	0		0b0000000
0	1	0	0b00000001	0		0b0000000
1	1	0	0b00000001	0		0b0000000
0	1	0	0b00000001	0		0b0000000
1	1	0	0b00000001	0		0b0000000
0	1	0	0b00000001	0		0b0000000
1	1	0	0b00000001	0		0b0000000
0	1	0	0b00000001	0		0b0000000
1	1	0	0b00000001	0		0b0000000
*/
