// Digital circuit DDS_ROM.dig as structural Verilog
module DDS_ROM (
  input  RESET,
  input  clk,
  input  SET,
  input  [7:0] step_in,
  output [7:0] value,
  output zero_address
);

  wire [6:0] dds_without_valuetable_1_p5, dds_without_valuetable_1_p6;

  // DDS_without_ValueTable dds_without_valuetable_1: pin names not known; wires that end beside it: clk, RESET, SET, step_in, dds_without_valuetable_1_p5, dds_without_valuetable_1_p6, value, zero_address
  ROM #(.AddrBits(7), .Bits(7)) Sine (.A(dds_without_valuetable_1_p6), .sel(1'b1), .D(dds_without_valuetable_1_p5));

  // Notes on the sheet:
  //   contents of Sine (hex, n*v repeats v):
  //   0,4,7,a,d,10,13,16,19,1c,1f,22,25,28,2b,2e,31,34,37,3a,3c,3f,42,44,47,4a,4c,4f,51,
  //   53,56,58,5a,5c,5f,61,63,65,67,68,6a,6c,6d,6f,71,72,73,75,76,77,78,79,7a,7b,7c,7c,
  //   7d,7e,7e,7f,7f,7f,7f,7f,7f
endmodule

/* Test case:
clk	RESET	SET	step_in		zero_address	value
0	1	0	0b00000001	0		0b0000000
1	1	0	0b00000001	0		0b0000000
0	1	0	0b00000001	0		0b0000000
1	1	0	0b00000001	0		0b0000000
0	1	0	0b00000001	0		0b0000000
1	1	0	0b00000001	0		0b0000000
0	1	0	0b00000001	0		0b0000000
1	1	0	0b00000001	0		0b0000000
0	1	0	0b00000001	0		0b0000000
1	1	0	0b00000001	0		0b0000000
0	1	0	0b00000001	0		0b0000000
1	1	0	0b00000001	0		0b0000000
0	1	0	0b00000001	0		0b0000000
1	1	0	0b00000001	0		0b0000000
0	1	0	0b00000001	0		0b0000000
1	1	0	0b00000001	0		0b0000000
0	1	0	0b00000001	0		0b0000000
1	1	0	0b00000001	0		0b0000000
0	1	0	0b00000001	0		0b0000000
1	1	0	0b00000001	0		0b0000000
0	1	0	0b00000001	0		0b0000000
1	1	0	0b00000001	0		0b0000000
0	1	0	0b00000001	0		0b0000000
1	1	0	0b00000001	0		0b0000000
0	1	0	0b00000001	0		0b0000000
1	1	0	0b00000001	0		0b0000000
0	1	0	0b00000001	0		0b0000000
1	1	0	0b00000001	0		0b0000000
0	1	0	0b00000001	0		0b0000000
1	1	0	0b00000001	0		0b0000000
0	1	0	0b00000001	0		0b0000000
1	1	0	0b00000001	0		0b0000000
0	1	0	0b00000001	0		0b0000000
1	1	0	0b00000001	0		0b0000000
0	1	0	0b00000001	0		0b0000000
1	1	0	0b00000001	0		0b0000000
0	1	0	0b00000001	0		0b0000000
1	1	0	0b00000001	0		0b0000000
0	1	0	0b00000001	0		0b0000000
1	1	0	0b00000001	0		0b0000000
0	1	0	0b00000001	0		0b0000000
1	1	0	0b00000001	0		0b0000000
0	1	0	0b00000001	0		0b0000000
1	1	0	0b00000001	0		0b0000000
0	1	0	0b00000001	0		0b0000000
1	1	0	0b00000001	0		0b0000000
0	1	0	0b00000001	0		0b0000000
1	1	0	0b00000001	0		0b0000000
0	1	0	0b00000001	0		0b0000000
1	1	0	0b00000001	0		0b0000000
0	1	0	0b00000001	0		0b0000000
1	1	0	0b00000001	0		0b0000000
0	1	0	0b00000001	0		0b0000000
1	1	0	0b00000001	0		0b0000000
0	1	0	0b00000001	0		0b0000000
1	1	0	0b00000001	0		0b0000000
0	1	0	0b00000001	0		0b0000000
1	1	0	0b00000001	0		0b0000000
0	1	0	0b00000001	0		0b0000000
1	1	0	0b00000001	0		0b0000000
0	1	0	0b00000001	0		0b0000000
1	1	0	0b00000001	0		0b0000000
0	1	0	0b00000001	0		0b0000000
1	1	0	0b00000001	0		0b0000000
0	1	0	0b00000001	0		0b0000000
1	1	0	0b00000001	0		0b0000000
0	1	0	0b00000001	0		0b0000000
1	1	0	0b00000001	0		0b0000000
0	1	0	0b00000001	0		0b0000000
1	1	0	0b00000001	0		0b0000000
0	1	0	0b00000001	0		0b0000000
1	1	0	0b00000001	0		0b0000000
0	1	0	0b00000001	0		0b0000000
1	1	0	0b00000001	0		0b0000000
0	1	0	0b00000001	0		0b0000000
1	1	0	0b00000001	0		0b0000000
0	1	0	0b00000001	0		0b0000000
1	1	0	0b00000001	0		0b0000000
0	1	0	0b00000001	0		0b0000000
1	1	0	0b00000001	0		0b0000000
*/
