// Digital circuit DDS_without_ValueTable.dig as structural Verilog
module DDS_without_ValueTable (
  input  clk,
  input  RESET,
  input  SET,
  input  [7:0] step_in,
  input  [6:0] table_value,
  output [6:0] table_address,
  output [7:0] value,
  output zero_address
);

  wire address_adjust_1_symbol, comparator_1_eq, d_ff_as_1_q, d_ff_as_2_q, d_ff_as_3_q, not_1_out;
  wire [7:0] counter_1_counter;

  not not_1 (not_1_out, RESET);
  counter counter_1 (.RESET(RESET), .SET(SET), .clk(clk), .step_in(step_in), .counter(counter_1_counter));
  Comparator #(.Bits(8)) comparator_1 (.a(counter_1_counter), .b({8{1'b0}}), .eq(comparator_1_eq));  // open: gt, lt
  address_adjust address_adjust_1 (
    .long_address(counter_1_counter), .clk(clk), .RESET(RESET), .SET(SET), .symbol(address_adjust_1_symbol),
    .short_address(table_address));
  D_FF_AS d_ff_as_1 (.Set(SET), .D(address_adjust_1_symbol), .C(clk), .Clr(not_1_out), .Q(d_ff_as_1_q));  // open: nQ
  D_FF_AS d_ff_as_2 (.Set(1'b0), .D(comparator_1_eq), .C(clk), .Clr(not_1_out), .Q(d_ff_as_2_q));  // open: nQ
  value_2_signed value_2_signed_1 (
    .clk(clk), .RESET(RESET), .abs_value(table_value), .symbol(d_ff_as_1_q), .result(value));
  D_FF_AS d_ff_as_3 (.Set(1'b0), .D(d_ff_as_2_q), .C(clk), .Clr(not_1_out), .Q(d_ff_as_3_q));  // open: nQ
  D_FF_AS d_ff_as_4 (.Set(1'b0), .D(d_ff_as_3_q), .C(clk), .Clr(not_1_out), .Q(zero_address));  // open: nQ

  // Notes on the sheet:
  //   zero
  //   delay chain #3
endmodule

/* Test case:
clk	RESET	SET	step_in		table_value	zero_address	table_address	value
0	1	0	0b00000000	0b0000001	0		0b0000000	0b11111111
1	1	0	0b00000000	0b0000001	0		0b0000000	0b00000001
*/
