// Digital circuit Line_sin_0_90.dig as structural Verilog
module Line_sin_0_90 (
  input  [6:0] address,
  input  clk,
  input  RESET,
  output [6:0] value
);

  wire comparator_14_eq, comparator_15_eq, comparator_16_eq, comparator_17_eq, comparator_18_eq,
       comparator_19_eq, comparator_20_eq, comparator_21_eq, comparator_22_eq, comparator_23_eq,
       comparator_24_eq, comparator_25_eq, comparator_26_eq, comparator_27_eq, not_1_out;
  wire [5:0] d_ff_as_1_q, intra_address_delay_q, multiplexer_1_out;
  wire [6:0] multiplexer_16_out, multiplexer_17_out, multiplexer_18_out, multiplexer_19_out,
       multiplexer_20_out, multiplexer_21_out, multiplexer_22_out, multiplexer_23_out, multiplexer_24_out,
       multiplexer_25_out, multiplexer_26_out, multiplexer_27_out, multiplexer_28_out, multiplexer_29_out;
  wire [7:0] add_1_s, multiplexer_2_out, multiplexer_3_out, multiplexer_4_out, multiplexer_5_out,
       multiplexer_6_out, multiplexer_7_out, multiplexer_8_out, multiplexer_9_out, multiplexer_10_out,
       multiplexer_11_out, multiplexer_12_out, multiplexer_13_out, multiplexer_14_out, multiplexer_15_out;
  wire [12:0] comparator_1_lt;
  wire [15:0] mul_1_mul;

  not not_1 (not_1_out, RESET);
  Multiplexer #(.Bits(6)) multiplexer_1 (
    .sel(address[6]), .in_0(address[5:0]), .in_1({6{1'b1}}), .out(multiplexer_1_out));
  D_FF_AS #(.Bits(6)) d_ff_as_1 (
    .Set(1'b0), .D(multiplexer_1_out), .C(clk), .Clr(not_1_out), .Q(d_ff_as_1_q));  // open: nQ
  D_FF_AS #(.Bits(6)) intra_address_delay (
    .Set(1'b0), .D(d_ff_as_1_q), .C(clk), .Clr(not_1_out), .Q(intra_address_delay_q));  // open: nQ
  Comparator #(.Bits(6)) comparator_1 (.a(d_ff_as_1_q), .b(6'b000011), .lt(comparator_1_lt[0]));  // open: gt, eq
  Comparator #(.Bits(6)) comparator_2 (.a(d_ff_as_1_q), .b(6'b000101), .lt(comparator_1_lt[1]));  // open: gt, eq
  Comparator #(.Bits(6)) comparator_3 (.a(d_ff_as_1_q), .b(6'b000111), .lt(comparator_1_lt[2]));  // open: gt, eq
  Comparator #(.Bits(6)) comparator_4 (.a(d_ff_as_1_q), .b(6'b001001), .lt(comparator_1_lt[3]));  // open: gt, eq
  Comparator #(.Bits(6)) comparator_5 (.a(d_ff_as_1_q), .b(6'b001011), .lt(comparator_1_lt[4]));  // open: gt, eq
  Comparator #(.Bits(6)) comparator_6 (.a(d_ff_as_1_q), .b(6'b001101), .lt(comparator_1_lt[5]));  // open: gt, eq
  Comparator #(.Bits(6)) comparator_7 (.a(d_ff_as_1_q), .b(6'b001111), .lt(comparator_1_lt[6]));  // open: gt, eq
  Comparator #(.Bits(6)) comparator_8 (.a(d_ff_as_1_q), .b(6'b010010), .lt(comparator_1_lt[7]));  // open: gt, eq
  Comparator #(.Bits(6)) comparator_9 (.a(d_ff_as_1_q), .b(6'b010101), .lt(comparator_1_lt[8]));  // open: gt, eq
  Comparator #(.Bits(6)) comparator_10 (.a(d_ff_as_1_q), .b(6'b011001), .lt(comparator_1_lt[9]));  // open: gt, eq
  Comparator #(.Bits(6)) comparator_11 (.a(d_ff_as_1_q), .b(6'b100011), .lt(comparator_1_lt[10]));  // open: gt, eq
  Comparator #(.Bits(6)) comparator_12 (.a(d_ff_as_1_q), .b(6'b101111), .lt(comparator_1_lt[11]));  // open: gt, eq
  Comparator #(.Bits(6)) comparator_13 (.a(d_ff_as_1_q), .b(6'b111100), .lt(comparator_1_lt[12]));  // open: gt, eq
  Comparator #(.Bits(13)) comparator_14 (.a(comparator_1_lt), .b({13{1'b1}}), .eq(comparator_14_eq));  // open: gt, lt
  Comparator #(.Bits(13)) comparator_15 (.a(comparator_1_lt), .b(13'h1ffe), .eq(comparator_15_eq));  // open: gt, lt
  Comparator #(.Bits(13)) comparator_16 (.a(comparator_1_lt), .b(13'h1ffc), .eq(comparator_16_eq));  // open: gt, lt
  Comparator #(.Bits(13)) comparator_17 (.a(comparator_1_lt), .b(13'h1ff8), .eq(comparator_17_eq));  // open: gt, lt
  Comparator #(.Bits(13)) comparator_18 (.a(comparator_1_lt), .b(13'h1ff0), .eq(comparator_18_eq));  // open: gt, lt
  Comparator #(.Bits(13)) comparator_19 (.a(comparator_1_lt), .b(13'h1fe0), .eq(comparator_19_eq));  // open: gt, lt
  Comparator #(.Bits(13)) comparator_20 (.a(comparator_1_lt), .b(13'h1fc0), .eq(comparator_20_eq));  // open: gt, lt
  Comparator #(.Bits(13)) comparator_21 (.a(comparator_1_lt), .b(13'h1f80), .eq(comparator_21_eq));  // open: gt, lt
  Comparator #(.Bits(13)) comparator_22 (.a(comparator_1_lt), .b(13'h1f00), .eq(comparator_22_eq));  // open: gt, lt
  Comparator #(.Bits(13)) comparator_23 (.a(comparator_1_lt), .b(13'h1e00), .eq(comparator_23_eq));  // open: gt, lt
  Comparator #(.Bits(13)) comparator_24 (.a(comparator_1_lt), .b(13'h1c00), .eq(comparator_24_eq));  // open: gt, lt
  Comparator #(.Bits(13)) comparator_25 (.a(comparator_1_lt), .b(13'h1800), .eq(comparator_25_eq));  // open: gt, lt
  Comparator #(.Bits(13)) comparator_26 (.a(comparator_1_lt), .b(13'h1000), .eq(comparator_26_eq));  // open: gt, lt
  Comparator #(.Bits(13)) comparator_27 (.a(comparator_1_lt), .b({13{1'b0}}), .eq(comparator_27_eq));  // open: gt, lt
  Multiplexer #(.Bits(8)) multiplexer_2 (
    .sel(comparator_14_eq), .in_0(multiplexer_3_out), .in_1(8'hc8), .out(multiplexer_2_out));
  Multiplexer #(.Bits(8)) multiplexer_3 (
    .sel(comparator_15_eq), .in_0(multiplexer_4_out), .in_1(8'hc7), .out(multiplexer_3_out));
  Multiplexer #(.Bits(8)) multiplexer_4 (
    .sel(comparator_16_eq), .in_0(multiplexer_5_out), .in_1(8'hc6), .out(multiplexer_4_out));
  Multiplexer #(.Bits(8)) multiplexer_5 (
    .sel(comparator_17_eq), .in_0(multiplexer_6_out), .in_1(8'hc5), .out(multiplexer_5_out));
  Multiplexer #(.Bits(8)) multiplexer_6 (
    .sel(comparator_18_eq), .in_0(multiplexer_7_out), .in_1(8'hc3), .out(multiplexer_6_out));
  Multiplexer #(.Bits(8)) multiplexer_7 (
    .sel(comparator_19_eq), .in_0(multiplexer_8_out), .in_1(8'hc1), .out(multiplexer_7_out));
  Multiplexer #(.Bits(8)) multiplexer_8 (
    .sel(comparator_20_eq), .in_0(multiplexer_9_out), .in_1(8'hbe), .out(multiplexer_8_out));
  Multiplexer #(.Bits(8)) multiplexer_9 (
    .sel(comparator_21_eq), .in_0(multiplexer_10_out), .in_1(8'hb9), .out(multiplexer_9_out));
  Multiplexer #(.Bits(8)) multiplexer_10 (
    .sel(comparator_22_eq), .in_0(multiplexer_11_out), .in_1(8'hb3), .out(multiplexer_10_out));
  Multiplexer #(.Bits(8)) multiplexer_11 (
    .sel(comparator_23_eq), .in_0(multiplexer_12_out), .in_1(8'hab), .out(multiplexer_11_out));
  Multiplexer #(.Bits(8)) multiplexer_12 (
    .sel(comparator_24_eq), .in_0(multiplexer_13_out), .in_1(8'h96), .out(multiplexer_12_out));
  Multiplexer #(.Bits(8)) multiplexer_13 (
    .sel(comparator_25_eq), .in_0(multiplexer_14_out), .in_1(8'h6c), .out(multiplexer_13_out));
  Multiplexer #(.Bits(8)) multiplexer_14 (
    .sel(comparator_26_eq), .in_0(multiplexer_15_out), .in_1(8'h34), .out(multiplexer_14_out));
  Multiplexer #(.Bits(8)) multiplexer_15 (
    .sel(comparator_27_eq), .in_0({8{1'b0}}), .in_1(8'ha), .out(multiplexer_15_out));
  Mul #(.Bits(8)) mul_1 (.a({2'b00, intra_address_delay_q}), .b(multiplexer_2_out), .mul(mul_1_mul));
  Multiplexer #(.Bits(7)) multiplexer_16 (
    .sel(comparator_14_eq), .in_0(multiplexer_17_out), .in_1({7{1'b0}}), .out(multiplexer_16_out));
  Multiplexer #(.Bits(7)) multiplexer_17 (
    .sel(comparator_15_eq), .in_0(multiplexer_18_out), .in_1(7'b0000001), .out(multiplexer_17_out));
  Multiplexer #(.Bits(7)) multiplexer_18 (
    .sel(comparator_16_eq), .in_0(multiplexer_19_out), .in_1(7'b0000001), .out(multiplexer_18_out));
  Multiplexer #(.Bits(7)) multiplexer_19 (
    .sel(comparator_17_eq), .in_0(multiplexer_20_out), .in_1(7'b0000001), .out(multiplexer_19_out));
  Multiplexer #(.Bits(7)) multiplexer_20 (
    .sel(comparator_18_eq), .in_0(multiplexer_21_out), .in_1(7'b0000001), .out(multiplexer_20_out));
  Multiplexer #(.Bits(7)) multiplexer_21 (
    .sel(comparator_19_eq), .in_0(multiplexer_22_out), .in_1(7'b0000001), .out(multiplexer_21_out));
  Multiplexer #(.Bits(7)) multiplexer_22 (
    .sel(comparator_20_eq), .in_0(multiplexer_23_out), .in_1(7'b0000010), .out(multiplexer_22_out));
  Multiplexer #(.Bits(7)) multiplexer_23 (
    .sel(comparator_21_eq), .in_0(multiplexer_24_out), .in_1(7'b0000011), .out(multiplexer_23_out));
  Multiplexer #(.Bits(7)) multiplexer_24 (
    .sel(comparator_22_eq), .in_0(multiplexer_25_out), .in_1(7'b0000101), .out(multiplexer_24_out));
  Multiplexer #(.Bits(7)) multiplexer_25 (
    .sel(comparator_23_eq), .in_0(multiplexer_26_out), .in_1(7'b0000111), .out(multiplexer_25_out));
  Multiplexer #(.Bits(7)) multiplexer_26 (
    .sel(comparator_24_eq), .in_0(multiplexer_27_out), .in_1(7'b0001111), .out(multiplexer_26_out));
  Multiplexer #(.Bits(7)) multiplexer_27 (
    .sel(comparator_25_eq), .in_0(multiplexer_28_out), .in_1(7'b0100110), .out(multiplexer_27_out));
  Multiplexer #(.Bits(7)) multiplexer_28 (
    .sel(comparator_26_eq), .in_0(multiplexer_29_out), .in_1(7'b1001111), .out(multiplexer_28_out));
  Multiplexer #(.Bits(7)) multiplexer_29 (
    .sel(comparator_27_eq), .in_0({7{1'b0}}), .in_1(7'b1110110), .out(multiplexer_29_out));
  Add #(.Bits(8)) add_1 (.a(mul_1_mul[13:6]), .b({1'b0, multiplexer_16_out}), .c_i(1'b0), .s(add_1_s));  // open: c_o
  D_FF_AS #(.Bits(7)) d_ff_as_2 (.Set(1'b0), .D(add_1_s[6:0]), .C(clk), .Clr(not_1_out), .Q(value));  // open: nQ

  // Notes on the sheet:
  //   intra_address
  //   intra_address_delay
  //   judgement
endmodule

/* Test case:
clk	RESET	address	value	
0	1	0b0000000	0b0000000
1	1	0b0000000	0b0000000
0	1	0b0000001	0b0000000
1	1	0b0000001	0b0000001
0	1	0b0000010	0b0000001
1	1	0b0000010	0b0000001
0	1	0b0000011	0b0000001
1	1	0b0000011	0b0000001
0	1	0b0000100	0b0000001
1	1	0b0000100	0b0000100
0	1	0b0000101	0b0000100
1	1	0b0000101	0b0000110
0	1	0b0000110	0b0000100
1	1	0b0000110	0b0000110
*/
