// Digital circuit address_adjust.dig as structural Verilog
module address_adjust (
  input  [7:0] long_address,
  input  clk,
  input  RESET,
  input  SET,
  output symbol,
  output [6:0] short_address
);

  wire comparator_1_eq, d_ff_as_1_q, multiplexer_2_out, not_1_out;
  wire [6:0] d_ff_as_2_q, multiplexer_1_out, multiplexer_3_out, sub_1_s;

  not not_1 (not_1_out, RESET);
  Comparator #(.Bits(6)) comparator_1 (.a(long_address[5:0]), .b({6{1'b0}}), .eq(comparator_1_eq));  // open: gt, lt
  Sub #(.Bits(7)) sub_1 (.a(7'b1000000), .b({1'b0, long_address[5:0]}), .c_i(1'b0), .s(sub_1_s));  // open: c_o
  Multiplexer #(.Bits(7)) multiplexer_1 (
    .sel(comparator_1_eq), .in_0(sub_1_s), .in_1(7'b1000000), .out(multiplexer_1_out));
  Multiplexer #(.Selector_Bits(2)) multiplexer_2 (
    .sel(long_address[7:6]), .in_0(1'b0), .in_1(1'b0), .in_2(1'b1), .in_3(1'b1), .out(multiplexer_2_out));
  Multiplexer #(.Selector_Bits(2), .Bits(7)) multiplexer_3 (
    .sel(long_address[7:6]), .in_0({1'b0, long_address[5:0]}), .in_1(multiplexer_1_out),
    .in_2({1'b0, long_address[5:0]}), .in_3(multiplexer_1_out), .out(multiplexer_3_out));
  D_FF_AS d_ff_as_1 (.Set(SET), .D(multiplexer_2_out), .C(clk), .Clr(not_1_out), .Q(d_ff_as_1_q));  // open: nQ
  D_FF_AS #(.Bits(7)) d_ff_as_2 (
    .Set(SET), .D(multiplexer_3_out), .C(clk), .Clr(not_1_out), .Q(d_ff_as_2_q));  // open: nQ
  Multiplexer multiplexer_4 (.sel(not_1_out), .in_0(d_ff_as_1_q), .in_1(1'b0), .out(symbol));
  Multiplexer #(.Bits(7)) multiplexer_5 (.sel(not_1_out), .in_0(d_ff_as_2_q), .in_1({7{1'b0}}), .out(short_address));

  // Notes on the sheet:
  //   tail bit long add
endmodule

/* Test case:
clk	RESET	long_address			symbol		short_address
0	1	0b10100000			0b0		0b0000000
1	1	0b10100000			0b1		0b0100000
0	1	0b01111111			0b1		0b0100000
1	1	0b01111111			0b0		0b0000000
0	0	0b01110001			0b0		0b0000000
1	0	0b01110001			0b0		0b0000000
*/
