// Digital circuit counter.dig as structural Verilog
module counter (
  input  RESET,
  input  SET,
  input  clk,
  input  [7:0] step_in,
  output [7:0] counter
);

  wire not_1_out;
  wire [7:0] add_1_s, d_ff_as_1_q, multiplexer_1_out, multiplexer_2_out;

  not not_1 (not_1_out, RESET);
  Multiplexer #(.Bits(8)) multiplexer_1 (.sel(SET), .in_0(step_in), .in_1(d_ff_as_1_q), .out(multiplexer_1_out));
  D_FF_AS #(.Bits(8)) d_ff_as_1 (
    .Set(SET), .D(multiplexer_1_out), .C(clk), .Clr(not_1_out), .Q(d_ff_as_1_q));  // open: nQ
  Add #(.Bits(8)) add_1 (.a(d_ff_as_1_q), .b(counter), .c_i(1'b0), .s(add_1_s));  // open: c_o
  Multiplexer #(.Bits(8)) multiplexer_2 (.sel(SET), .in_0(add_1_s), .in_1({8{1'b0}}), .out(multiplexer_2_out));
  D_FF_AS #(.Bits(8)) d_ff_as_2 (.Set(SET), .D(multiplexer_2_out), .C(clk), .Clr(not_1_out), .Q(counter));  // open: nQ

  // Notes on the sheet:
  //   step
  //   cost two cycles
endmodule

/* Test case:
RESET	SET	clk	step_in	counter	
1	0	0	2	0	
1	0	1	2	0	
1	0	0	2	0
1	0	1	2	2
1	0	0	2	2
1	0	1	2	4
1	0	0	2	4
1	0	1	2	6
*/
