// Digital circuit shift_right.dig as structural Verilog
module shift_right (
  input  [9:0] x,
  input  [2:0] order,
  output [9:0] shifted
);

  Multiplexer #(.Selector_Bits(3), .Bits(10)) multiplexer_1 (
    .sel(order), .in_0(x), .in_1({1'b0, x[9:1]}), .in_2({2'b00, x[9:2]}), .in_3({3'b000, x[9:3]}),
    .in_4({4'b0000, x[9:4]}), .in_5({{5{1'b0}}, x[9:5]}), .in_6({{6{1'b0}}, x[9:6]}),
    .in_7({{7{1'b0}}, x[9:7]}), .out(shifted));
endmodule

/* Test case:
x	order	shifted
0b1111111111	1	0b0111111111
0b0000000001	1	0b0000000000
*/
