// Digital circuit value_2_signed.dig as structural Verilog
module value_2_signed (
  input  clk,
  input  RESET,
  input  [6:0] abs_value,
  input  symbol,
  output [7:0] result
);

  wire comparator_1_eq, not_1_out;
  wire [6:0] add_1_s, not_2_out;
  wire [7:0] multiplexer_1_out, multiplexer_2_out;

  not not_1 (not_1_out, RESET);
  assign not_2_out = ~abs_value;  // Not not_2, 7 bits wide
  Comparator #(.Bits(7)) comparator_1 (.a(abs_value), .b({7{1'b0}}), .eq(comparator_1_eq));  // open: gt, lt
  Add #(.Bits(7)) add_1 (.a(not_2_out), .b(7'b0000001), .c_i(1'b0), .s(add_1_s));  // open: c_o
  Multiplexer #(.Bits(8)) multiplexer_1 (
    .sel(symbol), .in_0({symbol, abs_value}), .in_1(multiplexer_2_out), .out(multiplexer_1_out));
  Multiplexer #(.Bits(8)) multiplexer_2 (
    .sel(comparator_1_eq), .in_0({symbol, add_1_s}), .in_1({8{1'b0}}), .out(multiplexer_2_out));
  D_FF_AS #(.Bits(8)) d_ff_as_1 (.Set(not_1_out), .D(multiplexer_1_out), .C(clk), .Clr(1'b0), .Q(result));  // open: nQ
endmodule

/* Test case:
clk	RESET	abs_value	symbol	result
0	1	0b0000001	0	0b11111111
1	1	0b0000001	0	0b00000001
0	1	0b0000010	0	0b00000001
1	1	0b0000010	0	0b00000010
0	1	0b0000001	1	0b00000010
1	1	0b0000001	1	0b11111111
0	1	0b0100000	1	0b11111111
1	1	0b0100000	1	0b11100000
*/
