// Digital circuit risc-v-micro-alu.dig as structural Verilog
module risc_v_micro_alu (
  input  [3:0] alu_op,
  input  [31:0] x,
  input  [31:0] y,
  output [31:0] rst
);

  wire gt__eq__lt_eq, gt__eq__lt_gt, s_gt__eq__lt_gt;
  wire [0:0] r9, r10, r11, r12, r13, r14;
  wire [31:0] r1, r2, r3, r4, r5, r6, r7, r8;

  Add #(.Bits(32)) plus (.a(x), .b(y), .c_i(1'b0), .s(r1));  // open: c_o
  Sub #(.Bits(32)) sub (.a(x), .b(y), .c_i(1'b0), .s(r2));  // open: c_o
  BarrelShifter #(.Bits(32)) LeftL (.in(x), .shift({1'b0, y[4:0]}), .out(r3));
  BarrelShifter #(.Bits(32), .direction("right")) RightL (.in(x), .shift({1'b0, y[4:0]}), .out(r4));
  BarrelShifter #(.Bits(32), .barrelShifterMode("arithmetic"), .direction("right")) RightA (
    .in(x), .shift({1'b0, y[4:0]}), .out(r5));
  assign r6 = x & y;  // And and_1, 32 bits wide
  assign r7 = x | y;  // Or or_1, 32 bits wide
  assign r8 = x ^ y;  // XOr xor_1, 32 bits wide
  Comparator #(.Signed("true"), .Bits(32)) s_gt__eq__lt (.a(x), .b(y), .gt(s_gt__eq__lt_gt), .eq(r11[0]), .lt(r10[0]));
  Comparator #(.Bits(32)) gt__eq__lt (.a(x), .b(y), .gt(gt__eq__lt_gt), .eq(gt__eq__lt_eq), .lt(r13[0]));
  or or_2 (r9[0], s_gt__eq__lt_gt, r11[0]);
  or or_3 (r12[0], gt__eq__lt_gt, gt__eq__lt_eq);
  not not_1 (r14[0], gt__eq__lt_eq);
  Multiplexer #(.Selector_Bits(4), .Bits(32)) multiplexer_1 (
    .sel(alu_op), .in_0(r1), .in_1(r2), .in_2(r3), .in_3(r4), .in_4(r5), .in_5(r6), .in_6(r7), .in_7(r8),
    .in_8({{31{1'b0}}, r9[0]}), .in_9({{31{1'b0}}, r10[0]}), .in_10({{31{1'b0}}, r11[0]}),
    .in_11({{31{1'b0}}, r12[0]}), .in_12({{31{1'b0}}, r13[0]}), .in_13({{31{1'b0}}, r14[0]}), .in_14(y),
    .in_15(x), .out(rst));

  // Other names for the same wires on the sheet: aluop[3:0] = alu_op; XIN[31:0] = x; YIN[31:0] = y
endmodule
