// Digital circuit risc-v-micro-aluI.dig as structural Verilog
module risc_v_micro_aluI (
  input  [31:0] ins,
  input  [31:0] rs1,
  input  [31:0] opc,
  input  [2:0] axI,
  input  [2:0] ayI,
  input  [31:0] csrIn,
  input  [31:0] rs2,
  input  en,
  input  jump,
  input  clock,
  output [31:0] x,
  output [31:0] y
);

  wire [10:0] multiplexer_4_out;
  wire [18:0] multiplexer_5_out;
  wire [19:0] multiplexer_2_out, multiplexer_3_out;
  wire [31:0] LeftL_2_out, LeftL_out, multiplexer_1_out, not_1_out, not_2_out, register_1_q;

  Register #(.Bits(32)) register_1 (.D(opc), .C(clock), .en(en), .Q(register_1_q));
  Multiplexer #(.Bits(32)) multiplexer_1 (.sel(jump), .in_0(opc), .in_1(register_1_q), .out(multiplexer_1_out));
  Multiplexer #(.Bits(20)) multiplexer_2 (.sel(ins[31]), .in_0({20{1'b0}}), .in_1({20{1'b1}}), .out(multiplexer_2_out));
  Multiplexer #(.Bits(20)) multiplexer_3 (.sel(ins[31]), .in_0({20{1'b0}}), .in_1({20{1'b1}}), .out(multiplexer_3_out));
  Multiplexer #(.Bits(11)) multiplexer_4 (.sel(ins[31]), .in_0({11{1'b0}}), .in_1({11{1'b1}}), .out(multiplexer_4_out));
  Multiplexer #(.Bits(19)) multiplexer_5 (.sel(ins[31]), .in_0({19{1'b0}}), .in_1({19{1'b1}}), .out(multiplexer_5_out));
  assign not_1_out = ~rs1;  // Not not_1, 32 bits wide
  Multiplexer #(.Selector_Bits(3), .Bits(32)) multiplexer_6 (
    .sel(axI), .in_0(rs1), .in_1(multiplexer_1_out), .in_2({{27{1'b0}}, ins[19:15]}), .in_3(not_1_out),
    .in_4(not_2_out), .in_5({32{1'b0}}), .in_6({32{1'b0}}), .in_7({32{1'b0}}), .out(x));
  assign not_2_out = ~{{27{1'b0}}, ins[19:15]};  // Not not_2, 32 bits wide
  BarrelShifter #(.Bits(32)) LeftL (
    .in({multiplexer_4_out, ins[31], ins[19:12], ins[20], ins[30:21], 1'b0}), .shift(6'b000001),
    .out(LeftL_out));
  BarrelShifter #(.Bits(32)) LeftL_2 (
    .in({multiplexer_5_out, ins[31], ins[7], ins[30:25], ins[11:8], 1'b0}), .shift(6'b000001),
    .out(LeftL_2_out));
  Multiplexer #(.Selector_Bits(3), .Bits(32)) multiplexer_7 (
    .sel(ayI), .in_0({multiplexer_2_out, ins[31:20]}), .in_1({multiplexer_3_out, ins[31:25], ins[11:7]}),
    .in_2({ins[31:12], {12{1'b0}}}), .in_3(rs2), .in_4(csrIn), .in_5(32'h4), .in_6(LeftL_out),
    .in_7(LeftL_2_out), .out(y));

  // Other names for the same wires on the sheet: aluxIn[2:0] = axI; aluyIn[2:0] = ayI

  // Notes on the sheet:
  //   ins: instruction
  //   axI: aluX input
  //   ayI: aluy input
  //   cssrwi 15-19 ZEimm
  //   lui,auipc
endmodule
