// Digital circuit risc-v-micro-controller.dig as structural Verilog
module risc_v_micro_controller (
  input  \int ,
  input  clock,
  input  [31:0] ins,
  input  en,
  output [3:0] alu_op,
  output csrW,
  output bxx,
  output Irw,
  output mr,
  output [1:0] mwf,
  output mw,
  output rwe,
  output [2:0] rws,
  output [2:0] aluy,
  output [2:0] alux,
  output pcEn,
  output pcsrc,
  output jump
);

  wire add, add_type, addi, addi_type, aluCon, \and , and_24_out, andi, auipc, beq, bge, bgeu, blt, bltu,
       bne, bxx_type, comparator_12_eq, comparator_13_eq, comparator_14_eq, comparator_15_eq,
       comparator_16_eq, comparator_17_eq, comparator_18_eq, comparator_19_eq, comparator_20_eq,
       comparator_21_eq, comparator_22_eq, comparator_23_eq, comparator_24_eq, comparator_25_eq,
       comparator_26_eq, comparator_27_eq, comparator_28_eq, comparator_29_eq, comparator_30_eq,
       comparator_31_eq, comparator_32_eq, comparator_33_eq, comparator_34_eq, comparator_35_eq,
       comparator_36_eq, comparator_37_eq, comparator_38_eq, comparator_39_eq, comparator_40_eq,
       comparator_41_eq, comparator_42_eq, comparator_43_eq, comparator_44_eq, comparator_45_eq,
       comparator_46_eq, comparator_47_eq, comparator_48_eq, comparator_49_eq, comparator_50_eq,
       comparator_51_eq, comparator_52_eq, comparator_53_eq, comparator_54_eq, comparator_55_eq,
       comparator_56_eq, comparator_57_eq, comparator_58_eq, comparator_59_eq, comparator_60_eq,
       comparator_61_eq, comparator_62_eq, csrrc, csrrci, csrrs, csrrsi, csrrw, csrrwi, ebreak, ecall, fence,
       fencei, jal, jalr, lb, lbu, lh, lhu, lui, lw, N1, N2, not_1_out, op_eq__eq_0F, op_eq__eq_03,
       op_eq__eq_13, op_eq__eq_23, op_eq__eq_33, op_eq__eq_63, op_eq__eq_73, \or , or_1_out, or_2_out,
       or_3_out, or_4_out, or_5_out, or_6_out, or_7_out, or_8_out, or_9_out, or_10_out, ori, s0, s1, s2, s3,
       s4, s5, sb, sh, sll, slli, slt, slti, sltiu, sltu, sra, srai, srl, srli, sub, sw, u_type, \xor , xori;
  wire [3:0] aluopPri_num;
  wire [6:0] multiplexer_2_out, multiplexer_3_out, uAR_q, uRom_p5;
  wire [31:30] uRom_p5_2;

  Comparator #(.Signed("true"), .Bits(8)) comparator_1 (.a({1'b0, ins[6:0]}), .b(8'h37), .eq(lui));  // open: gt, lt
  Comparator #(.Signed("true"), .Bits(8)) comparator_2 (.a({1'b0, ins[6:0]}), .b(8'h17), .eq(auipc));  // open: gt, lt
  Comparator #(.Signed("true"), .Bits(8)) comparator_3 (.a({1'b0, ins[6:0]}), .b(8'h6f), .eq(jal));  // open: gt, lt
  Comparator #(.Signed("true"), .Bits(8)) comparator_4 (.a({1'b0, ins[6:0]}), .b(8'h67), .eq(jalr));  // open: gt, lt
  Comparator #(.Signed("true"), .Bits(8)) comparator_5 (
    .a({1'b0, ins[6:0]}), .b(8'h63), .eq(op_eq__eq_63));  // open: gt, lt
  Comparator #(.Signed("true"), .Bits(8)) comparator_6 (
    .a({1'b0, ins[6:0]}), .b(8'h3), .eq(op_eq__eq_03));  // open: gt, lt
  Comparator #(.Signed("true"), .Bits(8)) comparator_7 (
    .a({1'b0, ins[6:0]}), .b(8'h23), .eq(op_eq__eq_23));  // open: gt, lt
  Comparator #(.Signed("true"), .Bits(8)) comparator_8 (
    .a({1'b0, ins[6:0]}), .b(8'h13), .eq(op_eq__eq_13));  // open: gt, lt
  Comparator #(.Bits(8)) comparator_9 (.a({1'b0, ins[6:0]}), .b(8'h33), .eq(op_eq__eq_33));  // open: gt, lt
  Comparator #(.Signed("true"), .Bits(8)) comparator_10 (
    .a({1'b0, ins[6:0]}), .b(8'hf), .eq(op_eq__eq_0F));  // open: gt, lt
  Comparator #(.Signed("true"), .Bits(8)) comparator_11 (
    .a({1'b0, ins[6:0]}), .b(8'h73), .eq(op_eq__eq_73));  // open: gt, lt
  or or_1 (or_1_out, addi, auipc, add, jal, jalr, lw, lh, lhu, lb, lbu, sw, sh, sb);
  or or_2 (or_2_out, slli, sll);
  or or_3 (or_3_out, srli, srl);
  or or_4 (or_4_out, srai, sra);
  or or_5 (or_5_out, andi, \and , csrrc, csrrci);
  or or_6 (or_6_out, ori, \or , csrrs, csrrsi);
  or or_7 (or_7_out, xori, \xor );
  or or_8 (or_8_out, slti, slt, blt);
  or or_9 (or_9_out, sltiu, bltu, sltu);
  Comparator #(.Bits(3)) comparator_12 (.a(ins[14:12]), .b(3'b000), .eq(comparator_12_eq));  // open: gt, lt
  Comparator #(.Bits(3)) comparator_13 (.a(ins[14:12]), .b(3'b001), .eq(comparator_13_eq));  // open: gt, lt
  Comparator #(.Bits(3)) comparator_14 (.a(ins[14:12]), .b(3'b100), .eq(comparator_14_eq));  // open: gt, lt
  Comparator #(.Bits(3)) comparator_15 (.a(ins[14:12]), .b(3'b101), .eq(comparator_15_eq));  // open: gt, lt
  Comparator #(.Bits(3)) comparator_16 (.a(ins[14:12]), .b(3'b110), .eq(comparator_16_eq));  // open: gt, lt
  Comparator #(.Bits(3)) comparator_17 (.a(ins[14:12]), .b(3'b111), .eq(comparator_17_eq));  // open: gt, lt
  Comparator #(.Bits(3)) comparator_18 (.a(ins[14:12]), .b(3'b000), .eq(comparator_18_eq));  // open: gt, lt
  Comparator #(.Bits(3)) comparator_19 (.a(ins[14:12]), .b(3'b001), .eq(comparator_19_eq));  // open: gt, lt
  Comparator #(.Bits(3)) comparator_20 (.a(ins[14:12]), .b(3'b010), .eq(comparator_20_eq));  // open: gt, lt
  Comparator #(.Bits(3)) comparator_21 (.a(ins[14:12]), .b(3'b100), .eq(comparator_21_eq));  // open: gt, lt
  Comparator #(.Bits(3)) comparator_22 (.a(ins[14:12]), .b(3'b101), .eq(comparator_22_eq));  // open: gt, lt
  or or_10 (or_10_out, csrrw, csrrwi);
  and and_1 (beq, comparator_12_eq, op_eq__eq_63);
  and and_2 (bne, comparator_13_eq, op_eq__eq_63);
  and and_3 (blt, comparator_14_eq, op_eq__eq_63);
  and and_4 (bge, comparator_15_eq, op_eq__eq_63);
  and and_5 (bltu, comparator_16_eq, op_eq__eq_63);
  and and_6 (bgeu, comparator_17_eq, op_eq__eq_63);
  and and_7 (lb, comparator_18_eq, op_eq__eq_03);
  and and_8 (lh, comparator_19_eq, op_eq__eq_03);
  and and_9 (lw, comparator_20_eq, op_eq__eq_03);
  and and_10 (lbu, comparator_21_eq, op_eq__eq_03);
  and and_11 (lhu, comparator_22_eq, op_eq__eq_03);
  PriorityEncoder #(.Selector_Bits(4)) aluopPri (
    .in0(or_1_out), .in1(sub), .in2(or_2_out), .in3(or_3_out), .in4(or_4_out), .in5(or_5_out),
    .in6(or_6_out), .in7(or_7_out), .in8(bge), .in9(or_8_out), .in10(beq), .in11(bgeu), .in12(or_9_out),
    .in13(bne), .in14(lui), .in15(or_10_out), .num(aluopPri_num));  // open: any
  Multiplexer #(.Bits(4)) multiplexer_1 (.sel(aluCon), .in_0(4'b0000), .in_1(aluopPri_num), .out(alu_op));
  Comparator #(.Bits(3)) comparator_23 (.a(ins[14:12]), .b(3'b000), .eq(comparator_23_eq));  // open: gt, lt
  Comparator #(.Bits(3)) comparator_24 (.a(ins[14:12]), .b(3'b001), .eq(comparator_24_eq));  // open: gt, lt
  Comparator #(.Bits(3)) comparator_25 (.a(ins[14:12]), .b(3'b010), .eq(comparator_25_eq));  // open: gt, lt
  Comparator #(.Bits(3)) comparator_26 (.a(ins[14:12]), .b(3'b000), .eq(comparator_26_eq));  // open: gt, lt
  Comparator #(.Bits(3)) comparator_27 (.a(ins[14:12]), .b(3'b010), .eq(comparator_27_eq));  // open: gt, lt
  Comparator #(.Bits(3)) comparator_28 (.a(ins[14:12]), .b(3'b011), .eq(comparator_28_eq));  // open: gt, lt
  Comparator #(.Bits(3)) comparator_29 (.a(ins[14:12]), .b(3'b100), .eq(comparator_29_eq));  // open: gt, lt
  Comparator #(.Bits(3)) comparator_30 (.a(ins[14:12]), .b(3'b110), .eq(comparator_30_eq));  // open: gt, lt
  Comparator #(.Bits(3)) comparator_31 (.a(ins[14:12]), .b(3'b111), .eq(comparator_31_eq));  // open: gt, lt
  Comparator #(.Bits(3)) comparator_32 (.a(ins[14:12]), .b(3'b001), .eq(comparator_32_eq));  // open: gt, lt
  Comparator #(.Bits(3)) comparator_33 (.a(ins[14:12]), .b(3'b101), .eq(comparator_33_eq));  // open: gt, lt
  Comparator #(.Bits(7)) comparator_34 (.a(ins[31:25]), .b({7{1'b0}}), .eq(comparator_34_eq));  // open: gt, lt
  Comparator #(.Bits(3)) comparator_35 (.a(ins[14:12]), .b(3'b101), .eq(comparator_35_eq));  // open: gt, lt
  Comparator #(.Bits(7)) comparator_36 (.a(ins[31:25]), .b(7'b0100000), .eq(comparator_36_eq));  // open: gt, lt
  and and_12 (sb, comparator_23_eq, op_eq__eq_23);
  and and_13 (sh, comparator_24_eq, op_eq__eq_23);
  and and_14 (sw, comparator_25_eq, op_eq__eq_23);
  and and_15 (addi, comparator_26_eq, op_eq__eq_13);
  and and_16 (slti, comparator_27_eq, op_eq__eq_13);
  and and_17 (sltiu, comparator_28_eq, op_eq__eq_13);
  and and_18 (xori, comparator_29_eq, op_eq__eq_13);
  and and_19 (ori, comparator_30_eq, op_eq__eq_13);
  and and_20 (andi, comparator_31_eq, op_eq__eq_13);
  and and_21 (slli, comparator_32_eq, op_eq__eq_13);
  and and_22 (srli, comparator_33_eq, comparator_34_eq, op_eq__eq_13);
  and and_23 (srai, comparator_35_eq, comparator_36_eq, op_eq__eq_13);
  Multiplexer #(.Bits(7)) multiplexer_2 (
    .sel(N1), .in_0(uRom_p5), .in_1({1'b0, s5, s4, s3, s2, s1, s0}), .out(multiplexer_2_out));
  and and_24 (and_24_out, N2, \int );
  Multiplexer #(.Bits(7)) multiplexer_3 (
    .sel(and_24_out), .in_0(multiplexer_2_out), .in_1(7'b0100000), .out(multiplexer_3_out));
  not not_1 (not_1_out, clock);
  or or_11 (addi_type, addi, slti, sltiu, andi, ori, xori, slli, srli, srai);
  or or_12 (add_type, add, sub, slt, sltu, \and , \or , \xor , sll, srl, sra);
  or or_13 (bxx_type, beq, bne, blt, bltu, bge, bgeu);
  or or_14 (u_type, lui, auipc);
  Comparator #(.Bits(3)) comparator_37 (.a(ins[14:12]), .b(3'b000), .eq(comparator_37_eq));  // open: gt, lt
  Comparator #(.Bits(7)) comparator_38 (.a(ins[31:25]), .b({7{1'b0}}), .eq(comparator_38_eq));  // open: gt, lt
  Comparator #(.Bits(3)) comparator_39 (.a(ins[14:12]), .b(3'b000), .eq(comparator_39_eq));  // open: gt, lt
  Comparator #(.Bits(7)) comparator_40 (.a(ins[31:25]), .b(7'b0100000), .eq(comparator_40_eq));  // open: gt, lt
  Comparator #(.Bits(3)) comparator_41 (.a(ins[14:12]), .b(3'b001), .eq(comparator_41_eq));  // open: gt, lt
  Comparator #(.Bits(3)) comparator_42 (.a(ins[14:12]), .b(3'b010), .eq(comparator_42_eq));  // open: gt, lt
  Comparator #(.Bits(3)) comparator_43 (.a(ins[14:12]), .b(3'b011), .eq(comparator_43_eq));  // open: gt, lt
  Comparator #(.Bits(3)) comparator_44 (.a(ins[14:12]), .b(3'b100), .eq(comparator_44_eq));  // open: gt, lt
  Comparator #(.Bits(3)) comparator_45 (.a(ins[14:12]), .b(3'b101), .eq(comparator_45_eq));  // open: gt, lt
  Comparator #(.Bits(7)) comparator_46 (.a(ins[31:25]), .b({7{1'b0}}), .eq(comparator_46_eq));  // open: gt, lt
  Comparator #(.Bits(3)) comparator_47 (.a(ins[14:12]), .b(3'b101), .eq(comparator_47_eq));  // open: gt, lt
  Comparator #(.Bits(7)) comparator_48 (.a(ins[31:25]), .b(7'b0100000), .eq(comparator_48_eq));  // open: gt, lt
  Comparator #(.Bits(3)) comparator_49 (.a(ins[14:12]), .b(3'b110), .eq(comparator_49_eq));  // open: gt, lt
  Comparator #(.Bits(3)) comparator_50 (.a(ins[14:12]), .b(3'b111), .eq(comparator_50_eq));  // open: gt, lt
  Register #(.Bits(7)) uAR (.D(multiplexer_3_out), .C(not_1_out), .en(1'b1), .Q(uAR_q));
  and and_25 (add, comparator_37_eq, comparator_38_eq, op_eq__eq_33);
  and and_26 (sub, comparator_39_eq, comparator_40_eq, op_eq__eq_33);
  and and_27 (sll, comparator_41_eq, op_eq__eq_33);
  and and_28 (slt, comparator_42_eq, op_eq__eq_33);
  and and_29 (sltu, comparator_43_eq, op_eq__eq_33);
  and and_30 (\xor , comparator_44_eq, op_eq__eq_33);
  and and_31 (srl, comparator_45_eq, comparator_46_eq, op_eq__eq_33);
  and and_32 (sra, comparator_47_eq, comparator_48_eq, op_eq__eq_33);
  and and_33 (\or , comparator_49_eq, op_eq__eq_33);
  and and_34 (\and , comparator_50_eq, op_eq__eq_33);
  // LRom #(.AddrBits(7), .Bits(32)) uRom: pin names not known; wires that end beside it: uAR_q, clock, en, 1'b0, {uRom_p5_2, jump, pcEn, pcsrc, alux, aluy, rws, rwe, mw, mwf, mr, Irw, bxx, csrW, aluCon, N2, N1, uRom_p5}
  or or_15 (s0, add_type, bxx_type, lh, lhu, sb, sh, sw);
  or or_16 (s1, addi_type, bxx_type, lb, lh, sb, sw);
  or or_17 (s2, csrrw, csrrwi, jal, lhu, u_type, lh, sb, sh, lw);
  Comparator #(.Bits(3)) comparator_51 (.a(ins[14:12]), .b(3'b000), .eq(comparator_51_eq));  // open: gt, lt
  Comparator #(.Bits(3)) comparator_52 (.a(ins[14:12]), .b(3'b001), .eq(comparator_52_eq));  // open: gt, lt
  Comparator #(.Bits(3)) comparator_53 (.a(ins[14:12]), .b(3'b000), .eq(comparator_53_eq));  // open: gt, lt
  Comparator comparator_54 (.a(ins[20]), .b(1'b0), .eq(comparator_54_eq));  // open: gt, lt
  Comparator #(.Bits(3)) comparator_55 (.a(ins[14:12]), .b(3'b000), .eq(comparator_55_eq));  // open: gt, lt
  Comparator comparator_56 (.a(ins[20]), .b(1'b1), .eq(comparator_56_eq));  // open: gt, lt
  Comparator #(.Bits(3)) comparator_57 (.a(ins[14:12]), .b(3'b001), .eq(comparator_57_eq));  // open: gt, lt
  Comparator #(.Bits(3)) comparator_58 (.a(ins[14:12]), .b(3'b010), .eq(comparator_58_eq));  // open: gt, lt
  Comparator #(.Bits(3)) comparator_59 (.a(ins[14:12]), .b(3'b011), .eq(comparator_59_eq));  // open: gt, lt
  Comparator #(.Bits(3)) comparator_60 (.a(ins[14:12]), .b(3'b101), .eq(comparator_60_eq));  // open: gt, lt
  Comparator #(.Bits(3)) comparator_61 (.a(ins[14:12]), .b(3'b110), .eq(comparator_61_eq));  // open: gt, lt
  Comparator #(.Bits(3)) comparator_62 (.a(ins[14:12]), .b(3'b111), .eq(comparator_62_eq));  // open: gt, lt
  and and_35 (fence, comparator_51_eq, op_eq__eq_0F);
  and and_36 (fencei, comparator_52_eq, op_eq__eq_0F);
  and and_37 (ecall, comparator_53_eq, comparator_54_eq, op_eq__eq_73);
  and and_38 (ebreak, comparator_55_eq, comparator_56_eq, op_eq__eq_73);
  and and_39 (csrrw, comparator_57_eq, op_eq__eq_73);
  and and_40 (csrrs, comparator_58_eq, op_eq__eq_73);
  and and_41 (csrrc, comparator_59_eq, op_eq__eq_73);
  and and_42 (csrrwi, comparator_60_eq, op_eq__eq_73);
  and and_43 (csrrsi, comparator_61_eq, op_eq__eq_73);
  and and_44 (csrrci, comparator_62_eq, op_eq__eq_73);
  or or_18 (s5, csrrc, csrrci, csrrwi, jal, jalr, u_type);
  or or_19 (s3, add_type, bxx_type, csrrci, csrrw, jal, lb, lhu);
  or or_20 (s4, add_type, bxx_type, csrrw, jalr, lbu, u_type, sb, sh, sw);

  // Other names for the same wires on the sheet: aluOp[3:0] = alu_op; op[6:0] = ins[6:0]; fun3[2:0] = ins[14:12];
  //   ecallBreak = ins[20]; fun7[6:0] = ins[31:25]

  // Notes on the sheet:
  //   int: 中断信号
  //   aluop=0000  +
  //   aluop=0010
  //    logic left
  //   0011 logic right
  //   0100 arithmetic right
  //   0101 and
  //   0110 or
  //   0111 xor
  //   1001 s<
  //   1100 <
  //   1110 ==  aluy stright
  //   1111 alux stright
  //   contents of uRom (hex, n*v repeats v):
  //   11a01001,21e00080,203,1e20100,205,1e02006,1ea0100,208,1e02009,1f60100,20b,1e0200c,
  //   1fa0100,20e,1e0200f,1ee0100,211,1e02012,1f20100,200214,1e10100,200216,1e14100,200218,
  //   1e18100,60021a,1e20100,28600a38,1e6001e,0,80021f,1e00500,1e60022,0,3800223,1e00500,
  //   1e60026,0,2800227,1e00500,1e6002a,0,480022b,1e00500,21a0022d,1e2002e,31c0022f,1e00100,
  //   21a00231,1e20032,30000233,1e00100,1400235,1e20100,0,0,1e00100
endmodule
