// Digital circuit risc-v-micro-cpu.dig as structural Verilog
module risc_v_micro_cpu (
  input  clock,
  input  enable,
  output [7:0] ramDataIn,
  output [7:0] ramDataOut,
  output [7:0] csrDataIn,
  output csrW,
  output [7:0] csrDataOut,
  output mW,
  output mR,
  output [7:0] pcOut,
  output [9:0] clkCount,
  output irEn
);

  wire and_1_out, not_1_out, not_2_out, not_3_out, not_4_out, or_1_out, risc_v_micro_controller_1_bxx,
       risc_v_micro_controller_1_jump, risc_v_micro_controller_1_pcen, risc_v_micro_controller_1_pcsrc,
       risc_v_micro_controller_1_rwe;
  wire [1:0] risc_v_micro_controller_1_mwf;
  wire [2:0] risc_v_micro_controller_1_alux, risc_v_micro_controller_1_aluy, risc_v_micro_controller_1_rws;
  wire [3:0] risc_v_micro_controller_1_alu_op;
  wire [15:0] RS2_q;
  wire [31:0] IR_q, Irom_p5, multiplexer_2_out, pc_q, registerfile_1_da, registerfile_1_db,
       risc_v_micro_alu_1_rst, risc_v_micro_alui_1_x, risc_v_micro_alui_1_y, risc_v_micro_regwrite_1_rwdata,
       RS1_q;
  wire [31:8] csr_p3, csr_p10, Drom_p10, multiplexer_1_out;
  wire [31:16] RS2_q_2;

  Register #(.Bits(32)) pc (.D(multiplexer_2_out), .C(clock), .en(or_1_out), .Q({pc_q[31:10], pcOut, pc_q[1:0]}));
  // LRom #(.AddrBits(8), .Bits(32)) Irom: pin names not known; wires that end beside it: pcOut, clock, enable, 1'b0, Irom_p5
  not not_1 (not_1_out, clock);
  Register #(.Bits(32)) IR (.D(Irom_p5), .C(not_1_out), .en(irEn), .Q(IR_q));
  risc_v_micro_controller risc_v_micro_controller_1 (
    .\int (1'b0), .clock(clock), .ins(IR_q), .en(enable), .alu_op(risc_v_micro_controller_1_alu_op),
    .csrW(csrW), .bxx(risc_v_micro_controller_1_bxx), .Irw(irEn), .mr(mR),
    .mwf(risc_v_micro_controller_1_mwf), .mw(mW), .rwe(risc_v_micro_controller_1_rwe),
    .rws(risc_v_micro_controller_1_rws), .aluy(risc_v_micro_controller_1_aluy),
    .alux(risc_v_micro_controller_1_alux), .pcEn(risc_v_micro_controller_1_pcen),
    .pcsrc(risc_v_micro_controller_1_pcsrc), .jump(risc_v_micro_controller_1_jump));
  risc_v_micro_regWrite risc_v_micro_regwrite_1 (
    .aluR({csr_p3, csrDataIn}), .rws(risc_v_micro_controller_1_rws), .ramData({Drom_p10, ramDataOut}),
    .csrIn({csr_p10, csrDataOut}), .rwData(risc_v_micro_regwrite_1_rwdata));
  not not_2 (not_2_out, clock);
  or or_1 (or_1_out, risc_v_micro_controller_1_pcen, and_1_out);
  not not_3 (not_3_out, clock);
  RegisterFile #(.AddrBits(5), .Bits(32)) registerfile_1 (
    .Din(risc_v_micro_regwrite_1_rwdata), .we(risc_v_micro_controller_1_rwe), .Rw(IR_q[11:7]), .C(not_3_out),
    .Ra(IR_q[19:15]), .Rb(IR_q[24:20]), .Da(registerfile_1_da), .Db(registerfile_1_db));
  // LRamDP #(.AddrBits(8), .Bits(32)) csr: pin names not known; wires that end beside it: IR_q[27:20], IR_q[27:20], {csr_p3, csrDataIn}, csrW, 1'b1, not_2_out, csrW, not_2_out, 1'b0, {csr_p10, csrDataOut}
  Register #(.Bits(32)) RS1 (.D(registerfile_1_da), .C(clock), .en(1'b1), .Q(RS1_q));
  Register #(.Bits(32)) RS2 (.D(registerfile_1_db), .C(clock), .en(1'b1), .Q({RS2_q_2, RS2_q}));
  Counter #(.Bits(10)) counter_1 (.en(enable), .C(clock), .clr(1'b0), .out(clkCount));  // open: ovf
  risc_v_micro_aluI risc_v_micro_alui_1 (
    .ins(IR_q), .rs1(RS1_q), .opc({pc_q[31:10], pcOut, pc_q[1:0]}), .axI(risc_v_micro_controller_1_alux),
    .ayI(risc_v_micro_controller_1_aluy), .csrIn({csr_p10, csrDataOut}), .rs2({RS2_q_2, RS2_q}),
    .en(risc_v_micro_controller_1_pcen), .jump(risc_v_micro_controller_1_jump), .clock(clock),
    .x(risc_v_micro_alui_1_x), .y(risc_v_micro_alui_1_y));
  risc_v_micro_alu risc_v_micro_alu_1 (
    .alu_op(risc_v_micro_controller_1_alu_op), .x(risc_v_micro_alui_1_x), .y(risc_v_micro_alui_1_y),
    .rst(risc_v_micro_alu_1_rst));
  Multiplexer #(.Selector_Bits(2), .Bits(32)) multiplexer_1 (
    .sel(risc_v_micro_controller_1_mwf), .in_0({RS2_q_2, RS2_q}), .in_1({{16{1'b0}}, RS2_q}),
    .in_2({{24{1'b0}}, RS2_q[7:0]}), .in_3({32{1'b0}}), .out({multiplexer_1_out, ramDataIn}));
  Register #(.Bits(32)) register_1 (.D(risc_v_micro_alu_1_rst), .C(clock), .en(1'b1), .Q({csr_p3, csrDataIn}));
  and and_1 (and_1_out, risc_v_micro_controller_1_bxx, risc_v_micro_alu_1_rst[0]);
  Multiplexer #(.Bits(32)) multiplexer_2 (
    .sel(risc_v_micro_controller_1_pcsrc), .in_0(risc_v_micro_alu_1_rst), .in_1({csr_p3, csrDataIn}),
    .out(multiplexer_2_out));
  not not_4 (not_4_out, clock);
  // LRamDP #(.AddrBits(8), .Bits(32)) Drom: pin names not known; wires that end beside it: {csr_p3[9:8], csrDataIn[7:2]}, {csr_p3[9:8], csrDataIn[7:2]}, {multiplexer_1_out, ramDataIn}, mW, mR, not_4_out, mW, not_4_out, 1'b0, {Drom_p10, ramDataOut}

  // Notes on the sheet:
  //   contents of Irom (hex, n*v repeats v):
  //   0,fff00513,593,a5a023,150513,458593,a5a023,150513,458593,a5a023,150513,458593,a5a023,
  //   150513,458593,a5a023,150513,458593,a5a023,150513,458593,a5a023,150513,458593,a5a023,
  //   533,52083,5a103,114363,15a023,252023,ffc58593,feb51ae3,450513,1c00593,feb517e3,1000193,
  //   ffffffff
endmodule
