// Digital circuit risc-v-micro-regWrite.dig as structural Verilog
module risc_v_micro_regWrite (
  input  [31:0] aluR,
  input  [2:0] rws,
  input  [31:0] ramData,
  input  [31:0] csrIn,
  output [31:0] rwData
);

  wire [15:0] multiplexer_1_out;
  wire [23:0] multiplexer_2_out;

  Multiplexer #(.Bits(16)) multiplexer_1 (
    .sel(ramData[15]), .in_0({16{1'b0}}), .in_1({16{1'b1}}), .out(multiplexer_1_out));
  Multiplexer #(.Bits(24)) multiplexer_2 (
    .sel(ramData[7]), .in_0({24{1'b0}}), .in_1({24{1'b1}}), .out(multiplexer_2_out));
  Multiplexer #(.Selector_Bits(3), .Bits(32)) multiplexer_3 (
    .sel(rws), .in_0(aluR), .in_1(csrIn), .in_2(ramData), .in_3({{16{1'b0}}, ramData[15:0]}),
    .in_4({{24{1'b0}}, ramData[7:0]}), .in_5({multiplexer_1_out, ramData[15:0]}),
    .in_6({multiplexer_2_out, ramData[7:0]}), .in_7({32{1'b0}}), .out(rwData));

  // Other names for the same wires on the sheet: regWriteData[31:0] = rwData
endmodule
