// Digital circuit monocycle-aluI.dig as structural Verilog
module monocycle_aluI (
  input  [2:0] axI,
  input  [2:0] ayI,
  input  siC,
  input  [31:0] opc,
  input  [31:0] ins,
  input  [31:0] rs1,
  input  [31:0] rs2,
  input  [31:0] csrIn,
  output [31:0] x,
  output [31:0] y
);

  wire [19:0] multiplexer_1_out, multiplexer_2_out;
  wire [31:0] multiplexer_3_out, not_1_out, not_2_out;

  Multiplexer #(.Bits(20)) multiplexer_1 (.sel(ins[31]), .in_0({20{1'b0}}), .in_1({20{1'b1}}), .out(multiplexer_1_out));
  Multiplexer #(.Bits(20)) multiplexer_2 (.sel(ins[31]), .in_0({20{1'b0}}), .in_1({20{1'b1}}), .out(multiplexer_2_out));
  assign not_1_out = ~rs1;  // Not not_1, 32 bits wide
  Multiplexer #(.Bits(32)) multiplexer_3 (
    .sel(siC), .in_0({multiplexer_1_out, ins[31:20]}), .in_1({multiplexer_2_out, ins[31:25], ins[11:7]}),
    .out(multiplexer_3_out));
  assign not_2_out = ~{{27{1'b0}}, ins[19:15]};  // Not not_2, 32 bits wide
  Multiplexer #(.Selector_Bits(3), .Bits(32)) multiplexer_4 (
    .sel(axI), .in_0(rs1), .in_1(opc), .in_2({{27{1'b0}}, ins[19:15]}), .in_3(not_1_out), .in_4(not_2_out),
    .in_5({32{1'b0}}), .in_6({32{1'b0}}), .in_7({32{1'b0}}), .out(x));
  Multiplexer #(.Selector_Bits(3), .Bits(32)) multiplexer_5 (
    .sel(ayI), .in_0(multiplexer_3_out), .in_1({{27{1'b0}}, ins[24:20]}), .in_2({ins[31:12], {12{1'b0}}}),
    .in_3(rs2), .in_4({{27{1'b0}}, rs2[4:0]}), .in_5(csrIn), .in_6(32'h4), .in_7({32{1'b0}}), .out(y));

  // Other names for the same wires on the sheet: aluxIn[2:0] = axI; aluyIn[2:0] = ayI

  // Notes on the sheet:
  //   axI: aluX input
  //   ayI: aluy input
  //   ins: instruction
  //   lui,auipc
  //   cssrwi 15-19 ZEimm
endmodule
