// Digital circuit monocycle-pc.dig as structural Verilog
module monocycle_pc (
  input  [31:0] instr,
  input  [1:0] pcw,
  input  bxx,
  input  clock,
  input  pcen,
  input  [31:0] rs1,
  input  result,
  output [31:0] pc
);

  wire and_1_out;
  wire [10:0] multiplexer_1_out;
  wire [18:0] multiplexer_3_out;
  wire [31:0] add_1_s, LeftL_2_out, LeftL_out, multiplexer_4_out, multiplexer_5_out, multiplexer_6_out;
  wire [31:12] multiplexer_2_out;

  Multiplexer #(.Bits(11)) multiplexer_1 (
    .sel(instr[31]), .in_0({11{1'b0}}), .in_1({11{1'b1}}), .out(multiplexer_1_out));
  Multiplexer #(.Bits(20)) multiplexer_2 (
    .sel(instr[31]), .in_0({20{1'b0}}), .in_1({20{1'b1}}), .out(multiplexer_2_out));
  Multiplexer #(.Bits(19)) multiplexer_3 (
    .sel(instr[31]), .in_0({19{1'b0}}), .in_1({19{1'b1}}), .out(multiplexer_3_out));
  BarrelShifter #(.Bits(32)) LeftL (
    .in({multiplexer_1_out, instr[31], instr[19:12], instr[20], instr[30:21], 1'b0}), .shift(6'b000001),
    .out(LeftL_out));
  BarrelShifter #(.Bits(32)) LeftL_2 (
    .in({multiplexer_3_out, instr[31], instr[7], instr[30:25], instr[11:8], 1'b0}), .shift(6'b000001),
    .out(LeftL_2_out));
  and and_1 (and_1_out, bxx, result);
  Multiplexer #(.Bits(32)) multiplexer_4 (.sel(and_1_out), .in_0(32'h4), .in_1(LeftL_2_out), .out(multiplexer_4_out));
  Multiplexer #(.Selector_Bits(2), .Bits(32)) multiplexer_5 (
    .sel(pcw), .in_0(pc), .in_1(pc), .in_2(pc), .in_3(rs1), .out(multiplexer_5_out));
  Multiplexer #(.Selector_Bits(2), .Bits(32)) multiplexer_6 (
    .sel(pcw), .in_0(32'h4), .in_1(LeftL_out), .in_2(multiplexer_4_out),
    .in_3({multiplexer_2_out, instr[31:20]}), .out(multiplexer_6_out));
  Add #(.Bits(32)) add_1 (.a(multiplexer_5_out), .b(multiplexer_6_out), .c_i(1'b0), .s(add_1_s));  // open: c_o
  Register #(.Bits(32)) u_pc (.D(add_1_s), .C(clock), .en(pcen), .Q(pc));

  // Other names for the same wires on the sheet: pcOut[31:0] = pc
endmodule
