// Digital circuit risc-v-monocycle-cpu.dig as structural Verilog
module risc_v_monocycle_cpu (
  input  en,
  input  clock,
  output [8:0] pcOut,
  output [7:0] ramDataOut,
  output [7:0] ramDataIn,
  output [7:0] csrRDataOut,
  output csrW,
  output csrR,
  output ramW,
  output ramR,
  output rwe,
  output [7:0] clkCount,
  output [7:0] csrRDataIn
);

  wire monocycle_controller_1_bxx, monocycle_controller_1_sic, not_1_out, not_2_out, not_3_out;
  wire [1:0] monocycle_controller_1_mwf, monocycle_controller_1_pcw, monocycle_controller_1_rws;
  wire [2:0] monocycle_controller_1_a_x, monocycle_controller_1_a_y, monocycle_controller_1_mrf;
  wire [3:0] monocycle_controller_1_a_op;
  wire [7:6] monocycle_alu_1_rst;
  wire [15:0] multiplexer_3_out;
  wire [23:0] multiplexer_4_out;
  wire [31:0] cpuRam_d, cpuRom_d, monocycle_alui_1_x, monocycle_alui_1_y, monocycle_pc_1_pc,
       multiplexer_1_out, regsFile_da, regsFile_db;
  wire [31:8] csr_d, multiplexer_2_out, multiplexer_5_out;
  wire [31:10] monocycle_alu_1_rst_2;

  monocycle_pc monocycle_pc_1 (
    .instr(cpuRom_d), .pcw(monocycle_controller_1_pcw), .bxx(monocycle_controller_1_bxx), .clock(clock),
    .pcen(en), .rs1(regsFile_da), .result(csrRDataIn[0]),
    .pc({monocycle_pc_1_pc[31:11], pcOut, monocycle_pc_1_pc[1:0]}));
  ROM #(.AddrBits(9), .Bits(32)) cpuRom (.A(pcOut), .sel(1'b1), .D(cpuRom_d));
  monocycle_controller monocycle_controller_1 (
    .ins(cpuRom_d), .pcw(monocycle_controller_1_pcw), .bxx(monocycle_controller_1_bxx),
    .a_op(monocycle_controller_1_a_op), .a_x(monocycle_controller_1_a_x), .a_y(monocycle_controller_1_a_y),
    .siC(monocycle_controller_1_sic), .rwe(rwe), .rws(monocycle_controller_1_rws), .mw(ramW),
    .mRF(monocycle_controller_1_mrf), .mWF(monocycle_controller_1_mwf), .mR(ramR), .csrR(csrR), .csrW(csrW));
  Multiplexer #(.Selector_Bits(2), .Bits(32)) multiplexer_1 (
    .sel(monocycle_controller_1_rws), .in_0({monocycle_alu_1_rst_2, monocycle_alu_1_rst, csrRDataIn}),
    .in_1({multiplexer_5_out, ramDataOut}), .in_2({csr_d, csrRDataOut}), .in_3({32{1'b0}}),
    .out(multiplexer_1_out));
  not not_1 (not_1_out, clock);
  not not_2 (not_2_out, clock);
  RegisterFile #(.AddrBits(5), .Bits(32)) regsFile (
    .Din(multiplexer_1_out), .we(rwe), .Rw(cpuRom_d[11:7]), .C(not_1_out), .Ra(cpuRom_d[19:15]),
    .Rb(cpuRom_d[24:20]), .Da(regsFile_da), .Db(regsFile_db));
  RAMDualPort #(.AddrBits(8), .Bits(32)) csr (
    .A(cpuRom_d[27:20]), .Din({monocycle_alu_1_rst_2, monocycle_alu_1_rst, csrRDataIn}), .str(csrW),
    .C(not_2_out), .ld(csrR), .D({csr_d, csrRDataOut}));
  monocycle_aluI monocycle_alui_1 (
    .axI(monocycle_controller_1_a_x), .ayI(monocycle_controller_1_a_y), .siC(monocycle_controller_1_sic),
    .opc({monocycle_pc_1_pc[31:11], pcOut, monocycle_pc_1_pc[1:0]}), .ins(cpuRom_d), .rs1(regsFile_da),
    .rs2(regsFile_db), .csrIn({csr_d, csrRDataOut}), .x(monocycle_alui_1_x), .y(monocycle_alui_1_y));
  monocycle_alu monocycle_alu_1 (
    .alu_op(monocycle_controller_1_a_op), .x(monocycle_alui_1_x), .y(monocycle_alui_1_y),
    .rst({monocycle_alu_1_rst_2, monocycle_alu_1_rst, csrRDataIn}));
  Counter #(.Bits(8)) counter_1 (.en(en), .C(clock), .clr(1'b0), .out(clkCount));  // open: ovf
  not not_3 (not_3_out, clock);
  Multiplexer #(.Selector_Bits(2), .Bits(32)) multiplexer_2 (
    .sel(monocycle_controller_1_mwf), .in_0(regsFile_db), .in_1({{16{1'b0}}, regsFile_db[15:0]}),
    .in_2({{24{1'b0}}, regsFile_db[7:0]}), .in_3({32{1'b0}}), .out({multiplexer_2_out, ramDataIn}));
  RAMDualPort #(.AddrBits(8), .Bits(32)) cpuRam (
    .A({monocycle_alu_1_rst, csrRDataIn[7:2]}), .Din({multiplexer_2_out, ramDataIn}), .str(ramW),
    .C(not_3_out), .ld(ramR), .D(cpuRam_d));
  Multiplexer #(.Bits(16)) multiplexer_3 (
    .sel(cpuRam_d[15]), .in_0({16{1'b0}}), .in_1({16{1'b1}}), .out(multiplexer_3_out));
  Multiplexer #(.Bits(24)) multiplexer_4 (
    .sel(cpuRam_d[7]), .in_0({24{1'b0}}), .in_1({24{1'b1}}), .out(multiplexer_4_out));
  Multiplexer #(.Selector_Bits(3), .Bits(32)) multiplexer_5 (
    .sel(monocycle_controller_1_mrf), .in_0(cpuRam_d), .in_1({multiplexer_3_out, cpuRam_d[15:0]}),
    .in_2({{16{1'b0}}, cpuRam_d[15:0]}), .in_3({multiplexer_4_out, cpuRam_d[7:0]}),
    .in_4({{24{1'b0}}, cpuRam_d[7:0]}), .in_5({32{1'b0}}), .in_6({32{1'b0}}), .in_7({32{1'b0}}),
    .out({multiplexer_5_out, ramDataOut}));

  // Notes on the sheet:
  //   contents of cpuRom (hex, n*v repeats v):
  //   0,fffff0b7,400093,40016f,158513,feb50fe3,fff20193,318233,308023,309023,30a023,40a223,
  //   402383,800403,801403,804403,805403,802403,ff3a413,ffe3b413,fff44413,247493,249513,
  //   1f4d593,25d593,40125613,40460633,c616b3,c42733,c43733,864733,e6d7b3,40f75733,d77733,
  //   c76833,200713,11d873,11d873,810f3,710f3,a973,25973,1039f3,10f9f3,e7
endmodule
