// Digital circuit ID-EX.dig as structural Verilog
module ID_EX (
  input  [31:0] pi2,
  input  [31:0] ii2,
  input  preJ_IDEX,
  input  [31:0] rai1,
  input  [31:0] rbi1,
  input  [31:0] con1,
  input  clr2,
  input  en2,
  input  c2,
  input  [31:0] csrIn1,
  output [31:0] po2,
  output [31:0] io2,
  output [31:0] ra1,
  output [31:0] cono1,
  output [31:0] rb1,
  output preJo_IDEX,
  output [31:0] csr
);

  wire multiplexer_1_out;
  wire [31:0] multiplexer_2_out, multiplexer_3_out, multiplexer_4_out, multiplexer_5_out, multiplexer_6_out,
       multiplexer_7_out;

  Multiplexer multiplexer_1 (.sel(clr2), .in_0(preJ_IDEX), .in_1(1'b0), .out(multiplexer_1_out));
  Multiplexer #(.Bits(32)) multiplexer_2 (.sel(clr2), .in_0(pi2), .in_1({32{1'b0}}), .out(multiplexer_2_out));
  Multiplexer #(.Bits(32)) multiplexer_3 (.sel(clr2), .in_0(ii2), .in_1({32{1'b0}}), .out(multiplexer_3_out));
  Multiplexer #(.Bits(32)) multiplexer_4 (.sel(clr2), .in_0(con1), .in_1({32{1'b0}}), .out(multiplexer_4_out));
  Register #(.Bits(32)) pIn2 (.D(multiplexer_2_out), .C(c2), .en(en2), .Q(po2));
  Register #(.Bits(32)) iIn2 (.D(multiplexer_3_out), .C(c2), .en(en2), .Q(io2));
  Register #(.Bits(32)) controIn1 (.D(multiplexer_4_out), .C(c2), .en(en2), .Q(cono1));
  Register register_1 (.D(multiplexer_1_out), .C(c2), .en(en2), .Q(preJo_IDEX));
  Multiplexer #(.Bits(32)) multiplexer_5 (.sel(clr2), .in_0(rai1), .in_1({32{1'b0}}), .out(multiplexer_5_out));
  Multiplexer #(.Bits(32)) multiplexer_6 (.sel(clr2), .in_0(rbi1), .in_1({32{1'b0}}), .out(multiplexer_6_out));
  Multiplexer #(.Bits(32)) multiplexer_7 (.sel(clr2), .in_0(csrIn1), .in_1({32{1'b0}}), .out(multiplexer_7_out));
  Register #(.Bits(32)) u_raI1 (.D(multiplexer_5_out), .C(c2), .en(en2), .Q(ra1));
  Register #(.Bits(32)) u_rbI1 (.D(multiplexer_6_out), .C(c2), .en(en2), .Q(rb1));
  Register #(.Bits(32)) csr1 (.D(multiplexer_7_out), .C(c2), .en(en2), .Q(csr));

  // Other names for the same wires on the sheet: clkIn2 = c2; controIn1[31:0] = con1; controOut1[31:0] = cono1;
  //   insIn2[31:0] = ii2; insOut2[31:0] = io2; pcIn2[31:0] = pi2; pcOut2[31:0] = po2; preJIn = preJ_IDEX;
  //   preJOut = preJo_IDEX; raIn1[31:0] = rai1; rbIn1[31:0] = rbi1

  // Notes on the sheet:
  //   pi2: pc input
endmodule
