// Digital circuit IF-ID.dig as structural Verilog
module IF_ID (
  input  c1,
  input  [31:0] pi1,
  input  [31:0] ii1,
  input  clr1,
  input  en_IFID,
  input  preJ_IFID,
  output [31:0] po1,
  output [31:0] io1,
  output preJo_IFID
);

  wire multiplexer_3_out;
  wire [31:0] multiplexer_1_out, multiplexer_2_out;

  Multiplexer #(.Bits(32)) multiplexer_1 (.sel(clr1), .in_0(pi1), .in_1({32{1'b0}}), .out(multiplexer_1_out));
  Multiplexer #(.Bits(32)) multiplexer_2 (.sel(clr1), .in_0(ii1), .in_1({32{1'b0}}), .out(multiplexer_2_out));
  Multiplexer multiplexer_3 (.sel(clr1), .in_0(preJ_IFID), .in_1(1'b0), .out(multiplexer_3_out));
  Register #(.Bits(32)) pc1 (.D(multiplexer_1_out), .C(c1), .en(en_IFID), .Q(po1));
  Register #(.Bits(32)) ir1 (.D(multiplexer_2_out), .C(c1), .en(en_IFID), .Q(io1));
  Register register_1 (.D(multiplexer_3_out), .C(c1), .en(en_IFID), .Q(preJo_IFID));

  // Other names for the same wires on the sheet: clkIn1 = c1; clrIn1 = clr1; en1 = en_IFID; insIn1[31:0] = ii1;
  //   insOut1[31:0] = io1; pcIn1[31:0] = pi1; pcOut1[31:0] = po1; preJIn = preJ_IFID; preJOut = preJo_IFID
endmodule
