// Digital circuit ME-WB.dig as structural Verilog
module ME_WB (
  input  [31:0] ii4,
  input  en4,
  input  clr4,
  input  c4,
  input  [31:0] csri3,
  input  [31:0] con3,
  input  [31:0] aluRi2,
  input  [31:0] ramIn,
  output [31:0] io4,
  output [31:0] cono3,
  output [31:0] csr3,
  output [31:0] aluRo2,
  output [31:0] ramOut
);

  wire [31:0] multiplexer_1_out, multiplexer_2_out, multiplexer_3_out, multiplexer_4_out, multiplexer_5_out;

  Multiplexer #(.Bits(32)) multiplexer_1 (.sel(clr4), .in_0(con3), .in_1({32{1'b0}}), .out(multiplexer_1_out));
  Multiplexer #(.Bits(32)) multiplexer_2 (.sel(clr4), .in_0(ii4), .in_1({32{1'b0}}), .out(multiplexer_2_out));
  Multiplexer #(.Bits(32)) multiplexer_3 (.sel(clr4), .in_0(csri3), .in_1({32{1'b0}}), .out(multiplexer_3_out));
  Register #(.Bits(32)) register_1 (.D(multiplexer_1_out), .C(c4), .en(en4), .Q(cono3));
  Register #(.Bits(32)) register_2 (.D(multiplexer_2_out), .C(c4), .en(en4), .Q(io4));
  Register #(.Bits(32)) register_3 (.D(multiplexer_3_out), .C(c4), .en(en4), .Q(csr3));
  Multiplexer #(.Bits(32)) multiplexer_4 (.sel(clr4), .in_0(ramIn), .in_1({32{1'b0}}), .out(multiplexer_4_out));
  Multiplexer #(.Bits(32)) multiplexer_5 (.sel(clr4), .in_0(aluRi2), .in_1({32{1'b0}}), .out(multiplexer_5_out));
  Register #(.Bits(32)) register_4 (.D(multiplexer_4_out), .C(c4), .en(en4), .Q(ramOut));
  Register #(.Bits(32)) register_5 (.D(multiplexer_5_out), .C(c4), .en(en4), .Q(aluRo2));

  // Other names for the same wires on the sheet: aluOut2[31:0] = aluRo2; aluR2[31:0] = aluRi2; clkIn4 = c4;
  //   controIn3[31:0] = con3; controOut3[31:0] = cono3; csrIn3[31:0] = csri3; insIn4[31:0] = ii4; insOut4[31:0] = io4

  // Notes on the sheet:
  //   csr3: csr 寄存器的值
  //   aluRo2: alu output
  //   ramOut: alu output
endmodule
