// Digital circuit brachPre.dig as structural Verilog
module brachPre (
  input  [31:0] instr,
  input  [31:0] rs1,
  input  [1:0] pcws,
  input  [31:0] romD,
  input  preRI,
  input  clock,
  input  pcen,
  input  bubble,
  input  [31:0] oPc,
  input  ret,
  input  [31:0] mePc,
  input  [1:0] status,
  input  inters,
  output [31:0] PC,
  output preJPc,
  output [2:0] \type 
);

  wire and_1_out, and_2_out, and_3_out, multiplexer_7_out, not_1_out, not_2_out, or_1_out;
  wire [10:0] multiplexer_3_out;
  wire [18:0] multiplexer_4_out;
  wire [19:0] multiplexer_2_out;
  wire [31:0] add_1_s, add_2_s, add_3_s, LeftL_2_out, LeftL_3_out, LeftL_out, multiplexer_1_out,
       multiplexer_5_out, multiplexer_6_out, multiplexer_9_out, multiplexer_10_out, multiplexer_11_out,
       multiplexer_12_out;

  Multiplexer #(.Bits(32)) multiplexer_1 (.sel(preRI), .in_0(romD), .in_1(instr), .out(multiplexer_1_out));
  Multiplexer #(.Bits(20)) multiplexer_2 (
    .sel(multiplexer_1_out[31]), .in_0({20{1'b0}}), .in_1({20{1'b1}}), .out(multiplexer_2_out));
  Comparator #(.Bits(8)) BXX (.a({1'b0, multiplexer_1_out[6:0]}), .b(8'h63), .eq(\type [2]));  // open: gt, lt
  Multiplexer #(.Bits(11)) multiplexer_3 (
    .sel(multiplexer_1_out[31]), .in_0({11{1'b0}}), .in_1({11{1'b1}}), .out(multiplexer_3_out));
  Comparator #(.Bits(8)) JAL (.a({1'b0, multiplexer_1_out[6:0]}), .b(8'h6f), .eq(\type [0]));  // open: gt, lt
  Comparator #(.Bits(8)) JALR (.a({1'b0, multiplexer_1_out[6:0]}), .b(8'h67), .eq(\type [1]));  // open: gt, lt
  and and_1 (and_1_out, \type [2], multiplexer_1_out[31]);
  Multiplexer #(.Bits(19)) multiplexer_4 (
    .sel(multiplexer_1_out[31]), .in_0({19{1'b0}}), .in_1({19{1'b1}}), .out(multiplexer_4_out));
  BarrelShifter #(.Bits(32)) LeftL (
    .in({multiplexer_3_out, multiplexer_1_out[31], multiplexer_1_out[19:12], multiplexer_1_out[20], multiplexer_1_out[30:21], 1'b0}),
    .shift(6'b000001), .out(LeftL_out));
  BarrelShifter #(.Bits(32)) LeftL_2 (
    .in({multiplexer_4_out, multiplexer_1_out[31], multiplexer_1_out[7], multiplexer_1_out[30:25], multiplexer_1_out[11:8], 1'b0}),
    .shift(6'b000001), .out(LeftL_2_out));
  or or_1 (or_1_out, \type [0], and_1_out);
  Multiplexer #(.Bits(32)) multiplexer_5 (
    .sel(multiplexer_7_out), .in_0(32'h4), .in_1(LeftL_2_out), .out(multiplexer_5_out));
  Multiplexer #(.Bits(32)) multiplexer_6 (
    .sel(multiplexer_7_out), .in_0(32'h4), .in_1({multiplexer_2_out, multiplexer_1_out[31:20]}),
    .out(multiplexer_6_out));
  Multiplexer multiplexer_7 (.sel(preRI), .in_0(or_1_out), .in_1(not_1_out), .out(multiplexer_7_out));
  not not_1 (not_1_out, or_1_out);
  Multiplexer multiplexer_8 (.sel(preRI), .in_0(multiplexer_7_out), .in_1(1'b0), .out(preJPc));
  Multiplexer #(.Selector_Bits(3), .Bits(32)) multiplexer_9 (
    .sel(\type ), .in_0(32'h4), .in_1(LeftL_out), .in_2(multiplexer_6_out), .in_3({32{1'b0}}),
    .in_4(multiplexer_5_out), .in_5({32{1'b0}}), .in_6({32{1'b0}}), .in_7({32{1'b0}}), .out(multiplexer_9_out));
  Multiplexer #(.Bits(32)) multiplexer_10 (.sel(preRI), .in_0(PC), .in_1(oPc), .out(multiplexer_10_out));
  and and_2 (and_2_out, \type [1], multiplexer_7_out);
  Multiplexer #(.Bits(32)) multiplexer_11 (
    .sel(and_2_out), .in_0(multiplexer_10_out), .in_1(rs1), .out(multiplexer_11_out));
  Add #(.Bits(32)) add_1 (.a(multiplexer_11_out), .b(multiplexer_9_out), .c_i(1'b0), .s(add_1_s));  // open: c_o
  BarrelShifter #(.Bits(32)) LeftL_3 (.in({{30{1'b0}}, status}), .shift(6'b000010), .out(LeftL_3_out));
  Add #(.Bits(32)) add_2 (.a(32'hc0), .b(LeftL_3_out), .c_i(1'b0), .s(add_2_s));  // open: c_o
  Add #(.Bits(32)) add_3 (.a({3'b000, mePc[28:0]}), .b(32'h4), .c_i(1'b0), .s(add_3_s));  // open: c_o
  Multiplexer #(.Selector_Bits(2), .Bits(32)) multiplexer_12 (
    .sel({inters, ret}), .in_0(add_1_s), .in_1(add_3_s), .in_2(add_2_s), .in_3(add_1_s),
    .out(multiplexer_12_out));
  not not_2 (not_2_out, bubble);
  and and_3 (and_3_out, not_2_out, pcen);
  Register #(.Bits(32)) u_pc (.D(multiplexer_12_out), .C(clock), .en(and_3_out), .Q(PC));

  // Other names for the same wires on the sheet: originalPc[31:0] = oPc; pcOut[31:0] = PC; preJ = preJPc;
  //   preResult = preRI; romData[31:0] = romD

  // Notes on the sheet:
  //   preRI: 执行阶段检测之前bxx的预测结果
  //   preJPc: 预测跳转情况
  //   if bxx true imm else not jump 4
  //   if jarl imm else not jump 4
endmodule
