// Digital circuit bubble.dig as structural Verilog
module bubble (
  input  raRead,
  input  rbRead,
  input  [4:0] raAdd,
  input  [4:0] rbAdd,
  input  rwe_EX,
  input  [4:0] rw_EX,
  input  load,
  output bubble
);

  wire and_1_out, and_2_out, comparator_1_eq, comparator_2_eq, comparator_3_eq, comparator_4_eq,
       comparator_5_eq, not_1_out, not_2_out, not_3_out, or_1_out;

  Comparator #(.Bits(5)) comparator_1 (.a(rw_EX), .b({5{1'b0}}), .eq(comparator_1_eq));  // open: gt, lt
  Comparator #(.Bits(5)) comparator_2 (.a(raAdd), .b({5{1'b0}}), .eq(comparator_2_eq));  // open: gt, lt
  Comparator #(.Bits(5)) comparator_3 (.a(rbAdd), .b({5{1'b0}}), .eq(comparator_3_eq));  // open: gt, lt
  Comparator #(.Bits(5)) comparator_4 (.a(rw_EX), .b(raAdd), .eq(comparator_4_eq));  // open: gt, lt
  Comparator #(.Bits(5)) comparator_5 (.a(rw_EX), .b(rbAdd), .eq(comparator_5_eq));  // open: gt, lt
  not not_1 (not_1_out, comparator_1_eq);
  not not_2 (not_2_out, comparator_2_eq);
  not not_3 (not_3_out, comparator_3_eq);
  and and_1 (and_1_out, not_1_out, not_2_out, comparator_4_eq, raRead, rwe_EX);
  and and_2 (and_2_out, not_1_out, not_3_out, rbRead, comparator_5_eq, rwe_EX);
  or or_1 (or_1_out, and_1_out, and_2_out);
  and and_3 (bubble, or_1_out, load);

  // Other names for the same wires on the sheet: rwAdd[4:0] = rw_EX; rwEn = rwe_EX
endmodule
