// Digital circuit controller.dig as structural Verilog
module controller (
  input  [31:0] ins,
  output [3:0] a_op,
  output [2:0] a_x,
  output [2:0] a_y,
  output rwe,
  output [1:0] rws,
  output mw,
  output [1:0] pcw,
  output raR,
  output rbR,
  output csrR,
  output csrw,
  output bxx,
  output siC,
  output jalrj,
  output load,
  output mR,
  output [2:0] mRF,
  output [1:0] mWF,
  output mret,
  output wfi
);

  wire add, addi, \and , andi, auipc, beq, bge, bgeu, blt, bltu, bne, comparator_12_eq, comparator_13_eq,
       comparator_14_eq, comparator_15_eq, comparator_16_eq, comparator_17_eq, comparator_18_eq,
       comparator_19_eq, comparator_20_eq, comparator_21_eq, comparator_22_eq, comparator_23_eq,
       comparator_24_eq, comparator_25_eq, comparator_26_eq, comparator_27_eq, comparator_28_eq,
       comparator_29_eq, comparator_30_eq, comparator_31_eq, comparator_32_eq, comparator_33_eq,
       comparator_34_eq, comparator_35_eq, comparator_36_eq, comparator_37_eq, comparator_38_eq,
       comparator_39_eq, comparator_40_eq, comparator_41_eq, comparator_42_eq, comparator_43_eq,
       comparator_44_eq, comparator_45_eq, comparator_46_eq, comparator_47_eq, comparator_48_eq,
       comparator_49_eq, comparator_50_eq, comparator_51_eq, comparator_52_eq, comparator_53_eq,
       comparator_54_eq, comparator_55_eq, comparator_56_eq, comparator_57_eq, comparator_58_eq,
       comparator_59_eq, comparator_60_eq, comparator_61_eq, comparator_62_eq, comparator_63_eq,
       comparator_64_eq, comparator_65_eq, comparator_66_eq, csrrc, csrrci, csrrs, csrrsi, csrrw, csrrwi,
       ebreak, ecall, fence, fencei, jal, lb, lbu, lh, lhu, lui, lw, op_eq__eq_0F, op_eq__eq_03,
       op_eq__eq_13, op_eq__eq_23, op_eq__eq_33, op_eq__eq_63, op_eq__eq_73, \or , or_1_out, or_2_out,
       or_3_out, or_4_out, or_5_out, or_6_out, or_7_out, or_8_out, or_10_out, or_11_out, or_12_out,
       or_13_out, or_14_out, or_15_out, or_17_out, or_18_out, or_19_out, or_20_out, or_21_out, or_22_out,
       or_23_out, or_24_out, or_28_out, or_29_out, ori, sb, sh, sll, slli, slt, slti, sltiu, sltu, sra, srai,
       srl, srli, sub, sw, \xor , xori;

  Comparator #(.Signed("true"), .Bits(8)) comparator_1 (.a({1'b0, ins[6:0]}), .b(8'h37), .eq(lui));  // open: gt, lt
  Comparator #(.Signed("true"), .Bits(8)) comparator_2 (.a({1'b0, ins[6:0]}), .b(8'h17), .eq(auipc));  // open: gt, lt
  Comparator #(.Signed("true"), .Bits(8)) comparator_3 (.a({1'b0, ins[6:0]}), .b(8'h6f), .eq(jal));  // open: gt, lt
  Comparator #(.Signed("true"), .Bits(8)) comparator_4 (.a({1'b0, ins[6:0]}), .b(8'h67), .eq(jalrj));  // open: gt, lt
  Comparator #(.Signed("true"), .Bits(8)) comparator_5 (
    .a({1'b0, ins[6:0]}), .b(8'h63), .eq(op_eq__eq_63));  // open: gt, lt
  Comparator #(.Signed("true"), .Bits(8)) comparator_6 (
    .a({1'b0, ins[6:0]}), .b(8'h3), .eq(op_eq__eq_03));  // open: gt, lt
  Comparator #(.Signed("true"), .Bits(8)) comparator_7 (
    .a({1'b0, ins[6:0]}), .b(8'h23), .eq(op_eq__eq_23));  // open: gt, lt
  Comparator #(.Signed("true"), .Bits(8)) comparator_8 (
    .a({1'b0, ins[6:0]}), .b(8'h13), .eq(op_eq__eq_13));  // open: gt, lt
  Comparator #(.Bits(8)) comparator_9 (.a({1'b0, ins[6:0]}), .b(8'h33), .eq(op_eq__eq_33));  // open: gt, lt
  Comparator #(.Signed("true"), .Bits(8)) comparator_10 (
    .a({1'b0, ins[6:0]}), .b(8'hf), .eq(op_eq__eq_0F));  // open: gt, lt
  Comparator #(.Signed("true"), .Bits(8)) comparator_11 (
    .a({1'b0, ins[6:0]}), .b(8'h73), .eq(op_eq__eq_73));  // open: gt, lt
  Comparator #(.Bits(3)) comparator_12 (.a(ins[14:12]), .b(3'b000), .eq(comparator_12_eq));  // open: gt, lt
  Comparator #(.Bits(3)) comparator_13 (.a(ins[14:12]), .b(3'b001), .eq(comparator_13_eq));  // open: gt, lt
  Comparator #(.Bits(3)) comparator_14 (.a(ins[14:12]), .b(3'b100), .eq(comparator_14_eq));  // open: gt, lt
  Comparator #(.Bits(3)) comparator_15 (.a(ins[14:12]), .b(3'b101), .eq(comparator_15_eq));  // open: gt, lt
  Comparator #(.Bits(3)) comparator_16 (.a(ins[14:12]), .b(3'b110), .eq(comparator_16_eq));  // open: gt, lt
  Comparator #(.Bits(3)) comparator_17 (.a(ins[14:12]), .b(3'b111), .eq(comparator_17_eq));  // open: gt, lt
  Comparator #(.Bits(3)) comparator_18 (.a(ins[14:12]), .b(3'b000), .eq(comparator_18_eq));  // open: gt, lt
  Comparator #(.Bits(3)) comparator_19 (.a(ins[14:12]), .b(3'b001), .eq(comparator_19_eq));  // open: gt, lt
  Comparator #(.Bits(3)) comparator_20 (.a(ins[14:12]), .b(3'b010), .eq(comparator_20_eq));  // open: gt, lt
  Comparator #(.Bits(3)) comparator_21 (.a(ins[14:12]), .b(3'b100), .eq(comparator_21_eq));  // open: gt, lt
  Comparator #(.Bits(3)) comparator_22 (.a(ins[14:12]), .b(3'b101), .eq(comparator_22_eq));  // open: gt, lt
  or or_1 (or_1_out, lb, lbu, lw, lh, lhu);
  or or_2 (or_2_out, csrrw, csrrs, csrrc, csrrwi, csrrsi, csrrci);
  or or_3 (or_3_out, addi, slti, sltiu, andi, ori, xori, lb, lw, lh, lhu, sw, sh, sb, lbu);
  or or_4 (or_4_out, slli, srli, srai);
  or or_5 (or_5_out, lui, auipc);
  and and_1 (beq, comparator_12_eq, op_eq__eq_63);
  and and_2 (bne, comparator_13_eq, op_eq__eq_63);
  and and_3 (blt, comparator_14_eq, op_eq__eq_63);
  and and_4 (bge, comparator_15_eq, op_eq__eq_63);
  and and_5 (bltu, comparator_16_eq, op_eq__eq_63);
  and and_6 (bgeu, comparator_17_eq, op_eq__eq_63);
  and and_7 (lb, comparator_18_eq, op_eq__eq_03);
  and and_8 (lh, comparator_19_eq, op_eq__eq_03);
  and and_9 (lw, comparator_20_eq, op_eq__eq_03);
  and and_10 (lbu, comparator_21_eq, op_eq__eq_03);
  and and_11 (lhu, comparator_22_eq, op_eq__eq_03);
  PriorityEncoder #(.Selector_Bits(2)) rwsPri (
    .in0(1'b1), .in1(or_1_out), .in2(or_2_out), .in3(1'b0), .num(rws));  // open: any
  or or_6 (or_6_out, add, sub, slt, sltu, \and , \or , \xor , beq, bne, blt, bltu, bge, bgeu);
  or or_7 (or_7_out, sll, srl, sra);
  or or_8 (or_8_out, csrrw, csrrs, csrrc, csrrsi, csrrci);
  or or_9 (rwe, srai, csrrci, csrrsi, csrrwi, csrrc, csrrs, csrrw, \and , \or , sra, srl, \xor , sltu, slt, sll, sub, add, srli, slli, andi, ori, xori, sltiu, slti, addi, lhu, lbu, lw, lh, lb, jalrj, jal, auipc, lui);
  or or_10 (or_10_out, jal, jalrj);
  PriorityEncoder #(.Selector_Bits(3)) aluyPri (
    .in0(or_3_out), .in1(or_4_out), .in2(or_5_out), .in3(or_6_out), .in4(or_7_out), .in5(or_8_out),
    .in6(or_10_out), .in7(csrrwi), .num(a_y));  // open: any
  Comparator #(.Bits(3)) comparator_23 (.a(ins[14:12]), .b(3'b000), .eq(comparator_23_eq));  // open: gt, lt
  Comparator #(.Bits(3)) comparator_24 (.a(ins[14:12]), .b(3'b001), .eq(comparator_24_eq));  // open: gt, lt
  Comparator #(.Bits(3)) comparator_25 (.a(ins[14:12]), .b(3'b010), .eq(comparator_25_eq));  // open: gt, lt
  Comparator #(.Bits(3)) comparator_26 (.a(ins[14:12]), .b(3'b000), .eq(comparator_26_eq));  // open: gt, lt
  Comparator #(.Bits(3)) comparator_27 (.a(ins[14:12]), .b(3'b010), .eq(comparator_27_eq));  // open: gt, lt
  Comparator #(.Bits(3)) comparator_28 (.a(ins[14:12]), .b(3'b011), .eq(comparator_28_eq));  // open: gt, lt
  Comparator #(.Bits(3)) comparator_29 (.a(ins[14:12]), .b(3'b100), .eq(comparator_29_eq));  // open: gt, lt
  Comparator #(.Bits(3)) comparator_30 (.a(ins[14:12]), .b(3'b110), .eq(comparator_30_eq));  // open: gt, lt
  Comparator #(.Bits(3)) comparator_31 (.a(ins[14:12]), .b(3'b111), .eq(comparator_31_eq));  // open: gt, lt
  Comparator #(.Bits(3)) comparator_32 (.a(ins[14:12]), .b(3'b001), .eq(comparator_32_eq));  // open: gt, lt
  Comparator #(.Bits(3)) comparator_33 (.a(ins[14:12]), .b(3'b101), .eq(comparator_33_eq));  // open: gt, lt
  Comparator #(.Bits(7)) comparator_34 (.a(ins[31:25]), .b({7{1'b0}}), .eq(comparator_34_eq));  // open: gt, lt
  Comparator #(.Bits(3)) comparator_35 (.a(ins[14:12]), .b(3'b101), .eq(comparator_35_eq));  // open: gt, lt
  Comparator #(.Bits(7)) comparator_36 (.a(ins[31:25]), .b(7'b0100000), .eq(comparator_36_eq));  // open: gt, lt
  and and_12 (sb, comparator_23_eq, op_eq__eq_23);
  and and_13 (sh, comparator_24_eq, op_eq__eq_23);
  and and_14 (sw, comparator_25_eq, op_eq__eq_23);
  and and_15 (addi, comparator_26_eq, op_eq__eq_13);
  and and_16 (slti, comparator_27_eq, op_eq__eq_13);
  and and_17 (sltiu, comparator_28_eq, op_eq__eq_13);
  and and_18 (xori, comparator_29_eq, op_eq__eq_13);
  and and_19 (ori, comparator_30_eq, op_eq__eq_13);
  and and_20 (andi, comparator_31_eq, op_eq__eq_13);
  and and_21 (slli, comparator_32_eq, op_eq__eq_13);
  and and_22 (srli, comparator_33_eq, comparator_34_eq, op_eq__eq_13);
  and and_23 (srai, comparator_35_eq, comparator_36_eq, op_eq__eq_13);
  or or_11 (or_11_out, addi, auipc, add, jal, jalrj, lw, lh, lhu, lb, lbu, sw, sh, sb);
  or or_12 (or_12_out, slli, sll);
  or or_13 (or_13_out, srli, srl);
  or or_14 (or_14_out, srai, sra);
  or or_15 (or_15_out, andi, \and , csrrc, csrrci);
  or or_16 (mw, sw, sh, sb);
  or or_17 (or_17_out, ori, \or , csrrs, csrrsi);
  or or_18 (or_18_out, xori, \xor );
  or or_19 (or_19_out, slti, slt, blt);
  or or_20 (or_20_out, sltiu, bltu, sltu);
  or or_21 (or_21_out, auipc, jalrj, jal);
  or or_22 (or_22_out, csrrsi, csrrwi);
  Comparator #(.Bits(3)) comparator_37 (.a(ins[14:12]), .b(3'b000), .eq(comparator_37_eq));  // open: gt, lt
  Comparator #(.Bits(7)) comparator_38 (.a(ins[31:25]), .b({7{1'b0}}), .eq(comparator_38_eq));  // open: gt, lt
  Comparator #(.Bits(3)) comparator_39 (.a(ins[14:12]), .b(3'b000), .eq(comparator_39_eq));  // open: gt, lt
  Comparator #(.Bits(7)) comparator_40 (.a(ins[31:25]), .b(7'b0100000), .eq(comparator_40_eq));  // open: gt, lt
  Comparator #(.Bits(3)) comparator_41 (.a(ins[14:12]), .b(3'b001), .eq(comparator_41_eq));  // open: gt, lt
  Comparator #(.Bits(3)) comparator_42 (.a(ins[14:12]), .b(3'b010), .eq(comparator_42_eq));  // open: gt, lt
  Comparator #(.Bits(3)) comparator_43 (.a(ins[14:12]), .b(3'b011), .eq(comparator_43_eq));  // open: gt, lt
  Comparator #(.Bits(3)) comparator_44 (.a(ins[14:12]), .b(3'b100), .eq(comparator_44_eq));  // open: gt, lt
  Comparator #(.Bits(3)) comparator_45 (.a(ins[14:12]), .b(3'b101), .eq(comparator_45_eq));  // open: gt, lt
  Comparator #(.Bits(7)) comparator_46 (.a(ins[31:25]), .b({7{1'b0}}), .eq(comparator_46_eq));  // open: gt, lt
  Comparator #(.Bits(3)) comparator_47 (.a(ins[14:12]), .b(3'b101), .eq(comparator_47_eq));  // open: gt, lt
  Comparator #(.Bits(7)) comparator_48 (.a(ins[31:25]), .b(7'b0100000), .eq(comparator_48_eq));  // open: gt, lt
  Comparator #(.Bits(3)) comparator_49 (.a(ins[14:12]), .b(3'b110), .eq(comparator_49_eq));  // open: gt, lt
  Comparator #(.Bits(3)) comparator_50 (.a(ins[14:12]), .b(3'b111), .eq(comparator_50_eq));  // open: gt, lt
  or or_23 (or_23_out, beq, bne, blt, bltu, bge, bgeu);
  and and_24 (add, comparator_37_eq, comparator_38_eq, op_eq__eq_33);
  and and_25 (sub, comparator_39_eq, comparator_40_eq, op_eq__eq_33);
  and and_26 (sll, comparator_41_eq, op_eq__eq_33);
  and and_27 (slt, comparator_42_eq, op_eq__eq_33);
  and and_28 (sltu, comparator_43_eq, op_eq__eq_33);
  and and_29 (\xor , comparator_44_eq, op_eq__eq_33);
  and and_30 (srl, comparator_45_eq, comparator_46_eq, op_eq__eq_33);
  and and_31 (sra, comparator_47_eq, comparator_48_eq, op_eq__eq_33);
  and and_32 (\or , comparator_49_eq, op_eq__eq_33);
  and and_33 (\and , comparator_50_eq, op_eq__eq_33);
  or or_24 (or_24_out, csrrw, csrrwi);
  PriorityEncoder #(.Selector_Bits(3)) aluxPri (
    .in0(1'b1), .in1(or_21_out), .in2(or_22_out), .in3(csrrc), .in4(csrrci), .in5(lui), .in6(1'b0),
    .in7(1'b0), .num(a_x));  // open: any
  PriorityEncoder #(.Selector_Bits(2)) pcwPri (
    .in0(1'b1), .in1(jal), .in2(or_23_out), .in3(jalrj), .num(pcw));  // open: any
  PriorityEncoder #(.Selector_Bits(4)) aluopPri (
    .in0(or_11_out), .in1(sub), .in2(or_12_out), .in3(or_13_out), .in4(or_14_out), .in5(or_15_out),
    .in6(or_17_out), .in7(or_18_out), .in8(bge), .in9(or_19_out), .in10(beq), .in11(bgeu), .in12(or_20_out),
    .in13(bne), .in14(lui), .in15(or_24_out), .num(a_op));  // open: any
  Comparator #(.Bits(3)) comparator_51 (.a(ins[14:12]), .b(3'b000), .eq(comparator_51_eq));  // open: gt, lt
  Comparator #(.Bits(3)) comparator_52 (.a(ins[14:12]), .b(3'b001), .eq(comparator_52_eq));  // open: gt, lt
  Comparator #(.Bits(3)) comparator_53 (.a(ins[14:12]), .b(3'b000), .eq(comparator_53_eq));  // open: gt, lt
  Comparator #(.Bits(5)) comparator_54 (.a(ins[24:20]), .b({5{1'b0}}), .eq(comparator_54_eq));  // open: gt, lt
  Comparator #(.Bits(3)) comparator_55 (.a(ins[14:12]), .b(3'b000), .eq(comparator_55_eq));  // open: gt, lt
  Comparator #(.Bits(5)) comparator_56 (.a(ins[24:20]), .b(5'b00001), .eq(comparator_56_eq));  // open: gt, lt
  Comparator #(.Bits(3)) comparator_57 (.a(ins[14:12]), .b(3'b001), .eq(comparator_57_eq));  // open: gt, lt
  Comparator #(.Bits(3)) comparator_58 (.a(ins[14:12]), .b(3'b010), .eq(comparator_58_eq));  // open: gt, lt
  Comparator #(.Bits(3)) comparator_59 (.a(ins[14:12]), .b(3'b011), .eq(comparator_59_eq));  // open: gt, lt
  Comparator #(.Bits(3)) comparator_60 (.a(ins[14:12]), .b(3'b101), .eq(comparator_60_eq));  // open: gt, lt
  Comparator #(.Bits(3)) comparator_61 (.a(ins[14:12]), .b(3'b110), .eq(comparator_61_eq));  // open: gt, lt
  Comparator #(.Bits(3)) comparator_62 (.a(ins[14:12]), .b(3'b111), .eq(comparator_62_eq));  // open: gt, lt
  or or_25 (raR, addi, slti, sltiu, andi, ori, xori, slli, srli, srai, add, sub, slt, sltu, \and , \or , \xor , sll, srl, sra, jalrj, beq, bne, blt, bltu, bge, bgeu, lw, lh, lhu, lb, lbu, sw, sh, sb, csrrw, csrrs, csrrc);
  or or_26 (rbR, add, sub, slt, sltu, \and , \or , \xor , sll, srl, sra, beq, bne, blt, bltu, bge, bgeu, sw, sh, sb);
  or or_27 (csrR, csrrw, csrrwi, csrrs, csrrsi, csrrc, csrrci);
  or or_28 (or_28_out, addi, slti, sltiu, andi, ori, xori, lw, lh, lhu, lb, lbu);
  or or_29 (or_29_out, sw, sh, sb);
  or or_30 (bxx, beq, bne, blt, bltu, bge, bgeu);
  or or_31 (load, lw, lh, lhu, lb, lbu);
  or or_32 (mR, lw, lh, lhu, lb, lbu);
  PriorityEncoder #(.Selector_Bits(3)) memRF (
    .in0(lw), .in1(lh), .in2(lhu), .in3(lb), .in4(lbu), .in5(1'b0), .in6(1'b0), .in7(1'b0), .num(mRF));  // open: any
  PriorityEncoder #(.Selector_Bits(2)) memWFormat (.in0(sw), .in1(sh), .in2(sb), .in3(1'b0), .num(mWF));  // open: any
  and and_34 (fence, comparator_51_eq, op_eq__eq_0F);
  and and_35 (fencei, comparator_52_eq, op_eq__eq_0F);
  and and_36 (ecall, comparator_53_eq, comparator_54_eq, op_eq__eq_73);
  and and_37 (ebreak, comparator_55_eq, comparator_56_eq, op_eq__eq_73);
  and and_38 (csrrw, comparator_57_eq, op_eq__eq_73);
  and and_39 (csrrs, comparator_58_eq, op_eq__eq_73);
  and and_40 (csrrc, comparator_59_eq, op_eq__eq_73);
  and and_41 (csrrwi, comparator_60_eq, op_eq__eq_73);
  and and_42 (csrrsi, comparator_61_eq, op_eq__eq_73);
  and and_43 (csrrci, comparator_62_eq, op_eq__eq_73);
  PriorityEncoder priorityencoder_1 (.in0(or_28_out), .in1(or_29_out), .num(siC));  // open: any
  Comparator #(.Bits(2)) comparator_63 (.a(ins[29:28]), .b(2'b11), .eq(comparator_63_eq));  // open: gt, lt
  Comparator #(.Bits(5)) comparator_64 (.a(ins[24:20]), .b(5'b00010), .eq(comparator_64_eq));  // open: gt, lt
  Comparator #(.Bits(2)) comparator_65 (.a(ins[29:28]), .b(2'b01), .eq(comparator_65_eq));  // open: gt, lt
  Comparator #(.Bits(5)) comparator_66 (.a(ins[24:20]), .b(5'b00101), .eq(comparator_66_eq));  // open: gt, lt
  and and_44 (mret, comparator_63_eq, comparator_64_eq, op_eq__eq_73);
  and and_45 (wfi, comparator_65_eq, comparator_66_eq, op_eq__eq_73);

  assign csrw = csrR;

  // Other names for the same wires on the sheet: aluop[3:0] = a_op; alux[2:0] = a_x; aluy[2:0] = a_y;
  //   op[6:0] = ins[6:0]; fun3[2:0] = ins[14:12]; inter[4:0] = ins[24:20]; fun7[6:0] = ins[31:25];
  //   ret[1:0] = ins[29:28]; jalr = jalrj; loadUse = load; memR = mR; memRFormat[2:0] = mRF; memw = mw;
  //   memWFormat[1:0] = mWF; rWsrc[1:0] = rws

  // Notes on the sheet:
  //   rws: 寄存器写入数据来源，ram或alu
  //   mw: memory write
  //   pcw: pc数据源（顺序取指令pc+4,jal bxx pc+立即数，jalr pc+rs）
  //   0->pc+4
  //   1->jarl
  //   2->jal
  //   3->bxx
  //   raR: ra read
  //   rbR: ra read
  //   siC: aluy的SEimm 来源于12位连续立即数，还是由不同位拼接而成
  //   0表示连续12位，1表示拼接,sw,sh,sb是拼接
  //   jalrj: jarl跳转
  //   load: 判断是否是load相关指令，决定是否插入气泡
  //   mR: memory read
  //   mRF: memory Read format
  //   mWF: memory write format
  //   000 SEimm->aluy
  //   001 ZEimm->aluy
  //   010 imm shift lefit 12 bits
  //   011 rs2->aluy
  //   100 ZErs2[4:0]->aluy
  //   101 csr 110->4
  //   111 ->0
  //   register write source  
  //   00->aluR 
  //   01->ram 10->csr
  //   aluop=0000  +
  //   aluop=0010
  //    logic left
  //   0011 logic right
  //   0100 arithmetic right
  //   0101 and
  //   0110 or
  //   0111 xor
  //   1001 s<
  //   1100 <
  //   1110 ==  aluy stright
  //   1111 alux stright
  //   000  default rs1->alux
  //   001 pc->alux
  //   010 ZEimm->alux
  //   011  not rs1->alux
  //   100 not ZEimm->alux
  //   101  0->alux
  //   pcw  00->pc+4 
  //   01->pc+imm(jal)
  //   10->pc+imm(bxx)
  //   11->rs1+imm(jalr)
endmodule
