// Digital circuit judgePre.dig as structural Verilog
module judgePre (
  input  bxxI,
  input  preJI,
  input  [31:0] aluRI,
  input  jalrj,
  output preRo
);

  wire and_1_out, comparator_1_eq, multiplexer_1_out, multiplexer_2_out;

  and and_1 (and_1_out, bxxI, aluRI[0]);
  Comparator comparator_1 (.a(multiplexer_2_out), .b(preJI), .eq(comparator_1_eq));  // open: gt, lt
  Multiplexer multiplexer_1 (.sel(jalrj), .in_0(comparator_1_eq), .in_1(1'b0), .out(multiplexer_1_out));
  Multiplexer multiplexer_2 (.sel(bxxI), .in_0(preJI), .in_1(and_1_out), .out(multiplexer_2_out));
  not not_1 (preRo, multiplexer_1_out);

  // Other names for the same wires on the sheet: aluRIn[31:0] = aluRI; bxxIn = bxxI; jalr = jalrj; preJIn = preJI;
  //   preRout = preRo

  // Notes on the sheet:
  //   preJI: 前面的跳转预测结果
  //   preRo: 判断预测是否正确
endmodule
