// Digital circuit redirect.dig as structural Verilog
module redirect (
  input  raR,
  input  rbR,
  input  csrR,
  input  rwe_ME,
  input  rwe_WB,
  input  csrwe_ME,
  input  [4:0] raA,
  input  [4:0] rbA,
  input  [11:0] csrA,
  input  [4:0] rw_ME,
  input  [4:0] rw_WB,
  input  [11:0] csrw_ME,
  input  [11:0] csrw_WB,
  input  csrwe_WB,
  output [3:0] aluRed,
  output [1:0] csrRed
);

  wire comparator_1_eq, comparator_2_eq, comparator_3_eq, comparator_4_eq, comparator_5_eq, comparator_6_eq,
       comparator_7_eq, comparator_8_eq, comparator_9_eq, comparator_10_eq, not_1_out, not_2_out, not_3_out,
       not_4_out;

  Comparator #(.Bits(5)) comparator_1 (.a(rw_ME), .b({5{1'b0}}), .eq(comparator_1_eq));  // open: gt, lt
  Comparator #(.Bits(5)) comparator_2 (.a(rw_WB), .b({5{1'b0}}), .eq(comparator_2_eq));  // open: gt, lt
  Comparator #(.Bits(5)) comparator_3 (.a(raA), .b({5{1'b0}}), .eq(comparator_3_eq));  // open: gt, lt
  Comparator #(.Bits(5)) comparator_4 (.a(rbA), .b({5{1'b0}}), .eq(comparator_4_eq));  // open: gt, lt
  Comparator #(.Bits(5)) comparator_5 (.a(rw_ME), .b(raA), .eq(comparator_5_eq));  // open: gt, lt
  Comparator #(.Bits(5)) comparator_6 (.a(rw_ME), .b(rbA), .eq(comparator_6_eq));  // open: gt, lt
  Comparator #(.Bits(5)) comparator_7 (.a(rw_WB), .b(raA), .eq(comparator_7_eq));  // open: gt, lt
  Comparator #(.Bits(5)) comparator_8 (.a(rw_WB), .b(rbA), .eq(comparator_8_eq));  // open: gt, lt
  Comparator #(.Bits(12)) comparator_9 (.a(csrw_ME), .b(csrA), .eq(comparator_9_eq));  // open: gt, lt
  Comparator #(.Bits(12)) comparator_10 (.a(csrw_WB), .b(csrA), .eq(comparator_10_eq));  // open: gt, lt
  not not_1 (not_1_out, comparator_1_eq);
  not not_2 (not_2_out, comparator_2_eq);
  not not_3 (not_3_out, comparator_3_eq);
  not not_4 (not_4_out, comparator_4_eq);
  and and_1 (csrRed[0], comparator_9_eq, csrR, csrwe_ME);
  and and_2 (csrRed[1], comparator_10_eq, csrR, csrwe_WB);
  and and_3 (aluRed[0], not_1_out, not_3_out, comparator_5_eq, raR, rwe_ME);
  and and_4 (aluRed[1], not_1_out, not_4_out, comparator_6_eq, rbR, rwe_ME);
  and and_5 (aluRed[2], not_2_out, not_3_out, comparator_7_eq, raR, rwe_WB);
  and and_6 (aluRed[3], not_2_out, not_4_out, comparator_8_eq, rbR, rwe_WB);

  // Other names for the same wires on the sheet: csrRedirect[1:0] = csrRed; aluRedirect[3:0] = aluRed;
  //   csrAdd[11:0] = csrA; csrRead = csrR; raAdd[4:0] = raA; raRead = raR; rbAdd[4:0] = rbA; rbRead = rbR

  // Notes on the sheet:
  //   aluRed: aluRedirect
  //   csrRed: csrRedirect
  //   redirect RA-WB
  //   redirect RA-ME
  //   redirect RB-ME
  //   redirect RB-WB
  //   redirect csr-ME
  //   redirect csr-WB
  //   01 csr_me
  //   10 csr_wb
  //   0001 ra-me
  //   0010 rb-me
  //   0100 ra-wb
  //   1000rb-wb
endmodule
