// Digital circuit regCache.dig as structural Verilog
module regCache (
  input  [31:0] pcData,
  input  clockIn,
  input  preJF,
  input  bubble,
  output [31:0] out
);

  wire not_1_out;
  wire [31:0] multiplexer_1_out;

  Multiplexer #(.Bits(32)) multiplexer_1 (.sel(preJF), .in_0(pcData), .in_1({32{1'b0}}), .out(multiplexer_1_out));
  not not_1 (not_1_out, bubble);
  Register #(.Bits(32)) register_1 (.D(multiplexer_1_out), .C(clockIn), .en(not_1_out), .Q(out));
endmodule
