// Digital circuit risc-v-cpu.dig as structural Verilog
module risc_v_cpu (
  input  clock,
  input  enable,
  input  clear,
  input  reset,
  output [7:0] clkCount,
  output [7:0] pcOut,
  output inter,
  output ret,
  output [1:0] status,
  output [1:0] exeStatus,
  output interp1,
  output interp2,
  output interp3
);

  wire and_2_out, and_3_out, and_4_out, and_6_out, and_7_out, and_8_out, and_9_out, brachpre_1_p15, bubble,
       clear_IDEX, comparator_1_eq, comparator_2_lt, comparator_5_eq, comparator_6_eq, comparator_7_eq,
       comparator_11_eq, counter_2_out, en_IFID, id_ex_1_prejo_idex, if_id_1_prejo_ifid, inter1, inter2,
       inter3, interbubble, interO, multiplexer_3_out, multiplexer_11_out, multiplexer_12_out,
       multiplexer_13_out, not_1_out, not_2_out, not_3_out, not_4_out, not_5_out, not_6_out, not_7_out,
       not_8_out, not_9_out, not_10_out, not_11_out, not_12_out, or_1_out, or_2_out, or_4_out, or_5_out,
       or_6_out, or_7_out, or_8_out, or_9_out, preJF, Reg2_q;
  wire [1:0] controller_1_mwf, controller_1_pcw, controller_1_rws, counter_1_out, csrRedirect,
       multiplexer_4_out, rws1, rws2;
  wire [2:0] controller_1_a_x, controller_1_a_y, controller_1_mrf, me_wb_1_cono3_2;
  wire [3:0] aluRedirect, controller_1_a_op;
  wire [4:0] brachpre_1_p1_2, ex_me_1_io3_2, me_wb_1_io4_2;
  wire [7:0] brachpre_1_p14_2, multiplexer_1_out;
  wire [11:0] ex_me_1_io3_3, me_wb_1_io4_3;
  wire [15:0] multiplexer_15_out;
  wire [19:0] ex_me_1_io3, me_wb_1_io4;
  wire [23:0] multiplexer_16_out;
  wire [28:8] brachpre_1_p9;
  wire [31:0] alu_1_rst, alui_1_x, alui_1_y, brachpre_1_p1, brachpre_1_p4, brachpre_1_p14, counter_4_out,
       counter_5_out, counter_6_out, ex_me_1_aluro1, ex_me_1_cono2, ex_me_1_csr2, ex_me_1_rb2, id_ex_1_cono1,
       id_ex_1_csr, id_ex_1_ra1, id_ex_1_rb1, if_id_1_io1, if_id_1_po1, me_wb_1_aluro2, me_wb_1_cono3,
       me_wb_1_csr3, me_wb_1_ramout, mepc, mpc, multiplexer_2_out, multiplexer_5_out, multiplexer_6_out,
       multiplexer_7_out, multiplexer_8_out, multiplexer_9_out, multiplexer_14_out, multiplexer_17_out,
       multiplexer_18_out, registerfile_1_da, registerfile_1_db, rs1;
  wire [31:10] controller_1_wfi;
  wire [31:29] brachpre_1_p9_2;

  or or_1 (or_1_out, preJF, ret, inter);
  not not_1 (not_1_out, clock);
  // brachPre brachpre_1: pin names not known; wires that end beside it: {brachpre_1_p1[31:12], brachpre_1_p1_2, brachpre_1_p1[6:0]}, rs1, 3'b000, brachpre_1_p4, preJF, clock, enable, bubble, {brachpre_1_p9_2, brachpre_1_p9, pcOut}, ret, mpc, status, inter, {brachpre_1_p14[31:10], brachpre_1_p14_2, brachpre_1_p14[1:0]}, brachpre_1_p15
  // LRom #(.AddrBits(8), .Bits(32)) rom1: pin names not known; wires that end beside it: brachpre_1_p14_2, not_1_out, 1'b1, 1'b0, brachpre_1_p4
  IF_ID if_id_1 (
    .c1(clock), .pi1({brachpre_1_p14[31:10], brachpre_1_p14_2, brachpre_1_p14[1:0]}), .ii1(brachpre_1_p4),
    .clr1(or_1_out), .en_IFID(en_IFID), .preJ_IFID(brachpre_1_p15), .po1(if_id_1_po1), .io1(if_id_1_io1),
    .preJo_IFID(if_id_1_prejo_ifid));
  Multiplexer #(.Bits(8)) multiplexer_1 (
    .sel(inter), .in_0(me_wb_1_io4_3[7:0]), .in_1({8{1'b0}}), .out(multiplexer_1_out));
  controller controller_1 (
    .ins(if_id_1_io1), .a_op(controller_1_a_op), .a_x(controller_1_a_x), .a_y(controller_1_a_y),
    .rwe(controller_1_wfi[10]), .rws(controller_1_rws), .mw(controller_1_wfi[13]), .pcw(controller_1_pcw),
    .raR(controller_1_wfi[16]), .rbR(controller_1_wfi[17]), .csrR(controller_1_wfi[18]),
    .csrw(controller_1_wfi[19]), .bxx(controller_1_wfi[20]), .siC(controller_1_wfi[21]),
    .jalrj(controller_1_wfi[22]), .load(controller_1_wfi[23]), .mR(controller_1_wfi[24]),
    .mRF(controller_1_mrf), .mWF(controller_1_mwf), .mret(controller_1_wfi[30]), .wfi(controller_1_wfi[31]));
  Multiplexer #(.Bits(32)) multiplexer_2 (
    .sel(inter), .in_0(me_wb_1_aluro2), .in_1({exeStatus, 1'b1, brachpre_1_p9, pcOut}),
    .out(multiplexer_2_out));
  Multiplexer multiplexer_3 (.sel(inter), .in_0(and_9_out), .in_1(1'b1), .out(multiplexer_3_out));
  or or_2 (or_2_out, inter, ret);
  Multiplexer #(.Bits(2)) multiplexer_4 (.sel(ret), .in_0(status), .in_1(mpc[31:30]), .out(multiplexer_4_out));
  not not_2 (not_2_out, clock);
  not not_3 (not_3_out, bubble);
  or or_3 (clear_IDEX, bubble, ret, preJF);
  Register Reg2 (.D(ret), .C(clock), .en(or_2_out), .Q(Reg2_q));
  or or_4 (or_4_out, ret, inter);
  or or_5 (or_5_out, preJF, ret);
  and and_1 (en_IFID, not_3_out, enable);
  // LRamDP #(.AddrBits(8), .Bits(32)) csr: pin names not known; wires that end beside it: multiplexer_1_out, {8{1'b0}}, multiplexer_2_out, multiplexer_3_out, 1'b1, clock, multiplexer_3_out, clock, reset, mepc
  RegisterFile #(.AddrBits(5), .Bits(32)) registerfile_1 (
    .Din(multiplexer_8_out), .we(and_2_out), .Rw(me_wb_1_io4_2), .C(not_2_out), .Ra(if_id_1_io1[19:15]),
    .Rb(if_id_1_io1[24:20]), .Da(registerfile_1_da), .Db(registerfile_1_db));
  not not_4 (not_4_out, mepc[29]);
  not not_5 (not_5_out, interO);
  not not_6 (not_6_out, interbubble);
  not not_7 (not_7_out, comparator_1_eq);
  and and_2 (and_2_out, me_wb_1_cono3[10], not_7_out);
  and and_3 (and_3_out, interO, interbubble, not_4_out);
  and and_4 (and_4_out, Reg2_q, interO);
  Register #(.Bits(2)) Reg1 (.D(multiplexer_4_out), .C(clock), .en(or_4_out), .Q(exeStatus));
  Counter #(.Bits(2)) counter_1 (.en(not_5_out), .C(clock), .clr(or_5_out), .out(counter_1_out));  // open: ovf
  Counter counter_2 (.en(not_6_out), .C(clock), .clr(bubble), .out(counter_2_out));  // open: ovf
  Comparator #(.Bits(5)) comparator_1 (.a(me_wb_1_io4_2), .b({5{1'b0}}), .eq(comparator_1_eq));  // open: gt, lt
  bubble bubble_1 (
    .raRead(controller_1_wfi[16]), .rbRead(controller_1_wfi[17]), .raAdd(if_id_1_io1[19:15]),
    .rbAdd(if_id_1_io1[24:20]), .rwe_EX(id_ex_1_cono1[10]), .rw_EX(brachpre_1_p1_2),
    .load(id_ex_1_cono1[23]), .bubble(bubble));
  or or_6 (or_6_out, and_3_out, and_4_out);
  Comparator #(.Bits(2)) comparator_2 (.a(exeStatus), .b(status), .lt(comparator_2_lt));  // open: gt, eq
  Comparator #(.Bits(2)) comparator_3 (.a(counter_1_out), .b(2'b10), .eq(interO));  // open: gt, lt
  Comparator comparator_4 (.a(counter_2_out), .b(1'b1), .eq(interbubble));  // open: gt, lt
  not not_8 (not_8_out, inter);
  and and_5 (inter, or_6_out, comparator_2_lt);
  ID_EX id_ex_1 (
    .pi2(if_id_1_po1), .ii2(if_id_1_io1), .preJ_IDEX(if_id_1_prejo_ifid), .rai1(registerfile_1_da),
    .rbi1(registerfile_1_db),
    .con1({controller_1_wfi[31:30], controller_1_mwf, controller_1_mrf, controller_1_wfi[24:16], controller_1_pcw, controller_1_wfi[13], controller_1_rws, controller_1_wfi[10], controller_1_a_y, controller_1_a_x, controller_1_a_op}),
    .clr2(clear_IDEX), .en2(not_8_out), .c2(clock), .csrIn1(mepc),
    .po2({brachpre_1_p9_2, brachpre_1_p9, pcOut}),
    .io2({brachpre_1_p1[31:12], brachpre_1_p1_2, brachpre_1_p1[6:0]}), .ra1(id_ex_1_ra1),
    .cono1({id_ex_1_cono1[31], ret, id_ex_1_cono1[29:0]}), .rb1(id_ex_1_rb1),
    .preJo_IDEX(id_ex_1_prejo_idex), .csr(id_ex_1_csr));
  Counter #(.Bits(8)) counter_3 (.en(enable), .C(clock), .clr(1'b0), .out(clkCount));  // open: ovf
  Comparator #(.Bits(2)) comparator_5 (.a(status), .b(2'b01), .eq(comparator_5_eq));  // open: gt, lt
  Comparator #(.Bits(2)) comparator_6 (.a(status), .b(2'b10), .eq(comparator_6_eq));  // open: gt, lt
  Comparator #(.Bits(2)) comparator_7 (.a(status), .b(2'b11), .eq(comparator_7_eq));  // open: gt, lt
  and and_6 (and_6_out, comparator_5_eq, inter);
  and and_7 (and_7_out, comparator_6_eq, inter);
  and and_8 (and_8_out, comparator_7_eq, inter);
  Multiplexer #(.Selector_Bits(2), .Bits(32)) multiplexer_5 (
    .sel(rws1), .in_0(ex_me_1_aluro1), .in_1({32{1'b0}}), .in_2(ex_me_1_csr2), .in_3({32{1'b0}}),
    .out(multiplexer_5_out));
  Multiplexer #(.Selector_Bits(2), .Bits(32)) multiplexer_6 (
    .sel(rws2), .in_0(me_wb_1_aluro2), .in_1(me_wb_1_ramout), .in_2(me_wb_1_csr3), .in_3({32{1'b0}}),
    .out(multiplexer_6_out));
  Multiplexer #(.Selector_Bits(2), .Bits(32)) multiplexer_7 (
    .sel(rws1), .in_0(ex_me_1_aluro1), .in_1({32{1'b0}}), .in_2(ex_me_1_csr2), .in_3({32{1'b0}}),
    .out(multiplexer_7_out));
  Multiplexer #(.Selector_Bits(2), .Bits(32)) multiplexer_8 (
    .sel(rws2), .in_0(me_wb_1_aluro2), .in_1(me_wb_1_ramout), .in_2(me_wb_1_csr3), .in_3({32{1'b0}}),
    .out(multiplexer_8_out));
  or or_7 (or_7_out, and_8_out, inter3);
  redirect redirect_1 (
    .raR(id_ex_1_cono1[16]), .rbR(id_ex_1_cono1[17]), .csrR(id_ex_1_cono1[18]), .rwe_ME(ex_me_1_cono2[10]),
    .rwe_WB(me_wb_1_cono3[10]), .csrwe_ME(ex_me_1_cono2[19]), .raA(brachpre_1_p1[19:15]),
    .rbA(brachpre_1_p1[24:20]), .csrA(brachpre_1_p1[31:20]), .rw_ME(ex_me_1_io3_2), .rw_WB(me_wb_1_io4_2),
    .csrw_ME(ex_me_1_io3_3), .csrw_WB(me_wb_1_io4_3), .csrwe_WB(me_wb_1_cono3[19]), .aluRed(aluRedirect),
    .csrRed(csrRedirect));
  Multiplexer #(.Selector_Bits(2), .Bits(32)) multiplexer_9 (
    .sel({aluRedirect[3], aluRedirect[1]}), .in_0(id_ex_1_rb1), .in_1(multiplexer_7_out),
    .in_2(multiplexer_8_out), .in_3(multiplexer_7_out), .out(multiplexer_9_out));
  or or_8 (or_8_out, and_6_out, inter1);
  or or_9 (or_9_out, and_7_out, inter2);
  Multiplexer #(.Selector_Bits(2), .Bits(32)) multiplexer_10 (
    .sel({aluRedirect[2], aluRedirect[0]}), .in_0(id_ex_1_ra1), .in_1(multiplexer_5_out),
    .in_2(multiplexer_6_out), .in_3(multiplexer_5_out), .out(rs1));
  Multiplexer multiplexer_11 (.sel(inter1), .in_0(1'b0), .in_1(1'b1), .out(multiplexer_11_out));
  Multiplexer multiplexer_12 (.sel(inter2), .in_0(1'b0), .in_1(1'b1), .out(multiplexer_12_out));
  Multiplexer multiplexer_13 (.sel(inter3), .in_0(1'b0), .in_1(1'b1), .out(multiplexer_13_out));
  Register register_1 (.D(multiplexer_11_out), .C(clock), .en(or_8_out), .Q(interp1));
  Register register_2 (.D(multiplexer_12_out), .C(clock), .en(or_9_out), .Q(interp2));
  Register register_3 (.D(multiplexer_13_out), .C(clock), .en(or_7_out), .Q(interp3));
  ALUI alui_1 (
    .ins({brachpre_1_p1[31:12], brachpre_1_p1_2, brachpre_1_p1[6:0]}), .rs1(rs1),
    .opc({brachpre_1_p9_2, brachpre_1_p9, pcOut}), .rs2(multiplexer_9_out), .axI(id_ex_1_cono1[6:4]),
    .ayI(id_ex_1_cono1[9:7]), .siC(id_ex_1_cono1[21]), .csrIn(multiplexer_14_out), .x(alui_1_x), .y(alui_1_y));
  judgePre judgepre_1 (
    .bxxI(id_ex_1_cono1[20]), .preJI(id_ex_1_prejo_idex), .aluRI(alu_1_rst), .jalrj(id_ex_1_cono1[22]),
    .preRo(preJF));
  Multiplexer #(.Selector_Bits(2), .Bits(32)) multiplexer_14 (
    .sel(csrRedirect), .in_0(id_ex_1_csr), .in_1(ex_me_1_aluro1), .in_2(me_wb_1_aluro2),
    .in_3(ex_me_1_aluro1), .out(multiplexer_14_out));
  ALU alu_1 (.alu_op(id_ex_1_cono1[3:0]), .x(alui_1_x), .y(alui_1_y), .rst(alu_1_rst));
  not not_9 (not_9_out, inter);
  Counter #(.Bits(32)) counter_4 (.en(enable), .C(clock), .clr(1'b0), .out(counter_4_out));  // open: ovf
  Counter #(.Bits(32)) counter_5 (.en(enable), .C(clock), .clr(1'b0), .out(counter_5_out));  // open: ovf
  Counter #(.Bits(32)) counter_6 (.en(enable), .C(clock), .clr(1'b0), .out(counter_6_out));  // open: ovf
  EX_ME ex_me_1 (
    .ii3({brachpre_1_p1[31:12], brachpre_1_p1_2, brachpre_1_p1[6:0]}), .en3(not_9_out), .clr3(1'b0),
    .rbi2(multiplexer_9_out), .csri2(multiplexer_14_out),
    .con2({id_ex_1_cono1[31], ret, id_ex_1_cono1[29:0]}), .c3(clock), .aluRi1(alu_1_rst),
    .cono2({ex_me_1_cono2[31:13], rws1, ex_me_1_cono2[10:0]}), .csr2(ex_me_1_csr2), .rb2(ex_me_1_rb2),
    .aluRo1(ex_me_1_aluro1), .io3({ex_me_1_io3_3, ex_me_1_io3[19:12], ex_me_1_io3_2, ex_me_1_io3[6:0]}));
  Comparator #(.Bits(32)) comparator_8 (.a(counter_4_out), .b(32'h3), .eq(inter1));  // open: gt, lt
  Comparator #(.Bits(32)) comparator_9 (.a(counter_5_out), .b(32'ha), .eq(inter2));  // open: gt, lt
  Comparator #(.Bits(32)) comparator_10 (.a(counter_6_out), .b(32'ha), .eq(inter3));  // open: gt, lt
  PriorityEncoder #(.Selector_Bits(2)) priorityencoder_1 (
    .in0(1'b0), .in1(interp1), .in2(interp2), .in3(interp3), .num(status));  // open: any
  Multiplexer #(.Bits(16)) multiplexer_15 (
    .sel(mpc[15]), .in_0({16{1'b0}}), .in_1({16{1'b1}}), .out(multiplexer_15_out));
  Multiplexer #(.Bits(24)) multiplexer_16 (
    .sel(mpc[7]), .in_0({24{1'b0}}), .in_1({24{1'b1}}), .out(multiplexer_16_out));
  Multiplexer #(.Selector_Bits(2), .Bits(32)) multiplexer_17 (
    .sel(ex_me_1_cono2[29:28]), .in_0(ex_me_1_rb2), .in_1({{16{1'b0}}, ex_me_1_rb2[15:0]}),
    .in_2({{24{1'b0}}, ex_me_1_rb2[7:0]}), .in_3({32{1'b0}}), .out(multiplexer_17_out));
  not not_10 (not_10_out, clock);
  // LRamDP #(.AddrBits(8), .Bits(32)) ram1: pin names not known; wires that end beside it: ex_me_1_aluro1[9:2], ex_me_1_aluro1[9:2], multiplexer_17_out, 1'b1, ex_me_1_cono2[24], not_10_out, ex_me_1_cono2[13], not_10_out, reset, mpc
  Multiplexer #(.Selector_Bits(3), .Bits(32)) multiplexer_18 (
    .sel(me_wb_1_cono3_2), .in_0(mpc), .in_1({multiplexer_15_out, mpc[15:0]}),
    .in_2({{16{1'b0}}, mpc[15:0]}), .in_3({multiplexer_16_out, mpc[7:0]}), .in_4({{24{1'b0}}, mpc[7:0]}),
    .in_5({32{1'b0}}), .in_6({32{1'b0}}), .in_7({32{1'b0}}), .out(multiplexer_18_out));
  ME_WB me_wb_1 (
    .ii4({ex_me_1_io3_3, ex_me_1_io3[19:12], ex_me_1_io3_2, ex_me_1_io3[6:0]}), .en4(not_11_out),
    .clr4(1'b0), .c4(clock), .csri3(ex_me_1_csr2), .con3({ex_me_1_cono2[31:13], rws1, ex_me_1_cono2[10:0]}),
    .aluRi2(ex_me_1_aluro1), .ramIn(multiplexer_18_out),
    .io4({me_wb_1_io4_3, me_wb_1_io4[19:12], me_wb_1_io4_2, me_wb_1_io4[6:0]}),
    .cono3({me_wb_1_cono3[31:28], me_wb_1_cono3_2, me_wb_1_cono3[24:13], rws2, me_wb_1_cono3[10:0]}),
    .csr3(me_wb_1_csr3), .aluRo2(me_wb_1_aluro2), .ramOut(me_wb_1_ramout));
  not not_11 (not_11_out, inter);
  and and_9 (and_9_out, not_12_out, me_wb_1_cono3[19]);
  Comparator #(.Bits(5)) comparator_11 (.a({5{1'b0}}), .b(me_wb_1_io4[19:15]), .eq(comparator_11_eq));  // open: gt, lt
  not not_12 (not_12_out, comparator_11_eq);

  // Other names for the same wires on the sheet: clkIn = clock; clrIn = clear; enIn = enable; rst = reset

  // Notes on the sheet:
  //   contents of rom1 (hex, n*v repeats v):
  //   0,fffff0b7,400093,40016f,158513,feb50fe3,fff20193,318233,308023,309023,30a023,40a223,
  //   402383,800403,801403,804403,805403,802403,ff3a413,ffe3b413,fff44413,247493,249513,
  //   1f4d593,25d593,40125613,40460633,c616b3,c42733,c43733,864733,e6d7b3,40f75733,d77733,
  //   c76833,200713,11d873,11d873,810f3,710f3,a973,25973,1039f3,10f9f3,e7,0,0,0,180006f,
  //   540006f,8c0006f,c60006f,0,0,0,0,0,0,0,0,3f73,3de02023,20000f13,14f1f13,f3073,20000f13,
  //   14f1f13,f2073,3c002f03,f1f73,20000f13,14f1f13,f3073,30200073,0,0,0,0,0,0,0,0,0,0,
  //   0,0,0,0,0,0,0,3f73,3de02823,20000f13,14f1f13,f3073,0,0,0,0,0,20000f13,14f1f13,f2073,
  //   3d002f03,f1f73,30200073,0,0,0,0,0,0,0,0,0,0,0,0,0,3f73,3fe02023,20000f13,14f1f13,
  //   f3073,0,0,0,0,0,0,20000f13,14f1f13,f2073,3e002f03,f1f73,30200073,0,0,0,0,0,0,0,0,
  //   0,0,0,0,0,3f73,3fe02823,20000f13,14f1f13,f3073,0,0,0,0,0,0,20000f13,14f1f13,f2073,
  //   3f002f03,f1f73,30200073
  //   pre redirect becausetwo clock 
  //   wiil be need wen access ram
endmodule
