// Digital circuit EX-ME.dig as structural Verilog
module EX_ME (
  input  [31:0] ii3,
  input  en3,
  input  clr3,
  input  [31:0] rbi2,
  input  [31:0] csri2,
  input  [31:0] con2,
  input  c3,
  input  [31:0] aluRi1,
  output [31:0] cono2,
  output [31:0] csr2,
  output [31:0] rb2,
  output [31:0] aluRo1,
  output [31:0] io3
);

  wire [31:0] multiplexer_1_out, multiplexer_2_out, multiplexer_3_out, multiplexer_4_out, multiplexer_5_out;

  Multiplexer #(.Bits(32)) multiplexer_1 (.sel(clr3), .in_0(ii3), .in_1({32{1'b0}}), .out(multiplexer_1_out));
  Multiplexer #(.Bits(32)) multiplexer_2 (.sel(clr3), .in_0(rbi2), .in_1({32{1'b0}}), .out(multiplexer_2_out));
  Multiplexer #(.Bits(32)) multiplexer_3 (.sel(clr3), .in_0(csri2), .in_1({32{1'b0}}), .out(multiplexer_3_out));
  Register #(.Bits(32)) register_1 (.D(multiplexer_1_out), .C(c3), .en(en3), .Q(io3));
  Register #(.Bits(32)) register_2 (.D(multiplexer_2_out), .C(c3), .en(en3), .Q(rb2));
  Register #(.Bits(32)) register_3 (.D(multiplexer_3_out), .C(c3), .en(en3), .Q(csr2));
  Multiplexer #(.Bits(32)) multiplexer_4 (.sel(clr3), .in_0(con2), .in_1({32{1'b0}}), .out(multiplexer_4_out));
  Multiplexer #(.Bits(32)) multiplexer_5 (.sel(clr3), .in_0(aluRi1), .in_1({32{1'b0}}), .out(multiplexer_5_out));
  Register #(.Bits(32)) register_4 (.D(multiplexer_4_out), .C(c3), .en(en3), .Q(cono2));
  Register #(.Bits(32)) register_5 (.D(multiplexer_5_out), .C(c3), .en(en3), .Q(aluRo1));

  // Other names for the same wires on the sheet: aluOut1[31:0] = aluRo1; aluR1[31:0] = aluRi1; clkIn3 = c3;
  //   controIn2[31:0] = con2; controOut2[31:0] = cono2; csrIn2[31:0] = csri2; insIn3[31:0] = ii3; insOut3[31:0] = io3;
  //   rbIn2[31:0] = rbi2

  // Notes on the sheet:
  //   csr2: csr 寄存器的值
  //   aluRo1: alu output
endmodule
