// Digital circuit risc-v-cpu.dig as structural Verilog
module risc_v_cpu (
  input  clock,
  input  clear,
  input  reset,
  input  enable,
  output [31:0] prePc,
  output preJIF,
  output [2:0] \type ,
  output [31:0] Pc,
  output preJF,
  output preJEX,
  output [31:0] aluData,
  output [31:0] csrData,
  output [31:0] ramDataOut,
  output [31:0] Da,
  output [31:0] ramDataIn,
  output [31:0] insOutIF,
  output [31:0] insOutEX
);

  wire bubble, clear_IDEX, en_IFID, if_id_1_prejo_ifid, not_1_out;
  wire [1:0] controller_1_mwf, controller_1_pcw, controller_1_rws, csrRedirect, rws;
  wire [2:0] controller_1_a_x, controller_1_a_y, controller_1_mrf, me_wb_1_cono3_2;
  wire [3:0] aluRedirect, controller_1_a_op;
  wire [4:0] ex_me_1_io3_2, if_id_1_io1_2, if_id_1_io1_3, me_wb_1_io4_2;
  wire [7:0] csr_p1;
  wire [7:5] if_id_1_io1_4;
  wire [11:0] me_wb_1_io4_3;
  wire [11:8] ex_me_1_io3_3;
  wire [15:0] multiplexer_8_out;
  wire [19:0] ex_me_1_io3, me_wb_1_io4;
  wire [23:0] multiplexer_9_out;
  wire [24:10] controller_1_mr;
  wire [31:0] alu_1_rst, alui_1_x, alui_1_y, brachpre_1_p9, csr_p3, csr_p10, ex_me_1_cono2, ex_me_1_csr2,
       ex_me_1_rb2, id_ex_1_cono1, id_ex_1_ra1, id_ex_1_rb1, if_id_1_io1, if_id_1_po1, me_wb_1_cono3,
       multiplexer_1_out, multiplexer_2_out, multiplexer_3_out, multiplexer_5_out, multiplexer_7_out,
       ram1_p10, registerfile_1_da, registerfile_1_db, rs1;

  // brachPre brachpre_1: pin names not known; wires that end beside it: insOutEX, rs1, 3'b000, insOutIF, preJF, clock, enable, bubble, brachpre_1_p9, Pc, preJIF, prePc, \type 
  // LRom #(.AddrBits(9), .Bits(32)) rom1: pin names not known; wires that end beside it: prePc[10:2], clock, en_IFID, 1'b0, insOutIF
  IF_ID if_id_1 (
    .c1(clock), .pi1(Pc), .ii1(insOutIF), .clr1(preJF), .en_IFID(en_IFID), .preJ_IFID(preJIF),
    .po1(if_id_1_po1),
    .io1({if_id_1_io1[31:28], if_id_1_io1_4, if_id_1_io1_3, if_id_1_io1_2, if_id_1_io1[14:0]}),
    .preJo_IFID(if_id_1_prejo_ifid));
  controller controller_1 (
    .ins({if_id_1_io1[31:28], if_id_1_io1_4, if_id_1_io1_3, if_id_1_io1_2, if_id_1_io1[14:0]}),
    .a_op(controller_1_a_op), .a_x(controller_1_a_x), .a_y(controller_1_a_y), .rwe(controller_1_mr[10]),
    .rws(controller_1_rws), .mw(controller_1_mr[13]), .pcw(controller_1_pcw), .raR(controller_1_mr[16]),
    .rbR(controller_1_mr[17]), .csrR(controller_1_mr[18]), .csrw(controller_1_mr[19]),
    .bxx(controller_1_mr[20]), .siC(controller_1_mr[21]), .jalrj(controller_1_mr[22]),
    .load(controller_1_mr[23]), .mR(controller_1_mr[24]), .mRF(controller_1_mrf), .mWF(controller_1_mwf));
  not not_1 (not_1_out, bubble);
  or or_1 (clear_IDEX, bubble, preJF);
  and and_1 (en_IFID, not_1_out, enable);
  // LRamDP #(.AddrBits(8), .Bits(32)) csr: pin names not known; wires that end beside it: csr_p1, {if_id_1_io1_4, if_id_1_io1_3}, csr_p3, ex_me_1_cono2[19], controller_1_mr[18], clock, ex_me_1_cono2[19], clock, reset, csr_p10
  RegisterFile #(.AddrBits(5), .Bits(32)) registerfile_1 (
    .Din(Da), .we(me_wb_1_cono3[10]), .Rw(me_wb_1_io4_2), .C(clock), .Ra(if_id_1_io1_2), .Rb(if_id_1_io1_3),
    .Da(registerfile_1_da), .Db(registerfile_1_db));
  bubble bubble_1 (
    .raRead(controller_1_mr[16]), .rbRead(controller_1_mr[17]), .raAdd(if_id_1_io1_2), .rbAdd(if_id_1_io1_3),
    .rwe_EX(id_ex_1_cono1[10]), .rw_EX(insOutEX[11:7]), .load(id_ex_1_cono1[23]), .bubble(bubble));
  ID_EX id_ex_1 (
    .pi2(if_id_1_po1),
    .ii2({if_id_1_io1[31:28], if_id_1_io1_4, if_id_1_io1_3, if_id_1_io1_2, if_id_1_io1[14:0]}),
    .preJ_IDEX(if_id_1_prejo_ifid), .rai1(registerfile_1_da), .rbi1(registerfile_1_db),
    .con1({2'b00, controller_1_mwf, controller_1_mrf, controller_1_mr[24:16], controller_1_pcw, controller_1_mr[13], controller_1_rws, controller_1_mr[10], controller_1_a_y, controller_1_a_x, controller_1_a_op}),
    .clr2(clear_IDEX), .en2(enable), .c2(clock), .po2(brachpre_1_p9), .io2(insOutEX), .ra1(id_ex_1_ra1),
    .cono1(id_ex_1_cono1), .rb1(id_ex_1_rb1), .preJo_IDEX(preJEX));
  Multiplexer #(.Selector_Bits(2), .Bits(32)) multiplexer_1 (
    .sel(rws), .in_0(csr_p3), .in_1({32{1'b0}}), .in_2(ex_me_1_csr2), .in_3({32{1'b0}}),
    .out(multiplexer_1_out));
  Multiplexer #(.Selector_Bits(2), .Bits(32)) multiplexer_2 (
    .sel(rws), .in_0(aluData), .in_1(ramDataOut), .in_2(csrData), .in_3({32{1'b0}}), .out(multiplexer_2_out));
  Multiplexer #(.Selector_Bits(2), .Bits(32)) multiplexer_3 (
    .sel(rws), .in_0(csr_p3), .in_1({32{1'b0}}), .in_2(ex_me_1_csr2), .in_3({32{1'b0}}),
    .out(multiplexer_3_out));
  Multiplexer #(.Selector_Bits(2), .Bits(32)) multiplexer_4 (
    .sel(rws), .in_0(aluData), .in_1(ramDataOut), .in_2(csrData), .in_3({32{1'b0}}), .out(Da));
  redirect redirect_1 (
    .raR(id_ex_1_cono1[16]), .rbR(id_ex_1_cono1[17]), .csrR(id_ex_1_cono1[18]), .rwe_ME(ex_me_1_cono2[10]),
    .rwe_WB(me_wb_1_cono3[10]), .csrwe_ME(ex_me_1_cono2[19]), .raA(insOutEX[19:15]), .rbA(insOutEX[24:20]),
    .csrA(insOutEX[31:20]), .rw_ME(ex_me_1_io3_2), .rw_WB(me_wb_1_io4_2), .csrw_ME({ex_me_1_io3_3, csr_p1}),
    .csrw_WB(me_wb_1_io4_3), .csrwe_WB(me_wb_1_cono3[19]), .aluRed(aluRedirect), .csrRed(csrRedirect));
  Multiplexer #(.Selector_Bits(2), .Bits(32)) multiplexer_5 (
    .sel({aluRedirect[3], aluRedirect[1]}), .in_0(id_ex_1_rb1), .in_1(multiplexer_3_out), .in_2(Da),
    .in_3(multiplexer_3_out), .out(multiplexer_5_out));
  Multiplexer #(.Selector_Bits(2), .Bits(32)) multiplexer_6 (
    .sel({aluRedirect[2], aluRedirect[0]}), .in_0(id_ex_1_ra1), .in_1(multiplexer_1_out),
    .in_2(multiplexer_2_out), .in_3(multiplexer_1_out), .out(rs1));
  ALUI alui_1 (
    .ins(insOutEX), .rs1(rs1), .opc(brachpre_1_p9), .rs2(multiplexer_5_out), .axI(id_ex_1_cono1[6:4]),
    .ayI(id_ex_1_cono1[9:7]), .siC(id_ex_1_cono1[21]), .csrIn(multiplexer_7_out), .x(alui_1_x), .y(alui_1_y));
  judgePre judgepre_1 (
    .bxxI(id_ex_1_cono1[20]), .preJI(preJEX), .aluRI(alu_1_rst), .jalrj(id_ex_1_cono1[22]), .preRo(preJF));
  Multiplexer #(.Selector_Bits(2), .Bits(32)) multiplexer_7 (
    .sel(csrRedirect), .in_0(csr_p10), .in_1(csr_p3), .in_2(aluData), .in_3(csr_p3), .out(multiplexer_7_out));
  ALU alu_1 (.alu_op(id_ex_1_cono1[3:0]), .x(alui_1_x), .y(alui_1_y), .rst(alu_1_rst));
  EX_ME ex_me_1 (
    .ii3(insOutEX), .en3(enable), .clr3(1'b0), .rbi2(multiplexer_5_out), .csri2(multiplexer_7_out),
    .con2(id_ex_1_cono1), .c3(clock), .aluRi1(alu_1_rst), .cono2(ex_me_1_cono2), .csr2(ex_me_1_csr2),
    .rb2(ex_me_1_rb2), .aluRo1(csr_p3),
    .io3({ex_me_1_io3_3, csr_p1, ex_me_1_io3[19:12], ex_me_1_io3_2, ex_me_1_io3[6:0]}));
  Multiplexer #(.Bits(16)) multiplexer_8 (
    .sel(ram1_p10[15]), .in_0({16{1'b0}}), .in_1({16{1'b1}}), .out(multiplexer_8_out));
  Multiplexer #(.Bits(24)) multiplexer_9 (
    .sel(ram1_p10[7]), .in_0({24{1'b0}}), .in_1({24{1'b1}}), .out(multiplexer_9_out));
  Multiplexer #(.Selector_Bits(2), .Bits(32)) multiplexer_10 (
    .sel(ex_me_1_cono2[29:28]), .in_0(ex_me_1_rb2), .in_1({{16{1'b0}}, ex_me_1_rb2[15:0]}),
    .in_2({{24{1'b0}}, ex_me_1_rb2[7:0]}), .in_3({32{1'b0}}), .out(ramDataIn));
  // LRamDP #(.AddrBits(8), .Bits(32)) ram1: pin names not known; wires that end beside it: csr_p3[9:2], csr_p3[9:2], ramDataIn, 1'b1, ex_me_1_cono2[24], clock, ex_me_1_cono2[13], clock, reset, ram1_p10
  Multiplexer #(.Selector_Bits(3), .Bits(32)) multiplexer_11 (
    .sel(me_wb_1_cono3_2), .in_0(ram1_p10), .in_1({multiplexer_8_out, ram1_p10[15:0]}),
    .in_2({{16{1'b0}}, ram1_p10[15:0]}), .in_3({multiplexer_9_out, ram1_p10[7:0]}),
    .in_4({{24{1'b0}}, ram1_p10[7:0]}), .in_5({32{1'b0}}), .in_6({32{1'b0}}), .in_7({32{1'b0}}),
    .out(ramDataOut));
  ME_WB me_wb_1 (
    .ii4({ex_me_1_io3_3, csr_p1, ex_me_1_io3[19:12], ex_me_1_io3_2, ex_me_1_io3[6:0]}), .en4(enable),
    .clr4(1'b0), .c4(clock), .csri3(ex_me_1_csr2), .con3(ex_me_1_cono2), .aluRi2(csr_p3),
    .io4({me_wb_1_io4_3, me_wb_1_io4[19:12], me_wb_1_io4_2, me_wb_1_io4[6:0]}),
    .cono3({me_wb_1_cono3[31:28], me_wb_1_cono3_2, me_wb_1_cono3[24:13], rws, me_wb_1_cono3[10:0]}),
    .csr3(csrData), .aluRo2(aluData));

  // Other names for the same wires on the sheet: clkIn = clock; clrIn = clear; enIn = enable; rst = reset

  // Notes on the sheet:
  //   contents of rom1 (hex, n*v repeats v):
  //   0,fffff0b7,400093,40016f,158513,feb50fe3,fff20193,318233,308023,309023,30a023,40a223,
  //   402383,800403,801403,804403,805403,802403,ff3a413,ffe3b413,fff44413,247493,249513,
  //   1f4d593,25d593,40125613,40460633,c616b3,c42733,c43733,864733,e6d7b3,40f75733,d77733,
  //   c76833,200713,11d873,11d873,810f3,710f3,a973,25973,1039f3,10f9f3,e7
  //   ramDp need two clock to read 
  //   so it is need Delivery in advance
  //   pre redirect becausetwo clock 
  //   wiil be need wen access ram
endmodule
